// Logisim project CGA.circ as structural Verilog: 125 circuits, main circuit CGA
module CGA (
  input  XPTSTN,
  input  [4:0] XCSCOMM_4_0,
  input  [1:0] XCSMIS_1_0,
  input  [15:0] XCD_15_0,
  input  XEDON,
  input  [1:0] XCSCINSEL_1_0,
  input  [1:0] XCSSST_1_0,
  input  XALUCLK,
  input  [15:0] XCSBIT_15_0,
  input  [1:0] XCSALUM_1_0,
  input  [8:0] XCSALUI_8_0,
  input  [4:0] XCSIDBS_4_0,
  input  XMRN,
  input  XCSLOOP,
  input  XCSECOND,
  input  [1:0] XCSRASEL_1_0,
  input  [3:0] XCSRB_3_0,
  input  XCSBIT20,
  input  [1:0] XCSRBSEL_1_0,
  input  XCSSCOND,
  input  [3:0] XCSTS_6_3,
  input  XCSVECT,
  input  XCSXRF3,
  input  XEWCAN,
  input  XMAPN,
  input  XSPARE,
  input  XSTP,
  input  XETRAPN,
  input  XFTRAPN,
  input  XVTRAPN,
  input  [6:0] XPT_9_15,
  input  XTCLK,
  input  XPANN,
  input  XMCLK,
  input  XBINT10N,
  input  XBINT11N,
  input  XBINT12N,
  input  XBINT13N,
  input  XILCSN,
  input  XBINT15N,
  input  XEMPIDN,
  input  XIOXERRN,
  input  XMORN,
  input  XPARERRN,
  input  XPOWFAILN,
  input  [2:0] XTSEL_2_0,
  input  [15:0] XFIDB_15_0_IN,
  output XLSHADOW,
  output [3:0] XPIL_3_0,
  output XBRKN,
  output XIONI,
  output XINTRQN,
  output XDOUBLE,
  output XPONI,
  output XACONDN,
  output XWCSN,
  output XERFN,
  output XWRTRF,
  output XECCR,
  output XTRAPN,
  output [3:0] XLAA_3_0,
  output [3:0] XLBA_3_0,
  output [1:0] XRF_1_0,
  output [1:0] XPCR_1_0,
  output [4:0] XTEST_4_0,
  output [12:0] XMA_12_0,
  output [13:0] XLA_23_10,
  output [9:0] XMCA_9_0,
  output [15:0] XFIDB_15_0_OUT
);

  wire ALU_bdest, CBRKN, CFETCH, CLFFN, COND, CRY, CSMREQ, DCD_clirqn, DCD_epcrn, DCD_epgsn, DCD_epic,
       DCD_epicsn, DCD_epicvn, DCD_fetchn, DEEP, DSTOPN, DZD, F11, F15, FIDBO5, INDN, INTR_epicmaskn,
       INTR_higsn, INTR_logsn, INTR_pd, IRQ, LCZN, LDDBRN, LDGPRN, LDIRV, LDLCN, LDPILN, LWCAN, MI, OOD, OVF,
       PN, PTM, RESTR, SGR, TN, TRAP_pviol, UPN, VACCN, VEX, WPN, WR3, WR7, WRITEN, XFETCHN, Z, ZF;
  wire [2:0] INTR_pics_2_0, INTR_picv_2_0;
  wire [3:0] SC_6_3, TVEC_3_0;
  wire [15:0] ALU_rb_15_0, EA_15_0, FIDBI_15_0, FIDBO_15_0, INTR_picmask_15_0, MAC_nlca_15_0, WRF_a_15_0,
       WRF_b_15_0, WRF_br_15_0, WRF_pr_15_0, WRF_xr_15_0, XFIDBI_15_0;
  wire [15:2] PCR_15_0;

  // Probe on {FIDBO_15_0[15:6], FIDBO5, FIDBO_15_0[4:0]}
  BusDriver16 BD_FIDBO (
    .A_15_0({FIDBO_15_0[15:6], FIDBO5, FIDBO_15_0[4:0]}), .IN_15_0(XFIDB_15_0_IN), .EN(XEDON), .TN(XPTSTN),
    .ZI_15_0(XFIDBI_15_0), .OUT_15_0(XFIDB_15_0_OUT));
  CGA_DCD DCD (
    .CSCOMM_4_0(XCSCOMM_4_0), .CSMIS_1_0(XCSMIS_1_0), .MCLK(XMCLK), .ILCSN(XILCSN), .F15(F15), .ZF(ZF),
    .CRY(CRY), .SGR(SGR), .WPN(WPN), .PONI(XPONI), .VEX(VEX), .BRKN(XBRKN), .FIDBO5(FIDBO5), .MRN(XMRN),
    .LSHADOW(XLSHADOW), .INTRQN(XINTRQN), .CSIDBS_4_0(XCSIDBS_4_0), .INDN(INDN), .XFETCHN(XFETCHN),
    .CBRKN(CBRKN), .DSTOPN(DSTOPN), .LDLCN(LDLCN), .LDPILN(LDPILN), .LDIRV(LDIRV), .CSMREQ(CSMREQ),
    .LDDBRN(LDDBRN), .FETCHN(DCD_fetchn), .WRITEN(WRITEN), .CLFFN(CLFFN), .EPIC(DCD_epic), .LWCAN(LWCAN),
    .LDGPRN(LDGPRN), .WRTRF(XWRTRF), .CFETCH(CFETCH), .VACCN(VACCN), .CLIRQN(DCD_clirqn), .EPGSN(DCD_epgsn),
    .EPCRN(DCD_epcrn), .EPICVN(DCD_epicvn), .EPICSN(DCD_epicsn), .ERFN(XERFN));
  // Probe on TVEC_3_0
  // Probe on XTSEL_2_0
  CGA_INTR INTR (
    .PANN(XPANN), .MCLK(XMCLK), .CLIRQN(DCD_clirqn), .EMPIDN(XEMPIDN), .BINT15N(XBINT15N),
    .POWFAILN(XPOWFAILN), .NORN(XMORN), .PARERRN(XPARERRN), .IOXERRN(XIOXERRN), .Z(Z), .BINT13N(XBINT13N),
    .BINT12N(XBINT12N), .BINT11N(XBINT11N), .BINT10N(XBINT10N),
    .FIDBO_15_0({FIDBO_15_0[15:6], FIDBO5, FIDBO_15_0[4:0]}), .LAA_3_0(XLAA_3_0), .EPIC(DCD_epic),
    .INTRQN(XINTRQN), .PICMASK_15_0(INTR_picmask_15_0), .HIGSN(INTR_higsn), .PD(INTR_pd),
    .PICV_2_0(INTR_picv_2_0), .IRQ(IRQ), .LOGSN(INTR_logsn), .PICS_2_0(INTR_pics_2_0),
    .EPICMASKN(INTR_epicmaskn));
  CGA_MIC MIC (
    .CSBIT_15_0(XCSBIT_15_0), .CSBIT20(XCSBIT20), .MI(MI), .IRQ(IRQ), .RESTR(RESTR), .CFETCH(CFETCH),
    .SPARE(XSPARE), .OVF(OVF), .CRY(CRY), .F11(F11), .F15(F15), .ZF(ZF), .STP(XSTP), .ALUCLK(XALUCLK),
    .MCLK(XMCLK), .CSLOOP(XCSLOOP), .CSECOND(XCSECOND), .CLFFN(CLFFN), .CSALUI8(XCSALUI_8_0[8]),
    .CSCOND(XCSSCOND), .ILCSN(XILCSN), .CSTS_6_3(XCSTS_6_3), .TVEC_3_0(TVEC_3_0), .TRAPN(XTRAPN),
    .MAPN(XMAPN), .EWCAN(XEWCAN), .CSMIS0(XCSMIS_1_0[0]), .CSVECT(XCSVECT), .CD_15_0(XCD_15_0),
    .LDIRV(LDIRV), .LWCAN(LWCAN), .MRN(XMRN), .LDLCN(LDLCN), .PIL_3_0(XPIL_3_0), .CSXRF3(XCSXRF3),
    .CSRB_3_0(XCSRB_3_0), .CSRASEL_1_0(XCSRASEL_1_0), .CSRBSEL_1_0(XCSRBSEL_1_0), .DZD(DZD), .COND(COND),
    .OOD(OOD), .ACONDN(XACONDN), .SC_6_3(SC_6_3), .MA_12_0(XMA_12_0), .WCSN(XWCSN), .DEEP(DEEP), .UPN(UPN),
    .PN(PN), .LCZN(LCZN), .TN(TN), .LAA_3_0(XLAA_3_0), .LBA_3_0(XLBA_3_0), .RF_1_0(XRF_1_0));  // open: LCZ
  CGA_MAC MAC (
    .MCLK(XMCLK), .PTM(PTM), .FIDBO_15_0({FIDBO_15_0[15:6], FIDBO5, FIDBO_15_0[4:0]}), .PONI(XPONI),
    .CMIS_1_0(XCSMIS_1_0), .CSCOMM_4_0(XCSCOMM_4_0), .WR3(WR3), .WR7(WR7), .ILCSN(XILCSN), .DOUBLE(XDOUBLE),
    .CSMREQ(CSMREQ), .CD_15_0(XCD_15_0), .RB_15_0(ALU_rb_15_0), .XR_15_0(WRF_xr_15_0), .BR_15_0(WRF_br_15_0),
    .PR_15_0(WRF_pr_15_0), .VEX(VEX), .PCR_15_0({PCR_15_0, XPCR_1_0}), .LA_23_10(XLA_23_10),
    .LSHADOW(XLSHADOW), .ECCR(XECCR), .MCA_9_0(XMCA_9_0), .NLCA_15_0(MAC_nlca_15_0));
  // Probe on SC_6_3
  // Probe on XTEST_4_0
  CGA_TESTMUX TESTMUX (
    .TVEC_3_0(TVEC_3_0), .SC_6_3(SC_6_3), .PTREEOUT(1'b1), .VACCN(VACCN), .MI(MI), .OVF(OVF), .UPN(UPN),
    .LCZN(LCZN), .CSMREQ(CSMREQ), .INDN(INDN), .PTM(PTM), .ZF(ZF), .COND(COND), .DZD(DZD), .LDIRV(LDIRV),
    .CBRKN(CBRKN), .WPN(WPN), .F15(F15), .PN(PN), .OOD(OOD), .VEX(VEX), .WRITEN(WRITEN), .XFETCHN(XFETCHN),
    .SGR(SGR), .TN(TN), .CFETCH(CFETCH), .DSTOPN(DSTOPN), .CRY(CRY), .RESTR(RESTR), .DEEP(DEEP),
    .TSEL_2_0(XTSEL_2_0), .PTSTN(XPTSTN), .TEST_4_0(XTEST_4_0));
  // Probe on {PCR_15_0, XPCR_1_0}
  // Probe on XPT_9_15
  // Probe on XPCR_1_0
  CGA_ALU ALU (
    .A_15_0(WRF_a_15_0), .B_15_0(WRF_b_15_0), .CSBIT_15_0(XCSBIT_15_0), .EA_15_0(EA_15_0),
    .FIDBI_15_0(FIDBI_15_0), .CSIDBS_4_0(XCSIDBS_4_0), .LBA_3_0(XLBA_3_0), .LAA_3_0(XLAA_3_0),
    .LDPILN(LDPILN), .LDDBRN(LDDBRN), .XFETCHN(XFETCHN), .LDGPRN(LDGPRN), .CSMIS_1_0(XCSMIS_1_0),
    .CSSST_1_0(XCSSST_1_0), .CSCINSEL_1_0(XCSCINSEL_1_0), .LDIRV(LDIRV), .UPN(UPN), .LCZN(LCZN),
    .CSALUI_8_0(XCSALUI_8_0), .CSALUM_1_0(XCSALUM_1_0), .ALUCLK(XALUCLK), .CD_15_0(XCD_15_0), .ZF(CRY),
    .CRY(ZF), .SGR(SGR), .OVF(OVF), .RB_15_0(ALU_rb_15_0), .F11(F11), .F15(F15), .BDEST(ALU_bdest), .MI(MI),
    .PTM(PTM), .Z(Z), .PIL_3_0(XPIL_3_0), .DOUBLE(XDOUBLE), .PONI(XPONI), .IONI(XIONI),
    .FIDBO_15_0({FIDBO_15_0[15:6], FIDBO5, FIDBO_15_0[4:0]}));
  CGA_TRAP TRAP (
    .CBRKN(CBRKN), .ETRAPN(XETRAPN), .PT_15_9(XPT_9_15), .PCR_1_0(XPCR_1_0), .FETCHN(DCD_fetchn),
    .WRITEN(WRITEN), .INDN(INDN), .INTRQN(XINTRQN), .PANN(XPANN), .VACCN(VACCN), .PONI(XPONI), .TCLK(XTCLK),
    .VTRAPN(XVTRAPN), .FTRAPN(XFTRAPN), .DSTOPN(DSTOPN), .BRKN(XBRKN), .TRAPN(XTRAPN), .RESTR(RESTR),
    .TVEC_3_0(TVEC_3_0), .PVIOL(TRAP_pviol));
  // Probe on nothing
  CGA_IDBCTL IDBCTL (
    .MCLK(XMCLK), .VACCN(VACCN), .LA_21_10(XLA_23_10[11:0]), .FETCHN(DCD_fetchn), .PVIOL(TRAP_pviol),
    .EPGSN(DCD_epgsn), .EPCRN(DCD_epcrn), .EPICSN(DCD_epicsn), .EPICVN(DCD_epicvn),
    .EPICMASKN(INTR_epicmaskn), .PD(INTR_pd), .HIGSN(INTR_higsn), .LOGSN(INTR_logsn),
    .PCR_15_0({PCR_15_0, XPCR_1_0}), .XFIDBI_15_0(XFIDBI_15_0), .PICMASK_15_0(INTR_picmask_15_0),
    .PICV_2_0(INTR_picv_2_0), .PICS_2_0(INTR_pics_2_0), .FIDBI_15_0(FIDBI_15_0));
  // Probe on FIDBI_15_0
  CGA_WRF WRF (
    .BDEST(ALU_bdest), .LBA_3_0(XLBA_3_0), .LAA_3_0(XLAA_3_0), .ALUCLK(XALUCLK), .RB_15_0(ALU_rb_15_0),
    .NLCA_15_0(MAC_nlca_15_0), .XFETCHN(XFETCHN), .WPN(WPN), .WR3(WR3), .WR7(WR7), .B_15_0(WRF_b_15_0),
    .A_15_0(WRF_a_15_0), .PR_15_0(WRF_pr_15_0), .BR_15_0(WRF_br_15_0), .XR_15_0(WRF_xr_15_0),
    .EA_15_0(EA_15_0));

  // Other names for the same wires on the sheet: ACONDN = XACONDN; ALUCLK = XALUCLK; BINT10N = XBINT10N;
  //   BINT11N = XBINT11N; BINT12N = XBINT12N; BINT13N = XBINT13N; BINT15N = XBINT15N; BRKN = XBRKN; CD0 = XCD_15_0[0];
  //   CD_15_0[15:0] = XCD_15_0; CD1 = XCD_15_0[1]; CD2 = XCD_15_0[2]; CD3 = XCD_15_0[3]; CD4 = XCD_15_0[4];
  //   CD5 = XCD_15_0[5]; CD6 = XCD_15_0[6]; CD7 = XCD_15_0[7]; CD8 = XCD_15_0[8]; CD9 = XCD_15_0[9];
  //   CD10 = XCD_15_0[10]; CD11 = XCD_15_0[11]; CD12 = XCD_15_0[12]; CD13 = XCD_15_0[13]; CD14 = XCD_15_0[14];
  //   CD15 = XCD_15_0[15]; CSALUI0 = XCSALUI_8_0[0]; CSALUI_8_0[8:0] = XCSALUI_8_0; CSALUI1 = XCSALUI_8_0[1];
  //   CSALUI2 = XCSALUI_8_0[2]; CSALUI3 = XCSALUI_8_0[3]; CSALUI4 = XCSALUI_8_0[4]; CSALUI5 = XCSALUI_8_0[5];
  //   CSALUI6 = XCSALUI_8_0[6]; CSALUI7 = XCSALUI_8_0[7]; CSALUI8 = XCSALUI_8_0[8]; CSALUM0 = XCSALUM_1_0[0];
  //   CSALUM_1_0[1:0] = XCSALUM_1_0; CSALUM1 = XCSALUM_1_0[1]; CSBIT20 = XCSBIT20; CSBIT0 = XCSBIT_15_0[0];
  //   CSBIT_15_0[15:0] = XCSBIT_15_0; CSBIT1 = XCSBIT_15_0[1]; CSBIT2 = XCSBIT_15_0[2]; CSBIT3 = XCSBIT_15_0[3];
  //   CSBIT4 = XCSBIT_15_0[4]; CSBIT5 = XCSBIT_15_0[5]; CSBIT6 = XCSBIT_15_0[6]; CSBIT7 = XCSBIT_15_0[7];
  //   CSBIT8 = XCSBIT_15_0[8]; CSBIT9 = XCSBIT_15_0[9]; CSBIT10 = XCSBIT_15_0[10]; CSBIT11 = XCSBIT_15_0[11];
  //   CSBIT12 = XCSBIT_15_0[12]; CSBIT13 = XCSBIT_15_0[13]; CSBIT14 = XCSBIT_15_0[14]; CSBIT15 = XCSBIT_15_0[15];
  //   CSCINSEL0 = XCSCINSEL_1_0[0]; CSCINSEL_1_0[1:0] = XCSCINSEL_1_0; CSCINSEL1 = XCSCINSEL_1_0[1];
  //   CSCOMM0 = XCSCOMM_4_0[0]; CSCOMM_4_0[4:0] = XCSCOMM_4_0; CSCOMM1 = XCSCOMM_4_0[1]; CSCOMM2 = XCSCOMM_4_0[2];
  //   CSCOMM3 = XCSCOMM_4_0[3]; CSCOMM4 = XCSCOMM_4_0[4]; CSECOND = XCSECOND; CSIDBS0 = XCSIDBS_4_0[0];
  //   CSIDBS_4_0[4:0] = XCSIDBS_4_0; CSIDBS1 = XCSIDBS_4_0[1]; CSIDBS2 = XCSIDBS_4_0[2]; CSIDBS3 = XCSIDBS_4_0[3];
  //   CSIDBS4 = XCSIDBS_4_0[4]; CSLOOP = XCSLOOP; CSMIS0 = XCSMIS_1_0[0]; CSMIS_1_0[1:0] = XCSMIS_1_0;
  //   CSMIS1 = XCSMIS_1_0[1]; CSRASEL0 = XCSRASEL_1_0[0]; CSRASEL_1_0[1:0] = XCSRASEL_1_0; CSRASEL1 = XCSRASEL_1_0[1];
  //   CSRB0 = XCSRB_3_0[0]; CSRB_3_0[3:0] = XCSRB_3_0; CSRB1 = XCSRB_3_0[1]; CSRB2 = XCSRB_3_0[2];
  //   CSRB3 = XCSRB_3_0[3]; CSRBSEL0 = XCSRBSEL_1_0[0]; CSRBSEL_1_0[1:0] = XCSRBSEL_1_0; CSRBSEL1 = XCSRBSEL_1_0[1];
  //   CSSCOND = XCSSCOND; CSSST0 = XCSSST_1_0[0]; CSSST_1_0[1:0] = XCSSST_1_0; CSSST1 = XCSSST_1_0[1];
  //   CSTS3 = XCSTS_6_3[0]; CSTS_6_3[3:0] = XCSTS_6_3; CSTS4 = XCSTS_6_3[1]; CSTS5 = XCSTS_6_3[2];
  //   CSTS6 = XCSTS_6_3[3]; CSVECT = XCSVECT; CSXRF3 = XCSXRF3; DOUBLE = XDOUBLE; ECCR = XECCR; EDON = XEDON;
  //   EMPIDN = XEMPIDN; ERFN = XERFN; ETRAPN = XETRAPN; EWCAN = XEWCAN; FIDBO_15_0[5] = FIDBO5; FTRAPN = XFTRAPN;
  //   ILCSN = XILCSN; INTRQN = XINTRQN; IONI = XIONI; IOXERRN = XIOXERRN; LA_21_10[11:0] = XLA_23_10[11:0];
  //   LA_23_10[13:0] = XLA_23_10; LAA_3_0[3:0] = XLAA_3_0; LBA_3_0[3:0] = XLBA_3_0; LSHADOW = XLSHADOW;
  //   MA_12_0[12:0] = XMA_12_0; MAPN = XMAPN; MCA_9_0[9:0] = XMCA_9_0; MCLK = XMCLK; MORN = XMORN; MRN = XMRN;
  //   PANN = XPANN; PARERRN = XPARERRN; PCR_1_0[1:0] = XPCR_1_0; PCR_15_0[1:0] = XPCR_1_0; PIL_3_0[3:0] = XPIL_3_0;
  //   PONI = XPONI; POWFAILN = XPOWFAILN; PT9 = XPT_9_15[0]; PT_15_9[6:0] = XPT_9_15; PT10 = XPT_9_15[1];
  //   PT11 = XPT_9_15[2]; PT12 = XPT_9_15[3]; PT13 = XPT_9_15[4]; PT14 = XPT_9_15[5]; PT15 = XPT_9_15[6];
  //   PTSTN = XPTSTN; RF_1_0[1:0] = XRF_1_0; SPARE = XSPARE; STP = XSTP; TCLK = XTCLK; TEST_4_0[4:0] = XTEST_4_0;
  //   TRAPN = XTRAPN; TSEL0 = XTSEL_2_0[0]; TSEL_2_0[2:0] = XTSEL_2_0; TSEL1 = XTSEL_2_0[1]; TSEL2 = XTSEL_2_0[2];
  //   VTRAPN = XVTRAPN; WCSN = XWCSN; WRTRF = XWRTRF

  // Notes on the sheet:
  //   Page 3 - CGA - Sheet 2/8  (down)
  //   Page 4 - CGA - Sheet 3/8  (down)
  //   Page 7 - CGA - Sheet 6/8 (down)
  //   Page 8 - CGA - Sheet 7/8 (down)
  //   Page 2 - CGA - Sheet 1/8
  //   Page 5 - CGA - Sheet 4/8  (down)
  //   Page 6 - CGA - Sheet 5/8 (down)
  //   Page 9 - CGA - Sheet 8/8 (down)
  //   Normally IN and OUT will be connected together - but Logisim doesnt allow IN and OUT on the same pin
  //   WILL SHOW RED AS THERE IS LATCHES THAT IS "UNDEFINED" UNTIL USED
endmodule

module CGA_TESTMUX (
  input  [3:0] TVEC_3_0,
  input  [3:0] SC_6_3,
  input  PTREEOUT,
  input  VACCN,
  input  MI,
  input  OVF,
  input  UPN,
  input  LCZN,
  input  CSMREQ,
  input  INDN,
  input  PTM,
  input  ZF,
  input  COND,
  input  DZD,
  input  LDIRV,
  input  CBRKN,
  input  WPN,
  input  F15,
  input  PN,
  input  OOD,
  input  VEX,
  input  WRITEN,
  input  XFETCHN,
  input  SGR,
  input  TN,
  input  CFETCH,
  input  DSTOPN,
  input  CRY,
  input  RESTR,
  input  DEEP,
  input  [2:0] TSEL_2_0,
  input  PTSTN,
  output [4:0] TEST_4_0
);

  wire and_1_out, and_2_out, and_3_out, nand_1_out;

  and and_1 (and_1_out, TSEL_2_0[0], PTSTN);
  and and_2 (and_2_out, TSEL_2_0[1], PTSTN);
  and and_3 (and_3_out, TSEL_2_0[2], PTSTN);
  nand nand_1 (nand_1_out, ~PTSTN, ~PTREEOUT);  // NAND_Gate
  MUX81 TM0 (
    .D0(nand_1_out), .D1(VACCN), .D2(MI), .D3(OVF), .D4(UPN), .D5(LCZN), .D6(SC_6_3[0]), .D7(TVEC_3_0[0]),
    .A(and_1_out), .B(and_2_out), .C(and_3_out), .Z(TEST_4_0[0]));
  MUX81 TM1 (
    .D0(CSMREQ), .D1(INDN), .D2(PTM), .D3(ZF), .D4(COND), .D5(DZD), .D6(SC_6_3[1]), .D7(TVEC_3_0[1]),
    .A(and_1_out), .B(and_2_out), .C(and_3_out), .Z(TEST_4_0[1]));
  MUX81 TM2 (
    .D0(LDIRV), .D1(CBRKN), .D2(WPN), .D3(F15), .D4(PN), .D5(OOD), .D6(SC_6_3[2]), .D7(TVEC_3_0[2]),
    .A(and_1_out), .B(and_2_out), .C(and_3_out), .Z(TEST_4_0[2]));
  MUX81 TM3 (
    .D0(VEX), .D1(WRITEN), .D2(XFETCHN), .D3(SGR), .D4(TN), .D5(CFETCH), .D6(SC_6_3[3]), .D7(TVEC_3_0[3]),
    .A(and_1_out), .B(and_2_out), .C(and_3_out), .Z(TEST_4_0[3]));
  MUX81 TM4 (
    .D0(1'b1), .D1(DSTOPN), .D2(1'b1), .D3(CRY), .D4(1'b1), .D5(RESTR), .D6(DEEP), .D7(1'b0), .A(and_1_out),
    .B(and_2_out), .C(and_3_out), .Z(TEST_4_0[4]));

  // Notes on the sheet:
  //   TSEL0
  //   TSEL1
  //   TSEL2
  //   SC3
  //   TVEC0
  //   SC4
  //   TVEC1
  //   SC5
  //   TVEC2
  //   SC6
  //   TVEC3
  //   TEST0
  //   TEST1
  //   TEST2
  //   TEST3
  //   TEST4
endmodule

module CGA_ALU (
  input  [15:0] A_15_0,
  input  [15:0] B_15_0,
  input  [15:0] CSBIT_15_0,
  input  [15:0] EA_15_0,
  input  [15:0] FIDBI_15_0,
  input  [4:0] CSIDBS_4_0,
  input  [3:0] LBA_3_0,
  input  [3:0] LAA_3_0,
  input  LDPILN,
  input  LDDBRN,
  input  XFETCHN,
  input  LDGPRN,
  input  [1:0] CSMIS_1_0,
  input  [1:0] CSSST_1_0,
  input  [1:0] CSCINSEL_1_0,
  input  LDIRV,
  input  UPN,
  input  LCZN,
  input  [8:0] CSALUI_8_0,
  input  [1:0] CSALUM_1_0,
  input  ALUCLK,
  input  [15:0] CD_15_0,
  output ZF,
  output CRY,
  output SGR,
  output OVF,
  output [15:0] RB_15_0,
  output F11,
  output F15,
  output BDEST,
  output MI,
  output PTM,
  output Z,
  output [3:0] PIL_3_0,
  output DOUBLE,
  output PONI,
  output IONI,
  output [15:0] FIDBO_15_0
);

  wire AARG0, AARG0_MUX_zn, ALUD2N, ALUI4, ALUI7, ALUI8N, CI, d_ff_1_q, DGPR0N, F0, FSEL, GPR0, GPR7, GPRLI,
       LOG, Q0, Q15, QLI, RA, RD, RLI, RRI, RSN, SA, SB, STS6, STS7;
  wire [1:0] CSTS_1_0, QSEL_1_0;
  wire [2:0] GPRC_2_0;
  wire [12:1] STS_15_0;
  wire [14:1] F_15_0, Q_15_0;
  wire [15:0] ALU_RMUX_rn_15_0, ALU_SMUX_s_15_0, ARG_15_0, D_15_0, DBR_15_0, G_15_0, SW_15_0;
  wire [15:1] GPR_15_0;

  // Probe on A_15_0
  // Probe on D_15_0
  CGA_ALU_QREG ALU_QREG (
    .F_15_0({F15, F_15_0[14:12], F11, F_15_0[10:1], F0}), .QLI(QLI), .QSEL_1_0(QSEL_1_0), .ALUCLK(ALUCLK),
    .Q_15_0({Q15, Q_15_0, Q0}));
  CGA_CPU_ALU_RMUX ALU_RMUX (.D_15_0(D_15_0), .A_15_0(A_15_0), .RD(RD), .RA(RA), .RN_15_0(ALU_RMUX_rn_15_0));
  CGA_ALU_SMUX ALU_SMUX (
    .A_15_0(A_15_0), .B_15_0(B_15_0), .Q_15_0({Q15, Q_15_0, Q0}), .SA(SA), .SB(SB), .S_15_0(ALU_SMUX_s_15_0));
  CGA_CPU_ALU_CONTR ALU_CONTR (
    .STS7(STS7), .CRY(CRY), .F0(F0), .Q0(Q0), .Q15(Q15), .XFETCHN(XFETCHN), .LDGPRN(LDGPRN),
    .CSMIS_1_0(CSMIS_1_0), .CD_10_9(CD_15_0[10:9]), .CSSST_1_0(CSSST_1_0), .CSCINSEL_1_0(CSCINSEL_1_0),
    .LDIRV(LDIRV), .UPN(UPN), .STS6(STS6), .GPR0(GPR0), .LCZN(LCZN), .ALUCLK(ALUCLK),
    .CSALUI_8_0(CSALUI_8_0), .CSALUM_1_0(CSALUM_1_0), .DGPR0N(DGPR0N), .F15(F15), .ALUD2N(ALUD2N),
    .QSEL_1_0(QSEL_1_0), .GPRLI(GPRLI), .RRI(RRI), .QLI(QLI), .RLI(RLI), .GPRC_2_0(GPRC_2_0),
    .ALUI8N(ALUI8N), .CI(CI), .BDEST(BDEST), .CSTS_1_0(CSTS_1_0), .ALUI7(ALUI7), .MI(MI), .RSN(RSN),
    .FSEL(FSEL), .LOG(LOG), .ALUI4(ALUI4), .SB(SB), .SA(SA), .RA(RA), .RD(RD));
  // Probe on ALU_RMUX_rn_15_0
  // Probe on ALU_SMUX_s_15_0
  // Probe on GPRC_2_0
  CGA_CPU_ALU_RALU ALU_RALU (
    .CI(CI), .LOG(LOG), .ALUI4(ALUI4), .FSEL(FSEL), .RSN(RSN), .RN_15_0(ALU_RMUX_rn_15_0),
    .S_15_0(ALU_SMUX_s_15_0), .ZF(ZF), .F_15_0({F15, F_15_0[14:12], F11, F_15_0[10:1], F0}), .CRY(CRY),
    .SGR(SGR), .OVF(OVF));
  // Probe on ZF
  // Probe on {F15, F_15_0[14:12], F11, F_15_0[10:1], F0}
  CGA_ALU_SHIFT ALU_SHIFT (
    .RRI(RRI), .F_15_0({F15, F_15_0[14:12], F11, F_15_0[10:1], F0}), .RLI(RLI), .ALUI7(ALUI7),
    .ALUI8N(ALUI8N), .RB_15_0(RB_15_0));
  CGA_ALU_GPR ALU_GPR (
    .CD_15_0(CD_15_0), .FIDBO_15_0(FIDBO_15_0), .GPRC_2_0(GPRC_2_0), .GPRLI(GPRLI), .ALUCLK(ALUCLK),
    .GPR_15_0({GPR_15_0[15:8], GPR7, GPR_15_0[6:1], GPR0}), .DGPR0N(DGPR0N));
  CGA_ALU_STS ALU_STS (
    .LDPILN(LDPILN), .ALUCLK(ALUCLK), .FIDBO_15_0(FIDBO_15_0), .MI(MI), .CRY(CRY), .OVF(OVF),
    .CSTS_1_0(CSTS_1_0),
    .STS_15_0({IONI, PONI, DOUBLE, STS_15_0[12], PIL_3_0, STS7, STS6, STS_15_0[5:4], Z, STS_15_0[2:1], PTM}));
  // Probe on {IONI, PONI, DOUBLE, STS_15_0[12], PIL_3_0, STS7, STS6, STS_15_0[5:4], Z, STS_15_0[2:1], PTM}
  D_Flip_Flop d_ff_1 (.D(CSIDBS_4_0[2]), .clk(ALUCLK), .Q(d_ff_1_q));  // open: Qn, preset, reset
  not not_1 (FIDBO_15_0[15], G_15_0[15]);
  not not_2 (FIDBO_15_0[14], G_15_0[14]);
  not not_3 (FIDBO_15_0[13], G_15_0[13]);
  not not_4 (FIDBO_15_0[12], G_15_0[12]);
  not not_5 (FIDBO_15_0[11], G_15_0[11]);
  not not_6 (FIDBO_15_0[10], G_15_0[10]);
  not not_7 (FIDBO_15_0[9], G_15_0[9]);
  not not_8 (FIDBO_15_0[8], G_15_0[8]);
  not not_9 (FIDBO_15_0[7], G_15_0[7]);
  not not_10 (FIDBO_15_0[6], G_15_0[6]);
  not not_11 (FIDBO_15_0[5], G_15_0[5]);
  not not_12 (FIDBO_15_0[4], G_15_0[4]);
  not not_13 (FIDBO_15_0[3], G_15_0[3]);
  not not_14 (FIDBO_15_0[2], G_15_0[2]);
  not not_15 (FIDBO_15_0[1], G_15_0[1]);
  not not_16 (FIDBO_15_0[0], G_15_0[0]);
  // Probe on CSIDBS_4_0
  CGA_ALU_DBR ALU_DBR (.ALUCLK(ALUCLK), .LDDBRN(LDDBRN), .CD_15_0(CD_15_0), .DBR_15_0(DBR_15_0));
  CGA_ALU_ARG ALU_ARG (.CSBIT_15_0(CSBIT_15_0), .ALUCLK(ALUCLK), .ARG_15_0(ARG_15_0));
  CGA_ALU_SWAP ALU_SWAP (.FIDBO_15_0(FIDBO_15_0), .ALUCLK(ALUCLK), .SW_15_0(SW_15_0));
  MUX21LP AARG0_MUX (.A(LBA_3_0[3]), .B(LAA_3_0[0]), .S(d_ff_1_q), .ZN(AARG0_MUX_zn));
  CGA_ALU_OUTMUX ALU_OUTMUX (
    .EA_15_0(EA_15_0), .DBR_15_0(DBR_15_0), .ARG_15_0(ARG_15_0),
    .STS_15_0({IONI, PONI, DOUBLE, STS_15_0[12], PIL_3_0, STS7, STS6, STS_15_0[5:4], Z, STS_15_0[2:1], PTM}),
    .SW_15_0(SW_15_0), .FIDBI_15_0(FIDBI_15_0), .GPR_15_0({GPR_15_0[15:8], GPR7, GPR_15_0[6:1], GPR0}),
    .LBA_2_0(LBA_3_0[2:0]), .LAA_3_1(LAA_3_0[3:1]), .AARG0(AARG0),
    .F_15_0({F15, F_15_0[14:12], F11, F_15_0[10:1], F0}), .A_15_0(A_15_0), .ALUCLK(ALUCLK), .ALUD2N(ALUD2N),
    .CSIDBS_4_0(CSIDBS_4_0), .G_15_0(G_15_0), .D_15_0(D_15_0));
  not not_17 (AARG0, AARG0_MUX_zn);
  // Probe on G_15_0
  // Probe on D_15_0

  // Other names for the same wires on the sheet: CD_10_9[1:0] = CD_15_0[10:9]; CSIDBS_2 = CSIDBS_4_0[2];
  //   F_15_0 (some bits) = {F15, F11, F0}; GPR_15_0 (some bits) = {GPR7, GPR0}; LAA_0 = LAA_3_0[0];
  //   LAA_3_1[2:0] = LAA_3_0[3:1]; LBA_2_0[2:0] = LBA_3_0[2:0]; LBA_3 = LBA_3_0[3];
  //   STS_15_0 (some bits) = {IONI, PONI, DOUBLE, PIL_3_0, STS7, STS6, Z, PTM}; Q_15_0 (some bits) = {Q15, Q0}

  // Notes on the sheet:
  //   Input to ARG register ONLY
  //   Selection if input has been validated by ronny 04.12.2023
endmodule

module CGA_CPU_ALU_CONTR (
  input  STS7,
  input  CRY,
  input  F0,
  input  Q0,
  input  Q15,
  input  XFETCHN,
  input  LDGPRN,
  input  [1:0] CSMIS_1_0,
  input  [1:0] CD_10_9,
  input  [1:0] CSSST_1_0,
  input  [1:0] CSCINSEL_1_0,
  input  LDIRV,
  input  UPN,
  input  STS6,
  input  GPR0,
  input  LCZN,
  input  ALUCLK,
  input  [8:0] CSALUI_8_0,
  input  [1:0] CSALUM_1_0,
  input  DGPR0N,
  input  F15,
  output ALUD2N,
  output [1:0] QSEL_1_0,
  output GPRLI,
  output RRI,
  output QLI,
  output RLI,
  output [2:0] GPRC_2_0,
  output ALUI8N,
  output CI,
  output BDEST,
  output [1:0] CSTS_1_0,
  output ALUI7,
  output MI,
  output RSN,
  output FSEL,
  output LOG,
  output ALUI4,
  output SB,
  output SA,
  output RA,
  output RD
);

  wire ALUI1N, ALUI3, ALUI6, ALUI6N, ALUI7N, ALUI8, and_1_out, and_2_out, and_3_out, and_4_out, and_5_out,
       CONTR_REG_qc, CONTR_REG_qd, CONTR_REG_qfn, CONTR_REG_qg, CONTR_REG_qh, CSALUI7_MUX_zn, CSALUI8_MUX_zn,
       CSMIS0_MUX_zn, CSMIS1_MUX_zn, d_ff_1_q, d_ff_2_q, d_ff_4_q, nand_1_out, nand_2_out, nand_3_out,
       nand_4_out, nand_5_out, nand_6_out, nand_7_out, nand_8_out, nand_9_out, nand_10_out, nand_11_out,
       nand_12_out, nand_13_out, nand_14_out, nand_15_out, nand_16_out, nand_18_out, nand_20_out,
       nand_21_out, nand_22_out, nand_23_out, nand_24_out, nand_25_out, nand_26_out, nand_27_out,
       nand_28_out, nand_29_out, nand_33_out, nand_35_out, nand_37_out, nand_38_out, nand_39_out,
       nand_40_out, nor_1_out, nor_2_out, nor_3_out, nor_4_out, nor_5_out, nor_6_out, nor_7_out, not_1_out,
       not_2_out, not_3_out, not_4_out, not_5_out, REG_BAAD_qan, REG_BAAD_qbn, REG_BAAD_qc, REG_BAAD_qd,
       REG_RFLA4_qa, REG_RFLA4_qbn, REG_RFLA4_qc, REG_RFLA4_qdn, SSEL0, SSEL0N, SSEL1, SSEL1N;

  D_Flip_Flop d_ff_1 (.D(CD_10_9[1]), .clk(LDIRV), .Q(d_ff_1_q));  // open: Qn, preset, reset
  D_Flip_Flop d_ff_2 (.D(CD_10_9[0]), .clk(LDIRV), .Q(d_ff_2_q));  // open: Qn, preset, reset
  not not_1 (not_1_out, CSALUM_1_0[0]);
  and and_1 (and_1_out, CSALUM_1_0[1], CSALUM_1_0[0]);
  nor nor_1 (nor_1_out, CSALUM_1_0[1], not_1_out);
  nand nand_1 (nand_1_out, CSALUM_1_0[1], not_1_out);
  not not_2 (not_2_out, CSALUI_8_0[3]);
  not not_3 (not_3_out, CSALUI_8_0[4]);
  not not_4 (not_4_out, CSALUI_8_0[2]);
  not not_5 (not_5_out, CSALUI_8_0[0]);
  and and_2 (and_2_out, not_3_out, ALUI3);
  and and_3 (and_3_out, ALUI3, CSALUI_8_0[5]);
  nand nand_2 (nand_2_out, CSALUI_8_0[5], CSALUI_8_0[4]);
  and and_4 (and_4_out, ALUI3, CSALUI_8_0[4]);
  nand nand_3 (nand_3_out, CSALUI_8_0[2], CSALUI_8_0[0]);
  nand nand_4 (nand_4_out, CSALUI_8_0[2], ALUI1N);
  nand nand_5 (nand_5_out, not_4_out, CSALUI_8_0[0]);
  nand nand_6 (nand_6_out, ALUI1N, not_4_out);
  nand nand_7 (nand_7_out, ALUI1N, not_5_out);
  MUX21LP CSMIS1_MUX (.A(CSMIS_1_0[1]), .B(d_ff_1_q), .S(and_1_out), .ZN(CSMIS1_MUX_zn));
  MUX21LP CSMIS0_MUX (.A(CSMIS_1_0[0]), .B(d_ff_2_q), .S(and_1_out), .ZN(CSMIS0_MUX_zn));
  MUX21LP CSALUI7_MUX (.A(CSALUI_8_0[7]), .B(UPN), .S(and_1_out), .ZN(CSALUI7_MUX_zn));
  MUX21LP CSALUI8_MUX (.A(CSALUI_8_0[8]), .B(LCZN), .S(and_1_out), .ZN(CSALUI8_MUX_zn));
  nand nand_8 (nand_8_out, ALUI7, F15);
  nand nand_9 (nand_9_out, ALUI7N, ALUI6N, Q0);
  nand nand_10 (nand_10_out, ALUI7N, ALUI6, F0);
  nor nor_2 (nor_2_out, and_2_out, and_3_out);
  nor nor_3 (nor_3_out, and_4_out, CSALUI_8_0[5], 1'b0);
  nand nand_11 (nand_11_out, nand_3_out, nand_4_out);
  nand nand_12 (nand_12_out, nand_4_out, nand_5_out);
  nand nand_13 (nand_13_out, nand_7_out, CSALUI_8_0[2]);
  not nand_14 (nand_14_out, F0);  // NAND_Gate
  nand nand_15 (nand_15_out, Q0, ALUI6N);
  nand nand_16 (nand_16_out, ALUI6N, Q15);
  MUX21LP ALUI3_MUX (.A(DGPR0N), .B(not_2_out), .S(nand_1_out), .ZN(ALUI3));
  MUX21LP ALUI1N_MUX (.A(CSALUI_8_0[1]), .B(DGPR0N), .S(nor_1_out), .ZN(ALUI1N));
  nand nand_17 (MI, nand_8_out, nand_9_out, nand_10_out);
  nor nor_4 (nor_4_out, SSEL1N, SSEL0N);
  nor nor_5 (nor_5_out, SSEL1N, SSEL0, ALUI6);
  nor nor_6 (nor_6_out, SSEL0N, SSEL1);
  nor nor_7 (nor_7_out, SSEL0, SSEL1);
  nand nand_18 (nand_18_out, nand_14_out, nand_15_out);
  D_Flip_Flop d_ff_3 (.D(CSALUI_8_0[6]), .clk(ALUCLK), .Q(ALUI6), .Qn(ALUI6N));  // open: preset, reset
  nand nand_19 (ALUD2N, ALUI6N, ALUI7, ALUI8N);
  nand nand_20 (nand_20_out, ALUI6N, ALUI8);
  nand nand_21 (nand_21_out, ALUI6N, ALUI7N);
  nand nand_22 (nand_22_out, STS7, CRY);
  nand nand_23 (nand_23_out, STS7, GPR0);
  nand nand_24 (nand_24_out, GPR0, CRY);
  nand nand_25 (nand_25_out, STS7, nor_4_out);
  nand nand_26 (nand_26_out, CRY, nor_5_out);
  nand nand_27 (nand_27_out, nand_18_out, nor_6_out);
  nand nand_28 (nand_28_out, F15, nor_7_out);
  nand nand_29 (nand_29_out, F15, nor_6_out);
  and and_5 (and_5_out, CSALUI7_MUX_zn, CSALUI8_MUX_zn);
  R41P REG_RFLA4 (
    .A(nor_2_out), .B(nand_2_out), .C(nor_3_out), .D(CSALUI_8_0[4]), .CP(ALUCLK), .QA(REG_RFLA4_qa),
    .QBN(REG_RFLA4_qbn), .QC(REG_RFLA4_qc), .QDN(REG_RFLA4_qdn));  // open: QAN, QB, QCN, QD
  R41P REG_BAAD (
    .A(nand_11_out), .B(nand_12_out), .C(nand_6_out), .D(nand_13_out), .CP(ALUCLK), .QAN(REG_BAAD_qan),
    .QBN(REG_BAAD_qbn), .QC(REG_BAAD_qc), .QD(REG_BAAD_qd));  // open: QA, QB, QCN, QDN
  not not_6 (QSEL_1_0[1], nand_20_out);
  not not_7 (QSEL_1_0[0], nand_21_out);
  D_Flip_Flop d_ff_4 (.D(and_5_out), .clk(ALUCLK), .Q(d_ff_4_q));  // open: Qn, preset, reset
  not not_8 (RSN, REG_RFLA4_qa);
  not not_9 (FSEL, REG_RFLA4_qbn);
  not not_10 (LOG, REG_RFLA4_qc);
  not not_11 (ALUI4, REG_RFLA4_qdn);
  not not_12 (SB, REG_BAAD_qan);
  not not_13 (SA, REG_BAAD_qbn);
  not not_14 (RA, REG_BAAD_qc);
  not not_15 (RD, REG_BAAD_qd);
  nand nand_30 (GPRLI, nand_22_out, nand_23_out, nand_24_out);
  nand nand_31 (RRI, nand_25_out, nand_26_out, nand_27_out, nand_28_out);
  nand nand_32 (QLI, nand_25_out, nand_29_out);
  nand nand_33 (nand_33_out, QLI, ALUI6);
  not not_16 (BDEST, d_ff_4_q);
  nand nand_34 (RLI, nand_33_out, nand_16_out);
  R81 CONTR_REG (
    .A(CSMIS1_MUX_zn), .B(CSMIS0_MUX_zn), .C(CSALUI7_MUX_zn), .D(CSALUI8_MUX_zn), .E(CSSST_1_0[0]),
    .F(CSSST_1_0[1]), .G(CSCINSEL_1_0[0]), .H(CSCINSEL_1_0[1]), .CP(ALUCLK), .QA(SSEL1N), .QAN(SSEL1),
    .QB(SSEL0N), .QBN(SSEL0), .QC(CONTR_REG_qc), .QD(CONTR_REG_qd), .QE(CSTS_1_0[0]), .QFN(CONTR_REG_qfn),
    .QG(CONTR_REG_qg), .QH(CONTR_REG_qh));  // open: QCN, QDN, QEN, QF, QGN, QHN
  not not_17 (ALUI7, CONTR_REG_qc);
  not not_18 (ALUI8, CONTR_REG_qd);
  nand nand_35 (nand_35_out, ALUI8, and_1_out);
  not not_19 (ALUI7N, ALUI7);
  not not_20 (ALUI8N, ALUI8);
  nand nand_36 (CSTS_1_0[1], CONTR_REG_qfn, nand_35_out);
  nand nand_37 (nand_37_out, XFETCHN, ALUI7N);
  nand nand_38 (nand_38_out, nand_37_out, LDGPRN);
  not not_21 (GPRC_2_0[0], nand_38_out);
  nand nand_39 (nand_39_out, LDGPRN, XFETCHN);
  not not_22 (GPRC_2_0[1], nand_39_out);
  nand nand_40 (nand_40_out, GPRC_2_0[1], ALUI8N);
  not not_23 (GPRC_2_0[2], nand_40_out);
  MUX41P CI_SEL_MUX (.D0(1'b0), .D1(1'b1), .D2(STS6), .D3(GPR0), .A(CONTR_REG_qg), .B(CONTR_REG_qh), .Z(CI));

  // Other names for the same wires on the sheet: CD9 = CD_10_9[0]; CD10 = CD_10_9[1]; CSALUI0 = CSALUI_8_0[0];
  //   CSALUI1 = CSALUI_8_0[1]; CSALUI2 = CSALUI_8_0[2]; CSALUI3 = CSALUI_8_0[3]; CSALUI4 = CSALUI_8_0[4];
  //   CSALUI5 = CSALUI_8_0[5]; CSALUI6 = CSALUI_8_0[6]; CSALUI7 = CSALUI_8_0[7]; CSALUI8 = CSALUI_8_0[8]

  // Notes on the sheet:
  //   SHOULD BE LATCH Gated by LDIRV!!!
  //   CSCALUM = ALU.MODE = 0=uShift, 1=FMU (multiply) 2=FDV (div) 3=IR Shift
  //   CSMIS1
  //   CSMIS0
  //   CSSTS =  0=HOLD,1=SET C O Q, 2=SET M, 3=LOAD STS
  //   CSCINSEL = Carry In Select = 0: 0=1,  1=1, 2=C, 3=GPR0
  //   CSMIS = Shift Mode = 0=Arithm, 1=ROT, 2=IN, 3=LIN
  //   Calculates ALU Source
  //   Calulates ALU Function
  //   QSEL1
  //   QSEL0
  //   RSN=1 => Subtract, else ADD
  //   LOG=1, Logic function (AND/OR) else ADD/SUB
  //   CINSEL0
  //   CINSEL1
  //   FSEL = 1, Logic function XOR else OR/AND/NOT
  //   STS6= STS.Carry
  //   CSTS0
  //   CSTS1
  //   Controls STS bits 4-5-6-7
  //   GPRC0
  //   GPRC1
  //   GPRC2
  //   GPR Commands: 0=??  010=FMU
endmodule

module CGA_ALU_QREG (
  input  [15:0] F_15_0,
  input  QLI,
  input  [1:0] QSEL_1_0,
  input  ALUCLK,
  output [15:0] Q_15_0
);

  wire MUXQ0_z, MUXQ1_z, MUXQ2_z, MUXQ3_z, MUXQ4_z, MUXQ5_z, MUXQ6_z, MUXQ7_z, MUXQ8_z, MUXQ9_z, MUXQ10_z,
       MUXQ11_z, MUXQ12_z, MUXQ13_z, MUXQ14_z, MUXQ15_z;

  MUX41P MUXQ15 (
    .D0(Q_15_0[7]), .D1(F_15_0[15]), .D2(Q_15_0[6]), .D3(Q_15_0[8]), .A(QSEL_1_0[0]), .B(QSEL_1_0[1]),
    .Z(MUXQ15_z));
  MUX41P MUXQ14 (
    .D0(Q_15_0[6]), .D1(F_15_0[14]), .D2(Q_15_0[5]), .D3(Q_15_0[7]), .A(QSEL_1_0[0]), .B(QSEL_1_0[1]),
    .Z(MUXQ14_z));
  MUX41P MUXQ13 (
    .D0(Q_15_0[5]), .D1(F_15_0[13]), .D2(Q_15_0[4]), .D3(Q_15_0[6]), .A(QSEL_1_0[0]), .B(QSEL_1_0[1]),
    .Z(MUXQ13_z));
  MUX41P MUXQ12 (
    .D0(Q_15_0[4]), .D1(F_15_0[12]), .D2(Q_15_0[3]), .D3(Q_15_0[5]), .A(QSEL_1_0[0]), .B(QSEL_1_0[1]),
    .Z(MUXQ12_z));
  MUX41P MUXQ11 (
    .D0(Q_15_0[3]), .D1(F_15_0[11]), .D2(Q_15_0[2]), .D3(Q_15_0[4]), .A(QSEL_1_0[0]), .B(QSEL_1_0[1]),
    .Z(MUXQ11_z));
  MUX41P MUXQ10 (
    .D0(Q_15_0[2]), .D1(F_15_0[10]), .D2(Q_15_0[1]), .D3(Q_15_0[3]), .A(QSEL_1_0[0]), .B(QSEL_1_0[1]),
    .Z(MUXQ10_z));
  MUX41P MUXQ9 (
    .D0(Q_15_0[1]), .D1(F_15_0[9]), .D2(Q_15_0[0]), .D3(Q_15_0[2]), .A(QSEL_1_0[0]), .B(QSEL_1_0[1]),
    .Z(MUXQ9_z));
  MUX41P MUXQ8 (
    .D0(Q_15_0[0]), .D1(F_15_0[8]), .D2(Q_15_0[15]), .D3(Q_15_0[1]), .A(QSEL_1_0[0]), .B(QSEL_1_0[1]),
    .Z(MUXQ8_z));
  MUX41P MUXQ7 (
    .D0(Q_15_0[15]), .D1(F_15_0[7]), .D2(Q_15_0[14]), .D3(Q_15_0[0]), .A(QSEL_1_0[0]), .B(QSEL_1_0[1]),
    .Z(MUXQ7_z));
  MUX41P MUXQ6 (
    .D0(Q_15_0[14]), .D1(F_15_0[6]), .D2(Q_15_0[13]), .D3(Q_15_0[15]), .A(QSEL_1_0[0]), .B(QSEL_1_0[1]),
    .Z(MUXQ6_z));
  MUX41P MUXQ5 (
    .D0(Q_15_0[13]), .D1(F_15_0[5]), .D2(Q_15_0[12]), .D3(Q_15_0[14]), .A(QSEL_1_0[0]), .B(QSEL_1_0[1]),
    .Z(MUXQ5_z));
  MUX41P MUXQ4 (
    .D0(Q_15_0[12]), .D1(F_15_0[4]), .D2(Q_15_0[11]), .D3(Q_15_0[13]), .A(QSEL_1_0[0]), .B(QSEL_1_0[1]),
    .Z(MUXQ4_z));
  MUX41P MUXQ3 (
    .D0(Q_15_0[11]), .D1(F_15_0[3]), .D2(Q_15_0[10]), .D3(Q_15_0[12]), .A(QSEL_1_0[0]), .B(QSEL_1_0[1]),
    .Z(MUXQ3_z));
  MUX41P MUXQ2 (
    .D0(Q_15_0[10]), .D1(F_15_0[2]), .D2(Q_15_0[9]), .D3(Q_15_0[11]), .A(QSEL_1_0[0]), .B(QSEL_1_0[1]),
    .Z(MUXQ2_z));
  MUX41P MUXQ1 (
    .D0(Q_15_0[9]), .D1(F_15_0[1]), .D2(Q_15_0[8]), .D3(Q_15_0[10]), .A(QSEL_1_0[0]), .B(QSEL_1_0[1]),
    .Z(MUXQ1_z));
  MUX41P MUXQ0 (
    .D0(Q_15_0[8]), .D1(F_15_0[0]), .D2(QLI), .D3(Q_15_0[9]), .A(QSEL_1_0[0]), .B(QSEL_1_0[1]), .Z(MUXQ0_z));
  R81P REG_Q_HI (
    .A(MUXQ15_z), .B(MUXQ14_z), .C(MUXQ13_z), .D(MUXQ12_z), .E(MUXQ11_z), .F(MUXQ10_z), .G(MUXQ9_z),
    .H(MUXQ8_z), .CP(ALUCLK), .QA(Q_15_0[7]), .QB(Q_15_0[6]), .QC(Q_15_0[5]), .QD(Q_15_0[4]), .QE(Q_15_0[3]),
    .QF(Q_15_0[2]), .QG(Q_15_0[1]), .QH(Q_15_0[0]));  // open: QAN, QBN, QCN, QDN, QEN, QFN, QGN, QHN
  R81P REG_Q_LO (
    .A(MUXQ7_z), .B(MUXQ6_z), .C(MUXQ5_z), .D(MUXQ4_z), .E(MUXQ3_z), .F(MUXQ2_z), .G(MUXQ1_z), .H(MUXQ0_z),
    .CP(ALUCLK), .QA(Q_15_0[15]), .QB(Q_15_0[14]), .QC(Q_15_0[13]), .QD(Q_15_0[12]), .QE(Q_15_0[11]),
    .QF(Q_15_0[10]), .QG(Q_15_0[9]), .QH(Q_15_0[8]));  // open: QAN, QBN, QCN, QDN, QEN, QFN, QGN, QHN

  // Other names for the same wires on the sheet: F0 = F_15_0[0]; F1 = F_15_0[1]; F2 = F_15_0[2]; F3 = F_15_0[3];
  //   F4 = F_15_0[4]; F5 = F_15_0[5]; F6 = F_15_0[6]; F7 = F_15_0[7]; F8 = F_15_0[8]; F9 = F_15_0[9];
  //   F10 = F_15_0[10]; F11 = F_15_0[11]; F12 = F_15_0[12]; F13 = F_15_0[13]; F14 = F_15_0[14]; F15 = F_15_0[15];
  //   Q8 = Q_15_0[0]; Q9 = Q_15_0[1]; Q10 = Q_15_0[2]; Q11 = Q_15_0[3]; Q12 = Q_15_0[4]; Q13 = Q_15_0[5];
  //   Q14 = Q_15_0[6]; Q15 = Q_15_0[7]; Q0 = Q_15_0[8]; Q1 = Q_15_0[9]; Q2 = Q_15_0[10]; Q3 = Q_15_0[11];
  //   Q4 = Q_15_0[12]; Q5 = Q_15_0[13]; Q6 = Q_15_0[14]; Q7 = Q_15_0[15]

  // Notes on the sheet:
  //   Page 43 - CGA_ALU_QREG (tested manually, Ronny 09.06.2023)
endmodule

module CGA_CPU_ALU_RMUX (
  input  [15:0] D_15_0,
  input  [15:0] A_15_0,
  input  RD,
  input  RA,
  output [15:0] RN_15_0
);

  RMUX_Gates RN15 (.A(A_15_0[15]), .RA(RA), .D(D_15_0[15]), .RD(RD), .RN(RN_15_0[15]));
  RMUX_Gates RN14 (.A(A_15_0[14]), .RA(RA), .D(D_15_0[14]), .RD(RD), .RN(RN_15_0[14]));
  RMUX_Gates RN13 (.A(A_15_0[13]), .RA(RA), .D(D_15_0[13]), .RD(RD), .RN(RN_15_0[13]));
  RMUX_Gates RN12 (.A(A_15_0[12]), .RA(RA), .D(D_15_0[12]), .RD(RD), .RN(RN_15_0[12]));
  RMUX_Gates RN11 (.A(A_15_0[11]), .RA(RA), .D(D_15_0[11]), .RD(RD), .RN(RN_15_0[11]));
  RMUX_Gates RN10 (.A(A_15_0[10]), .RA(RA), .D(D_15_0[10]), .RD(RD), .RN(RN_15_0[10]));
  RMUX_Gates RN9 (.A(A_15_0[9]), .RA(RA), .D(D_15_0[9]), .RD(RD), .RN(RN_15_0[9]));
  RMUX_Gates RN8 (.A(A_15_0[8]), .RA(RA), .D(D_15_0[8]), .RD(RD), .RN(RN_15_0[8]));
  RMUX_Gates RN7 (.A(A_15_0[7]), .RA(RA), .D(D_15_0[7]), .RD(RD), .RN(RN_15_0[7]));
  RMUX_Gates RN6 (.A(A_15_0[6]), .RA(RA), .D(D_15_0[6]), .RD(RD), .RN(RN_15_0[6]));
  RMUX_Gates RN5 (.A(A_15_0[5]), .RA(RA), .D(D_15_0[5]), .RD(RD), .RN(RN_15_0[5]));
  RMUX_Gates RN4 (.A(A_15_0[4]), .RA(RA), .D(D_15_0[4]), .RD(RD), .RN(RN_15_0[4]));
  RMUX_Gates RN3 (.A(A_15_0[3]), .RA(RA), .D(D_15_0[3]), .RD(RD), .RN(RN_15_0[3]));
  RMUX_Gates RN2 (.A(A_15_0[2]), .RA(RA), .D(D_15_0[2]), .RD(RD), .RN(RN_15_0[2]));
  RMUX_Gates RN1 (.A(A_15_0[1]), .RA(RA), .D(D_15_0[1]), .RD(RD), .RN(RN_15_0[1]));
  RMUX_Gates RN0 (.A(A_15_0[0]), .RA(RA), .D(D_15_0[0]), .RD(RD), .RN(RN_15_0[0]));

  // Notes on the sheet:
  //   Page 44 - CGA_ALU_RMUX (tested manually, Ronny 09.06.2023)
endmodule

module RMUX_Gates (
  input  A,
  input  RA,
  input  D,
  input  RD,
  output RN
);

  wire and_1_out, and_2_out;

  and and_1 (and_1_out, A, RA);
  and and_2 (and_2_out, D, RD);
  nor nor_1 (RN, and_1_out, and_2_out);
endmodule

module CGA_ALU_SMUX (
  input  [15:0] A_15_0,
  input  [15:0] B_15_0,
  input  [15:0] Q_15_0,
  input  SA,
  input  SB,
  output [15:0] S_15_0
);

  MUX41P MUXS15 (.D0(Q_15_0[15]), .D1(B_15_0[15]), .D2(1'b0), .D3(A_15_0[15]), .A(SA), .B(SB), .Z(S_15_0[15]));
  MUX41P MUXS14 (.D0(Q_15_0[14]), .D1(B_15_0[14]), .D2(1'b0), .D3(A_15_0[14]), .A(SA), .B(SB), .Z(S_15_0[14]));
  MUX41P MUXS13 (.D0(Q_15_0[13]), .D1(B_15_0[13]), .D2(1'b0), .D3(A_15_0[13]), .A(SA), .B(SB), .Z(S_15_0[13]));
  MUX41P MUXS12 (.D0(Q_15_0[12]), .D1(B_15_0[12]), .D2(1'b0), .D3(A_15_0[12]), .A(SA), .B(SB), .Z(S_15_0[12]));
  MUX41P MUXS11 (.D0(Q_15_0[11]), .D1(B_15_0[11]), .D2(1'b0), .D3(A_15_0[11]), .A(SA), .B(SB), .Z(S_15_0[11]));
  MUX41P MUXS10 (.D0(Q_15_0[10]), .D1(B_15_0[10]), .D2(1'b0), .D3(A_15_0[10]), .A(SA), .B(SB), .Z(S_15_0[10]));
  MUX41P MUXS9 (.D0(Q_15_0[9]), .D1(B_15_0[9]), .D2(1'b0), .D3(A_15_0[9]), .A(SA), .B(SB), .Z(S_15_0[9]));
  MUX41P MUXS8 (.D0(Q_15_0[8]), .D1(B_15_0[8]), .D2(1'b0), .D3(A_15_0[8]), .A(SA), .B(SB), .Z(S_15_0[8]));
  MUX41P MUXS7 (.D0(Q_15_0[7]), .D1(B_15_0[7]), .D2(1'b0), .D3(A_15_0[7]), .A(SA), .B(SB), .Z(S_15_0[7]));
  MUX41P MUXS6 (.D0(Q_15_0[6]), .D1(B_15_0[6]), .D2(1'b0), .D3(A_15_0[6]), .A(SA), .B(SB), .Z(S_15_0[6]));
  MUX41P MUXS5 (.D0(Q_15_0[5]), .D1(B_15_0[5]), .D2(1'b0), .D3(A_15_0[5]), .A(SA), .B(SB), .Z(S_15_0[5]));
  MUX41P MUXS4 (.D0(Q_15_0[4]), .D1(B_15_0[4]), .D2(1'b0), .D3(A_15_0[4]), .A(SA), .B(SB), .Z(S_15_0[4]));
  MUX41P MUXS3 (.D0(Q_15_0[3]), .D1(B_15_0[3]), .D2(1'b0), .D3(A_15_0[3]), .A(SA), .B(SB), .Z(S_15_0[3]));
  MUX41P MUXS2 (.D0(Q_15_0[2]), .D1(B_15_0[2]), .D2(1'b0), .D3(A_15_0[2]), .A(SA), .B(SB), .Z(S_15_0[2]));
  MUX41P MUXS1 (.D0(Q_15_0[1]), .D1(B_15_0[1]), .D2(1'b0), .D3(A_15_0[1]), .A(SA), .B(SB), .Z(S_15_0[1]));
  MUX41P MUXS0 (.D0(Q_15_0[0]), .D1(B_15_0[0]), .D2(1'b0), .D3(A_15_0[0]), .A(SA), .B(SB), .Z(S_15_0[0]));

  // Notes on the sheet:
  //   Page 45 - CGA_ALU_SMUX (tested manually, Ronny 09.06.2023)
endmodule

module CGA_CPU_ALU_RALU (
  input  CI,
  input  LOG,
  input  ALUI4,
  input  FSEL,
  input  RSN,
  input  [15:0] RN_15_0,
  input  [15:0] S_15_0,
  output ZF,
  output [15:0] F_15_0,
  output CRY,
  output SGR,
  output OVF
);

  wire adder_1_cout, nand_1_out, nand_2_out, nand_3_out, nand_4_out, nand_5_out, nand_6_out, nand_7_out,
       nand_9_out, not_3_out, not_4_out, not_5_out, not_22_out, not_23_out, not_24_out;
  wire [15:0] adder_1_out, AF_LF_MUX_o_15_0, LOGOP_lf_15_0, not_1_out, not_2_out, RN_R_MUX_o_15_0,
       SN_S_MUX_o_15_0;

  assign not_1_out = ~RN_15_0;  // NOT_Gate not_1, 16 bits wide
  CGA_ALU_RALU_MUX216L RN_R_MUX (.T_15_0(RN_15_0), .F_15_0(not_1_out), .S(RSN), .O_15_0(RN_R_MUX_o_15_0));
  assign not_2_out = ~S_15_0;  // NOT_Gate not_2, 16 bits wide
  not not_3 (not_3_out, RN_R_MUX_o_15_0[15]);
  // Probe on RN_R_MUX_o_15_0
  CGA_ALU_RALU_MUX216L SN_S_MUX (.T_15_0(not_2_out), .F_15_0(S_15_0), .S(ALUI4), .O_15_0(SN_S_MUX_o_15_0));
  not not_4 (not_4_out, SN_S_MUX_o_15_0[15]);
  // Probe on RN_R_MUX_o_15_0
  // Probe on SN_S_MUX_o_15_0
  // Probe on RN_R_MUX_o_15_0
  // Probe on S_15_0
  Adder #(.width(16)) adder_1 (
    .a(RN_R_MUX_o_15_0), .b(SN_S_MUX_o_15_0), .out(adder_1_out), .cin(CI), .cout(adder_1_cout));
  // Probe on adder_1_out
  CGA_ALU_RALU_LOGOP LOGOP (
    .A_15_0(RN_R_MUX_o_15_0), .S_15_0(S_15_0), .FSEL(FSEL), .ALU14(ALUI4), .LF_15_0(LOGOP_lf_15_0));
  // Probe on LOGOP_lf_15_0
  CGA_ALU_RALU_MUX216L AF_LF_MUX (.T_15_0(adder_1_out), .F_15_0(LOGOP_lf_15_0), .S(LOG), .O_15_0(AF_LF_MUX_o_15_0));
  // Probe on AF_LF_MUX_o_15_0
  not not_5 (not_5_out, F_15_0[15]);
  not not_6 (F_15_0[15], AF_LF_MUX_o_15_0[15]);
  not not_7 (F_15_0[14], AF_LF_MUX_o_15_0[14]);
  not not_8 (F_15_0[13], AF_LF_MUX_o_15_0[13]);
  not not_9 (F_15_0[12], AF_LF_MUX_o_15_0[12]);
  not not_10 (F_15_0[11], AF_LF_MUX_o_15_0[11]);
  not not_11 (F_15_0[10], AF_LF_MUX_o_15_0[10]);
  not not_12 (F_15_0[9], AF_LF_MUX_o_15_0[9]);
  not not_13 (F_15_0[8], AF_LF_MUX_o_15_0[8]);
  not not_14 (F_15_0[7], AF_LF_MUX_o_15_0[7]);
  not not_15 (F_15_0[6], AF_LF_MUX_o_15_0[6]);
  not not_16 (F_15_0[5], AF_LF_MUX_o_15_0[5]);
  not not_17 (F_15_0[4], AF_LF_MUX_o_15_0[4]);
  not not_18 (F_15_0[3], AF_LF_MUX_o_15_0[3]);
  not not_19 (F_15_0[2], AF_LF_MUX_o_15_0[2]);
  not not_20 (F_15_0[1], AF_LF_MUX_o_15_0[1]);
  not not_21 (F_15_0[0], AF_LF_MUX_o_15_0[0]);
  nand nand_1 (nand_1_out, not_3_out, not_5_out);
  nand nand_2 (nand_2_out, not_3_out, not_4_out);
  nand nand_3 (nand_3_out, not_4_out, not_5_out);
  nand nand_4 (nand_4_out, AF_LF_MUX_o_15_0[11], AF_LF_MUX_o_15_0[10], AF_LF_MUX_o_15_0[9], AF_LF_MUX_o_15_0[8]);
  nand nand_5 (nand_5_out, AF_LF_MUX_o_15_0[7], AF_LF_MUX_o_15_0[6], AF_LF_MUX_o_15_0[5], AF_LF_MUX_o_15_0[4], AF_LF_MUX_o_15_0[3], AF_LF_MUX_o_15_0[2], AF_LF_MUX_o_15_0[1], AF_LF_MUX_o_15_0[0]);
  nand nand_6 (nand_6_out, RN_R_MUX_o_15_0[15], SN_S_MUX_o_15_0[15], not_5_out);
  nand nand_7 (nand_7_out, not_3_out, not_4_out, F_15_0[15]);
  not not_22 (not_22_out, nand_4_out);
  not not_23 (not_23_out, nand_5_out);
  not not_24 (not_24_out, LOG);
  and and_1 (CRY, not_24_out, adder_1_cout);
  nand nand_8 (SGR, nand_1_out, nand_2_out, nand_3_out);
  nand nand_9 (nand_9_out, AF_LF_MUX_o_15_0[15], AF_LF_MUX_o_15_0[14], AF_LF_MUX_o_15_0[13], AF_LF_MUX_o_15_0[12], not_22_out, not_23_out);
  nand nand_10 (OVF, nand_6_out, nand_7_out);
  not not_25 (ZF, nand_9_out);

  // Notes on the sheet:
  //   Page 46 - CGA_ALU_RALU (reviewed manually, Ronny 09.06.2023)
  //   RSN=1 => Subtract, else ADD
  //   CI = 1, Carry IN =1 else NO Carry
  //   LOG=1, Logic function (AND/OR) else ADD/SUB
  //   FSEL = 1, Logic function XOR else OR/AND/NOT
  //   RN
  //   R
  //   A_15_0
  //   SN
  //   S
  //   S_15_0
  //   A_15_0
  //   B_15_0
  //   AF_15_0
  //   LF_15_0
endmodule

module CGA_ALU_RALU_MUX216L (
  input  [15:0] T_15_0,
  input  [15:0] F_15_0,
  input  S,
  output [15:0] O_15_0
);

  wire not_1_out;

  not not_1 (not_1_out, S);
  MUX21LP MUXQ15 (.A(F_15_0[15]), .B(T_15_0[15]), .S(not_1_out), .ZN(O_15_0[15]));
  MUX21LP MUXQ14 (.A(F_15_0[14]), .B(T_15_0[14]), .S(not_1_out), .ZN(O_15_0[14]));
  MUX21LP MUXQ13 (.A(F_15_0[13]), .B(T_15_0[13]), .S(not_1_out), .ZN(O_15_0[13]));
  MUX21LP MUXQ12 (.A(F_15_0[12]), .B(T_15_0[12]), .S(not_1_out), .ZN(O_15_0[12]));
  MUX21LP MUXQ11 (.A(F_15_0[11]), .B(T_15_0[11]), .S(not_1_out), .ZN(O_15_0[11]));
  MUX21LP MUXQ10 (.A(F_15_0[10]), .B(T_15_0[10]), .S(not_1_out), .ZN(O_15_0[10]));
  MUX21LP MUXQ9 (.A(F_15_0[9]), .B(T_15_0[9]), .S(not_1_out), .ZN(O_15_0[9]));
  MUX21LP MUXQ8 (.A(F_15_0[8]), .B(T_15_0[8]), .S(not_1_out), .ZN(O_15_0[8]));
  MUX21LP MUXQ7 (.A(F_15_0[7]), .B(T_15_0[7]), .S(not_1_out), .ZN(O_15_0[7]));
  MUX21LP MUXQ6 (.A(F_15_0[6]), .B(T_15_0[6]), .S(not_1_out), .ZN(O_15_0[6]));
  MUX21LP MUXQ5 (.A(F_15_0[5]), .B(T_15_0[5]), .S(not_1_out), .ZN(O_15_0[5]));
  MUX21LP MUXQ4 (.A(F_15_0[4]), .B(T_15_0[4]), .S(not_1_out), .ZN(O_15_0[4]));
  MUX21LP MUXQ3 (.A(F_15_0[3]), .B(T_15_0[3]), .S(not_1_out), .ZN(O_15_0[3]));
  MUX21LP MUXQ2 (.A(F_15_0[2]), .B(T_15_0[2]), .S(not_1_out), .ZN(O_15_0[2]));
  MUX21LP MUXQ1 (.A(F_15_0[1]), .B(T_15_0[1]), .S(not_1_out), .ZN(O_15_0[1]));
  MUX21LP MUXQ0 (.A(F_15_0[0]), .B(T_15_0[0]), .S(not_1_out), .ZN(O_15_0[0]));

  // Notes on the sheet:
  //   Page 47 - CGA_ALU_RALU_MUX216L(tested manually, Ronny 09.06.2023)
endmodule

module CGA_ALU_RALU_LOGOP (
  input  [15:0] A_15_0,
  input  [15:0] S_15_0,
  input  FSEL,
  input  ALU14,
  output [15:0] LF_15_0
);

  MUX41P MUXLF15 (.D0(1'b0), .D1(ALU14), .D2(ALU14), .D3(FSEL), .A(A_15_0[15]), .B(S_15_0[15]), .Z(LF_15_0[15]));
  MUX41P MUXLF14 (.D0(1'b0), .D1(ALU14), .D2(ALU14), .D3(FSEL), .A(A_15_0[14]), .B(S_15_0[14]), .Z(LF_15_0[14]));
  MUX41P MUXLF13 (.D0(1'b0), .D1(ALU14), .D2(ALU14), .D3(FSEL), .A(A_15_0[13]), .B(S_15_0[13]), .Z(LF_15_0[13]));
  MUX41P MUXLF12 (.D0(1'b0), .D1(ALU14), .D2(ALU14), .D3(FSEL), .A(A_15_0[12]), .B(S_15_0[12]), .Z(LF_15_0[12]));
  MUX41P MUXLF11 (.D0(1'b0), .D1(ALU14), .D2(ALU14), .D3(FSEL), .A(A_15_0[11]), .B(S_15_0[11]), .Z(LF_15_0[11]));
  MUX41P MUXLF10 (.D0(1'b0), .D1(ALU14), .D2(ALU14), .D3(FSEL), .A(A_15_0[10]), .B(S_15_0[10]), .Z(LF_15_0[10]));
  MUX41P MUXLF9 (.D0(1'b0), .D1(ALU14), .D2(ALU14), .D3(FSEL), .A(A_15_0[9]), .B(S_15_0[9]), .Z(LF_15_0[9]));
  MUX41P MUXLF8 (.D0(1'b0), .D1(ALU14), .D2(ALU14), .D3(FSEL), .A(A_15_0[8]), .B(S_15_0[8]), .Z(LF_15_0[8]));
  MUX41P MUXLF7 (.D0(1'b0), .D1(ALU14), .D2(ALU14), .D3(FSEL), .A(A_15_0[7]), .B(S_15_0[7]), .Z(LF_15_0[7]));
  MUX41P MUXLF6 (.D0(1'b0), .D1(ALU14), .D2(ALU14), .D3(FSEL), .A(A_15_0[6]), .B(S_15_0[6]), .Z(LF_15_0[6]));
  MUX41P MUXLF5 (.D0(1'b0), .D1(ALU14), .D2(ALU14), .D3(FSEL), .A(A_15_0[5]), .B(S_15_0[5]), .Z(LF_15_0[5]));
  MUX41P MUXLF4 (.D0(1'b0), .D1(ALU14), .D2(ALU14), .D3(FSEL), .A(A_15_0[4]), .B(S_15_0[4]), .Z(LF_15_0[4]));
  MUX41P MUXLL3 (.D0(1'b0), .D1(ALU14), .D2(ALU14), .D3(FSEL), .A(A_15_0[3]), .B(S_15_0[3]), .Z(LF_15_0[3]));
  MUX41P MUXLF2 (.D0(1'b0), .D1(ALU14), .D2(ALU14), .D3(FSEL), .A(A_15_0[2]), .B(S_15_0[2]), .Z(LF_15_0[2]));
  MUX41P MUXLF1 (.D0(1'b0), .D1(ALU14), .D2(ALU14), .D3(FSEL), .A(A_15_0[1]), .B(S_15_0[1]), .Z(LF_15_0[1]));
  MUX41P MUXLF0 (.D0(1'b0), .D1(ALU14), .D2(ALU14), .D3(FSEL), .A(A_15_0[0]), .B(S_15_0[0]), .Z(LF_15_0[0]));

  // Notes on the sheet:
  //   Page 48 - CGA_ALU_RALU_LOGOP (reviewed manually, Ronny 09.06.2023)
endmodule

module CGA_ALU_SHIFT (
  input  RRI,
  input  [15:0] F_15_0,
  input  RLI,
  input  ALUI7,
  input  ALUI8N,
  output [15:0] RB_15_0
);

  wire RB0MUX_zn, RB1MUX_zn, RB2MUX_zn, RB3MUX_zn, RB4MUX_zn, RB5MUX_zn, RB6MUX_zn, RB7MUX_zn, RB8MUX_zn,
       RB9MUX_zn, RB10MUX_zn, RB11MUX_zn, RB12MUX_zn, RB13MUX_zn, RB14MUX_zn, RB15MUX_zn;

  MUX31LP RB15MUX (.D0(RRI), .D1(F_15_0[14]), .D2(F_15_0[15]), .A(ALUI7), .B(ALUI8N), .ZN(RB15MUX_zn));
  MUX31LP RB14MUX (.D0(F_15_0[15]), .D1(F_15_0[13]), .D2(F_15_0[14]), .A(ALUI7), .B(ALUI8N), .ZN(RB14MUX_zn));
  MUX31LP RB13MUX (.D0(F_15_0[14]), .D1(F_15_0[12]), .D2(F_15_0[13]), .A(ALUI7), .B(ALUI8N), .ZN(RB13MUX_zn));
  MUX31LP RB12MUX (.D0(F_15_0[13]), .D1(F_15_0[11]), .D2(F_15_0[12]), .A(ALUI7), .B(ALUI8N), .ZN(RB12MUX_zn));
  MUX31LP RB11MUX (.D0(F_15_0[12]), .D1(F_15_0[10]), .D2(F_15_0[11]), .A(ALUI7), .B(ALUI8N), .ZN(RB11MUX_zn));
  MUX31LP RB10MUX (.D0(F_15_0[11]), .D1(F_15_0[9]), .D2(F_15_0[10]), .A(ALUI7), .B(ALUI8N), .ZN(RB10MUX_zn));
  MUX31LP RB9MUX (.D0(F_15_0[10]), .D1(F_15_0[8]), .D2(F_15_0[9]), .A(ALUI7), .B(ALUI8N), .ZN(RB9MUX_zn));
  MUX31LP RB8MUX (.D0(F_15_0[9]), .D1(F_15_0[7]), .D2(F_15_0[8]), .A(ALUI7), .B(ALUI8N), .ZN(RB8MUX_zn));
  MUX31LP RB7MUX (.D0(F_15_0[8]), .D1(F_15_0[6]), .D2(F_15_0[7]), .A(ALUI7), .B(ALUI8N), .ZN(RB7MUX_zn));
  MUX31LP RB6MUX (.D0(F_15_0[7]), .D1(F_15_0[5]), .D2(F_15_0[6]), .A(ALUI7), .B(ALUI8N), .ZN(RB6MUX_zn));
  MUX31LP RB5MUX (.D0(F_15_0[6]), .D1(F_15_0[4]), .D2(F_15_0[5]), .A(ALUI7), .B(ALUI8N), .ZN(RB5MUX_zn));
  MUX31LP RB4MUX (.D0(F_15_0[5]), .D1(F_15_0[3]), .D2(F_15_0[4]), .A(ALUI7), .B(ALUI8N), .ZN(RB4MUX_zn));
  MUX31LP RB3MUX (.D0(F_15_0[4]), .D1(F_15_0[2]), .D2(F_15_0[3]), .A(ALUI7), .B(ALUI8N), .ZN(RB3MUX_zn));
  MUX31LP RB2MUX (.D0(F_15_0[3]), .D1(F_15_0[1]), .D2(F_15_0[2]), .A(ALUI7), .B(ALUI8N), .ZN(RB2MUX_zn));
  MUX31LP RB1MUX (.D0(F_15_0[2]), .D1(F_15_0[0]), .D2(F_15_0[1]), .A(ALUI7), .B(ALUI8N), .ZN(RB1MUX_zn));
  MUX31LP RB0MUX (.D0(F_15_0[1]), .D1(RLI), .D2(F_15_0[0]), .A(ALUI7), .B(ALUI8N), .ZN(RB0MUX_zn));
  not not_1 (RB_15_0[15], RB15MUX_zn);
  not not_2 (RB_15_0[14], RB14MUX_zn);
  not not_3 (RB_15_0[13], RB13MUX_zn);
  not not_4 (RB_15_0[12], RB12MUX_zn);
  not not_5 (RB_15_0[11], RB11MUX_zn);
  not not_6 (RB_15_0[10], RB10MUX_zn);
  not not_7 (RB_15_0[9], RB9MUX_zn);
  not not_8 (RB_15_0[8], RB8MUX_zn);
  not not_9 (RB_15_0[7], RB7MUX_zn);
  not not_10 (RB_15_0[6], RB6MUX_zn);
  not not_11 (RB_15_0[5], RB5MUX_zn);
  not not_12 (RB_15_0[4], RB4MUX_zn);
  not not_13 (RB_15_0[3], RB3MUX_zn);
  not not_14 (RB_15_0[2], RB2MUX_zn);
  not not_15 (RB_15_0[1], RB1MUX_zn);
  not not_16 (RB_15_0[0], RB0MUX_zn);

  // Other names for the same wires on the sheet: F0 = F_15_0[0]; F1 = F_15_0[1]; F2 = F_15_0[2]; F3 = F_15_0[3];
  //   F4 = F_15_0[4]; F5 = F_15_0[5]; F6 = F_15_0[6]; F7 = F_15_0[7]; F8 = F_15_0[8]; F9 = F_15_0[9];
  //   F10 = F_15_0[10]; F11 = F_15_0[11]; F12 = F_15_0[12]; F13 = F_15_0[13]; F14 = F_15_0[14]; F15 = F_15_0[15]

  // Notes on the sheet:
  //   Page 49 - CGA_ALU_SHIFT (tested in test-circuit, Ronny 09.06.2023)
endmodule

module CGA_ALU_GPR (
  input  [15:0] CD_15_0,
  input  [15:0] FIDBO_15_0,
  input  [2:0] GPRC_2_0,
  input  GPRLI,
  input  ALUCLK,
  output [15:0] GPR_15_0,
  output DGPR0N
);

  wire GPR0M_z, GPR1M_z, GPR2M_z, GPR3M_z, GPR4M_z, GPR5M_z, GPR6M_z, GPR7M_z, GPR8M_z, GPR9M_z, GPR10M_z,
       GPR11M_z, GPR12M_z, GPR13M_z, GPR14M_z, GPR15M_z;

  // Probe on GPR_15_0
  MUX41P GPR15M (
    .D0(FIDBO_15_0[15]), .D1(CD_15_0[15]), .D2(1'b0), .D3(GPR_15_0[14]), .A(GPRC_2_0[0]), .B(GPRC_2_0[1]),
    .Z(GPR15M_z));
  MUX41P GPR14M (
    .D0(FIDBO_15_0[14]), .D1(CD_15_0[14]), .D2(GPR_15_0[15]), .D3(GPR_15_0[13]), .A(GPRC_2_0[0]),
    .B(GPRC_2_0[1]), .Z(GPR14M_z));
  MUX41P GPR13M (
    .D0(FIDBO_15_0[13]), .D1(CD_15_0[13]), .D2(GPR_15_0[14]), .D3(GPR_15_0[12]), .A(GPRC_2_0[0]),
    .B(GPRC_2_0[1]), .Z(GPR13M_z));
  MUX41P GPR12M (
    .D0(FIDBO_15_0[12]), .D1(CD_15_0[12]), .D2(GPR_15_0[13]), .D3(GPR_15_0[11]), .A(GPRC_2_0[0]),
    .B(GPRC_2_0[1]), .Z(GPR12M_z));
  MUX41P GPR11M (
    .D0(FIDBO_15_0[11]), .D1(CD_15_0[11]), .D2(GPR_15_0[12]), .D3(GPR_15_0[10]), .A(GPRC_2_0[0]),
    .B(GPRC_2_0[1]), .Z(GPR11M_z));
  MUX41P GPR10M (
    .D0(FIDBO_15_0[10]), .D1(CD_15_0[10]), .D2(GPR_15_0[11]), .D3(GPR_15_0[9]), .A(GPRC_2_0[0]),
    .B(GPRC_2_0[1]), .Z(GPR10M_z));
  MUX41P GPR9M (
    .D0(FIDBO_15_0[9]), .D1(CD_15_0[9]), .D2(GPR_15_0[10]), .D3(GPR_15_0[8]), .A(GPRC_2_0[0]),
    .B(GPRC_2_0[1]), .Z(GPR9M_z));
  MUX41P GPR8M (
    .D0(FIDBO_15_0[8]), .D1(CD_15_0[8]), .D2(GPR_15_0[9]), .D3(GPR_15_0[7]), .A(GPRC_2_0[0]),
    .B(GPRC_2_0[1]), .Z(GPR8M_z));
  MUX41P GPR7M (
    .D0(FIDBO_15_0[7]), .D1(CD_15_0[7]), .D2(GPR_15_0[8]), .D3(GPR_15_0[6]), .A(GPRC_2_0[0]),
    .B(GPRC_2_0[1]), .Z(GPR7M_z));
  MUX41P GPR6M (
    .D0(FIDBO_15_0[6]), .D1(CD_15_0[6]), .D2(GPR_15_0[7]), .D3(GPR_15_0[5]), .A(GPRC_2_0[0]),
    .B(GPRC_2_0[1]), .Z(GPR6M_z));
  MUX41P GPR5M (
    .D0(FIDBO_15_0[5]), .D1(CD_15_0[5]), .D2(GPR_15_0[6]), .D3(GPR_15_0[4]), .A(GPRC_2_0[0]),
    .B(GPRC_2_0[1]), .Z(GPR5M_z));
  MUX41P GPR4M (
    .D0(FIDBO_15_0[4]), .D1(CD_15_0[4]), .D2(GPR_15_0[5]), .D3(GPR_15_0[3]), .A(GPRC_2_0[0]),
    .B(GPRC_2_0[1]), .Z(GPR4M_z));
  MUX41P GPR3M (
    .D0(FIDBO_15_0[3]), .D1(CD_15_0[3]), .D2(GPR_15_0[4]), .D3(GPR_15_0[2]), .A(GPRC_2_0[0]),
    .B(GPRC_2_0[1]), .Z(GPR3M_z));
  MUX41P GPR2M (
    .D0(FIDBO_15_0[2]), .D1(CD_15_0[2]), .D2(GPR_15_0[3]), .D3(GPR_15_0[1]), .A(GPRC_2_0[0]),
    .B(GPRC_2_0[1]), .Z(GPR2M_z));
  MUX41P GPR1M (
    .D0(FIDBO_15_0[1]), .D1(CD_15_0[1]), .D2(GPR_15_0[2]), .D3(GPR_15_0[0]), .A(GPRC_2_0[0]),
    .B(GPRC_2_0[1]), .Z(GPR1M_z));
  MUX41P GPR0M (
    .D0(FIDBO_15_0[0]), .D1(CD_15_0[0]), .D2(GPR_15_0[1]), .D3(GPRLI), .A(GPRC_2_0[0]), .B(GPRC_2_0[1]),
    .Z(GPR0M_z));
  SCAN_FF GPR15FF (.D(GPR15M_z), .TE(GPRC_2_0[2]), .TI(GPR_15_0[15]), .CLK(ALUCLK), .Q(GPR_15_0[15]));  // open: QN
  SCAN_FF GPR14FF (.D(GPR14M_z), .TE(GPRC_2_0[2]), .TI(GPR_15_0[14]), .CLK(ALUCLK), .Q(GPR_15_0[14]));  // open: QN
  SCAN_FF GPR13FF (.D(GPR13M_z), .TE(GPRC_2_0[2]), .TI(GPR_15_0[13]), .CLK(ALUCLK), .Q(GPR_15_0[13]));  // open: QN
  SCAN_FF GPR12FF (.D(GPR12M_z), .TE(GPRC_2_0[2]), .TI(GPR_15_0[12]), .CLK(ALUCLK), .Q(GPR_15_0[12]));  // open: QN
  SCAN_FF GPR11FF (.D(GPR11M_z), .TE(GPRC_2_0[2]), .TI(GPR_15_0[11]), .CLK(ALUCLK), .Q(GPR_15_0[11]));  // open: QN
  SCAN_FF GPR10FF (.D(GPR10M_z), .TE(GPRC_2_0[2]), .TI(GPR_15_0[10]), .CLK(ALUCLK), .Q(GPR_15_0[10]));  // open: QN
  SCAN_FF GPR9FF (.D(GPR9M_z), .TE(GPRC_2_0[2]), .TI(GPR_15_0[9]), .CLK(ALUCLK), .Q(GPR_15_0[9]));  // open: QN
  SCAN_FF GPR8FF (.D(GPR8M_z), .TE(GPRC_2_0[2]), .TI(GPR_15_0[8]), .CLK(ALUCLK), .Q(GPR_15_0[8]));  // open: QN
  SCAN_FF GPR7FF (.D(GPR7M_z), .TE(GPRC_2_0[2]), .TI(GPR_15_0[7]), .CLK(ALUCLK), .Q(GPR_15_0[7]));  // open: QN
  SCAN_FF GPR6FF (.D(GPR6M_z), .TE(GPRC_2_0[2]), .TI(GPR_15_0[6]), .CLK(ALUCLK), .Q(GPR_15_0[6]));  // open: QN
  SCAN_FF GPR5FF (.D(GPR5M_z), .TE(GPRC_2_0[2]), .TI(GPR_15_0[5]), .CLK(ALUCLK), .Q(GPR_15_0[5]));  // open: QN
  SCAN_FF GPR4FF (.D(GPR4M_z), .TE(GPRC_2_0[2]), .TI(GPR_15_0[4]), .CLK(ALUCLK), .Q(GPR_15_0[4]));  // open: QN
  SCAN_FF GPR3FF (.D(GPR3M_z), .TE(GPRC_2_0[2]), .TI(GPR_15_0[3]), .CLK(ALUCLK), .Q(GPR_15_0[3]));  // open: QN
  SCAN_FF GPR2FF (.D(GPR2M_z), .TE(GPRC_2_0[2]), .TI(GPR_15_0[2]), .CLK(ALUCLK), .Q(GPR_15_0[2]));  // open: QN
  SCAN_FF GPR1FF (.D(GPR1M_z), .TE(GPRC_2_0[2]), .TI(GPR_15_0[1]), .CLK(ALUCLK), .Q(GPR_15_0[1]));  // open: QN
  MUX21LP GPR0M21 (.A(GPR0M_z), .B(GPR_15_0[0]), .S(GPRC_2_0[2]), .ZN(DGPR0N));
  D_Flip_Flop d_ff_1 (.D(DGPR0N), .clk(ALUCLK), .Qn(GPR_15_0[0]));  // open: Q, preset, reset

  // Notes on the sheet:
  //   Page 50 - CGA_ALU_GPR (reviewed manually, Ronny 09.06.2023)
  //   GPRC = 000 = LOAD FIDB 15_0
  //   GPRC = 001 = LOAD CD 15_0
  //   GPRC = 011 =>  GPR SHIFT LEFT, GPRLI => GPR bit 0
  //   alu 876 = 10x  => GPRC = 010 shift right 
  //   alu 876 = 11x  => GPRC = 011 shift left
  //   alu 876 = 00x  => GPRC = 110 ?? no shift 
  //   alu 876 = 01x  => GPRC = 111 ?? no shift..  
  //   GPRC = 010 = FMU = MULTIPLY=> GPR SHIFT RIGHT
  //   GPRC0
  //   GPRC1
  //   GPR LEFT SHIFT INPUT BIT 0
  //   GPRC2
endmodule

module CGA_ALU_STS (
  input  LDPILN,
  input  ALUCLK,
  input  [15:0] FIDBO_15_0,
  input  MI,
  input  CRY,
  input  OVF,
  input  [1:0] CSTS_1_0,
  output [15:0] STS_15_0
);

  wire nand_1_out, nand_2_out, not_1_out, not_2_out, not_3_out, STS0_FF_qn, STS1_FF_qn, STS2_FF_qn,
       STS3_FF_qn, STS4_MUX_zn, STS5_MUX_zn, STS6_MUX_zn, STS7_MUX_z, STS8_FF_qn, STS9_FF_qn, STS10_FF_qn,
       STS11_FF_qn, STS12_FF_qn, STS13_FF_qn, STS14_FF_qn, STS15_FF_qn, STS_REG_MID_qan, STS_REG_MID_qb,
       STS_REG_MID_qc, STS_REG_MID_qd;

  not not_1 (not_1_out, OVF);
  nand nand_1 (nand_1_out, not_1_out, STS_REG_MID_qc);
  not not_2 (not_2_out, CSTS_1_0[1]);
  not not_3 (not_3_out, CSTS_1_0[0]);
  nand nand_2 (nand_2_out, CSTS_1_0[1], CSTS_1_0[0]);
  MUX41P STS7_MUX (
    .D0(FIDBO_15_0[7]), .D1(STS_15_0[7]), .D2(MI), .D3(STS_15_0[7]), .A(not_2_out), .B(not_3_out),
    .Z(STS7_MUX_z));
  MUX31LP STS6_MUX (.D0(FIDBO_15_0[6]), .D1(CRY), .D2(STS_15_0[6]), .A(not_2_out), .B(not_3_out), .ZN(STS6_MUX_zn));
  MUX31LP STS5_MUX (
    .D0(FIDBO_15_0[5]), .D1(nand_1_out), .D2(STS_15_0[5]), .A(not_2_out), .B(not_3_out), .ZN(STS5_MUX_zn));
  MUX31LP STS4_MUX (.D0(FIDBO_15_0[4]), .D1(OVF), .D2(STS_15_0[4]), .A(not_2_out), .B(not_3_out), .ZN(STS4_MUX_zn));
  R41P STS_REG_MID (
    .A(STS7_MUX_z), .B(STS6_MUX_zn), .C(STS5_MUX_zn), .D(STS4_MUX_zn), .CP(ALUCLK), .QAN(STS_REG_MID_qan),
    .QB(STS_REG_MID_qb), .QC(STS_REG_MID_qc), .QD(STS_REG_MID_qd));  // open: QA, QBN, QCN, QDN
  not not_4 (STS_15_0[7], STS_REG_MID_qan);
  not not_5 (STS_15_0[6], STS_REG_MID_qb);
  not not_6 (STS_15_0[5], STS_REG_MID_qc);
  not not_7 (STS_15_0[4], STS_REG_MID_qd);
  SCAN_FF STS15_FF (.D(FIDBO_15_0[15]), .TE(LDPILN), .TI(STS_15_0[15]), .CLK(ALUCLK), .QN(STS15_FF_qn));  // open: Q
  not not_8 (STS_15_0[15], STS15_FF_qn);
  SCAN_FF STS14_FF (.D(FIDBO_15_0[14]), .TE(LDPILN), .TI(STS_15_0[14]), .CLK(ALUCLK), .QN(STS14_FF_qn));  // open: Q
  not not_9 (STS_15_0[14], STS14_FF_qn);
  SCAN_FF STS13_FF (.D(FIDBO_15_0[13]), .TE(LDPILN), .TI(STS_15_0[13]), .CLK(ALUCLK), .QN(STS13_FF_qn));  // open: Q
  not not_10 (STS_15_0[13], STS13_FF_qn);
  SCAN_FF STS12_FF (.D(FIDBO_15_0[12]), .TE(LDPILN), .TI(STS_15_0[12]), .CLK(ALUCLK), .QN(STS12_FF_qn));  // open: Q
  not not_11 (STS_15_0[12], STS12_FF_qn);
  SCAN_FF STS11_FF (.D(FIDBO_15_0[11]), .TE(LDPILN), .TI(STS_15_0[11]), .CLK(ALUCLK), .QN(STS11_FF_qn));  // open: Q
  not not_12 (STS_15_0[11], STS11_FF_qn);
  SCAN_FF STS10_FF (.D(FIDBO_15_0[10]), .TE(LDPILN), .TI(STS_15_0[10]), .CLK(ALUCLK), .QN(STS10_FF_qn));  // open: Q
  not not_13 (STS_15_0[10], STS10_FF_qn);
  SCAN_FF STS9_FF (.D(FIDBO_15_0[9]), .TE(LDPILN), .TI(STS_15_0[9]), .CLK(ALUCLK), .QN(STS9_FF_qn));  // open: Q
  not not_14 (STS_15_0[9], STS9_FF_qn);
  SCAN_FF STS8_FF (.D(FIDBO_15_0[8]), .TE(LDPILN), .TI(STS_15_0[8]), .CLK(ALUCLK), .QN(STS8_FF_qn));  // open: Q
  not not_15 (STS_15_0[8], STS8_FF_qn);
  SCAN_FF STS3_FF (.D(FIDBO_15_0[3]), .TE(nand_2_out), .TI(STS_15_0[3]), .CLK(ALUCLK), .QN(STS3_FF_qn));  // open: Q
  not not_16 (STS_15_0[3], STS3_FF_qn);
  SCAN_FF STS2_FF (.D(FIDBO_15_0[2]), .TE(nand_2_out), .TI(STS_15_0[2]), .CLK(ALUCLK), .QN(STS2_FF_qn));  // open: Q
  not not_17 (STS_15_0[2], STS2_FF_qn);
  SCAN_FF STS1_FF (.D(FIDBO_15_0[1]), .TE(nand_2_out), .TI(STS_15_0[1]), .CLK(ALUCLK), .QN(STS1_FF_qn));  // open: Q
  not not_18 (STS_15_0[1], STS1_FF_qn);
  SCAN_FF STS0_FF (.D(FIDBO_15_0[0]), .TE(nand_2_out), .TI(STS_15_0[0]), .CLK(ALUCLK), .QN(STS0_FF_qn));  // open: Q
  not not_19 (STS_15_0[0], STS0_FF_qn);

  // Other names for the same wires on the sheet: FIDBO4 = FIDBO_15_0[4]; FIDBO5 = FIDBO_15_0[5];
  //   FIDBO6 = FIDBO_15_0[6]; FIDBO7 = FIDBO_15_0[7]; STS4 = STS_15_0[4]; STS5 = STS_15_0[5]; STS6 = STS_15_0[6];
  //   STS7 = STS_15_0[7]

  // Notes on the sheet:
  //   Page 51 - CGA_ALU_STS (reviewed manually, Ronny 09.06.2023)
  //   CSTS1
  //   CSTS0
endmodule

module CGA_ALU_DBR (
  input  ALUCLK,
  input  LDDBRN,
  input  [15:0] CD_15_0,
  output [15:0] DBR_15_0
);

  wire not_1_out;

  not not_1 (not_1_out, LDDBRN);
  SCAN_FF DBRF15 (.D(DBR_15_0[15]), .TE(not_1_out), .TI(CD_15_0[15]), .CLK(ALUCLK), .Q(DBR_15_0[15]));  // open: QN
  SCAN_FF DBRF14 (.D(DBR_15_0[14]), .TE(not_1_out), .TI(CD_15_0[14]), .CLK(ALUCLK), .Q(DBR_15_0[14]));  // open: QN
  SCAN_FF DBRf13 (.D(DBR_15_0[13]), .TE(not_1_out), .TI(CD_15_0[13]), .CLK(ALUCLK), .Q(DBR_15_0[13]));  // open: QN
  SCAN_FF DBRF12 (.D(DBR_15_0[12]), .TE(not_1_out), .TI(CD_15_0[12]), .CLK(ALUCLK), .Q(DBR_15_0[12]));  // open: QN
  SCAN_FF DBRF11 (.D(DBR_15_0[11]), .TE(not_1_out), .TI(CD_15_0[11]), .CLK(ALUCLK), .Q(DBR_15_0[11]));  // open: QN
  SCAN_FF DBRF10 (.D(DBR_15_0[10]), .TE(not_1_out), .TI(CD_15_0[10]), .CLK(ALUCLK), .Q(DBR_15_0[10]));  // open: QN
  SCAN_FF DBRF9 (.D(DBR_15_0[9]), .TE(not_1_out), .TI(CD_15_0[9]), .CLK(ALUCLK), .Q(DBR_15_0[9]));  // open: QN
  SCAN_FF DBRF8 (.D(DBR_15_0[8]), .TE(not_1_out), .TI(CD_15_0[8]), .CLK(ALUCLK), .Q(DBR_15_0[8]));  // open: QN
  SCAN_FF DBRF7 (.D(DBR_15_0[7]), .TE(not_1_out), .TI(CD_15_0[7]), .CLK(ALUCLK), .Q(DBR_15_0[7]));  // open: QN
  SCAN_FF DBRF6 (.D(DBR_15_0[6]), .TE(not_1_out), .TI(CD_15_0[6]), .CLK(ALUCLK), .Q(DBR_15_0[6]));  // open: QN
  SCAN_FF DBRF5 (.D(DBR_15_0[5]), .TE(not_1_out), .TI(CD_15_0[5]), .CLK(ALUCLK), .Q(DBR_15_0[5]));  // open: QN
  SCAN_FF DBRF4 (.D(DBR_15_0[4]), .TE(not_1_out), .TI(CD_15_0[4]), .CLK(ALUCLK), .Q(DBR_15_0[4]));  // open: QN
  SCAN_FF DBRF3 (.D(DBR_15_0[3]), .TE(not_1_out), .TI(CD_15_0[3]), .CLK(ALUCLK), .Q(DBR_15_0[3]));  // open: QN
  SCAN_FF DBRF2 (.D(DBR_15_0[2]), .TE(not_1_out), .TI(CD_15_0[2]), .CLK(ALUCLK), .Q(DBR_15_0[2]));  // open: QN
  SCAN_FF DBRF1 (.D(DBR_15_0[1]), .TE(not_1_out), .TI(CD_15_0[1]), .CLK(ALUCLK), .Q(DBR_15_0[1]));  // open: QN
  SCAN_FF DBRF0 (.D(DBR_15_0[0]), .TE(not_1_out), .TI(CD_15_0[0]), .CLK(ALUCLK), .Q(DBR_15_0[0]));  // open: QN

  // Notes on the sheet:
  //   Page 52 - CGA_ALU_DBR (tested manually, Ronny 09.06.2023)
endmodule

module CGA_ALU_ARG (
  input  [15:0] CSBIT_15_0,
  input  ALUCLK,
  output [15:0] ARG_15_0
);

  R81 ARG_HI_REG (
    .A(CSBIT_15_0[15]), .B(CSBIT_15_0[14]), .C(CSBIT_15_0[13]), .D(CSBIT_15_0[12]), .E(CSBIT_15_0[11]),
    .F(CSBIT_15_0[10]), .G(CSBIT_15_0[9]), .H(CSBIT_15_0[8]), .CP(ALUCLK), .QA(ARG_15_0[15]),
    .QB(ARG_15_0[14]), .QC(ARG_15_0[13]), .QD(ARG_15_0[12]), .QE(ARG_15_0[11]), .QF(ARG_15_0[10]),
    .QG(ARG_15_0[9]), .QH(ARG_15_0[8]));  // open: QAN, QBN, QCN, QDN, QEN, QFN, QGN, QHN
  R81 ARG_LO_REG (
    .A(CSBIT_15_0[7]), .B(CSBIT_15_0[6]), .C(CSBIT_15_0[5]), .D(CSBIT_15_0[4]), .E(CSBIT_15_0[3]),
    .F(CSBIT_15_0[2]), .G(CSBIT_15_0[1]), .H(CSBIT_15_0[0]), .CP(ALUCLK), .QA(ARG_15_0[7]), .QB(ARG_15_0[6]),
    .QC(ARG_15_0[5]), .QD(ARG_15_0[4]), .QE(ARG_15_0[3]), .QF(ARG_15_0[2]), .QG(ARG_15_0[1]), .QH(ARG_15_0[0]));  // open: QAN, QBN, QCN, QDN, QEN, QFN, QGN, QHN

  // Notes on the sheet:
  //   Page 53 - CGA_ALU_ARG (tested manually, Ronny 09.06.2023)
endmodule

module CGA_ALU_SWAP (
  input  [15:0] FIDBO_15_0,
  input  ALUCLK,
  output [15:0] SW_15_0
);

  R81 SWAP_LO_REG (
    .A(FIDBO_15_0[15]), .B(FIDBO_15_0[14]), .C(FIDBO_15_0[13]), .D(FIDBO_15_0[12]), .E(FIDBO_15_0[11]),
    .F(FIDBO_15_0[10]), .G(FIDBO_15_0[9]), .H(FIDBO_15_0[8]), .CP(ALUCLK), .QA(SW_15_0[7]), .QB(SW_15_0[6]),
    .QC(SW_15_0[5]), .QD(SW_15_0[4]), .QE(SW_15_0[3]), .QF(SW_15_0[2]), .QG(SW_15_0[1]), .QH(SW_15_0[0]));  // open: QAN, QBN, QCN, QDN, QEN, QFN, QGN, QHN
  R81 SWAP_HI_REG (
    .A(FIDBO_15_0[7]), .B(FIDBO_15_0[6]), .C(FIDBO_15_0[5]), .D(FIDBO_15_0[4]), .E(FIDBO_15_0[3]),
    .F(FIDBO_15_0[2]), .G(FIDBO_15_0[1]), .H(FIDBO_15_0[0]), .CP(ALUCLK), .QA(SW_15_0[15]), .QB(SW_15_0[14]),
    .QC(SW_15_0[13]), .QD(SW_15_0[12]), .QE(SW_15_0[11]), .QF(SW_15_0[10]), .QG(SW_15_0[9]), .QH(SW_15_0[8]));  // open: QAN, QBN, QCN, QDN, QEN, QFN, QGN, QHN

  // Notes on the sheet:
  //   Page 54 - CGA_ALU_SWAP (Tested manually, Ronny 08.06.2023)
  //   SW7
  //   6
  //   5
  //   4
  //   3
  //   2
  //   1
  //   SW0
  //   SW15
  //   6
  //   5
  //   4
  //   3
  //   2
  //   1
  //   SW8
endmodule

module CGA_ALU_OUTMUX (
  input  [15:0] EA_15_0,
  input  [15:0] DBR_15_0,
  input  [15:0] ARG_15_0,
  input  [15:0] STS_15_0,
  input  [15:0] SW_15_0,
  input  [15:0] FIDBI_15_0,
  input  [15:0] GPR_15_0,
  input  [2:0] LBA_2_0,
  input  [2:0] LAA_3_1,
  input  AARG0,
  input  [15:0] F_15_0,
  input  [15:0] A_15_0,
  input  ALUCLK,
  input  ALUD2N,
  input  [4:0] CSIDBS_4_0,
  output [15:0] G_15_0,
  output [15:0] D_15_0
);

  wire EA, EAARG, EABARG, EARG, EBARG, EBMG, EDBR, EF, EFIDB, EGPRH, EGPRL, EGPRS, ESTS, ESWAP;

  CGA_ALU_OUTMUX_SEL8 DMUX15 (
    .SI_7_0({GPR_15_0[7], GPR_15_0[15], FIDBI_15_0[15], SW_15_0[15], STS_15_0[15], ARG_15_0[15], DBR_15_0[15], EA_15_0[15]}),
    .E_7_0({EGPRS, EGPRH, EFIDB, ESWAP, ESTS, EARG, EDBR, EBMG}), .D(D_15_0[15]));
  CGA_ALU_OUTMUX_SEL8 DMUX14 (
    .SI_7_0({GPR_15_0[7], GPR_15_0[14], FIDBI_15_0[14], SW_15_0[14], STS_15_0[14], ARG_15_0[14], DBR_15_0[14], EA_15_0[14]}),
    .E_7_0({EGPRS, EGPRH, EFIDB, ESWAP, ESTS, EARG, EDBR, EBMG}), .D(D_15_0[14]));
  CGA_ALU_OUTMUX_SEL8 DMUX13 (
    .SI_7_0({GPR_15_0[7], GPR_15_0[13], FIDBI_15_0[13], SW_15_0[13], STS_15_0[13], ARG_15_0[13], DBR_15_0[13], EA_15_0[13]}),
    .E_7_0({EGPRS, EGPRH, EFIDB, ESWAP, ESTS, EARG, EDBR, EBMG}), .D(D_15_0[13]));
  CGA_ALU_OUTMUX_SEL8 DMUX12 (
    .SI_7_0({GPR_15_0[7], GPR_15_0[12], FIDBI_15_0[12], SW_15_0[12], STS_15_0[12], ARG_15_0[12], DBR_15_0[12], EA_15_0[12]}),
    .E_7_0({EGPRS, EGPRH, EFIDB, ESWAP, ESTS, EARG, EDBR, EBMG}), .D(D_15_0[12]));
  CGA_ALU_OUTMUX_SEL8 DMUX11 (
    .SI_7_0({GPR_15_0[7], GPR_15_0[11], FIDBI_15_0[11], SW_15_0[11], STS_15_0[11], ARG_15_0[11], DBR_15_0[11], EA_15_0[11]}),
    .E_7_0({EGPRS, EGPRH, EFIDB, ESWAP, ESTS, EARG, EDBR, EBMG}), .D(D_15_0[11]));
  CGA_ALU_OUTMUX_SEL8 DMUX10 (
    .SI_7_0({GPR_15_0[7], GPR_15_0[10], FIDBI_15_0[10], SW_15_0[10], STS_15_0[10], ARG_15_0[10], DBR_15_0[10], EA_15_0[10]}),
    .E_7_0({EGPRS, EGPRH, EFIDB, ESWAP, ESTS, EARG, EDBR, EBMG}), .D(D_15_0[10]));
  CGA_ALU_OUTMUX_SEL8 DMUX9 (
    .SI_7_0({GPR_15_0[7], GPR_15_0[9], FIDBI_15_0[9], SW_15_0[9], STS_15_0[9], ARG_15_0[9], DBR_15_0[9], EA_15_0[9]}),
    .E_7_0({EGPRS, EGPRH, EFIDB, ESWAP, ESTS, EARG, EDBR, EBMG}), .D(D_15_0[9]));
  CGA_ALU_OUTMUX_SEL8 DMUX8 (
    .SI_7_0({GPR_15_0[7], GPR_15_0[8], FIDBI_15_0[8], SW_15_0[8], STS_15_0[8], ARG_15_0[8], DBR_15_0[8], EA_15_0[8]}),
    .E_7_0({EGPRS, EGPRH, EFIDB, ESWAP, ESTS, EARG, EDBR, EBMG}), .D(D_15_0[8]));
  CGA_CPU_ALU_OUTMUX_SEL7 DMUX7 (
    .SI_6_0({GPR_15_0[7], FIDBI_15_0[7], SW_15_0[7], STS_15_0[7], ARG_15_0[7], DBR_15_0[7], EA_15_0[7]}),
    .E_6_0({EGPRL, EFIDB, ESWAP, ESTS, EARG, EDBR, EBMG}), .D(D_15_0[7]));
  CGA_ALU_OUTMUX_SEL8 DMUX6 (
    .SI_7_0({LAA_3_1[2], GPR_15_0[6], FIDBI_15_0[6], SW_15_0[6], STS_15_0[6], ARG_15_0[6], DBR_15_0[6], EA_15_0[6]}),
    .E_7_0({EAARG, EGPRL, EFIDB, ESWAP, ESTS, EARG, EDBR, EBMG}), .D(D_15_0[6]));
  CGA_ALU_OUTMUX_SEL8 DMUX5 (
    .SI_7_0({LAA_3_1[1], GPR_15_0[5], FIDBI_15_0[5], SW_15_0[5], STS_15_0[5], ARG_15_0[5], DBR_15_0[5], EA_15_0[5]}),
    .E_7_0({EAARG, EGPRL, EFIDB, ESWAP, ESTS, EARG, EDBR, EBMG}), .D(D_15_0[5]));
  CGA_ALU_OUTMUX_SEL8 DMUX4 (
    .SI_7_0({LAA_3_1[0], GPR_15_0[4], FIDBI_15_0[4], SW_15_0[4], STS_15_0[4], ARG_15_0[4], DBR_15_0[4], EA_15_0[4]}),
    .E_7_0({EAARG, EGPRL, EFIDB, ESWAP, ESTS, EARG, EDBR, EBMG}), .D(D_15_0[4]));
  CGA_ALU_OUTMUX_SEL8 DMUX3 (
    .SI_7_0({AARG0, GPR_15_0[3], FIDBI_15_0[3], SW_15_0[3], STS_15_0[3], ARG_15_0[3], DBR_15_0[3], EA_15_0[3]}),
    .E_7_0({EABARG, EGPRL, EFIDB, ESWAP, ESTS, EARG, EDBR, EBMG}), .D(D_15_0[3]));
  CGA_ALU_OUTMUX_SEL8 DMUX2 (
    .SI_7_0({LBA_2_0[2], GPR_15_0[2], FIDBI_15_0[2], SW_15_0[2], STS_15_0[2], ARG_15_0[2], DBR_15_0[2], EA_15_0[2]}),
    .E_7_0({EBARG, EGPRL, EFIDB, ESWAP, ESTS, EARG, EDBR, EBMG}), .D(D_15_0[2]));
  CGA_ALU_OUTMUX_SEL8 DMUX1 (
    .SI_7_0({LBA_2_0[1], GPR_15_0[1], FIDBI_15_0[1], SW_15_0[1], STS_15_0[1], ARG_15_0[1], DBR_15_0[1], EA_15_0[1]}),
    .E_7_0({EBARG, EGPRL, EFIDB, ESWAP, ESTS, EARG, EDBR, EBMG}), .D(D_15_0[1]));
  CGA_ALU_OUTMUX_SEL8 DMUX0 (
    .SI_7_0({LBA_2_0[0], GPR_15_0[0], FIDBI_15_0[0], SW_15_0[0], STS_15_0[0], ARG_15_0[0], DBR_15_0[0], EA_15_0[0]}),
    .E_7_0({EBARG, EGPRL, EFIDB, ESWAP, ESTS, EARG, EDBR, EBMG}), .D(D_15_0[0]));
  CGA_ALU_OUTMUX_IDBS OUTMUX_IDBS (
    .ALUCLK(ALUCLK), .ALUD2N(ALUD2N), .CSIDBS_4_0(CSIDBS_4_0), .EBMG(EBMG), .EGPRH(EGPRH), .EDBR(EDBR),
    .EARG(EARG), .ESTS(ESTS), .EBARG(EBARG), .ESWAP(ESWAP), .EAARG(EAARG), .EABARG(EABARG), .EFIDB(EFIDB),
    .EGPRL(EGPRL), .EGPRS(EGPRS), .EA(EA), .EF(EF));
  MUX31LP GMUX15 (.D0(D_15_0[15]), .D1(A_15_0[15]), .D2(F_15_0[15]), .A(EA), .B(EF), .ZN(G_15_0[15]));
  MUX31LP GMUX14 (.D0(D_15_0[14]), .D1(A_15_0[14]), .D2(F_15_0[14]), .A(EA), .B(EF), .ZN(G_15_0[14]));
  MUX31LP GMUX13 (.D0(D_15_0[13]), .D1(A_15_0[13]), .D2(F_15_0[13]), .A(EA), .B(EF), .ZN(G_15_0[13]));
  MUX31LP GMUX12 (.D0(D_15_0[12]), .D1(A_15_0[12]), .D2(F_15_0[12]), .A(EA), .B(EF), .ZN(G_15_0[12]));
  MUX31LP GMUX11 (.D0(D_15_0[11]), .D1(A_15_0[11]), .D2(F_15_0[11]), .A(EA), .B(EF), .ZN(G_15_0[11]));
  MUX31LP GMUX10 (.D0(D_15_0[10]), .D1(A_15_0[10]), .D2(F_15_0[10]), .A(EA), .B(EF), .ZN(G_15_0[10]));
  MUX31LP GMUX9 (.D0(D_15_0[9]), .D1(A_15_0[9]), .D2(F_15_0[9]), .A(EA), .B(EF), .ZN(G_15_0[9]));
  MUX31LP GMUX8 (.D0(D_15_0[8]), .D1(A_15_0[8]), .D2(F_15_0[8]), .A(EA), .B(EF), .ZN(G_15_0[8]));
  MUX31LP GMUX7 (.D0(D_15_0[7]), .D1(A_15_0[7]), .D2(F_15_0[7]), .A(EA), .B(EF), .ZN(G_15_0[7]));
  MUX31LP GMUX6 (.D0(D_15_0[6]), .D1(A_15_0[6]), .D2(F_15_0[6]), .A(EA), .B(EF), .ZN(G_15_0[6]));
  MUX31LP GMUX5 (.D0(D_15_0[5]), .D1(A_15_0[5]), .D2(F_15_0[5]), .A(EA), .B(EF), .ZN(G_15_0[5]));
  MUX31LP GMUX4 (.D0(D_15_0[4]), .D1(A_15_0[4]), .D2(F_15_0[4]), .A(EA), .B(EF), .ZN(G_15_0[4]));
  MUX31LP GMUX3 (.D0(D_15_0[3]), .D1(A_15_0[3]), .D2(F_15_0[3]), .A(EA), .B(EF), .ZN(G_15_0[3]));
  MUX31LP GMUX2 (.D0(D_15_0[2]), .D1(A_15_0[2]), .D2(F_15_0[2]), .A(EA), .B(EF), .ZN(G_15_0[2]));
  MUX31LP GMUX1 (.D0(D_15_0[1]), .D1(A_15_0[1]), .D2(F_15_0[1]), .A(EA), .B(EF), .ZN(G_15_0[1]));
  MUX31LP GMUX0 (.D0(D_15_0[0]), .D1(A_15_0[0]), .D2(F_15_0[0]), .A(EA), .B(EF), .ZN(G_15_0[0]));

  // Other names for the same wires on the sheet: EA3 = EA_15_0[3]; DBR3 = DBR_15_0[3]; ARG3 = ARG_15_0[3];
  //   STS3 = STS_15_0[3]; SW3 = SW_15_0[3]; FIDBI3 = FIDBI_15_0[3]; GPR3 = GPR_15_0[3]; EA2 = EA_15_0[2];
  //   DBR2 = DBR_15_0[2]; ARG2 = ARG_15_0[2]; STS2 = STS_15_0[2]; SW2 = SW_15_0[2]; FIDBI2 = FIDBI_15_0[2];
  //   GPR2 = GPR_15_0[2]; LBA2 = LBA_2_0[2]; EA1 = EA_15_0[1]; DBR1 = DBR_15_0[1]; ARG1 = ARG_15_0[1];
  //   STS1 = STS_15_0[1]; SW1 = SW_15_0[1]; FIDBI1 = FIDBI_15_0[1]; GPR1 = GPR_15_0[1]; LBA1 = LBA_2_0[1];
  //   EA0 = EA_15_0[0]; DBR0 = DBR_15_0[0]; ARG0 = ARG_15_0[0]; STS0 = STS_15_0[0]; SW0 = SW_15_0[0];
  //   FIDBI0 = FIDBI_15_0[0]; GPR0 = GPR_15_0[0]; LBA0 = LBA_2_0[0]; EA7 = EA_15_0[7]; DBR7 = DBR_15_0[7];
  //   ARG7 = ARG_15_0[7]; STS7 = STS_15_0[7]; SW7 = SW_15_0[7]; FIDBI7 = FIDBI_15_0[7]; GPR7 = GPR_15_0[7];
  //   EA6 = EA_15_0[6]; DBR6 = DBR_15_0[6]; ARG6 = ARG_15_0[6]; STS6 = STS_15_0[6]; SW6 = SW_15_0[6];
  //   FIDBI6 = FIDBI_15_0[6]; GPR6 = GPR_15_0[6]; LAA3 = LAA_3_1[2]; EA5 = EA_15_0[5]; DBR5 = DBR_15_0[5];
  //   ARG5 = ARG_15_0[5]; STS5 = STS_15_0[5]; SW5 = SW_15_0[5]; FIDBI5 = FIDBI_15_0[5]; GPR5 = GPR_15_0[5];
  //   LAA2 = LAA_3_1[1]; EA4 = EA_15_0[4]; DBR4 = DBR_15_0[4]; ARG4 = ARG_15_0[4]; STS4 = STS_15_0[4];
  //   SW4 = SW_15_0[4]; FIDBI4 = FIDBI_15_0[4]; GPR4 = GPR_15_0[4]; LAA1 = LAA_3_1[0]; EA14 = EA_15_0[14];
  //   DBR14 = DBR_15_0[14]; ARG14 = ARG_15_0[14]; STS14 = STS_15_0[14]; SW14 = SW_15_0[14]; FIDBI14 = FIDBI_15_0[14];
  //   GPR14 = GPR_15_0[14]; EA13 = EA_15_0[13]; DBR13 = DBR_15_0[13]; ARG13 = ARG_15_0[13]; STS13 = STS_15_0[13];
  //   SW13 = SW_15_0[13]; FIDBI13 = FIDBI_15_0[13]; GPR13 = GPR_15_0[13]; EA12 = EA_15_0[12]; DBR12 = DBR_15_0[12];
  //   ARG12 = ARG_15_0[12]; STS12 = STS_15_0[12]; SW12 = SW_15_0[12]; FIDBI12 = FIDBI_15_0[12]; GPR12 = GPR_15_0[12];
  //   EA11 = EA_15_0[11]; DBR11 = DBR_15_0[11]; ARG11 = ARG_15_0[11]; STS11 = STS_15_0[11]; SW11 = SW_15_0[11];
  //   FIDBI11 = FIDBI_15_0[11]; GPR11 = GPR_15_0[11]; EA10 = EA_15_0[10]; DBR10 = DBR_15_0[10]; ARG10 = ARG_15_0[10];
  //   STS10 = STS_15_0[10]; SW10 = SW_15_0[10]; FIDBI10 = FIDBI_15_0[10]; GPR10 = GPR_15_0[10]; EA9 = EA_15_0[9];
  //   DBR9 = DBR_15_0[9]; ARG9 = ARG_15_0[9]; STS9 = STS_15_0[9]; SW9 = SW_15_0[9]; FIDBI9 = FIDBI_15_0[9];
  //   GPR9 = GPR_15_0[9]; EA8 = EA_15_0[8]; DBR8 = DBR_15_0[8]; ARG8 = ARG_15_0[8]; STS8 = STS_15_0[8];
  //   SW8 = SW_15_0[8]; FIDBI8 = FIDBI_15_0[8]; GPR8 = GPR_15_0[8]; EA15 = EA_15_0[15]; DBR15 = DBR_15_0[15];
  //   ARG15 = ARG_15_0[15]; STS15 = STS_15_0[15]; SW15 = SW_15_0[15]; FIDBI15 = FIDBI_15_0[15]; GPR15 = GPR_15_0[15];
  //   A0 = A_15_0[0]; A1 = A_15_0[1]; A2 = A_15_0[2]; A3 = A_15_0[3]; A4 = A_15_0[4]; A5 = A_15_0[5]; A6 = A_15_0[6];
  //   A7 = A_15_0[7]; A8 = A_15_0[8]; A9 = A_15_0[9]; A10 = A_15_0[10]; A11 = A_15_0[11]; A12 = A_15_0[12];
  //   A13 = A_15_0[13]; A14 = A_15_0[14]; A15 = A_15_0[15]; D0 = D_15_0[0]; D1 = D_15_0[1]; D2 = D_15_0[2];
  //   D3 = D_15_0[3]; D4 = D_15_0[4]; D5 = D_15_0[5]; D6 = D_15_0[6]; D7 = D_15_0[7]; D8 = D_15_0[8]; D9 = D_15_0[9];
  //   D10 = D_15_0[10]; D11 = D_15_0[11]; D12 = D_15_0[12]; D13 = D_15_0[13]; D14 = D_15_0[14]; D15 = D_15_0[15];
  //   F0 = F_15_0[0]; F1 = F_15_0[1]; F2 = F_15_0[2]; F3 = F_15_0[3]; F4 = F_15_0[4]; F5 = F_15_0[5]; F6 = F_15_0[6];
  //   F7 = F_15_0[7]; F8 = F_15_0[8]; F9 = F_15_0[9]; F10 = F_15_0[10]; F11 = F_15_0[11]; F12 = F_15_0[12];
  //   F13 = F_15_0[13]; F14 = F_15_0[14]; F15 = F_15_0[15]; G0 = G_15_0[0]; G1 = G_15_0[1]; G2 = G_15_0[2];
  //   G3 = G_15_0[3]; G4 = G_15_0[4]; G5 = G_15_0[5]; G6 = G_15_0[6]; G7 = G_15_0[7]; G8 = G_15_0[8]; G9 = G_15_0[9];
  //   G10 = G_15_0[10]; G11 = G_15_0[11]; G12 = G_15_0[12]; G13 = G_15_0[13]; G14 = G_15_0[14]; G15 = G_15_0[15]

  // Notes on the sheet:
  //   Page 55 - CGA_ALU_OUTMUX (reviewed manually, Ronny 09.06.2023)
  //   EGPRS, BIT 7 is unclear
  //   Guessing its "sign extended bit 7"
  //   It looks like bit 7 for MUX 7-15 should be GPR7
endmodule

module CGA_ALU_OUTMUX_SEL8 (
  input  [7:0] SI_7_0,
  input  [7:0] E_7_0,
  output D
);

  wire nand_1_out, nand_2_out, nand_3_out, nand_4_out, nand_5_out, nand_6_out, nand_7_out, nand_8_out;

  nand nand_1 (nand_1_out, SI_7_0[7], E_7_0[7]);
  nand nand_2 (nand_2_out, SI_7_0[6], E_7_0[6]);
  nand nand_3 (nand_3_out, SI_7_0[5], E_7_0[5]);
  nand nand_4 (nand_4_out, SI_7_0[4], E_7_0[4]);
  nand nand_5 (nand_5_out, SI_7_0[3], E_7_0[3]);
  nand nand_6 (nand_6_out, SI_7_0[2], E_7_0[2]);
  nand nand_7 (nand_7_out, SI_7_0[1], E_7_0[1]);
  nand nand_8 (nand_8_out, SI_7_0[0], E_7_0[0]);
  nand nand_9 (D, nand_1_out, nand_2_out, nand_3_out, nand_4_out, nand_5_out, nand_6_out, nand_7_out, nand_8_out);

  // Notes on the sheet:
  //   Page 56 - CGA_ALU_OUTMUX_SEL8 (Tested manually, Ronny 08.06.2023)
endmodule

module CGA_CPU_ALU_OUTMUX_SEL7 (
  input  [6:0] SI_6_0,
  input  [6:0] E_6_0,
  output D
);

  wire nand_1_out, nand_2_out, nand_3_out, nand_4_out, nand_5_out, nand_6_out, nand_7_out;

  nand nand_1 (nand_1_out, SI_6_0[0], E_6_0[0]);
  nand nand_2 (nand_2_out, SI_6_0[1], E_6_0[1]);
  nand nand_3 (nand_3_out, SI_6_0[2], E_6_0[2]);
  nand nand_4 (nand_4_out, SI_6_0[3], E_6_0[3]);
  nand nand_5 (nand_5_out, SI_6_0[4], E_6_0[4]);
  nand nand_6 (nand_6_out, SI_6_0[5], E_6_0[5]);
  nand nand_7 (nand_7_out, SI_6_0[6], E_6_0[6]);
  or or_1 (D, ~nand_1_out, ~nand_2_out, ~nand_3_out, ~nand_4_out, ~nand_5_out, ~nand_6_out, ~nand_7_out);  // OR_Gate

  // Notes on the sheet:
  //   Page 57 - CGA_ALU_OUTMUX_SEL7 (Tested manually, Ronny 08.06.2023)
endmodule

module CGA_ALU_OUTMUX_IDBS (
  input  ALUCLK,
  input  ALUD2N,
  input  [4:0] CSIDBS_4_0,
  output EBMG,
  output EGPRH,
  output EDBR,
  output EARG,
  output ESTS,
  output EBARG,
  output ESWAP,
  output EAARG,
  output EABARG,
  output EFIDB,
  output EGPRL,
  output EGPRS,
  output EA,
  output EF
);

  wire and_1_out, and_2_out, IDBS_G1_z0, IDBS_G1_z1, IDBS_G1_z2, IDBS_G1_z3, IDBS_G1_z4, IDBS_G1_z6,
       IDBS_G2_z0, IDBS_G2_z1, IDBS_G2_z4, IDBS_R1_qan, IDBS_R1_qb, IDBS_R1_qd, IDBS_R1_qe, IDBS_R1_qf,
       IDBS_R1_qh, IDBS_R2_qa, IDBS_R2_qc, nand_1_out, nand_2_out, nand_3_out, nand_4_out, nand_5_out,
       nand_6_out, not_1_out, not_2_out, not_3_out, not_4_out, not_5_out, not_6_out, not_7_out;

  not not_1 (not_1_out, CSIDBS_4_0[4]);
  and and_1 (and_1_out, not_1_out, CSIDBS_4_0[3]);
  not not_2 (not_2_out, CSIDBS_4_0[3]);
  not not_3 (not_3_out, CSIDBS_4_0[2]);
  not not_4 (not_4_out, CSIDBS_4_0[0]);
  not not_5 (not_5_out, CSIDBS_4_0[3]);
  nand nand_1 (nand_1_out, CSIDBS_4_0[4], not_2_out, not_3_out, CSIDBS_4_0[1], not_4_out);
  and and_2 (and_2_out, not_5_out, not_1_out);
  ND38GLP IDBS_G2 (
    .A(CSIDBS_4_0[0]), .B(CSIDBS_4_0[1]), .C(CSIDBS_4_0[2]), .G(and_1_out), .Z0(IDBS_G2_z0), .Z1(IDBS_G2_z1),
    .Z4(IDBS_G2_z4));  // open: Z2, Z3, Z5, Z6, Z7
  ND38GLP IDBS_G1 (
    .A(CSIDBS_4_0[0]), .B(CSIDBS_4_0[1]), .C(CSIDBS_4_0[2]), .G(and_2_out), .Z0(IDBS_G1_z0), .Z1(IDBS_G1_z1),
    .Z2(IDBS_G1_z2), .Z3(IDBS_G1_z3), .Z4(IDBS_G1_z4), .Z6(IDBS_G1_z6));  // open: Z5, Z7
  nand nand_2 (nand_2_out, IDBS_G2_z0, IDBS_G2_z4);
  not not_6 (not_6_out, nand_2_out);
  nand nand_3 (nand_3_out, IDBS_G1_z2, nand_1_out);
  nand nand_4 (nand_4_out, IDBS_G1_z1, IDBS_G1_z2, IDBS_G1_z3, IDBS_G1_z4, IDBS_G1_z6, IDBS_G2_z1, not_6_out, nand_1_out);
  R81P IDBS_R1 (
    .A(IDBS_G1_z0), .B(IDBS_G1_z1), .C(IDBS_G1_z2), .D(IDBS_G1_z3), .E(IDBS_G1_z4), .F(IDBS_G1_z6),
    .G(IDBS_G2_z0), .H(IDBS_G2_z1), .CP(ALUCLK), .QAN(IDBS_R1_qan), .QB(IDBS_R1_qb), .QCN(EGPRH),
    .QD(IDBS_R1_qd), .QE(IDBS_R1_qe), .QF(IDBS_R1_qf), .QGN(EBARG), .QH(IDBS_R1_qh));  // open: QA, QBN, QC, QDN, QEN, QFN, QG, QHN
  R81P IDBS_R2 (
    .A(IDBS_G2_z4), .B(nand_2_out), .C(nand_4_out), .D(nand_3_out), .E(nand_1_out), .CP(ALUCLK),
    .QA(IDBS_R2_qa), .QB(EABARG), .QC(IDBS_R2_qc), .QD(EGPRL), .QEN(EGPRS));  // open: F, G, H, QAN, QBN, QCN, QDN, QE, QF, QFN, QG, QGN, QH, QHN
  not not_7 (not_7_out, ALUD2N);
  not not_8 (EBMG, IDBS_R1_qb);
  not not_9 (EDBR, IDBS_R1_qd);
  not not_10 (EARG, IDBS_R1_qe);
  not not_11 (ESTS, IDBS_R1_qf);
  not not_12 (ESWAP, IDBS_R1_qh);
  not not_13 (EAARG, IDBS_R2_qa);
  not not_14 (EFIDB, IDBS_R2_qc);
  nand nand_5 (nand_5_out, not_7_out, IDBS_R1_qan);
  not not_15 (EA, nand_5_out);
  nand nand_6 (nand_6_out, ALUD2N, IDBS_R1_qan);
  not not_16 (EF, nand_6_out);

  // Other names for the same wires on the sheet: CSIDBS0 = CSIDBS_4_0[0]; CSIDBS1 = CSIDBS_4_0[1];
  //   CSIDBS2 = CSIDBS_4_0[2]; CSIDBS3 = CSIDBS_4_0[3]; CSIDBS4 = CSIDBS_4_0[4]

  // Notes on the sheet:
  //   Page 58 - CGA_ALU_OUTMUX_IDBS (Tested manually, Ronny 08.06.2023)
endmodule

module ALU_test (
  input  [15:0] A_15_0,
  input  [15:0] B_15_0,
  input  [15:0] EA_15_0,
  input  [15:0] FIDBI_15_0,
  input  [15:0] in_5,
  input  [4:0] in_6,
  input  [3:0] in_7,
  input  [3:0] in_8,
  input  in_9,
  input  in_10,
  input  in_11,
  input  in_12,
  input  [1:0] in_13,
  input  [1:0] in_14,
  input  [1:0] in_15,
  input  in_16,
  input  in_17,
  input  in_18,
  input  [2:0] in_19,
  input  [1:0] in_20,
  input  [2:0] in_21,
  input  in_22,
  input  [2:0] in_23,
  input  [15:0] in_24,
  input  in_25,
  input  in_26,
  input  in_27,
  input  in_28,
  input  [15:0] in_29,
  input  [15:0] in_30,
  input  [15:0] in_31,
  input  [15:0] in_32,
  input  [15:0] in_33,
  input  [2:0] in_34,
  input  [2:0] in_35,
  input  in_36,
  input  [4:0] in_37,
  output F11,
  output F15
);

  wire Alu_under_test_bdest, Alu_under_test_cry, Alu_under_test_double, Alu_under_test_f11,
       Alu_under_test_f15, Alu_under_test_ioni, Alu_under_test_mi, Alu_under_test_ovf, Alu_under_test_poni,
       Alu_under_test_ptm, Alu_under_test_sgr, Alu_under_test_z, Alu_under_test_zf,
       cga_cpu_alu_contr_1_alud2n, cga_cpu_alu_contr_1_alui4, cga_cpu_alu_contr_1_alui7,
       cga_cpu_alu_contr_1_alui8n, cga_cpu_alu_contr_1_bdest, cga_cpu_alu_contr_1_ci,
       cga_cpu_alu_contr_1_fsel, cga_cpu_alu_contr_1_gprli, cga_cpu_alu_contr_1_log, cga_cpu_alu_contr_1_qli,
       cga_cpu_alu_contr_1_rli, cga_cpu_alu_contr_1_rri, cga_cpu_alu_contr_1_rsn, cga_cpu_alu_ralu_1_cry,
       cga_cpu_alu_ralu_1_ovf, cga_cpu_alu_ralu_1_sgr, cga_cpu_alu_ralu_1_zf, F0, RA, RD, SA, SB;
  wire [1:0] cga_cpu_alu_contr_1_qsel_1_0;
  wire [2:0] cga_cpu_alu_contr_1_gprc_2_0;
  wire [3:0] Alu_under_test_pil_3_0;
  wire [14:1] F_15_0;
  wire [15:0] ALU_QREG_q_15_0, Alu_under_test_fidbo_15_0, Alu_under_test_rb_15_0, cga_alu_outmux_1_g_15_0,
       D_15_0, G_15_0, RB_15_0, RN_15_0, S_15_0;

  // Probe on FIDBI_15_0
  // Probe on A_15_0
  // Probe on {F15, F_15_0[14:12], F11, F_15_0[10:1], F0}
  // Probe on B_15_0
  // Probe on {in_23, in_21, in_19}
  // Probe on EA_15_0
  // Probe on A_15_0
  assign G_15_0 = ~cga_alu_outmux_1_g_15_0;  // NOT_Gate not_1, 16 bits wide
  CGA_ALU_OUTMUX cga_alu_outmux_1 (
    .EA_15_0(EA_15_0), .DBR_15_0(in_33), .ARG_15_0(in_32), .STS_15_0(in_31), .SW_15_0(in_30),
    .FIDBI_15_0(FIDBI_15_0), .GPR_15_0(in_29), .LBA_2_0(in_34), .LAA_3_1(in_35), .AARG0(in_36),
    .F_15_0({F15, F_15_0[14:12], F11, F_15_0[10:1], F0}), .A_15_0(A_15_0), .ALUCLK(in_22),
    .ALUD2N(cga_cpu_alu_contr_1_alud2n), .CSIDBS_4_0(in_37), .G_15_0(cga_alu_outmux_1_g_15_0), .D_15_0(D_15_0));
  // Probe on G_15_0
  // Probe on D_15_0
  CGA_ALU Alu_under_test (
    .A_15_0(A_15_0), .B_15_0(B_15_0), .CSBIT_15_0(in_5), .EA_15_0(EA_15_0), .FIDBI_15_0(FIDBI_15_0),
    .CSIDBS_4_0(in_6), .LBA_3_0(in_7), .LAA_3_0(in_8), .LDPILN(in_9), .LDDBRN(in_10), .XFETCHN(in_11),
    .LDGPRN(in_12), .CSMIS_1_0(in_13), .CSSST_1_0(in_14), .CSCINSEL_1_0(in_15), .LDIRV(in_16), .UPN(in_17),
    .LCZN(in_18), .CSALUI_8_0({in_23, in_21, in_19}), .CSALUM_1_0(in_20), .ALUCLK(in_22), .CD_15_0(in_24),
    .ZF(Alu_under_test_zf), .CRY(Alu_under_test_cry), .SGR(Alu_under_test_sgr), .OVF(Alu_under_test_ovf),
    .RB_15_0(Alu_under_test_rb_15_0), .F11(Alu_under_test_f11), .F15(Alu_under_test_f15),
    .BDEST(Alu_under_test_bdest), .MI(Alu_under_test_mi), .PTM(Alu_under_test_ptm), .Z(Alu_under_test_z),
    .PIL_3_0(Alu_under_test_pil_3_0), .DOUBLE(Alu_under_test_double), .PONI(Alu_under_test_poni),
    .IONI(Alu_under_test_ioni), .FIDBO_15_0(Alu_under_test_fidbo_15_0));
  CGA_CPU_ALU_CONTR cga_cpu_alu_contr_1 (
    .STS7(in_25), .CRY(in_26), .Q0(in_27), .CSMIS_1_0(in_13), .CSSST_1_0(in_14), .CSCINSEL_1_0(in_15),
    .ALUCLK(in_22), .CSALUI_8_0({in_23, in_21, in_19}), .CSALUM_1_0(in_20), .F15(in_28),
    .ALUD2N(cga_cpu_alu_contr_1_alud2n), .QSEL_1_0(cga_cpu_alu_contr_1_qsel_1_0),
    .GPRLI(cga_cpu_alu_contr_1_gprli), .RRI(cga_cpu_alu_contr_1_rri), .QLI(cga_cpu_alu_contr_1_qli),
    .RLI(cga_cpu_alu_contr_1_rli), .GPRC_2_0(cga_cpu_alu_contr_1_gprc_2_0),
    .ALUI8N(cga_cpu_alu_contr_1_alui8n), .CI(cga_cpu_alu_contr_1_ci), .BDEST(cga_cpu_alu_contr_1_bdest),
    .ALUI7(cga_cpu_alu_contr_1_alui7), .RSN(cga_cpu_alu_contr_1_rsn), .FSEL(cga_cpu_alu_contr_1_fsel),
    .LOG(cga_cpu_alu_contr_1_log), .ALUI4(cga_cpu_alu_contr_1_alui4), .SB(SB), .SA(SA), .RA(RA), .RD(RD));  // open: F0, Q15, XFETCHN, LDGPRN, CD_10_9, LDIRV, UPN, STS6, GPR0, LCZN, DGPR0N, CSTS_1_0, MI
  // Probe on Alu_under_test_zf
  // Probe on Alu_under_test_cry
  // Probe on Alu_under_test_sgr
  // Probe on Alu_under_test_ovf
  // Probe on Alu_under_test_f11
  // Probe on Alu_under_test_f15
  // Probe on Alu_under_test_bdest
  // Probe on Alu_under_test_mi
  // Probe on Alu_under_test_ptm
  // Probe on Alu_under_test_z
  // Probe on Alu_under_test_pil_3_0
  // Probe on Alu_under_test_double
  // Probe on Alu_under_test_poni
  // Probe on Alu_under_test_ioni
  // Probe on Alu_under_test_rb_15_0
  // Probe on Alu_under_test_fidbo_15_0
  // Probe on cga_cpu_alu_contr_1_qsel_1_0
  // Probe on cga_cpu_alu_contr_1_gprli
  // Probe on cga_cpu_alu_contr_1_rri
  // Probe on cga_cpu_alu_contr_1_rli
  // Probe on cga_cpu_alu_contr_1_gprc_2_0
  // Probe on cga_cpu_alu_contr_1_bdest
  // Probe on cga_cpu_alu_contr_1_alui7
  // Probe on {F15, F_15_0[14:12], F11, F_15_0[10:1], F0}
  // Probe on cga_cpu_alu_contr_1_alui7
  // Probe on RN_15_0
  CGA_ALU_QREG ALU_QREG (
    .F_15_0({F15, F_15_0[14:12], F11, F_15_0[10:1], F0}), .QLI(cga_cpu_alu_contr_1_qli),
    .QSEL_1_0(cga_cpu_alu_contr_1_qsel_1_0), .ALUCLK(in_22), .Q_15_0(ALU_QREG_q_15_0));
  // Probe on S_15_0
  // Probe on ALU_QREG_q_15_0
  // Probe on B_15_0
  // Probe on cga_cpu_alu_ralu_1_zf
  CGA_CPU_ALU_RALU cga_cpu_alu_ralu_1 (
    .CI(cga_cpu_alu_contr_1_ci), .LOG(cga_cpu_alu_contr_1_log), .ALUI4(cga_cpu_alu_contr_1_alui4),
    .FSEL(cga_cpu_alu_contr_1_fsel), .RSN(cga_cpu_alu_contr_1_rsn), .RN_15_0(RN_15_0), .S_15_0(S_15_0),
    .ZF(cga_cpu_alu_ralu_1_zf), .F_15_0({F15, F_15_0[14:12], F11, F_15_0[10:1], F0}),
    .CRY(cga_cpu_alu_ralu_1_cry), .SGR(cga_cpu_alu_ralu_1_sgr), .OVF(cga_cpu_alu_ralu_1_ovf));
  // Probe on cga_cpu_alu_ralu_1_cry
  // Probe on cga_cpu_alu_ralu_1_sgr
  // Probe on cga_cpu_alu_ralu_1_ovf
  // Probe on A_15_0
  // Probe on D_15_0
  // Probe on {F15, F_15_0[14:12], F11, F_15_0[10:1], F0}
  // Probe on RB_15_0
  CGA_ALU_SHIFT ALU_SHIFT (
    .RRI(cga_cpu_alu_contr_1_rri), .F_15_0({F15, F_15_0[14:12], F11, F_15_0[10:1], F0}),
    .RLI(cga_cpu_alu_contr_1_rli), .ALUI7(cga_cpu_alu_contr_1_alui7), .ALUI8N(cga_cpu_alu_contr_1_alui8n),
    .RB_15_0(RB_15_0));
  CGA_CPU_ALU_RMUX ALU_RMUX (.D_15_0(D_15_0), .A_15_0(A_15_0), .RD(RD), .RA(RA), .RN_15_0(RN_15_0));
  CGA_ALU_SMUX ALU_SMUX (.A_15_0(A_15_0), .B_15_0(B_15_0), .Q_15_0(ALU_QREG_q_15_0), .SA(SA), .SB(SB), .S_15_0(S_15_0));
  // Probe on RN_15_0
  // Probe on S_15_0

  // Other names for the same wires on the sheet: F_15_0 (some bits) = {F15, F11, F0}

  // Notes on the sheet:
  //   ALU Source
  //   ALU Function
  //   ALU Destination
  //   bitmap gen?
  //   internal bus (IDB?)
  //   i8=> 1=DO Shift (not logical operation. Also shift GPR register)
  //   ALUI7=0, Right shift. 1=LEFT shift
  //   Selection if input has been validated by ronny 04.12.2023
endmodule

module test_RALU (
  input  [2:0] in_1,
  input  in_2,
  input  in_3,
  input  in_4,
  input  [4:0] in_5,
  input  in_6,
  input  in_7,
  input  [2:0] in_8,
  input  [2:0] in_9,
  input  [15:0] in_10,
  input  [2:0] in_11,
  input  [15:0] in_12,
  output SB,
  output SA,
  output RA,
  output RD
);

  wire ALUCLK, ALUI1N, cga_alu_outmux_idbs_1_ea, cga_alu_outmux_idbs_1_eaarg, cga_alu_outmux_idbs_1_eabarg,
       cga_alu_outmux_idbs_1_earg, cga_alu_outmux_idbs_1_ebarg, cga_alu_outmux_idbs_1_ebmg,
       cga_alu_outmux_idbs_1_edbr, cga_alu_outmux_idbs_1_ef, cga_alu_outmux_idbs_1_efidb,
       cga_alu_outmux_idbs_1_egprh, cga_alu_outmux_idbs_1_egprl, cga_alu_outmux_idbs_1_egprs,
       cga_alu_outmux_idbs_1_ests, cga_alu_outmux_idbs_1_eswap, cga_cpu_alu_contr_1_alui4,
       cga_cpu_alu_contr_1_alui8n, cga_cpu_alu_contr_1_ci, cga_cpu_alu_contr_1_fsel, cga_cpu_alu_contr_1_log,
       cga_cpu_alu_contr_1_mi, cga_cpu_alu_contr_1_ra, cga_cpu_alu_contr_1_rd, cga_cpu_alu_contr_1_rsn,
       cga_cpu_alu_contr_1_sa, cga_cpu_alu_contr_1_sb, cga_cpu_alu_ralu_1_cry, cga_cpu_alu_ralu_1_ovf,
       cga_cpu_alu_ralu_1_sgr, cga_cpu_alu_ralu_1_zf, nand_1_out, nand_2_out, nand_3_out, nand_4_out,
       nand_5_out, nand_6_out, nand_7_out, nand_8_out, not_2_out, not_3_out, REG_BAAD_qan, REG_BAAD_qbn,
       REG_BAAD_qc, REG_BAAD_qd;
  wire [15:0] cga_cpu_alu_ralu_1_f_15_0, not_8_out;

  not not_1 (ALUI1N, in_1[1]);
  not not_2 (not_2_out, in_1[2]);
  not not_3 (not_3_out, in_1[0]);
  nand nand_1 (nand_1_out, in_1[2], in_1[0]);
  nand nand_2 (nand_2_out, in_1[2], ALUI1N);
  nand nand_3 (nand_3_out, not_2_out, in_1[0]);
  nand nand_4 (nand_4_out, ALUI1N, not_2_out);
  nand nand_5 (nand_5_out, ALUI1N, not_3_out);
  nand nand_6 (nand_6_out, nand_1_out, nand_2_out);
  nand nand_7 (nand_7_out, nand_2_out, nand_3_out);
  nand nand_8 (nand_8_out, nand_5_out, in_1[2]);
  R41P REG_BAAD (
    .A(nand_6_out), .B(nand_7_out), .C(nand_4_out), .D(nand_8_out), .CP(ALUCLK), .QAN(REG_BAAD_qan),
    .QBN(REG_BAAD_qbn), .QC(REG_BAAD_qc), .QD(REG_BAAD_qd));  // open: QA, QB, QCN, QDN
  CGA_CPU_ALU_CONTR cga_cpu_alu_contr_1 (
    .CRY(in_6), .ALUCLK(in_7), .CSALUI_8_0({in_11, in_9, in_8}), .ALUI8N(cga_cpu_alu_contr_1_alui8n),
    .CI(cga_cpu_alu_contr_1_ci), .MI(cga_cpu_alu_contr_1_mi), .RSN(cga_cpu_alu_contr_1_rsn),
    .FSEL(cga_cpu_alu_contr_1_fsel), .LOG(cga_cpu_alu_contr_1_log), .ALUI4(cga_cpu_alu_contr_1_alui4),
    .SB(cga_cpu_alu_contr_1_sb), .SA(cga_cpu_alu_contr_1_sa), .RA(cga_cpu_alu_contr_1_ra),
    .RD(cga_cpu_alu_contr_1_rd));  // open: STS7, F0, Q0, Q15, XFETCHN, LDGPRN, CSMIS_1_0, CD_10_9, CSSST_1_0, CSCINSEL_1_0, LDIRV, UPN, STS6, GPR0, LCZN, CSALUM_1_0, DGPR0N, F15, ALUD2N, QSEL_1_0, GPRLI, RRI, QLI, RLI, GPRC_2_0, BDEST, CSTS_1_0, ALUI7
  not not_4 (SB, REG_BAAD_qan);
  not not_5 (SA, REG_BAAD_qbn);
  not not_6 (RA, REG_BAAD_qc);
  not not_7 (RD, REG_BAAD_qd);
  // Probe on cga_cpu_alu_contr_1_alui8n
  // Probe on cga_cpu_alu_contr_1_mi
  // Probe on cga_cpu_alu_contr_1_rsn
  // Probe on cga_cpu_alu_contr_1_fsel
  // Probe on cga_cpu_alu_contr_1_log
  // Probe on cga_cpu_alu_contr_1_alui4
  // Probe on cga_cpu_alu_contr_1_sb
  // Probe on cga_cpu_alu_contr_1_sa
  // Probe on cga_cpu_alu_contr_1_ra
  // Probe on cga_cpu_alu_contr_1_rd
  assign not_8_out = ~in_10;  // NOT_Gate not_8, 16 bits wide
  CGA_CPU_ALU_RALU cga_cpu_alu_ralu_1 (
    .CI(cga_cpu_alu_contr_1_ci), .LOG(cga_cpu_alu_contr_1_log), .ALUI4(cga_cpu_alu_contr_1_alui4),
    .FSEL(cga_cpu_alu_contr_1_fsel), .RSN(cga_cpu_alu_contr_1_rsn), .RN_15_0(not_8_out), .S_15_0(in_12),
    .ZF(cga_cpu_alu_ralu_1_zf), .F_15_0(cga_cpu_alu_ralu_1_f_15_0), .CRY(cga_cpu_alu_ralu_1_cry),
    .SGR(cga_cpu_alu_ralu_1_sgr), .OVF(cga_cpu_alu_ralu_1_ovf));
  // Probe on cga_cpu_alu_ralu_1_zf
  // Probe on cga_cpu_alu_ralu_1_cry
  // Probe on cga_cpu_alu_ralu_1_sgr
  // Probe on cga_cpu_alu_ralu_1_ovf
  // Probe on cga_cpu_alu_ralu_1_f_15_0
  // Probe on cga_alu_outmux_idbs_1_ebmg
  CGA_ALU_OUTMUX_IDBS cga_alu_outmux_idbs_1 (
    .ALUCLK(in_3), .ALUD2N(in_4), .CSIDBS_4_0(in_5), .EBMG(cga_alu_outmux_idbs_1_ebmg),
    .EGPRH(cga_alu_outmux_idbs_1_egprh), .EDBR(cga_alu_outmux_idbs_1_edbr),
    .EARG(cga_alu_outmux_idbs_1_earg), .ESTS(cga_alu_outmux_idbs_1_ests),
    .EBARG(cga_alu_outmux_idbs_1_ebarg), .ESWAP(cga_alu_outmux_idbs_1_eswap),
    .EAARG(cga_alu_outmux_idbs_1_eaarg), .EABARG(cga_alu_outmux_idbs_1_eabarg),
    .EFIDB(cga_alu_outmux_idbs_1_efidb), .EGPRL(cga_alu_outmux_idbs_1_egprl),
    .EGPRS(cga_alu_outmux_idbs_1_egprs), .EA(cga_alu_outmux_idbs_1_ea), .EF(cga_alu_outmux_idbs_1_ef));
  // Probe on cga_alu_outmux_idbs_1_egprh
  // Probe on cga_alu_outmux_idbs_1_edbr
  // Probe on cga_alu_outmux_idbs_1_earg
  // Probe on cga_alu_outmux_idbs_1_ests
  // Probe on cga_alu_outmux_idbs_1_ebarg
  // Probe on cga_alu_outmux_idbs_1_eswap
  // Probe on cga_alu_outmux_idbs_1_eaarg
  // Probe on cga_alu_outmux_idbs_1_eabarg
  // Probe on cga_alu_outmux_idbs_1_efidb
  // Probe on cga_alu_outmux_idbs_1_egprl
  // Probe on cga_alu_outmux_idbs_1_egprs
  // Probe on cga_alu_outmux_idbs_1_ea
  // Probe on cga_alu_outmux_idbs_1_ef

  // Other names for the same wires on the sheet: CSALUI0 = in_1[0]; CSALUI2 = in_1[2]
endmodule
module CGA_DCD (
  input  [4:0] CSCOMM_4_0,
  input  [1:0] CSMIS_1_0,
  input  MCLK,
  input  ILCSN,
  input  F15,
  input  ZF,
  input  CRY,
  input  SGR,
  input  WPN,
  input  PONI,
  input  VEX,
  input  BRKN,
  input  FIDBO5,
  input  MRN,
  input  LSHADOW,
  input  INTRQN,
  input  [4:0] CSIDBS_4_0,
  output INDN,
  output XFETCHN,
  output CBRKN,
  output DSTOPN,
  output LDLCN,
  output LDPILN,
  output LDIRV,
  output CSMREQ,
  output LDDBRN,
  output FETCHN,
  output WRITEN,
  output CLFFN,
  output EPIC,
  output LWCAN,
  output LDGPRN,
  output WRTRF,
  output CFETCH,
  output VACCN,
  output CLIRQN,
  output EPGSN,
  output EPCRN,
  output EPICVN,
  output EPICSN,
  output ERFN
);

  wire and_1_out, C22_z0, C22_z1, C22_z3, C22_z4, C22_z5, C22_z6, C22_z7, C24_z0, C24_z1, C24_z2, C24_z3,
       C24_z4, C24_z5, C24_z6, C24_z7, CFETCH_FF_q, COMM_MIS_REG_qa, COMM_MIS_REG_qan, COMM_MIS_REG_qb,
       COMM_MIS_REG_qbn, COMM_MIS_REG_qc, COMM_MIS_REG_qcn, COMM_MIS_REG_qe, COMM_MIS_REG_qen,
       COMM_MIS_REG_qf, COMM_MIS_REG_qfn, COMM_MIS_REG_qg, COMM_MIS_REG_qgn, d_ff_5_q, d_ff_7_q, d_ff_7_qn,
       d_ff_8_q, d_ff_10_qn, d_ff_11_q, d_ff_16_qn, d_ff_17_q, FD25_q, LCSN, MREQ, nand_1_out, nand_2_out,
       nand_3_out, nand_5_out, nand_6_out, nand_7_out, nand_8_out, nand_9_out, nand_10_out, nand_11_out,
       nand_12_out, nand_13_out, nand_14_out, nand_16_out, nand_18_out, nand_19_out, nand_20_out,
       nand_21_out, nand_22_out, nand_23_out, nand_24_out, nand_25_out, nand_26_out, nand_27_out,
       nand_28_out, nand_29_out, nand_30_out, nand_31_out, nand_32_out, nand_33_out, nand_34_out,
       nand_35_out, nand_36_out, nand_37_out, nand_38_out, nand_39_out, nand_40_out, nand_41_out,
       nand_42_out, nand_43_out, nand_44_out, nand_45_out, nand_46_out, nand_47_out, nand_48_out,
       nand_49_out, nand_50_out, nand_51_out, nand_52_out, nand_53_out, nand_54_out, nand_55_out,
       nand_56_out, nand_57_out, nand_58_out, nand_59_out, nand_60_out, nand_61_out, nand_62_out,
       nand_63_out, nand_64_out, nor_1_out, not_1_out, not_2_out, not_3_out, not_4_out, not_5_out, not_7_out,
       not_8_out, not_9_out, not_10_out, not_11_out, not_51_out, not_55_out, not_57_out, not_58_out,
       not_59_out, or_1_out, or_2_out, or_3_out, or_4_out, or_5_out, or_6_out, or_7_out, or_8_out, or_9_out,
       or_10_out, or_12_out, or_13_out, SIOCN, WRTRFN;
  wire [1:0] ICSMIS_1_0, ICSMIS_1_0_N, MIS_1_0, MIS_1_0_N;
  wire [4:0] COMM_4_0, COMM_4_0_N, ICSCOMM_4_0, ICSCOMM_4_0_N, ICSIDBS_4_0, ICSIDBS_4_0_N;

  not not_1 (not_1_out, F15);
  not not_2 (not_2_out, ZF);
  not not_3 (not_3_out, CRY);
  not not_4 (not_4_out, WPN);
  not not_5 (not_5_out, ILCSN);
  not not_6 (LCSN, not_5_out);
  not not_7 (not_7_out, not_1_out);
  not not_8 (not_8_out, not_2_out);
  not not_9 (not_9_out, not_3_out);
  not not_10 (not_10_out, SGR);
  not not_11 (not_11_out, not_4_out);
  not not_12 (ICSIDBS_4_0_N[0], CSIDBS_4_0[0]);
  not not_13 (ICSIDBS_4_0_N[1], CSIDBS_4_0[1]);
  not not_14 (ICSIDBS_4_0_N[2], CSIDBS_4_0[2]);
  not not_15 (ICSIDBS_4_0_N[3], CSIDBS_4_0[3]);
  not not_16 (ICSIDBS_4_0_N[4], CSIDBS_4_0[4]);
  nand nand_1 (nand_1_out, CSCOMM_4_0[4], LCSN);
  nand nand_2 (nand_2_out, COMM_4_0[4], COMM_4_0_N[3], COMM_4_0[2]);
  nand nand_3 (nand_3_out, LCSN, ICSIDBS_4_0[4], ICSIDBS_4_0_N[3], ICSIDBS_4_0_N[2], ICSIDBS_4_0[1], ICSIDBS_4_0[0]);
  nand nand_4 (LDLCN, COMM_4_0_N[4], COMM_4_0[3], COMM_4_0[2], COMM_4_0[1], COMM_4_0[0], LCSN);
  not not_17 (ICSIDBS_4_0[0], ICSIDBS_4_0_N[0]);
  not not_18 (ICSIDBS_4_0[1], ICSIDBS_4_0_N[1]);
  not not_19 (ICSIDBS_4_0[2], ICSIDBS_4_0_N[2]);
  not not_20 (ICSIDBS_4_0[3], ICSIDBS_4_0_N[3]);
  not not_21 (ICSIDBS_4_0[4], ICSIDBS_4_0_N[4]);
  D_Flip_Flop d_ff_1 (.D(nand_3_out), .clk(MCLK), .Q(EPGSN));  // open: Qn, preset, reset
  nand nand_5 (nand_5_out, COMM_4_0[4], COMM_4_0_N[3], COMM_4_0_N[2], COMM_4_0[1], COMM_4_0_N[0], MIS_1_0[1], MIS_1_0[0], not_11_out);
  nand nand_6 (nand_6_out, COMM_4_0[4], COMM_4_0_N[3], COMM_4_0_N[0], MIS_1_0[1], MIS_1_0[0], LCSN);
  nand nand_7 (nand_7_out, COMM_4_0[4], COMM_4_0_N[3], COMM_4_0_N[2], COMM_4_0[1], COMM_4_0[0], MIS_1_0_N[1], MIS_1_0_N[0], not_7_out);
  or or_1 (or_1_out, ~nand_2_out, ~nand_5_out, ~nand_7_out, ~nand_10_out, ~nand_12_out, ~nand_14_out);  // OR_Gate
  nand nand_8 (nand_8_out, COMM_4_0[4], COMM_4_0_N[3], COMM_4_0[1], MIS_1_0[1], LCSN);
  nor nor_1 (nor_1_out, ~nand_6_out, ~nand_8_out, ~nand_11_out, ~nand_13_out);  // NOR_Gate
  nand nand_9 (nand_9_out, LCSN, ICSIDBS_4_0[4], ICSIDBS_4_0_N[3], ICSIDBS_4_0[2], ICSIDBS_4_0_N[1], ICSIDBS_4_0[0]);
  R81P COMM_MIS_REG (
    .A(CSCOMM_4_0[0]), .B(CSCOMM_4_0[1]), .C(CSCOMM_4_0[2]), .D(CSCOMM_4_0[3]), .E(nand_1_out),
    .F(CSMIS_1_0[0]), .G(CSMIS_1_0[1]), .CP(MCLK), .QA(COMM_MIS_REG_qa), .QAN(COMM_MIS_REG_qan),
    .QB(COMM_MIS_REG_qb), .QBN(COMM_MIS_REG_qbn), .QC(COMM_MIS_REG_qc), .QCN(COMM_MIS_REG_qcn),
    .QD(COMM_4_0[3]), .QE(COMM_MIS_REG_qe), .QEN(COMM_MIS_REG_qen), .QF(COMM_MIS_REG_qf),
    .QFN(COMM_MIS_REG_qfn), .QG(COMM_MIS_REG_qg), .QGN(COMM_MIS_REG_qgn));  // open: H, QDN, QH, QHN
  nand nand_10 (nand_10_out, COMM_4_0[4], COMM_4_0_N[3], COMM_4_0_N[2], COMM_4_0[1], COMM_4_0[0], MIS_1_0_N[1], MIS_1_0[0], not_1_out);
  nand nand_11 (nand_11_out, COMM_4_0[4], COMM_4_0_N[3], COMM_4_0[1], COMM_4_0[0], LCSN);
  D_Flip_Flop d_ff_2 (.D(nand_9_out), .clk(MCLK), .Q(EPCRN));  // open: Qn, preset, reset
  nand nand_12 (nand_12_out, COMM_4_0[4], COMM_4_0_N[3], COMM_4_0_N[2], COMM_4_0[1], COMM_4_0[0], MIS_1_0[1], not_8_out, MIS_1_0_N[0]);
  not not_22 (XFETCHN, or_1_out);
  nand nand_13 (nand_13_out, COMM_4_0[4], COMM_4_0_N[3], COMM_4_0[2], LCSN);
  nor nor_2 (LDIRV, nor_1_out, MCLK);
  not not_23 (COMM_4_0_N[0], COMM_MIS_REG_qa);
  not not_24 (COMM_4_0[0], COMM_MIS_REG_qan);
  not not_25 (COMM_4_0_N[1], COMM_MIS_REG_qb);
  not not_26 (COMM_4_0[1], COMM_MIS_REG_qbn);
  not not_27 (COMM_4_0_N[2], COMM_MIS_REG_qc);
  not not_28 (COMM_4_0[2], COMM_MIS_REG_qcn);
  not not_29 (COMM_4_0_N[3], COMM_4_0[3]);
  not not_30 (COMM_4_0[4], COMM_MIS_REG_qe);
  not not_31 (COMM_4_0_N[4], COMM_MIS_REG_qen);
  not not_32 (MIS_1_0_N[0], COMM_MIS_REG_qf);
  not not_33 (MIS_1_0[0], COMM_MIS_REG_qfn);
  not not_34 (MIS_1_0_N[1], COMM_MIS_REG_qg);
  not not_35 (MIS_1_0[1], COMM_MIS_REG_qgn);
  nand nand_14 (nand_14_out, COMM_4_0[4], COMM_4_0_N[3], COMM_4_0_N[2], COMM_4_0[1], COMM_4_0[0], MIS_1_0[1], MIS_1_0[0], not_2_out);
  nand nand_15 (LDPILN, COMM_4_0_N[4], COMM_4_0_N[3], COMM_4_0_N[2], COMM_4_0_N[1], COMM_4_0[0], LCSN);
  nand nand_16 (nand_16_out, LCSN, ICSIDBS_4_0[4], ICSIDBS_4_0[3], ICSIDBS_4_0_N[2], ICSIDBS_4_0_N[1], ICSIDBS_4_0[0]);
  D_Flip_Flop d_ff_3 (.D(nand_16_out), .clk(MCLK), .Q(EPICVN));  // open: Qn, preset, reset
  nand nand_17 (SIOCN, COMM_4_0_N[4], COMM_4_0_N[3], COMM_4_0[2], COMM_4_0[1], COMM_4_0[0], LCSN);
  nand nand_18 (nand_18_out, COMM_4_0[1], COMM_4_0_N[2], COMM_4_0_N[3], COMM_4_0[4]);
  nand nand_19 (nand_19_out, COMM_4_0[4], COMM_4_0[3], COMM_4_0_N[2], COMM_4_0_N[1], LCSN);
  nand nand_20 (nand_20_out, LCSN, ICSIDBS_4_0_N[4], ICSIDBS_4_0[3], ICSIDBS_4_0[2], ICSIDBS_4_0_N[1], ICSIDBS_4_0[0]);
  D_Flip_Flop d_ff_4 (.D(nand_20_out), .clk(MCLK), .Q(EPICSN));  // open: Qn, preset, reset
  ND38GHP C22 (
    .A(MIS_1_0[0]), .B(MIS_1_0[1]), .C(COMM_4_0[0]), .G(nand_18_out), .Z0(C22_z0), .Z1(C22_z1), .Z3(C22_z3),
    .Z4(C22_z4), .Z5(C22_z5), .Z6(C22_z6), .Z7(C22_z7));  // open: Z2
  nand nand_21 (nand_21_out, COMM_4_0[4], COMM_4_0[3], COMM_4_0_N[1], COMM_4_0_N[0], LCSN);
  nor nor_3 (INDN, C22_z0, C22_z1);
  nand nand_22 (nand_22_out, COMM_4_0[4], COMM_4_0[2], COMM_4_0[1], COMM_4_0[0], MIS_1_0[1], LCSN);
  and and_1 (and_1_out, not_4_out, C22_z3);
  nand nand_23 (nand_23_out, COMM_4_0[4], COMM_4_0_N[3], COMM_4_0[1], COMM_4_0[0], LCSN);
  or or_2 (or_2_out, ~nand_19_out, ~nand_21_out, ~nand_22_out, ~nand_23_out, ~nand_25_out, ~nand_28_out, ~nand_31_out);  // OR_Gate
  not not_36 (ICSCOMM_4_0_N[4], CSCOMM_4_0[4]);
  not not_37 (ICSCOMM_4_0_N[3], CSCOMM_4_0[3]);
  not not_38 (ICSCOMM_4_0_N[2], CSCOMM_4_0[2]);
  not not_39 (ICSCOMM_4_0_N[1], CSCOMM_4_0[1]);
  not not_40 (ICSCOMM_4_0_N[0], CSCOMM_4_0[0]);
  not not_41 (ICSMIS_1_0_N[1], CSMIS_1_0[1]);
  not not_42 (ICSMIS_1_0_N[0], CSMIS_1_0[0]);
  nand nand_24 (nand_24_out, not_1_out, C22_z4);
  nand nand_25 (nand_25_out, COMM_4_0[4], COMM_4_0_N[3], COMM_4_0[2]);
  D_Flip_Flop d_ff_5 (.D(or_2_out), .clk(MCLK), .Q(d_ff_5_q));  // open: Qn, preset, reset
  nand nand_26 (nand_26_out, LCSN, ICSIDBS_4_0_N[4], ICSIDBS_4_0_N[3], ICSIDBS_4_0[2], ICSIDBS_4_0_N[1], ICSIDBS_4_0[0]);
  not not_43 (ICSMIS_1_0[1], ICSMIS_1_0_N[1]);
  not not_44 (ICSMIS_1_0[0], ICSMIS_1_0_N[0]);
  nand nand_27 (nand_27_out, not_7_out, C22_z5);
  nand nand_28 (nand_28_out, COMM_4_0[4], COMM_4_0_N[3], COMM_4_0[1], MIS_1_0_N[1]);
  not not_45 (LDDBRN, d_ff_5_q);
  not not_46 (ICSCOMM_4_0[4], ICSCOMM_4_0_N[4]);
  not not_47 (ICSCOMM_4_0[3], ICSCOMM_4_0_N[3]);
  not not_48 (ICSCOMM_4_0[2], ICSCOMM_4_0_N[2]);
  not not_49 (ICSCOMM_4_0[1], ICSCOMM_4_0_N[1]);
  not not_50 (ICSCOMM_4_0[0], ICSCOMM_4_0_N[0]);
  nand nand_29 (nand_29_out, not_2_out, C22_z6);
  D_Flip_Flop d_ff_6 (.D(or_3_out), .clk(MCLK), .Qn(ERFN));  // open: Q, preset, reset
  or or_3 (or_3_out, ~nand_26_out, ~WRTRFN);  // OR_Gate
  nand nand_30 (nand_30_out, not_8_out, C22_z7);
  nand nand_31 (nand_31_out, COMM_4_0[4], COMM_4_0_N[3], COMM_4_0[1], MIS_1_0[0]);
  or or_4 (or_4_out, ~nand_24_out, ~nand_27_out, ~nand_29_out, ~nand_30_out);  // OR_Gate
  nand nand_32 (nand_32_out, LCSN, COMM_4_0[4], COMM_4_0_N[3], COMM_4_0[1], MIS_1_0[1], MIS_1_0[0]);
  nand nand_33 (nand_33_out, LCSN, COMM_4_0[4], COMM_4_0_N[3], COMM_4_0[1], COMM_4_0[0]);
  or or_5 (or_5_out, ~nand_32_out, ~nand_33_out, ~nand_34_out);  // OR_Gate
  nand nand_34 (nand_34_out, LCSN, COMM_4_0[4], COMM_4_0_N[3], COMM_4_0[2]);
  D_Flip_Flop d_ff_7 (.D(or_5_out), .clk(MCLK), .Q(d_ff_7_q), .Qn(d_ff_7_qn));  // open: preset, reset
  not not_51 (not_51_out, BRKN);
  not not_52 (FETCHN, d_ff_7_q);
  nand nand_35 (nand_35_out, COMM_4_0_N[1], COMM_4_0[2], COMM_4_0_N[3], COMM_4_0[4]);
  SCAN_FF CFETCH_FF (.D(CFETCH_FF_q), .TE(not_51_out), .TI(d_ff_7_qn), .CLK(MCLK), .Q(CFETCH_FF_q), .QN(CFETCH));
  ND38GHP C24 (
    .A(MIS_1_0[0]), .B(MIS_1_0[1]), .C(COMM_4_0[0]), .G(nand_35_out), .Z0(C24_z0), .Z1(C24_z1), .Z2(C24_z2),
    .Z3(C24_z3), .Z4(C24_z4), .Z5(C24_z5), .Z6(C24_z6), .Z7(C24_z7));
  nand nand_36 (nand_36_out, not_10_out, C24_z0);
  nand nand_37 (nand_37_out, SGR, C24_z1);
  nand nand_38 (nand_38_out, not_3_out, C24_z2);
  nand nand_39 (nand_39_out, not_9_out, C24_z3);
  or or_6 (or_6_out, ~nand_36_out, ~nand_37_out, ~nand_38_out, ~nand_39_out);  // OR_Gate
  nand nand_40 (nand_40_out, COMM_4_0[4], COMM_4_0[3], COMM_4_0_N[2], COMM_4_0[1], LCSN);
  or or_7 (or_7_out, ~nand_40_out, ~nand_41_out);  // OR_Gate
  nand nand_41 (nand_41_out, COMM_4_0[4], COMM_4_0[3], COMM_4_0[2], COMM_4_0_N[1], COMM_4_0[0], LCSN);
  D_Flip_Flop d_ff_8 (.D(or_7_out), .clk(MCLK), .Q(d_ff_8_q));  // open: Qn, preset, reset
  nand nand_42 (nand_42_out, not_1_out, C24_z4);
  nand nand_43 (nand_43_out, not_7_out, C24_z5);
  not not_53 (WRITEN, d_ff_8_q);
  nand nand_44 (nand_44_out, not_2_out, C24_z6);
  nand nand_45 (nand_45_out, not_8_out, C24_z7);
  nand nand_46 (nand_46_out, LCSN, COMM_4_0_N[4], COMM_4_0[3], COMM_4_0[2], COMM_4_0[1], COMM_4_0_N[0]);
  D_Flip_Flop d_ff_9 (.D(nand_46_out), .clk(MCLK), .Q(CLFFN));  // open: Qn, preset, reset
  or or_8 (or_8_out, ~nand_42_out, ~nand_43_out, ~nand_44_out, ~nand_45_out);  // OR_Gate
  or or_9 (or_9_out, or_6_out, or_8_out, and_1_out, or_4_out);
  nand nand_47 (nand_47_out, LCSN, COMM_4_0_N[4], COMM_4_0_N[3], COMM_4_0[2], COMM_4_0_N[1], COMM_4_0_N[0]);
  not not_54 (CBRKN, or_9_out);
  D_Flip_Flop d_ff_10 (.D(nand_47_out), .clk(MCLK), .Qn(d_ff_10_qn));  // open: Q, preset, reset
  not not_55 (not_55_out, MRN);
  nor nor_4 (CLIRQN, d_ff_10_qn, not_55_out);
  nand nand_48 (nand_48_out, LCSN, COMM_4_0_N[4], COMM_4_0[3], COMM_4_0_N[2], COMM_4_0_N[1], COMM_4_0[0]);
  D_Flip_Flop d_ff_11 (.D(nand_48_out), .clk(MCLK), .Q(d_ff_11_q));  // open: Qn, preset, reset
  not not_56 (EPIC, d_ff_11_q);
  nand nand_49 (nand_49_out, LCSN, COMM_4_0[4], COMM_4_0[3], COMM_4_0[2], COMM_4_0[1], COMM_4_0_N[0], MIS_1_0_N[1], MIS_1_0_N[0]);
  D_Flip_Flop d_ff_12 (.D(nand_49_out), .clk(MCLK), .Q(LWCAN));  // open: Qn, preset, reset
  nand nand_50 (nand_50_out, LCSN, COMM_4_0_N[4], COMM_4_0_N[3], COMM_4_0_N[2], COMM_4_0[1], COMM_4_0_N[0]);
  or or_10 (or_10_out, ~nand_50_out, ~nand_51_out);  // OR_Gate
  nand nand_51 (nand_51_out, LCSN, COMM_4_0[4], COMM_4_0_N[3], COMM_4_0_N[2], COMM_4_0[1], COMM_4_0_N[0], MIS_1_0[1], MIS_1_0_N[0]);
  D_Flip_Flop d_ff_13 (.D(or_10_out), .clk(MCLK), .Q(LDGPRN));  // open: Qn, preset, reset
  nand nand_52 (nand_52_out, LCSN, COMM_4_0_N[4], COMM_4_0_N[3], COMM_4_0_N[2], COMM_4_0[1], COMM_4_0[0]);
  D_Flip_Flop d_ff_14 (.D(nand_52_out), .clk(MCLK), .Q(WRTRFN), .Qn(WRTRF));  // open: preset, reset
  nand nand_53 (nand_53_out, LCSN, COMM_4_0[4], COMM_4_0_N[3], COMM_4_0_N[2], COMM_4_0[1], COMM_4_0_N[0], MIS_1_0_N[1]);
  nand nand_54 (nand_54_out, LCSN, COMM_4_0[4], COMM_4_0_N[3], COMM_4_0_N[2], COMM_4_0[1], COMM_4_0_N[0], MIS_1_0[0]);
  nand nand_55 (nand_55_out, LCSN, COMM_4_0[4], COMM_4_0_N[3], COMM_4_0[1], COMM_4_0[0]);
  nand nand_56 (nand_56_out, LCSN, COMM_4_0[4], COMM_4_0_N[3], COMM_4_0[2]);
  or or_11 (CSMREQ, ~nand_53_out, ~nand_54_out, ~nand_55_out, ~nand_56_out, ~nand_57_out, ~nand_58_out);  // OR_Gate
  D_Flip_Flop d_ff_15 (.D(CSMREQ), .clk(MCLK), .Q(MREQ));  // open: Qn, preset, reset
  nand nand_57 (nand_57_out, LCSN, COMM_4_0[4], COMM_4_0[3], COMM_4_0_N[2]);
  nand nand_58 (nand_58_out, LCSN, COMM_4_0[4], COMM_4_0[3], COMM_4_0_N[1]);
  not not_57 (not_57_out, PONI);
  not not_58 (not_58_out, VEX);
  nand nand_59 (nand_59_out, not_57_out, LCSN);
  nand nand_60 (nand_60_out, COMM_4_0[4], COMM_4_0[3], COMM_4_0[2], COMM_4_0_N[1], MIS_1_0[1], MIS_1_0[0], not_58_out, LCSN);
  or or_12 (or_12_out, ~nand_59_out, ~nand_60_out, ~nand_61_out);  // OR_Gate
  not not_59 (not_59_out, LSHADOW);
  nand nand_61 (nand_61_out, COMM_4_0[4], COMM_4_0[3], COMM_4_0[2], COMM_4_0[1], COMM_4_0[0], MIS_1_0[1], LCSN);
  D_Flip_Flop d_ff_16 (.D(or_12_out), .clk(MCLK), .Qn(d_ff_16_qn));  // open: Q, preset, reset
  SCAN_WITH_RESET_N FD25 (.D(FIDBO5), .TE(SIOCN), .TI(FD25_q), .CLK(MCLK), .R(MRN), .Q(FD25_q));  // open: QN
  nand nand_62 (nand_62_out, d_ff_16_qn, not_59_out, MREQ, FD25_q, not_58_out, FETCHN);
  nand nand_63 (nand_63_out, d_ff_16_qn, not_59_out, MREQ, FD25_q, not_58_out, INTRQN);
  or or_13 (or_13_out, ~nand_62_out, ~nand_63_out);  // OR_Gate
  not not_60 (VACCN, or_13_out);
  nand nand_64 (nand_64_out, COMM_4_0_N[4], COMM_4_0[3], COMM_4_0[2], COMM_4_0_N[1], COMM_4_0_N[0], LCSN);
  D_Flip_Flop d_ff_17 (.D(nand_64_out), .clk(MCLK), .Q(d_ff_17_q));  // open: Qn, preset, reset
  D_Flip_Flop d_ff_18 (.D(d_ff_17_q), .clk(MCLK), .Q(DSTOPN));  // open: Qn, preset, reset

  // Notes on the sheet:
  //   Page 65 - CGA_DCD
  //   ICRY
  //   ICRYN
  //   SGR
  //   ISGRN
  //   IWP
  //   IWPN
  //   Page 72 - Sheet 8 of 10
  //   Page 68 - Sheet 4 of 10
  //   23
  //   Page 66 - Sheet 2 of 10
  //   25
  //   31
  //   Page 67 - Sheet 3 of 10
  //   MIS0
  //   MIS1
  //   MIS0N
  //   MIS1N
  //   15
  //   Page 69 - Sheet  5 of 10
  //   IWP
  //   IF15N
  //   IF15
  //   5
  //   IZFN
  //   IZ
  //   22.2
  //   23
  //   22.2, 23,24,25,26,27
  //   24-27
  //   ISGRN
  //   SGR
  //   ICRYN
  //   ICRY
  //   Page 70 - Sheet  6 of 10
  //   32
  //   33
  //   IF15N
  //   35
  //   IF15
  //   IZFN
  //   IZF
  //   16
  //   04
  //   11
  //   Page 71 - Sheet 7 of 10
  //   2
  //   3
  //   Page 73 - Sheet 9 of 10
  //   Page 75 - Sheet 10 of 10
  //   34.3
  //   35.3
  //   LSHADOWN
  //   37.2, 37.3
  //   DVACCN
  //   EMCLN
  //   14
endmodule

module test_DCD (
  input  in_1,
  input  in_2,
  input  in_3,
  output XFETCHN,
  output LDLCN,
  output LDPILN,
  output CSMREQ,
  output FETCHN,
  output WRITEN,
  output EPIC,
  output CFETCH
);

  wire CSMIS_1_0_carry, MASTER_CLOCK_out, not_1_out;
  wire [1:0] CSMIS_1_0_q;
  wire [4:0] CSCOMM_4_0_q;

  Counter #(.max('h3), .width(2)) CSMIS_1_0 (
    .clr(in_2), .load(1'b0), .up(1'b1), .clk(MASTER_CLOCK_out), .carry(CSMIS_1_0_carry), .Q(CSMIS_1_0_q));  // open: count, D
  Counter #(.max('h1f), .width(5)) CSCOMM_4_0 (
    .clr(in_2), .load(1'b0), .up(1'b1), .clk(not_1_out), .Q(CSCOMM_4_0_q));  // open: count, D, carry
  not not_1 (not_1_out, CSMIS_1_0_carry);
  // Probe on CSCOMM_4_0_q
  // Probe on CSMIS_1_0_q
  Clock MASTER_CLOCK (.out(MASTER_CLOCK_out));
  CGA_DCD cga_dcd_1 (
    .CSCOMM_4_0(CSCOMM_4_0_q), .CSMIS_1_0(CSMIS_1_0_q), .MCLK(MASTER_CLOCK_out), .ILCSN(in_1), .INTRQN(in_3),
    .XFETCHN(XFETCHN), .LDLCN(LDLCN), .LDPILN(LDPILN), .CSMREQ(CSMREQ), .FETCHN(FETCHN), .WRITEN(WRITEN),
    .EPIC(EPIC), .CFETCH(CFETCH));  // open: F15, ZF, CRY, SGR, WPN, PONI, VEX, BRKN, FIDBO5, MRN, LSHADOW, CSIDBS_4_0, INDN, CBRKN, DSTOPN, LDIRV, LDDBRN, CLFFN, LWCAN, LDGPRN, WRTRF, VACCN, CLIRQN, EPGSN, EPCRN, EPICVN, EPICSN, ERFN

  // Notes on the sheet:
  //   Need to research if this is correct..
  //   One could have been expected, but 2 ?
  //   Test shows that output signals (like WRITEN) changes value 2 clock signals after the CSCOMM signal changes.
endmodule

module BusDriver16 (
  input  [15:0] A_15_0,
  input  [15:0] IN_15_0,
  input  EN,
  input  TN,
  output [15:0] ZI_15_0,
  output [15:0] OUT_15_0
);

  BD4TU BD0 (.EN(EN), .TN(TN), .A(A_15_0[0]), .BUF_IN(IN_15_0[0]), .ZI(ZI_15_0[0]), .BUF_OUT(OUT_15_0[0]));
  BD4TU BD1 (.EN(EN), .TN(TN), .A(A_15_0[1]), .BUF_IN(IN_15_0[1]), .ZI(ZI_15_0[1]), .BUF_OUT(OUT_15_0[1]));
  BD4TU BD2 (.EN(EN), .TN(TN), .A(A_15_0[2]), .BUF_IN(IN_15_0[2]), .ZI(ZI_15_0[2]), .BUF_OUT(OUT_15_0[2]));
  BD4TU BD3 (.EN(EN), .TN(TN), .A(A_15_0[3]), .BUF_IN(IN_15_0[3]), .ZI(ZI_15_0[3]), .BUF_OUT(OUT_15_0[3]));
  BD4TU BD4 (.EN(EN), .TN(TN), .A(A_15_0[4]), .BUF_IN(IN_15_0[4]), .ZI(ZI_15_0[4]), .BUF_OUT(OUT_15_0[4]));
  BD4TU BD5 (.EN(EN), .TN(TN), .A(A_15_0[5]), .BUF_IN(IN_15_0[5]), .ZI(ZI_15_0[5]), .BUF_OUT(OUT_15_0[5]));
  BD4TU BD6 (.EN(EN), .TN(TN), .A(A_15_0[6]), .BUF_IN(IN_15_0[6]), .ZI(ZI_15_0[6]), .BUF_OUT(OUT_15_0[6]));
  BD4TU BD7 (.EN(EN), .TN(TN), .A(A_15_0[7]), .BUF_IN(IN_15_0[7]), .ZI(ZI_15_0[7]), .BUF_OUT(OUT_15_0[7]));
  BD4TU BD8 (.EN(EN), .TN(TN), .A(A_15_0[8]), .BUF_IN(IN_15_0[8]), .ZI(ZI_15_0[8]), .BUF_OUT(OUT_15_0[8]));
  BD4TU BD9 (.EN(EN), .TN(TN), .A(A_15_0[9]), .BUF_IN(IN_15_0[9]), .ZI(ZI_15_0[9]), .BUF_OUT(OUT_15_0[9]));
  BD4TU BD10 (.EN(EN), .TN(TN), .A(A_15_0[10]), .BUF_IN(IN_15_0[10]), .ZI(ZI_15_0[10]), .BUF_OUT(OUT_15_0[10]));
  BD4TU BD11 (.EN(EN), .TN(TN), .A(A_15_0[11]), .BUF_IN(IN_15_0[11]), .ZI(ZI_15_0[11]), .BUF_OUT(OUT_15_0[11]));
  BD4TU BD12 (.EN(EN), .TN(TN), .A(A_15_0[12]), .BUF_IN(IN_15_0[12]), .ZI(ZI_15_0[12]), .BUF_OUT(OUT_15_0[12]));
  BD4TU BD13 (.EN(EN), .TN(TN), .A(A_15_0[13]), .BUF_IN(IN_15_0[13]), .ZI(ZI_15_0[13]), .BUF_OUT(OUT_15_0[13]));
  BD4TU BD14 (.EN(EN), .TN(TN), .A(A_15_0[14]), .BUF_IN(IN_15_0[14]), .ZI(ZI_15_0[14]), .BUF_OUT(OUT_15_0[14]));
  BD4TU BD15 (.EN(EN), .TN(TN), .A(A_15_0[15]), .BUF_IN(IN_15_0[15]), .ZI(ZI_15_0[15]), .BUF_OUT(OUT_15_0[15]));

  // Notes on the sheet:
  //   16 bit three-state bus driver
  //   Special made for CGA page 6 (Sheet 5 of 8)
endmodule

module CGA_IDBCTL (
  input  MCLK,
  input  VACCN,
  input  [11:0] LA_21_10,
  input  FETCHN,
  input  PVIOL,
  input  EPGSN,
  input  EPCRN,
  input  EPICSN,
  input  EPICVN,
  input  EPICMASKN,
  input  PD,
  input  HIGSN,
  input  LOGSN,
  input  [15:0] PCR_15_0,
  input  [15:0] XFIDBI_15_0,
  input  [15:0] PICMASK_15_0,
  input  [2:0] PICV_2_0,
  input  [2:0] PICS_2_0,
  output [15:0] FIDBI_15_0
);

  wire nand_1_out;
  wire [1:0] PGSREG_pgs_15_14;
  wire [5:0] not_1_out;
  wire [11:0] PGSREG_pgs_11_0;

  nand nand_1 (nand_1_out, EPICMASKN, EPICVN, EPICSN, EPCRN, EPGSN);
  not not_1 (not_1_out[0], EPGSN);
  not not_2 (not_1_out[1], EPCRN);
  not not_3 (not_1_out[2], EPICSN);
  not not_4 (not_1_out[3], EPICVN);
  not not_5 (not_1_out[4], EPICMASKN);
  not not_6 (not_1_out[5], nand_1_out);
  CGA_IDBCTL_PGSREG PGSREG (
    .MCLK(MCLK), .VACCN(VACCN), .LA_21_10(LA_21_10), .FETCHN(FETCHN), .PVIOL(PVIOL),
    .PGS_15_14(PGSREG_pgs_15_14), .PGS_11_0(PGSREG_pgs_11_0));
  CGA_IDBCTL_SEL6 IDB15 (
    .D(XFIDBI_15_0[15]), .M(PICMASK_15_0[15]), .V(1'b0), .S(1'b0), .PCR(PCR_15_0[15]),
    .PGS(PGSREG_pgs_15_14[1]), .E_PINS(not_1_out), .D0(FIDBI_15_0[15]));
  CGA_IDBCTL_SEL6 IDB14 (
    .D(XFIDBI_15_0[14]), .M(PICMASK_15_0[14]), .V(1'b0), .S(1'b0), .PCR(PCR_15_0[14]),
    .PGS(PGSREG_pgs_15_14[0]), .E_PINS(not_1_out), .D0(FIDBI_15_0[14]));
  CGA_IDBCTL_SEL6 IDB13 (
    .D(XFIDBI_15_0[13]), .M(PICMASK_15_0[13]), .V(1'b0), .S(1'b0), .PCR(PCR_15_0[13]), .PGS(1'b0),
    .E_PINS(not_1_out), .D0(FIDBI_15_0[13]));
  CGA_IDBCTL_SEL6 IDB12 (
    .D(XFIDBI_15_0[12]), .M(PICMASK_15_0[12]), .V(1'b0), .S(1'b0), .PCR(PCR_15_0[12]), .PGS(1'b0),
    .E_PINS(not_1_out), .D0(FIDBI_15_0[12]));
  CGA_IDBCTL_SEL6 IDB11 (
    .D(XFIDBI_15_0[11]), .M(PICMASK_15_0[11]), .V(1'b0), .S(1'b0), .PCR(PCR_15_0[11]),
    .PGS(PGSREG_pgs_11_0[11]), .E_PINS(not_1_out), .D0(FIDBI_15_0[11]));
  CGA_IDBCTL_SEL6 IDB10 (
    .D(XFIDBI_15_0[10]), .M(PICMASK_15_0[10]), .PCR(PCR_15_0[10]), .PGS(PGSREG_pgs_11_0[10]),
    .E_PINS(not_1_out), .D0(FIDBI_15_0[10]));  // open: V, S
  CGA_IDBCTL_SEL6 IDB9 (
    .D(XFIDBI_15_0[9]), .M(PICMASK_15_0[9]), .V(1'b0), .S(1'b0), .PCR(PCR_15_0[9]), .PGS(PGSREG_pgs_11_0[9]),
    .E_PINS(not_1_out), .D0(FIDBI_15_0[9]));
  CGA_IDBCTL_SEL6 IDB8 (
    .D(XFIDBI_15_0[8]), .M(PICMASK_15_0[8]), .V(1'b0), .S(1'b0), .PCR(PCR_15_0[8]), .PGS(PGSREG_pgs_11_0[8]),
    .E_PINS(not_1_out), .D0(FIDBI_15_0[8]));
  CGA_IDBCTL_SEL6 IDB7 (
    .D(XFIDBI_15_0[7]), .M(PICMASK_15_0[7]), .V(1'b0), .S(1'b0), .PCR(PCR_15_0[7]), .PGS(PGSREG_pgs_11_0[7]),
    .E_PINS(not_1_out), .D0(FIDBI_15_0[7]));
  CGA_IDBCTL_SEL6 IDB6 (
    .D(XFIDBI_15_0[6]), .M(PICMASK_15_0[6]), .V(1'b0), .S(1'b0), .PCR(1'b0), .PGS(PGSREG_pgs_11_0[6]),
    .E_PINS(not_1_out), .D0(FIDBI_15_0[6]));
  CGA_IDBCTL_SEL6 IDB5 (
    .D(XFIDBI_15_0[5]), .M(PICMASK_15_0[5]), .V(1'b0), .S(1'b0), .PCR(1'b0), .PGS(PGSREG_pgs_11_0[5]),
    .E_PINS(not_1_out), .D0(FIDBI_15_0[5]));
  CGA_IDBCTL_SEL6 IDB4 (
    .D(XFIDBI_15_0[4]), .M(PICMASK_15_0[4]), .V(1'b0), .S(LOGSN), .PCR(1'b0), .PGS(PGSREG_pgs_11_0[4]),
    .E_PINS(not_1_out), .D0(FIDBI_15_0[4]));
  CGA_IDBCTL_SEL6 IDB3 (
    .D(XFIDBI_15_0[3]), .M(PICMASK_15_0[3]), .V(PD), .S(HIGSN), .PCR(1'b0), .PGS(PGSREG_pgs_11_0[3]),
    .E_PINS(not_1_out), .D0(FIDBI_15_0[3]));
  CGA_IDBCTL_SEL6 IDB2 (
    .D(XFIDBI_15_0[2]), .M(PICMASK_15_0[2]), .V(PICV_2_0[2]), .S(PICS_2_0[2]), .PCR(PCR_15_0[2]),
    .PGS(PGSREG_pgs_11_0[2]), .E_PINS(not_1_out), .D0(FIDBI_15_0[2]));
  CGA_IDBCTL_SEL6 IDB1 (
    .D(XFIDBI_15_0[1]), .M(PICMASK_15_0[1]), .V(PICV_2_0[1]), .S(PICS_2_0[1]), .PCR(PCR_15_0[1]),
    .PGS(PGSREG_pgs_11_0[1]), .E_PINS(not_1_out), .D0(FIDBI_15_0[1]));
  CGA_IDBCTL_SEL6 IDB0 (
    .D(XFIDBI_15_0[0]), .M(PICMASK_15_0[0]), .V(PICV_2_0[0]), .S(PICS_2_0[0]), .PCR(PCR_15_0[0]),
    .PGS(PGSREG_pgs_11_0[0]), .E_PINS(not_1_out), .D0(FIDBI_15_0[0]));

  // Notes on the sheet:
  //   Bit 5 = ED
  //   Page 97 - CGA_IDBCTL
  //   ED,EM,EV,ES,EPCR,EPGS
  //   BIT 0 = EPGS
  //   EPGS
  //   EPCR
  //   ES
  //   EV
  //   EM
  //   ED
  //   XFIDBI15
  //   XFIDBI0
  //   PICMASK15
  //   PICMASK0
  //   PCR15
  //   PCR0
  //   PGS15
  //   PGS14
  //   PGS11
  //   PGS0
  //   PICV2
  //   PICV1
  //   PICV0
  //   PICS2
  //   PICS1
  //   PICS0
endmodule

module CGA_IDBCTL_PGSREG (
  input  MCLK,
  input  VACCN,
  input  [11:0] LA_21_10,
  input  FETCHN,
  input  PVIOL,
  output [1:0] PGS_15_14,
  output [11:0] PGS_11_0
);

  wire not_1_out, PGS15_q;

  not not_1 (not_1_out, VACCN);
  SCAN_FF PGS15 (.D(PGS15_q), .TE(not_1_out), .TI(FETCHN), .CLK(MCLK), .Q(PGS15_q), .QN(PGS_15_14[1]));
  SCAN_FF PGS14 (.D(PGS_15_14[0]), .TE(not_1_out), .TI(PVIOL), .CLK(MCLK), .Q(PGS_15_14[0]));  // open: QN
  SCAN_FF PGS11 (.D(PGS_11_0[11]), .TE(not_1_out), .TI(LA_21_10[11]), .CLK(MCLK), .Q(PGS_11_0[11]));  // open: QN
  SCAN_FF PGS10 (.D(PGS_11_0[10]), .TE(not_1_out), .TI(LA_21_10[10]), .CLK(MCLK), .Q(PGS_11_0[10]));  // open: QN
  SCAN_FF PGS9 (.D(PGS_11_0[9]), .TE(not_1_out), .TI(LA_21_10[9]), .CLK(MCLK), .Q(PGS_11_0[9]));  // open: QN
  SCAN_FF PGS8 (.D(PGS_11_0[8]), .TE(not_1_out), .TI(LA_21_10[8]), .CLK(MCLK), .Q(PGS_11_0[8]));  // open: QN
  SCAN_FF PGS7 (.D(PGS_11_0[7]), .TE(not_1_out), .TI(LA_21_10[7]), .CLK(MCLK), .Q(PGS_11_0[7]));  // open: QN
  SCAN_FF PGS6 (.D(PGS_11_0[6]), .TE(not_1_out), .TI(LA_21_10[6]), .CLK(MCLK), .Q(PGS_11_0[6]));  // open: QN
  SCAN_FF PGS5 (.D(PGS_11_0[5]), .TE(not_1_out), .TI(LA_21_10[5]), .CLK(MCLK), .Q(PGS_11_0[5]));  // open: QN
  SCAN_FF PGS4 (.D(PGS_11_0[4]), .TE(not_1_out), .TI(LA_21_10[4]), .CLK(MCLK), .Q(PGS_11_0[4]));  // open: QN
  SCAN_FF PGS3 (.D(PGS_11_0[3]), .TE(not_1_out), .TI(LA_21_10[3]), .CLK(MCLK), .Q(PGS_11_0[3]));  // open: QN
  SCAN_FF PGS2 (.D(PGS_11_0[2]), .TE(not_1_out), .TI(LA_21_10[2]), .CLK(MCLK), .Q(PGS_11_0[2]));  // open: QN
  SCAN_FF PGS1 (.D(PGS_11_0[1]), .TE(not_1_out), .TI(LA_21_10[1]), .CLK(MCLK), .Q(PGS_11_0[1]));  // open: QN
  SCAN_FF PGS0 (.D(PGS_11_0[0]), .TE(not_1_out), .TI(LA_21_10[0]), .CLK(MCLK), .Q(PGS_11_0[0]));  // open: QN

  // Notes on the sheet:
  //   Page 98 - CGA_IDBCTL_PGSREG - Completed, not tested
endmodule

module CGA_IDBCTL_SEL6 (
  input  D,
  input  M,
  input  V,
  input  S,
  input  PCR,
  input  PGS,
  input  [5:0] E_PINS,
  output D0
);

  wire nand_1_out, nand_2_out, nand_3_out, nand_4_out, nand_5_out, nand_6_out;

  nand nand_1 (nand_1_out, D, E_PINS[5]);
  nand nand_2 (nand_2_out, M, E_PINS[4]);
  nand nand_3 (nand_3_out, V, E_PINS[3]);
  nand nand_4 (nand_4_out, S, E_PINS[2]);
  nand nand_5 (nand_5_out, PCR, E_PINS[1]);
  nand nand_6 (nand_6_out, PGS, E_PINS[0]);
  or or_1 (D0, ~nand_1_out, ~nand_2_out, ~nand_3_out, ~nand_4_out, ~nand_5_out, ~nand_6_out);  // OR_Gate

  // Notes on the sheet:
  //   Bit 5 = ED
  //   ED,EM,EV,ES,EPCR,EPGS
  //   Page 99 - CGA_IDBCTL_SEL6   - Tested manually
  //   BIT 0 = EPGS
endmodule

module test_IDBCTL (
);

  CGA_IDBCTL cga_idbctl_1 ();  // open: MCLK, VACCN, LA_21_10, FETCHN, PVIOL, EPGSN, EPCRN, EPICSN, EPICVN, EPICMASKN, PD, HIGSN, LOGSN, PCR_15_0, XFIDBI_15_0, PICMASK_15_0, PICV_2_0, PICS_2_0, FIDBI_15_0
endmodule

module CGA_INTR (
  input  PANN,
  input  MCLK,
  input  CLIRQN,
  input  EMPIDN,
  input  BINT15N,
  input  POWFAILN,
  input  NORN,
  input  PARERRN,
  input  IOXERRN,
  input  Z,
  input  BINT13N,
  input  BINT12N,
  input  BINT11N,
  input  BINT10N,
  input  [15:0] FIDBO_15_0,
  input  [3:0] LAA_3_0,
  input  EPIC,
  output INTRQN,
  output [15:0] PICMASK_15_0,
  output HIGSN,
  output PD,
  output [2:0] PICV_2_0,
  output IRQ,
  output LOGSN,
  output [2:0] PICS_2_0,
  output EPICMASKN
);

  wire CNTLR_irqn, not_2_out, or_1_out;
  wire [15:0] IRSRC_ireq_15_0_n;

  CGA_INTR_IRSRC IRSRC (
    .EMPIDN(EMPIDN), .BINT15N(BINT15N), .POWFAILN(POWFAILN), .NORN(NORN), .PARERRN(PARERRN),
    .IOXERRN(IOXERRN), .Z(Z), .BINT13N(BINT13N), .BINT12N(BINT12N), .BINT11N(BINT11N), .BINT10N(BINT10N),
    .FIDBO_15_0(FIDBO_15_0), .IREQ_15_0_N(IRSRC_ireq_15_0_n));
  CGA_INTR_CNTLR CNTLR (
    .IREQ_15_0_N(IRSRC_ireq_15_0_n), .MCLK(MCLK), .FIDBO_15_0(FIDBO_15_0), .LAA_3_0(LAA_3_0), .EPIC(EPIC),
    .PICMASK_15_0(PICMASK_15_0), .HIGSN(HIGSN), .PD(PD), .PICV_2_0(PICV_2_0), .IRQN(CNTLR_irqn),
    .LOGSN(LOGSN), .PICS_2_0(PICS_2_0), .EPICMASKN(EPICMASKN));
  not not_1 (IRQ, CNTLR_irqn);
  or or_1 (or_1_out, ~PANN, ~CNTLR_irqn);  // OR_Gate
  not not_2 (not_2_out, CLIRQN);
  D_Flip_Flop d_ff_1 (.D(or_1_out), .clk(MCLK), .Qn(INTRQN), .reset(not_2_out));  // open: Q, preset

  // Notes on the sheet:
  //   Page 74 - CGA_INTR
endmodule

module CGA_INTR_IRSRC (
  input  EMPIDN,
  input  BINT15N,
  input  POWFAILN,
  input  NORN,
  input  PARERRN,
  input  IOXERRN,
  input  Z,
  input  BINT13N,
  input  BINT12N,
  input  BINT11N,
  input  BINT10N,
  input  [15:0] FIDBO_15_0,
  output [15:0] IREQ_15_0_N
);

  wire nand_1_out, nand_3_out, nand_4_out, nand_5_out, nand_6_out, nand_8_out, nand_13_out, nand_14_out,
       nand_15_out, nand_16_out, not_1_out, not_2_out;

  not not_1 (not_1_out, Z);
  not not_2 (not_2_out, EMPIDN);
  nand nand_1 (nand_1_out, FIDBO_15_0[15], not_2_out);
  nand nand_2 (IREQ_15_0_N[14], FIDBO_15_0[14], not_2_out);
  nand nand_3 (nand_3_out, FIDBO_15_0[13], not_2_out);
  nand nand_4 (nand_4_out, FIDBO_15_0[12], not_2_out);
  nand nand_5 (nand_5_out, FIDBO_15_0[11], not_2_out);
  nand nand_6 (nand_6_out, FIDBO_15_0[10], not_2_out);
  nand nand_7 (IREQ_15_0_N[9], FIDBO_15_0[9], not_2_out);
  nand nand_8 (nand_8_out, FIDBO_15_0[8], not_2_out);
  nand nand_9 (IREQ_15_0_N[7], FIDBO_15_0[7], not_2_out);
  nand nand_10 (IREQ_15_0_N[6], FIDBO_15_0[6], not_2_out);
  nand nand_11 (IREQ_15_0_N[5], FIDBO_15_0[5], not_2_out);
  nand nand_12 (IREQ_15_0_N[4], FIDBO_15_0[4], not_2_out);
  nand nand_13 (nand_13_out, FIDBO_15_0[3], not_2_out);
  nand nand_14 (nand_14_out, FIDBO_15_0[2], not_2_out);
  nand nand_15 (nand_15_out, FIDBO_15_0[1], not_2_out);
  nand nand_16 (nand_16_out, FIDBO_15_0[0], not_2_out);
  nor nor_1 (IREQ_15_0_N[15], ~nand_1_out, ~BINT15N);  // NOR_Gate
  nor nor_2 (IREQ_15_0_N[13], ~nand_3_out, ~POWFAILN);  // NOR_Gate
  nor nor_3 (IREQ_15_0_N[12], ~nand_4_out, ~NORN);  // NOR_Gate
  nor nor_4 (IREQ_15_0_N[11], ~nand_5_out, ~PARERRN);  // NOR_Gate
  nor nor_5 (IREQ_15_0_N[10], ~nand_6_out, ~IOXERRN);  // NOR_Gate
  nor nor_6 (IREQ_15_0_N[8], ~nand_8_out, ~not_1_out);  // NOR_Gate
  nor nor_7 (IREQ_15_0_N[3], ~nand_13_out, ~BINT13N);  // NOR_Gate
  nor nor_8 (IREQ_15_0_N[2], ~nand_14_out, ~BINT12N);  // NOR_Gate
  nor nor_9 (IREQ_15_0_N[1], ~nand_15_out, ~BINT11N);  // NOR_Gate
  nor nor_10 (IREQ_15_0_N[0], ~nand_16_out, ~BINT10N);  // NOR_Gate

  // Notes on the sheet:
  //   Page 76 - CGA_INTR_IRSRC
  //   EMPID
  //   IREQ15N
  //   IREQ14N
  //   IREQ13N
  //   IREQ12N
  //   IREQ11N
  //   IREQ10N
endmodule

module CGA_INTR_CNTLR (
  input  [15:0] IREQ_15_0_N,
  input  MCLK,
  input  [15:0] FIDBO_15_0,
  input  [3:0] LAA_3_0,
  input  EPIC,
  output [15:0] PICMASK_15_0,
  output HIGSN,
  output PD,
  output [2:0] PICV_2_0,
  output IRQN,
  output LOGSN,
  output [2:0] PICS_2_0,
  output EPICMASKN
);

  wire A, B, C, D, E, G, H, HIF, HIK, HIPASSALL, J, L, LOF, LOK, LOPASSALL, M, N, not_1_out, OEM, OESN, S,
       VECGEN_hidet, VECGEN_hivges, VECGEN_lodet, VECGEN_lovges;
  wire [2:0] VECGEN_hivec_2_0, VECGEN_hx_2_0, VECGEN_hx_2_0_n, VECGEN_lovec_2_0, VECGEN_lx_2_0,
       VECGEN_lx_2_0_n;
  wire [7:0] multiplexer_1_out, multiplexer_1_out_2;
  wire [15:0] CLR_CLEAR_CONTROL_clrq, IRQ_mireq_15_0_n;

  Multiplexer #(.width(16)) multiplexer_1 (
    .in0(FIDBO_15_0), .in1(PICMASK_15_0), .out({multiplexer_1_out_2, multiplexer_1_out}), .sel(OEM));
  not not_1 (not_1_out, MCLK);
  CGA_INTR_CNTLR_MDCD MDCD (
    .LAA_3_0(LAA_3_0), .EPIC(EPIC), .HIPASSALL(HIPASSALL), .LOPASSALL(LOPASSALL), .MCLK(MCLK), .OESN(OESN),
    .E(E), .J(J), .D(D), .N(N), .HIK(HIK), .A(A), .HIF(HIF), .G(G), .H(H), .L(L), .B(B), .S(S), .M(M),
    .LOF(LOF), .C(C), .LOK(LOK), .OEM(OEM), .EPICMASKN(EPICMASKN));
  CGA_INTR_CNTLR_IRQ IRQ (
    .CLRQ_15_0(CLR_CLEAR_CONTROL_clrq), .IREQ_15_0_N(IREQ_15_0_N), .CPN(not_1_out), .MCLK(MCLK),
    .DIN_15_0({multiplexer_1_out_2, multiplexer_1_out}), .A(A), .B(B), .C(C),
    .MIREQ_15_0_N(IRQ_mireq_15_0_n), .PICMASK_15_0(PICMASK_15_0));
  CGA_INTR_CNTLR_VECGEN VECGEN (
    .MIREQ_15_0_N(IRQ_mireq_15_0_n), .MCLK(MCLK), .N(N), .HIF(HIF), .FIDBO3(FIDBO_15_0[3]), .LOF(LOF), .G(G),
    .FIDBO4(FIDBO_15_0[4]), .HIGSN(HIGSN), .FIDBO_2_0(FIDBO_15_0[2:0]), .LOGSN(LOGSN), .OESN(OESN),
    .HIDET(VECGEN_hidet), .HIVEC_2_0(VECGEN_hivec_2_0), .LODET(VECGEN_lodet), .LOVEC_2_0(VECGEN_lovec_2_0),
    .HX_2_0(VECGEN_hx_2_0), .HX_2_0_N(VECGEN_hx_2_0_n), .LX_2_0(VECGEN_lx_2_0), .LX_2_0_N(VECGEN_lx_2_0_n),
    .PICS_2_0(PICS_2_0), .HIVGES(VECGEN_hivges), .LOVGES(VECGEN_lovges));
  CGA_INTR_CNTLR_CLR CLR_CLEAR_CONTROL (
    .J(J), .LOK(LOK), .HIK(HIK), .DIN_7_0(multiplexer_1_out), .DIN_15_8(multiplexer_1_out_2),
    .LX_2_0(VECGEN_lx_2_0), .HX_2_0(VECGEN_hx_2_0), .LX_2_0_N(VECGEN_lx_2_0_n), .HX_2_0_N(VECGEN_hx_2_0_n),
    .CLRQ(CLR_CLEAR_CONTROL_clrq));
  CGA_INTR_CNTLR_IRGEL IRGEL (
    .FIDB03(FIDBO_15_0[3]), .HIDET(VECGEN_hidet), .HIVGES(VECGEN_hivges), .E(E), .MCLK(MCLK), .D(D), .S(S),
    .H(H), .HIVEC_2_0(VECGEN_hivec_2_0), .LOVEC_2_0(VECGEN_lovec_2_0), .LODET(VECGEN_lodet),
    .LOVGES(VECGEN_lovges), .N(N), .L(L), .FIDB04(FIDBO_15_0[4]), .M(M), .HIGSN(HIGSN), .PD(PD),
    .HIPASSALL(HIPASSALL), .PICV_2_0(PICV_2_0), .IRQN(IRQN), .LOPASSALL(LOPASSALL), .LOGSN(LOGSN));

  // Other names for the same wires on the sheet: FIDB0_2_0[2:0] = FIDBO_15_0[2:0]; FIDB03 = FIDBO_15_0[3];
  //   FIDB04 = FIDBO_15_0[4]

  // Notes on the sheet:
  //   Page 77 - CGA_INTR_CNTLR
  //   Vector Generator & Status
endmodule

module CGA_INTR_CNTLR_IRQ_REG (
  input  [15:0] CLRQ_15_0,
  input  [15:0] IRQ_15_0_N,
  input  CPN,
  input  MCLK,
  output [15:0] LREQ_15_0
);

  CGA_INTR_CNTLR_IRQ_REG_RQBIT RQBIT_0 (
    .PN(IRQ_15_0_N[0]), .CPN(CPN), .CLR(CLRQ_15_0[0]), .CP(MCLK), .INR(LREQ_15_0[0]));
  CGA_INTR_CNTLR_IRQ_REG_RQBIT RQBIT_1 (
    .PN(IRQ_15_0_N[1]), .CPN(CPN), .CLR(CLRQ_15_0[1]), .CP(MCLK), .INR(LREQ_15_0[1]));
  CGA_INTR_CNTLR_IRQ_REG_RQBIT RQBIT_2 (
    .PN(IRQ_15_0_N[2]), .CPN(CPN), .CLR(CLRQ_15_0[2]), .CP(MCLK), .INR(LREQ_15_0[2]));
  CGA_INTR_CNTLR_IRQ_REG_RQBIT RQBIT_3 (
    .PN(IRQ_15_0_N[3]), .CPN(CPN), .CLR(CLRQ_15_0[3]), .CP(MCLK), .INR(LREQ_15_0[3]));
  CGA_INTR_CNTLR_IRQ_REG_RQBIT RQBIT_4 (
    .PN(IRQ_15_0_N[4]), .CPN(CPN), .CLR(CLRQ_15_0[4]), .CP(MCLK), .INR(LREQ_15_0[4]));
  CGA_INTR_CNTLR_IRQ_REG_RQBIT RQBIT_5 (
    .PN(IRQ_15_0_N[5]), .CPN(CPN), .CLR(CLRQ_15_0[5]), .CP(MCLK), .INR(LREQ_15_0[5]));
  CGA_INTR_CNTLR_IRQ_REG_RQBIT RQBIT_6 (
    .PN(IRQ_15_0_N[6]), .CPN(CPN), .CLR(CLRQ_15_0[6]), .CP(MCLK), .INR(LREQ_15_0[6]));
  CGA_INTR_CNTLR_IRQ_REG_RQBIT RQBIT_7 (
    .PN(IRQ_15_0_N[7]), .CPN(CPN), .CLR(CLRQ_15_0[7]), .CP(MCLK), .INR(LREQ_15_0[7]));
  CGA_INTR_CNTLR_IRQ_REG_RQBIT RQBIT_8 (
    .PN(CLRQ_15_0[8]), .CPN(CPN), .CLR(IRQ_15_0_N[8]), .CP(MCLK), .INR(LREQ_15_0[8]));
  CGA_INTR_CNTLR_IRQ_REG_RQBIT RQBIT_9 (
    .PN(CLRQ_15_0[9]), .CPN(CPN), .CLR(IRQ_15_0_N[9]), .CP(MCLK), .INR(LREQ_15_0[9]));
  CGA_INTR_CNTLR_IRQ_REG_RQBIT RQBIT_10 (
    .PN(CLRQ_15_0[10]), .CPN(CPN), .CLR(IRQ_15_0_N[10]), .CP(MCLK), .INR(LREQ_15_0[10]));
  CGA_INTR_CNTLR_IRQ_REG_RQBIT RQBIT_11 (
    .PN(CLRQ_15_0[11]), .CPN(CPN), .CLR(IRQ_15_0_N[11]), .CP(MCLK), .INR(LREQ_15_0[11]));
  CGA_INTR_CNTLR_IRQ_REG_RQBIT RQBIT_12 (
    .PN(CLRQ_15_0[12]), .CPN(CPN), .CLR(IRQ_15_0_N[12]), .CP(MCLK), .INR(LREQ_15_0[12]));
  CGA_INTR_CNTLR_IRQ_REG_RQBIT RQBIT_13 (
    .PN(CLRQ_15_0[13]), .CPN(CPN), .CLR(IRQ_15_0_N[13]), .CP(MCLK), .INR(LREQ_15_0[13]));
  CGA_INTR_CNTLR_IRQ_REG_RQBIT RQBIT_14 (
    .PN(CLRQ_15_0[14]), .CPN(CPN), .CLR(IRQ_15_0_N[14]), .CP(MCLK), .INR(LREQ_15_0[14]));
  CGA_INTR_CNTLR_IRQ_REG_RQBIT RQBIT_15 (
    .PN(CLRQ_15_0[15]), .CPN(CPN), .CLR(IRQ_15_0_N[15]), .CP(MCLK), .INR(LREQ_15_0[15]));

  // Notes on the sheet:
  //   Page 78 - CGA_INTR_CNTLR_IRQ_REG - Completed, not tested
endmodule

module CGA_INTR_CNTLR_IRQ_REG_RQBIT (
  input  PN,
  input  CPN,
  input  CLR,
  input  CP,
  output INR
);

  wire nand_1_out, nand_2_out, nand_3_out, not_1_out, not_2_out, not_3_out, or_1_out;

  nand nand_1 (nand_1_out, CPN, CLR);
  not not_1 (not_1_out, CLR);
  not not_2 (not_2_out, PN);
  not not_3 (not_3_out, nand_2_out);
  or or_1 (or_1_out, not_2_out, not_3_out);
  nand nand_2 (nand_2_out, or_1_out, nand_1_out);
  nand nand_3 (nand_3_out, or_1_out, not_1_out);
  D_Flip_Flop d_ff_1 (.D(nand_3_out), .clk(CP), .Qn(INR));  // open: Q, preset, reset

  // Notes on the sheet:
  //   Page 78 - CGA_INTR_CNTLR_IRQ_REG_RQBIT - Completed, not tested
endmodule

module CGA_INTR_CNTLR_IRQ (
  input  [15:0] CLRQ_15_0,
  input  [15:0] IREQ_15_0_N,
  input  CPN,
  input  MCLK,
  input  [15:0] DIN_15_0,
  input  A,
  input  B,
  input  C,
  output [15:0] MIREQ_15_0_N,
  output [15:0] PICMASK_15_0
);

  wire [15:0] IRQ_MASK_picmask_15_0_n, IRQ_REG_lreq_15_0;

  CGA_INTR_CNTLR_IRQ_REG IRQ_REG (
    .CLRQ_15_0(CLRQ_15_0), .IRQ_15_0_N(IREQ_15_0_N), .CPN(CPN), .MCLK(MCLK), .LREQ_15_0(IRQ_REG_lreq_15_0));
  CGA_INTR_CNTLR_IRQ_MASK IRQ_MASK (
    .DIN_15_0(DIN_15_0), .A(A), .B(B), .C(C), .MCLK(MCLK), .PICMASK_15_0_N(IRQ_MASK_picmask_15_0_n),
    .PICMASK_15_0(PICMASK_15_0));
  CGA_INTR_CNTLR_IRQ_MREQ IRQ_MREQ (
    .LREQ_15_0(IRQ_REG_lreq_15_0), .PICMASK_15_0_N(IRQ_MASK_picmask_15_0_n), .MIREQ_15_0(MIREQ_15_0_N));

  // Notes on the sheet:
  //   Page 79 - CGA_INTR_CNTLR_IRQ 
endmodule

module CGA_INTR_CNTLR_IRQ_MASK (
  input  [15:0] DIN_15_0,
  input  A,
  input  B,
  input  C,
  input  MCLK,
  output [15:0] PICMASK_15_0_N,
  output [15:0] PICMASK_15_0
);

  wire not_1_out;

  not not_1 (not_1_out, C);
  CGA_INTR_CNTLR_IRQ_MASK_MASKBIT MASKBIT15 (
    .DCDA(A), .DATAIN(DIN_15_0[15]), .DCDB(B), .DCDCN(not_1_out), .CLOCK(MCLK), .MSKN(PICMASK_15_0_N[15]),
    .MSK(PICMASK_15_0[15]));
  CGA_INTR_CNTLR_IRQ_MASK_MASKBIT MASKBIT14 (
    .DCDA(A), .DATAIN(DIN_15_0[14]), .DCDB(B), .DCDCN(not_1_out), .CLOCK(MCLK), .MSKN(PICMASK_15_0_N[14]),
    .MSK(PICMASK_15_0[14]));
  CGA_INTR_CNTLR_IRQ_MASK_MASKBIT MASKBIT13 (
    .DCDA(A), .DATAIN(DIN_15_0[13]), .DCDB(B), .DCDCN(not_1_out), .CLOCK(MCLK), .MSKN(PICMASK_15_0_N[13]),
    .MSK(PICMASK_15_0[13]));
  CGA_INTR_CNTLR_IRQ_MASK_MASKBIT MASKBIT12 (
    .DCDA(A), .DATAIN(DIN_15_0[12]), .DCDB(B), .DCDCN(not_1_out), .CLOCK(MCLK), .MSKN(PICMASK_15_0_N[12]),
    .MSK(PICMASK_15_0[12]));
  CGA_INTR_CNTLR_IRQ_MASK_MASKBIT MASKBIT11 (
    .DCDA(A), .DATAIN(DIN_15_0[11]), .DCDB(B), .DCDCN(not_1_out), .CLOCK(MCLK), .MSKN(PICMASK_15_0_N[11]),
    .MSK(PICMASK_15_0[11]));
  CGA_INTR_CNTLR_IRQ_MASK_MASKBIT MASKBIT10 (
    .DCDA(A), .DATAIN(DIN_15_0[10]), .DCDB(B), .DCDCN(not_1_out), .CLOCK(MCLK), .MSKN(PICMASK_15_0_N[10]),
    .MSK(PICMASK_15_0[10]));
  CGA_INTR_CNTLR_IRQ_MASK_MASKBIT MASKBIT9 (
    .DCDA(A), .DATAIN(DIN_15_0[9]), .DCDB(B), .DCDCN(not_1_out), .CLOCK(MCLK), .MSKN(PICMASK_15_0_N[9]),
    .MSK(PICMASK_15_0[9]));
  CGA_INTR_CNTLR_IRQ_MASK_MASKBIT MASKBIT8 (
    .DCDA(A), .DATAIN(DIN_15_0[8]), .DCDB(B), .DCDCN(not_1_out), .CLOCK(MCLK), .MSKN(PICMASK_15_0_N[8]),
    .MSK(PICMASK_15_0[8]));
  CGA_INTR_CNTLR_IRQ_MASK_MASKBIT MASKBIT7 (
    .DCDA(A), .DATAIN(DIN_15_0[7]), .DCDB(B), .DCDCN(not_1_out), .CLOCK(MCLK), .MSKN(PICMASK_15_0_N[7]),
    .MSK(PICMASK_15_0[7]));
  CGA_INTR_CNTLR_IRQ_MASK_MASKBIT MASKBIT6 (
    .DCDA(A), .DATAIN(DIN_15_0[6]), .DCDB(B), .DCDCN(not_1_out), .CLOCK(MCLK), .MSKN(PICMASK_15_0_N[6]),
    .MSK(PICMASK_15_0[6]));
  CGA_INTR_CNTLR_IRQ_MASK_MASKBIT MASKBIT5 (
    .DCDA(A), .DATAIN(DIN_15_0[5]), .DCDB(B), .DCDCN(not_1_out), .CLOCK(MCLK), .MSKN(PICMASK_15_0_N[5]),
    .MSK(PICMASK_15_0[5]));
  CGA_INTR_CNTLR_IRQ_MASK_MASKBIT MASKBIT4 (
    .DCDA(A), .DATAIN(DIN_15_0[4]), .DCDB(B), .DCDCN(not_1_out), .CLOCK(MCLK), .MSKN(PICMASK_15_0_N[4]),
    .MSK(PICMASK_15_0[4]));
  CGA_INTR_CNTLR_IRQ_MASK_MASKBIT MASKBIT3 (
    .DCDA(A), .DATAIN(DIN_15_0[3]), .DCDB(B), .DCDCN(not_1_out), .CLOCK(MCLK), .MSKN(PICMASK_15_0_N[3]),
    .MSK(PICMASK_15_0[3]));
  CGA_INTR_CNTLR_IRQ_MASK_MASKBIT MASKBIT2 (
    .DCDA(A), .DATAIN(DIN_15_0[2]), .DCDB(B), .DCDCN(not_1_out), .CLOCK(MCLK), .MSKN(PICMASK_15_0_N[2]),
    .MSK(PICMASK_15_0[2]));
  CGA_INTR_CNTLR_IRQ_MASK_MASKBIT MASKBIT1 (
    .DCDA(A), .DATAIN(DIN_15_0[1]), .DCDB(B), .DCDCN(not_1_out), .CLOCK(MCLK), .MSKN(PICMASK_15_0_N[1]),
    .MSK(PICMASK_15_0[1]));
  CGA_INTR_CNTLR_IRQ_MASK_MASKBIT MASKBIT0 (
    .DCDA(A), .DATAIN(DIN_15_0[0]), .DCDB(B), .DCDCN(not_1_out), .CLOCK(MCLK), .MSKN(PICMASK_15_0_N[0]),
    .MSK(PICMASK_15_0[0]));

  // Notes on the sheet:
  //   Page 80 - CGA_INTR_CNTLR_IRQ_MASK 
  //   CN
endmodule

module CGA_INTR_CNTLR_IRQ_MASK_MASKBIT (
  input  DCDA,
  input  DATAIN,
  input  DCDB,
  input  DCDCN,
  input  CLOCK,
  output MSKN,
  output MSK
);

  wire nand_1_out, nand_2_out, nand_3_out, or_1_out, xnor_1_out;

  nand nand_1 (nand_1_out, MSK, DCDA);
  nand nand_2 (nand_2_out, DATAIN, DCDB);
  nand nand_3 (nand_3_out, DCDB, MSKN, DCDCN);
  or or_1 (or_1_out, ~nand_1_out, ~nand_2_out, ~nand_3_out);  // OR_Gate
  xnor xnor_1 (xnor_1_out, or_1_out, DCDCN);
  D_Flip_Flop d_ff_1 (.D(xnor_1_out), .clk(CLOCK), .Q(MSKN), .Qn(MSK));  // open: preset, reset

  // Notes on the sheet:
  //   Page 80 - CGA_INTR_CNTLR_IRQ_MASK_MASKBIT
endmodule

module CGA_INTR_CNTLR_IRQ_MREQ (
  input  [15:0] LREQ_15_0,
  input  [15:0] PICMASK_15_0_N,
  output [15:0] MIREQ_15_0
);

  nand nand_1 (MIREQ_15_0[15], LREQ_15_0[15], PICMASK_15_0_N[15]);
  nand nand_2 (MIREQ_15_0[14], LREQ_15_0[14], PICMASK_15_0_N[14]);
  nand nand_3 (MIREQ_15_0[13], LREQ_15_0[13], PICMASK_15_0_N[13]);
  nand nand_4 (MIREQ_15_0[12], LREQ_15_0[12], PICMASK_15_0_N[12]);
  nand nand_5 (MIREQ_15_0[11], LREQ_15_0[11], PICMASK_15_0_N[11]);
  nand nand_6 (MIREQ_15_0[10], LREQ_15_0[10], PICMASK_15_0_N[10]);
  nand nand_7 (MIREQ_15_0[9], LREQ_15_0[9], PICMASK_15_0_N[9]);
  nand nand_8 (MIREQ_15_0[8], LREQ_15_0[8], PICMASK_15_0_N[8]);
  nand nand_9 (MIREQ_15_0[7], LREQ_15_0[7], PICMASK_15_0_N[7]);
  nand nand_10 (MIREQ_15_0[6], LREQ_15_0[6], PICMASK_15_0_N[6]);
  nand nand_11 (MIREQ_15_0[5], LREQ_15_0[5], PICMASK_15_0_N[5]);
  nand nand_12 (MIREQ_15_0[4], LREQ_15_0[4], PICMASK_15_0_N[4]);
  nand nand_13 (MIREQ_15_0[3], LREQ_15_0[3], PICMASK_15_0_N[3]);
  nand nand_14 (MIREQ_15_0[2], LREQ_15_0[2], PICMASK_15_0_N[2]);
  nand nand_15 (MIREQ_15_0[1], LREQ_15_0[1], PICMASK_15_0_N[1]);
  nand nand_16 (MIREQ_15_0[0], LREQ_15_0[0], PICMASK_15_0_N[0]);

  // Notes on the sheet:
  //   Page 81 - CGA_INTR_CNTLR_IRQ_MREQ
  //   PICMASK0N
  //   PICMASK15N
  //   MIREQ15N
  //   MIREQ0N
endmodule

module CGA_INTR_CNTLR_CLR (
  input  J,
  input  LOK,
  input  HIK,
  input  [7:0] DIN_7_0,
  input  [7:0] DIN_15_8,
  input  [2:0] LX_2_0,
  input  [2:0] HX_2_0,
  input  [2:0] LX_2_0_N,
  input  [2:0] HX_2_0_N,
  output [15:0] CLRQ
);

  CGA_INTR_CNTLR_CLR_CLRBIT CLRB7 (
    .DCDJ(J), .DCDK(LOK), .DATA(DIN_7_0[7]), .X0(LX_2_0[0]), .X1(LX_2_0[1]), .X2(LX_2_0[2]), .BIT(CLRQ[7]));
  CGA_INTR_CNTLR_CLR_CLRBIT CLRB6 (
    .DCDJ(J), .DCDK(LOK), .DATA(DIN_7_0[6]), .X0(LX_2_0_N[0]), .X1(LX_2_0[1]), .X2(LX_2_0[2]), .BIT(CLRQ[6]));
  CGA_INTR_CNTLR_CLR_CLRBIT CLRB5 (
    .DCDJ(J), .DCDK(LOK), .DATA(DIN_7_0[5]), .X0(LX_2_0[0]), .X1(LX_2_0_N[1]), .X2(LX_2_0[2]), .BIT(CLRQ[5]));
  CGA_INTR_CNTLR_CLR_CLRBIT CLRB4 (
    .DCDJ(J), .DCDK(LOK), .DATA(DIN_7_0[4]), .X0(LX_2_0_N[0]), .X1(LX_2_0_N[1]), .X2(LX_2_0[2]), .BIT(CLRQ[4]));
  CGA_INTR_CNTLR_CLR_CLRBIT CLRB3 (
    .DCDJ(J), .DCDK(LOK), .DATA(DIN_7_0[3]), .X0(LX_2_0[0]), .X1(LX_2_0[1]), .X2(LX_2_0_N[2]), .BIT(CLRQ[3]));
  CGA_INTR_CNTLR_CLR_CLRBIT CLRB2 (
    .DCDJ(J), .DCDK(LOK), .DATA(DIN_7_0[2]), .X0(LX_2_0_N[0]), .X1(LX_2_0[1]), .X2(LX_2_0_N[2]), .BIT(CLRQ[2]));
  CGA_INTR_CNTLR_CLR_CLRBIT CLRB1 (
    .DCDJ(J), .DCDK(LOK), .DATA(DIN_7_0[1]), .X0(LX_2_0[0]), .X1(LX_2_0_N[1]), .X2(LX_2_0_N[2]), .BIT(CLRQ[1]));
  CGA_INTR_CNTLR_CLR_CLRBIT CLRB0 (
    .DCDJ(J), .DCDK(LOK), .DATA(DIN_7_0[0]), .X0(LX_2_0_N[0]), .X1(LX_2_0_N[1]), .X2(LX_2_0_N[2]),
    .BIT(CLRQ[0]));
  CGA_INTR_CNTLR_CLR_CLRBIT CLRB15 (
    .DCDJ(J), .DCDK(HIK), .DATA(DIN_15_8[7]), .X0(HX_2_0[0]), .X1(HX_2_0[1]), .X2(HX_2_0[2]), .BIT(CLRQ[15]));
  CGA_INTR_CNTLR_CLR_CLRBIT CLRB14 (
    .DCDJ(J), .DCDK(HIK), .DATA(DIN_15_8[6]), .X0(HX_2_0_N[0]), .X1(HX_2_0[1]), .X2(HX_2_0[2]), .BIT(CLRQ[14]));
  CGA_INTR_CNTLR_CLR_CLRBIT CLRB13 (
    .DCDJ(J), .DCDK(HIK), .DATA(DIN_15_8[5]), .X0(HX_2_0[0]), .X1(HX_2_0_N[1]), .X2(HX_2_0[2]), .BIT(CLRQ[13]));
  CGA_INTR_CNTLR_CLR_CLRBIT CLRB12 (
    .DCDJ(J), .DCDK(HIK), .DATA(DIN_15_8[4]), .X0(HX_2_0_N[0]), .X1(HX_2_0_N[1]), .X2(HX_2_0[2]),
    .BIT(CLRQ[12]));
  CGA_INTR_CNTLR_CLR_CLRBIT CLRB11 (
    .DCDJ(J), .DCDK(HIK), .DATA(DIN_15_8[3]), .X0(HX_2_0[0]), .X1(HX_2_0[1]), .X2(HX_2_0_N[2]), .BIT(CLRQ[11]));
  CGA_INTR_CNTLR_CLR_CLRBIT CLRB10 (
    .DCDJ(J), .DCDK(HIK), .DATA(DIN_15_8[2]), .X0(HX_2_0_N[0]), .X1(HX_2_0[1]), .X2(HX_2_0_N[2]),
    .BIT(CLRQ[10]));
  CGA_INTR_CNTLR_CLR_CLRBIT CLRB9 (
    .DCDJ(J), .DCDK(HIK), .DATA(DIN_15_8[1]), .X0(HX_2_0[0]), .X1(HX_2_0_N[1]), .X2(HX_2_0_N[2]),
    .BIT(CLRQ[9]));
  CGA_INTR_CNTLR_CLR_CLRBIT CLRB8 (
    .DCDJ(J), .DCDK(HIK), .DATA(DIN_15_8[0]), .X0(HX_2_0_N[0]), .X1(HX_2_0_N[1]), .X2(HX_2_0_N[2]),
    .BIT(CLRQ[8]));

  // Notes on the sheet:
  //   Page 82 - CGA_INTR_CNTLR_CLR
  //   CLRQ7
  //   CLRQ15
endmodule

module CGA_INTR_CNTLR_CLR_CLRBIT (
  input  DCDJ,
  input  DCDK,
  input  DATA,
  input  X0,
  input  X1,
  input  X2,
  output BIT
);

  wire nand_1_out, nand_2_out, nand_3_out;

  nand nand_1 (nand_1_out, DCDJ, DCDK);
  nand nand_2 (nand_2_out, DCDJ, DATA);
  nand nand_3 (nand_3_out, DCDK, X0, X1, X2);
  or or_1 (BIT, ~nand_1_out, ~nand_2_out, ~nand_3_out);  // OR_Gate
endmodule

module CGA_INTR_CNTLR_VECGEN (
  input  [15:0] MIREQ_15_0_N,
  input  MCLK,
  input  N,
  input  HIF,
  input  FIDBO3,
  input  LOF,
  input  G,
  input  FIDBO4,
  input  HIGSN,
  input  [2:0] FIDBO_2_0,
  input  LOGSN,
  input  OESN,
  output HIDET,
  output [2:0] HIVEC_2_0,
  output LODET,
  output [2:0] LOVEC_2_0,
  output [2:0] HX_2_0,
  output [2:0] HX_2_0_N,
  output [2:0] LX_2_0,
  output [2:0] LX_2_0_N,
  output [2:0] PICS_2_0,
  output HIVGES,
  output LOVGES
);

  wire [2:0] ISMUX_hisin_2_0, ISMUX_losin_2_0, STAT_histat_2_0, STAT_lostat_2_0;

  CGA_INTR_CNTLR_VECGEN_PTY PTY (
    .MIREQ_15_0_N(MIREQ_15_0_N), .HIDET(HIDET), .HIVEC(HIVEC_2_0), .LODET(LODET), .LOVEC(LOVEC_2_0));
  CGA_INTR_CNTLR_VECGEN_VHR VHR (
    .HIVEC_2_0(HIVEC_2_0), .LOVEC_2_0(LOVEC_2_0), .MCLK(MCLK), .N(N), .HX_2_0(HX_2_0), .HX_2_0_N(HX_2_0_N),
    .LX_2_0(LX_2_0), .LX_2_0_N(LX_2_0_N));
  CGA_INTR_CNTLR_VECGEN_ISMUX ISMUX (
    .HIGSN(HIGSN), .HISTAT_2_0(STAT_histat_2_0), .FIDBO_2_0(FIDBO_2_0), .LOSTAT_2_0(STAT_lostat_2_0),
    .LOGSN(LOGSN), .OESN(OESN), .HISIN_2_0(ISMUX_hisin_2_0), .LOSIN_2_0(ISMUX_losin_2_0));
  CGA_INTR_CNTLR_VECGEN_CMP CMP (
    .HIVEC_2_0(HIVEC_2_0), .HISTAT_2_0(STAT_histat_2_0), .LOVEC_2_0(LOVEC_2_0), .LOSTAT_2_0(STAT_lostat_2_0),
    .HIVGES(HIVGES), .LOVGES(LOVGES));
  CGA_INTR_CNTLR_VECGEN_STAT STAT (
    .HIVEC_2_0(HIVEC_2_0), .HISIN_2_0(ISMUX_hisin_2_0), .HIF(HIF), .FIDBO3(FIDBO3), .LOVEC_2_0(LOVEC_2_0),
    .LOSIN_2_0(ISMUX_losin_2_0), .LOF(LOF), .G(G), .FIDBO4(FIDBO4), .MCLK(MCLK),
    .HISTAT_2_0(STAT_histat_2_0), .LOSTAT_2_0(STAT_lostat_2_0));
  CGA_INTR_CNTLR_VECGEN_OSMUX OSMUX (
    .HIGSN(HIGSN), .HISTAT_2_0(STAT_histat_2_0), .LOSTAT_2_0(STAT_lostat_2_0), .LOGSN(LOGSN), .OESN(OESN),
    .PICS_2_0(PICS_2_0));

  // Notes on the sheet:
  //   Page 83 - CGA_INTR_CNTLR_VECGEN 
  //   HIGSN
  //   LOGSN
  //   HISTAT
  //   LOSTAT
endmodule

module CGA_INTR_CNTLR_VECGEN_PTY (
  input  [15:0] MIREQ_15_0_N,
  output HIDET,
  output [2:0] HIVEC,
  output LODET,
  output [2:0] LOVEC
);

  CGA_INTR_CNTLR_VECGEN_PTY_PTYENC PTYENC_HI (.RN(MIREQ_15_0_N[15:8]), .DET(HIDET), .V_2_0(HIVEC));
  CGA_INTR_CNTLR_VECGEN_PTY_PTYENC PTYENC_LO (.RN(MIREQ_15_0_N[7:0]), .DET(LODET), .V_2_0(LOVEC));

  // Notes on the sheet:
  //   Page 84 - CGA_INTR_CNTLR_VECGEN_PTY  Completed. Tested manually
endmodule

module CGA_INTR_CNTLR_VECGEN_PTY_PTYENC (
  input  [7:0] RN,
  output DET,
  output [2:0] V_2_0
);

  wire ND2_out, ND3_out, ND4_out, not_1_out, not_2_out, not_3_out, not_4_out, not_5_out, not_6_out,
       not_7_out, NR2_out, NR3_out, NR4_out, NRx_out, O1_out, OR2_out;

  not not_1 (not_1_out, RN[7]);
  not not_2 (not_2_out, RN[6]);
  not not_3 (not_3_out, RN[5]);
  not not_4 (not_4_out, RN[4]);
  not not_5 (not_5_out, RN[3]);
  not not_6 (not_6_out, RN[2]);
  not not_7 (not_7_out, RN[1]);
  or ND8P (DET, ~RN[0], ~RN[1], ~RN[2], ~RN[3], ~RN[4], ~RN[5], ~RN[6], ~RN[7]);  // OR_Gate
  nor NR4 (NR4_out, not_4_out, not_3_out, not_2_out, not_1_out);
  not V2 (V_2_0[2], NR4_out);
  or OR2 (OR2_out, not_1_out, not_2_out);
  nor O1 (O1_out, OR2_out, NR3_out);
  not V1 (V_2_0[1], O1_out);
  nor NR2 (NR2_out, not_5_out, not_6_out);
  and NR3 (NR3_out, ~not_3_out, ~not_4_out, ~NR2_out);  // AND_Gate
  not V0 (V_2_0[0], NRx_out);
  nand ND2 (ND2_out, RN[6], not_3_out);
  nor NRx (NRx_out, ~RN[7], ~ND2_out, ~ND3_out, ~ND4_out);  // NOR_Gate
  nand ND3 (ND3_out, RN[6], RN[4], not_5_out);
  nand ND4 (ND4_out, RN[6], RN[4], RN[2], not_7_out);

  // Notes on the sheet:
  //   R7-0
  //   R7-0N
  //   Page 84 - CGA_INTR_CNTLR_VECGEN_PTY_PTYENC  Completed, tested manually
endmodule

module CGA_INTR_CNTLR_VECGEN_ISMUX (
  input  HIGSN,
  input  [2:0] HISTAT_2_0,
  input  [2:0] FIDBO_2_0,
  input  [2:0] LOSTAT_2_0,
  input  LOGSN,
  input  OESN,
  output [2:0] HISIN_2_0,
  output [2:0] LOSIN_2_0
);

  wire and_1_out, and_2_out, nand_1_out, nand_2_out, nand_3_out, nand_4_out, nand_5_out, nand_6_out,
       nand_7_out, nand_8_out, nand_9_out, nand_10_out, nand_11_out, nand_12_out, not_1_out, not_2_out,
       not_3_out, not_4_out;

  not not_1 (not_1_out, HIGSN);
  not not_2 (not_2_out, OESN);
  and and_1 (and_1_out, not_1_out, not_2_out);
  and and_2 (and_2_out, ~LOGSN, ~OESN);  // AND_Gate
  not not_3 (not_3_out, and_1_out);
  not not_4 (not_4_out, and_2_out);
  nand nand_1 (nand_1_out, HISTAT_2_0[2], and_1_out);
  nand nand_2 (nand_2_out, FIDBO_2_0[2], not_3_out);
  nand nand_3 (nand_3_out, HISTAT_2_0[1], and_1_out);
  nand nand_4 (nand_4_out, FIDBO_2_0[1], not_3_out);
  nand nand_5 (nand_5_out, HISTAT_2_0[0], and_1_out);
  nand nand_6 (nand_6_out, FIDBO_2_0[0], not_3_out);
  nand nand_7 (nand_7_out, LOSTAT_2_0[2], and_2_out);
  nand nand_8 (nand_8_out, FIDBO_2_0[2], not_4_out);
  nand nand_9 (nand_9_out, LOSTAT_2_0[1], and_2_out);
  nand nand_10 (nand_10_out, FIDBO_2_0[1], not_4_out);
  nand nand_11 (nand_11_out, LOSTAT_2_0[0], and_2_out);
  nand nand_12 (nand_12_out, FIDBO_2_0[0], not_4_out);
  or or_1 (HISIN_2_0[2], ~nand_1_out, ~nand_2_out);  // OR_Gate
  or or_2 (HISIN_2_0[1], ~nand_3_out, ~nand_4_out);  // OR_Gate
  or or_3 (HISIN_2_0[0], ~nand_5_out, ~nand_6_out);  // OR_Gate
  or or_4 (LOSIN_2_0[2], ~nand_7_out, ~nand_8_out);  // OR_Gate
  or or_5 (LOSIN_2_0[1], ~nand_9_out, ~nand_10_out);  // OR_Gate
  or or_6 (LOSIN_2_0[0], ~nand_11_out, ~nand_12_out);  // OR_Gate

  // Notes on the sheet:
  //   Page 85 - CGA_INTR_CNTLR_VECGEN_ISMUX  
  //   HISTAT2
  //   FIDBO2
  //   HISTAT1
  //   FIDBO1
  //   HISTAT0
  //   FIDBO0
  //   LOSTAT2
  //   FIDBO2
  //   LOSTAT1
  //   FIDBO1
  //   LOSTAT0
  //   FIDBO0
  //   HISIN2
  //   HISIN1
  //   HISIN0
  //   LOSIN2
  //   LOSIN1
  //   LOSIN0
endmodule

module CGA_INTR_CNTLR_VECGEN_VHR (
  input  [2:0] HIVEC_2_0,
  input  [2:0] LOVEC_2_0,
  input  MCLK,
  input  N,
  output [2:0] HX_2_0,
  output [2:0] HX_2_0_N,
  output [2:0] LX_2_0,
  output [2:0] LX_2_0_N
);

  SCAN_FF HX2 (.D(HIVEC_2_0[2]), .TE(N), .TI(HX_2_0[2]), .CLK(MCLK), .Q(HX_2_0[2]), .QN(HX_2_0_N[2]));
  SCAN_FF HX1 (.D(HIVEC_2_0[1]), .TE(N), .TI(HX_2_0[1]), .CLK(MCLK), .Q(HX_2_0[1]), .QN(HX_2_0_N[1]));
  SCAN_FF HX0 (.D(HIVEC_2_0[0]), .TE(N), .TI(HX_2_0[0]), .CLK(MCLK), .Q(HX_2_0[0]), .QN(HX_2_0_N[0]));
  SCAN_FF LX2 (.D(LOVEC_2_0[2]), .TE(N), .TI(LX_2_0[2]), .CLK(MCLK), .Q(LX_2_0[2]), .QN(LX_2_0_N[2]));
  SCAN_FF LX1 (.D(LOVEC_2_0[1]), .TE(N), .TI(LX_2_0[1]), .CLK(MCLK), .Q(LX_2_0[1]), .QN(LX_2_0_N[1]));
  SCAN_FF LX0 (.D(LOVEC_2_0[0]), .TE(N), .TI(LX_2_0[0]), .CLK(MCLK), .Q(LX_2_0[0]), .QN(LX_2_0_N[0]));

  // Notes on the sheet:
  //   Page 86 - CGA_INTR_CNTLR_VECGEN_VHR  Completed. Tested manually
endmodule

module CGA_INTR_CNTLR_VECGEN_STAT (
  input  [2:0] HIVEC_2_0,
  input  [2:0] HISIN_2_0,
  input  HIF,
  input  FIDBO3,
  input  [2:0] LOVEC_2_0,
  input  [2:0] LOSIN_2_0,
  input  LOF,
  input  G,
  input  FIDBO4,
  input  MCLK,
  output [2:0] HISTAT_2_0,
  output [2:0] LOSTAT_2_0
);

  wire and_1_out, and_2_out, not_1_out, not_2_out, not_3_out, not_4_out, not_5_out, not_6_out, not_7_out,
       not_8_out, not_9_out, not_10_out, not_11_out, xnor_1_out, xnor_2_out, xnor_3_out, xnor_4_out;

  not not_1 (not_1_out, HIF);
  not not_2 (not_2_out, FIDBO3);
  not not_3 (not_3_out, LOF);
  not not_4 (not_4_out, G);
  not not_5 (not_5_out, FIDBO4);
  not not_6 (not_6_out, HIVEC_2_0[2]);
  not not_7 (not_7_out, HIVEC_2_0[1]);
  not not_8 (not_8_out, HIVEC_2_0[0]);
  not not_9 (not_9_out, LOVEC_2_0[2]);
  not not_10 (not_10_out, LOVEC_2_0[1]);
  not not_11 (not_11_out, LOVEC_2_0[0]);
  and and_1 (and_1_out, ~not_7_out, ~not_8_out);  // AND_Gate
  and and_2 (and_2_out, ~not_10_out, ~not_11_out);  // AND_Gate
  xnor xnor_1 (xnor_1_out, not_6_out, and_1_out);
  xnor xnor_2 (xnor_2_out, HIVEC_2_0[1], not_8_out);
  xnor xnor_3 (xnor_3_out, not_9_out, and_2_out);
  xnor xnor_4 (xnor_4_out, LOVEC_2_0[1], not_11_out);
  CGA_INTR_CNTLR_VECGEN_STAT_SBIT SBIT2_HI (
    .SIN(HISIN_2_0[2]), .DCDF(xnor_1_out), .GPE(HIF), .DCDG(not_1_out), .DCDFN(G), .VINN(not_4_out),
    .DCDGN(not_2_out), .CK(MCLK), .STS(HISTAT_2_0[2]));
  CGA_INTR_CNTLR_VECGEN_STAT_SBIT SBIT1_HI (
    .SIN(HISIN_2_0[1]), .DCDF(xnor_2_out), .GPE(HIF), .DCDG(not_1_out), .DCDFN(G), .VINN(not_4_out),
    .DCDGN(not_2_out), .CK(MCLK), .STS(HISTAT_2_0[1]));
  CGA_INTR_CNTLR_VECGEN_STAT_SBIT SBIT0_HI (
    .SIN(HISIN_2_0[0]), .DCDF(not_8_out), .GPE(HIF), .DCDG(not_1_out), .DCDFN(G), .VINN(not_4_out),
    .DCDGN(not_2_out), .CK(MCLK), .STS(HISTAT_2_0[0]));
  CGA_INTR_CNTLR_VECGEN_STAT_SBIT SBIT2_LO (
    .SIN(LOSIN_2_0[2]), .DCDF(xnor_3_out), .GPE(LOF), .DCDG(not_3_out), .DCDFN(G), .VINN(not_4_out),
    .DCDGN(not_5_out), .CK(MCLK), .STS(LOSTAT_2_0[2]));
  CGA_INTR_CNTLR_VECGEN_STAT_SBIT SBIT1_LO (
    .SIN(LOSIN_2_0[1]), .DCDF(xnor_4_out), .GPE(LOF), .DCDG(not_3_out), .DCDFN(G), .VINN(not_4_out),
    .DCDGN(not_5_out), .CK(MCLK), .STS(LOSTAT_2_0[1]));
  CGA_INTR_CNTLR_VECGEN_STAT_SBIT SBIT0_LO (
    .SIN(LOSIN_2_0[0]), .DCDF(not_11_out), .GPE(LOF), .DCDG(not_3_out), .DCDFN(G), .VINN(not_4_out),
    .DCDGN(not_5_out), .CK(MCLK), .STS(LOSTAT_2_0[0]));

  // Notes on the sheet:
  //   Page 87 - CGA_INTR_CNTLR_VECGEN_STAT
  //   HIVEC2
  //   HIVEC1
  //   HIVEC0
  //   HIF
  //   HIFN
  //   HIGE
  //   LOVEC2
  //   LOVEC1
  //   LOVEC0
  //   HIVEC2N
  //   HIVEC1N
  //   HIVEC0N
  //   LOVEC2N
  //   LOVEC1N
  //   LOVEC0N
  //   HIVEC2N
  //   HIVEC1
  //   HIVEC0N
  //   LOVEC1
  //   LOVEC0N
  //   HISIN2
  //   HISIN1
  //   HISIN0
  //   LOSIN2
  //   LOSIN1
  //   LOSIN0
  //   HISTAT2
  //   HISTAT1
  //   HISTAT0
  //   LOSTAT2
  //   LOSTAT1
  //   LOSTAT0
endmodule

module CGA_INTR_CNTLR_VECGEN_STAT_SBIT (
  input  SIN,
  input  DCDF,
  input  GPE,
  input  DCDG,
  input  DCDFN,
  input  VINN,
  input  DCDGN,
  input  CK,
  output STS
);

  wire nand_1_out, nand_2_out, nand_3_out, or_1_out;

  nand nand_1 (nand_1_out, SIN, DCDG, DCDF, GPE);
  nand nand_2 (nand_2_out, DCDG, DCDFN, STS);
  nand nand_3 (nand_3_out, VINN, GPE, DCDGN);
  or or_1 (or_1_out, ~nand_1_out, ~nand_2_out, ~nand_3_out);  // OR_Gate
  D_Flip_Flop d_ff_1 (.D(or_1_out), .clk(CK), .Q(STS));  // open: Qn, preset, reset

  // Notes on the sheet:
  //   Page 87 - CGA_INTR_CNTLR_VECGEN_STAT_SBIT
endmodule

module CGA_INTR_CNTLR_VECGEN_CMP (
  input  [2:0] HIVEC_2_0,
  input  [2:0] HISTAT_2_0,
  input  [2:0] LOVEC_2_0,
  input  [2:0] LOSTAT_2_0,
  output HIVGES,
  output LOVGES
);

  CGA_INTR_CNTLR_VECGEN_CMP_MAGCMP HICMP (.S_2_0(HISTAT_2_0), .V_2_0(HIVEC_2_0), .VGES(HIVGES));
  CGA_INTR_CNTLR_VECGEN_CMP_MAGCMP LOCMP (.S_2_0(LOSTAT_2_0), .V_2_0(LOVEC_2_0), .VGES(LOVGES));

  // Notes on the sheet:
  //   Page 88 - CGA_INTR_CNTLR_VECGEN_CMP
endmodule

module CGA_INTR_CNTLR_VECGEN_CMP_MAGCMP (
  input  [2:0] S_2_0,
  input  [2:0] V_2_0,
  output VGES
);

  wire nand_1_out, nand_2_out, nand_3_out, nand_4_out, nand_5_out, not_1_out, not_2_out, not_3_out,
       not_4_out, not_5_out;

  not not_1 (not_1_out, S_2_0[1]);
  nand nand_1 (nand_1_out, V_2_0[1], not_1_out);
  not not_2 (not_2_out, V_2_0[0]);
  not not_3 (not_3_out, S_2_0[2]);
  nand nand_2 (nand_2_out, V_2_0[2], not_3_out);
  not not_4 (not_4_out, V_2_0[1]);
  not not_5 (not_5_out, V_2_0[2]);
  nand nand_3 (nand_3_out, nand_1_out, S_2_0[0], not_2_out, nand_2_out);
  nand nand_4 (nand_4_out, nand_2_out, not_4_out, S_2_0[1]);
  nand nand_5 (nand_5_out, not_5_out, S_2_0[2]);
  nor nor_1 (VGES, ~nand_3_out, ~nand_4_out, ~nand_5_out);  // NOR_Gate

  // Notes on the sheet:
  //   Page 88 - CGA_INTR_CNTLR_VECGEN_CMP
  //   S1
  //   V1
  //   S0
  //   V0
  //   V2
  //   S2
  //   V1
  //   S1
  //   V2
  //   S2
endmodule

module CGA_INTR_CNTLR_VECGEN_OSMUX (
  input  HIGSN,
  input  [2:0] HISTAT_2_0,
  input  [2:0] LOSTAT_2_0,
  input  LOGSN,
  input  OESN,
  output [2:0] PICS_2_0
);

  wire and_1_out, and_2_out, nand_1_out, nand_2_out, nand_3_out, nand_4_out, nand_5_out, nand_6_out;

  and and_1 (and_1_out, ~HIGSN, ~OESN);  // AND_Gate
  and and_2 (and_2_out, ~OESN, ~LOGSN);  // AND_Gate
  nand nand_1 (nand_1_out, and_1_out, HISTAT_2_0[2]);
  nand nand_2 (nand_2_out, and_2_out, LOSTAT_2_0[2]);
  or or_1 (PICS_2_0[2], ~nand_1_out, ~nand_2_out);  // OR_Gate
  nand nand_3 (nand_3_out, and_1_out, HISTAT_2_0[1]);
  nand nand_4 (nand_4_out, and_2_out, LOSTAT_2_0[1]);
  or or_2 (PICS_2_0[1], ~nand_3_out, ~nand_4_out);  // OR_Gate
  nand nand_5 (nand_5_out, and_1_out, HISTAT_2_0[0]);
  nand nand_6 (nand_6_out, and_2_out, LOSTAT_2_0[0]);
  or or_3 (PICS_2_0[0], ~nand_5_out, ~nand_6_out);  // OR_Gate

  // Notes on the sheet:
  //   HI
  //   Page 89 - CGA_INTR_CNTLR_VECGEN_OSMUX
  //   LO
  //   PICS2
  //   PICS1
  //   PICS0
endmodule

module CGA_INTR_CNTLR_IRGEL (
  input  FIDB03,
  input  HIDET,
  input  HIVGES,
  input  E,
  input  MCLK,
  input  D,
  input  S,
  input  H,
  input  [2:0] HIVEC_2_0,
  input  [2:0] LOVEC_2_0,
  input  LODET,
  input  LOVGES,
  input  N,
  input  L,
  input  FIDB04,
  input  M,
  output HIGSN,
  output PD,
  output HIPASSALL,
  output [2:0] PICV_2_0,
  output IRQN,
  output LOPASSALL,
  output LOGSN
);

  wire HIRL_hienabn, HIRL_higas, HIRL_hirq, HIRL_hve, HIRL_rdn, LORL_lienabn, LORL_lirq, LORL_logas,
       LORL_logasn, LORL_lve;

  CGA_INTR_CNTLR_IRGEL_HIRL HIRL (
    .HIGSN(HIGSN), .HIDET(HIDET), .HIVGES(HIVGES), .E(E), .MCLK(MCLK), .D(D), .S(S), .HIVEC_2_0(HIVEC_2_0),
    .H(H), .RDN(HIRL_rdn), .PD(PD), .HIPASSALL(HIPASSALL), .HIRQ(HIRL_hirq), .HVE(HIRL_hve),
    .HIGAS(HIRL_higas), .HIENABN(HIRL_hienabn));
  CGA_INTR_CNTLR_IRGEL_LORL LORL (
    .RDN(HIRL_rdn), .LODET(LODET), .LOVGES(LOVGES), .E(E), .MCLK(MCLK), .D(D), .S(S), .LOVEC_2_0(LOVEC_2_0),
    .LIENABN(LORL_lienabn), .LOPASSALL(LOPASSALL), .LIRQ(LORL_lirq), .LVE(LORL_lve), .LOGAS(LORL_logas),
    .LOGASN(LORL_logasn));
  CGA_INTR_CNTLR_IRGEL_HIGEL HIGEL (
    .FIDB03(FIDB03), .LOGASN(LORL_logasn), .HIDET(HIDET), .HIGAS(HIRL_higas), .HIENABN(HIRL_hienabn),
    .MCLK(MCLK), .N(N), .L(L), .M(M), .HIGSN(HIGSN));
  CGA_INTR_CNTLR_IRGEL_VMUX VMUX (
    .HIVEC_2_0(HIVEC_2_0), .LOVEC_2_0(LOVEC_2_0), .LVE(LORL_lve), .HVE(HIRL_hve), .PICV_2_0(PICV_2_0));
  CGA_INTR_CNTLR_IRGEL_LOGEL LOGEL (
    .FIDB04(FIDB04), .LOGAS(LORL_logas), .LIENABN(LORL_lienabn), .MCLK(MCLK), .N(N), .L(L), .M(M),
    .LOGSN(LOGSN));
  nor nor_1 (IRQN, HIRL_hirq, LORL_lirq);

  // Notes on the sheet:
  //   Page 90 - CGA_INTR_CNTLR_IRGEL
endmodule

module CGA_INTR_CNTLR_IRGEL_HIRL (
  input  HIGSN,
  input  HIDET,
  input  HIVGES,
  input  E,
  input  MCLK,
  input  D,
  input  S,
  input  [2:0] HIVEC_2_0,
  input  H,
  output RDN,
  output PD,
  output HIPASSALL,
  output HIRQ,
  output HVE,
  output HIGAS,
  output HIENABN
);

  wire HIDISN, INT_REQ_ENABLE_FF_q, INT_REQ_ENABLE_FF_qn, nand_1_out, nand_2_out, nand_3_out;

  nand nand_1 (nand_1_out, HIDET, HIVGES);
  nand nand_2 (nand_2_out, HIVGES, HIDET, HIDISN);
  nor nor_1 (RDN, ~HIDISN, ~HIGSN, ~nand_1_out);  // NOR_Gate
  or or_1 (PD, ~HIGSN, ~nand_1_out);  // OR_Gate
  SCAN_FF INT_REQ_ENABLE_FF (
    .D(E), .TE(D), .TI(INT_REQ_ENABLE_FF_q), .CLK(MCLK), .Q(INT_REQ_ENABLE_FF_q), .QN(INT_REQ_ENABLE_FF_qn));
  not not_1 (HIPASSALL, nand_2_out);
  and and_1 (HIRQ, ~nand_2_out, ~INT_REQ_ENABLE_FF_qn);  // AND_Gate
  and and_2 (HVE, ~nand_2_out, ~S);  // AND_Gate
  nand nand_3 (nand_3_out, HVE, HIVEC_2_0[2], HIVEC_2_0[1], HIVEC_2_0[0]);
  not not_2 (HIGAS, nand_3_out);
  SCAN_FF STATUS_OVERFLOW_FF (.D(HIDISN), .TE(H), .TI(nand_3_out), .CLK(MCLK), .Q(HIDISN), .QN(HIENABN));

  // Notes on the sheet:
  //   Page 91 - CGA_INTR_CNTLR_IRGEL_HIGEL
endmodule

module CGA_INTR_CNTLR_IRGEL_LORL (
  input  RDN,
  input  LODET,
  input  LOVGES,
  input  E,
  input  MCLK,
  input  D,
  input  S,
  input  [2:0] LOVEC_2_0,
  output LIENABN,
  output LOPASSALL,
  output LIRQ,
  output LVE,
  output LOGAS,
  output LOGASN
);

  wire INT_REQ_ENABLE_FF_q, INT_REQ_ENABLE_FF_qn, nand_1_out;

  nand nand_1 (nand_1_out, RDN, LODET, LOVGES);
  SCAN_FF INT_REQ_ENABLE_FF (
    .D(E), .TE(D), .TI(INT_REQ_ENABLE_FF_q), .CLK(MCLK), .Q(INT_REQ_ENABLE_FF_q), .QN(INT_REQ_ENABLE_FF_qn));
  and and_1 (LIRQ, ~nand_1_out, ~INT_REQ_ENABLE_FF_qn);  // AND_Gate
  and and_2 (LVE, ~nand_1_out, ~S);  // AND_Gate
  not not_1 (LIENABN, RDN);
  not not_2 (LOPASSALL, nand_1_out);
  nand nand_2 (LOGASN, LVE, LOVEC_2_0[2], LOVEC_2_0[1], LOVEC_2_0[0]);
  not not_3 (LOGAS, LOGASN);

  // Notes on the sheet:
  //   Page 92 - CGA_INTR_CNTLR_IRGEL_LOGEL  
endmodule

module CGA_INTR_CNTLR_IRGEL_HIGEL (
  input  FIDB03,
  input  LOGASN,
  input  HIDET,
  input  HIGAS,
  input  HIENABN,
  input  MCLK,
  input  N,
  input  L,
  input  M,
  output HIGSN
);

  wire nand_1_out, nand_2_out, nand_3_out, nand_4_out, nand_5_out, nand_6_out, not_1_out, not_2_out,
       not_3_out, or_1_out;

  not not_1 (not_1_out, HIDET);
  not not_2 (not_2_out, L);
  not not_3 (not_3_out, M);
  nand nand_1 (nand_1_out, FIDB03, L, M);
  nand nand_2 (nand_2_out, LOGASN, L, not_3_out);
  nand nand_3 (nand_3_out, LOGASN, not_1_out, N);
  nand nand_4 (nand_4_out, HIGAS, N);
  nand nand_5 (nand_5_out, HIENABN, N);
  nand nand_6 (nand_6_out, not_2_out, M, HIGSN);
  or or_1 (or_1_out, ~nand_1_out, ~nand_2_out, ~nand_3_out, ~nand_4_out, ~nand_5_out, ~nand_6_out);  // OR_Gate
  D_Flip_Flop d_ff_1 (.D(or_1_out), .clk(MCLK), .Q(HIGSN));  // open: Qn, preset, reset

  // Notes on the sheet:
  //   Page 93 - CGA_INTR_CNTLR_IRGEL_LOGEL  
endmodule

module CGA_INTR_CNTLR_IRGEL_LOGEL (
  input  FIDB04,
  input  LOGAS,
  input  LIENABN,
  input  MCLK,
  input  N,
  input  L,
  input  M,
  output LOGSN
);

  wire nand_1_out, nand_2_out, nand_3_out, nand_4_out, not_1_out, or_1_out;

  not not_1 (not_1_out, L);
  nand nand_1 (nand_1_out, FIDB04, L, M);
  nand nand_2 (nand_2_out, LOGAS, N);
  nand nand_3 (nand_3_out, LIENABN, N);
  nand nand_4 (nand_4_out, not_1_out, M, LOGSN);
  or or_1 (or_1_out, ~nand_1_out, ~nand_2_out, ~nand_3_out, ~nand_4_out);  // OR_Gate
  D_Flip_Flop d_ff_1 (.D(or_1_out), .clk(MCLK), .Q(LOGSN));  // open: Qn, preset, reset

  // Notes on the sheet:
  //   Page 94 - CGA_INTR_CNTLR_IRGEL_LOGEL  
endmodule

module CGA_INTR_CNTLR_IRGEL_VMUX (
  input  [2:0] HIVEC_2_0,
  input  [2:0] LOVEC_2_0,
  input  LVE,
  input  HVE,
  output [2:0] PICV_2_0
);

  wire nand_1_out, nand_2_out, nand_3_out, nand_4_out, nand_5_out, nand_6_out;

  nand nand_1 (nand_1_out, HIVEC_2_0[2], HVE);
  nand nand_2 (nand_2_out, LOVEC_2_0[2], LVE);
  or or_1 (PICV_2_0[2], ~nand_1_out, ~nand_2_out);  // OR_Gate
  nand nand_3 (nand_3_out, HIVEC_2_0[1], HVE);
  nand nand_4 (nand_4_out, LOVEC_2_0[1], LVE);
  or or_2 (PICV_2_0[1], ~nand_3_out, ~nand_4_out);  // OR_Gate
  nand nand_5 (nand_5_out, HIVEC_2_0[0], HVE);
  nand nand_6 (nand_6_out, LOVEC_2_0[0], LVE);
  or or_3 (PICV_2_0[0], ~nand_5_out, ~nand_6_out);  // OR_Gate

  // Notes on the sheet:
  //   Page 95 - CGA_INTR_CNTLR_IRGEL_VMUX 
  //   PICV2
  //   PICV1
  //   PICV0
endmodule

module CGA_INTR_CNTLR_MDCD (
  input  [3:0] LAA_3_0,
  input  EPIC,
  input  HIPASSALL,
  input  LOPASSALL,
  input  MCLK,
  output OESN,
  output E,
  output J,
  output D,
  output N,
  output HIK,
  output A,
  output HIF,
  output G,
  output H,
  output L,
  output B,
  output S,
  output M,
  output LOF,
  output C,
  output LOK,
  output OEM,
  output EPICMASKN
);

  wire and_1_out, and_2_out, and_3_out, and_4_out, and_5_out, and_6_out, and_7_out, and_8_out, and_9_out,
       d_ff_1_q, d_ff_2_q, GLP_HI_z0, GLP_HI_z1, GLP_HI_z2, GLP_HI_z3, GLP_HI_z4, GLP_HI_z5, GLP_HI_z6,
       GLP_HI_z7, GLP_LO_z0, GLP_LO_z1, GLP_LO_z2, GLP_LO_z3, GLP_LO_z4, GLP_LO_z5, GLP_LO_z6, GLP_LO_z7,
       HIVCEN, LOVCEN, nand_1_out, nand_5_out, nand_6_out, nand_7_out, nand_8_out, nand_9_out, nand_11_out,
       nor_1_out, nor_2_out, nor_3_out, nor_4_out, not_1_out, not_2_out, not_3_out, not_4_out, not_15_out,
       or_1_out, or_2_out, or_3_out, or_4_out, or_5_out, or_6_out, or_7_out, or_8_out, or_9_out, or_10_out,
       or_11_out, or_12_out, or_13_out, R;

  not not_1 (not_1_out, EPIC);
  not not_2 (not_2_out, HIPASSALL);
  not not_3 (not_3_out, LOPASSALL);
  not not_4 (not_4_out, LAA_3_0[3]);
  ND38GLP GLP_LO (
    .A(LAA_3_0[0]), .B(LAA_3_0[1]), .C(LAA_3_0[2]), .G(not_4_out), .Z0(GLP_LO_z0), .Z1(GLP_LO_z1),
    .Z2(GLP_LO_z2), .Z3(GLP_LO_z3), .Z4(GLP_LO_z4), .Z5(GLP_LO_z5), .Z6(GLP_LO_z6), .Z7(GLP_LO_z7));
  ND38GLP GLP_HI (
    .A(LAA_3_0[0]), .B(LAA_3_0[1]), .C(LAA_3_0[2]), .G(LAA_3_0[3]), .Z0(GLP_HI_z0), .Z1(GLP_HI_z1),
    .Z2(GLP_HI_z2), .Z3(GLP_HI_z3), .Z4(GLP_HI_z4), .Z5(GLP_HI_z5), .Z6(GLP_HI_z6), .Z7(GLP_HI_z7));
  or or_1 (or_1_out, ~GLP_LO_z0, ~GLP_HI_z0, ~GLP_HI_z2, ~GLP_HI_z4, ~GLP_HI_z6);  // OR_Gate
  or or_2 (or_2_out, ~GLP_HI_z6, ~GLP_HI_z3, ~GLP_HI_z2);  // OR_Gate
  or or_3 (or_3_out, ~GLP_HI_z0, ~GLP_HI_z2);  // OR_Gate
  or or_4 (or_4_out, ~GLP_LO_z3, ~GLP_LO_z7);  // OR_Gate
  and and_1 (and_1_out, or_1_out, EPIC);
  nand nand_1 (nand_1_out, or_2_out, EPIC);
  nand nand_2 (C, or_3_out, EPIC);
  nand nand_3 (EPICMASKN, or_4_out, EPIC);
  not not_5 (A, and_1_out);
  not not_6 (B, nand_1_out);
  not not_7 (OEM, EPICMASKN);
  nand nand_4 (OESN, ~GLP_LO_z6, ~not_1_out);  // NAND_Gate
  and and_2 (and_2_out, ~GLP_LO_z5, ~not_2_out, ~not_1_out);  // AND_Gate
  and and_3 (and_3_out, ~GLP_HI_z1, ~not_1_out);  // AND_Gate
  and and_4 (and_4_out, ~GLP_LO_z5, ~not_3_out, ~not_1_out);  // AND_Gate
  nand nand_5 (nand_5_out, d_ff_1_q, R);
  nand nand_6 (nand_6_out, LOPASSALL, N);
  nor nor_1 (nor_1_out, and_2_out, and_3_out);
  not not_8 (HIF, nor_1_out);
  nor nor_2 (nor_2_out, and_3_out, and_4_out);
  not not_9 (LOF, nor_2_out);
  nand nand_7 (nand_7_out, d_ff_2_q, R);
  nand nand_8 (nand_8_out, HIPASSALL, N);
  or or_5 (or_5_out, ~nand_5_out, ~nand_6_out);  // OR_Gate
  or or_6 (or_6_out, ~nand_7_out, ~nand_8_out);  // OR_Gate
  D_Flip_Flop d_ff_1 (.D(or_5_out), .clk(MCLK), .Q(d_ff_1_q), .Qn(LOVCEN));  // open: preset, reset
  D_Flip_Flop d_ff_2 (.D(or_6_out), .clk(MCLK), .Q(d_ff_2_q), .Qn(HIVCEN));  // open: preset, reset
  or or_7 (or_7_out, ~GLP_LO_z0, ~GLP_LO_z5);  // OR_Gate
  or or_8 (or_8_out, ~GLP_LO_z0, ~GLP_HI_z1);  // OR_Gate
  or or_9 (or_9_out, ~GLP_LO_z0, ~GLP_LO_z5);  // OR_Gate
  and and_5 (and_5_out, or_7_out, EPIC);
  nand nand_9 (nand_9_out, or_8_out, EPIC);
  nand nand_10 (M, or_9_out, EPIC);
  not not_10 (G, and_5_out);
  not not_11 (L, nand_9_out);
  or or_10 (or_10_out, ~GLP_LO_z0, ~GLP_LO_z1, ~GLP_LO_z2, ~GLP_LO_z3);  // OR_Gate
  nand nand_11 (nand_11_out, or_10_out, EPIC);
  not not_12 (J, nand_11_out);
  and and_6 (and_6_out, ~GLP_LO_z4, ~not_1_out, ~HIVCEN);  // AND_Gate
  and and_7 (and_7_out, ~GLP_LO_z0, ~not_1_out);  // AND_Gate
  and and_8 (and_8_out, ~GLP_LO_z1, ~not_1_out);  // AND_Gate
  and and_9 (and_9_out, ~GLP_LO_z4, ~not_1_out, ~LOVCEN);  // AND_Gate
  nor nor_3 (nor_3_out, and_6_out, and_7_out, and_8_out);
  nor nor_4 (nor_4_out, and_8_out, and_7_out, and_9_out);
  not not_13 (HIK, nor_3_out);
  not not_14 (LOK, nor_4_out);
  or or_11 (or_11_out, ~GLP_LO_z0, ~GLP_HI_z5, ~GLP_HI_z7);  // OR_Gate
  nand nand_12 (D, or_11_out, EPIC);
  nand nand_13 (S, ~GLP_LO_z5, ~not_1_out);  // NAND_Gate
  not not_15 (not_15_out, GLP_HI_z5);
  not not_16 (N, S);
  not not_17 (E, not_15_out);
  or or_12 (or_12_out, ~GLP_LO_z0, ~GLP_LO_z1, ~GLP_LO_z4, ~GLP_LO_z5);  // OR_Gate
  or or_13 (or_13_out, ~GLP_LO_z0, ~GLP_LO_z5, ~GLP_HI_z1);  // OR_Gate
  nand nand_14 (R, or_12_out, EPIC);
  and and_10 (H, or_13_out, EPIC);

  // Notes on the sheet:
  //   EPICN
  //   HIPASSALLN
  //   LOPASSALLN
  //   Page 96 - CGA_INTR_CNTLR_MDCD
  //   D0N
  //   D1N
  //   D2N
  //   D3N
  //   D4N
  //   D5N
  //   D6N
  //   D7N
  //   D8N
  //   D9N
  //   D10N
  //   D11N
  //   D12N
  //   D13N
  //   D14N
  //   D15N
  //   D6N
  //   D5N
  //   EPICN
  //   VECTOR CLEAR ENABLE FLIP-FLOPS
  //   D9N
  //   D5N
  //   D0N
  //   D5N
  //   D0N
  //   D9N
  //   D0N
  //   D5N
  //   D0N-D3N
  //   D4N
  //   D0N
  //   D1N
  //   D4N
  //   D13N
  //   D15N
  //   D0N
  //   D5N
  //   D13N
  //   D1N
  //   D4N
  //   D5N
  //   D0N
  //   D9N
endmodule

module CGA_MAC (
  input  MCLK,
  input  PTM,
  input  [15:0] FIDBO_15_0,
  input  PONI,
  input  [1:0] CMIS_1_0,
  input  [4:0] CSCOMM_4_0,
  input  WR3,
  input  WR7,
  input  ILCSN,
  input  DOUBLE,
  input  CSMREQ,
  input  [15:0] CD_15_0,
  input  [15:0] RB_15_0,
  input  [15:0] XR_15_0,
  input  [15:0] BR_15_0,
  input  [15:0] PR_15_0,
  output VEX,
  output [15:0] PCR_15_0,
  output [13:0] LA_23_10,
  output LSHADOW,
  output ECCR,
  output [9:0] MCA_9_0,
  output [15:0] NLCA_15_0
);

  wire MAC_DECODE_addsel, MAC_DECODE_cds, MAC_DECODE_cdsel, MAC_DECODE_exmn, MAC_DECODE_hold,
       MAC_DECODE_lldexm, MAC_DECODE_lldpcr, MAC_DECODE_lldseg, MAC_DECODE_nlcasel, MAC_DECODE_pb,
       MAC_DECODE_plca, MAC_DECODE_prb, MAC_DECODE_psel, MAC_DECODE_px, MAC_DECODE_sapt, MAC_DECODE_sptn,
       MAC_LA1025_eccrhin, MAC_LASEL_a10, MAC_LASEL_a1617, MAC_LASEL_a1619, MAC_LASEL_a1819, MAC_LASEL_b1819,
       MAC_LASEL_b1821, MAC_LASEL_bb10, MAC_LASEL_c10, MAC_LASEL_d1617, MAC_LASEL_e1617, MAC_LASEL_f1617,
       MAC_PTSEL_selptn, MAC_SEGPT_pex, MAC_SEGPT_segzn, not_1_out, not_2_out;
  wire [1:0] MAC_SEGPT_xpt_1_0;
  wire [7:0] MAC_SEGPT_seg_7_0;
  wire [15:0] MAC_ADD_add_15_0, MAC_AP09_ica_15_0, MAC_AP09_lca_15_0, MAC_SEGPT_pcr_14_13_10_9_n;

  not not_1 (not_1_out, ILCSN);
  not not_2 (not_2_out, not_1_out);
  CGA_MAC_DECODE MAC_DECODE (
    .LCSN(not_2_out), .CSCOMM_4_0(CSCOMM_4_0), .CSMIS_1_0(CMIS_1_0), .WR3(WR3), .MCLK(MCLK), .WR7(WR7),
    .EXMN(MAC_DECODE_exmn), .PB(MAC_DECODE_pb), .PX(MAC_DECODE_px), .PRB(MAC_DECODE_prb),
    .PLCA(MAC_DECODE_plca), .CDSEL(MAC_DECODE_cdsel), .LLDEXM(MAC_DECODE_lldexm), .LLDSEG(MAC_DECODE_lldseg),
    .LLDPCR(MAC_DECODE_lldpcr), .NLCASEL(MAC_DECODE_nlcasel), .ADDSEL(MAC_DECODE_addsel),
    .CDS(MAC_DECODE_cds), .SPTN(MAC_DECODE_sptn), .SAPT(MAC_DECODE_sapt), .PSEL(MAC_DECODE_psel),
    .HOLD(MAC_DECODE_hold));
  CGA_MAC_ADD MAC_ADD (
    .CD_15_0(CD_15_0), .CDS(MAC_DECODE_cds), .PRB(MAC_DECODE_prb), .PB(MAC_DECODE_pb), .PX(MAC_DECODE_px),
    .PLCA(MAC_DECODE_plca), .RB_15_0(RB_15_0), .BR_15_0(BR_15_0), .XR_15_0(XR_15_0),
    .LCA_15_0(MAC_AP09_lca_15_0), .ADD_15_0(MAC_ADD_add_15_0));
  CGA_MAC_AP09 MAC_AP09 (
    .PSEL(MAC_DECODE_psel), .ADDSEL(MAC_DECODE_addsel), .CDSEL(MAC_DECODE_cdsel),
    .NLCASEL(MAC_DECODE_nlcasel), .HOLD(MAC_DECODE_hold), .PR_15_0(PR_15_0), .ADD_15_0(MAC_ADD_add_15_0),
    .CD_15_0(CD_15_0), .ECCRHIN(MAC_LA1025_eccrhin), .MCLK(MCLK), .ICA_15_0(MAC_AP09_ica_15_0), .ECCR(ECCR),
    .MCA_9_0(MCA_9_0), .LCA_15_0(MAC_AP09_lca_15_0), .NLCA_15_0(NLCA_15_0));
  CGA_MAC_SEGPT MAC_SEGPT (
    .FIDBO_15_0(FIDBO_15_0), .MCLK(MCLK), .LLDSEG(MAC_DECODE_lldseg), .LLDPCR(MAC_DECODE_lldpcr),
    .LLDEXM(MAC_DECODE_lldexm), .EXMN(MAC_DECODE_exmn), .SEG_7_0(MAC_SEGPT_seg_7_0), .SEGZN(MAC_SEGPT_segzn),
    .PCR_15_7_2_0(PCR_15_0), .PCR_14_13_10_9_N(MAC_SEGPT_pcr_14_13_10_9_n), .XPT_1_0(MAC_SEGPT_xpt_1_0),
    .VEX(VEX), .PEX(MAC_SEGPT_pex));
  CGA_MAC_PTSEL MAC_PTSEL (
    .SPTN(MAC_DECODE_sptn), .SAPT(MAC_DECODE_sapt), .PONI(PONI), .PTM(PTM), .MCLK(MCLK),
    .SELPTN(MAC_PTSEL_selptn));
  CGA_MAC_LASEL MAC_LASEL (
    .DOUBLE(DOUBLE), .PCR_15_7_2_0(PCR_15_0), .ICA_15_8(MAC_AP09_ica_15_0), .CSMREQ(CSMREQ), .VEX(VEX),
    .PONI(PONI), .PEX(MAC_SEGPT_pex), .SEGZN(MAC_SEGPT_segzn), .EXMN(MAC_DECODE_exmn),
    .SELPTN(MAC_PTSEL_selptn), .MCLK(MCLK), .A10(MAC_LASEL_a10), .BB10(MAC_LASEL_bb10), .C10(MAC_LASEL_c10),
    .A1617(MAC_LASEL_a1617), .D1617(MAC_LASEL_d1617), .E1617(MAC_LASEL_e1617), .F1617(MAC_LASEL_f1617),
    .A1819(MAC_LASEL_a1819), .B1821(MAC_LASEL_b1821), .B1819(MAC_LASEL_b1819), .A1619(MAC_LASEL_a1619),
    .LSHADOW(LSHADOW));
  CGA_MAC_LA1025 MAC_LA1025 (
    .ICA_15_0(MAC_AP09_ica_15_0), .A10(MAC_LASEL_a10), .BB10(MAC_LASEL_bb10), .C10(MAC_LASEL_c10),
    .A1617(MAC_LASEL_a1617), .D1617(MAC_LASEL_d1617), .E1617(MAC_LASEL_e1617), .F1617(MAC_LASEL_f1617),
    .A1819(MAC_LASEL_a1819), .B1821(MAC_LASEL_b1821), .B1819(MAC_LASEL_b1819), .A1619(MAC_LASEL_a1619),
    .SEG_7_0(MAC_SEGPT_seg_7_0), .PCR_15_0(PCR_15_0), .PCR_15_0_N(MAC_SEGPT_pcr_14_13_10_9_n),
    .XPT_1_0(MAC_SEGPT_xpt_1_0), .MCLK(MCLK), .ECCRHIN(MAC_LA1025_eccrhin), .LA_23_10(LA_23_10));

  // Notes on the sheet:
  //   Page 24 - CGA_MAC
  //   PCR_15_7_2_0
endmodule

module CGA_MAC_DECODE (
  input  LCSN,
  input  [4:0] CSCOMM_4_0,
  input  [1:0] CSMIS_1_0,
  input  WR3,
  input  MCLK,
  input  WR7,
  output EXMN,
  output PB,
  output PX,
  output PRB,
  output PLCA,
  output CDSEL,
  output LLDEXM,
  output LLDSEG,
  output LLDPCR,
  output NLCASEL,
  output ADDSEL,
  output CDS,
  output SPTN,
  output SAPT,
  output PSEL,
  output HOLD
);

  wire LDEXMN, LDPCRN, LDSEGN, nand_1_out, nand_3_out, nand_4_out, nand_6_out, nand_7_out, nand_8_out,
       nand_9_out, nand_10_out, nand_11_out, nand_12_out, nand_13_out, nand_14_out, nand_15_out, nand_16_out,
       nand_18_out, nand_19_out, nand_20_out, nand_21_out, nand_22_out, nand_23_out, nand_24_out,
       nand_25_out, nand_26_out, nand_27_out, nand_28_out, nand_29_out, nand_30_out, nand_31_out,
       nand_32_out, nand_33_out, nand_34_out, nand_35_out, nand_36_out, nand_37_out, nand_38_out,
       nand_39_out, nand_40_out, nand_41_out, nand_42_out, nand_43_out, nand_45_out, nand_46_out,
       nand_47_out, nand_48_out, nand_49_out, nand_50_out, nand_51_out, nand_52_out, nand_53_out,
       nand_54_out, nor_1_out, nor_2_out, nor_3_out, not_3_out, not_4_out, not_5_out, not_6_out, not_7_out,
       not_8_out, not_9_out, not_10_out, not_11_out, not_12_out, not_13_out, not_14_out, not_15_out,
       not_16_out, WR3N, WR7N;

  not not_1 (WR3N, WR3);
  not not_2 (WR7N, WR7);
  not not_3 (not_3_out, CSCOMM_4_0[0]);
  not not_4 (not_4_out, CSCOMM_4_0[1]);
  not not_5 (not_5_out, CSCOMM_4_0[2]);
  not not_6 (not_6_out, CSCOMM_4_0[3]);
  not not_7 (not_7_out, CSCOMM_4_0[4]);
  not not_8 (not_8_out, CSMIS_1_0[0]);
  not not_9 (not_9_out, CSMIS_1_0[1]);
  not not_10 (not_10_out, not_3_out);
  not not_11 (not_11_out, not_4_out);
  not not_12 (not_12_out, not_5_out);
  not not_13 (not_13_out, not_6_out);
  not not_14 (not_14_out, not_7_out);
  not not_15 (not_15_out, not_8_out);
  not not_16 (not_16_out, not_9_out);
  nand nand_1 (nand_1_out, not_6_out, not_5_out, not_4_out);
  nand nand_2 (LDPCRN, LCSN, not_7_out, not_6_out, not_12_out, not_11_out, not_3_out, not_16_out, not_15_out);
  nand nand_3 (nand_3_out, not_13_out, not_12_out, not_11_out);
  nand nand_4 (nand_4_out, not_5_out, not_9_out, not_15_out);
  nand nand_5 (SPTN, nand_1_out, nand_3_out, not_14_out, nand_4_out, nand_7_out, nand_8_out, nand_9_out, nand_10_out);
  nand nand_6 (nand_6_out, WR3N, not_15_out, not_9_out, not_3_out);
  nand nand_7 (nand_7_out, not_5_out, not_10_out, not_16_out, not_8_out);
  not not_17 (PB, nand_6_out);
  nand nand_8 (nand_8_out, not_13_out, not_16_out);
  nand nand_9 (nand_9_out, not_13_out, not_5_out, not_10_out);
  nand nand_10 (nand_10_out, not_13_out, not_9_out, not_7_out);
  nand nand_11 (nand_11_out, not_6_out, not_5_out, not_10_out);
  nand nand_12 (nand_12_out, not_3_out, not_9_out);
  nand nand_13 (nand_13_out, WR7N, not_15_out, nand_11_out, nand_12_out);
  nand nand_14 (nand_14_out, not_15_out, not_14_out, not_9_out, not_3_out, not_11_out, not_5_out);
  not not_18 (PX, nand_13_out);
  nand nand_15 (nand_15_out, not_15_out, not_14_out, not_9_out, not_4_out, not_12_out, not_13_out);
  nand nand_16 (nand_16_out, not_9_out, not_10_out, not_5_out, not_13_out, not_14_out);
  nand nand_17 (SAPT, nand_14_out, nand_15_out, nand_16_out, nand_19_out, nand_21_out);
  nand nand_18 (nand_18_out, nand_11_out, nand_12_out, WR7, not_15_out);
  nor nor_1 (nor_1_out, ~nand_18_out, ~nand_20_out, ~nand_22_out, ~nand_23_out);  // NOR_Gate
  nand nand_19 (nand_19_out, not_16_out, not_3_out, not_5_out, not_13_out, not_14_out);
  nand nand_20 (nand_20_out, WR3, not_15_out, not_9_out, not_3_out);
  not not_19 (PRB, nor_1_out);
  nand nand_21 (nand_21_out, not_15_out, not_3_out, not_5_out, not_13_out, not_14_out);
  nand nand_22 (nand_22_out, not_10_out, not_12_out, not_8_out);
  nand nand_23 (nand_23_out, not_10_out, not_13_out, not_8_out);
  nand nand_24 (nand_24_out, not_6_out, not_4_out);
  nand nand_25 (nand_25_out, not_8_out, not_16_out, not_3_out, not_11_out, not_12_out, not_14_out);
  nand nand_26 (nand_26_out, not_13_out, not_12_out);
  nand nand_27 (nand_27_out, not_8_out, not_16_out, not_3_out, not_13_out, not_14_out);
  nand nand_28 (nand_28_out, not_6_out, not_5_out, not_16_out, not_3_out);
  nor nor_2 (nor_2_out, ~nand_25_out, ~nand_27_out, ~nand_29_out, ~nand_32_out);  // NOR_Gate
  nand nand_29 (nand_29_out, not_14_out, not_4_out, not_5_out, not_6_out);
  not not_20 (CDSEL, nor_2_out);
  nand nand_30 (nand_30_out, not_8_out, not_12_out, not_11_out, not_16_out);
  nand nand_31 (nand_31_out, nand_24_out, not_14_out, nand_26_out, nand_28_out, nand_30_out, nand_33_out, nand_34_out, nand_35_out);
  nand nand_32 (nand_32_out, not_14_out, not_12_out, not_13_out);
  nand nand_33 (nand_33_out, not_13_out, not_3_out, not_16_out, not_8_out);
  not not_21 (ADDSEL, nand_31_out);
  nand nand_34 (nand_34_out, not_13_out, not_10_out, not_16_out);
  nand nand_35 (nand_35_out, not_12_out, not_11_out, not_10_out, not_16_out);
  nand nand_36 (nand_36_out, not_13_out, not_10_out, not_5_out, not_16_out, not_14_out, nand_37_out);
  not not_22 (NLCASEL, nand_36_out);
  nand nand_37 (nand_37_out, not_16_out, not_8_out, not_11_out);
  nand nand_38 (nand_38_out, not_16_out, not_15_out);
  nand nand_39 (nand_39_out, not_5_out, not_11_out, not_16_out, nand_38_out, nand_40_out, nand_41_out);
  nor nor_3 (nor_3_out, ~not_14_out, ~nand_39_out);  // NOR_Gate
  not not_23 (HOLD, nor_3_out);
  nand nand_40 (nand_40_out, not_6_out, not_10_out, not_16_out);
  nand nand_41 (nand_41_out, not_13_out, not_3_out, not_16_out);
  nand nand_42 (nand_42_out, not_15_out, not_10_out, not_13_out);
  nand nand_43 (nand_43_out, not_15_out, not_10_out, not_12_out, not_6_out);
  nor nor_4 (CDS, ~nand_42_out, ~nand_43_out);  // NOR_Gate
  nand nand_44 (EXMN, not_15_out, not_16_out, not_4_out, not_12_out, not_13_out, not_14_out);
  nand nand_45 (nand_45_out, not_15_out, not_3_out);
  nand nand_46 (nand_46_out, not_13_out, not_10_out);
  nand nand_47 (nand_47_out, nand_45_out, nand_46_out, nand_49_out);
  nand nand_48 (nand_48_out, not_5_out, not_4_out);
  nand nand_49 (nand_49_out, not_12_out, not_10_out);
  not not_24 (PLCA, nand_47_out);
  nand nand_50 (nand_50_out, not_5_out, not_11_out, not_10_out);
  nand nand_51 (nand_51_out, not_9_out, not_11_out);
  nand nand_52 (nand_52_out, not_5_out, not_16_out, not_8_out);
  nand nand_53 (nand_53_out, nand_48_out, nand_50_out, nand_51_out, not_6_out, nand_52_out, nand_54_out, not_14_out);
  nand nand_54 (nand_54_out, not_12_out, not_11_out, not_3_out);
  not not_25 (PSEL, nand_53_out);
  nand nand_55 (LDEXMN, LCSN, not_15_out, not_16_out, not_10_out, not_4_out, not_5_out, not_6_out, not_14_out);
  nand nand_56 (LDSEGN, LCSN, not_8_out, not_9_out, not_3_out, not_4_out, not_5_out, not_6_out, not_14_out);
  R41P DECODE_R41 (
    .A(LDEXMN), .B(LDSEGN), .C(LDPCRN), .CP(MCLK), .QAN(LLDEXM), .QBN(LLDSEG), .QCN(LLDPCR));  // open: D, QA, QB, QC, QD, QDN

  // Notes on the sheet:
  //   Page 25-28 - CGA_MAC_DECODE
  //   CSCOMM0
  //   CSCOMM1
  //   CSOMM2
  //   CSCOMM3
  //   CSCOMM4
  //   CSMIS0
  //   CSMIS1
  //   Page 25 ->
  //   Page 26 ->
  //   Page 27 ->
  //   Page 28 ->
endmodule

module CGA_MAC_ADD (
  input  [15:0] CD_15_0,
  input  CDS,
  input  PRB,
  input  PB,
  input  PX,
  input  PLCA,
  input  [15:0] RB_15_0,
  input  [15:0] BR_15_0,
  input  [15:0] XR_15_0,
  input  [15:0] LCA_15_0,
  output [15:0] ADD_15_0
);

  wire A02_1_z, A02_2_z, A02_3_z, A02_4_z, A02_5_z, A02_6_z, A02_7_z, A02_8_z, A02_9_z, A02_10_z, A02_11_z,
       A02_12_z, A02_13_z, A02_14_z, A02_15_z, A02_16_z, A02_17_z, A02_18_z, A02_19_z, A02_20_z, A02_21_z,
       A02_22_z, A02_23_z, A02_24_z, A02_25_z, A02_26_z, A02_27_z, A02_28_z, A02_29_z, A02_30_z, A02_31_z,
       A02_32_z, nand_1_out, nand_2_out, nand_3_out, nand_4_out, nand_5_out, nand_6_out, nand_7_out,
       nand_8_out, nand_9_out, nand_10_out, not_1_out;
  wire [7:0] nand_11_out;
  wire [15:0] or_1_out;

  A02 A02_16 (.A(XR_15_0[7]), .B(PX), .C(LCA_15_0[7]), .D(PLCA), .Z(A02_16_z));
  A02 A02_18 (.A(XR_15_0[8]), .B(PX), .C(LCA_15_0[8]), .D(PLCA), .Z(A02_18_z));
  A02 A02_20 (.A(XR_15_0[9]), .B(PX), .C(LCA_15_0[9]), .D(PLCA), .Z(A02_20_z));
  A02 A02_22 (.A(XR_15_0[10]), .B(PX), .C(LCA_15_0[10]), .D(PLCA), .Z(A02_22_z));
  A02 A02_24 (.A(XR_15_0[11]), .B(PX), .C(LCA_15_0[11]), .D(PLCA), .Z(A02_24_z));
  A02 A02_26 (.A(XR_15_0[12]), .B(PX), .C(LCA_15_0[12]), .D(PLCA), .Z(A02_26_z));
  A02 A02_28 (.A(XR_15_0[13]), .B(PX), .C(LCA_15_0[13]), .D(PLCA), .Z(A02_28_z));
  A02 A02_30 (.A(XR_15_0[14]), .B(PX), .C(LCA_15_0[14]), .D(PLCA), .Z(A02_30_z));
  A02 A02_32 (.A(XR_15_0[15]), .B(PX), .C(LCA_15_0[15]), .D(PLCA), .Z(A02_32_z));
  A02 A02_2 (.A(XR_15_0[0]), .B(PX), .C(LCA_15_0[0]), .D(PLCA), .Z(A02_2_z));
  A02 A02_4 (.A(XR_15_0[1]), .B(PX), .C(LCA_15_0[1]), .D(PLCA), .Z(A02_4_z));
  A02 A02_6 (.A(XR_15_0[2]), .B(PX), .C(LCA_15_0[2]), .D(PLCA), .Z(A02_6_z));
  A02 A02_8 (.A(XR_15_0[3]), .B(PX), .C(LCA_15_0[3]), .D(PLCA), .Z(A02_8_z));
  A02 A02_10 (.A(XR_15_0[4]), .B(PX), .C(LCA_15_0[4]), .D(PLCA), .Z(A02_10_z));
  A02 A02_12 (.A(XR_15_0[5]), .B(PX), .C(LCA_15_0[5]), .D(PLCA), .Z(A02_12_z));
  A02 A02_14 (.A(XR_15_0[6]), .B(PX), .C(LCA_15_0[6]), .D(PLCA), .Z(A02_14_z));
  A02 A02_11 (.A(RB_15_0[5]), .B(PRB), .C(BR_15_0[5]), .D(PB), .Z(A02_11_z));
  A02 A02_13 (.A(RB_15_0[6]), .B(PRB), .C(BR_15_0[6]), .D(PB), .Z(A02_13_z));
  A02 A02_15 (.A(RB_15_0[7]), .B(PRB), .C(BR_15_0[7]), .D(PB), .Z(A02_15_z));
  A02 A02_17 (.A(RB_15_0[8]), .B(PRB), .C(BR_15_0[8]), .D(PB), .Z(A02_17_z));
  A02 A02_19 (.A(RB_15_0[9]), .B(PRB), .C(BR_15_0[9]), .D(PB), .Z(A02_19_z));
  A02 A02_21 (.A(RB_15_0[10]), .B(PRB), .C(BR_15_0[10]), .D(PB), .Z(A02_21_z));
  A02 A02_23 (.A(RB_15_0[11]), .B(PRB), .C(BR_15_0[11]), .D(PB), .Z(A02_23_z));
  A02 A02_25 (.A(RB_15_0[12]), .B(PRB), .C(BR_15_0[12]), .D(PB), .Z(A02_25_z));
  A02 A02_27 (.A(RB_15_0[13]), .B(PRB), .C(BR_15_0[13]), .D(PB), .Z(A02_27_z));
  A02 A02_29 (.A(RB_15_0[14]), .B(PRB), .C(BR_15_0[14]), .D(PB), .Z(A02_29_z));
  A02 A02_31 (.A(RB_15_0[15]), .B(PRB), .C(BR_15_0[15]), .D(PB), .Z(A02_31_z));
  A02 A02_1 (.A(RB_15_0[0]), .B(PRB), .C(BR_15_0[0]), .D(PB), .Z(A02_1_z));
  A02 A02_3 (.A(RB_15_0[1]), .B(PRB), .C(BR_15_0[1]), .D(PB), .Z(A02_3_z));
  A02 A02_5 (.A(RB_15_0[2]), .B(PRB), .C(BR_15_0[2]), .D(PB), .Z(A02_5_z));
  A02 A02_7 (.A(RB_15_0[3]), .B(PRB), .C(BR_15_0[3]), .D(PB), .Z(A02_7_z));
  A02 A02_9 (.A(RB_15_0[4]), .B(PRB), .C(BR_15_0[4]), .D(PB), .Z(A02_9_z));
  or or_1 (or_1_out[0], ~A02_1_z, ~A02_2_z);  // OR_Gate
  or or_2 (or_1_out[1], ~A02_3_z, ~A02_4_z);  // OR_Gate
  or or_3 (or_1_out[2], ~A02_5_z, ~A02_6_z);  // OR_Gate
  or or_4 (or_1_out[3], ~A02_7_z, ~A02_8_z);  // OR_Gate
  or or_5 (or_1_out[4], ~A02_9_z, ~A02_10_z);  // OR_Gate
  or or_6 (or_1_out[5], ~A02_11_z, ~A02_12_z);  // OR_Gate
  or or_7 (or_1_out[6], ~A02_13_z, ~A02_14_z);  // OR_Gate
  or or_8 (or_1_out[7], ~A02_15_z, ~A02_16_z);  // OR_Gate
  or or_9 (or_1_out[8], ~A02_17_z, ~A02_18_z);  // OR_Gate
  or or_10 (or_1_out[9], ~A02_19_z, ~A02_20_z);  // OR_Gate
  or or_11 (or_1_out[10], ~A02_21_z, ~A02_22_z);  // OR_Gate
  or or_12 (or_1_out[11], ~A02_23_z, ~A02_24_z);  // OR_Gate
  or or_13 (or_1_out[12], ~A02_25_z, ~A02_26_z);  // OR_Gate
  or or_14 (or_1_out[13], ~A02_27_z, ~A02_28_z);  // OR_Gate
  or or_15 (or_1_out[14], ~A02_29_z, ~A02_30_z);  // OR_Gate
  or or_16 (or_1_out[15], ~A02_31_z, ~A02_32_z);  // OR_Gate
  nand nand_1 (nand_1_out, not_1_out, CD_15_0[8]);
  nand nand_2 (nand_2_out, not_1_out, CD_15_0[9]);
  not nand_3 (nand_3_out, not_1_out);  // NAND_Gate
  nand nand_4 (nand_4_out, not_1_out, CD_15_0[11]);
  nand nand_5 (nand_5_out, not_1_out, CD_15_0[12]);
  nand nand_6 (nand_6_out, not_1_out, CD_15_0[13]);
  nand nand_7 (nand_7_out, not_1_out, CD_15_0[14]);
  nand nand_8 (nand_8_out, not_1_out, CD_15_0[15]);
  nand nand_9 (nand_9_out, CD_15_0[7], CDS);
  nand nand_10 (nand_10_out, CDS, CD_15_0[7]);
  nand nand_11 (nand_11_out[0], nand_1_out, nand_9_out);
  nand nand_12 (nand_11_out[1], nand_2_out, nand_9_out);
  nand nand_13 (nand_11_out[2], nand_3_out, nand_9_out);
  nand nand_14 (nand_11_out[3], nand_4_out, nand_9_out);
  nand nand_15 (nand_11_out[4], nand_5_out, nand_10_out);
  nand nand_16 (nand_11_out[5], nand_6_out, nand_10_out);
  nand nand_17 (nand_11_out[6], nand_7_out, nand_10_out);
  nand nand_18 (nand_11_out[7], nand_8_out, nand_10_out);
  not not_1 (not_1_out, CDS);
  CGA_MAC_FASTADD FASTADD (.CD_7_0(CD_15_0[7:0]), .CDE_15_8(nand_11_out), .PRP_15_0(or_1_out), .ADD_15_0(ADD_15_0));
endmodule

module CGA_MAC_FASTADD (
  input  [7:0] CD_7_0,
  input  [7:0] CDE_15_8,
  input  [15:0] PRP_15_0,
  output [15:0] ADD_15_0
);

  Adder adder_1 (.a(CD_7_0), .b(PRP_15_0[7:0]), .out(ADD_15_0[7:0]));  // open: cin, cout
  Adder adder_2 (.a(CDE_15_8), .b(PRP_15_0[15:8]), .out(ADD_15_0[15:8]));  // open: cin, cout
endmodule

module CGA_MAC_AP09 (
  input  PSEL,
  input  ADDSEL,
  input  CDSEL,
  input  NLCASEL,
  input  HOLD,
  input  [15:0] PR_15_0,
  input  [15:0] ADD_15_0,
  input  [15:0] CD_15_0,
  input  ECCRHIN,
  input  MCLK,
  output [15:0] ICA_15_0,
  output ECCR,
  output [9:0] MCA_9_0,
  output [15:0] LCA_15_0,
  output [15:0] NLCA_15_0
);

  wire ICA0A_z, ICA0B_z, ICA1A_z, ICA1B_z, ICA2A_z, ICA2B_z, ICA3A_z, ICA3B_z, ICA4A_z, ICA4B_z, ICA5A_z,
       ICA5B_z, ICA6A_z, ICA6B_z, ICA7A_z, ICA7B_z, ICA8A_z, ICA8B_z, ICA9A_z, ICA9B_z, ICA10A_z, ICA10B_z,
       ICA11A_z, ICA11B_z, ICA12A_z, ICA12B_z, ICA13A_z, ICA13B_z, ICA14A_z, ICA14B_z, ICA15A_z, ICA15B_z,
       nand_1_out, nand_2_out, nand_3_out, nand_4_out, nand_5_out, nand_6_out, nand_7_out, nand_8_out,
       nand_9_out, nand_10_out, nand_11_out, nand_12_out, nand_13_out, nand_14_out, nand_15_out, nand_16_out;

  A02 ICA0A (.A(HOLD), .B(PSEL), .C(PR_15_0[0]), .D(LCA_15_0[0]), .Z(ICA0A_z));
  A02 ICA0B (.A(ADDSEL), .B(ADD_15_0[0]), .C(CDSEL), .D(CD_15_0[0]), .Z(ICA0B_z));
  nand nand_1 (nand_1_out, NLCASEL, NLCA_15_0[0]);
  A02 ICA1A (.A(HOLD), .B(PSEL), .C(PR_15_0[1]), .D(LCA_15_0[1]), .Z(ICA1A_z));
  A02 ICA1B (.A(ADDSEL), .B(ADD_15_0[1]), .C(CD_15_0[1]), .D(CDSEL), .Z(ICA1B_z));
  nand nand_2 (nand_2_out, NLCASEL, NLCA_15_0[1]);
  A02 ICA2A (.A(HOLD), .B(PSEL), .C(PR_15_0[2]), .D(LCA_15_0[2]), .Z(ICA2A_z));
  A02 ICA2B (.A(ADDSEL), .B(ADD_15_0[2]), .C(CD_15_0[2]), .D(CDSEL), .Z(ICA2B_z));
  nand nand_3 (nand_3_out, NLCASEL, NLCA_15_0[2]);
  A02 ICA3A (.A(HOLD), .B(PSEL), .C(PR_15_0[3]), .D(LCA_15_0[3]), .Z(ICA3A_z));
  A02 ICA3B (.A(ADDSEL), .B(ADD_15_0[3]), .C(CD_15_0[3]), .D(CDSEL), .Z(ICA3B_z));
  nand nand_4 (nand_4_out, NLCASEL, NLCA_15_0[3]);
  A02 ICA4A (.A(HOLD), .B(PSEL), .C(PR_15_0[4]), .D(CDSEL), .Z(ICA4A_z));
  A02 ICA4B (.A(ADDSEL), .B(ADD_15_0[4]), .C(CD_15_0[4]), .D(LCA_15_0[4]), .Z(ICA4B_z));
  nand nand_5 (nand_5_out, NLCASEL, NLCA_15_0[4]);
  A02 ICA5A (.A(HOLD), .B(PSEL), .C(PR_15_0[5]), .D(LCA_15_0[5]), .Z(ICA5A_z));
  A02 ICA5B (.A(ADDSEL), .B(ADD_15_0[5]), .C(CD_15_0[5]), .D(CDSEL), .Z(ICA5B_z));
  nand nand_6 (nand_6_out, NLCASEL, NLCA_15_0[5]);
  A02 ICA6A (.A(HOLD), .B(PSEL), .C(PR_15_0[6]), .D(LCA_15_0[6]), .Z(ICA6A_z));
  A02 ICA6B (.A(ADDSEL), .B(ADD_15_0[6]), .C(CD_15_0[6]), .D(CDSEL), .Z(ICA6B_z));
  nand nand_7 (nand_7_out, NLCASEL, NLCA_15_0[6]);
  A02 ICA7A (.A(HOLD), .B(PSEL), .C(PR_15_0[7]), .D(LCA_15_0[7]), .Z(ICA7A_z));
  A02 ICA7B (.A(ADDSEL), .B(ADD_15_0[7]), .C(CD_15_0[7]), .D(CDSEL), .Z(ICA7B_z));
  nand nand_8 (nand_8_out, NLCASEL, NLCA_15_0[7]);
  A02 ICA8A (.A(HOLD), .B(PSEL), .C(PR_15_0[8]), .D(LCA_15_0[8]), .Z(ICA8A_z));
  A02 ICA8B (.A(ADDSEL), .B(ADD_15_0[8]), .C(CD_15_0[8]), .D(CDSEL), .Z(ICA8B_z));
  nand nand_9 (nand_9_out, NLCASEL, NLCA_15_0[8]);
  A02 ICA9A (.A(HOLD), .B(PSEL), .C(PR_15_0[9]), .D(LCA_15_0[9]), .Z(ICA9A_z));
  A02 ICA9B (.A(ADDSEL), .B(ADD_15_0[9]), .C(CD_15_0[9]), .D(CDSEL), .Z(ICA9B_z));
  nand nand_10 (nand_10_out, NLCASEL, NLCA_15_0[9]);
  A02 ICA10A (.A(HOLD), .B(PSEL), .C(PR_15_0[10]), .D(LCA_15_0[10]), .Z(ICA10A_z));
  A02 ICA10B (.A(ADDSEL), .B(ADD_15_0[10]), .C(CD_15_0[10]), .D(CDSEL), .Z(ICA10B_z));
  nand nand_11 (nand_11_out, NLCASEL, NLCA_15_0[10]);
  A02 ICA11A (.A(HOLD), .B(PSEL), .C(PR_15_0[11]), .D(LCA_15_0[11]), .Z(ICA11A_z));
  A02 ICA11B (.A(ADDSEL), .B(ADD_15_0[11]), .C(CD_15_0[11]), .D(CDSEL), .Z(ICA11B_z));
  nand nand_12 (nand_12_out, NLCASEL, NLCA_15_0[11]);
  A02 ICA12A (.A(HOLD), .B(PSEL), .C(PR_15_0[12]), .D(LCA_15_0[12]), .Z(ICA12A_z));
  A02 ICA12B (.A(ADDSEL), .B(ADD_15_0[12]), .C(CD_15_0[12]), .D(CDSEL), .Z(ICA12B_z));
  nand nand_13 (nand_13_out, NLCASEL, NLCA_15_0[12]);
  A02 ICA13A (.A(HOLD), .B(PSEL), .C(PR_15_0[13]), .D(LCA_15_0[13]), .Z(ICA13A_z));
  A02 ICA13B (.A(ADDSEL), .B(ADD_15_0[13]), .C(CD_15_0[13]), .D(CDSEL), .Z(ICA13B_z));
  nand nand_14 (nand_14_out, NLCASEL, NLCA_15_0[13]);
  A02 ICA14A (.A(HOLD), .B(PSEL), .C(PR_15_0[14]), .D(LCA_15_0[14]), .Z(ICA14A_z));
  A02 ICA14B (.A(ADDSEL), .B(ADD_15_0[14]), .C(CD_15_0[14]), .D(CDSEL), .Z(ICA14B_z));
  nand nand_15 (nand_15_out, NLCASEL, NLCA_15_0[14]);
  A02 ICA15A (.A(HOLD), .B(PSEL), .C(PR_15_0[15]), .D(LCA_15_0[15]), .Z(ICA15A_z));
  A02 ICA15B (.A(ADDSEL), .B(ADD_15_0[15]), .C(CD_15_0[15]), .D(CDSEL), .Z(ICA15B_z));
  nand nand_16 (nand_16_out, NLCASEL, NLCA_15_0[15]);
  CGA_MAC_APOS_CALCA CALCA (
    .ECCRHIN(ECCRHIN), .ICA_15_0(ICA_15_0), .MCLK(MCLK), .MCA_15_0(MCA_9_0), .LCA_15_0(LCA_15_0), .ECCR(ECCR));
  CGA_MAC_APOS_INC AINC (.LCA_15_0(LCA_15_0), .NLCA_15_0(NLCA_15_0));
  or or_1 (ICA_15_0[0], ~ICA0A_z, ~ICA0B_z, ~nand_1_out);  // OR_Gate
  or or_2 (ICA_15_0[1], ~ICA1A_z, ~ICA1B_z, ~nand_2_out);  // OR_Gate
  or or_3 (ICA_15_0[2], ~ICA2A_z, ~ICA2B_z, ~nand_3_out);  // OR_Gate
  or or_4 (ICA_15_0[3], ~ICA3A_z, ~ICA3B_z, ~nand_4_out);  // OR_Gate
  or or_5 (ICA_15_0[4], ~ICA4A_z, ~ICA4B_z, ~nand_5_out);  // OR_Gate
  or or_6 (ICA_15_0[5], ~ICA5A_z, ~ICA5B_z, ~nand_6_out);  // OR_Gate
  or or_7 (ICA_15_0[6], ~ICA6A_z, ~ICA6B_z, ~nand_7_out);  // OR_Gate
  or or_8 (ICA_15_0[7], ~ICA7A_z, ~ICA7B_z, ~nand_8_out);  // OR_Gate
  or or_9 (ICA_15_0[8], ~ICA8A_z, ~ICA8B_z, ~nand_9_out);  // OR_Gate
  or or_10 (ICA_15_0[9], ~ICA9A_z, ~ICA9B_z, ~nand_10_out);  // OR_Gate
  or or_11 (ICA_15_0[10], ~ICA10A_z, ~ICA10B_z, ~nand_11_out);  // OR_Gate
  or or_12 (ICA_15_0[11], ~ICA11A_z, ~ICA11B_z, ~nand_12_out);  // OR_Gate
  or or_13 (ICA_15_0[12], ~ICA12A_z, ~ICA12B_z, ~nand_13_out);  // OR_Gate
  or or_14 (ICA_15_0[13], ~ICA13A_z, ~ICA13B_z, ~nand_14_out);  // OR_Gate
  or or_15 (ICA_15_0[14], ~ICA14A_z, ~ICA14B_z, ~nand_15_out);  // OR_Gate
  or or_16 (ICA_15_0[15], ~ICA15A_z, ~ICA15B_z, ~nand_16_out);  // OR_Gate

  // Notes on the sheet:
  //   Page 31 - CGA_MAC_APO9
  //   ICA0
  //   ICA1
  //   ICA2
  //   ICA3
  //   ICA4
  //   ICA5
  //   ICA6
  //   ICA7
  //   ICA8
  //   ICA9
  //   ICA10
  //   ICA11
  //   ICA12
  //   ICA13
  //   ICA14
  //   ICA15
endmodule

module CGA_MAC_APOS_CALCA (
  input  ECCRHIN,
  input  [15:0] ICA_15_0,
  input  MCLK,
  output [9:0] MCA_15_0,
  output [15:0] LCA_15_0,
  output ECCR
);

  wire L_HI_qc, L_HI_qd, L_HI_qe, L_HI_qf, L_HI_qg, L_HI_qh, nand_1_out, nand_2_out, not_1_out;
  wire [9:1] R_LO_qbn;

  not not_1 (not_1_out, MCLK);
  L8 L_LO (
    .A(ICA_15_0[0]), .B(ICA_15_0[1]), .C(ICA_15_0[2]), .D(ICA_15_0[3]), .E(ICA_15_0[4]), .F(ICA_15_0[5]),
    .G(ICA_15_0[6]), .H(ICA_15_0[7]), .L(not_1_out), .QA(MCA_15_0[0]), .QB(MCA_15_0[1]), .QC(MCA_15_0[2]),
    .QD(MCA_15_0[3]), .QE(MCA_15_0[4]), .QF(MCA_15_0[5]), .QG(MCA_15_0[6]), .QH(MCA_15_0[7]));  // open: QAN, QBN, QCN, QDN, QEN, QFN, QGN, QHN
  L8 L_HI (
    .A(ICA_15_0[8]), .B(ICA_15_0[9]), .C(ICA_15_0[10]), .D(ICA_15_0[11]), .E(ICA_15_0[12]), .F(ICA_15_0[13]),
    .G(ICA_15_0[14]), .H(ICA_15_0[15]), .L(not_1_out), .QA(MCA_15_0[8]), .QB(MCA_15_0[9]), .QC(L_HI_qc),
    .QD(L_HI_qd), .QE(L_HI_qe), .QF(L_HI_qf), .QG(L_HI_qg), .QH(L_HI_qh));  // open: QAN, QBN, QCN, QDN, QEN, QFN, QGN, QHN
  R81 R_LO (
    .A(MCA_15_0[0]), .B(MCA_15_0[1]), .C(MCA_15_0[2]), .D(MCA_15_0[3]), .E(MCA_15_0[4]), .F(MCA_15_0[5]),
    .G(MCA_15_0[6]), .H(MCA_15_0[7]), .CP(MCLK), .QA(LCA_15_0[0]), .QB(LCA_15_0[1]), .QBN(R_LO_qbn[1]),
    .QC(LCA_15_0[2]), .QD(LCA_15_0[3]), .QE(LCA_15_0[4]), .QEN(R_LO_qbn[4]), .QF(LCA_15_0[5]),
    .QFN(R_LO_qbn[5]), .QG(LCA_15_0[6]), .QH(LCA_15_0[7]), .QHN(R_LO_qbn[7]));  // open: QAN, QCN, QDN, QGN
  R81 R_HI (
    .A(MCA_15_0[8]), .B(MCA_15_0[9]), .C(L_HI_qc), .D(L_HI_qd), .E(L_HI_qe), .F(L_HI_qf), .G(L_HI_qg),
    .H(L_HI_qh), .CP(MCLK), .QA(LCA_15_0[8]), .QAN(R_LO_qbn[8]), .QB(LCA_15_0[9]), .QBN(R_LO_qbn[9]),
    .QC(LCA_15_0[10]), .QD(LCA_15_0[11]), .QE(LCA_15_0[12]), .QF(LCA_15_0[13]), .QG(LCA_15_0[14]),
    .QH(LCA_15_0[15]));  // open: QCN, QDN, QEN, QFN, QGN, QHN
  nand nand_1 (nand_1_out, LCA_15_0[0], R_LO_qbn[1], LCA_15_0[2], LCA_15_0[3], R_LO_qbn[4]);
  nand nand_2 (nand_2_out, R_LO_qbn[5], LCA_15_0[6], R_LO_qbn[7], R_LO_qbn[8], R_LO_qbn[9]);
  and and_1 (ECCR, ~ECCRHIN, ~nand_1_out, ~nand_2_out);  // AND_Gate

  // Notes on the sheet:
  //   Page 32 - CGA_MAC_APOS_CALCA
  //   LCA0
  //   LCA9N
  //   DECODE TRR ECCR = IOX 100115
endmodule

module CGA_MAC_APOS_INC (
  input  [15:0] LCA_15_0,
  output [15:0] NLCA_15_0
);

  wire adder_1_cout, adder_2_cout, adder_3_cout, adder_4_cout, adder_5_cout, adder_6_cout, adder_7_cout,
       adder_9_cout, adder_10_cout, adder_11_cout, adder_12_cout, adder_14_cout, adder_15_cout, nand_1_out,
       nand_2_out, not_1_out, not_2_out;

  Adder #(.width(1)) adder_1 (.a(LCA_15_0[0]), .b(1'b1), .out(NLCA_15_0[0]), .cout(adder_1_cout));  // open: cin
  Adder #(.width(1)) adder_2 (.a(LCA_15_0[1]), .b(adder_1_cout), .out(NLCA_15_0[1]), .cout(adder_2_cout));  // open: cin
  Adder #(.width(1)) adder_3 (.a(LCA_15_0[2]), .b(adder_2_cout), .out(NLCA_15_0[2]), .cout(adder_3_cout));  // open: cin
  Adder #(.width(1)) adder_4 (.a(LCA_15_0[3]), .b(adder_3_cout), .out(NLCA_15_0[3]), .cout(adder_4_cout));  // open: cin
  Adder #(.width(1)) adder_5 (.a(LCA_15_0[4]), .b(adder_4_cout), .out(NLCA_15_0[4]), .cout(adder_5_cout));  // open: cin
  Adder #(.width(1)) adder_6 (.a(LCA_15_0[5]), .b(adder_5_cout), .out(NLCA_15_0[5]), .cout(adder_6_cout));  // open: cin
  Adder #(.width(1)) adder_7 (.a(LCA_15_0[6]), .b(adder_6_cout), .out(NLCA_15_0[6]), .cout(adder_7_cout));  // open: cin
  Adder #(.width(1)) adder_8 (.a(LCA_15_0[7]), .b(adder_7_cout), .out(NLCA_15_0[7]));  // open: cin, cout
  nand nand_1 (nand_1_out, LCA_15_0[7], LCA_15_0[6], LCA_15_0[5], LCA_15_0[4], LCA_15_0[3], LCA_15_0[2], LCA_15_0[1], LCA_15_0[0]);
  not not_1 (not_1_out, nand_1_out);
  Adder #(.width(1)) adder_9 (.a(LCA_15_0[8]), .b(not_1_out), .out(NLCA_15_0[8]), .cout(adder_9_cout));  // open: cin
  Adder #(.width(1)) adder_10 (
    .a(LCA_15_0[9]), .b(adder_9_cout), .out(NLCA_15_0[9]), .cout(adder_10_cout));  // open: cin
  Adder #(.width(1)) adder_11 (
    .a(LCA_15_0[10]), .b(adder_10_cout), .out(NLCA_15_0[10]), .cout(adder_11_cout));  // open: cin
  Adder #(.width(1)) adder_12 (
    .a(LCA_15_0[11]), .b(adder_11_cout), .out(NLCA_15_0[11]), .cout(adder_12_cout));  // open: cin
  nand nand_2 (nand_2_out, LCA_15_0[12], LCA_15_0[11], LCA_15_0[10], LCA_15_0[9], LCA_15_0[8], not_1_out);
  Adder #(.width(1)) adder_13 (.a(LCA_15_0[12]), .b(adder_12_cout), .out(NLCA_15_0[12]));  // open: cin, cout
  not not_2 (not_2_out, nand_2_out);
  Adder #(.width(1)) adder_14 (
    .a(LCA_15_0[13]), .b(not_2_out), .out(NLCA_15_0[13]), .cout(adder_14_cout));  // open: cin
  Adder #(.width(1)) adder_15 (
    .a(LCA_15_0[14]), .b(adder_14_cout), .out(NLCA_15_0[14]), .cout(adder_15_cout));  // open: cin
  Adder #(.width(1)) adder_16 (.a(LCA_15_0[15]), .b(adder_15_cout), .out(NLCA_15_0[15]));  // open: cin, cout

  // Notes on the sheet:
  //   Page 33 - CGA_MAC_APOS_INC
endmodule

module CGA_MAC_PTSEL (
  input  SPTN,
  input  SAPT,
  input  PONI,
  input  PTM,
  input  MCLK,
  output SELPTN
);

  wire j_k_ff_1_qn, nor_1_out, not_1_out, not_2_out, or_1_out, or_2_out;

  nor nor_1 (nor_1_out, ~PTM, ~PONI);  // NOR_Gate
  not not_1 (not_1_out, SPTN);
  not not_2 (not_2_out, nor_1_out);
  J_K_Flip_Flop j_k_ff_1 (
    .J(not_1_out), .K(SAPT), .clk(MCLK), .Qn(j_k_ff_1_qn), .preset(not_2_out), .reset(1'b0));  // open: Q
  or or_1 (or_1_out, ~SPTN, ~j_k_ff_1_qn);  // OR_Gate
  or or_2 (or_2_out, ~SAPT, ~PONI, ~PTM);  // OR_Gate
  nand nand_1 (SELPTN, or_1_out, or_2_out);

  // Notes on the sheet:
  //   Page 34 - CGA_MAC_PTSEL
  //   In the original schematics for the FF the PR and CL is negated, this LogiSim J/K FF doesnt support that - so the signals has been changed to accomodate
endmodule

module CGA_MAC_SEGPT (
  input  [15:0] FIDBO_15_0,
  input  MCLK,
  input  LLDSEG,
  input  LLDPCR,
  input  LLDEXM,
  input  EXMN,
  output [7:0] SEG_7_0,
  output SEGZN,
  output [15:0] PCR_15_7_2_0,
  output [15:0] PCR_14_13_10_9_N,
  output [1:0] XPT_1_0,
  output VEX,
  output PEX
);

  wire not_1_out;
  wire [6:3] undriven;

  not not_1 (not_1_out, MCLK);
  CGA_MAC_SEGPT_SEG SEG (
    .FIDB_7_0(FIDBO_15_0[7:0]), .MCLKN(not_1_out), .LLDSEG(LLDSEG), .SEG_7_0(SEG_7_0), .SEGZN(SEGZN));
  CGA_MAC_SEGPT_PCR PCR (
    .FIDB_15_7_2_0({FIDBO_15_0[15:7], undriven, FIDBO_15_0[2:0]}), .MCLKN(not_1_out), .LLDPCR(LLDPCR),
    .PCR_15_7_2_0(PCR_15_7_2_0), .PCR_14_13_10_9_N(PCR_14_13_10_9_N));
  CGA_MAC_SEGPT_XPT XPT (
    .FIDBO_2_0(FIDBO_15_0[2:0]), .MCLKN(not_1_out), .LLDEXM(LLDEXM), .EXMN(EXMN), .XPT_1_0(XPT_1_0),
    .VEX(VEX), .PEX(PEX));

  // Notes on the sheet:
  //   MCLKN
  //   MCLKN
  //   MCLKN
endmodule
module CGA_MAC_SEGPT_SEG (
  input  [7:0] FIDB_7_0,
  input  MCLKN,
  input  LLDSEG,
  output [7:0] SEG_7_0,
  output SEGZN
);

  wire and_1_out;
  wire [7:0] SEG_L_qan;

  and and_1 (and_1_out, MCLKN, LLDSEG);
  L8 SEG_L (
    .A(FIDB_7_0[0]), .B(FIDB_7_0[1]), .C(FIDB_7_0[2]), .D(FIDB_7_0[3]), .E(FIDB_7_0[4]), .F(FIDB_7_0[5]),
    .G(FIDB_7_0[6]), .H(FIDB_7_0[7]), .L(and_1_out), .QA(SEG_7_0[0]), .QAN(SEG_L_qan[0]), .QB(SEG_7_0[1]),
    .QBN(SEG_L_qan[1]), .QC(SEG_7_0[2]), .QCN(SEG_L_qan[2]), .QD(SEG_7_0[3]), .QDN(SEG_L_qan[3]),
    .QE(SEG_7_0[4]), .QEN(SEG_L_qan[4]), .QF(SEG_7_0[5]), .QFN(SEG_L_qan[5]), .QG(SEG_7_0[6]),
    .QGN(SEG_L_qan[6]), .QH(SEG_7_0[7]), .QHN(SEG_L_qan[7]));
  nand nand_1 (SEGZN, SEG_L_qan[0], SEG_L_qan[1], SEG_L_qan[2], SEG_L_qan[3], SEG_L_qan[4], SEG_L_qan[5], SEG_L_qan[6], SEG_L_qan[7]);
endmodule

module CGA_MAC_SEGPT_PCR (
  input  [15:0] FIDB_15_7_2_0,
  input  MCLKN,
  input  LLDPCR,
  output [15:0] PCR_15_7_2_0,
  output [15:0] PCR_14_13_10_9_N
);

  wire and_1_out, PCR_HI_qdn;

  and and_1 (and_1_out, MCLKN, LLDPCR);
  L8 PCR_HI (
    .A(FIDB_15_7_2_0[15]), .B(FIDB_15_7_2_0[14]), .C(FIDB_15_7_2_0[13]), .D(FIDB_15_7_2_0[12]),
    .E(FIDB_15_7_2_0[11]), .F(FIDB_15_7_2_0[10]), .G(FIDB_15_7_2_0[9]), .H(FIDB_15_7_2_0[8]), .L(and_1_out),
    .QA(PCR_15_7_2_0[15]), .QB(PCR_15_7_2_0[14]), .QBN(PCR_14_13_10_9_N[14]), .QC(PCR_15_7_2_0[13]),
    .QCN(PCR_14_13_10_9_N[13]), .QD(PCR_15_7_2_0[12]), .QDN(PCR_HI_qdn), .QE(PCR_15_7_2_0[11]),
    .QF(PCR_15_7_2_0[10]), .QFN(PCR_14_13_10_9_N[10]), .QG(PCR_15_7_2_0[9]), .QGN(PCR_14_13_10_9_N[9]),
    .QH(PCR_15_7_2_0[8]));  // open: QAN, QEN, QHN
  L4 PCR_LO (
    .A(FIDB_15_7_2_0[7]), .B(FIDB_15_7_2_0[2]), .C(FIDB_15_7_2_0[1]), .D(FIDB_15_7_2_0[0]), .L(and_1_out),
    .QA(PCR_15_7_2_0[7]), .QB(PCR_15_7_2_0[2]), .QC(PCR_15_7_2_0[1]), .QD(PCR_15_7_2_0[0]));  // open: QAN, QBN, QCN, QDN

  // Notes on the sheet:
  //   Page 37 - CGA_MAC_SEGPTR_PCR
endmodule

module CGA_MAC_SEGPT_XPT (
  input  [2:0] FIDBO_2_0,
  input  MCLKN,
  input  LLDEXM,
  input  EXMN,
  output [1:0] XPT_1_0,
  output VEX,
  output PEX
);

  wire and_1_out, not_1_out, XPT_L_qc, XPT_L_qcn;

  and and_1 (and_1_out, MCLKN, LLDEXM);
  not not_1 (not_1_out, EXMN);
  L4 XPT_L (
    .A(FIDBO_2_0[0]), .B(FIDBO_2_0[1]), .C(FIDBO_2_0[2]), .L(and_1_out), .QA(XPT_1_0[0]), .QB(XPT_1_0[1]),
    .QC(XPT_L_qc), .QCN(XPT_L_qcn));  // open: D, QAN, QBN, QD, QDN
  and and_2 (VEX, not_1_out, XPT_L_qc);
  and and_3 (PEX, XPT_L_qcn, not_1_out);

  // Notes on the sheet:
  //   Page 38 - CGA_MAC_SEGPT_XPT
  //   FIDBO0
  //   FIDBO1
  //   FIDBO2
  //   XPT0
  //   XPT1
endmodule

module CGA_MAC_LASEL (
  input  DOUBLE,
  input  [15:0] PCR_15_7_2_0,
  input  [15:0] ICA_15_8,
  input  CSMREQ,
  input  VEX,
  input  PONI,
  input  PEX,
  input  SEGZN,
  input  EXMN,
  input  SELPTN,
  input  MCLK,
  output A10,
  output BB10,
  output C10,
  output A1617,
  output D1617,
  output E1617,
  output F1617,
  output A1819,
  output B1821,
  output B1819,
  output A1619,
  output LSHADOW
);

  wire and_1_out, nand_1_out, nand_2_out, nand_3_out, nand_4_out, nand_5_out, nand_6_out, nand_7_out,
       nor_1_out, not_1_out, not_2_out, not_3_out, not_4_out, not_5_out, not_6_out, not_7_out, not_8_out,
       not_9_out, not_10_out, or_1_out, or_2_out, or_3_out;

  not not_1 (not_1_out, DOUBLE);
  not not_2 (not_2_out, PCR_15_7_2_0[2]);
  nand nand_1 (nand_1_out, not_1_out, not_2_out);
  nand nand_2 (nand_2_out, PCR_15_7_2_0[2], DOUBLE);
  nand nand_3 (nand_3_out, ICA_15_8[10], ICA_15_8[9]);
  nor nor_1 (nor_1_out, nand_1_out, ICA_15_8[8]);
  nand nand_4 (nand_4_out, ICA_15_8[15], ICA_15_8[14], ICA_15_8[13], ICA_15_8[12], ICA_15_8[11]);
  not not_3 (not_3_out, PEX);
  nand nand_5 (nand_5_out, PCR_15_7_2_0[1], PCR_15_7_2_0[0]);
  or or_1 (or_1_out, ~nand_2_out, ~nand_3_out);  // OR_Gate
  and and_1 (and_1_out, ~nor_1_out, ~nand_4_out);  // AND_Gate
  or or_2 (or_2_out, ~nand_5_out, ~PONI, ~not_3_out);  // OR_Gate
  or or_3 (or_3_out, ~PEX, ~SEGZN);  // OR_Gate
  nand nand_6 (nand_6_out, or_1_out, and_1_out, CSMREQ, or_2_out, or_3_out);
  not not_4 (not_4_out, nand_6_out);
  nand nand_7 (nand_7_out, EXMN, CSMREQ, PONI);
  not not_5 (not_5_out, not_4_out);
  not not_6 (not_6_out, SELPTN);
  not not_7 (not_7_out, EXMN);
  not not_8 (not_8_out, nand_7_out);
  not not_9 (not_9_out, nand_1_out);
  not not_10 (not_10_out, nand_2_out);
  D_Flip_Flop d_ff_1 (.D(not_5_out), .clk(MCLK), .Qn(LSHADOW));  // open: Q, preset, reset
  and and_2 (A10, not_4_out, not_9_out);
  and and_3 (BB10, not_4_out, nand_1_out);
  and and_4 (C10, not_5_out, 1'b1);
  and and_5 (A1617, not_5_out, PEX);
  and and_6 (D1617, not_5_out, nand_2_out, not_6_out, not_8_out);
  and and_7 (E1617, not_5_out, not_8_out, SELPTN);
  and and_8 (F1617, not_5_out, VEX);
  and and_9 (A1819, not_4_out, not_10_out);
  and and_10 (B1821, not_5_out, not_7_out);
  and and_11 (B1819, not_5_out, SELPTN, not_8_out, not_10_out);
  and and_12 (A1619, not_5_out, not_8_out, not_6_out, not_10_out);

  // Notes on the sheet:
  //   Page 39 - CGA_MAC_LASEL
  //   REXN
  //   EXN
  //   SHADOW
  //   SHADOWN
  //   ISELPT
  //   SHADOWN
endmodule

module CGA_MAC_LA1025 (
  input  [15:0] ICA_15_0,
  input  A10,
  input  BB10,
  input  C10,
  input  A1617,
  input  D1617,
  input  E1617,
  input  F1617,
  input  A1819,
  input  B1821,
  input  B1819,
  input  A1619,
  input  [7:0] SEG_7_0,
  input  [15:0] PCR_15_0,
  input  [15:0] PCR_15_0_N,
  input  [1:0] XPT_1_0,
  input  MCLK,
  output ECCRHIN,
  output [13:0] LA_23_10
);

  wire ILA10A_z, ILA11A_z, ILA12A_z, ILA13A_z, ILA14A_z, ILA15A_z, ILA16A_z, ILA16B_z, ILA16C_z, ILA17A_z,
       ILA17B_z, ILA17C_z, ILA18A_z, ILA18B_z, ILA19A_z, ILA19B_z, nand_1_out, nand_2_out, nand_3_out,
       nand_4_out, nand_5_out, nand_6_out, nand_7_out, nand_8_out, nand_9_out, nand_10_out, nand_11_out,
       nand_12_out, not_1_out, not_2_out, or_1_out, or_2_out, or_3_out, or_4_out, or_5_out, or_6_out,
       or_7_out, or_8_out, or_9_out, or_10_out, R_LA_L_qdn, R_LA_L_qen, R_LA_L_qfn, R_LA_L_qgn, R_LA_L_qhn;

  not not_1 (not_1_out, ICA_15_0[9]);
  not not_2 (not_2_out, ICA_15_0[10]);
  A02 ILA15A (.A(ICA_15_0[5]), .B(A10), .C(ICA_15_0[6]), .D(BB10), .Z(ILA15A_z));
  nand nand_1 (nand_1_out, ICA_15_0[15], C10);
  A02 ILA14A (.A(ICA_15_0[4]), .B(A10), .C(ICA_15_0[5]), .D(BB10), .Z(ILA14A_z));
  nand nand_2 (nand_2_out, ICA_15_0[14], C10);
  A02 ILA13A (.A(ICA_15_0[3]), .B(A10), .C(ICA_15_0[4]), .D(BB10), .Z(ILA13A_z));
  nand nand_3 (nand_3_out, ICA_15_0[13], C10);
  A02 ILA12A (.A(ICA_15_0[2]), .B(A10), .C(ICA_15_0[3]), .D(BB10), .Z(ILA12A_z));
  nand nand_4 (nand_4_out, ICA_15_0[12], C10);
  A02 ILA11A (.A(ICA_15_0[1]), .B(A10), .C(ICA_15_0[2]), .D(BB10), .Z(ILA11A_z));
  nand nand_5 (nand_5_out, ICA_15_0[11], C10);
  A02 ILA10A (.A(ICA_15_0[0]), .B(A10), .C(ICA_15_0[1]), .D(BB10), .Z(ILA10A_z));
  nand nand_6 (nand_6_out, ICA_15_0[10], C10);
  nand nand_7 (nand_7_out, SEG_7_0[5], B1821);
  nand nand_8 (nand_8_out, SEG_7_0[4], B1821);
  A02 ILA19A (.A(A1619), .B(PCR_15_0_N[14]), .C(SEG_7_0[3]), .D(B1821), .Z(ILA19A_z));
  A02 ILA19B (.A(not_2_out), .B(A1819), .C(PCR_15_0_N[10]), .D(B1819), .Z(ILA19B_z));
  A02 ILA18A (.A(A1619), .B(PCR_15_0_N[13]), .C(PCR_15_0_N[9]), .D(B1819), .Z(ILA18A_z));
  A02 ILA18B (.A(SEG_7_0[2]), .B(B1821), .C(not_1_out), .D(A1819), .Z(ILA18B_z));
  nand nand_9 (nand_9_out, SEG_7_0[7], A1617);
  nand nand_10 (nand_10_out, SEG_7_0[6], A1617);
  A02 ILA17A (.A(ICA_15_0[7]), .B(A10), .C(ICA_15_0[8]), .D(BB10), .Z(ILA17A_z));
  A02 ILA17B (.A(PCR_15_0[12]), .B(A1619), .C(SEG_7_0[1]), .D(A1617), .Z(ILA17B_z));
  A02 ILA17C (.A(PCR_15_0[10]), .B(D1617), .C(PCR_15_0[8]), .D(E1617), .Z(ILA17C_z));
  nand nand_11 (nand_11_out, XPT_1_0[1], F1617);
  A02 ILA16A (.A(ICA_15_0[6]), .B(A10), .C(ICA_15_0[7]), .D(BB10), .Z(ILA16A_z));
  A02 ILA16B (.A(PCR_15_0[11]), .B(A1619), .C(SEG_7_0[0]), .D(A1617), .Z(ILA16B_z));
  A02 ILA16C (.A(PCR_15_0[9]), .B(D1617), .C(PCR_15_0[7]), .D(E1617), .Z(ILA16C_z));
  nand nand_12 (nand_12_out, XPT_1_0[0], F1617);
  or or_1 (or_1_out, ~ILA15A_z, ~nand_1_out);  // OR_Gate
  or or_2 (or_2_out, ~ILA14A_z, ~nand_2_out);  // OR_Gate
  or or_3 (or_3_out, ~ILA13A_z, ~nand_3_out);  // OR_Gate
  or or_4 (or_4_out, ~ILA12A_z, ~nand_4_out);  // OR_Gate
  or or_5 (or_5_out, ~ILA11A_z, ~nand_5_out);  // OR_Gate
  or or_6 (or_6_out, ~ILA10A_z, ~nand_6_out);  // OR_Gate
  or or_7 (or_7_out, ~ILA19A_z, ~ILA19B_z);  // OR_Gate
  or or_8 (or_8_out, ~ILA18A_z, ~ILA18B_z);  // OR_Gate
  or or_9 (or_9_out, ~ILA17A_z, ~ILA17B_z, ~ILA17C_z, ~nand_11_out);  // OR_Gate
  or or_10 (or_10_out, ~ILA16A_z, ~ILA16B_z, ~ILA16C_z, ~nand_12_out);  // OR_Gate
  R81 R_LA_H (
    .C(nand_9_out), .D(nand_10_out), .E(nand_7_out), .F(nand_8_out), .G(or_7_out), .H(or_8_out), .CP(MCLK),
    .QCN(LA_23_10[13]), .QDN(LA_23_10[12]), .QEN(LA_23_10[11]), .QFN(LA_23_10[10]), .QG(LA_23_10[9]),
    .QH(LA_23_10[8]));  // open: A, B, QA, QAN, QB, QBN, QC, QD, QE, QF, QGN, QHN
  R81 R_LA_L (
    .A(or_9_out), .B(or_10_out), .C(or_1_out), .D(or_2_out), .E(or_3_out), .F(or_4_out), .G(or_5_out),
    .H(or_6_out), .CP(MCLK), .QA(LA_23_10[7]), .QB(LA_23_10[6]), .QC(LA_23_10[5]), .QD(LA_23_10[4]),
    .QDN(R_LA_L_qdn), .QE(LA_23_10[3]), .QEN(R_LA_L_qen), .QF(LA_23_10[2]), .QFN(R_LA_L_qfn),
    .QG(LA_23_10[1]), .QGN(R_LA_L_qgn), .QH(LA_23_10[0]), .QHN(R_LA_L_qhn));  // open: QAN, QBN, QCN
  nand nand_13 (ECCRHIN, LA_23_10[5], R_LA_L_qhn, R_LA_L_qgn, R_LA_L_qfn, R_LA_L_qen, R_LA_L_qdn);

  // Notes on the sheet:
  //   Page 40 - CGA_MAC_LA1025
  //   ILA15
  //   ILA14
  //   ILA13
  //   ILA12
  //   ILA11
  //   ILA10
  //   ILA21N
  //   ILA20N
  //   ILA19
  //   ILA18
  //   ILA23N
  //   ILA22N
  //   ILA17
  //   ILA16
  //   LA10
  //   LA23
endmodule

module test_MAC (
  input  in_1,
  input  in_2,
  input  [15:0] in_3,
  input  in_4,
  input  [1:0] in_5,
  input  [4:0] in_6,
  input  in_7,
  input  in_8,
  input  in_9,
  input  in_10,
  input  in_11,
  input  [15:0] in_12,
  input  [15:0] in_13,
  input  [15:0] in_14,
  input  [15:0] in_15,
  input  [15:0] in_16
);

  wire cga_mac_1_eccr, cga_mac_1_lshadow, cga_mac_1_vex;
  wire [9:0] cga_mac_1_mca_9_0;
  wire [13:0] cga_mac_1_la_23_10;
  wire [15:0] cga_mac_1_nlca_15_0, cga_mac_1_pcr_15_0;

  CGA_MAC cga_mac_1 (
    .MCLK(in_1), .PTM(in_2), .FIDBO_15_0(in_3), .PONI(in_4), .CMIS_1_0(in_5), .CSCOMM_4_0(in_6), .WR3(in_7),
    .WR7(in_8), .ILCSN(in_9), .DOUBLE(in_10), .CSMREQ(in_11), .CD_15_0(in_12), .RB_15_0(in_13),
    .XR_15_0(in_14), .BR_15_0(in_15), .PR_15_0(in_16), .VEX(cga_mac_1_vex), .PCR_15_0(cga_mac_1_pcr_15_0),
    .LA_23_10(cga_mac_1_la_23_10), .LSHADOW(cga_mac_1_lshadow), .ECCR(cga_mac_1_eccr),
    .MCA_9_0(cga_mac_1_mca_9_0), .NLCA_15_0(cga_mac_1_nlca_15_0));
  // Probe on cga_mac_1_vex
  // Probe on cga_mac_1_lshadow
  // Probe on cga_mac_1_eccr
  // Probe on cga_mac_1_nlca_15_0
  // Probe on cga_mac_1_la_23_10
  // Probe on cga_mac_1_mca_9_0
  // Probe on cga_mac_1_pcr_15_0

  // Notes on the sheet:
  //   MAC UNDER TEST
endmodule

module CGA_MIC (
  input  [15:0] CSBIT_15_0,
  input  CSBIT20,
  input  LCZ,
  input  MI,
  input  IRQ,
  input  RESTR,
  input  CFETCH,
  input  SPARE,
  input  OVF,
  input  CRY,
  input  F11,
  input  F15,
  input  ZF,
  input  STP,
  input  ALUCLK,
  input  MCLK,
  input  CSLOOP,
  input  CSECOND,
  input  CLFFN,
  input  CSALUI8,
  input  CSCOND,
  input  ILCSN,
  input  [3:0] CSTS_6_3,
  input  [3:0] TVEC_3_0,
  input  TRAPN,
  input  MAPN,
  input  EWCAN,
  input  CSMIS0,
  input  CSVECT,
  input  [15:0] CD_15_0,
  input  LDIRV,
  input  LWCAN,
  input  MRN,
  input  LDLCN,
  input  [3:0] PIL_3_0,
  input  CSXRF3,
  input  [3:0] CSRB_3_0,
  input  [1:0] CSRASEL_1_0,
  input  [1:0] CSRBSEL_1_0,
  output DZD,
  output COND,
  output OOD,
  output ACONDN,
  output [3:0] SC_6_3,
  output [12:0] MA_12_0,
  output WCSN,
  output DEEP,
  output UPN,
  output PN,
  output LCZN,
  output TN,
  output [3:0] LAA_3_0,
  output [3:0] LBA_3_0,
  output [1:0] RF_1_0
);

  wire and_1_out, and_2_out, and_3_out, and_4_out, and_5_out, and_6_out, and_7_out, and_8_out, and_9_out,
       and_10_out, and_11_out, CIN, CSEL_condn, d_ff_1_q, d_ff_2_q, d_ff_5_q, d_ff_6_q, d_ff_7_qn, DZD_FF_q,
       LAA_REG_qan, LAA_REG_qbn, LAA_REG_qcn, LAA_REG_qdn, LBA_REG_qan, LBA_REG_qbn, LBA_REG_qcn,
       LBA_REG_qdn, LC_CMP_aeb, LC_HI_con, LC_HI_qa, LC_HI_qb, LC_HI_qc, LC_HI_qd, LCSN, LCZ_t, M_LAA_0_z,
       M_LAA_1_z, M_LAA_2_z, M_LAA_3_z, M_LBA_0_z, M_LBA_1_z, M_LBA_2_z, M_LBA_3_z, MIC_LOOP, nand_1_out,
       nand_2_out, nand_3_out, nand_5_out, nand_6_out, nand_9_out, nor_1_out, nor_2_out, nor_3_out,
       nor_4_out, nor_5_out, nor_6_out, nor_7_out, nor_8_out, nor_9_out, not_1_out, not_2_out, not_3_out,
       not_4_out, not_5_out, not_6_out, not_8_out, not_10_out, not_11_out, not_12_out, not_13_out,
       not_18_out, OOD_FF_q, or_1_out, or_2_out;
  wire [1:0] CSWAN_1_0;
  wire [3:0] CONDREG_fs_6_3, CONDREG_tsel_3_0, ILC_MUX_z0, LC_3_0, LCC_3_0;
  wire [6:0] IR_6_0;
  wire [12:0] MIC_IINC_next_12_0, MIC_MASEL_iw_12_0, MIC_MASEL_w_12_0, MIC_STACK_ret_12_0,
       MIC_WCAREG_wca_12_0;

  not not_1 (not_1_out, LCSN);
  not not_2 (not_2_out, CLFFN);
  nand nand_1 (nand_1_out, CSRASEL_1_0[0], CSXRF3);
  not not_3 (not_3_out, CSRASEL_1_0[1]);
  nand nand_2 (nand_2_out, CSXRF3, not_3_out);
  // Probe on CSBIT_15_0[11:0]
  not not_4 (not_4_out, CSVECT);
  not not_5 (not_5_out, CSXRF3);
  and and_1 (and_1_out, not_5_out, IR_6_0[6]);
  D_Flip_Flop d_ff_1 (.D(nand_2_out), .clk(MCLK), .Q(d_ff_1_q));  // open: Qn, preset, reset
  D_Flip_Flop d_ff_2 (.D(nand_1_out), .clk(MCLK), .Q(d_ff_2_q));  // open: Qn, preset, reset
  not not_6 (not_6_out, ILCSN);
  not not_7 (LCSN, not_6_out);
  nand nand_3 (nand_3_out, LCSN, EWCAN);
  CGA_MIC_CSEL CSEL (
    .DZD(DZD), .LCZ(LCZ), .IRQ(IRQ), .RESTR(RESTR), .CFETCH(CFETCH), .OOD(OOD), .SPARE(SPARE), .COND(COND),
    .OVF(OVF), .CRY(CRY), .F11(F11), .F15(F15), .ZF(ZF), .STP(STP), .ALUCLK(ALUCLK),
    .TSEL_3_0(CONDREG_tsel_3_0), .CONDN(CSEL_condn));
  not not_8 (not_8_out, CSLOOP);
  MUX41P M_LAA_3 (
    .D0(CSBIT_15_0[12]), .D1(PIL_3_0[0]), .D2(and_1_out), .D3(LC_3_0[3]), .A(CSRASEL_1_0[0]),
    .B(CSRASEL_1_0[1]), .Z(M_LAA_3_z));
  CGA_MIC_INCOUNT MIC_INCOUNT (
    .CD0(CD_15_0[0]), .LWCAN(LWCAN), .EC(not_1_out), .MRN(MRN), .CD1(CD_15_0[1]), .MCLK(MCLK),
    .CSWAN0(CSWAN_1_0[0]), .CSWAN1(CSWAN_1_0[1]));
  M169C LC_HI (
    .A(CD_15_0[4]), .B(CD_15_0[5]), .C(CD_15_0[5]), .D(CD_15_0[5]), .NL(LDLCN), .CP(MCLK), .PN(PN), .TN(TN),
    .UP(not_11_out), .QA(LC_HI_qa), .QB(LC_HI_qb), .QC(LC_HI_qc), .QD(LC_HI_qd), .CON(LC_HI_con));
  M169C LC_LO (
    .A(CD_15_0[0]), .B(CD_15_0[1]), .C(CD_15_0[2]), .D(CD_15_0[3]), .NL(LDLCN), .CP(MCLK), .PN(PN),
    .TN(1'b0), .UP(not_11_out), .QA(LC_3_0[0]), .QB(LC_3_0[1]), .QC(LC_3_0[2]), .QD(LC_3_0[3]), .CON(TN));
  D_Flip_Flop d_ff_3 (.D(CSEL_condn), .clk(MCLK), .Qn(COND));  // open: Q, preset, reset
  D_Flip_Flop d_ff_4 (.D(CSLOOP), .clk(MCLK), .Q(MIC_LOOP));  // open: Qn, preset, reset
  not not_9 (UPN, LC_HI_qd);
  MUX21L M_RF1 (.A(d_ff_1_q), .B(CSWAN_1_0[1]), .S(nand_3_out), .ZN(RF_1_0[1]));
  MUX21L M_RF0 (.A(d_ff_2_q), .B(CSWAN_1_0[0]), .S(nand_3_out), .ZN(RF_1_0[0]));
  not not_10 (not_10_out, CSECOND);
  MUX34P ILC_MUX (
    .D00(IR_6_0[0]), .D10(LAA_3_0[0]), .D20(CSBIT_15_0[0]), .D01(IR_6_0[1]), .D11(LAA_3_0[1]),
    .D21(CSBIT_15_0[1]), .D02(IR_6_0[2]), .D12(LAA_3_0[2]), .D22(CSBIT_15_0[2]), .D03(IR_6_0[3]),
    .D13(LAA_3_0[3]), .D23(CSBIT_15_0[3]), .A(CSMIS0), .B(not_4_out), .Z0(ILC_MUX_z0[0]), .Z1(ILC_MUX_z0[1]),
    .Z2(ILC_MUX_z0[2]), .Z3(ILC_MUX_z0[3]));
  L8 IRLATCH (
    .A(CD_15_0[0]), .B(CD_15_0[1]), .C(CD_15_0[2]), .D(CD_15_0[3]), .E(CD_15_0[4]), .F(CD_15_0[5]),
    .G(CD_15_0[6]), .L(LDIRV), .QA(IR_6_0[0]), .QB(IR_6_0[1]), .QC(IR_6_0[2]), .QD(IR_6_0[3]),
    .QE(IR_6_0[4]), .QF(IR_6_0[5]), .QG(IR_6_0[6]));  // open: H, QAN, QBN, QCN, QDN, QEN, QFN, QGN, QH, QHN
  or or_1 (or_1_out, CSWAN_1_0[1], CSWAN_1_0[0]);
  not not_11 (not_11_out, UPN);
  nand nand_4 (CIN, or_1_out, not_1_out, 1'b1);
  CGA_MIC_CONDREG CONDREG (
    .CSBIT_11_0(CSBIT_15_0[11:0]), .CSSCOND(CSCOND), .MCLK(MCLK), .LCSN(LCSN), .LCC_3_0(LCC_3_0),
    .FS_6_3(CONDREG_fs_6_3), .TSEL_3_0(CONDREG_tsel_3_0), .ACONDN(ACONDN));
  nor nor_1 (nor_1_out, LC_HI_qa, LC_HI_qb, not_2_out);
  MUX41P M_LAA_2 (
    .D0(CSBIT_15_0[13]), .D1(PIL_3_0[1]), .D2(IR_6_0[5]), .D3(LC_3_0[2]), .A(CSRASEL_1_0[0]),
    .B(CSRASEL_1_0[1]), .Z(M_LAA_2_z));
  // Probe on CONDREG_tsel_3_0
  or or_2 (or_2_out, LC_HI_con, not_11_out);
  nand nand_5 (nand_5_out, LCSN, not_8_out, not_10_out);
  and and_2 (and_2_out, CSEL_condn, not_8_out, LCSN, CSECOND);
  nand nand_6 (nand_6_out, CSEL_condn, nand_5_out);
  nand nand_7 (PN, or_2_out, MIC_LOOP, 1'b1);
  CMP4 LC_CMP (
    .A0(LCC_3_0[0]), .A1(LCC_3_0[1]), .A2(LCC_3_0[2]), .A3(LCC_3_0[3]), .B0(LC_3_0[0]), .B1(LC_3_0[1]),
    .B2(LC_3_0[2]), .B3(LC_3_0[3]), .AEB(LC_CMP_aeb));  // open: AGB, ALB
  and and_3 (and_3_out, nand_6_out, CSTS_6_3[3]);
  and and_4 (and_4_out, and_2_out, CONDREG_fs_6_3[3]);
  and and_5 (and_5_out, nand_6_out, CSTS_6_3[2]);
  and and_6 (and_6_out, and_2_out, CONDREG_fs_6_3[2]);
  and and_7 (and_7_out, nand_6_out, CSTS_6_3[1]);
  and and_8 (and_8_out, and_2_out, CONDREG_fs_6_3[1]);
  and and_9 (and_9_out, nand_6_out, CSTS_6_3[0]);
  and and_10 (and_10_out, and_2_out, CONDREG_fs_6_3[0]);
  not not_12 (not_12_out, MCLK);
  not not_13 (not_13_out, MCLK);
  CGA_MIC_IINC MIC_IINC (.IW_12_0(MIC_MASEL_iw_12_0), .CIN(CIN), .NEXT_12_0(MIC_IINC_next_12_0));
  nand nand_8 (LCZN, nor_1_out, LC_CMP_aeb);
  MUX41P M_LAA_1 (
    .D0(CSBIT_15_0[14]), .D1(PIL_3_0[2]), .D2(IR_6_0[4]), .D3(LC_3_0[1]), .A(CSRASEL_1_0[0]),
    .B(CSRASEL_1_0[1]), .Z(M_LAA_1_z));
  nand nand_9 (nand_9_out, LCSN, CSEL_condn, CSLOOP);
  nor nor_2 (nor_2_out, and_3_out, and_4_out);
  nor nor_3 (nor_3_out, and_5_out, and_6_out);
  nor nor_4 (nor_4_out, and_7_out, and_8_out);
  nor nor_5 (nor_5_out, and_9_out, and_10_out);
  not not_14 (LCZ_t, LCZN);
  D_Flip_Flop #(.trigger("falling")) d_ff_5 (.D(nor_5_out), .clk(MCLK), .Q(d_ff_5_q));  // open: Qn, preset, reset
  D_Flip_Flop d_ff_6 (.D(ZF), .clk(MCLK), .Q(d_ff_6_q), .reset(not_18_out));  // open: Qn, preset
  D_Flip_Flop d_ff_7 (.D(CSALUI8), .clk(MCLK), .Qn(d_ff_7_qn));  // open: Q, preset, reset
  nor nor_6 (nor_6_out, ~LCSN, ~nor_2_out);  // NOR_Gate
  nor nor_7 (nor_7_out, ~nand_9_out, ~nor_3_out);  // NOR_Gate
  CGA_MIC_STACK MIC_STACK (
    .NEXT_12_0(MIC_IINC_next_12_0), .SCLKN(not_13_out), .MCLK(MCLK), .DEEP(DEEP),
    .RET_12_0(MIC_STACK_ret_12_0));  // open: SC3, SC4
  not not_15 (SC_6_3[3], nor_6_out);
  not not_16 (SC_6_3[2], nor_7_out);
  not not_17 (SC_6_3[1], d_ff_5_q);
  D_Flip_Flop #(.trigger("falling")) d_ff_8 (.D(nor_4_out), .clk(MCLK), .Qn(SC_6_3[0]));  // open: Q, preset, reset
  MUX41P M_LAA_0 (
    .D0(CSBIT_15_0[15]), .D1(PIL_3_0[3]), .D2(IR_6_0[3]), .D3(LC_3_0[0]), .A(CSRASEL_1_0[0]),
    .B(CSRASEL_1_0[1]), .Z(M_LAA_0_z));
  and and_11 (and_11_out, d_ff_6_q, ZF);
  not not_18 (not_18_out, CLFFN);
  nor nor_8 (nor_8_out, OOD, MI);
  nor nor_9 (nor_9_out, and_11_out, DZD, 1'b0);
  R41P LAA_REG (
    .A(M_LAA_0_z), .B(M_LAA_1_z), .C(M_LAA_2_z), .D(M_LAA_3_z), .CP(MCLK), .QAN(LAA_REG_qan),
    .QBN(LAA_REG_qbn), .QCN(LAA_REG_qcn), .QDN(LAA_REG_qdn));  // open: QA, QB, QC, QD
  CGA_MIC_MASEL MIC_MASEL (
    .JMP_3_0(ILC_MUX_z0), .CSBIT_11_0(CSBIT_15_0[11:0]), .RET_12_0(MIC_STACK_ret_12_0),
    .NEXT_12_0(MIC_IINC_next_12_0), .SC5(SC_6_3[2]), .SC6(SC_6_3[3]), .CSBIT20(CSBIT20), .MCLK(MCLK),
    .MRN(MRN), .MCLKN(not_12_out), .IW_12_0(MIC_MASEL_iw_12_0), .W_12_0(MIC_MASEL_w_12_0));
  not not_19 (LAA_3_0[0], LAA_REG_qan);
  not not_20 (LAA_3_0[1], LAA_REG_qbn);
  not not_21 (LAA_3_0[2], LAA_REG_qcn);
  not not_22 (LAA_3_0[3], LAA_REG_qdn);
  SCAN_WITH_SET_N OOD_FF (.S(CLFFN), .D(nor_8_out), .TE(d_ff_7_qn), .TI(OOD_FF_q), .CLK(MCLK), .Q(OOD_FF_q), .QN(OOD));
  SCAN_WITH_SET_N DZD_FF (.S(CLFFN), .D(nor_9_out), .TE(d_ff_7_qn), .TI(DZD_FF_q), .CLK(MCLK), .Q(DZD_FF_q), .QN(DZD));
  MUX41P M_LBA_3 (
    .D0(CSRB_3_0[3]), .D1(1'b0), .D2(1'b0), .D3(LC_3_0[3]), .A(CSRBSEL_1_0[0]), .B(CSRBSEL_1_0[1]),
    .Z(M_LBA_3_z));
  CGA_MIC_WCAREG MIC_WCAREG (
    .LWCAN(LWCAN), .LCSN(LCSN), .MCLK(MCLK), .CD_15_0(CD_15_0), .WCSN(WCSN), .WCA_12_0(MIC_WCAREG_wca_12_0));
  MUX41P M_LBA_2 (
    .D0(CSRB_3_0[2]), .D1(IR_6_0[2]), .D2(IR_6_0[5]), .D3(LC_3_0[2]), .A(CSRBSEL_1_0[0]), .B(CSRBSEL_1_0[1]),
    .Z(M_LBA_2_z));
  MUX41P M_LBA_1 (
    .D0(CSRB_3_0[1]), .D1(IR_6_0[1]), .D2(IR_6_0[4]), .D3(LC_3_0[1]), .A(CSRBSEL_1_0[0]), .B(CSRBSEL_1_0[1]),
    .Z(M_LBA_1_z));
  CGA_MIC_IPOS MIC_IPOS (
    .W_12_0(MIC_MASEL_w_12_0), .WCA_12_0(MIC_WCAREG_wca_12_0), .CD_15_0(CD_15_0), .TVEC_3_0(TVEC_3_0),
    .TRAPN(TRAPN), .MAPN(MAPN), .EWCAN(EWCAN), .MA_12_0(MA_12_0));
  MUX41P M_LBA_0 (
    .D0(CSRB_3_0[0]), .D1(IR_6_0[0]), .D2(IR_6_0[3]), .D3(LC_3_0[0]), .A(CSRBSEL_1_0[0]), .B(CSRBSEL_1_0[1]),
    .Z(M_LBA_0_z));
  R41P LBA_REG (
    .A(M_LBA_0_z), .B(M_LBA_1_z), .C(M_LBA_2_z), .D(M_LBA_3_z), .CP(MCLK), .QAN(LBA_REG_qan),
    .QBN(LBA_REG_qbn), .QCN(LBA_REG_qcn), .QDN(LBA_REG_qdn));  // open: QA, QB, QC, QD
  not not_23 (LBA_3_0[0], LBA_REG_qan);
  not not_24 (LBA_3_0[1], LBA_REG_qbn);
  not not_25 (LBA_3_0[2], LBA_REG_qcn);
  not not_26 (LBA_3_0[3], LBA_REG_qdn);

  // Other names for the same wires on the sheet: CSBIT_3_0[3:0] = CSBIT_15_0[3:0];
  //   CSBIT_11_0[11:0] = CSBIT_15_0[11:0]; CSBIT_15_12[3:0] = CSBIT_15_0[15:12]; SC5 = SC_6_3[2]; SC6 = SC_6_3[3]

  // Notes on the sheet:
  //   Notes:
  //   Page 10-14 CGA_MIC (Sheet 1-4)
  //   Sheet 1/4 ->
  //   Sheet 2/4 ->
  //   Sheet 3/4 ->
  //   CSBIT = Microinstruction Bits
  //   LC = Loop Counter
  //   RF(1:0) = Register File selector
  //   Sheet 4/4 ->
  //   IR = Instruction Register (Current MacroInstruction)
  //   CSRASEL0
  //   CD0
  //   LC3
  //   CD3
  //   PIL3
  //   IR6
  //   CSRASEL1
  //   CD0
  //   CD6
  //   CD5
  //   CD4
  //   CD5
  //   CD0
  //   CD1
  //   CD2
  //   CSBIT15
  //   LCSN
  //   IR0
  //   LAA0
  //   CSBIT0
  //   IR3
  //   LAA3
  //   CSBIT3
  //   PIL2
  //   IR5
  //   LC2
  //   A
  //   B
  //   C
  //   D
  //   IR0
  //   IR1
  //   IR2
  //   IR3
  //   IR4
  //   IR5
  //   IR6
  //   LC0
  //   LC1
  //   LC2
  //   LC3
  //   CSBIT14
  //   RF1
  //   RF0
  //   A
  //   B
  //   C
  //   D
  //   IR4
  //   LC1
  //   PIL1
  //   EFALSE
  //   CSTS6
  //   FS6
  //   CSTS5
  //   FS5
  //   CSTS4
  //   FS4
  //   CSTS3
  //   FS3
  //   CSBIT13
  //   ETRUE
  //   CSALUI8
  //   ZF
  //   MCLK
  //   MCLKN
  //   SCLKN
  //   G8C5
  //   PIL0
  //   IR3
  //   LC0
  //   CSBIT12
  //   SC4
  //   SC3
  //   LC3
  //   CSRB3
  //   LAA2
  //   LAA0
  //   LAA1
  //   LAA3
  //   DZD
  //   OOD
  //   DZD
  //   IR5
  //   LC2
  //   IR2
  //   CSRB2
  //   IR4
  //   LC1
  //   IR1
  //   CSRB1
  //   LC0
  //   IR3
  //   IR0
  //   CSRB0
  //   LBA0
  //   LBA1
  //   LBA2
  //   LBA3
endmodule

module CGA_MIC_CSEL (
  input  DZD,
  input  LCZ,
  input  IRQ,
  input  RESTR,
  input  CFETCH,
  input  OOD,
  input  SPARE,
  input  COND,
  input  OVF,
  input  CRY,
  input  F11,
  input  F15,
  input  ZF,
  input  STP,
  input  ALUCLK,
  input  [3:0] TSEL_3_0,
  output CONDN
);

  wire multiplexer_1_out, multiplexer_2_out, multiplexer_3_out, not_1_out, not_2_out;

  Multiplexer #(.select(3)) multiplexer_1 (
    .in0(DZD), .in1(LCZ), .in2(IRQ), .in3(RESTR), .in4(CFETCH), .in5(OOD), .in6(SPARE), .in7(COND),
    .out(multiplexer_1_out), .sel(TSEL_3_0[2:0]));
  Multiplexer #(.select(3)) multiplexer_2 (
    .in0(1'b0), .in1(1'b0), .in2(OVF), .in3(CRY), .in4(F11), .in5(F15), .in6(ZF), .in7(STP),
    .out(multiplexer_2_out), .sel(TSEL_3_0[2:0]));
  Multiplexer multiplexer_3 (
    .in0(multiplexer_1_out), .in1(multiplexer_2_out), .out(multiplexer_3_out), .sel(TSEL_3_0[3]));
  not not_1 (not_1_out, multiplexer_3_out);
  not not_2 (not_2_out, ALUCLK);
  LATCH CSEL_LATCH (.D(not_1_out), .ENABLE(not_2_out), .Q(CONDN));  // open: QN
endmodule

module CGA_MIC_CONDREG (
  input  [11:0] CSBIT_11_0,
  input  CSSCOND,
  input  MCLK,
  input  LCSN,
  output [3:0] LCC_3_0,
  output [3:0] FS_6_3,
  output [3:0] TSEL_3_0,
  output ACONDN
);

  wire CSBIT4_q, CSBIT5_q, CSBIT6_q, CSBIT7_qn, nand_2_out, nand_4_out, nand_5_out, not_1_out, xnor_1_out;

  not not_1 (not_1_out, CSSCOND);
  SCAN_FF CSBIT11 (.D(CSBIT_11_0[11]), .TE(not_1_out), .TI(LCC_3_0[3]), .CLK(MCLK), .Q(LCC_3_0[3]));  // open: QN
  SCAN_FF CSBIT10 (.D(CSBIT_11_0[10]), .TE(not_1_out), .TI(LCC_3_0[2]), .CLK(MCLK), .Q(LCC_3_0[2]));  // open: QN
  SCAN_FF CSBIT9 (.D(CSBIT_11_0[9]), .TE(not_1_out), .TI(LCC_3_0[1]), .CLK(MCLK), .Q(LCC_3_0[1]));  // open: QN
  SCAN_FF CSBIT8 (.D(CSBIT_11_0[8]), .TE(not_1_out), .TI(LCC_3_0[0]), .CLK(MCLK), .Q(LCC_3_0[0]));  // open: QN
  SCAN_FF CSBIT7 (.D(CSBIT_11_0[7]), .TE(not_1_out), .TI(CSBIT7_qn), .CLK(MCLK), .QN(CSBIT7_qn));  // open: Q
  nand nand_1 (TSEL_3_0[3], LCSN, CSBIT7_qn);
  SCAN_FF CSBIT6 (.D(CSBIT_11_0[6]), .TE(not_1_out), .TI(CSBIT6_q), .CLK(MCLK), .Q(CSBIT6_q));  // open: QN
  and and_1 (TSEL_3_0[2], LCSN, CSBIT6_q);
  xnor xnor_1 (xnor_1_out, TSEL_3_0[2], TSEL_3_0[1]);
  nand nand_2 (nand_2_out, xnor_1_out, nand_4_out);
  nand nand_3 (ACONDN, nand_2_out, TSEL_3_0[3]);
  SCAN_FF CSBIT5 (.D(CSBIT_11_0[5]), .TE(not_1_out), .TI(CSBIT5_q), .CLK(MCLK), .Q(CSBIT5_q));  // open: QN
  and and_2 (TSEL_3_0[1], LCSN, CSBIT5_q);
  nand nand_4 (nand_4_out, TSEL_3_0[1], nand_5_out);
  SCAN_FF CSBIT4 (.D(CSBIT_11_0[4]), .TE(not_1_out), .TI(CSBIT4_q), .CLK(MCLK), .Q(CSBIT4_q));  // open: QN
  nand nand_5 (nand_5_out, LCSN, CSBIT4_q);
  not not_2 (TSEL_3_0[0], nand_5_out);
  SCAN_FF CSBIT3 (.D(CSBIT_11_0[3]), .TE(not_1_out), .TI(FS_6_3[3]), .CLK(MCLK), .Q(FS_6_3[3]));  // open: QN
  SCAN_FF CSBIT2 (.D(CSBIT_11_0[2]), .TE(not_1_out), .TI(FS_6_3[2]), .CLK(MCLK), .Q(FS_6_3[2]));  // open: QN
  SCAN_FF CSBIT1 (.D(CSBIT_11_0[1]), .TE(not_1_out), .TI(FS_6_3[1]), .CLK(MCLK), .Q(FS_6_3[1]));  // open: QN
  SCAN_FF CSBIT0 (.D(CSBIT_11_0[0]), .TE(not_1_out), .TI(FS_6_3[0]), .CLK(MCLK), .Q(FS_6_3[0]));  // open: QN

  // Notes on the sheet:
  //   Page  15 - CGA_MIC_CONDREG
  //   Tested ?
  //   LCC3
  //   LCC2
  //   LCC1
  //   LCC0
  //   TSEL3
  //   TSEL2
  //   TSEL1
  //   TSEL0
  //   FS6
  //   FS5
  //   FS4
  //   FS3
endmodule

module CGA_MIC_IINC (
  input  [12:0] IW_12_0,
  input  CIN,
  output [12:0] NEXT_12_0
);

  wire adder_1_cout, adder_2_cout, adder_3_cout, adder_4_cout, adder_6_cout, adder_7_cout, adder_8_cout,
       adder_9_cout, adder_11_cout, adder_12_cout, nand_1_out, nand_2_out, not_1_out, not_2_out;

  Adder #(.width(1)) adder_1 (.a(IW_12_0[0]), .b(CIN), .out(NEXT_12_0[0]), .cout(adder_1_cout));  // open: cin
  Adder #(.width(1)) adder_2 (.a(IW_12_0[1]), .b(adder_1_cout), .out(NEXT_12_0[1]), .cout(adder_2_cout));  // open: cin
  Adder #(.width(1)) adder_3 (.a(IW_12_0[2]), .b(adder_2_cout), .out(NEXT_12_0[2]), .cout(adder_3_cout));  // open: cin
  Adder #(.width(1)) adder_4 (.a(IW_12_0[3]), .b(adder_3_cout), .out(NEXT_12_0[3]), .cout(adder_4_cout));  // open: cin
  Adder #(.width(1)) adder_5 (.a(IW_12_0[4]), .b(adder_4_cout), .out(NEXT_12_0[4]));  // open: cin, cout
  nand nand_1 (nand_1_out, IW_12_0[4], IW_12_0[3], IW_12_0[2], IW_12_0[1], IW_12_0[0], CIN);
  Adder #(.width(1)) adder_6 (.a(IW_12_0[5]), .b(not_1_out), .out(NEXT_12_0[5]), .cout(adder_6_cout));  // open: cin
  not not_1 (not_1_out, nand_1_out);
  Adder #(.width(1)) adder_7 (.a(IW_12_0[6]), .b(adder_6_cout), .out(NEXT_12_0[6]), .cout(adder_7_cout));  // open: cin
  Adder #(.width(1)) adder_8 (.a(IW_12_0[7]), .b(adder_7_cout), .out(NEXT_12_0[7]), .cout(adder_8_cout));  // open: cin
  Adder #(.width(1)) adder_9 (.a(IW_12_0[8]), .b(adder_8_cout), .out(NEXT_12_0[8]), .cout(adder_9_cout));  // open: cin
  Adder #(.width(1)) adder_10 (.a(IW_12_0[9]), .b(adder_9_cout), .out(NEXT_12_0[9]));  // open: cin, cout
  nand nand_2 (nand_2_out, IW_12_0[9], IW_12_0[8], IW_12_0[7], IW_12_0[6], IW_12_0[5], not_1_out);
  not not_2 (not_2_out, nand_2_out);
  Adder #(.width(1)) adder_11 (.a(IW_12_0[10]), .b(not_2_out), .out(NEXT_12_0[10]), .cout(adder_11_cout));  // open: cin
  Adder #(.width(1)) adder_12 (
    .a(IW_12_0[11]), .b(adder_11_cout), .out(NEXT_12_0[11]), .cout(adder_12_cout));  // open: cin
  Adder #(.width(1)) adder_13 (.a(IW_12_0[12]), .b(adder_12_cout), .out(NEXT_12_0[12]));  // open: cin, cout

  // Notes on the sheet:
  //   Page  16 - CGA_MIC_IINC
  //   Tested manually OK 19.05.23 RH
endmodule

module CGA_MIC_STACK (
  input  SC3,
  input  SC4,
  input  [12:0] NEXT_12_0,
  input  SCLKN,
  input  MCLK,
  output DEEP,
  output [12:0] RET_12_0
);

  wire nand_1_out, nand_2_out, nor_1_out, not_1_out, not_2_out, not_3_out, not_4_out, not_5_out, not_6_out,
       not_7_out;

  // Probe on RET_12_0
  not not_1 (not_1_out, SC3);
  not not_2 (not_2_out, SC3);
  not not_3 (not_3_out, SC4);
  not not_4 (not_4_out, not_1_out);
  nand nand_1 (nand_1_out, not_2_out, SC4);
  nand nand_2 (nand_2_out, not_2_out, not_3_out);
  nor nor_1 (nor_1_out, not_2_out, not_3_out);
  not not_5 (not_5_out, nand_1_out);
  not not_6 (not_6_out, nand_2_out);
  not not_7 (not_7_out, nor_1_out);
  CGA_MIC_STACK_BIT12 Bit12 (
    .STIN(NEXT_12_0[12]), .MCLK(MCLK), .S3N(not_2_out), .S4S3N(not_5_out), .S4NS3N(not_6_out),
    .S3(not_4_out), .LOAD(not_7_out), .SCLKN(SCLKN), .STOUT(RET_12_0[12]), .DEEP(DEEP));
  CGA_MIC_STACK_BIT Bit11 (
    .STIN(NEXT_12_0[11]), .CLK(MCLK), .S3N(not_2_out), .S4S3N(not_5_out), .S4NS3N(not_6_out), .S3(not_4_out),
    .LOAD(not_7_out), .CLKN(SCLKN), .STOUT(RET_12_0[11]));
  CGA_MIC_STACK_BIT Bit10 (
    .STIN(NEXT_12_0[10]), .CLK(MCLK), .S3N(not_2_out), .S4S3N(not_5_out), .S4NS3N(not_6_out), .S3(not_4_out),
    .LOAD(not_7_out), .CLKN(SCLKN), .STOUT(RET_12_0[10]));
  CGA_MIC_STACK_BIT Bit9 (
    .STIN(NEXT_12_0[9]), .CLK(MCLK), .S3N(not_2_out), .S4S3N(not_5_out), .S4NS3N(not_6_out), .S3(not_4_out),
    .LOAD(not_7_out), .CLKN(SCLKN), .STOUT(RET_12_0[9]));
  CGA_MIC_STACK_BIT Bit8 (
    .STIN(NEXT_12_0[8]), .CLK(MCLK), .S3N(not_2_out), .S4S3N(not_5_out), .S4NS3N(not_6_out), .S3(not_4_out),
    .LOAD(not_7_out), .CLKN(SCLKN), .STOUT(RET_12_0[8]));
  CGA_MIC_STACK_BIT Bit7 (
    .STIN(NEXT_12_0[7]), .CLK(MCLK), .S3N(not_2_out), .S4S3N(not_5_out), .S4NS3N(not_6_out), .S3(not_4_out),
    .LOAD(not_7_out), .CLKN(SCLKN), .STOUT(RET_12_0[7]));
  CGA_MIC_STACK_BIT Bit6 (
    .STIN(NEXT_12_0[6]), .CLK(MCLK), .S3N(not_2_out), .S4S3N(not_5_out), .S4NS3N(not_6_out), .S3(not_4_out),
    .LOAD(not_7_out), .CLKN(SCLKN), .STOUT(RET_12_0[6]));
  CGA_MIC_STACK_BIT Bit5 (
    .STIN(NEXT_12_0[5]), .CLK(MCLK), .S3N(not_2_out), .S4S3N(not_5_out), .S4NS3N(not_6_out), .S3(not_4_out),
    .LOAD(not_7_out), .CLKN(SCLKN), .STOUT(RET_12_0[5]));
  CGA_MIC_STACK_BIT Bit4 (
    .STIN(NEXT_12_0[4]), .CLK(MCLK), .S3N(not_2_out), .S4S3N(not_5_out), .S4NS3N(not_6_out), .S3(not_4_out),
    .LOAD(not_7_out), .CLKN(SCLKN), .STOUT(RET_12_0[4]));
  CGA_MIC_STACK_BIT Bit3 (
    .STIN(NEXT_12_0[3]), .CLK(MCLK), .S3N(not_2_out), .S4S3N(not_5_out), .S4NS3N(not_6_out), .S3(not_4_out),
    .LOAD(not_7_out), .CLKN(SCLKN), .STOUT(RET_12_0[3]));
  CGA_MIC_STACK_BIT Bit2 (
    .STIN(NEXT_12_0[2]), .CLK(MCLK), .S3N(not_2_out), .S4S3N(not_5_out), .S4NS3N(not_6_out), .S3(not_4_out),
    .LOAD(not_7_out), .CLKN(SCLKN), .STOUT(RET_12_0[2]));
  CGA_MIC_STACK_BIT Bit1 (
    .STIN(NEXT_12_0[1]), .CLK(MCLK), .S3N(not_2_out), .S4S3N(not_5_out), .S4NS3N(not_6_out), .S3(not_4_out),
    .LOAD(not_7_out), .CLKN(SCLKN), .STOUT(RET_12_0[1]));
  CGA_MIC_STACK_BIT Bit0 (
    .STIN(NEXT_12_0[0]), .CLK(MCLK), .S3N(not_2_out), .S4S3N(not_5_out), .S4NS3N(not_6_out), .S3(not_4_out),
    .LOAD(not_7_out), .CLKN(SCLKN), .STOUT(RET_12_0[0]));

  // Notes on the sheet:
  //   Page 17 - CGA_MIC_STACK (tested manually OK 19.05.23 RH)
  //   NEXT0
  //   NEXT12
  //   POP
  //   HOLD
  //   PUSH
  //   LOAD
  //   LOAD
  //   PUSH
  //   POP
  //   HOLD
  //   Function  (Simulates the 74S482)
  //   S3
  //   S4
  //   L
  //   H
  //   H
  //   H
  //   H
  //   L
  //   L
  //   L
endmodule

module CGA_MIC_STACK_BIT (
  input  STIN,
  input  CLK,
  input  S3N,
  input  S4S3N,
  input  S4NS3N,
  input  S3,
  input  LOAD,
  input  CLKN,
  output STOUT
);

  wire d_ff_1_q, nand_1_out, nand_2_out, nand_3_out, nand_4_out, nand_5_out, or_1_out, or_2_out, or_3_out,
       or_4_out, or_5_out, SR44_1_qbn, SR44_1_qcn, SR44_1_qd, SR44_1_qdn;

  D_Flip_Flop d_ff_1 (.D(STIN), .clk(CLK), .Q(d_ff_1_q));  // open: Qn, preset, reset
  nand nand_1 (nand_1_out, d_ff_1_q, S4S3N);
  nand nand_2 (nand_2_out, STOUT, S4NS3N);
  or or_1 (or_1_out, SR44_1_qbn, S3N);
  or or_2 (or_2_out, S3, SR44_1_qbn);
  or or_3 (or_3_out, S3N, SR44_1_qcn);
  or or_4 (or_4_out, S3, SR44_1_qcn);
  or or_5 (or_5_out, S3N, SR44_1_qdn);
  nand nand_3 (nand_3_out, or_1_out, nand_1_out, nand_2_out);
  nand nand_4 (nand_4_out, or_2_out, or_3_out);
  nand nand_5 (nand_5_out, or_4_out, or_5_out);
  SR44 SR44_1 (
    .SI(d_ff_1_q), .A(nand_3_out), .B(nand_4_out), .C(nand_5_out), .D(SR44_1_qd), .L(LOAD), .CP(CLKN),
    .QA(STOUT), .QBN(SR44_1_qbn), .QCN(SR44_1_qcn), .QD(SR44_1_qd), .QDN(SR44_1_qdn));  // open: QAN, QB, QC

  // Notes on the sheet:
  //   S4SN3=1 AND LOAD=1 => HOLD
  //   A
  //   B
  //   C
  //   D
endmodule

module CGA_MIC_STACK_BIT12 (
  input  STIN,
  input  MCLK,
  input  S3N,
  input  S4S3N,
  input  S4NS3N,
  input  S3,
  input  LOAD,
  input  SCLKN,
  output STOUT,
  output DEEP
);

  wire d_ff_1_q, nand_1_out, nand_2_out, nand_3_out, nand_4_out, nand_5_out, or_1_out, or_2_out, or_3_out,
       or_4_out, or_5_out, SR44_2_qbn, SR44_2_qcn, SR44_2_qdn;

  D_Flip_Flop d_ff_1 (.D(STIN), .clk(MCLK), .Q(d_ff_1_q));  // open: Qn, preset, reset
  nand nand_1 (nand_1_out, d_ff_1_q, S4S3N);
  nand nand_2 (nand_2_out, STOUT, S4NS3N);
  or or_1 (or_1_out, SR44_2_qbn, S3N);
  or or_2 (or_2_out, S3, SR44_2_qbn);
  or or_3 (or_3_out, S3N, SR44_2_qcn);
  or or_4 (or_4_out, S3, SR44_2_qcn);
  or or_5 (or_5_out, S3N, SR44_2_qdn);
  nand nand_3 (nand_3_out, or_1_out, nand_1_out, nand_2_out);
  nand nand_4 (nand_4_out, or_2_out, or_3_out);
  nand nand_5 (nand_5_out, or_4_out, or_5_out);
  SR44 SR44_2 (
    .SI(d_ff_1_q), .A(nand_3_out), .B(nand_4_out), .C(nand_5_out), .D(DEEP), .L(LOAD), .CP(SCLKN),
    .QA(STOUT), .QBN(SR44_2_qbn), .QCN(SR44_2_qcn), .QD(DEEP), .QDN(SR44_2_qdn));  // open: QAN, QB, QC

  // Notes on the sheet:
  //   S4SN3=1 AND LOAD=1 => HOLD
  //   A
  //   B
  //   C
  //   D
endmodule

module CGA_MIC_MASEL (
  input  [3:0] JMP_3_0,
  input  [11:0] CSBIT_11_0,
  input  [12:0] RET_12_0,
  input  [12:0] NEXT_12_0,
  input  SC5,
  input  SC6,
  input  CSBIT20,
  input  MCLK,
  input  MRN,
  input  MCLKN,
  output [12:0] IW_12_0,
  output [12:0] W_12_0
);

  wire [12:0] multiplexer_13_out;

  Multiplexer #(.select(2)) multiplexer_1 (
    .in0(CSBIT20), .in1(RET_12_0[12]), .in2(NEXT_12_0[12]), .in3(IW_12_0[12]), .out(multiplexer_13_out[12]),
    .sel({SC6, SC5}));
  Multiplexer #(.select(2)) multiplexer_2 (
    .in0(CSBIT_11_0[11]), .in1(RET_12_0[11]), .in2(NEXT_12_0[11]), .in3(IW_12_0[11]),
    .out(multiplexer_13_out[11]), .sel({SC6, SC5}));
  Multiplexer #(.select(2)) multiplexer_3 (
    .in0(CSBIT_11_0[10]), .in1(RET_12_0[10]), .in2(NEXT_12_0[10]), .in3(IW_12_0[10]),
    .out(multiplexer_13_out[10]), .sel({SC6, SC5}));
  Multiplexer #(.select(2)) multiplexer_4 (
    .in0(CSBIT_11_0[9]), .in1(RET_12_0[9]), .in2(NEXT_12_0[9]), .in3(IW_12_0[9]),
    .out(multiplexer_13_out[9]), .sel({SC6, SC5}));
  Multiplexer #(.select(2)) multiplexer_5 (
    .in0(CSBIT_11_0[8]), .in1(RET_12_0[8]), .in2(NEXT_12_0[8]), .in3(IW_12_0[8]),
    .out(multiplexer_13_out[8]), .sel({SC6, SC5}));
  Multiplexer #(.select(2)) multiplexer_6 (
    .in0(CSBIT_11_0[7]), .in1(RET_12_0[7]), .in2(NEXT_12_0[7]), .in3(IW_12_0[7]),
    .out(multiplexer_13_out[7]), .sel({SC6, SC5}));
  Multiplexer #(.select(2)) multiplexer_7 (
    .in0(CSBIT_11_0[6]), .in1(RET_12_0[6]), .in2(NEXT_12_0[6]), .in3(IW_12_0[6]),
    .out(multiplexer_13_out[6]), .sel({SC6, SC5}));
  Multiplexer #(.select(2)) multiplexer_8 (
    .in0(CSBIT_11_0[5]), .in1(RET_12_0[5]), .in2(NEXT_12_0[5]), .in3(IW_12_0[5]),
    .out(multiplexer_13_out[5]), .sel({SC6, SC5}));
  Multiplexer #(.select(2)) multiplexer_9 (
    .in0(CSBIT_11_0[4]), .in1(RET_12_0[4]), .in2(NEXT_12_0[4]), .in3(IW_12_0[4]),
    .out(multiplexer_13_out[4]), .sel({SC6, SC5}));
  Multiplexer #(.select(2)) multiplexer_10 (
    .in0(JMP_3_0[3]), .in1(RET_12_0[3]), .in2(NEXT_12_0[3]), .in3(IW_12_0[3]), .out(multiplexer_13_out[3]),
    .sel({SC6, SC5}));
  Multiplexer #(.select(2)) multiplexer_11 (
    .in0(JMP_3_0[2]), .in1(RET_12_0[2]), .in2(NEXT_12_0[2]), .in3(IW_12_0[2]), .out(multiplexer_13_out[2]),
    .sel({SC6, SC5}));
  Multiplexer #(.select(2)) multiplexer_12 (
    .in0(JMP_3_0[1]), .in1(RET_12_0[1]), .in2(NEXT_12_0[1]), .in3(IW_12_0[1]), .out(multiplexer_13_out[1]),
    .sel({SC6, SC5}));
  Multiplexer #(.select(2)) multiplexer_13 (
    .in0(JMP_3_0[0]), .in1(RET_12_0[0]), .in2(NEXT_12_0[0]), .in3(IW_12_0[0]), .out(multiplexer_13_out[0]),
    .sel({SC6, SC5}));
  L8 WL_HI (
    .A(multiplexer_13_out[12]), .B(multiplexer_13_out[11]), .C(multiplexer_13_out[10]),
    .D(multiplexer_13_out[9]), .E(multiplexer_13_out[8]), .F(multiplexer_13_out[7]),
    .G(multiplexer_13_out[6]), .H(multiplexer_13_out[5]), .L(MCLKN), .QA(W_12_0[12]), .QB(W_12_0[11]),
    .QC(W_12_0[10]), .QD(W_12_0[9]), .QE(W_12_0[8]), .QF(W_12_0[7]), .QG(W_12_0[6]), .QH(W_12_0[5]));  // open: QAN, QBN, QCN, QDN, QEN, QFN, QGN, QHN
  L8 WL_LO (
    .A(multiplexer_13_out[4]), .B(multiplexer_13_out[3]), .C(multiplexer_13_out[2]),
    .D(multiplexer_13_out[1]), .E(multiplexer_13_out[0]), .L(MCLKN), .QA(W_12_0[4]), .QB(W_12_0[3]),
    .QC(W_12_0[2]), .QD(W_12_0[1]), .QE(W_12_0[0]));  // open: F, G, H, QAN, QBN, QCN, QDN, QEN, QF, QFN, QG, QGN, QH, QHN
  CGA_MIC_MASEL_REPEAT MASEL_REPEAT (.REP_12_0(multiplexer_13_out), .MCLK(MCLK), .MPN(MRN), .IW_12_0(IW_12_0));

  // Other names for the same wires on the sheet: CSBIT_11_4[7:0] = CSBIT_11_0[11:4]

  // Notes on the sheet:
  //   A
  //   B
  //   CSBIT11
  //   CSBIT4
  //   RET12
  //   RET0
  //   NEXT12
  //   NEXT0
  //   IW12
  //   IW0
  //   REP12
  //   REP11
  //   REP10
  //   REP9
  //   REP8
  //   REP7
  //   REP6
  //   REP5
  //   REP4
  //   REP3
  //   REP2
  //   REP1
  //   REP0
endmodule

module CGA_MIC_MASEL_REPEAT (
  input  [12:0] REP_12_0,
  input  MCLK,
  input  MPN,
  output [12:0] IW_12_0
);

  wire not_1_out;

  not not_1 (not_1_out, MPN);
  D_Flip_Flop IWFF12 (.D(REP_12_0[12]), .clk(MCLK), .Q(IW_12_0[12]), .reset(not_1_out));  // open: Qn, preset
  D_Flip_Flop IWFF11 (.D(REP_12_0[11]), .clk(MCLK), .Q(IW_12_0[11]), .reset(not_1_out));  // open: Qn, preset
  D_Flip_Flop IWFF10 (.D(REP_12_0[10]), .clk(MCLK), .Q(IW_12_0[10]), .reset(not_1_out));  // open: Qn, preset
  D_Flip_Flop IWFF9 (.D(REP_12_0[9]), .clk(MCLK), .Q(IW_12_0[9]), .reset(not_1_out));  // open: Qn, preset
  D_Flip_Flop IWFF8 (.D(REP_12_0[8]), .clk(MCLK), .Q(IW_12_0[8]), .reset(not_1_out));  // open: Qn, preset
  D_Flip_Flop IWFF7 (.D(REP_12_0[7]), .clk(MCLK), .Q(IW_12_0[7]), .reset(not_1_out));  // open: Qn, preset
  D_Flip_Flop IWFF6 (.D(REP_12_0[6]), .clk(MCLK), .Q(IW_12_0[6]), .reset(not_1_out));  // open: Qn, preset
  D_Flip_Flop IWFF5 (.D(REP_12_0[5]), .clk(MCLK), .Q(IW_12_0[5]), .reset(not_1_out));  // open: Qn, preset
  D_Flip_Flop IWFF4 (.D(REP_12_0[4]), .clk(MCLK), .Q(IW_12_0[4]), .reset(not_1_out));  // open: Qn, preset
  D_Flip_Flop IWFF3 (.D(REP_12_0[3]), .clk(MCLK), .Q(IW_12_0[3]), .reset(not_1_out));  // open: Qn, preset
  D_Flip_Flop IWFF2 (.D(REP_12_0[2]), .clk(MCLK), .Q(IW_12_0[2]), .reset(not_1_out));  // open: Qn, preset
  D_Flip_Flop IWFF1 (.D(REP_12_0[1]), .clk(MCLK), .Q(IW_12_0[1]), .reset(not_1_out));  // open: Qn, preset
  D_Flip_Flop IWFF0 (.D(REP_12_0[0]), .clk(MCLK), .Q(IW_12_0[0]), .reset(not_1_out));  // open: Qn, preset

  // Notes on the sheet:
  //   Page 20 - CGA_MIC_MASEL_REPEAT
  //   REP12
  //   REP0
  //   IW0
  //   IW12
endmodule

module CGA_MIC_WCAREG (
  input  LWCAN,
  input  LCSN,
  input  MCLK,
  input  [15:0] CD_15_0,
  output WCSN,
  output [12:0] WCA_12_0
);

  wire not_1_out, WCAFF0_q, WCAFF1_q, WCAFF2_q, WCAFF3_q, WCAFF4_q, WCAFF5_q, WCAFF6_q, WCAFF7_q, WCAFF8_q,
       WCAFF9_q, WCAFF10_q, WCAFF11_q, WCSNFF_q;

  not not_1 (not_1_out, LWCAN);
  SCAN_FF WCSNFF (.D(WCSNFF_q), .TE(not_1_out), .TI(CD_15_0[15]), .CLK(MCLK), .Q(WCSNFF_q));  // open: QN
  SCAN_FF WCAFF12 (.D(WCA_12_0[12]), .TE(not_1_out), .TI(CD_15_0[14]), .CLK(MCLK), .Q(WCA_12_0[12]));  // open: QN
  nor nor_1 (WCSN, ~WCSNFF_q, ~LCSN);  // NOR_Gate
  SCAN_FF WCAFF11 (.D(WCAFF11_q), .TE(not_1_out), .TI(CD_15_0[13]), .CLK(MCLK), .Q(WCAFF11_q), .QN(WCA_12_0[11]));
  SCAN_FF WCAFF10 (.D(WCAFF10_q), .TE(not_1_out), .TI(CD_15_0[12]), .CLK(MCLK), .Q(WCAFF10_q), .QN(WCA_12_0[10]));
  SCAN_FF WCAFF9 (.D(WCAFF9_q), .TE(not_1_out), .TI(CD_15_0[11]), .CLK(MCLK), .Q(WCAFF9_q), .QN(WCA_12_0[9]));
  SCAN_FF WCAFF8 (.D(WCAFF8_q), .TE(not_1_out), .TI(CD_15_0[10]), .CLK(MCLK), .Q(WCAFF8_q), .QN(WCA_12_0[8]));
  SCAN_FF WCAFF7 (.D(WCAFF7_q), .TE(not_1_out), .TI(CD_15_0[9]), .CLK(MCLK), .Q(WCAFF7_q), .QN(WCA_12_0[7]));
  SCAN_FF WCAFF6 (.D(WCAFF6_q), .TE(not_1_out), .TI(CD_15_0[8]), .CLK(MCLK), .Q(WCAFF6_q), .QN(WCA_12_0[6]));
  SCAN_FF WCAFF5 (.D(WCAFF5_q), .TE(not_1_out), .TI(CD_15_0[7]), .CLK(MCLK), .Q(WCAFF5_q), .QN(WCA_12_0[5]));
  SCAN_FF WCAFF4 (.D(WCAFF4_q), .TE(not_1_out), .TI(CD_15_0[6]), .CLK(MCLK), .Q(WCAFF4_q), .QN(WCA_12_0[4]));
  SCAN_FF WCAFF3 (.D(WCAFF3_q), .TE(not_1_out), .TI(CD_15_0[5]), .CLK(MCLK), .Q(WCAFF3_q), .QN(WCA_12_0[3]));
  SCAN_FF WCAFF2 (.D(WCAFF2_q), .TE(not_1_out), .TI(CD_15_0[4]), .CLK(MCLK), .Q(WCAFF2_q), .QN(WCA_12_0[2]));
  SCAN_FF WCAFF1 (.D(WCAFF1_q), .TE(not_1_out), .TI(CD_15_0[3]), .CLK(MCLK), .Q(WCAFF1_q), .QN(WCA_12_0[1]));
  SCAN_FF WCAFF0 (.D(WCAFF0_q), .TE(not_1_out), .TI(CD_15_0[2]), .CLK(MCLK), .Q(WCAFF0_q), .QN(WCA_12_0[0]));

  // Notes on the sheet:
  //   CD(15:2)
  //   Page 21 - CGA_MIC_WGAREG
  //   CD15
  //   CD2
endmodule

module CGA_MIC_IPOS (
  input  [12:0] W_12_0,
  input  [12:0] WCA_12_0,
  input  [15:0] CD_15_0,
  input  [3:0] TVEC_3_0,
  input  TRAPN,
  input  MAPN,
  input  EWCAN,
  output [12:0] MA_12_0
);

  wire and_1_out, and_2_out, nand_1_out, not_1_out;
  wire [1:0] nand_2_out, not_3_out;

  not not_1 (not_1_out, EWCAN);
  nand nand_1 (nand_1_out, MAPN, not_1_out);
  nand nand_2 (nand_2_out[0], TRAPN, EWCAN, MAPN);
  nand nand_3 (nand_2_out[1], MAPN, TRAPN);
  and and_1 (and_1_out, MAPN, TRAPN);
  not not_2 (not_3_out[1], and_1_out);
  and and_2 (and_2_out, TRAPN, nand_1_out);
  not not_3 (not_3_out[0], and_2_out);
  Multiplexer #(.select(2)) multiplexer_1 (
    .in0(W_12_0[12]), .in1(WCA_12_0[12]), .in2(1'b1), .in3(1'b0), .out(MA_12_0[12]), .sel(nand_2_out));
  Multiplexer #(.select(2)) multiplexer_2 (
    .in0(W_12_0[11]), .in1(WCA_12_0[11]), .in2(1'b1), .in3(1'b0), .out(MA_12_0[11]), .sel(not_3_out));
  Multiplexer #(.select(2)) multiplexer_3 (
    .in0(W_12_0[10]), .in1(WCA_12_0[10]), .in2(1'b1), .in3(1'b0), .out(MA_12_0[10]), .sel(not_3_out));
  Multiplexer #(.select(2)) multiplexer_4 (
    .in0(W_12_0[9]), .in1(WCA_12_0[9]), .in2(CD_15_0[15]), .in3(1'b0), .out(MA_12_0[9]), .sel(not_3_out));
  Multiplexer #(.select(2)) multiplexer_5 (
    .in0(W_12_0[8]), .in1(WCA_12_0[8]), .in2(CD_15_0[14]), .in3(1'b0), .out(MA_12_0[8]), .sel(not_3_out));
  Multiplexer #(.select(2)) multiplexer_6 (
    .in0(W_12_0[7]), .in1(WCA_12_0[7]), .in2(CD_15_0[13]), .in3(1'b0), .out(MA_12_0[7]), .sel(not_3_out));
  Multiplexer #(.select(2)) multiplexer_7 (
    .in0(W_12_0[6]), .in1(WCA_12_0[6]), .in2(CD_15_0[12]), .in3(1'b0), .out(MA_12_0[6]), .sel(not_3_out));
  Multiplexer #(.select(2)) multiplexer_8 (
    .in0(W_12_0[5]), .in1(WCA_12_0[5]), .in2(CD_15_0[11]), .in3(1'b0), .out(MA_12_0[5]), .sel(not_3_out));
  Multiplexer #(.select(2)) multiplexer_9 (
    .in0(W_12_0[4]), .in1(WCA_12_0[4]), .in2(CD_15_0[10]), .in3(1'b0), .out(MA_12_0[4]), .sel(not_3_out));
  Multiplexer #(.select(2)) multiplexer_10 (
    .in0(W_12_0[3]), .in1(WCA_12_0[3]), .in2(CD_15_0[9]), .in3(TVEC_3_0[3]), .out(MA_12_0[3]), .sel(not_3_out));
  Multiplexer #(.select(2)) multiplexer_11 (
    .in0(W_12_0[2]), .in1(WCA_12_0[2]), .in2(CD_15_0[8]), .in3(TVEC_3_0[2]), .out(MA_12_0[2]), .sel(not_3_out));
  Multiplexer #(.select(2)) multiplexer_12 (
    .in0(W_12_0[1]), .in1(WCA_12_0[1]), .in2(CD_15_0[7]), .in3(TVEC_3_0[1]), .out(MA_12_0[1]), .sel(not_3_out));
  Multiplexer #(.select(2)) multiplexer_13 (
    .in0(W_12_0[0]), .in1(WCA_12_0[0]), .in2(CD_15_0[6]), .in3(TVEC_3_0[0]), .out(MA_12_0[0]), .sel(not_3_out));

  // Notes on the sheet:
  //   Page 22 - CGA_MIC_IPOS
  //   W12
  //   W0
  //   WCA12
  //   WCA0
  //   CD15
  //   CD6
  //   TVEC3
  //   TVEC0
  //   B-Select
  //   A-Select
  //   MA12
  //   MA11
  //   MA10
  //   MA9
  //   MA8
  //   MA7
  //   MA6
  //   MA5
  //   MA4
  //   MA3
  //   MA2
  //   MA1
  //   MA0
endmodule

module CGA_MIC_INCOUNT (
  input  CD0,
  input  LWCAN,
  input  EC,
  input  MRN,
  input  CD1,
  input  MCLK,
  output CSWAN0,
  output CSWAN1
);

  wire d_ff_1_qn, d_ff_2_qn, multiplexer_1_out, multiplexer_2_out, nand_1_out, not_1_out, not_2_out,
       not_3_out, not_4_out, xnor_1_out, xor_1_out;

  xor xor_1 (xor_1_out, EC, d_ff_1_qn);
  nand nand_1 (nand_1_out, d_ff_1_qn, EC);
  xnor xnor_1 (xnor_1_out, nand_1_out, d_ff_2_qn);
  Multiplexer multiplexer_1 (.in0(CD0), .in1(xor_1_out), .out(multiplexer_1_out), .sel(LWCAN));
  Multiplexer multiplexer_2 (.in0(CD1), .in1(xnor_1_out), .out(multiplexer_2_out), .sel(LWCAN));
  not not_1 (not_1_out, multiplexer_1_out);
  not not_2 (not_2_out, multiplexer_2_out);
  not not_3 (not_3_out, MRN);
  not not_4 (not_4_out, MRN);
  D_Flip_Flop d_ff_1 (.D(not_1_out), .clk(MCLK), .Q(CSWAN0), .Qn(d_ff_1_qn), .preset(not_3_out));  // open: reset
  D_Flip_Flop d_ff_2 (.D(not_2_out), .clk(MCLK), .Q(CSWAN1), .Qn(d_ff_2_qn), .preset(not_4_out));  // open: reset

  // Notes on the sheet:
  //   Page 23 - CGA_MIC_INCOUNT
endmodule

module test_MIC (
);

  CGA_MIC cga_mic_1 ();  // open: CSBIT_15_0, CSBIT20, LCZ, MI, IRQ, RESTR, CFETCH, SPARE, OVF, CRY, F11, F15, ZF, STP, ALUCLK, MCLK, CSLOOP, CSECOND, CLFFN, CSALUI8, CSCOND, ILCSN, CSTS_6_3, TVEC_3_0, TRAPN, MAPN, EWCAN, CSMIS0, CSVECT, CD_15_0, LDIRV, LWCAN, MRN, LDLCN, PIL_3_0, CSXRF3, CSRB_3_0, CSRASEL_1_0, CSRBSEL_1_0, DZD, COND, OOD, ACONDN, SC_6_3, MA_12_0, WCSN, DEEP, UPN, PN, LCZN, TN, LAA_3_0, LBA_3_0, RF_1_0
endmodule

module CGA_TRAP (
  input  CBRKN,
  input  ETRAPN,
  input  [6:0] PT_15_9,
  input  [1:0] PCR_1_0,
  input  FETCHN,
  input  WRITEN,
  input  INDN,
  input  INTRQN,
  input  PANN,
  input  VACCN,
  input  PONI,
  input  TCLK,
  input  VTRAPN,
  input  FTRAPN,
  input  DSTOPN,
  output BRKN,
  output TRAPN,
  output RESTR,
  output [3:0] TVEC_3_0,
  output PVIOL
);

  wire TBUF_ifetch, TBUF_ifetchn, TBUF_iind, TBUF_iindn, TBUF_intrq, TBUF_iwrite, TBUF_iwriten, TBUF_pan,
       TBUF_vacc;
  wire [1:0] TBUF_ipcr_1_0, TBUF_ipcr_1_0_n;
  wire [6:0] TBUF_ipt_15_9, TBUF_ipt_15_9_n;

  CGA_TRAP_TBUF TBUF (
    .PT_15_9(PT_15_9), .PCR_1_0(PCR_1_0), .FETCHN(FETCHN), .WRITEN(WRITEN), .INDN(INDN), .INTRQN(INTRQN),
    .PANN(PANN), .VACCN(VACCN), .IPT_15_9_N(TBUF_ipt_15_9_n), .IPT_15_9(TBUF_ipt_15_9),
    .IPCR_1_0_N(TBUF_ipcr_1_0_n), .IPCR_1_0(TBUF_ipcr_1_0), .IFETCH(TBUF_ifetch), .IFETCHN(TBUF_ifetchn),
    .IWRITE(TBUF_iwrite), .IWRITEN(TBUF_iwriten), .IIND(TBUF_iind), .IINDN(TBUF_iindn), .INTRQ(TBUF_intrq),
    .PAN(TBUF_pan), .VACC(TBUF_vacc));
  CGA_TRAP_BRKDET BRKDET (
    .IPT_15_9(TBUF_ipt_15_9), .IPT_15_9_N(TBUF_ipt_15_9_n), .IPCR_1_0(TBUF_ipcr_1_0),
    .IPCR_1_0_N(TBUF_ipcr_1_0_n), .IWRITE(TBUF_iwrite), .IWRITEN(TBUF_iwriten), .IFETCH(TBUF_ifetch),
    .IFETCHN(TBUF_ifetchn), .VACC(TBUF_vacc), .IINDN(TBUF_iindn), .INTRQ(TBUF_intrq), .FTRAPN(FTRAPN),
    .VTRAPN(VTRAPN), .CBRKN(CBRKN), .ETRAPN(ETRAPN), .BRKN(BRKN), .TRAPN(TRAPN));
  CGA_TRAP_TVGEN TVGEN (
    .IPT_15_9(TBUF_ipt_15_9_n), .IPT_15_9_N(TBUF_ipt_15_9), .IPCR_1_0(TBUF_ipcr_1_0_n),
    .IPCR_1_0_N(TBUF_ipcr_1_0), .IWRITE(TBUF_iwrite), .PONI(PONI), .IWRITEN(TBUF_iwriten),
    .IFETCH(TBUF_ifetch), .IFETCHN(TBUF_ifetchn), .VACC(TBUF_vacc), .IIND(TBUF_iind), .IINDN(TBUF_iindn),
    .TCLK(TCLK), .VTRAPN(VTRAPN), .FTRAPN(FTRAPN), .INTRQ(TBUF_intrq), .PAN(TBUF_pan), .DSTOPN(DSTOPN),
    .RESTR(RESTR), .TVEC_3_0(TVEC_3_0), .PVIOL(PVIOL));

  // Notes on the sheet:
  //   Page 100 - /CGA/TRAP - Implemented, not tested
endmodule

module CGA_TRAP_TBUF (
  input  [6:0] PT_15_9,
  input  [1:0] PCR_1_0,
  input  FETCHN,
  input  WRITEN,
  input  INDN,
  input  INTRQN,
  input  PANN,
  input  VACCN,
  output [6:0] IPT_15_9_N,
  output [6:0] IPT_15_9,
  output [1:0] IPCR_1_0_N,
  output [1:0] IPCR_1_0,
  output IFETCH,
  output IFETCHN,
  output IWRITE,
  output IWRITEN,
  output IIND,
  output IINDN,
  output INTRQ,
  output PAN,
  output VACC
);

  not not_1 (IPCR_1_0_N[1], PCR_1_0[1]);
  not not_2 (IFETCH, FETCHN);
  not not_3 (IWRITE, WRITEN);
  not not_4 (IIND, INDN);
  not not_5 (INTRQ, INTRQN);
  not not_6 (PAN, PANN);
  not not_7 (VACC, VACCN);
  not not_8 (IPT_15_9_N[6], PT_15_9[6]);
  not not_9 (IPT_15_9_N[3], PT_15_9[3]);
  not not_10 (IPT_15_9_N[0], PT_15_9[0]);
  not not_11 (IPCR_1_0[1], IPCR_1_0_N[1]);
  not not_12 (IPT_15_9[6], IPT_15_9_N[6]);
  not not_13 (IPT_15_9_N[5], PT_15_9[5]);
  not not_14 (IPT_15_9_N[2], PT_15_9[2]);
  not not_15 (IPT_15_9[0], IPT_15_9_N[0]);
  not not_16 (IPCR_1_0_N[0], PCR_1_0[0]);
  not not_17 (IFETCHN, IFETCH);
  not not_18 (IWRITEN, IWRITE);
  not not_19 (IINDN, IIND);
  not not_20 (IPT_15_9_N[4], PT_15_9[4]);
  not not_21 (IPT_15_9_N[1], PT_15_9[1]);
  not not_22 (IPCR_1_0[0], IPCR_1_0_N[0]);
  not not_23 (IPT_15_9[4], IPT_15_9_N[4]);
  not not_24 (IPT_15_9[1], IPT_15_9_N[1]);

  // Notes on the sheet:
  //   Page 101 - /CGA/TRAP/TBUF - Completed, not tested
  //   IPT15
  //   IPT13
  //   IPT10
  //   IPT9
  //   IPT15N
  //   IPT14N
  //   IPT13N
  //   IPT12N
  //   IPT11N
  //   IPT10N
  //   IPT9N
endmodule

module CGA_TRAP_TVGEN (
  input  [6:0] IPT_15_9,
  input  [6:0] IPT_15_9_N,
  input  [1:0] IPCR_1_0,
  input  [1:0] IPCR_1_0_N,
  input  IWRITE,
  input  PONI,
  input  IWRITEN,
  input  IFETCH,
  input  IFETCHN,
  input  VACC,
  input  IIND,
  input  IINDN,
  input  TCLK,
  input  VTRAPN,
  input  FTRAPN,
  input  INTRQ,
  input  PAN,
  input  DSTOPN,
  output RESTR,
  output [3:0] TVEC_3_0,
  output PVIOL
);

  wire FPVN_out, IPVN_out, LEV1, LEV2, PGF, PGFN_out, PGU, PGUN, RD, RD1N_out, RD2N_out, RD3N_out, RPVN_out,
       RV, RV1N_out, RV2N_out, RV3N_out, WIP, WIPN, WPVN_out;

  nand PGFN (PGFN_out, VACC, IPT_15_9_N[6], IPT_15_9_N[5], IPT_15_9_N[4]);
  nand WPVN (WPVN_out, VACC, IWRITE, IINDN, IFETCHN, IPT_15_9_N[6]);
  nand IPVN (IPVN_out, VACC, IWRITEN, IIND, IFETCHN, IPT_15_9_N[5], IPT_15_9_N[4]);
  nand FPVN (FPVN_out, VACC, IWRITEN, IINDN, IFETCH, IPT_15_9_N[4]);
  nand RPVN (RPVN_out, VACC, IWRITEN, IINDN, IFETCHN, IPT_15_9_N[5]);
  nand RV1N (RV1N_out, VACC, IPT_15_9[1], IPCR_1_0_N[1]);
  nand RV2N (RV2N_out, VACC, IPT_15_9[0], IPCR_1_0_N[1], IPCR_1_0_N[0]);
  nand RV3N (RV3N_out, VACC, IPT_15_9[1], IPT_15_9[0], IPCR_1_0_N[0]);
  not not_1 (PGF, PGFN_out);
  or or_1 (LEV1, ~PGFN_out, ~WPVN_out, ~IPVN_out, ~FPVN_out, ~RPVN_out, ~RV1N_out, ~RV2N_out, ~RV3N_out);  // OR_Gate
  or or_2 (PVIOL, ~PGFN_out, ~WPVN_out, ~IPVN_out, ~FPVN_out, ~RPVN_out);  // OR_Gate
  or or_3 (RV, ~RV3N_out, ~RV2N_out, ~RV1N_out);  // OR_Gate
  nand u_WIPN (WIPN, VACC, IWRITE, IPT_15_9[6], IPT_15_9_N[3]);
  nand u_PGUN (PGUN, VACC, IPT_15_9_N[2]);
  nand RD1N (RD1N_out, VACC, IFETCH, IPT_15_9[4], IPT_15_9_N[1], IPCR_1_0[1]);
  nand RD2N (RD2N_out, VACC, IFETCH, IPT_15_9[4], IPT_15_9_N[1], IPT_15_9_N[0], IPCR_1_0[0]);
  nand RD3N (RD3N_out, VACC, IFETCH, IPT_15_9[4], IPT_15_9_N[0], IPCR_1_0[1], IPCR_1_0[0]);
  not not_2 (PGU, PGUN);
  not not_3 (WIP, WIPN);
  or or_4 (LEV2, ~WIPN, ~PGUN, ~RD1N_out, ~RD2N_out, ~RD3N_out);  // OR_Gate
  or or_5 (RD, ~RD3N_out, ~RD2N_out, ~RD1N_out);  // OR_Gate
  and and_1 (RESTR, IPCR_1_0_N[1], PONI);
  CGA_TRAP_TVGEN_P2 TRAP_TVGEN (
    .LEV2(LEV2), .LEV1(LEV1), .TCLK(TCLK), .RD(RD), .WIPN(WIPN), .PGUN(PGUN), .VTRAPN(VTRAPN), .VACC(VACC),
    .FTRAPN(FTRAPN), .WIP(WIP), .IFETCH(IFETCH), .PGU(PGU), .PGF(PGF), .INTRQ(INTRQ), .PAN(PAN),
    .DSTOPN(DSTOPN), .PVIOL(PVIOL), .RV(RV), .TVEC_3_0(TVEC_3_0));

  // Notes on the sheet:
  //   Page 102 - /CGA/TRAP/TVGEN (1/2) - Completed, not tested
  //   IPT15
  //   IPT9
  //   IPT15N
  //   IPT9N
  //   PGFN
  //   WPVN
  //   IPVN
  //   FPVN
  //   RPVN
endmodule

module CGA_TRAP_TVGEN_P2 (
  input  LEV2,
  input  LEV1,
  input  TCLK,
  input  RD,
  input  WIPN,
  input  PGUN,
  input  VTRAPN,
  input  VACC,
  input  FTRAPN,
  input  WIP,
  input  IFETCH,
  input  PGU,
  input  PGF,
  input  INTRQ,
  input  PAN,
  input  DSTOPN,
  input  PVIOL,
  input  RV,
  output [3:0] TVEC_3_0
);

  wire and_1_out, and_2_out, and_3_out, d_ff_1_qn, d_ff_2_qn, d_ff_3_qn, d_ff_4_q, d_ff_5_qn, d_ff_6_qn,
       d_ff_7_q, multiplexer_1_out, multiplexer_2_out, multiplexer_3_out, nand_1_out, nand_2_out, nand_3_out,
       nand_4_out, nand_5_out, nor_1_out, nor_2_out, not_1_out, not_2_out, not_3_out, not_4_out, not_5_out,
       not_6_out;

  not not_1 (not_1_out, VTRAPN);
  not not_2 (not_2_out, FTRAPN);
  nand nand_1 (nand_1_out, not_1_out, VACC);
  nand nand_2 (nand_2_out, VACC, not_2_out, IFETCH);
  nor nor_1 (nor_1_out, PVIOL, RV);
  and and_1 (and_1_out, nand_1_out, nand_2_out);
  nand nand_3 (nand_3_out, nand_1_out, IFETCH, INTRQ, PAN, DSTOPN);
  not not_3 (not_3_out, PGF);
  not not_4 (not_4_out, nor_1_out);
  nand nand_4 (nand_4_out, RD, WIPN, PGUN);
  nor nor_2 (nor_2_out, WIP, PGU);
  and and_2 (and_2_out, nand_2_out, nand_3_out);
  and and_3 (and_3_out, not_3_out, not_4_out);
  nand nand_5 (nand_5_out, WIPN, PGU);
  D_Flip_Flop d_ff_1 (.D(nand_4_out), .clk(TCLK), .Qn(d_ff_1_qn));  // open: Q, preset, reset
  D_Flip_Flop d_ff_2 (.D(and_1_out), .clk(TCLK), .Qn(d_ff_2_qn));  // open: Q, preset, reset
  D_Flip_Flop d_ff_3 (.D(nor_2_out), .clk(TCLK), .Qn(d_ff_3_qn));  // open: Q, preset, reset
  D_Flip_Flop d_ff_4 (.D(PGF), .clk(TCLK), .Q(d_ff_4_q));  // open: Qn, preset, reset
  D_Flip_Flop d_ff_5 (.D(and_2_out), .clk(TCLK), .Qn(d_ff_5_qn));  // open: Q, preset, reset
  D_Flip_Flop d_ff_6 (.D(nand_5_out), .clk(TCLK), .Qn(d_ff_6_qn));  // open: Q, preset, reset
  D_Flip_Flop d_ff_7 (.D(and_3_out), .clk(TCLK), .Q(d_ff_7_q));  // open: Qn, preset, reset
  not not_5 (not_5_out, LEV2);
  not not_6 (not_6_out, LEV1);
  and and_4 (TVEC_3_0[0], not_5_out, not_6_out);
  Multiplexer #(.select(2)) multiplexer_1 (
    .in0(1'b0), .in1(d_ff_1_qn), .in2(1'b1), .out(multiplexer_1_out), .sel({LEV1, LEV2}));  // open: in3
  Multiplexer #(.select(2)) multiplexer_2 (
    .in0(d_ff_2_qn), .in1(d_ff_3_qn), .in2(d_ff_4_q), .out(multiplexer_2_out), .sel({LEV1, LEV2}));  // open: in3
  Multiplexer #(.select(2)) multiplexer_3 (
    .in0(d_ff_5_qn), .in1(d_ff_6_qn), .in2(d_ff_7_q), .out(multiplexer_3_out), .sel({LEV1, LEV2}));  // open: in3
  not not_7 (TVEC_3_0[1], multiplexer_1_out);
  not not_8 (TVEC_3_0[2], multiplexer_2_out);
  not not_9 (TVEC_3_0[3], multiplexer_3_out);

  // Notes on the sheet:
  //   /CGA/TRAP/TVGEN_P2 - (2/2) Page 104 - Completed, not tested
  //   IVA
  //   IVA
  //   ND2
  //   ND3
  //   VTRPN
  //   NR2
  //   AN2
  //   ND5
  //   PGF
  //   WIPN
  //   PGU
  //   ND3
  //   NR2
  //   AN2
  //   ND2
  //   NR2
  //   L2V2N
  //   L3V1N
  //   L2V1N
  //   L3V0N
  //   L2V0N
  //   L1V0N
  //   L1V1N
  //   TVEC3
  //   TVEC2
  //   TVEC1
  //   TVEC0
endmodule

module CGA_TRAP_BRKDET (
  input  [6:0] IPT_15_9,
  input  [6:0] IPT_15_9_N,
  input  [1:0] IPCR_1_0,
  input  [1:0] IPCR_1_0_N,
  input  IWRITE,
  input  IWRITEN,
  input  IFETCH,
  input  IFETCHN,
  input  VACC,
  input  IINDN,
  input  INTRQ,
  input  FTRAPN,
  input  VTRAPN,
  input  CBRKN,
  input  ETRAPN,
  output BRKN,
  output TRAPN
);

  wire A02_1_z, A02_2_z, A02_3_z, A02_4_z, AN2_1_out, and_1_out, and_2_out, and_3_out, and_4_out, and_5_out,
       and_6_out, and_7_out, and_8_out, and_9_out, INTR_out, IPV_out, nand_1_out, nand_2_out, nor_1_out,
       not_1_out, not_2_out, or_1_out, or_2_out, or_3_out, PGF_out, RD2_out, RV3_out, WIP_out;

  and AN2_1 (AN2_1_out, VACC, IWRITE);
  and and_1 (and_1_out, VACC, IFETCH);
  A02 A02_1 (.A(IPT_15_9_N[4]), .B(and_1_out), .C(IPT_15_9_N[6]), .D(AN2_1_out), .Z(A02_1_z));
  and and_2 (and_2_out, VACC, IWRITEN, IINDN, IFETCHN);
  and and_3 (and_3_out, VACC, IFETCH, IPCR_1_0[1]);
  A02 A02_2 (.A(IPT_15_9_N[2]), .B(VACC), .C(IPT_15_9_N[5]), .D(and_2_out), .Z(A02_2_z));
  or or_1 (or_1_out, ~A02_1_z, ~A02_2_z, ~A02_3_z, ~A02_4_z);  // OR_Gate
  A02 A02_3 (.A(IPT_15_9_N[0]), .B(and_4_out), .C(IPT_15_9_N[1]), .D(and_3_out), .Z(A02_3_z));
  and and_4 (and_4_out, VACC, IFETCH, IPCR_1_0[1], IPCR_1_0[0]);
  and and_5 (and_5_out, VACC, IPCR_1_0_N[1]);
  and and_6 (and_6_out, VACC, IPCR_1_0_N[1], IPCR_1_0_N[0]);
  A02 A02_4 (.A(IPT_15_9[0]), .B(and_6_out), .C(IPT_15_9[1]), .D(and_5_out), .Z(A02_4_z));
  nand IPV (IPV_out, VACC, IPT_15_9_N[5], IPT_15_9_N[4]);
  and and_7 (and_7_out, VACC, IWRITE);
  nand WIP (WIP_out, and_7_out, IPT_15_9[6], IPT_15_9[3]);
  and and_8 (and_8_out, VACC, IFETCH, IPCR_1_0[0]);
  or or_2 (or_2_out, ~IPV_out, ~WIP_out, ~RD2_out, ~RV3_out);  // OR_Gate
  nand RD2 (RD2_out, and_8_out, IPT_15_9_N[1], IPT_15_9_N[0]);
  and and_9 (and_9_out, VACC, IPCR_1_0_N[0]);
  nand RV3 (RV3_out, and_9_out, IPT_15_9[1], IPT_15_9[0]);
  nand PGF (PGF_out, VACC, IPT_15_9_N[6], IPT_15_9_N[5], IPT_15_9_N[4]);
  or or_3 (or_3_out, ~PGF_out, ~INTR_out, ~nand_1_out, ~nand_2_out);  // OR_Gate
  nand INTR (INTR_out, IFETCH, INTRQ);
  nor nor_1 (nor_1_out, or_3_out, or_2_out, or_1_out);
  not not_1 (not_1_out, VTRAPN);
  nand nand_1 (nand_1_out, not_1_out, VACC);
  nor nor_2 (BRKN, ~nor_1_out, ~CBRKN);  // NOR_Gate
  not not_2 (not_2_out, CBRKN);
  nand nand_2 (nand_2_out, ~FTRAPN, ~IFETCHN);  // NAND_Gate
  nand nand_3 (TRAPN, ~BRKN, ~not_2_out, ~ETRAPN);  // NAND_Gate

  // Notes on the sheet:
  //   Page 103 - /CGA/TRAP/BRKDET - Partly
  //   SPARE VACC TRAP
  //   SPARE FETCH TRAP
endmodule

module CGA_WRF (
  input  BDEST,
  input  [3:0] LBA_3_0,
  input  [3:0] LAA_3_0,
  input  ALUCLK,
  input  [15:0] RB_15_0,
  input  [15:0] NLCA_15_0,
  input  XFETCHN,
  output WPN,
  output WR3,
  output WR7,
  output [15:0] B_15_0,
  output [15:0] A_15_0,
  output [15:0] PR_15_0,
  output [15:0] BR_15_0,
  output [15:0] XR_15_0,
  output [15:0] EA_15_0
);

  wire LAA_HI_z0, LAA_HI_z1, LAA_HI_z2, LAA_HI_z3, LAA_HI_z4, LAA_HI_z5, LAA_HI_z6, LAA_HI_z7, LAA_LO_z0,
       LAA_LO_z1, LAA_LO_z2, LAA_LO_z3, LAA_LO_z4, LAA_LO_z5, LAA_LO_z6, LAA_LO_z7, LBA_HI_z0, LBA_HI_z1,
       LBA_HI_z2, LBA_HI_z3, LBA_HI_z4, LBA_HI_z5, LBA_HI_z6, LBA_HI_z7, LBA_LO_z0, LBA_LO_z1, LBA_LO_z2,
       LBA_LO_z3, LBA_LO_z4, LBA_LO_z5, LBA_LO_z6, LBA_LO_z7, nand_1_out, nand_2_out, nand_4_out, nand_5_out,
       nand_6_out, nand_7_out, nand_8_out, nand_9_out, nand_10_out, nand_11_out, nand_12_out, nand_13_out,
       nand_14_out, nand_15_out, nand_16_out, not_1_out, not_2_out, not_3_out;
  wire [15:0] EB_15_0, WR_15_0;

  not not_1 (not_1_out, LBA_3_0[3]);
  not not_2 (not_2_out, LAA_3_0[3]);
  not not_3 (not_3_out, ALUCLK);
  ND38GLP LBA_LO (
    .A(LBA_3_0[0]), .B(LBA_3_0[1]), .C(LBA_3_0[2]), .G(not_1_out), .Z0(LBA_LO_z0), .Z1(LBA_LO_z1),
    .Z2(LBA_LO_z2), .Z3(LBA_LO_z3), .Z4(LBA_LO_z4), .Z5(LBA_LO_z5), .Z6(LBA_LO_z6), .Z7(LBA_LO_z7));
  ND38GLP LBA_HI (
    .A(LBA_3_0[0]), .B(LBA_3_0[1]), .C(LBA_3_0[2]), .G(LBA_3_0[3]), .Z0(LBA_HI_z0), .Z1(LBA_HI_z1),
    .Z2(LBA_HI_z2), .Z3(LBA_HI_z3), .Z4(LBA_HI_z4), .Z5(LBA_HI_z5), .Z6(LBA_HI_z6), .Z7(LBA_HI_z7));
  ND38GLP LAA_LO (
    .A(LAA_3_0[0]), .B(LAA_3_0[1]), .C(LAA_3_0[2]), .G(not_2_out), .Z0(LAA_LO_z0), .Z1(LAA_LO_z1),
    .Z2(LAA_LO_z2), .Z3(LAA_LO_z3), .Z4(LAA_LO_z4), .Z5(LAA_LO_z5), .Z6(LAA_LO_z6), .Z7(LAA_LO_z7));
  ND38GLP LAA_HI (
    .A(LAA_3_0[0]), .B(LAA_3_0[1]), .C(LAA_3_0[2]), .G(LAA_3_0[3]), .Z0(LAA_HI_z0), .Z1(LAA_HI_z1),
    .Z2(LAA_HI_z2), .Z3(LAA_HI_z3), .Z4(LAA_HI_z4), .Z5(LAA_HI_z5), .Z6(LAA_HI_z6), .Z7(LAA_HI_z7));
  not not_4 (EB_15_0[0], LBA_LO_z0);
  not not_5 (EB_15_0[1], LBA_LO_z1);
  not not_6 (EB_15_0[2], LBA_LO_z2);
  not not_7 (EB_15_0[3], LBA_LO_z3);
  not not_8 (EB_15_0[4], LBA_LO_z4);
  not not_9 (EB_15_0[5], LBA_LO_z5);
  not not_10 (EB_15_0[6], LBA_LO_z6);
  not not_11 (EB_15_0[7], LBA_LO_z7);
  not not_12 (EB_15_0[8], LBA_HI_z0);
  not not_13 (EB_15_0[9], LBA_HI_z1);
  not not_14 (EB_15_0[10], LBA_HI_z2);
  not not_15 (EB_15_0[11], LBA_HI_z3);
  not not_16 (EB_15_0[12], LBA_HI_z4);
  not not_17 (EB_15_0[13], LBA_HI_z5);
  not not_18 (EB_15_0[14], LBA_HI_z6);
  not not_19 (EB_15_0[15], LBA_HI_z7);
  not not_20 (EA_15_0[0], LAA_LO_z0);
  not not_21 (EA_15_0[1], LAA_LO_z1);
  not not_22 (EA_15_0[2], LAA_LO_z2);
  not not_23 (EA_15_0[3], LAA_LO_z3);
  not not_24 (EA_15_0[4], LAA_LO_z4);
  not not_25 (EA_15_0[5], LAA_LO_z5);
  not not_26 (EA_15_0[6], LAA_LO_z6);
  not not_27 (EA_15_0[7], LAA_LO_z7);
  not not_28 (EA_15_0[8], LAA_HI_z0);
  not not_29 (EA_15_0[9], LAA_HI_z1);
  not not_30 (EA_15_0[10], LAA_HI_z2);
  not not_31 (EA_15_0[11], LAA_HI_z3);
  not not_32 (EA_15_0[12], LAA_HI_z4);
  not not_33 (EA_15_0[13], LAA_HI_z5);
  not not_34 (EA_15_0[14], LAA_HI_z6);
  not not_35 (EA_15_0[15], LAA_HI_z7);
  CGA_WRF_RBLOCK RBLOCK (
    .EA_15_0(EA_15_0), .EB_15_0(EB_15_0), .ALUCLK(ALUCLK), .RB_15_0(RB_15_0),
    .WR_15_0({WR_15_0[15:8], WR7, WR_15_0[6:4], WR3, WR_15_0[2:0]}), .NLCA_15_0(NLCA_15_0),
    .XFETCHN(XFETCHN), .ALUCLKN(not_3_out), .B_15_0(B_15_0), .A_15_0(A_15_0), .PR_15_0(PR_15_0),
    .BR_15_0(BR_15_0), .XR_15_0(XR_15_0));
  // Probe on EA_15_0
  nand nand_1 (nand_1_out, BDEST, EB_15_0[0]);
  not not_36 (WR_15_0[0], nand_1_out);
  nand nand_2 (nand_2_out, BDEST, EB_15_0[1]);
  not not_37 (WR_15_0[1], nand_2_out);
  nand nand_3 (WPN, BDEST, EB_15_0[2]);
  not not_38 (WR_15_0[2], WPN);
  nand nand_4 (nand_4_out, BDEST, EB_15_0[3]);
  not not_39 (WR3, nand_4_out);
  nand nand_5 (nand_5_out, BDEST, EB_15_0[4]);
  not not_40 (WR_15_0[4], nand_5_out);
  nand nand_6 (nand_6_out, BDEST, EB_15_0[5]);
  not not_41 (WR_15_0[5], nand_6_out);
  nand nand_7 (nand_7_out, BDEST, EB_15_0[6]);
  not not_42 (WR_15_0[6], nand_7_out);
  nand nand_8 (nand_8_out, BDEST, EB_15_0[7]);
  not not_43 (WR7, nand_8_out);
  nand nand_9 (nand_9_out, BDEST, EB_15_0[8]);
  nand nand_10 (nand_10_out, BDEST, EB_15_0[9]);
  nand nand_11 (nand_11_out, BDEST, EB_15_0[10]);
  nand nand_12 (nand_12_out, BDEST, EB_15_0[11]);
  nand nand_13 (nand_13_out, BDEST, EB_15_0[12]);
  nand nand_14 (nand_14_out, BDEST, EB_15_0[13]);
  nand nand_15 (nand_15_out, BDEST, EB_15_0[14]);
  nand nand_16 (nand_16_out, BDEST, EB_15_0[15]);
  not not_44 (WR_15_0[8], nand_9_out);
  not not_45 (WR_15_0[9], nand_10_out);
  not not_46 (WR_15_0[10], nand_11_out);
  not not_47 (WR_15_0[11], nand_12_out);
  not not_48 (WR_15_0[12], nand_13_out);
  not not_49 (WR_15_0[13], nand_14_out);
  not not_50 (WR_15_0[14], nand_15_out);
  not not_51 (WR_15_0[15], nand_16_out);
  // Probe on {WR_15_0[15:8], WR7, WR_15_0[6:4], WR3, WR_15_0[2:0]}
  // Probe on EB_15_0

  // Other names for the same wires on the sheet: WR_15_0 (some bits) = {WR7, WR3}

  // Notes on the sheet:
  //   Page 59 - CGA_ALU_WRF
  //   LBA0
  //   LBA1
  //   LBA2
  //   LBA3
  //   LBA0
  //   LBA1
  //   LBA2
  //   LBA3
  //   LAA0
  //   LAA1
  //   LAA2
  //   LAA3
  //   LAA0
  //   LAA1
  //   LAA2
  //   LAA3
  //   EB0
  //   EB15
  //   EA0
  //   EA15
endmodule

module CGA_WRF_RBLOCK (
  input  [15:0] EA_15_0,
  input  [15:0] EB_15_0,
  input  ALUCLK,
  input  [15:0] RB_15_0,
  input  [15:0] WR_15_0,
  input  [15:0] NLCA_15_0,
  input  XFETCHN,
  input  ALUCLKN,
  output [15:0] B_15_0,
  output [15:0] A_15_0,
  output [15:0] PR_15_0,
  output [15:0] BR_15_0,
  output [15:0] XR_15_0
);

  wire AR0, AR1, AR2, AR3, AR4, AR5, AR6, AR7, AR8, AR9, AR10, AR11, AR12, AR13, AR14, AR15, C0, C1, C2, C3,
       C4, C5, C6, C7, C8, C9, C10, C11, C12, C13, C14, C15, D0, D1, D2, D3, D4, D5, D6, D7, D8, D9, D10,
       D11, D12, D13, D14, D15, IB0, IB1, IB2, IB3, IB4, IB5, IB6, IB7, IB8, IB9, IB10, IB11, IB12, IB13,
       IB14, IB15, P0, P1, P2, P3, P4, P5, P6, P7, P8, P9, P10, P11, P12, P13, P14, P15, R10, R11, R12, R13,
       R14, R15, R16, R17, R18, R19, R20, R21, R22, R23, R24, R25, R26, R27, R28, R29, R30, R31, R32, R33,
       R34, R35, R36, R37, R38, R39, R40, R41, R42, R43, R44, R45, R46, R47, R48, R49, R50, R51, R52, R53,
       R54, R55, R56, R57, R58, R59, R60, R61, R62, R63, R64, R65, R66, R67, R68, R69, R70, R71, R72, R73,
       R74, R75, R76, R77, R78, R79, R110, R111, R112, R113, R114, R115, R210, R211, R212, R213, R214, R215,
       R310, R311, R312, R313, R314, R315, R410, R411, R412, R413, R414, R415, R510, R511, R512, R513, R514,
       R515, R610, R611, R612, R613, R614, R615, R710, R711, R712, R713, R714, R715, STS0, STS1, STS2, STS3,
       STS4, STS5, STS6, STS7, STS8, STS9, STS10, STS11, STS12, STS13, STS14, STS15, T0, T1, T2, T3, T4, T5,
       T6, T7, T8, T9, T10, T11, T12, T13, T14, T15, X0, X1, X2, X3, X4, X5, X6, X7, X8, X9, X10, X11, X12,
       X13, X14, X15, Z0, Z1, Z2, Z3, Z4, Z5, Z6, Z7, Z8, Z9, Z10, Z11, Z12, Z13, Z14, Z15;

  CGA_WRF_RBLOCK_DR16 Z_REG_0 (
    .ALUCLK(ALUCLK), .WR(WR_15_0[0]), .RB_15_0(RB_15_0),
    .REG_15_0({Z15, Z14, Z13, Z12, Z11, Z10, Z9, Z8, Z7, Z6, Z5, Z4, Z3, Z2, Z1, Z0}));
  CGA_WRF_RBLOCK_DR16 D_REG_1 (
    .ALUCLK(ALUCLK), .WR(WR_15_0[1]), .RB_15_0(RB_15_0),
    .REG_15_0({D15, D14, D13, D12, D11, D10, D9, D8, D7, D6, D5, D4, D3, D2, D1, D0}));
  // Probe on {P15, P14, P13, P12, P11, P10, P9, P8, P7, P6, P5, P4, P3, P2, P1, P0}
  CGA_WRF_RBLOCK_PREG P_REG_2 (
    .NLCA_15_0(NLCA_15_0), .RB_15_0(RB_15_0), .XFETCHN(XFETCHN), .WR2(WR_15_0[2]), .ALUCLKN(ALUCLKN),
    .ALUCLK(ALUCLK), .P_15_0({P15, P14, P13, P12, P11, P10, P9, P8, P7, P6, P5, P4, P3, P2, P1, P0}),
    .PR_15_0(PR_15_0));
  CGA_WRF_RBLOCK_LR16 B_REG_3 (
    .RB_15_0(RB_15_0), .ALUCLK(ALUCLK), .WR(WR_15_0[3]),
    .R_15_0({IB15, IB14, IB13, IB12, IB11, IB10, IB9, IB8, IB7, IB6, IB5, IB4, IB3, IB2, IB1, IB0}),
    .LR_15_0(BR_15_0));
  CGA_WRF_RBLOCK_DR16 L_REG_4 (
    .ALUCLK(ALUCLK), .WR(WR_15_0[4]), .RB_15_0(RB_15_0),
    .REG_15_0({C15, C14, C13, C12, C11, C10, C9, C8, C7, C6, C5, C4, C3, C2, C1, C0}));
  CGA_WRF_RBLOCK_DR16 A_REG_5 (
    .ALUCLK(ALUCLK), .WR(WR_15_0[5]), .RB_15_0(RB_15_0),
    .REG_15_0({AR15, AR14, AR13, AR12, AR11, AR10, AR9, AR8, AR7, AR6, AR5, AR4, AR3, AR2, AR1, AR0}));
  CGA_WRF_RBLOCK_DR16 T_REG_6 (
    .ALUCLK(ALUCLK), .WR(WR_15_0[6]), .RB_15_0(RB_15_0),
    .REG_15_0({T15, T14, T13, T12, T11, T10, T9, T8, T7, T6, T5, T4, T3, T2, T1, T0}));
  CGA_WRF_RBLOCK_LR16 X_REG_7 (
    .RB_15_0(RB_15_0), .ALUCLK(ALUCLK), .WR(WR_15_0[7]),
    .R_15_0({X15, X14, X13, X12, X11, X10, X9, X8, X7, X6, X5, X4, X3, X2, X1, X0}), .LR_15_0(XR_15_0));
  CGA_WRF_RBLOCK_DR16 STS_REG_8 (
    .ALUCLK(ALUCLK), .WR(WR_15_0[8]), .RB_15_0(RB_15_0),
    .REG_15_0({STS15, STS14, STS13, STS12, STS11, STS10, STS9, STS8, STS7, STS6, STS5, STS4, STS3, STS2, STS1, STS0}));
  CGA_WRF_RBLOCK_DR16 R1_REG_9 (
    .ALUCLK(ALUCLK), .WR(WR_15_0[9]), .RB_15_0(RB_15_0),
    .REG_15_0({R115, R114, R113, R112, R111, R110, R19, R18, R17, R16, R15, R14, R13, R12, R11, R10}));
  CGA_WRF_RBLOCK_DR16 R2_REG_10 (
    .ALUCLK(ALUCLK), .WR(WR_15_0[10]), .RB_15_0(RB_15_0),
    .REG_15_0({R215, R214, R213, R212, R211, R210, R29, R28, R27, R26, R25, R24, R23, R22, R21, R20}));
  CGA_WRF_RBLOCK_DR16 R3_REG_11 (
    .ALUCLK(ALUCLK), .WR(WR_15_0[11]), .RB_15_0(RB_15_0),
    .REG_15_0({R315, R314, R313, R312, R311, R310, R39, R38, R37, R36, R35, R34, R33, R32, R31, R30}));
  CGA_WRF_RBLOCK_DR16 R4_REG_12 (
    .ALUCLK(ALUCLK), .WR(WR_15_0[12]), .RB_15_0(RB_15_0),
    .REG_15_0({R415, R414, R413, R412, R411, R410, R49, R48, R47, R46, R45, R44, R43, R42, R41, R40}));
  CGA_WRF_RBLOCK_DR16 R5_REG_13 (
    .ALUCLK(ALUCLK), .WR(WR_15_0[13]), .RB_15_0(RB_15_0),
    .REG_15_0({R515, R514, R513, R512, R511, R510, R59, R58, R57, R56, R55, R54, R53, R52, R51, R50}));
  CGA_WRF_RBLOCK_DR16 R6_REG_14 (
    .ALUCLK(ALUCLK), .WR(WR_15_0[14]), .RB_15_0(RB_15_0),
    .REG_15_0({R615, R614, R613, R612, R611, R610, R69, R68, R67, R66, R65, R64, R63, R62, R61, R60}));
  CGA_WRF_RBLOCK_DR16 R7_REG_15 (
    .ALUCLK(ALUCLK), .WR(WR_15_0[15]), .RB_15_0(RB_15_0),
    .REG_15_0({R715, R714, R713, R712, R711, R710, R79, R78, R77, R76, R75, R74, R73, R72, R71, R70}));
  // Probe on {Z15, Z14, Z13, Z12, Z11, Z10, Z9, Z8, Z7, Z6, Z5, Z4, Z3, Z2, Z1, Z0}
  // Probe on PR_15_0
  // Probe on {IB15, IB14, IB13, IB12, IB11, IB10, IB9, IB8, IB7, IB6, IB5, IB4, IB3, IB2, IB1, IB0}
  CGA_WRF_RBLOCK_SEL16 SEL_0 (
    .SI_15_0({R70, R60, R50, R40, R30, R20, R10, STS0, X0, T0, AR0, C0, IB0, P0, D0, Z0}), .EA_15_0(EA_15_0),
    .EB_15_0(EB_15_0), .PA(A_15_0[0]), .PB(B_15_0[0]));
  CGA_WRF_RBLOCK_SEL16 SEL_1 (
    .SI_15_0({R71, R61, R51, R41, R31, R21, R11, STS1, X1, T1, AR1, C1, IB1, P1, D1, Z1}), .EA_15_0(EA_15_0),
    .EB_15_0(EB_15_0), .PA(A_15_0[1]), .PB(B_15_0[1]));
  CGA_WRF_RBLOCK_SEL16 SEL_4 (
    .SI_15_0({R74, R64, R54, R44, R34, R24, R14, STS4, X4, T4, AR4, C4, IB4, P4, D4, Z4}), .EA_15_0(EA_15_0),
    .EB_15_0(EB_15_0), .PA(A_15_0[4]), .PB(B_15_0[4]));
  CGA_WRF_RBLOCK_SEL16 SEL_5 (
    .SI_15_0({R75, R65, R55, R45, R35, R25, R15, STS5, X5, T5, AR5, C5, IB5, P5, D5, Z5}), .EA_15_0(EA_15_0),
    .EB_15_0(EB_15_0), .PA(A_15_0[5]), .PB(B_15_0[5]));
  CGA_WRF_RBLOCK_SEL16 SEL_2 (
    .SI_15_0({R72, R62, R52, R42, R32, R22, R12, STS2, X2, T2, AR2, C2, IB2, P2, D2, Z2}), .EA_15_0(EA_15_0),
    .EB_15_0(EB_15_0), .PA(A_15_0[2]), .PB(B_15_0[2]));
  CGA_WRF_RBLOCK_SEL16 SEL_3 (
    .SI_15_0({R73, R63, R53, R43, R33, R23, R13, STS3, X3, T3, AR3, C3, IB3, P3, D3, Z3}), .EA_15_0(EA_15_0),
    .EB_15_0(EB_15_0), .PA(A_15_0[3]), .PB(B_15_0[3]));
  CGA_WRF_RBLOCK_SEL16 SEL_6 (
    .SI_15_0({R76, R66, R56, R46, R36, R26, R16, STS6, X6, T6, AR6, C6, IB6, P6, D6, Z6}), .EA_15_0(EA_15_0),
    .EB_15_0(EB_15_0), .PA(A_15_0[6]), .PB(B_15_0[6]));
  CGA_WRF_RBLOCK_SEL16 SEL_7 (
    .SI_15_0({R77, R67, R57, R47, R37, R27, R17, STS7, X7, T7, AR7, C7, IB7, P7, D7, Z7}), .EA_15_0(EA_15_0),
    .EB_15_0(EB_15_0), .PA(A_15_0[7]), .PB(B_15_0[7]));
  CGA_WRF_RBLOCK_SEL16 SEL_8 (
    .SI_15_0({R78, R68, R58, R48, R38, R28, R18, STS8, X8, T8, AR8, C8, IB8, P8, D8, Z8}), .EA_15_0(EA_15_0),
    .EB_15_0(EB_15_0), .PA(A_15_0[8]), .PB(B_15_0[8]));
  CGA_WRF_RBLOCK_SEL16 SEL_9 (
    .SI_15_0({R79, R69, R59, R49, R39, R29, R19, STS9, X9, T9, AR9, C9, IB9, P9, D9, Z9}), .EA_15_0(EA_15_0),
    .EB_15_0(EB_15_0), .PA(A_15_0[9]), .PB(B_15_0[9]));
  CGA_WRF_RBLOCK_SEL16 SEL_10 (
    .SI_15_0({R710, R610, R510, R410, R310, R210, R110, STS10, X10, T10, AR10, C10, IB10, P10, D10, Z10}),
    .EA_15_0(EA_15_0), .EB_15_0(EB_15_0), .PA(A_15_0[10]), .PB(B_15_0[10]));
  CGA_WRF_RBLOCK_SEL16 SEL_11 (
    .SI_15_0({R711, R611, R511, R411, R311, R211, R111, STS11, X11, T11, AR11, C11, IB11, P11, D11, Z11}),
    .EA_15_0(EA_15_0), .EB_15_0(EB_15_0), .PA(A_15_0[11]), .PB(B_15_0[11]));
  CGA_WRF_RBLOCK_SEL16 SEL_12 (
    .SI_15_0({R712, R612, R512, R412, R312, R212, R112, STS12, X12, T12, AR12, C12, IB12, P12, D12, Z12}),
    .EA_15_0(EA_15_0), .EB_15_0(EB_15_0), .PA(A_15_0[12]), .PB(B_15_0[12]));
  CGA_WRF_RBLOCK_SEL16 SEL_13 (
    .SI_15_0({R713, R613, R513, R413, R313, R213, R113, STS13, X13, T13, AR13, C13, IB13, P13, D13, Z13}),
    .EA_15_0(EA_15_0), .EB_15_0(EB_15_0), .PA(A_15_0[13]), .PB(B_15_0[13]));
  CGA_WRF_RBLOCK_SEL16 SEL_14 (
    .SI_15_0({R714, R614, R514, R414, R314, R214, R114, STS14, X14, T14, AR14, C14, IB14, P14, D14, Z14}),
    .EA_15_0(EA_15_0), .EB_15_0(EB_15_0), .PA(A_15_0[14]), .PB(B_15_0[14]));
  CGA_WRF_RBLOCK_SEL16 SEL_15 (
    .SI_15_0({R715, R615, R515, R415, R315, R215, R115, STS15, X15, T15, AR15, C15, IB15, P15, D15, Z15}),
    .EA_15_0(EA_15_0), .EB_15_0(EB_15_0), .PA(A_15_0[15]), .PB(B_15_0[15]));
  // Probe on B_15_0[2]

  // Other names for the same wires on the sheet: A0 = A_15_0[0]; A1 = A_15_0[1]; A2 = A_15_0[2]; A3 = A_15_0[3];
  //   A4 = A_15_0[4]; A5 = A_15_0[5]; A6 = A_15_0[6]; A7 = A_15_0[7]; A8 = A_15_0[8]; A9 = A_15_0[9];
  //   A10 = A_15_0[10]; A11 = A_15_0[11]; A12 = A_15_0[12]; A13 = A_15_0[13]; A14 = A_15_0[14]; A15 = A_15_0[15];
  //   B0 = B_15_0[0]; B1 = B_15_0[1]; B2 = B_15_0[2]; B3 = B_15_0[3]; B4 = B_15_0[4]; B5 = B_15_0[5]; B6 = B_15_0[6];
  //   B7 = B_15_0[7]; B8 = B_15_0[8]; B9 = B_15_0[9]; B10 = B_15_0[10]; B11 = B_15_0[11]; B12 = B_15_0[12];
  //   B13 = B_15_0[13]; B14 = B_15_0[14]; B15 = B_15_0[15]

  // Notes on the sheet:
  //   Page 60 - CGA_ALU_WRF_RBLOCK
  //   WR0
  //   WR1
  //   WR2
  //   WR3
  //   WR4
  //   WR5
  //   WR6
  //   WR7
  //   WR8
  //   WR9
  //   WR11
  //   WR10
  //   WR12
  //   WR13
  //   WR14
  //   WR15
endmodule

module CGA_WRF_RBLOCK_SEL16 (
  input  [15:0] SI_15_0,
  input  [15:0] EA_15_0,
  input  [15:0] EB_15_0,
  output PA,
  output PB
);

  wire A1_0_z, A3_2_z, A5_4_z, A7_6_z, A9_8_z, A11_10_z, A13_12_z, A15_14_z, B1_0_z, B4_3_z, B5_4_z, B7_6_z,
       B9_8_z, B11_10_z, B13_12_z, B15_14_z;

  A02 A15_14 (.A(SI_15_0[15]), .B(EA_15_0[15]), .C(SI_15_0[14]), .D(EA_15_0[14]), .Z(A15_14_z));
  A02 A13_12 (.A(SI_15_0[13]), .B(EA_15_0[13]), .C(SI_15_0[12]), .D(EA_15_0[12]), .Z(A13_12_z));
  A02 A11_10 (.A(SI_15_0[11]), .B(EA_15_0[11]), .C(SI_15_0[10]), .D(EA_15_0[10]), .Z(A11_10_z));
  A02 A9_8 (.A(SI_15_0[9]), .B(EA_15_0[9]), .C(SI_15_0[8]), .D(EA_15_0[8]), .Z(A9_8_z));
  A02 A7_6 (.A(SI_15_0[7]), .B(EA_15_0[7]), .C(SI_15_0[6]), .D(EA_15_0[6]), .Z(A7_6_z));
  A02 A5_4 (.A(SI_15_0[5]), .B(EA_15_0[5]), .C(SI_15_0[4]), .D(EA_15_0[4]), .Z(A5_4_z));
  A02 A3_2 (.A(SI_15_0[3]), .B(EA_15_0[3]), .C(SI_15_0[2]), .D(EA_15_0[2]), .Z(A3_2_z));
  A02 A1_0 (.A(SI_15_0[1]), .B(EA_15_0[1]), .C(SI_15_0[0]), .D(EA_15_0[0]), .Z(A1_0_z));
  nand nand_1 (PA, A15_14_z, A13_12_z, A11_10_z, A9_8_z, A7_6_z, A5_4_z, A3_2_z, A1_0_z);
  A02 B15_14 (.A(SI_15_0[15]), .B(EB_15_0[15]), .C(SI_15_0[14]), .D(EB_15_0[14]), .Z(B15_14_z));
  A02 B13_12 (.A(SI_15_0[13]), .B(EB_15_0[13]), .C(SI_15_0[12]), .D(EB_15_0[12]), .Z(B13_12_z));
  A02 B11_10 (.A(SI_15_0[11]), .B(EB_15_0[11]), .C(SI_15_0[10]), .D(EB_15_0[10]), .Z(B11_10_z));
  A02 B9_8 (.A(SI_15_0[9]), .B(EB_15_0[9]), .C(SI_15_0[8]), .D(EB_15_0[8]), .Z(B9_8_z));
  A02 B7_6 (.A(SI_15_0[7]), .B(EB_15_0[7]), .C(SI_15_0[6]), .D(EB_15_0[6]), .Z(B7_6_z));
  A02 B5_4 (.A(SI_15_0[5]), .B(EB_15_0[5]), .C(SI_15_0[4]), .D(EB_15_0[4]), .Z(B5_4_z));
  A02 B4_3 (.A(SI_15_0[3]), .B(EB_15_0[3]), .C(SI_15_0[2]), .D(EB_15_0[2]), .Z(B4_3_z));
  A02 B1_0 (.A(SI_15_0[1]), .B(EB_15_0[1]), .C(SI_15_0[0]), .D(EB_15_0[0]), .Z(B1_0_z));
  nand nand_2 (PB, B15_14_z, B13_12_z, B11_10_z, B9_8_z, B7_6_z, B5_4_z, B4_3_z, B1_0_z);

  // Notes on the sheet:
  //   Page 61 - CGA_ALU_WRF_RBLOCK_SEL16 
  //   EA15
  //   EA0
  //   SI0
  //   SI15
  //   EB15
  //   EB0
  //   SI0
  //   SI15
endmodule

module CGA_WRF_RBLOCK_PREG (
  input  [15:0] NLCA_15_0,
  input  [15:0] RB_15_0,
  input  XFETCHN,
  input  WR2,
  input  ALUCLKN,
  input  ALUCLK,
  output [15:0] P_15_0,
  output [15:0] PR_15_0
);

  wire not_1_out, R0_zn, R1_zn, R2_zn, R3_zn, R4_zn, R5_zn, R6_zn, R7_zn, R8_zn, R9_zn, R10_zn, R11_zn,
       R12_zn, R13_zn, R14_zn, R15_zn;

  not not_1 (not_1_out, XFETCHN);
  MUX31LP R0 (.D0(P_15_0[0]), .D1(NLCA_15_0[0]), .D2(RB_15_0[0]), .A(not_1_out), .B(WR2), .ZN(R0_zn));
  MUX31LP R1 (.D0(P_15_0[1]), .D1(NLCA_15_0[1]), .D2(RB_15_0[1]), .A(not_1_out), .B(WR2), .ZN(R1_zn));
  MUX31LP R2 (.D0(P_15_0[2]), .D1(NLCA_15_0[2]), .D2(RB_15_0[2]), .A(not_1_out), .B(WR2), .ZN(R2_zn));
  MUX31LP R3 (.D0(P_15_0[3]), .D1(NLCA_15_0[3]), .D2(RB_15_0[3]), .A(not_1_out), .B(WR2), .ZN(R3_zn));
  MUX31LP R4 (.D0(P_15_0[4]), .D1(NLCA_15_0[4]), .D2(RB_15_0[4]), .A(not_1_out), .B(WR2), .ZN(R4_zn));
  MUX31LP R5 (.D0(P_15_0[5]), .D1(NLCA_15_0[5]), .D2(RB_15_0[5]), .A(not_1_out), .B(WR2), .ZN(R5_zn));
  MUX31LP R6 (.D0(P_15_0[6]), .D1(NLCA_15_0[6]), .D2(RB_15_0[6]), .A(not_1_out), .B(WR2), .ZN(R6_zn));
  MUX31LP R7 (.D0(P_15_0[7]), .D1(NLCA_15_0[7]), .D2(RB_15_0[7]), .A(not_1_out), .B(WR2), .ZN(R7_zn));
  R81P R_P_0_7 (
    .A(R0_zn), .B(R1_zn), .C(R2_zn), .D(R3_zn), .E(R4_zn), .F(R5_zn), .G(R6_zn), .H(R7_zn), .CP(ALUCLK),
    .QAN(P_15_0[0]), .QBN(P_15_0[1]), .QCN(P_15_0[2]), .QDN(P_15_0[3]), .QEN(P_15_0[4]), .QFN(P_15_0[5]),
    .QGN(P_15_0[6]), .QHN(P_15_0[7]));  // open: QA, QB, QC, QD, QE, QF, QG, QH
  L8 L_PR_7_0 (
    .A(R0_zn), .B(R1_zn), .C(R2_zn), .D(R3_zn), .E(R4_zn), .F(R5_zn), .G(R6_zn), .H(R7_zn), .L(ALUCLKN),
    .QAN(PR_15_0[0]), .QBN(PR_15_0[1]), .QCN(PR_15_0[2]), .QDN(PR_15_0[3]), .QEN(PR_15_0[4]),
    .QFN(PR_15_0[5]), .QGN(PR_15_0[6]), .QHN(PR_15_0[7]));  // open: QA, QB, QC, QD, QE, QF, QG, QH
  MUX31LP R8 (.D0(P_15_0[8]), .D1(NLCA_15_0[8]), .D2(RB_15_0[8]), .A(not_1_out), .B(WR2), .ZN(R8_zn));
  MUX31LP R9 (.D0(P_15_0[9]), .D1(NLCA_15_0[9]), .D2(RB_15_0[9]), .A(not_1_out), .B(WR2), .ZN(R9_zn));
  MUX31LP R10 (.D0(P_15_0[10]), .D1(NLCA_15_0[10]), .D2(RB_15_0[10]), .A(not_1_out), .B(WR2), .ZN(R10_zn));
  MUX31LP R11 (.D0(P_15_0[11]), .D1(NLCA_15_0[11]), .D2(RB_15_0[11]), .A(not_1_out), .B(WR2), .ZN(R11_zn));
  MUX31LP R12 (.D0(P_15_0[12]), .D1(NLCA_15_0[12]), .D2(RB_15_0[12]), .A(not_1_out), .B(WR2), .ZN(R12_zn));
  MUX31LP R13 (.D0(P_15_0[13]), .D1(NLCA_15_0[13]), .D2(RB_15_0[13]), .A(not_1_out), .B(WR2), .ZN(R13_zn));
  MUX31LP R14 (.D0(P_15_0[14]), .D1(NLCA_15_0[14]), .D2(RB_15_0[14]), .A(not_1_out), .B(WR2), .ZN(R14_zn));
  MUX31LP R15 (.D0(P_15_0[15]), .D1(NLCA_15_0[15]), .D2(RB_15_0[15]), .A(not_1_out), .B(WR2), .ZN(R15_zn));
  R81P R_P_8_15 (
    .A(R8_zn), .B(R9_zn), .C(R10_zn), .D(R11_zn), .E(R12_zn), .F(R13_zn), .G(R14_zn), .H(R15_zn),
    .CP(ALUCLK), .QAN(P_15_0[8]), .QBN(P_15_0[9]), .QCN(P_15_0[10]), .QDN(P_15_0[11]), .QEN(P_15_0[12]),
    .QFN(P_15_0[13]), .QGN(P_15_0[14]), .QHN(P_15_0[15]));  // open: QA, QB, QC, QD, QE, QF, QG, QH
  L8 L_PR_8_15 (
    .A(R8_zn), .B(R9_zn), .C(R10_zn), .D(R11_zn), .E(R12_zn), .F(R13_zn), .G(R14_zn), .H(R15_zn),
    .L(ALUCLKN), .QAN(PR_15_0[8]), .QBN(PR_15_0[9]), .QCN(PR_15_0[10]), .QDN(PR_15_0[11]), .QEN(PR_15_0[12]),
    .QFN(PR_15_0[13]), .QGN(PR_15_0[14]), .QHN(PR_15_0[15]));  // open: QA, QB, QC, QD, QE, QF, QG, QH

  // Notes on the sheet:
  //   Page 62 - CGA_WRF_RBLOCK_PREG 
  //   IP0N
  //   IP1N
  //   IP2N
  //   IP3N
  //   IP4N
  //   IP5N
  //   IP6N
  //   IP7N
  //   IP0N
  //   PR7
  //   PR0
  //   P7
  //   P0
  //   IP8N
  //   IP9N
  //   IP10N
  //   IP11N
  //   IP12N
  //   IP13N
  //   IP14N
  //   IP15N
  //   IP8N
  //   PR15
  //   P15
  //   PR8
  //   P8
endmodule

module CGA_WRF_RBLOCK_LR16 (
  input  [15:0] RB_15_0,
  input  ALUCLK,
  input  WR,
  output [15:0] R_15_0,
  output [15:0] LR_15_0
);

  wire MUX_3_0_z0, MUX_3_0_z1, MUX_3_0_z2, MUX_3_0_z3, MUX_7_4_z0, MUX_7_4_z1, MUX_7_4_z2, MUX_7_4_z3,
       MUX_11_8_z0, MUX_11_8_z1, MUX_11_8_z2, MUX_11_8_z3, MUX_15_12_z0, MUX_15_12_z1, MUX_15_12_z2,
       MUX_15_12_z3, nand_1_out, not_1_out, not_2_out;

  not not_1 (not_1_out, WR);
  nand nand_1 (nand_1_out, ~ALUCLK, ~not_1_out);  // NAND_Gate
  MUX24P MUX_15_12 (
    .D00(R_15_0[15]), .D10(RB_15_0[15]), .D01(R_15_0[14]), .D11(RB_15_0[14]), .D02(R_15_0[13]),
    .D12(RB_15_0[13]), .D03(R_15_0[12]), .D13(RB_15_0[12]), .A(WR), .Z0(MUX_15_12_z0), .Z1(MUX_15_12_z1),
    .Z2(MUX_15_12_z2), .Z3(MUX_15_12_z3));
  MUX24P MUX_11_8 (
    .D00(R_15_0[11]), .D10(RB_15_0[11]), .D01(R_15_0[10]), .D11(RB_15_0[10]), .D02(R_15_0[9]),
    .D12(RB_15_0[9]), .D03(R_15_0[8]), .D13(RB_15_0[8]), .A(WR), .Z0(MUX_11_8_z0), .Z1(MUX_11_8_z1),
    .Z2(MUX_11_8_z2), .Z3(MUX_11_8_z3));
  not not_2 (not_2_out, nand_1_out);
  R81P R_15_8 (
    .A(MUX_15_12_z0), .B(MUX_15_12_z1), .C(MUX_15_12_z2), .D(MUX_15_12_z3), .E(MUX_11_8_z0), .F(MUX_11_8_z1),
    .G(MUX_11_8_z2), .H(MUX_11_8_z3), .CP(ALUCLK), .QA(R_15_0[15]), .QB(R_15_0[14]), .QC(R_15_0[13]),
    .QD(R_15_0[12]), .QE(R_15_0[11]), .QF(R_15_0[10]), .QG(R_15_0[9]), .QH(R_15_0[8]));  // open: QAN, QBN, QCN, QDN, QEN, QFN, QGN, QHN
  L8 L_15_8 (
    .A(MUX_15_12_z0), .B(MUX_15_12_z1), .C(MUX_15_12_z2), .D(MUX_15_12_z3), .E(MUX_11_8_z0), .F(MUX_11_8_z1),
    .G(MUX_11_8_z2), .H(MUX_11_8_z3), .L(not_2_out), .QA(LR_15_0[15]), .QB(LR_15_0[14]), .QC(LR_15_0[13]),
    .QD(LR_15_0[12]), .QE(LR_15_0[11]), .QF(LR_15_0[10]), .QG(LR_15_0[9]), .QH(LR_15_0[8]));  // open: QAN, QBN, QCN, QDN, QEN, QFN, QGN, QHN
  MUX24P MUX_7_4 (
    .D00(R_15_0[7]), .D10(RB_15_0[7]), .D01(R_15_0[6]), .D11(RB_15_0[6]), .D02(R_15_0[5]), .D12(RB_15_0[5]),
    .D03(R_15_0[4]), .D13(RB_15_0[4]), .A(WR), .Z0(MUX_7_4_z0), .Z1(MUX_7_4_z1), .Z2(MUX_7_4_z2),
    .Z3(MUX_7_4_z3));
  MUX24P MUX_3_0 (
    .D00(R_15_0[3]), .D10(RB_15_0[3]), .D01(R_15_0[2]), .D11(RB_15_0[2]), .D02(R_15_0[1]), .D12(RB_15_0[1]),
    .D03(R_15_0[0]), .D13(RB_15_0[0]), .A(WR), .Z0(MUX_3_0_z0), .Z1(MUX_3_0_z1), .Z2(MUX_3_0_z2),
    .Z3(MUX_3_0_z3));
  R81P R_7_0 (
    .A(MUX_7_4_z0), .B(MUX_7_4_z1), .C(MUX_7_4_z2), .D(MUX_7_4_z3), .E(MUX_3_0_z0), .F(MUX_3_0_z1),
    .G(MUX_3_0_z2), .H(MUX_3_0_z3), .CP(ALUCLK), .QA(R_15_0[7]), .QB(R_15_0[6]), .QC(R_15_0[5]),
    .QD(R_15_0[4]), .QE(R_15_0[3]), .QF(R_15_0[2]), .QG(R_15_0[1]), .QH(R_15_0[0]));  // open: QAN, QBN, QCN, QDN, QEN, QFN, QGN, QHN
  L8 L_7_0 (
    .A(MUX_7_4_z0), .B(MUX_7_4_z1), .C(MUX_7_4_z2), .D(MUX_7_4_z3), .E(MUX_3_0_z0), .F(MUX_3_0_z1),
    .G(MUX_3_0_z2), .H(MUX_3_0_z3), .L(not_2_out), .QA(LR_15_0[7]), .QB(LR_15_0[6]), .QC(LR_15_0[5]),
    .QD(LR_15_0[4]), .QE(LR_15_0[3]), .QF(LR_15_0[2]), .QG(LR_15_0[1]), .QH(LR_15_0[0]));  // open: QAN, QBN, QCN, QDN, QEN, QFN, QGN, QHN

  // Notes on the sheet:
  //   Page 63 - CGA_WRF_RBLOCK_LR16 
  //   IR15
  //   IR8
  //   /ALUCLK * WR
  //   LR8
  //   LR15
  //   LR0
  //   LR7
endmodule

module CGA_WRF_RBLOCK_DR16 (
  input  ALUCLK,
  input  WR,
  input  [15:0] RB_15_0,
  output [15:0] REG_15_0
);

  SCAN_FF R15 (.D(REG_15_0[15]), .TE(WR), .TI(RB_15_0[15]), .CLK(ALUCLK), .Q(REG_15_0[15]));  // open: QN
  SCAN_FF R14 (.D(REG_15_0[14]), .TE(WR), .TI(RB_15_0[14]), .CLK(ALUCLK), .Q(REG_15_0[14]));  // open: QN
  SCAN_FF R13 (.D(REG_15_0[13]), .TE(WR), .TI(RB_15_0[13]), .CLK(ALUCLK), .Q(REG_15_0[13]));  // open: QN
  SCAN_FF R12 (.D(REG_15_0[12]), .TE(WR), .TI(RB_15_0[12]), .CLK(ALUCLK), .Q(REG_15_0[12]));  // open: QN
  SCAN_FF R11 (.D(REG_15_0[11]), .TE(WR), .TI(RB_15_0[11]), .CLK(ALUCLK), .Q(REG_15_0[11]));  // open: QN
  SCAN_FF R10 (.D(REG_15_0[10]), .TE(WR), .TI(RB_15_0[10]), .CLK(ALUCLK), .Q(REG_15_0[10]));  // open: QN
  SCAN_FF R9 (.D(REG_15_0[9]), .TE(WR), .TI(RB_15_0[9]), .CLK(ALUCLK), .Q(REG_15_0[9]));  // open: QN
  SCAN_FF R8 (.D(REG_15_0[8]), .TE(WR), .TI(RB_15_0[8]), .CLK(ALUCLK), .Q(REG_15_0[8]));  // open: QN
  SCAN_FF R7 (.D(REG_15_0[7]), .TE(WR), .TI(RB_15_0[7]), .CLK(ALUCLK), .Q(REG_15_0[7]));  // open: QN
  SCAN_FF R6 (.D(REG_15_0[6]), .TE(WR), .TI(RB_15_0[6]), .CLK(ALUCLK), .Q(REG_15_0[6]));  // open: QN
  SCAN_FF R5 (.D(REG_15_0[5]), .TE(WR), .TI(RB_15_0[5]), .CLK(ALUCLK), .Q(REG_15_0[5]));  // open: QN
  SCAN_FF R4 (.D(REG_15_0[4]), .TE(WR), .TI(RB_15_0[4]), .CLK(ALUCLK), .Q(REG_15_0[4]));  // open: QN
  SCAN_FF R3 (.D(REG_15_0[3]), .TE(WR), .TI(RB_15_0[3]), .CLK(ALUCLK), .Q(REG_15_0[3]));  // open: QN
  SCAN_FF R2 (.D(REG_15_0[2]), .TE(WR), .TI(RB_15_0[2]), .CLK(ALUCLK), .Q(REG_15_0[2]));  // open: QN
  SCAN_FF R1 (.D(REG_15_0[1]), .TE(WR), .TI(RB_15_0[1]), .CLK(ALUCLK), .Q(REG_15_0[1]));  // open: QN
  SCAN_FF R0 (.D(REG_15_0[0]), .TE(WR), .TI(RB_15_0[0]), .CLK(ALUCLK), .Q(REG_15_0[0]));  // open: QN

  // Notes on the sheet:
  //   Page 64 - CGA_WRF_RBLOCK_DR16
endmodule

module test_WRF (
  input  in_1,
  input  [3:0] in_2,
  input  [3:0] in_3,
  input  in_4,
  input  [15:0] in_5,
  input  [15:0] in_6,
  input  in_7,
  input  [15:0] in_8,
  input  [15:0] in_9,
  input  [15:0] in_10
);

  wire cga_wrf_rblock_sel16_1_pa, cga_wrf_rblock_sel16_1_pb;
  wire [15:0] cga_wrf_1_a_15_0, cga_wrf_1_b_15_0, cga_wrf_1_br_15_0, cga_wrf_1_pr_15_0, cga_wrf_1_xr_15_0;

  CGA_WRF cga_wrf_1 (
    .BDEST(in_1), .LBA_3_0(in_2), .LAA_3_0(in_3), .ALUCLK(in_4), .RB_15_0(in_5), .NLCA_15_0(in_6),
    .XFETCHN(in_7), .B_15_0(cga_wrf_1_b_15_0), .A_15_0(cga_wrf_1_a_15_0), .PR_15_0(cga_wrf_1_pr_15_0),
    .BR_15_0(cga_wrf_1_br_15_0), .XR_15_0(cga_wrf_1_xr_15_0));  // open: WPN, WR3, WR7, EA_15_0
  CGA_WRF_RBLOCK_SEL16 cga_wrf_rblock_sel16_1 (
    .SI_15_0(in_8), .EA_15_0(in_9), .EB_15_0(in_10), .PA(cga_wrf_rblock_sel16_1_pa),
    .PB(cga_wrf_rblock_sel16_1_pb));
  // Probe on cga_wrf_1_pr_15_0
  // Probe on cga_wrf_1_br_15_0
  // Probe on cga_wrf_1_xr_15_0
  // Probe on cga_wrf_rblock_sel16_1_pa
  // Probe on cga_wrf_rblock_sel16_1_pb
  // Probe on cga_wrf_1_b_15_0
  // Probe on cga_wrf_1_a_15_0

  // Notes on the sheet:
  //   B
  //   A
endmodule

module SCAN_FF (
  input  D,
  input  TE,
  input  TI,
  input  CLK,
  output Q,
  output QN
);

  wire and_1_out, and_2_out, not_1_out, or_1_out;

  not not_1 (not_1_out, TE);
  and and_1 (and_1_out, D, not_1_out);
  and and_2 (and_2_out, TE, TI);
  or or_1 (or_1_out, and_1_out, and_2_out);
  D_Flip_Flop d_ff_1 (.D(or_1_out), .clk(CLK), .Q(Q), .Qn(QN));  // open: preset, reset

  // Notes on the sheet:
  //   Scan Flip Flop
  //   Positive-edge-triggered D flip-flop with scan
  //   It is a D flip-flop with a 2-input multiplexer on the D input
  //   Used in some Diagrams, was not a standard component in LogiSim so it was added.
  //   Also known as FDIS (In the Delilah Schematics)
  //   When TE (test enable) input is negated, circuit behaves like an ordinary D flip-flop. When TE is asserted, it takes its data from TI (test input) instead of from D.
endmodule

module SCAN_WITH_RESET_N (
  input  D,
  input  TE,
  input  TI,
  input  CLK,
  input  R,
  output Q,
  output QN
);

  wire and_1_out, and_2_out, not_1_out, not_2_out, or_1_out;

  not not_1 (not_1_out, TE);
  not not_2 (not_2_out, R);
  and and_1 (and_1_out, D, not_1_out);
  and and_2 (and_2_out, TE, TI);
  or or_1 (or_1_out, and_1_out, and_2_out);
  D_Flip_Flop d_ff_1 (.D(or_1_out), .clk(CLK), .Q(Q), .Qn(QN), .preset(1'b0), .reset(not_2_out));

  // Notes on the sheet:
  //   Reset is NEGATED
  //   Positive-edge-triggered D flip-flop with scan
  //   It is a D flip-flop with a 2-input multiplexer on the D input
  //   Used in some Diagrams, was not a standard component in LogiSim so it was added.
  //   When TE (test enable) input is negated, circuit behaves like an ordinary D flip-flop. When TE is asserted, it takes its data from TI (test input) instead of from D.
endmodule

module SCAN_WITH_SET_N (
  input  S,
  input  D,
  input  TE,
  input  TI,
  input  CLK,
  output Q,
  output QN
);

  wire and_1_out, and_2_out, not_1_out, not_2_out, or_1_out;

  not not_1 (not_1_out, S);
  not not_2 (not_2_out, TE);
  and and_1 (and_1_out, D, not_2_out);
  and and_2 (and_2_out, TE, TI);
  or or_1 (or_1_out, and_1_out, and_2_out);
  D_Flip_Flop d_ff_1 (.D(or_1_out), .clk(CLK), .Q(Q), .Qn(QN), .preset(not_1_out));  // open: reset

  // Notes on the sheet:
  //   Set is NEGATED
  //   Positive-edge-triggered D flip-flop with scan
  //   It is a D flip-flop with a 2-input multiplexer on the D input
  //   Used in some Diagrams, was not a standard component in LogiSim so it was added.
  //   When TE (test enable) input is negated, circuit behaves like an ordinary D flip-flop. When TE is asserted, it takes its data from TI (test input) instead of from D.
endmodule

module A02 (
  input  A,
  input  B,
  input  C,
  input  D,
  output Z
);

  wire and_1_out, and_2_out, or_1_out;

  and and_1 (and_1_out, A, B);
  and and_2 (and_2_out, C, D);
  or or_1 (or_1_out, and_1_out, and_2_out);
  not not_1 (Z, or_1_out);

  // Notes on the sheet:
  //   A02
  //   From Lasse Bockelie:
  //   As you can see, there wasn't even room for the title field on this page
  //   AO2 is an And Or Invert gate. So 2 And followed by an Or gate and then inverted. The function is a selector (multiplexer) of each of the 4 16-bit signal groups.
  //   AO2 was a component of LSI Logic's library on Daisy. The symbol for it was like in your drawing, but we didn't have room for that. We could also make our own components on Daisy, so I made the shrunken one.
endmodule

module ND38GLP (
  input  A,
  input  B,
  input  C,
  input  G,
  output Z0,
  output Z1,
  output Z2,
  output Z3,
  output Z4,
  output Z5,
  output Z6,
  output Z7
);

  wire decoder_1_out0, decoder_1_out1, decoder_1_out2, decoder_1_out3, decoder_1_out4, decoder_1_out5,
       decoder_1_out6, decoder_1_out7;

  // NOT_Gate not_1 is placed but not wired
  Decoder #(.select(3)) decoder_1 (
    .out0(decoder_1_out0), .out1(decoder_1_out1), .out2(decoder_1_out2), .out3(decoder_1_out3),
    .out4(decoder_1_out4), .out5(decoder_1_out5), .out6(decoder_1_out6), .out7(decoder_1_out7),
    .sel({C, B, A}), .en(G));
  not not_2 (Z0, decoder_1_out0);
  not not_3 (Z1, decoder_1_out1);
  not not_4 (Z2, decoder_1_out2);
  not not_5 (Z3, decoder_1_out3);
  not not_6 (Z4, decoder_1_out4);
  not not_7 (Z5, decoder_1_out5);
  not not_8 (Z6, decoder_1_out6);
  not not_9 (Z7, decoder_1_out7);

  // Notes on the sheet:
  //   3 to 8 decoder
  //   https://www.elprocus.com/designing-4-to-16-decoder-using-3-to-8-decoder/
endmodule

module ND38GHP (
  input  A,
  input  B,
  input  C,
  input  G,
  output Z0,
  output Z1,
  output Z2,
  output Z3,
  output Z4,
  output Z5,
  output Z6,
  output Z7
);

  wire decoder_1_out0, decoder_1_out1, decoder_1_out2, decoder_1_out3, decoder_1_out4, decoder_1_out5,
       decoder_1_out6, decoder_1_out7;

  Decoder #(.select(3)) decoder_1 (
    .out0(decoder_1_out0), .out1(decoder_1_out1), .out2(decoder_1_out2), .out3(decoder_1_out3),
    .out4(decoder_1_out4), .out5(decoder_1_out5), .out6(decoder_1_out6), .out7(decoder_1_out7),
    .sel({C, B, A}), .en(G));
  not not_1 (Z0, decoder_1_out0);
  not not_2 (Z1, decoder_1_out1);
  not not_3 (Z2, decoder_1_out2);
  not not_4 (Z3, decoder_1_out3);
  not not_5 (Z4, decoder_1_out4);
  not not_6 (Z5, decoder_1_out5);
  not not_7 (Z6, decoder_1_out6);
  not not_8 (Z7, decoder_1_out7);

  // Notes on the sheet:
  //   3 to 8 decoder
  //   TODO: Similar to the ND38GLP.. what is different ?
endmodule

module LATCH (
  input  D,
  input  ENABLE,
  output Q,
  output QN
);

  wire nand_1_out, nand_2_out, not_1_out;

  not not_1 (not_1_out, D);
  nand nand_1 (nand_1_out, D, ENABLE);
  nand nand_2 (nand_2_out, ENABLE, not_1_out);
  nand nand_3 (Q, nand_1_out, QN);
  nand nand_4 (QN, Q, nand_2_out);
endmodule

module L4 (
  input  A,
  input  B,
  input  C,
  input  D,
  input  L,
  output QA,
  output QAN,
  output QB,
  output QBN,
  output QC,
  output QCN,
  output QD,
  output QDN
);

  LATCH L0 (.D(A), .ENABLE(L), .Q(QA), .QN(QAN));
  LATCH L1 (.D(B), .ENABLE(L), .Q(QB), .QN(QBN));
  LATCH L2 (.D(C), .ENABLE(L), .Q(QC), .QN(QCN));
  LATCH L3 (.D(D), .ENABLE(L), .Q(QD), .QN(QDN));
endmodule

module L8 (
  input  A,
  input  B,
  input  C,
  input  D,
  input  E,
  input  F,
  input  G,
  input  H,
  input  L,
  output QA,
  output QAN,
  output QB,
  output QBN,
  output QC,
  output QCN,
  output QD,
  output QDN,
  output QE,
  output QEN,
  output QF,
  output QFN,
  output QG,
  output QGN,
  output QH,
  output QHN
);

  LATCH L0 (.D(A), .ENABLE(L), .Q(QA), .QN(QAN));
  LATCH L1 (.D(B), .ENABLE(L), .Q(QB), .QN(QBN));
  LATCH L2 (.D(C), .ENABLE(L), .Q(QC), .QN(QCN));
  LATCH L3 (.D(D), .ENABLE(L), .Q(QD), .QN(QDN));
  LATCH L4 (.D(E), .ENABLE(L), .Q(QE), .QN(QEN));
  LATCH L5 (.D(F), .ENABLE(L), .Q(QF), .QN(QFN));
  LATCH L6 (.D(G), .ENABLE(L), .Q(QG), .QN(QGN));
  LATCH L7 (.D(H), .ENABLE(L), .Q(QH), .QN(QHN));
endmodule

module SR44 (
  input  SI,
  input  A,
  input  B,
  input  C,
  input  D,
  input  L,
  input  CP,
  output QA,
  output QAN,
  output QB,
  output QBN,
  output QC,
  output QCN,
  output QD,
  output QDN
);

  wire multiplexer_1_out, multiplexer_2_out, multiplexer_3_out, multiplexer_4_out;

  Multiplexer multiplexer_1 (.in0(SI), .in1(A), .out(multiplexer_1_out), .sel(L));
  Multiplexer multiplexer_2 (.in0(QA), .in1(B), .out(multiplexer_2_out), .sel(L));
  Multiplexer multiplexer_3 (.in0(QB), .in1(C), .out(multiplexer_3_out), .sel(L));
  Multiplexer multiplexer_4 (.in0(QC), .in1(D), .out(multiplexer_4_out), .sel(L));
  D_Flip_Flop d_ff_1 (.D(multiplexer_1_out), .clk(CP), .Q(QA), .Qn(QAN));  // open: preset, reset
  D_Flip_Flop d_ff_2 (.D(multiplexer_2_out), .clk(CP), .Q(QB), .Qn(QBN));  // open: preset, reset
  D_Flip_Flop d_ff_3 (.D(multiplexer_3_out), .clk(CP), .Q(QC), .Qn(QCN));  // open: preset, reset
  D_Flip_Flop d_ff_4 (.D(multiplexer_4_out), .clk(CP), .Q(QD), .Qn(QDN));  // open: preset, reset

  // Notes on the sheet:
  //   Used by CGA_MIC_STACK_BIT12 (Page 17 and 18)
  //   4 bit shift register with Serial Input (SI) and Load (L) which triggers parallell load from A-D
endmodule

module MUX21L (
  input  A,
  input  B,
  input  S,
  output ZN
);

  wire multiplexer_1_out;

  Multiplexer multiplexer_1 (.in0(A), .in1(B), .out(multiplexer_1_out), .sel(S));
  not not_1 (ZN, multiplexer_1_out);

  // Notes on the sheet:
  //   Helper circuit for all MUX21L components
endmodule

module MUX21LP (
  input  A,
  input  B,
  input  S,
  output ZN
);

  wire multiplexer_1_out;

  Multiplexer multiplexer_1 (.in0(A), .in1(B), .out(multiplexer_1_out), .sel(S));
  not not_1 (ZN, multiplexer_1_out);

  // Notes on the sheet:
  //   Helper circuit for all MUX21LP components
  //   WAS: This is different from MUX21L in that its not NEGATED
  //   Chnaged 04.12.2023 - Its used in CGA_ALU mostly, and there it is definitively negated
endmodule

module MUX24P (
  input  D00,
  input  D10,
  input  D01,
  input  D11,
  input  D02,
  input  D12,
  input  D03,
  input  D13,
  input  A,
  output Z0,
  output Z1,
  output Z2,
  output Z3
);

  Multiplexer multiplexer_1 (.in0(D00), .in1(D10), .out(Z0), .sel(A));
  Multiplexer multiplexer_2 (.in0(D01), .in1(D11), .out(Z1), .sel(A));
  Multiplexer multiplexer_3 (.in0(D02), .in1(D12), .out(Z2), .sel(A));
  Multiplexer multiplexer_4 (.in0(D03), .in1(D13), .out(Z3), .sel(A));

  // Notes on the sheet:
  //   MUX24P
  //   Used in page 63, CGA_WRF_RBLOCK_LR16
  //   Undefined what happens with Z (out) when A = 1 and B = 1. Guessing 0
endmodule

module MUX31LP (
  input  D0,
  input  D1,
  input  D2,
  input  A,
  input  B,
  output ZN
);

  wire multiplexer_1_out;

  Multiplexer #(.select(2)) multiplexer_1 (
    .in0(D0), .in1(D1), .in2(D2), .in3(D2), .out(multiplexer_1_out), .sel({B, A}));
  not not_1 (ZN, multiplexer_1_out);

  // Notes on the sheet:
  //   Helper circuit for all MUX31LP components
  //   TODO: What about address 11 ? is 0 correct ?
  //   Was GND, now connected to D2..
endmodule

module MUX34P (
  input  D00,
  input  D10,
  input  D20,
  input  D01,
  input  D11,
  input  D21,
  input  D02,
  input  D12,
  input  D22,
  input  D03,
  input  D13,
  input  D23,
  input  A,
  input  B,
  output Z0,
  output Z1,
  output Z2,
  output Z3
);

  Multiplexer #(.select(2)) multiplexer_1 (.in0(D00), .in1(D10), .in2(D20), .in3(1'b0), .out(Z0), .sel({B, A}));
  Multiplexer #(.select(2)) multiplexer_2 (.in0(D01), .in1(D11), .in2(D21), .in3(1'b0), .out(Z1), .sel({B, A}));
  Multiplexer #(.select(2)) multiplexer_3 (.in0(D02), .in1(D12), .in2(D22), .in3(1'b0), .out(Z2), .sel({B, A}));
  Multiplexer #(.select(2)) multiplexer_4 (.in0(D03), .in1(D13), .in2(D23), .in3(1'b0), .out(Z3), .sel({B, A}));

  // Notes on the sheet:
  //   MUX34P
  //   Used in page 11, CGA_MIC
  //   TODO: Undefined what happens with Z (out) when A = 1 and B = 1. Guessing 0
endmodule

module MUX41P (
  input  D0,
  input  D1,
  input  D2,
  input  D3,
  input  A,
  input  B,
  output Z
);

  Multiplexer #(.select(2)) multiplexer_1 (.in0(D0), .in1(D1), .in2(D2), .in3(D3), .out(Z), .sel({B, A}));

  // Notes on the sheet:
  //   MUX41P - Used in many places
endmodule

module MUX81 (
  input  D0,
  input  D1,
  input  D2,
  input  D3,
  input  D4,
  input  D5,
  input  D6,
  input  D7,
  input  A,
  input  B,
  input  C,
  output Z
);

  Multiplexer #(.select(3)) multiplexer_1 (
    .in0(D0), .in1(D1), .in2(D2), .in3(D3), .in4(D4), .in5(D5), .in6(D6), .in7(D7), .out(Z), .sel({C, B, A}));

  // Notes on the sheet:
  //   MUX81 - Used in TESTMUX
endmodule

module R41P (
  input  A,
  input  B,
  input  C,
  input  D,
  input  CP,
  output QA,
  output QAN,
  output QB,
  output QBN,
  output QC,
  output QCN,
  output QD,
  output QDN
);

  D_Flip_Flop d_ff_1 (.D(A), .clk(CP), .Q(QA), .Qn(QAN));  // open: preset, reset
  D_Flip_Flop d_ff_2 (.D(B), .clk(CP), .Q(QB), .Qn(QBN));  // open: preset, reset
  D_Flip_Flop d_ff_3 (.D(C), .clk(CP), .Q(QC), .Qn(QCN));  // open: preset, reset
  D_Flip_Flop d_ff_4 (.D(D), .clk(CP), .Q(QD), .Qn(QDN));  // open: preset, reset

  // Notes on the sheet:
  //   4 bit register. Latched on positive clock pulse
endmodule

module R81 (
  input  A,
  input  B,
  input  C,
  input  D,
  input  E,
  input  F,
  input  G,
  input  H,
  input  CP,
  output QA,
  output QAN,
  output QB,
  output QBN,
  output QC,
  output QCN,
  output QD,
  output QDN,
  output QE,
  output QEN,
  output QF,
  output QFN,
  output QG,
  output QGN,
  output QH,
  output QHN
);

  D_Flip_Flop d_ff_1 (.D(A), .clk(CP), .Q(QA), .Qn(QAN));  // open: preset, reset
  D_Flip_Flop d_ff_2 (.D(B), .clk(CP), .Q(QB), .Qn(QBN));  // open: preset, reset
  D_Flip_Flop d_ff_3 (.D(C), .clk(CP), .Q(QC), .Qn(QCN));  // open: preset, reset
  D_Flip_Flop d_ff_4 (.D(D), .clk(CP), .Q(QD), .Qn(QDN));  // open: preset, reset
  D_Flip_Flop d_ff_5 (.D(E), .clk(CP), .Q(QE), .Qn(QEN));  // open: preset, reset
  D_Flip_Flop d_ff_6 (.D(F), .clk(CP), .Q(QF), .Qn(QFN));  // open: preset, reset
  D_Flip_Flop d_ff_7 (.D(G), .clk(CP), .Q(QG), .Qn(QGN));  // open: preset, reset
  D_Flip_Flop d_ff_8 (.D(H), .clk(CP), .Q(QH), .Qn(QHN));  // open: preset, reset

  // Notes on the sheet:
  //   8-bt register. Latched on RISING EDGE (Clock going LOW->HIGH)
endmodule
module R81P (
  input  A,
  input  B,
  input  C,
  input  D,
  input  E,
  input  F,
  input  G,
  input  H,
  input  CP,
  output QA,
  output QAN,
  output QB,
  output QBN,
  output QC,
  output QCN,
  output QD,
  output QDN,
  output QE,
  output QEN,
  output QF,
  output QFN,
  output QG,
  output QGN,
  output QH,
  output QHN
);

  D_Flip_Flop d_ff_1 (.D(A), .clk(CP), .Q(QA), .Qn(QAN));  // open: preset, reset
  D_Flip_Flop d_ff_2 (.D(B), .clk(CP), .Q(QB), .Qn(QBN));  // open: preset, reset
  D_Flip_Flop d_ff_3 (.D(C), .clk(CP), .Q(QC), .Qn(QCN));  // open: preset, reset
  D_Flip_Flop d_ff_4 (.D(D), .clk(CP), .Q(QD), .Qn(QDN));  // open: preset, reset
  D_Flip_Flop d_ff_5 (.D(E), .clk(CP), .Q(QE), .Qn(QEN));  // open: preset, reset
  D_Flip_Flop d_ff_6 (.D(F), .clk(CP), .Q(QF), .Qn(QFN));  // open: preset, reset
  D_Flip_Flop d_ff_7 (.D(G), .clk(CP), .Q(QG), .Qn(QGN));  // open: preset, reset
  D_Flip_Flop d_ff_8 (.D(H), .clk(CP), .Q(QH), .Qn(QHN));  // open: preset, reset

  // Notes on the sheet:
  //   8 bit flip flop with Q and QN outputs
  //   Used by CGA_DCD page 65
  //   Latched on RISING EDGE (Clock going LOW->HIGH)
endmodule

module M169C (
  input  A,
  input  B,
  input  C,
  input  D,
  input  NL,
  input  CP,
  input  PN,
  input  TN,
  input  UP,
  output QA,
  output QB,
  output QC,
  output QD,
  output CON
);

  wire and_1_out, and_2_out, and_3_out, and_4_out, and_5_out, and_6_out, and_7_out, and_8_out, and_9_out,
       and_10_out, and_11_out, and_12_out, and_13_out, and_14_out, and_15_out, and_16_out, and_17_out,
       and_18_out, and_19_out, and_20_out, and_21_out, and_22_out, d_ff_1_q, d_ff_1_qn, d_ff_2_q, d_ff_2_qn,
       d_ff_3_q, d_ff_3_qn, d_ff_4_q, d_ff_4_qn, nor_1_out, nor_2_out, nor_3_out, nor_4_out, nor_5_out,
       nor_6_out, nor_7_out, nor_8_out, not_1_out, not_2_out, not_3_out, not_4_out, not_5_out, not_6_out,
       not_7_out, not_8_out, not_9_out, not_10_out, not_11_out, not_12_out, xor_1_out, xor_2_out, xor_3_out,
       xor_4_out;

  not not_1 (not_1_out, UP);
  not not_2 (not_2_out, TN);
  and and_1 (and_1_out, ~PN, ~TN, ~not_3_out);  // AND_Gate
  not not_3 (not_3_out, NL);
  not not_4 (not_4_out, CP);
  and and_2 (and_2_out, d_ff_1_q, NL);
  and and_3 (and_3_out, d_ff_2_q, NL);
  and and_4 (and_4_out, and_1_out, nor_1_out);
  and and_5 (and_5_out, d_ff_3_q, NL);
  and and_6 (and_6_out, and_1_out, nor_1_out, nor_2_out);
  and and_7 (and_7_out, d_ff_4_q, NL);
  and and_8 (and_8_out, and_1_out, nor_1_out, nor_2_out, nor_3_out);
  xor xor_1 (xor_1_out, and_2_out, and_1_out);
  and and_9 (and_9_out, not_3_out, A);
  nor nor_1 (nor_1_out, and_13_out, and_14_out);
  xor xor_2 (xor_2_out, and_3_out, and_4_out);
  and and_10 (and_10_out, not_3_out, B);
  nor nor_2 (nor_2_out, and_15_out, and_16_out);
  xor xor_3 (xor_3_out, and_5_out, and_6_out);
  and and_11 (and_11_out, not_3_out, C);
  nor nor_3 (nor_3_out, and_17_out, and_18_out);
  xor xor_4 (xor_4_out, and_7_out, and_8_out);
  and and_12 (and_12_out, not_3_out, D);
  nor nor_4 (nor_4_out, and_19_out, and_20_out);
  and and_13 (and_13_out, UP, d_ff_1_qn);
  and and_14 (and_14_out, not_1_out, d_ff_1_q);
  and and_15 (and_15_out, UP, d_ff_2_qn);
  and and_16 (and_16_out, not_1_out, d_ff_2_q);
  and and_17 (and_17_out, UP, d_ff_3_qn);
  and and_18 (and_18_out, not_1_out, d_ff_3_q);
  and and_19 (and_19_out, UP, d_ff_4_qn);
  and and_20 (and_20_out, not_1_out, d_ff_4_q);
  nor nor_5 (nor_5_out, xor_1_out, and_9_out);
  nor nor_6 (nor_6_out, xor_2_out, and_10_out);
  nor nor_7 (nor_7_out, xor_3_out, and_11_out);
  nor nor_8 (nor_8_out, xor_4_out, and_12_out);
  and and_21 (and_21_out, nor_4_out, nor_3_out, nor_2_out, not_2_out, UP);
  and and_22 (and_22_out, not_1_out, not_2_out, nor_1_out, nor_2_out, nor_3_out, nor_4_out);
  D_Flip_Flop d_ff_1 (.D(not_5_out), .clk(not_6_out), .Q(d_ff_1_q), .Qn(d_ff_1_qn));  // open: preset, reset
  not not_5 (not_5_out, nor_5_out);
  not not_6 (not_6_out, not_4_out);
  D_Flip_Flop d_ff_2 (.D(not_7_out), .clk(not_8_out), .Q(d_ff_2_q), .Qn(d_ff_2_qn));  // open: preset, reset
  not not_7 (not_7_out, nor_6_out);
  not not_8 (not_8_out, not_4_out);
  D_Flip_Flop d_ff_3 (.D(not_9_out), .clk(not_10_out), .Q(d_ff_3_q), .Qn(d_ff_3_qn));  // open: preset, reset
  not not_9 (not_9_out, nor_7_out);
  not not_10 (not_10_out, not_4_out);
  D_Flip_Flop d_ff_4 (.D(not_11_out), .clk(not_12_out), .Q(d_ff_4_q), .Qn(d_ff_4_qn));  // open: preset, reset
  not not_11 (not_11_out, nor_8_out);
  not not_12 (not_12_out, not_4_out);
  nor nor_9 (CON, and_21_out, and_22_out);
  not not_13 (QA, d_ff_1_qn);
  not not_14 (QB, d_ff_2_qn);
  not not_15 (QC, d_ff_3_qn);
  not not_16 (QD, d_ff_4_qn);

  // Other names for the same wires on the sheet: CLK = CP; ENP_N = PN; ENT_N = TN; LOAD_N = NL; RCO_N = CON;
  //   U_DN = UP

  // Notes on the sheet:
  //   Circuit used in CGA_MIC page 12
  //   https://www.ti.com/lit/ds/symlink/sn74als169b.pdf
  //   M169C - 74LS169 - Synchronous 4-biy up/down binary counters
  //   CP Rising
  //   Count Enable P
  //   Count Enable N
  //   Count: UP  /DOWN
  //   Ripple Carry Out
endmodule

module CMP4 (
  input  A0,
  input  A1,
  input  A2,
  input  A3,
  input  B0,
  input  B1,
  input  B2,
  input  B3,
  output AGB,
  output AEB,
  output ALB
);

  Comparator #(.width(4)) comparator_1 (.a({A3, A2, A1, A0}), .b({B3, B2, B1, B0}), .gt(AGB), .eq(AEB), .lt(ALB));

  // Notes on the sheet:
  //   Wrapping the Logisim Comparator in a 4 bit ND Comparator
endmodule

module test_169 (
  input  [3:0] in_1,
  input  NL,
  input  CP,
  input  PN,
  input  TN,
  input  UP,
  output [3:0] CNT,
  output CON
);

  M169C ls169 (
    .A(in_1[0]), .B(in_1[1]), .C(in_1[2]), .D(in_1[3]), .NL(NL), .CP(CP), .PN(PN), .TN(TN), .UP(UP),
    .QA(CNT[0]), .QB(CNT[1]), .QC(CNT[2]), .QD(CNT[3]), .CON(CON));
endmodule

module BD4TU (
  input  EN,
  input  TN,
  input  A,
  input  BUF_IN,
  output BUF_OUT,
  output ZI
);

  wire controlled_buffer_1_out, not_1_out;

  not not_1 (not_1_out, EN);
  assign controlled_buffer_1_out = not_1_out ? A : 1'bz;  // Controlled_Buffer controlled_buffer_1
  assign BUF_OUT = not_1_out ? controlled_buffer_1_out : 1'bz;  // Controlled_Buffer controlled_buffer_2
  assign ZI = EN ? BUF_IN : 1'bz;  // Controlled_Buffer controlled_buffer_3

  // Notes on the sheet:
  //   Databuffer with 3-state
  //   Used in CGA (Sheet 5/10) page 6 
  //   Don't know what TN is, guessing its for testing. Seems like its not in use in the 3202 CPU board
endmodule

module test_BD (
  input  in_1,
  input  in_2,
  input  in_3,
  input  [15:0] in_4,
  input  [15:0] in_5,
  input  in_6,
  output [15:0] out_7
);

  wire bd4tu_1_zi, undriven;

  // Probe on bd4tu_1_zi
  BD4TU bd4tu_1 (.EN(in_1), .TN(undriven), .A(in_2), .BUF_IN(in_3), .ZI(bd4tu_1_zi), .BUF_OUT(in_3));
  // Probe on in_3
  BusDriver16xx busdriver16xx_1 (
    .A_15_0(in_4), .IN_15_0(in_5), .EN(in_6), .ZI_15_0(out_7), .OUT_15_0(in_5));  // open: TN
  // Probe on in_5
endmodule

module BusDriver16xx (
  input  [15:0] A_15_0,
  input  [15:0] IN_15_0,
  input  EN,
  input  TN,
  output [15:0] ZI_15_0,
  output [15:0] OUT_15_0
);

  BD4TU BD_0 (.EN(EN), .TN(TN), .A(A_15_0[0]), .BUF_IN(IN_15_0[0]), .ZI(ZI_15_0[0]), .BUF_OUT(OUT_15_0[0]));
  BD4TU BD_1 (.EN(EN), .TN(TN), .A(A_15_0[1]), .BUF_IN(IN_15_0[1]), .ZI(ZI_15_0[1]), .BUF_OUT(OUT_15_0[1]));
  BD4TU BD_2 (.EN(EN), .TN(TN), .A(A_15_0[2]), .BUF_IN(IN_15_0[2]), .ZI(ZI_15_0[2]), .BUF_OUT(OUT_15_0[2]));
  BD4TU BD_3 (.EN(EN), .TN(TN), .A(A_15_0[3]), .BUF_IN(IN_15_0[3]), .ZI(ZI_15_0[3]), .BUF_OUT(OUT_15_0[3]));
  BD4TU BD_4 (.EN(EN), .TN(TN), .A(A_15_0[4]), .BUF_IN(IN_15_0[4]), .ZI(ZI_15_0[4]), .BUF_OUT(OUT_15_0[4]));
  BD4TU BD_5 (.EN(EN), .TN(TN), .A(A_15_0[5]), .BUF_IN(IN_15_0[5]), .ZI(ZI_15_0[5]), .BUF_OUT(OUT_15_0[5]));
  BD4TU BD_6 (.EN(EN), .TN(TN), .A(A_15_0[6]), .BUF_IN(IN_15_0[6]), .ZI(ZI_15_0[6]), .BUF_OUT(OUT_15_0[6]));
  BD4TU BD_7 (.EN(EN), .TN(TN), .A(A_15_0[7]), .BUF_IN(IN_15_0[7]), .ZI(ZI_15_0[7]), .BUF_OUT(OUT_15_0[7]));
  BD4TU BD_8 (.EN(EN), .TN(TN), .A(A_15_0[8]), .BUF_IN(IN_15_0[8]), .ZI(ZI_15_0[8]), .BUF_OUT(OUT_15_0[8]));
  BD4TU BD_9 (.EN(EN), .TN(TN), .A(A_15_0[9]), .BUF_IN(IN_15_0[9]), .ZI(ZI_15_0[9]), .BUF_OUT(OUT_15_0[9]));
  BD4TU BD_10 (.EN(EN), .TN(TN), .A(A_15_0[10]), .BUF_IN(IN_15_0[10]), .ZI(ZI_15_0[10]), .BUF_OUT(OUT_15_0[10]));
  BD4TU BD_11 (.EN(EN), .TN(TN), .A(A_15_0[11]), .BUF_IN(IN_15_0[11]), .ZI(ZI_15_0[11]), .BUF_OUT(OUT_15_0[11]));
  BD4TU BD_12 (.EN(EN), .TN(TN), .A(A_15_0[12]), .BUF_IN(IN_15_0[12]), .ZI(ZI_15_0[12]), .BUF_OUT(OUT_15_0[12]));
  BD4TU BD_13 (.EN(EN), .TN(TN), .A(A_15_0[13]), .BUF_IN(IN_15_0[13]), .ZI(ZI_15_0[13]), .BUF_OUT(OUT_15_0[13]));
  BD4TU BD_14 (.EN(EN), .TN(TN), .A(A_15_0[14]), .BUF_IN(IN_15_0[14]), .ZI(ZI_15_0[14]), .BUF_OUT(OUT_15_0[14]));
  BD4TU BD_15 (.EN(EN), .TN(TN), .A(A_15_0[15]), .BUF_IN(IN_15_0[15]), .ZI(ZI_15_0[15]), .BUF_OUT(OUT_15_0[15]));

  // Notes on the sheet:
  //   16 bit three-state bus driver
  //   Special made for CGA page 6 (Sheet 5 of 8)
endmodule

module test_cga (
);

  CGA cga_1 ();  // open: XPTSTN, XCSCOMM_4_0, XCSMIS_1_0, XCD_15_0, XEDON, XCSCINSEL_1_0, XCSSST_1_0, XALUCLK, XCSBIT_15_0, XCSALUM_1_0, XCSALUI_8_0, XCSIDBS_4_0, XMRN, XCSLOOP, XCSECOND, XCSRASEL_1_0, XCSRB_3_0, XCSBIT20, XCSRBSEL_1_0, XCSSCOND, XCSTS_6_3, XCSVECT, XCSXRF3, XEWCAN, XMAPN, XSPARE, XSTP, XETRAPN, XFTRAPN, XVTRAPN, XPT_9_15, XTCLK, XPANN, XMCLK, XBINT10N, XBINT11N, XBINT12N, XBINT13N, XILCSN, XBINT15N, XEMPIDN, XIOXERRN, XMORN, XPARERRN, XPOWFAILN, XTSEL_2_0, XFIDB_15_0_IN, XLSHADOW, XPIL_3_0, XBRKN, XIONI, XINTRQN, XDOUBLE, XPONI, XACONDN, XWCSN, XERFN, XWRTRF, XECCR, XTRAPN, XLAA_3_0, XLBA_3_0, XRF_1_0, XPCR_1_0, XTEST_4_0, XMA_12_0, XLA_23_10, XMCA_9_0, XFIDB_15_0_OUT
endmodule
