// Logisim project ND_DGA.circ as structural Verilog: 16 circuits, main circuit DECODE_DGA_COMM
module DECODE_DGA (
  input  XCLK,
  input  XLCN,
  input  XLSH,
  input  XUCK,
  input  XEON,
  input  XBDN,
  input  XDAN,
  input  XPDI,
  input  [4:0] XID_4_0,
  input  [4:0] XCO_4_0,
  input  [1:0] XST_4_3,
  input  [1:0] XMI_1_0,
  input  XHIN,
  input  XBRN,
  input  XTON,
  input  XLON,
  input  XEFN,
  input  XCON,
  input  XPWC,
  input  XPOW,
  input  XRTO,
  input  XS5N,
  input  XCLO,
  input  XTES,
  input  XRMN,
  input  [3:0] XI_3_0_I,
  input  [3:0] XIB_7_4,
  output XFEC,
  output XWRI,
  output XMRN,
  output XRWN,
  output XECR,
  output XPAN,
  output XPEN,
  output XION,
  output XCSN,
  output XTRN,
  output XEPN,
  output XRIN,
  output XDON,
  output XPSN,
  output XVAL,
  output XRUN,
  output XEUN,
  output XDVN,
  output XPIN,
  output XOCN,
  output XFMI,
  output XWHN,
  output XESN,
  output XSWN,
  output XSHN,
  output XSSN,
  output XCRN,
  output XRTN,
  output XDTN,
  output XRQN,
  output XSCN,
  output XLHN,
  output XFON,
  output XC10,
  output [3:0] XI_3_0_O,
  output [3:0] XI_3_0_C,
  output XRFN,
  output XTOT,
  output XPSC,
  output XPFN,
  output XTE0,
  output XPNN,
  output XMCL,
  output XCLN,
  output XSTP,
  output [7:0] XA_7_0,
  output [7:0] XA_7_0_C,
  output XEMN,
  output XFUN
);

  wire A090_n02, buffer_2_out, CLEAR, COMM_clrtin, COMM_sstopn, COMM_startn, EMCLN, IDB0, IDB1, IDB2, IDBI0,
       IDBI1, IDBI2, IDBI3, IDBS_prqn, LDPANCN, RESET, STPN;
  wire [7:0] AD_7_0, buffer_1_out;
  wire [12:0] PFIFC_wel_12_0, PFIFC_weu_12_0;

  not not_1 (XCLN, CLEAR);
  not not_2 (XSTP, STPN);
  assign buffer_1_out = AD_7_0;  // Buffer buffer_1, 8 bits wide
  buf buffer_2 (buffer_2_out, XRMN);
  not not_3 (XA_7_0_C[7], buffer_2_out);
  assign XA_7_0 = XA_7_0_C[7] ? buffer_1_out : 8'bz;  // Controlled_Buffer controlled_buffer_1
  DECODE_DGA_IDBS IDBS (
    .CSIDBS_4_0(XID_4_0), .LCSN(XLCN), .CLK0(XCLK), .CLK1(XCLK), .STAT4(XST_4_3[1]), .STAT3(XST_4_3[0]),
    .ECSRN(XCSN), .EIORN(XION), .EPESN(XPEN), .EPEAN(XPAN), .RUARTN(XRUN), .EDON(XDON), .EPANSN(XPSN),
    .RINRN(XRIN), .EPANN(XEPN), .TRAALDN(XTRN), .PRQN(IDBS_prqn), .VAL(XVAL));
  DECODE_DGA_COMM COMM (
    .CSCOMM_4_0(XCO_4_0), .LCSN(XLCN), .CSMIS_1_0(XMI_1_0), .CLK2(XCLK), .CLK3(XCLK), .EORFN(XEON),
    .IDBI5(XIB_7_4[1]), .IDBI7(XIB_7_4[3]), .CLEAR(CLEAR), .PONI(XPDI), .IDBI2(IDBI2), .CLK1(XCLK),
    .HITN(XHIN), .BRKN(XBRN), .LSHADOW(XLSH), .DAPN(XDAN), .UCLK(XUCK), .FETCH(XFEC), .FMISS(XFMI),
    .DTN(XDTN), .WRITE(XWRI), .RTN(XRTN), .FORMN(XFON), .MREQ(XMRN), .CCLRN(XCRN), .SSTOPN(COMM_sstopn),
    .CLRTIN(COMM_clrtin), .CEUARTN(XEUN), .SSEMAN(XSSN), .EMPIDN(XPIN), .SLOWN(XSWN), .LDPANCN(LDPANCN),
    .STARTN(COMM_startn), .WCHIMN(XWHN), .EMCLN(EMCLN), .RESET(RESET), .SIOCN(XOCN), .DVACCN(XDVN),
    .SHORTN(XSHN), .IORQN(XRQN), .RWCSN(XRWN), .LHIT(XLHN), .ESTOFN(XESN), .ECREQ(XECR), .STOCN(XSCN),
    .CA10(XC10));
  not not_4 (XI_3_0_C[3], XEPN);
  F091 A090 (.N02(A090_n02));  // open: N01
  Multiplexer multiplexer_1 (.in0(XI_3_0_I[3]), .in1(A090_n02), .out(IDBI3), .sel(XI_3_0_C[3]));
  Multiplexer multiplexer_2 (.in0(XI_3_0_I[2]), .in1(IDB2), .out(IDBI2), .sel(XI_3_0_C[3]));
  Multiplexer multiplexer_3 (.in0(XI_3_0_I[1]), .in1(IDB1), .out(IDBI1), .sel(XI_3_0_C[3]));
  Multiplexer multiplexer_4 (.in0(XI_3_0_I[0]), .in1(IDB0), .out(IDBI0), .sel(XI_3_0_C[3]));
  assign XI_3_0_O[3] = XI_3_0_C[3] ? IDBI3 : 1'bz;  // Controlled_Buffer controlled_buffer_2
  assign XI_3_0_O[2] = XI_3_0_C[3] ? IDBI2 : 1'bz;  // Controlled_Buffer controlled_buffer_3
  assign XI_3_0_O[1] = XI_3_0_C[3] ? IDBI1 : 1'bz;  // Controlled_Buffer controlled_buffer_4
  assign XI_3_0_O[0] = XI_3_0_C[3] ? IDBI0 : 1'bz;  // Controlled_Buffer controlled_buffer_5
  DECODE_DGA_PFIFC PFIFC (
    .CLEAR(CLEAR), .LDPANCN(LDPANCN), .RMMN(XRMN), .FULN(XFUN), .WEL_12_0(PFIFC_wel_12_0),
    .WEU_12_0(PFIFC_weu_12_0), .EMPN(XEMN));
  DECODE_DGA_POW POW (
    .EMCLN(EMCLN), .LOADN(XLON), .CLRTIN(COMM_clrtin), .CONTINUEN(XCON), .SSTOPN(COMM_sstopn), .STOPN(XTON),
    .STARTN(COMM_startn), .PWCL(XPWC), .RTOSC(XRTO), .TESTE(XTES), .POWSENSE(XPOW), .PRQN(IDBS_prqn),
    .SEL5MSN(XS5N), .BDRY50N(XBDN), .REFN(XEFN), .CLOSC(XCLO), .RESET(RESET), .MCL(XMCL), .STPN(STPN),
    .CLEAR(CLEAR), .POWFAILN(XPFN), .IDB2(IDB2), .IDB1(IDB1), .IDB0(IDB0), .PANN(XPNN), .TESTO(XTE0),
    .PANOSC(XPSC), .REFRQN(XRFN), .TOUT(XTOT));
  DECODE_DGA_PFIFD PFIFD (
    .IDBI_7_0({XIB_7_4, IDBI3, IDBI2, IDBI1, IDBI0}), .WEL_12_0(PFIFC_wel_12_0), .WEU_12_0(PFIFC_weu_12_0),
    .AD_7_0(AD_7_0));

  assign XA_7_0_C[6:0] = {7{XA_7_0_C[7]}};
  assign XI_3_0_C[2:0] = {3{XI_3_0_C[3]}};

  // Other names for the same wires on the sheet: BDRY50N = XBDN; BRKN = XBRN; CA10 = XC10; CCLRN = XCRN;
  //   CEUARTN = XEUN; CLK0 = XCLK; CLK1 = XCLK; CLK2 = XCLK; CLK3 = XCLK; CLOSC = XCLO; CONTINUEN = XCON;
  //   CSCOMM_4_0[4:0] = XCO_4_0; CSIDBS_4_0[4:0] = XID_4_0; CSMIS_1_0[1:0] = XMI_1_0; DAPN = XDAN; DTN = XDTN;
  //   DVACCN = XDVN; ECREQ = XECR; ECSRN = XCSN; EDON = XDON; EIORN = XION; EMPIDN = XPIN; EMPN = XEMN; EORFN = XEON;
  //   EPANN = XEPN; EPANSN = XPSN; EPEAN = XPAN; EPESN = XPEN; ESTOFN = XESN; FETCH = XFEC; FMISS = XFMI;
  //   FORMN = XFON; FULN = XFUN; HITN = XHIN; IDBI_7_0[7:0] = {XIB_7_4, IDBI3, IDBI2, IDBI1, IDBI0};
  //   IDBI4 = XIB_7_4[0]; IDBI5 = XIB_7_4[1]; IDBI6 = XIB_7_4[2]; IDBI7 = XIB_7_4[3]; IORQN = XRQN; LCSN = XLCN;
  //   LHIT = XLHN; LOADN = XLON; LSHADOW = XLSH; MCL = XMCL; MREQ = XMRN; PANN = XPNN; PANOSC = XPSC; PONI = XPDI;
  //   POWFAILN = XPFN; POWSENSE = XPOW; PWCL = XPWC; REFN = XEFN; REFRQN = XRFN; RINRN = XRIN; RMMN = XRMN;
  //   RTN = XRTN; RTOSC = XRTO; RUARTN = XRUN; RWCSN = XRWN; SEL5MSN = XS5N; SHORTN = XSHN; SIOCN = XOCN;
  //   SLOWN = XSWN; SSEMAN = XSSN; STAT3 = XST_4_3[0]; STAT_4_3[1:0] = XST_4_3; STAT4 = XST_4_3[1]; STOCN = XSCN;
  //   STOPN = XTON; TEST0 = XTE0; TESTE = XTES; TOUT = XTOT; TRAALDN = XTRN; UCLK = XUCK; VAL = XVAL; WCHIMN = XWHN;
  //   WRITE = XWRI; XI0 = XI_3_0_I[0]; XI1 = XI_3_0_I[1]; XI2 = XI_3_0_I[2]; XI3 = XI_3_0_I[3]; XO0 = XI_3_0_O[0];
  //   XO1 = XI_3_0_O[1]; XO2 = XI_3_0_O[2]; XO3 = XI_3_0_O[3]

  // Notes on the sheet:
  //   XI_3_0_C: pull=up
  //   XI_3_0_O: pull=up
  //   XA_7_0: pull=up
  //   External signals coming IN to the DGA chip
  //   Internal signals OUT of DGA chip
  //   Internal signals OUT of DGA chip
  //   Internal signals IN and OUT of DGA chip
  //   Simplified the DGA design
  //   PDF Page 2 -> DECODE - DECODE_DGA- Sheet 1 of 6
  //   PDF Page 3 -> DECODE - DECODE_DGA- Sheet 2 of 6
  //   PDF Page 4 -> DECODE - DECODE_DGA- Sheet 3 of 6
  //   PDF Page 5 -> DECODE - DECODE_DGA- Sheet 4 of 6
  //   PDF Page 6 -> DECODE - DECODE_DGA- Sheet 5 of 6
  //   Internal signals IN and OUT of DGA chip
  //   Internal to external signals (sheet 5 of 6)
  //   PDF Page 7 -> DECODE - DECODE_DGA- Sheet 6 of 6
  //   Still wont compile to HDL, needs to be fixed by hand
  //   FIX IN VERILOG
  //   Redesignet circuit from original drawing, added second controlles buffer to control incomming signal from XI_3_0_I
endmodule

module DECODE_DGA_POW (
  input  EMCLN,
  input  LOADN,
  input  CLRTIN,
  input  CONTINUEN,
  input  SSTOPN,
  input  STOPN,
  input  STARTN,
  input  PWCL,
  input  RTOSC,
  input  TESTE,
  input  POWSENSE,
  input  PRQN,
  input  SEL5MSN,
  input  BDRY50N,
  input  REFN,
  input  CLOSC,
  input  RESET,
  output MCL,
  output STPN,
  output CLEAR,
  output POWFAILN,
  output IDB2,
  output IDB1,
  output IDB0,
  output PANN,
  output TESTO,
  output PANOSC,
  output REFRQN,
  output TOUT
);

  wire A504_out, A569_n02_qb, A570_n02_qb, A572_qn, A578_out, A579_out, A580_out, A590_out, A591_n02_qb,
       A592_out, A593_n02_qb, A594_n02_qb, A596_n02_qb, A597_out, A598_out, A599_out, A601_y, A602_n02_qb,
       A605_n02_qb, A609_out, A611_out, A613_n01, A616_q, A617_qn, A618_q, A618_qn, A620_y, A621_n02_qb,
       A622_n02_qb, A623_n02_qb, A624_n02_qb, A626_n02_qb, A627_n02_qb, A628_f_out, A631_n01_q, A632_n02_qb,
       A633_n02_qb, A634_n02_qb, A635_out, A637_n02, CONN, LODN, MCLN, MS20, not_1_out, not_2_out, not_4_out,
       not_5_out, not_6_out, not_7_out, not_9_out, not_10_out, not_11_out, not_12_out, not_13_out,
       not_15_out, not_16_out, POWFAIL, RSTN, RTCN, STP, ZZ1;

  not not_1 (not_1_out, CONTINUEN);
  not not_2 (not_2_out, PWCL);
  not not_3 (POWFAILN, POWFAIL);
  not A504 (A504_out, LOADN);
  nand A579 (A579_out, MCLN, CLRTIN, STP);
  nand A578 (A578_out, STPN, not_2_out);
  nor A635 (A635_out, CLOSC, RESET);
  F091 A613 (.N01(A613_n01));  // open: N02
  F103 A628 (.F_IN(A635_out), .F_OUT(A628_f_out));
  F595 A576 (.H01_S(A504_out), .H02_R(A579_out), .H03_G(ZZ1), .N02_QB(LODN));  // open: N01_Q
  F595 A574 (.H01_S(A572_qn), .H02_R(A579_out), .H03_G(ZZ1), .N02_QB(RSTN));  // open: N01_Q
  F571 A601 (.D0(MS20), .D1(RTOSC), .A(TESTE), .ENB_N(1'b0), .Y(A601_y));
  not not_4 (not_4_out, CONN);
  not not_5 (not_5_out, A613_n01);
  not not_6 (not_6_out, PRQN);
  not not_7 (not_7_out, RTCN);
  F595 A575 (.H01_S(not_1_out), .H02_R(A579_out), .H03_G(ZZ1), .N02_QB(CONN));  // open: N01_Q
  F595 A569 (.H01_S(A578_out), .H02_R(POWFAILN), .H03_G(ZZ1), .N02_QB(A569_n02_qb));  // open: N01_Q
  F714 A623 (.H03_S(1'b0), .H01_T(RTOSC), .H02_R(A628_f_out), .N02_QB(A623_n02_qb));  // open: N01_Q
  F714 A633 (.H03_S(1'b0), .H01_T(RTOSC), .H02_R(CLOSC), .N02_QB(A633_n02_qb));  // open: N01_Q
  not not_8 (CLEAR, A569_n02_qb);
  J_K_Flip_Flop A616 (
    .J(A618_qn), .K(1'b1), .clk(A624_n02_qb), .Q(A616_q), .preset(1'b0), .reset(A628_f_out));  // open: Qn
  F091 A613B (.N01(ZZ1));  // open: N02
  F714 A596 (.H03_S(1'b0), .H01_T(A601_y), .H02_R(POWSENSE), .N02_QB(A596_n02_qb));  // open: N01_Q
  F714 A632 (.H03_S(1'b0), .H01_T(A623_n02_qb), .H02_R(A628_f_out), .N02_QB(A632_n02_qb));  // open: N01_Q
  F714 A629 (.H03_S(1'b0), .H01_T(A633_n02_qb), .H02_R(CLOSC), .N02_QB(PANOSC));  // open: N01_Q
  nand A597 (A597_out, CONN, LODN, not_6_out);
  nand A609 (A609_out, CONN, LODN, not_5_out);
  nand A598 (A598_out, RSTN, not_4_out);
  nand A599 (A599_out, not_7_out, PRQN, LODN, RSTN);
  not not_9 (not_9_out, STARTN);
  nand A590 (A590_out, not_5_out, LODN, RSTN);
  J_K_Flip_Flop A618 (
    .J(A616_q), .K(1'b1), .clk(A624_n02_qb), .Q(A618_q), .Qn(A618_qn), .preset(1'b0), .reset(A628_f_out));
  nand A580 (A580_out, SSTOPN, A569_n02_qb, STOPN);
  F714 A602 (.H03_S(1'b0), .H01_T(A596_n02_qb), .H02_R(POWSENSE), .N02_QB(A602_n02_qb));  // open: N01_Q
  nand A606 (IDB2, LODN, CONN, RSTN, MCLN);
  nand A592 (A592_out, MCLN, RSTN, CONN, LODN, A613_n01, PRQN, RTCN, STPN);
  F714 A634 (.H03_S(1'b0), .H01_T(A632_n02_qb), .H02_R(A628_f_out), .N02_QB(A634_n02_qb));  // open: N01_Q
  F595 A570 (.H01_S(STPN), .H02_R(PWCL), .H03_G(ZZ1), .N02_QB(A570_n02_qb));  // open: N01_Q
  nand A603 (IDB1, A597_out, RSTN, MCLN, A609_out);
  nand A604 (IDB0, MCLN, A598_out, A599_out, A590_out);
  nand A595 (PANN, SSTOPN, A592_out);
  F595 A571 (.H01_S(A580_out), .H02_R(not_9_out), .H03_G(ZZ1), .N01_Q(STP), .N02_QB(STPN));
  not not_10 (not_10_out, CLRTIN);
  not not_11 (not_11_out, ZZ1);
  F714 A593 (.H03_S(1'b0), .H01_T(A602_n02_qb), .H02_R(POWSENSE), .N02_QB(A593_n02_qb));  // open: N01_Q
  F714 A621 (.H03_S(1'b0), .H01_T(A634_n02_qb), .H02_R(A628_f_out), .N02_QB(A621_n02_qb));  // open: N01_Q
  F091 A637 (.N02(A637_n02));  // open: N01
  nand A573 (MCL, EMCLN, A569_n02_qb);
  not not_12 (not_12_out, CLRTIN);
  D_Flip_Flop A577 (.D(1'b0), .clk(MS20), .Q(RTCN), .preset(not_12_out), .reset(not_13_out));  // open: Qn
  not not_13 (not_13_out, ZZ1);
  D_Flip_Flop A572 (
    .D(A570_n02_qb), .clk(A569_n02_qb), .Qn(A572_qn), .preset(not_10_out), .reset(not_11_out));  // open: Q
  J_K_Flip_Flop A617 (
    .J(A618_q), .K(A618_q), .clk(A624_n02_qb), .Qn(A617_qn), .preset(1'b0), .reset(A628_f_out));  // open: Q
  not not_14 (MCLN, MCL);
  F714 A594 (.H03_S(1'b0), .H01_T(A593_n02_qb), .H02_R(POWSENSE), .N02_QB(A594_n02_qb));  // open: N01_Q
  F714 A622 (.H03_S(1'b0), .H01_T(A621_n02_qb), .H02_R(A628_f_out), .N02_QB(A622_n02_qb));  // open: N01_Q
  F617 A630 (.H04_SB(REFN), .H01_D(A637_n02), .H02_C(A633_n02_qb), .H03_RB(1'b1), .N01_Q(REFRQN));  // open: N02_QB
  F714 A619 (.H03_S(1'b0), .H01_T(A622_n02_qb), .H02_R(A628_f_out), .N02_QB(TESTO));  // open: N01_Q
  F714 A591 (.H03_S(1'b0), .H01_T(A594_n02_qb), .H02_R(POWSENSE), .N02_QB(A591_n02_qb));  // open: N01_Q
  F714 A627 (.H03_S(1'b0), .H01_T(A617_qn), .H02_R(A628_f_out), .N02_QB(A627_n02_qb));  // open: N01_Q
  F714 A605 (.H03_S(1'b0), .H01_T(A591_n02_qb), .H02_R(POWSENSE), .N02_QB(A605_n02_qb));  // open: N01_Q
  nor A611 (A611_out, POWSENSE, PWCL);
  F617 A631 (.H04_SB(BDRY50N), .H01_D(REFRQN), .H02_C(A633_n02_qb), .H03_RB(1'b1), .N01_Q(A631_n01_q));  // open: N02_QB
  F571 A620 (.D0(TESTO), .D1(RTOSC), .A(TESTE), .ENB_N(1'b0), .Y(A620_y));
  F714 A626 (.H03_S(1'b0), .H01_T(A627_n02_qb), .H02_R(A628_f_out), .N02_QB(A626_n02_qb));  // open: N01_Q
  not not_15 (not_15_out, A611_out);
  D_Flip_Flop A600 (.D(1'b0), .clk(A605_n02_qb), .Q(POWFAIL), .preset(not_15_out), .reset(not_16_out));  // open: Qn
  not not_16 (not_16_out, POWFAIL);
  nor A636 (TOUT, A631_n01_q, A633_n02_qb);
  F714 A624 (.H03_S(1'b0), .H01_T(A620_y), .H02_R(A628_f_out), .N02_QB(A624_n02_qb));  // open: N01_Q
  F571 A625 (.D0(A617_qn), .D1(A626_n02_qb), .A(SEL5MSN), .ENB_N(1'b0), .Y(MS20));

  // Notes on the sheet:
  //   Page 8 DECODE - DECODE_DGA_POW- Sheet 1 of 3
  //   Page 9 DECODE - DECODE_DGA_POW- Sheet 2 of 3
  //   Page 10 DECODE - DECODE_DGA_POW- Sheet 3 of 3
  //   CONTINUE
  //   Restart
  //   Continue
  //   Load
  //   Panel Request)
  //   Stop
  //   F103 = INVERTER
  //   LOAD
  //   CLRTIN
  //   ZZ1
  //   Master Clear
  //   Real Time Clock
  //   RESCL
  //   RESCL
  //   CLEARN
  //   STPN
  //   A616, A618 and A617 = F774 (JK Flip Flop with R,S)
  //   START
  //   Via PANVC at 003760
  //   IDB[2:0] values are mapped to microcode functions
  //   And are read when there is a PANEL Trap
  //   CLEARN
  //   CLRTIN
  //   CLEARN
  //   STPN
  //   RTCN
  //   RESCL
  //   RESCL
  //   POWSN
  //   A600 = F617 => D-F/F WIRH RB,SB
endmodule

module DECODE_DGA_PFIFD (
  input  [7:0] IDBI_7_0,
  input  [12:0] WEL_12_0,
  input  [12:0] WEU_12_0,
  output [7:0] AD_7_0
);

  wire d_ff_1_q, d_ff_2_q, d_ff_3_q, d_ff_4_q, d_ff_5_q, d_ff_6_q, d_ff_7_q, d_ff_8_q, d_ff_9_q, d_ff_10_q,
       d_ff_11_q, d_ff_12_q, d_ff_13_q, d_ff_14_q, d_ff_15_q, d_ff_16_q, d_ff_17_q, d_ff_18_q, d_ff_19_q,
       d_ff_20_q, d_ff_21_q, d_ff_22_q, d_ff_23_q, d_ff_24_q, d_ff_25_q, d_ff_26_q, d_ff_27_q, d_ff_28_q,
       d_ff_29_q, d_ff_30_q, d_ff_31_q, d_ff_32_q, d_ff_33_q, d_ff_34_q, d_ff_35_q, d_ff_36_q, d_ff_37_q,
       d_ff_38_q, d_ff_39_q, d_ff_40_q, d_ff_41_q, d_ff_42_q, d_ff_43_q, d_ff_44_q, d_ff_45_q, d_ff_46_q,
       d_ff_47_q, d_ff_48_q, d_ff_49_q, d_ff_50_q, d_ff_51_q, d_ff_52_q, d_ff_53_q, d_ff_54_q, d_ff_55_q,
       d_ff_56_q, d_ff_57_q, d_ff_58_q, d_ff_59_q, d_ff_60_q, d_ff_61_q, d_ff_62_q, d_ff_63_q, d_ff_64_q,
       d_ff_65_q, d_ff_66_q, d_ff_67_q, d_ff_68_q, d_ff_69_q, d_ff_70_q, d_ff_71_q, d_ff_72_q, d_ff_73_q,
       d_ff_74_q, d_ff_75_q, d_ff_76_q, d_ff_77_q, d_ff_78_q, d_ff_79_q, d_ff_80_q, d_ff_81_q, d_ff_82_q,
       d_ff_83_q, d_ff_84_q, d_ff_85_q, d_ff_86_q, d_ff_87_q, d_ff_88_q, d_ff_89_q, d_ff_90_q, d_ff_91_q,
       d_ff_92_q, d_ff_93_q, d_ff_94_q, d_ff_95_q, d_ff_96_q;

  D_Flip_Flop d_ff_1 (.D(IDBI_7_0[7]), .clk(WEU_12_0[0]), .Q(d_ff_1_q));  // open: Qn, preset, reset
  D_Flip_Flop d_ff_2 (.D(IDBI_7_0[6]), .clk(WEU_12_0[0]), .Q(d_ff_2_q));  // open: Qn, preset, reset
  D_Flip_Flop d_ff_3 (.D(IDBI_7_0[5]), .clk(WEU_12_0[0]), .Q(d_ff_3_q));  // open: Qn, preset, reset
  D_Flip_Flop d_ff_4 (.D(IDBI_7_0[4]), .clk(WEU_12_0[0]), .Q(d_ff_4_q));  // open: Qn, preset, reset
  D_Flip_Flop d_ff_5 (.D(IDBI_7_0[3]), .clk(WEL_12_0[0]), .Q(d_ff_5_q));  // open: Qn, preset, reset
  D_Flip_Flop d_ff_6 (.D(IDBI_7_0[2]), .clk(WEL_12_0[0]), .Q(d_ff_6_q));  // open: Qn, preset, reset
  D_Flip_Flop d_ff_7 (.D(IDBI_7_0[1]), .clk(WEL_12_0[0]), .Q(d_ff_7_q));  // open: Qn, preset, reset
  D_Flip_Flop d_ff_8 (.D(IDBI_7_0[0]), .clk(WEL_12_0[0]), .Q(d_ff_8_q));  // open: Qn, preset, reset
  D_Flip_Flop d_ff_9 (.D(d_ff_1_q), .clk(WEU_12_0[1]), .Q(d_ff_9_q));  // open: Qn, preset, reset
  D_Flip_Flop d_ff_10 (.D(d_ff_2_q), .clk(WEU_12_0[1]), .Q(d_ff_10_q));  // open: Qn, preset, reset
  D_Flip_Flop d_ff_11 (.D(d_ff_3_q), .clk(WEU_12_0[1]), .Q(d_ff_11_q));  // open: Qn, preset, reset
  D_Flip_Flop d_ff_12 (.D(d_ff_4_q), .clk(WEU_12_0[1]), .Q(d_ff_12_q));  // open: Qn, preset, reset
  D_Flip_Flop d_ff_13 (.D(d_ff_5_q), .clk(WEL_12_0[1]), .Q(d_ff_13_q));  // open: Qn, preset, reset
  D_Flip_Flop d_ff_14 (.D(d_ff_6_q), .clk(WEL_12_0[1]), .Q(d_ff_14_q));  // open: Qn, preset, reset
  D_Flip_Flop d_ff_15 (.D(d_ff_7_q), .clk(WEL_12_0[1]), .Q(d_ff_15_q));  // open: Qn, preset, reset
  D_Flip_Flop d_ff_16 (.D(d_ff_8_q), .clk(WEL_12_0[1]), .Q(d_ff_16_q));  // open: Qn, preset, reset
  D_Flip_Flop d_ff_17 (.D(d_ff_9_q), .clk(WEU_12_0[2]), .Q(d_ff_17_q));  // open: Qn, preset, reset
  D_Flip_Flop d_ff_18 (.D(d_ff_10_q), .clk(WEU_12_0[2]), .Q(d_ff_18_q));  // open: Qn, preset, reset
  D_Flip_Flop d_ff_19 (.D(d_ff_11_q), .clk(WEU_12_0[2]), .Q(d_ff_19_q));  // open: Qn, preset, reset
  D_Flip_Flop d_ff_20 (.D(d_ff_12_q), .clk(WEU_12_0[2]), .Q(d_ff_20_q));  // open: Qn, preset, reset
  D_Flip_Flop d_ff_21 (.D(d_ff_13_q), .clk(WEL_12_0[2]), .Q(d_ff_21_q));  // open: Qn, preset, reset
  D_Flip_Flop d_ff_22 (.D(d_ff_14_q), .clk(WEL_12_0[2]), .Q(d_ff_22_q));  // open: Qn, preset, reset
  D_Flip_Flop d_ff_23 (.D(d_ff_15_q), .clk(WEL_12_0[2]), .Q(d_ff_23_q));  // open: Qn, preset, reset
  D_Flip_Flop d_ff_24 (.D(d_ff_16_q), .clk(WEL_12_0[2]), .Q(d_ff_24_q));  // open: Qn, preset, reset
  D_Flip_Flop d_ff_25 (.D(d_ff_17_q), .clk(WEU_12_0[3]), .Q(d_ff_25_q));  // open: Qn, preset, reset
  D_Flip_Flop d_ff_26 (.D(d_ff_18_q), .clk(WEU_12_0[3]), .Q(d_ff_26_q));  // open: Qn, preset, reset
  D_Flip_Flop d_ff_27 (.D(d_ff_19_q), .clk(WEU_12_0[3]), .Q(d_ff_27_q));  // open: Qn, preset, reset
  D_Flip_Flop d_ff_28 (.D(d_ff_20_q), .clk(WEU_12_0[3]), .Q(d_ff_28_q));  // open: Qn, preset, reset
  D_Flip_Flop d_ff_29 (.D(d_ff_21_q), .clk(WEL_12_0[3]), .Q(d_ff_29_q));  // open: Qn, preset, reset
  D_Flip_Flop d_ff_30 (.D(d_ff_22_q), .clk(WEL_12_0[3]), .Q(d_ff_30_q));  // open: Qn, preset, reset
  D_Flip_Flop d_ff_31 (.D(d_ff_23_q), .clk(WEL_12_0[3]), .Q(d_ff_31_q));  // open: Qn, preset, reset
  D_Flip_Flop d_ff_32 (.D(d_ff_24_q), .clk(WEL_12_0[3]), .Q(d_ff_32_q));  // open: Qn, preset, reset
  D_Flip_Flop d_ff_33 (.D(d_ff_25_q), .clk(WEU_12_0[4]), .Q(d_ff_33_q));  // open: Qn, preset, reset
  D_Flip_Flop d_ff_34 (.D(d_ff_26_q), .clk(WEU_12_0[4]), .Q(d_ff_34_q));  // open: Qn, preset, reset
  D_Flip_Flop d_ff_35 (.D(d_ff_27_q), .clk(WEU_12_0[4]), .Q(d_ff_35_q));  // open: Qn, preset, reset
  D_Flip_Flop d_ff_36 (.D(d_ff_28_q), .clk(WEU_12_0[4]), .Q(d_ff_36_q));  // open: Qn, preset, reset
  D_Flip_Flop d_ff_37 (.D(d_ff_29_q), .clk(WEL_12_0[4]), .Q(d_ff_37_q));  // open: Qn, preset, reset
  D_Flip_Flop d_ff_38 (.D(d_ff_30_q), .clk(WEL_12_0[4]), .Q(d_ff_38_q));  // open: Qn, preset, reset
  D_Flip_Flop d_ff_39 (.D(d_ff_31_q), .clk(WEL_12_0[4]), .Q(d_ff_39_q));  // open: Qn, preset, reset
  D_Flip_Flop d_ff_40 (.D(d_ff_32_q), .clk(WEL_12_0[4]), .Q(d_ff_40_q));  // open: Qn, preset, reset
  D_Flip_Flop d_ff_41 (.D(d_ff_33_q), .clk(WEU_12_0[5]), .Q(d_ff_41_q));  // open: Qn, preset, reset
  D_Flip_Flop d_ff_42 (.D(d_ff_34_q), .clk(WEU_12_0[5]), .Q(d_ff_42_q));  // open: Qn, preset, reset
  D_Flip_Flop d_ff_43 (.D(d_ff_35_q), .clk(WEU_12_0[5]), .Q(d_ff_43_q));  // open: Qn, preset, reset
  D_Flip_Flop d_ff_44 (.D(d_ff_36_q), .clk(WEU_12_0[5]), .Q(d_ff_44_q));  // open: Qn, preset, reset
  D_Flip_Flop d_ff_45 (.D(d_ff_37_q), .clk(WEL_12_0[5]), .Q(d_ff_45_q));  // open: Qn, preset, reset
  D_Flip_Flop d_ff_46 (.D(d_ff_38_q), .clk(WEL_12_0[5]), .Q(d_ff_46_q));  // open: Qn, preset, reset
  D_Flip_Flop d_ff_47 (.D(d_ff_39_q), .clk(WEL_12_0[5]), .Q(d_ff_47_q));  // open: Qn, preset, reset
  D_Flip_Flop d_ff_48 (.D(d_ff_40_q), .clk(WEL_12_0[5]), .Q(d_ff_48_q));  // open: Qn, preset, reset
  D_Flip_Flop d_ff_49 (.D(d_ff_41_q), .clk(WEU_12_0[6]), .Q(d_ff_49_q));  // open: Qn, preset, reset
  D_Flip_Flop d_ff_50 (.D(d_ff_42_q), .clk(WEU_12_0[6]), .Q(d_ff_50_q));  // open: Qn, preset, reset
  D_Flip_Flop d_ff_51 (.D(d_ff_43_q), .clk(WEU_12_0[6]), .Q(d_ff_51_q));  // open: Qn, preset, reset
  D_Flip_Flop d_ff_52 (.D(d_ff_44_q), .clk(WEU_12_0[6]), .Q(d_ff_52_q));  // open: Qn, preset, reset
  D_Flip_Flop d_ff_53 (.D(d_ff_45_q), .clk(WEL_12_0[6]), .Q(d_ff_53_q));  // open: Qn, preset, reset
  D_Flip_Flop d_ff_54 (.D(d_ff_46_q), .clk(WEL_12_0[6]), .Q(d_ff_54_q));  // open: Qn, preset, reset
  D_Flip_Flop d_ff_55 (.D(d_ff_47_q), .clk(WEL_12_0[6]), .Q(d_ff_55_q));  // open: Qn, preset, reset
  D_Flip_Flop d_ff_56 (.D(d_ff_48_q), .clk(WEL_12_0[6]), .Q(d_ff_56_q));  // open: Qn, preset, reset
  D_Flip_Flop d_ff_57 (.D(d_ff_49_q), .clk(WEU_12_0[7]), .Q(d_ff_57_q));  // open: Qn, preset, reset
  D_Flip_Flop d_ff_58 (.D(d_ff_50_q), .clk(WEU_12_0[7]), .Q(d_ff_58_q));  // open: Qn, preset, reset
  D_Flip_Flop d_ff_59 (.D(d_ff_51_q), .clk(WEU_12_0[7]), .Q(d_ff_59_q));  // open: Qn, preset, reset
  D_Flip_Flop d_ff_60 (.D(d_ff_52_q), .clk(WEU_12_0[7]), .Q(d_ff_60_q));  // open: Qn, preset, reset
  D_Flip_Flop d_ff_61 (.D(d_ff_53_q), .clk(WEL_12_0[7]), .Q(d_ff_61_q));  // open: Qn, preset, reset
  D_Flip_Flop d_ff_62 (.D(d_ff_54_q), .clk(WEL_12_0[7]), .Q(d_ff_62_q));  // open: Qn, preset, reset
  D_Flip_Flop d_ff_63 (.D(d_ff_55_q), .clk(WEL_12_0[7]), .Q(d_ff_63_q));  // open: Qn, preset, reset
  D_Flip_Flop d_ff_64 (.D(d_ff_56_q), .clk(WEL_12_0[7]), .Q(d_ff_64_q));  // open: Qn, preset, reset
  D_Flip_Flop d_ff_65 (.D(d_ff_57_q), .clk(WEU_12_0[8]), .Q(d_ff_65_q));  // open: Qn, preset, reset
  D_Flip_Flop d_ff_66 (.D(d_ff_58_q), .clk(WEU_12_0[8]), .Q(d_ff_66_q));  // open: Qn, preset, reset
  D_Flip_Flop d_ff_67 (.D(d_ff_59_q), .clk(WEU_12_0[8]), .Q(d_ff_67_q));  // open: Qn, preset, reset
  D_Flip_Flop d_ff_68 (.D(d_ff_60_q), .clk(WEU_12_0[8]), .Q(d_ff_68_q));  // open: Qn, preset, reset
  D_Flip_Flop d_ff_69 (.D(d_ff_61_q), .clk(WEL_12_0[8]), .Q(d_ff_69_q));  // open: Qn, preset, reset
  D_Flip_Flop d_ff_70 (.D(d_ff_62_q), .clk(WEL_12_0[8]), .Q(d_ff_70_q));  // open: Qn, preset, reset
  D_Flip_Flop d_ff_71 (.D(d_ff_63_q), .clk(WEL_12_0[8]), .Q(d_ff_71_q));  // open: Qn, preset, reset
  D_Flip_Flop d_ff_72 (.D(d_ff_64_q), .clk(WEL_12_0[8]), .Q(d_ff_72_q));  // open: Qn, preset, reset
  D_Flip_Flop d_ff_73 (.D(d_ff_65_q), .clk(WEU_12_0[9]), .Q(d_ff_73_q));  // open: Qn, preset, reset
  D_Flip_Flop d_ff_74 (.D(d_ff_66_q), .clk(WEU_12_0[9]), .Q(d_ff_74_q));  // open: Qn, preset, reset
  D_Flip_Flop d_ff_75 (.D(d_ff_67_q), .clk(WEU_12_0[9]), .Q(d_ff_75_q));  // open: Qn, preset, reset
  D_Flip_Flop d_ff_76 (.D(d_ff_68_q), .clk(WEU_12_0[9]), .Q(d_ff_76_q));  // open: Qn, preset, reset
  D_Flip_Flop d_ff_77 (.D(d_ff_69_q), .clk(WEL_12_0[9]), .Q(d_ff_77_q));  // open: Qn, preset, reset
  D_Flip_Flop d_ff_78 (.D(d_ff_70_q), .clk(WEL_12_0[9]), .Q(d_ff_78_q));  // open: Qn, preset, reset
  D_Flip_Flop d_ff_79 (.D(d_ff_71_q), .clk(WEL_12_0[9]), .Q(d_ff_79_q));  // open: Qn, preset, reset
  D_Flip_Flop d_ff_80 (.D(d_ff_72_q), .clk(WEL_12_0[9]), .Q(d_ff_80_q));  // open: Qn, preset, reset
  D_Flip_Flop d_ff_81 (.D(d_ff_73_q), .clk(WEU_12_0[10]), .Q(d_ff_81_q));  // open: Qn, preset, reset
  D_Flip_Flop d_ff_82 (.D(d_ff_74_q), .clk(WEU_12_0[10]), .Q(d_ff_82_q));  // open: Qn, preset, reset
  D_Flip_Flop d_ff_83 (.D(d_ff_75_q), .clk(WEU_12_0[10]), .Q(d_ff_83_q));  // open: Qn, preset, reset
  D_Flip_Flop d_ff_84 (.D(d_ff_76_q), .clk(WEU_12_0[10]), .Q(d_ff_84_q));  // open: Qn, preset, reset
  D_Flip_Flop d_ff_85 (.D(d_ff_77_q), .clk(WEL_12_0[10]), .Q(d_ff_85_q));  // open: Qn, preset, reset
  D_Flip_Flop d_ff_86 (.D(d_ff_78_q), .clk(WEL_12_0[10]), .Q(d_ff_86_q));  // open: Qn, preset, reset
  D_Flip_Flop d_ff_87 (.D(d_ff_79_q), .clk(WEL_12_0[10]), .Q(d_ff_87_q));  // open: Qn, preset, reset
  D_Flip_Flop d_ff_88 (.D(d_ff_80_q), .clk(WEL_12_0[10]), .Q(d_ff_88_q));  // open: Qn, preset, reset
  D_Flip_Flop d_ff_89 (.D(d_ff_81_q), .clk(WEU_12_0[11]), .Q(d_ff_89_q));  // open: Qn, preset, reset
  D_Flip_Flop d_ff_90 (.D(d_ff_82_q), .clk(WEU_12_0[11]), .Q(d_ff_90_q));  // open: Qn, preset, reset
  D_Flip_Flop d_ff_91 (.D(d_ff_83_q), .clk(WEU_12_0[11]), .Q(d_ff_91_q));  // open: Qn, preset, reset
  D_Flip_Flop d_ff_92 (.D(d_ff_84_q), .clk(WEU_12_0[11]), .Q(d_ff_92_q));  // open: Qn, preset, reset
  D_Flip_Flop d_ff_93 (.D(d_ff_85_q), .clk(WEL_12_0[11]), .Q(d_ff_93_q));  // open: Qn, preset, reset
  D_Flip_Flop d_ff_94 (.D(d_ff_86_q), .clk(WEL_12_0[11]), .Q(d_ff_94_q));  // open: Qn, preset, reset
  D_Flip_Flop d_ff_95 (.D(d_ff_87_q), .clk(WEL_12_0[11]), .Q(d_ff_95_q));  // open: Qn, preset, reset
  D_Flip_Flop d_ff_96 (.D(d_ff_88_q), .clk(WEL_12_0[11]), .Q(d_ff_96_q));  // open: Qn, preset, reset
  D_Flip_Flop d_ff_97 (.D(d_ff_89_q), .clk(WEU_12_0[12]), .Q(AD_7_0[7]));  // open: Qn, preset, reset
  D_Flip_Flop d_ff_98 (.D(d_ff_90_q), .clk(WEU_12_0[12]), .Q(AD_7_0[6]));  // open: Qn, preset, reset
  D_Flip_Flop d_ff_99 (.D(d_ff_91_q), .clk(WEU_12_0[12]), .Q(AD_7_0[5]));  // open: Qn, preset, reset
  D_Flip_Flop d_ff_100 (.D(d_ff_92_q), .clk(WEU_12_0[12]), .Q(AD_7_0[4]));  // open: Qn, preset, reset
  D_Flip_Flop d_ff_101 (.D(d_ff_93_q), .clk(WEL_12_0[12]), .Q(AD_7_0[3]));  // open: Qn, preset, reset
  D_Flip_Flop d_ff_102 (.D(d_ff_94_q), .clk(WEL_12_0[12]), .Q(AD_7_0[2]));  // open: Qn, preset, reset
  D_Flip_Flop d_ff_103 (.D(d_ff_95_q), .clk(WEL_12_0[12]), .Q(AD_7_0[1]));  // open: Qn, preset, reset
  D_Flip_Flop d_ff_104 (.D(d_ff_96_q), .clk(WEL_12_0[12]), .Q(AD_7_0[0]));  // open: Qn, preset, reset

  // Other names for the same wires on the sheet: AD0 = AD_7_0[0]; AD1 = AD_7_0[1]; AD2 = AD_7_0[2]; AD3 = AD_7_0[3];
  //   AD4 = AD_7_0[4]; AD5 = AD_7_0[5]; AD6 = AD_7_0[6]; AD7 = AD_7_0[7]; IDBI0 = IDBI_7_0[0]; IDBI1 = IDBI_7_0[1];
  //   IDBI2 = IDBI_7_0[2]; IDBI3 = IDBI_7_0[3]; IDBI4 = IDBI_7_0[4]; IDBI5 = IDBI_7_0[5]; IDBI6 = IDBI_7_0[6];
  //   IDBI7 = IDBI_7_0[7]; WEL0 = WEL_12_0[0]; WEL1 = WEL_12_0[1]; WEL2 = WEL_12_0[2]; WEL3 = WEL_12_0[3];
  //   WEL4 = WEL_12_0[4]; WEL5 = WEL_12_0[5]; WEL6 = WEL_12_0[6]; WEL7 = WEL_12_0[7]; WEL8 = WEL_12_0[8];
  //   WEL9 = WEL_12_0[9]; WEL10 = WEL_12_0[10]; WEL11 = WEL_12_0[11]; WEL12 = WEL_12_0[12]; WEU0 = WEU_12_0[0];
  //   WEU1 = WEU_12_0[1]; WEU2 = WEU_12_0[2]; WEU3 = WEU_12_0[3]; WEU4 = WEU_12_0[4]; WEU5 = WEU_12_0[5];
  //   WEU6 = WEU_12_0[6]; WEU7 = WEU_12_0[7]; WEU8 = WEU_12_0[8]; WEU9 = WEU_12_0[9]; WEU10 = WEU_12_0[10];
  //   WEU11 = WEU_12_0[11]; WEU12 = WEU_12_0[12]

  // Notes on the sheet:
  //   Page 11 DECODE - DECODE_DGA_PFIFD Sheet 1 of 1
endmodule

module DECODE_DGA_PFIFC (
  input  CLEAR,
  input  LDPANCN,
  input  RMMN,
  output FULN,
  output [12:0] WEL_12_0,
  output [12:0] WEU_12_0,
  output EMPN
);

  wire A292_out, A296_pin_out, A300_out, A301_n01_q, A301_n02_qb, A302_n01_q, A302_n02_qb, A304_n01_q,
       A304_n02_qb, A305_n01_q, A308_n01_q, A308_n02_qb, A309_pin_out, A310_pin_out, A312_pin_out,
       A314_n01_q, A314_n02_qb, A315_n01_q, A315_n02_qb, A316_n01_q, A316_n02_qb, A321_n01_q, A321_n02_qb,
       A322_n01_q, A322_n02_qb, A323_pin_out, A331_pin_out, A334_n01_q, A334_n02_qb, A339_n01_q, A339_n02_qb,
       A343_n02_qb, A347_pin_out, A362_pin_out, A363_pin_out, A364_pin_out, A365_pin_out, A366_pin_out,
       and_1_out, and_2_out, and_3_out, and_4_out, and_5_out, and_6_out, and_7_out, and_8_out, and_9_out,
       and_10_out, and_11_out, and_12_out, and_13_out, CLEARN, nand_1_out, nand_2_out, nand_3_out,
       nand_4_out, nand_5_out, nand_6_out, nand_7_out, nand_8_out, nand_9_out, nand_10_out, nand_11_out,
       nand_12_out, nand_13_out, nand_14_out, nand_15_out, nand_16_out, nand_17_out, nand_18_out,
       nand_19_out, nand_20_out, nand_21_out, nand_22_out, nand_23_out, not_15_out, not_16_out, not_17_out,
       not_18_out, not_19_out, not_20_out, not_21_out, not_22_out, not_23_out, not_24_out, not_25_out,
       not_26_out, ZZ1;

  not not_1 (CLEARN, CLEAR);
  F091 A351 (.N01(ZZ1));  // open: N02
  DECODE_DGA_PFIFC_DELAY A309 (.PIN_IN(WEL_12_0[1]), .PIN_OUT(A309_pin_out));
  DECODE_DGA_PFIFC_DELAY A323 (.PIN_IN(WEL_12_0[2]), .PIN_OUT(A323_pin_out));
  DECODE_DGA_PFIFC_DELAY A312 (.PIN_IN(WEL_12_0[3]), .PIN_OUT(A312_pin_out));
  DECODE_DGA_PFIFC_DELAY A331 (.PIN_IN(WEL_12_0[4]), .PIN_OUT(A331_pin_out));
  DECODE_DGA_PFIFC_DELAY A347 (.PIN_IN(WEL_12_0[5]), .PIN_OUT(A347_pin_out));
  DECODE_DGA_PFIFC_DELAY A296 (.PIN_IN(WEL_12_0[6]), .PIN_OUT(A296_pin_out));
  DECODE_DGA_PFIFC_DELAY A310 (.PIN_IN(WEL_12_0[7]), .PIN_OUT(A310_pin_out));
  DECODE_DGA_PFIFC_DELAY A362 (.PIN_IN(WEL_12_0[8]), .PIN_OUT(A362_pin_out));
  DECODE_DGA_PFIFC_DELAY A363 (.PIN_IN(WEL_12_0[9]), .PIN_OUT(A363_pin_out));
  DECODE_DGA_PFIFC_DELAY A364 (.PIN_IN(WEL_12_0[10]), .PIN_OUT(A364_pin_out));
  DECODE_DGA_PFIFC_DELAY A365 (.PIN_IN(WEL_12_0[11]), .PIN_OUT(A365_pin_out));
  DECODE_DGA_PFIFC_DELAY A366 (.PIN_IN(WEL_12_0[12]), .PIN_OUT(A366_pin_out));
  and and_1 (and_1_out, WEL_12_0[0], WEL_12_0[0], CLEARN);
  nand nand_1 (nand_1_out, CLEARN, not_15_out);
  and and_2 (and_2_out, A309_pin_out, A309_pin_out, CLEARN);
  nand nand_2 (nand_2_out, CLEARN, not_16_out);
  and and_3 (and_3_out, A323_pin_out, A323_pin_out, CLEARN);
  nand nand_3 (nand_3_out, CLEARN, not_17_out);
  and and_4 (and_4_out, A312_pin_out, A312_pin_out, CLEARN);
  nand nand_4 (nand_4_out, CLEARN, not_18_out);
  and and_5 (and_5_out, A331_pin_out, A331_pin_out, CLEARN);
  nand nand_5 (nand_5_out, CLEARN, not_19_out);
  and and_6 (and_6_out, A347_pin_out, A347_pin_out, CLEARN);
  nand nand_6 (nand_6_out, CLEARN, not_20_out);
  and and_7 (and_7_out, A296_pin_out, A296_pin_out, CLEARN);
  nand nand_7 (nand_7_out, CLEARN, not_21_out);
  and and_8 (and_8_out, A310_pin_out, A310_pin_out, CLEARN);
  nand nand_8 (nand_8_out, CLEARN, not_22_out);
  and and_9 (and_9_out, A362_pin_out, A362_pin_out, CLEARN);
  nand nand_9 (nand_9_out, CLEARN, not_23_out);
  and and_10 (and_10_out, A363_pin_out, A363_pin_out, CLEARN);
  nand nand_10 (nand_10_out, CLEARN, not_24_out);
  and and_11 (and_11_out, A364_pin_out, A364_pin_out, CLEARN);
  nand nand_11 (nand_11_out, CLEARN, not_25_out);
  and and_12 (and_12_out, A365_pin_out, A365_pin_out, CLEARN);
  nand nand_12 (nand_12_out, CLEARN, not_26_out);
  and and_13 (and_13_out, A366_pin_out, A366_pin_out, CLEARN);
  nand nand_13 (nand_13_out, CLEARN, RMMN);
  F595 A305 (.H01_S(and_1_out), .H02_R(nand_1_out), .H03_G(ZZ1), .N01_Q(A305_n01_q), .N02_QB(FULN));
  F595 A314 (.H01_S(and_2_out), .H02_R(nand_2_out), .H03_G(ZZ1), .N01_Q(A314_n01_q), .N02_QB(A314_n02_qb));
  F595 A321 (.H01_S(and_3_out), .H02_R(nand_3_out), .H03_G(ZZ1), .N01_Q(A321_n01_q), .N02_QB(A321_n02_qb));
  F595 A316 (.H01_S(and_4_out), .H02_R(nand_4_out), .H03_G(ZZ1), .N01_Q(A316_n01_q), .N02_QB(A316_n02_qb));
  F595 A308 (.H01_S(and_5_out), .H02_R(nand_5_out), .H03_G(ZZ1), .N01_Q(A308_n01_q), .N02_QB(A308_n02_qb));
  F595 A322 (.H01_S(and_6_out), .H02_R(nand_6_out), .H03_G(ZZ1), .N01_Q(A322_n01_q), .N02_QB(A322_n02_qb));
  F595 A302 (.H01_S(and_7_out), .H02_R(nand_7_out), .H03_G(ZZ1), .N01_Q(A302_n01_q), .N02_QB(A302_n02_qb));
  F595 A304 (.H01_S(and_8_out), .H02_R(nand_8_out), .H03_G(ZZ1), .N01_Q(A304_n01_q), .N02_QB(A304_n02_qb));
  F595 A301 (.H01_S(and_9_out), .H02_R(nand_9_out), .H03_G(ZZ1), .N01_Q(A301_n01_q), .N02_QB(A301_n02_qb));
  F595 A315 (.H01_S(and_10_out), .H02_R(nand_10_out), .H03_G(ZZ1), .N01_Q(A315_n01_q), .N02_QB(A315_n02_qb));
  F595 A339 (.H01_S(and_11_out), .H02_R(nand_11_out), .H03_G(ZZ1), .N01_Q(A339_n01_q), .N02_QB(A339_n02_qb));
  F595 A334 (.H01_S(and_12_out), .H02_R(nand_12_out), .H03_G(ZZ1), .N01_Q(A334_n01_q), .N02_QB(A334_n02_qb));
  F595 A343 (.H01_S(and_13_out), .H02_R(nand_13_out), .H03_G(ZZ1), .N01_Q(EMPN), .N02_QB(A343_n02_qb));
  nand A300 (A300_out, LDPANCN, A305_n01_q, A314_n02_qb, not_16_out);
  nand A292 (A292_out, not_15_out, A314_n01_q, A321_n02_qb, not_17_out);
  nand nand_14 (nand_14_out, not_16_out, A321_n01_q, A316_n02_qb, not_18_out);
  nand nand_15 (nand_15_out, not_17_out, A316_n01_q, A308_n02_qb, not_19_out);
  nand nand_16 (nand_16_out, not_18_out, A308_n01_q, A322_n02_qb, not_20_out);
  nand nand_17 (nand_17_out, not_19_out, A322_n01_q, A302_n02_qb, not_21_out);
  nand nand_18 (nand_18_out, not_20_out, A302_n01_q, A304_n02_qb, not_22_out);
  nand nand_19 (nand_19_out, not_21_out, A304_n01_q, A301_n02_qb, not_23_out);
  nand nand_20 (nand_20_out, not_22_out, A301_n01_q, A315_n02_qb, not_24_out);
  nand nand_21 (nand_21_out, not_23_out, A315_n01_q, A339_n02_qb, not_25_out);
  nand nand_22 (nand_22_out, not_24_out, A339_n01_q, A334_n02_qb, not_26_out);
  nand nand_23 (nand_23_out, not_25_out, A334_n01_q, A343_n02_qb, RMMN);
  not not_2 (WEL_12_0[0], LDPANCN);
  not not_3 (WEL_12_0[1], A300_out);
  not not_4 (WEL_12_0[2], A292_out);
  not not_5 (WEL_12_0[3], nand_14_out);
  not not_6 (WEL_12_0[4], nand_15_out);
  not not_7 (WEL_12_0[5], nand_16_out);
  not not_8 (WEL_12_0[6], nand_17_out);
  not not_9 (WEL_12_0[7], nand_18_out);
  not not_10 (WEL_12_0[8], nand_19_out);
  not not_11 (WEL_12_0[9], nand_20_out);
  not not_12 (WEL_12_0[10], nand_21_out);
  not not_13 (WEL_12_0[11], nand_22_out);
  not not_14 (WEL_12_0[12], nand_23_out);
  not not_15 (not_15_out, WEL_12_0[1]);
  not not_16 (not_16_out, WEL_12_0[2]);
  not not_17 (not_17_out, WEL_12_0[3]);
  not not_18 (not_18_out, WEL_12_0[4]);
  not not_19 (not_19_out, WEL_12_0[5]);
  not not_20 (not_20_out, WEL_12_0[6]);
  not not_21 (not_21_out, WEL_12_0[7]);
  not not_22 (not_22_out, WEL_12_0[8]);
  not not_23 (not_23_out, WEL_12_0[9]);
  not not_24 (not_24_out, WEL_12_0[10]);
  not not_25 (not_25_out, WEL_12_0[11]);
  not not_26 (not_26_out, WEL_12_0[12]);

  assign WEU_12_0 = WEL_12_0;

  // Other names for the same wires on the sheet: WEL0 = WEL_12_0[0]; WEU0 = WEL_12_0[0]; WEL1 = WEL_12_0[1];
  //   WEU1 = WEL_12_0[1]; WEL2 = WEL_12_0[2]; WEU2 = WEL_12_0[2]; WEL3 = WEL_12_0[3]; WEU3 = WEL_12_0[3];
  //   WEL4 = WEL_12_0[4]; WEU4 = WEL_12_0[4]; WEL5 = WEL_12_0[5]; WEU5 = WEL_12_0[5]; WEL6 = WEL_12_0[6];
  //   WEU6 = WEL_12_0[6]; WEL7 = WEL_12_0[7]; WEU7 = WEL_12_0[7]; WEL8 = WEL_12_0[8]; WEU8 = WEL_12_0[8];
  //   WEL9 = WEL_12_0[9]; WEU9 = WEL_12_0[9]; WEL10 = WEL_12_0[10]; WEU10 = WEL_12_0[10]; WEL11 = WEL_12_0[11];
  //   WEU11 = WEL_12_0[11]; WEL12 = WEL_12_0[12]; WEU12 = WEL_12_0[12]

  // Notes on the sheet:
  //   WEL1
  //   WEL2
endmodule

module DECODE_DGA_PFIFC_DELAY (
  input  PIN_IN,
  output PIN_OUT
);

  wire buffer_1_out, buffer_2_out, buffer_3_out, buffer_4_out, buffer_5_out, buffer_6_out;

  buf buffer_1 (buffer_1_out, PIN_IN);
  buf buffer_2 (buffer_2_out, buffer_1_out);
  buf buffer_3 (buffer_3_out, buffer_2_out);
  buf buffer_4 (buffer_4_out, buffer_3_out);
  buf buffer_5 (buffer_5_out, buffer_4_out);
  buf buffer_6 (buffer_6_out, buffer_5_out);
  buf buffer_7 (PIN_OUT, buffer_6_out);

  // Notes on the sheet:
  //   Page 13 DECODE - DECODE_DGA_PFIFC_DELAY Sheet 1 of 1
endmodule

module DECODE_DGA_IDBS (
  input  [4:0] CSIDBS_4_0,
  input  LCSN,
  input  CLK0,
  input  CLK1,
  input  STAT4,
  input  STAT3,
  output ECSRN,
  output EIORN,
  output EPESN,
  output EPEAN,
  output RUARTN,
  output EDON,
  output EPANSN,
  output RINRN,
  output EPANN,
  output TRAALDN,
  output PRQN,
  output VAL
);

  wire A249_out, A250_out, A251_out, A252_out, A253_out, A254_out, A255_out, A256_out, A257_out, A258_out,
       A261_out, A262_out, A263_out, A264_out, A265_out, A269_out, A274_out, A282_n02_q1, A282_n03_q2,
       A282_n06_q1b, A282_n07_q2b, A282_n08_q3b, A283_out, A284_out, A285_out, A286_out, and_1_out,
       and_2_out, and_3_out, and_4_out, and_5_out, and_6_out, CSEPANSN, ID0N, ID1N, ID2N, ID3N, ID4N, MAPANS,
       ZZ1;

  not not_1 (ID0N, CSIDBS_4_0[0]);
  not not_2 (ID1N, CSIDBS_4_0[1]);
  not not_3 (ID2N, CSIDBS_4_0[2]);
  not not_4 (ID3N, CSIDBS_4_0[3]);
  not not_5 (ID4N, CSIDBS_4_0[4]);
  and and_1 (and_1_out, VAL, STAT4, MAPANS, LCSN);
  and and_2 (and_2_out, ZZ1, STAT4, LCSN, A282_n06_q1b);
  and and_3 (and_3_out, A282_n07_q2b, STAT3, LCSN);
  and and_4 (and_4_out, STAT3, LCSN, A282_n08_q3b);
  and and_5 (and_5_out, STAT3, A282_n03_q2, CSEPANSN, LCSN);
  and and_6 (and_6_out, ZZ1, CSEPANSN, A282_n08_q3b, LCSN);
  nand A286 (A286_out, A282_n02_q1, STAT4, LCSN);
  nor A284 (A284_out, and_1_out, and_2_out);
  nor A285 (A285_out, and_3_out, and_4_out);
  nor A283 (A283_out, and_5_out, and_6_out);
  nand A264 (A264_out, ID4N, ID3N, ID2N, LCSN);
  nand A262 (A262_out, CSIDBS_4_0[4], ID3N, CSIDBS_4_0[2], CSIDBS_4_0[1], ID0N, LCSN);
  nand A263 (A263_out, ID4N, ID3N, ID0N, LCSN);
  nand A250 (A250_out, ID4N, CSIDBS_4_0[3], ID1N, LCSN);
  nand A258 (A258_out, CSIDBS_4_0[4], ID3N, CSIDBS_4_0[2], CSIDBS_4_0[1], CSIDBS_4_0[0], LCSN);
  F924 A282 (
    .D0_H01(A286_out), .D1_H02(A284_out), .D2_H03(A285_out), .D3_H04(A283_out), .C_H05(CLK1),
    .N02_Q1(A282_n02_q1), .N03_Q2(A282_n03_q2), .N04_Q3(PRQN), .N05_Q0B(VAL), .N06_Q1B(A282_n06_q1b),
    .N07_Q2B(A282_n07_q2b), .N08_Q3B(A282_n08_q3b));  // open: N01_Q0
  nand A256 (A256_out, ID3N, ID2N, CSIDBS_4_0[1], LCSN);
  nand A249 (A249_out, A264_out, A263_out, A250_out, A256_out, A261_out, A269_out, A255_out, ZZ1);
  nand A265 (A265_out, CSIDBS_4_0[4], CSIDBS_4_0[3], CSIDBS_4_0[2], ID1N, CSIDBS_4_0[0], LCSN);
  nand A261 (A261_out, CSIDBS_4_0[4], ID3N, CSIDBS_4_0[2], ID1N, CSIDBS_4_0[0], LCSN);
  nand A260 (CSEPANSN, CSIDBS_4_0[4], ID3N, ID2N, ID1N, LCSN);
  nand A269 (A269_out, CSIDBS_4_0[3], ID2N, ID1N, CSIDBS_4_0[0], LCSN);
  F091 A277 (.N01(ZZ1));  // open: N02
  F924 A259 (
    .D0_H01(CSEPANSN), .D1_H02(A265_out), .D2_H03(A258_out), .D3_H04(A262_out), .C_H05(CLK1),
    .N01_Q0(EPANSN), .N02_Q1(RINRN), .N03_Q2(EPANN), .N04_Q3(TRAALDN));  // open: N05_Q0B, N06_Q1B, N07_Q2B, N08_Q3B
  nand A255 (A255_out, CSIDBS_4_0[4], CSIDBS_4_0[3], CSIDBS_4_0[2], CSIDBS_4_0[1], ID0N, LCSN);
  nand A251 (A251_out, ID4N, CSIDBS_4_0[3], ID2N, CSIDBS_4_0[1], ID0N, LCSN);
  nand A257 (A257_out, CSIDBS_4_0[4], ID3N, ID2N, ID1N, CSIDBS_4_0[0], LCSN);
  nand A252 (A252_out, ID4N, CSIDBS_4_0[3], ID2N, CSIDBS_4_0[1], CSIDBS_4_0[0], LCSN);
  nand A274 (A274_out, CSIDBS_4_0[4], CSIDBS_4_0[3], CSIDBS_4_0[2], CSIDBS_4_0[1], CSIDBS_4_0[0], LCSN);
  nand A253 (A253_out, ID4N, CSIDBS_4_0[3], CSIDBS_4_0[2], CSIDBS_4_0[1], ID0N, LCSN);
  nand A254 (A254_out, CSIDBS_4_0[4], ID3N, CSIDBS_4_0[2], ID1N, ID0N, LCSN);
  F924 A248 (
    .D0_H01(A254_out), .D1_H02(A253_out), .D2_H03(A252_out), .D3_H04(A251_out), .C_H05(CLK0), .N01_Q0(ECSRN),
    .N02_Q1(EIORN), .N03_Q2(EPESN), .N04_Q3(EPEAN));  // open: N05_Q0B, N06_Q1B, N07_Q2B, N08_Q3B
  F924 A275 (
    .D0_H01(1'b1), .D1_H02(A249_out), .D2_H03(A274_out), .D3_H04(A257_out), .C_H05(CLK0), .N03_Q2(RUARTN),
    .N06_Q1B(EDON), .N08_Q3B(MAPANS));  // open: N01_Q0, N02_Q1, N04_Q3, N05_Q0B, N07_Q2B

  // Other names for the same wires on the sheet: ID0 = CSIDBS_4_0[0]; ID1 = CSIDBS_4_0[1]; ID2 = CSIDBS_4_0[2];
  //   ID3 = CSIDBS_4_0[3]; ID4 = CSIDBS_4_0[4]

  // Notes on the sheet:
  //   Page 14 DECODE - DECODE_DGA_IDBS Sheet 1 of 2
  //   Page 15 DECODE - DECODE_DGA_IDBS Sheet 2 of 2
  //   VAL
  //   STAT4
  //   MAPANS
  //   LCSN
  //   STAT4
  //   LCSN
  //   RIWR
  //   DSTAT3
  //   STAT3
  //   LCSN
  //   STAT3
  //   LCSN
  //   PRQ
  //   STAT3
  //   DSTAT3
  //   CSEPANSN
  //   LCSN
  //   CSEPANSN
  //   PRQ
  //   LCSN
  //   RIWRN
  //   STAT4
  //   LCSN
  //   0=ALU,1=BMG,2=GPR
  //   26 -  ALD
  //   2=GPR,4=ARG,6=STS
  //   27 -  PANEL
  //   14=AARG, 10=BARG,11=SWAP,10=BARG
  //   RIWRN
  //   DSTAT3N
  //   PRQN
  //   VAL
  //   RIWR
  //   DSTAT3
  //   PRQ
  //   2 - GPR, 3- DBR
  //   35 - RINR
  //   25 - PCR
  //   20 - MIPANS, 21 - MAPANS
  //   11 - SWAP
  //   36 - PICMSK
  //   12-PEA
  //   21 - MAPANS
  //   13-PES
  //   37 - UART
  //   16-IOR
  //   24 - CSR
endmodule

module DECODE_DGA_COMM (
  input  [4:0] CSCOMM_4_0,
  input  LCSN,
  input  [1:0] CSMIS_1_0,
  input  CLK2,
  input  CLK3,
  input  EORFN,
  input  IDBI5,
  input  IDBI7,
  input  CLEAR,
  input  PONI,
  input  IDBI2,
  input  CLK1,
  input  HITN,
  input  BRKN,
  input  LSHADOW,
  input  DAPN,
  input  UCLK,
  output FETCH,
  output FMISS,
  output DTN,
  output WRITE,
  output RTN,
  output FORMN,
  output MREQ,
  output CCLRN,
  output SSTOPN,
  output CLRTIN,
  output CEUARTN,
  output SSEMAN,
  output EMPIDN,
  output SLOWN,
  output LDPANCN,
  output STARTN,
  output WCHIMN,
  output EMCLN,
  output RESET,
  output SIOCN,
  output DVACCN,
  output SHORTN,
  output IORQN,
  output RWCSN,
  output LHIT,
  output ESTOFN,
  output ECREQ,
  output STOCN,
  output CA10
);

  wire A141_out, A142_out, A143_out, A144_out, A145_out, A147_out, A148_out, A149_out, A150_out, A152_out,
       A155_out, A156_out, A158_out, A162_out, A166_out, A167_out, A171_out, A172_out, A177_out, A180_out,
       A182_out, A183_out, A184_out, A185_out, A186_out, A187_n07_q2b, A188_n07_q2b, A189_out, A190_out,
       A191_out, A192_out, A193_out, A194_n01, A196_out, A197_out, A198_out, A199_out, A200_out, A201_y,
       A204_q, A206_out, A208_y, A211_out, A212_out, A213_out, A214_n01_q0, A215_out, A216_out, A217_out,
       A218_out, A219_out, A220_out, A221_y, A222_out, A223_out, A224_out, A225_n01, A226_q, A226_qn,
       A228_out, A229_out, A230_out, A232_q, A233_out, A235_out, A236_y, A237_out, A238_out, A240_out,
       A241_out, A242_out, A243_out, A245_out, C0N, C1N, C2N, C3N, C4N, EORF, ICA10, IORQ, M0N, M1N,
       not_9_out, not_10_out, RT, SSEMA, ZZ1;

  not not_1 (C0N, CSCOMM_4_0[0]);
  not not_2 (C1N, CSCOMM_4_0[1]);
  not not_3 (C2N, CSCOMM_4_0[2]);
  not not_4 (C3N, CSCOMM_4_0[3]);
  not not_5 (C4N, CSCOMM_4_0[4]);
  not not_6 (M0N, CSMIS_1_0[0]);
  not not_7 (M1N, CSMIS_1_0[1]);
  nand A192 (A192_out, SSEMA, MREQ, LCSN);
  F091 A225 (.N01(A225_n01));  // open: N02
  nand A206 (A206_out, A192_out, A193_out);
  nand A193 (A193_out, M1N, CSMIS_1_0[0], CSCOMM_4_0[4], C3N, C2N, C1N, CSCOMM_4_0[0], LCSN);
  nand A212 (A212_out, A225_n01, CSMIS_1_0[1], CSCOMM_4_0[4], CSCOMM_4_0[3], CSCOMM_4_0[2], CSCOMM_4_0[1], CSCOMM_4_0[0], LCSN);
  nand A156 (A156_out, CSCOMM_4_0[4], C3N, CSCOMM_4_0[2], LCSN);
  nand A149 (A149_out, A156_out, A142_out, A145_out, A152_out, A150_out, A155_out);
  nand A150 (A150_out, CSCOMM_4_0[4], C3N, CSCOMM_4_0[1], CSCOMM_4_0[0], LCSN);
  nand A199 (A199_out, C4N, C3N, CSCOMM_4_0[2], C1N, CSCOMM_4_0[0], LCSN);
  nand A211 (A211_out, M1N, CSMIS_1_0[0], CSCOMM_4_0[4], CSCOMM_4_0[3], CSCOMM_4_0[2], CSCOMM_4_0[1], C0N, LCSN);
  F924 A181 (
    .D0_H01(1'b1), .D1_H02(A191_out), .D2_H03(A199_out), .D3_H04(A206_out), .C_H05(CLK3), .N02_Q1(SSTOPN),
    .N03_Q2(CEUARTN), .N04_Q3(SSEMA), .N08_Q3B(SSEMAN));  // open: N01_Q0, N05_Q0B, N06_Q1B, N07_Q2B
  nand A155 (A155_out, CSCOMM_4_0[4], CSCOMM_4_0[3], C2N, C1N, LCSN);
  nand A191 (A191_out, C4N, CSCOMM_4_0[3], CSCOMM_4_0[2], C1N, C0N, LCSN);
  not A241 (A241_out, LSHADOW);
  nand A152 (A152_out, CSCOMM_4_0[4], CSCOMM_4_0[3], C1N, C0N, LCSN);
  nand A222 (A222_out, CSMIS_1_0[0], C4N, CSCOMM_4_0[2], CSCOMM_4_0[1], LCSN);
  nand A158 (A158_out, A147_out, A141_out, A145_out);
  F924 A214 (
    .D0_H01(A213_out), .D1_H02(A216_out), .D2_H03(A211_out), .D3_H04(A212_out), .C_H05(CLK2),
    .N01_Q0(A214_n01_q0), .N03_Q2(RWCSN), .N04_Q3(IORQN), .N06_Q1B(SHORTN), .N08_Q3B(IORQ));  // open: N02_Q1, N05_Q0B, N07_Q2B
  F924 A140 (
    .D0_H01(A162_out), .D1_H02(1'b1), .D2_H03(A158_out), .D3_H04(A149_out), .C_H05(CLK2), .N01_Q0(FETCH),
    .N04_Q3(RT), .N07_Q2B(DTN), .N08_Q3B(RTN));  // open: N02_Q1, N03_Q2, N05_Q0B, N06_Q1B
  nand A185 (A185_out, CSCOMM_4_0[4], CSCOMM_4_0[3], CSCOMM_4_0[2], CSCOMM_4_0[1], C0N, CSMIS_1_0[0]);
  and A242 (A242_out, BRKN, A241_out, EORF);
  nand A147 (A147_out, CSCOMM_4_0[4], CSCOMM_4_0[3], C2N, CSCOMM_4_0[1], LCSN);
  nand A223 (A223_out, CSMIS_1_0[0], C3N, C2N, C1N, LCSN);
  not A240 (A240_out, DAPN);
  nand A237 (A237_out, WRITE, UCLK);
  nand A198 (A198_out, C4N, C3N, CSCOMM_4_0[2], C1N, CSCOMM_4_0[0]);
  nand A200 (A200_out, A185_out, A198_out, LCSN);
  not not_8 (EORF, EORFN);
  D_Flip_Flop d_ff_1 (.D(ICA10), .clk(CLK1), .Q(CA10), .preset(1'b0), .reset(not_9_out));  // open: Qn
  not not_9 (not_9_out, A237_out);
  nand A141 (A141_out, CSCOMM_4_0[4], CSCOMM_4_0[3], C1N, LCSN);
  F091 A178 (.N01(ZZ1));  // open: N02
  nand A228 (A228_out, CSMIS_1_0[1], C3N, C2N, C1N, LCSN);
  and A246 (ESTOFN, LSHADOW, RT);
  nand A233 (A233_out, RT, HITN, A242_out);
  nand A238 (A238_out, WRITE, A242_out);
  nand A235 (A235_out, EORF, IORQ);
  nand A245 (A245_out, RT, A241_out);
  nand A243 (A243_out, IORQ, A240_out);
  F571 A221 (.D0(IDBI2), .D1(A226_q), .A(A214_n01_q0), .ENB_N(1'b0), .Y(A221_y));
  F571 A236 (.D0(A232_q), .D1(HITN), .A(RT), .ENB_N(1'b0), .Y(A236_y));
  nand A162 (A162_out, A156_out, A150_out, A142_out);
  nand A209 (EMPIDN, EORF, A187_n07_q2b);
  nand A183 (A183_out, C4N, CSCOMM_4_0[3], C2N, CSCOMM_4_0[1], C0N, LCSN);
  F924 A187 (
    .D0_H01(A184_out), .D1_H02(A182_out), .D2_H03(A183_out), .D3_H04(A200_out), .C_H05(CLK3),
    .N01_Q0(CLRTIN), .N02_Q1(SIOCN), .N04_Q3(SLOWN), .N07_Q2B(A187_n07_q2b));  // open: N03_Q2, N05_Q0B, N06_Q1B, N08_Q3B
  nand A239 (ECREQ, A233_out, A238_out, A235_out);
  nand A244 (STOCN, A245_out, A243_out);
  nand A145 (A145_out, ZZ1, M1N, CSCOMM_4_0[4], C3N, C2N, CSCOMM_4_0[1], C0N, LCSN);
  nand A229 (A229_out, C4N, CSCOMM_4_0[2], C1N, C0N, LCSN);
  nand A216 (A216_out, A225_n01, A222_out, A223_out, A228_out, A229_out, A217_out, A218_out, A219_out);
  D_Flip_Flop A226 (.D(A221_y), .clk(CLK2), .Q(A226_q), .Qn(A226_qn));  // open: preset, reset
  D_Flip_Flop A232 (.D(A236_y), .clk(CLK1), .Q(A232_q), .Qn(LHIT));  // open: preset, reset
  nand A167 (A167_out, A147_out, A144_out);
  nand A182 (A182_out, C4N, C3N, CSCOMM_4_0[2], CSCOMM_4_0[1], CSCOMM_4_0[0], LCSN);
  F924 A160 (
    .D0_H01(A171_out), .D1_H02(A166_out), .D2_H03(A148_out), .D3_H04(A167_out), .C_H05(CLK2), .N01_Q0(FMISS),
    .N04_Q3(WRITE), .N06_Q1B(FORMN), .N07_Q2B(MREQ));  // open: N02_Q1, N03_Q2, N05_Q0B, N08_Q3B
  F571 A208 (.D0(IDBI5), .D1(EMCLN), .A(SIOCN), .ENB_N(1'b0), .Y(A208_y));
  nand A217 (A217_out, C3N, C2N, C1N, C0N, LCSN);
  nand A142 (A142_out, CSMIS_1_0[0], CSMIS_1_0[1], CSCOMM_4_0[4], C3N, C2N, CSCOMM_4_0[1], C0N, LCSN);
  nand A184 (A184_out, C4N, CSCOMM_4_0[3], CSCOMM_4_0[2], C1N, CSCOMM_4_0[0], LCSN);
  D_Flip_Flop d_ff_2 (.D(A208_y), .clk(CLK3), .Q(EMCLN), .reset(CLEAR));  // open: Qn, preset
  nand A148 (A148_out, A145_out, A142_out, A156_out, A150_out, A141_out, A147_out);
  nand A218 (A218_out, C4N, C3N, C2N, LCSN);
  nand A143 (A143_out, ZZ1, CSMIS_1_0[1], CSCOMM_4_0[4], C3N, C2N, CSCOMM_4_0[1], C0N, LCSN);
  nand A180 (A180_out, M0N, M1N, CSCOMM_4_0[4], C3N, C2N, C1N, CSCOMM_4_0[0], LCSN);
  nand A219 (A219_out, C4N, CSCOMM_4_0[3], CSCOMM_4_0[2], LCSN);
  nand A166 (A166_out, A143_out, A156_out, A150_out);
  nand A144 (A144_out, CSCOMM_4_0[4], CSCOMM_4_0[3], CSCOMM_4_0[2], C1N, CSCOMM_4_0[0], LCSN);
  nand A195 (LDPANCN, EORF, A188_n07_q2b);
  nand A186 (A186_out, M0N, CSMIS_1_0[1], C4N, C3N, CSCOMM_4_0[2], CSCOMM_4_0[1], C0N, LCSN);
  F924 A188 (
    .D0_H01(1'b1), .D1_H02(A190_out), .D2_H03(A186_out), .D3_H04(A180_out), .C_H05(CLK3), .N02_Q1(STARTN),
    .N04_Q3(WCHIMN), .N07_Q2B(A188_n07_q2b));  // open: N01_Q0, N03_Q2, N05_Q0B, N06_Q1B, N08_Q3B
  nand A213 (A213_out, CSMIS_1_0[1], CSMIS_1_0[0], CSCOMM_4_0[4], C3N, C2N, C1N, CSCOMM_4_0[0], LCSN);
  nand A153 (ICA10, A142_out, A150_out, A144_out, A156_out, A147_out);
  nand A190 (A190_out, C4N, CSCOMM_4_0[3], C2N, CSCOMM_4_0[1], CSCOMM_4_0[0], LCSN);
  nand A177 (A177_out, LCSN, MREQ, FMISS);
  nand A215 (A215_out, A226_qn, CSMIS_1_0[1], CSMIS_1_0[0], CSCOMM_4_0[4], CSCOMM_4_0[3], CSCOMM_4_0[2], C1N, LCSN);
  nand A220 (A220_out, A212_out, A215_out, A224_out);
  nand A171 (A171_out, A177_out, A172_out);
  nand A172 (A172_out, LCSN, SSEMA);
  F571 A201 (.D0(IDBI7), .D1(RESET), .A(SIOCN), .ENB_N(1'b0), .Y(A201_y));
  not A230 (A230_out, PONI);
  D_Flip_Flop A227 (.D(A220_out), .clk(CLK2), .Qn(DVACCN));  // open: Q, preset, reset
  nand A224 (A224_out, A230_out, LCSN);
  nand A189 (A189_out, M0N, CSMIS_1_0[1], CSCOMM_4_0[4], C3N, C2N, C1N, CSCOMM_4_0[0], LCSN);
  not not_10 (not_10_out, CLK3);
  D_Flip_Flop d_ff_3 (.D(A201_y), .clk(CLK3), .Q(RESET), .reset(CLEAR));  // open: Qn, preset
  D_Flip_Flop A204 (.D(A189_out), .clk(not_10_out), .Q(A204_q));  // open: Qn, preset, reset
  not A197 (A197_out, CLK3);
  nor A196 (A196_out, A204_q, A197_out);
  F091 A194 (.N01(A194_n01));  // open: N02
  F595 A207 (.H01_S(A196_out), .H02_R(A197_out), .H03_G(A194_n01), .N02_QB(CCLRN));  // open: N01_Q

  // Other names for the same wires on the sheet: C0 = CSCOMM_4_0[0]; C1 = CSCOMM_4_0[1]; C2 = CSCOMM_4_0[2];
  //   C3 = CSCOMM_4_0[3]; C4 = CSCOMM_4_0[4]; M0 = CSMIS_1_0[0]; M1 = CSMIS_1_0[1]

  // Notes on the sheet:
  //   Page 16 DECODE - DECODE_DGA_COMM - Sheet 1 of 4
  //   Page 17 DECODE - DECODE_DGA_COMM - Sheet 2 of 4
  //   Page 18 DECODE - DECODE_DGA_COMM - Sheet 3 of 4
  //   SSEMA
  //   Page 19 DECODE - DECODE_DGA_COMM - Sheet 4 of 4
  //   IDENT 37,1   - IOXT 37,3
  //   Command 24, CNEXT
  //   Command 27, JMP & CONTINUE
  //   RWCS 36,1
  //   Command 23 (+27), CJUMP
  //   IRT
  //   Command 30, AREAD Command
  //   Command 34, READ+EXAMINE
  //   DT
  //   FETCH
  //   Command 32 & 33  - AWRITE
  //   HITN
  //   LHITN
  //   Command 30 & 31, AREAD
  //   Command 34 - READ & EXAMINE
  //   Command 35 - WRITE & DEPOSIT
  //   ISLOWN
  //   IEMPIDN
  //   VEX
  //   LHITN
  //   Command 22,0 (IREAD,PT) and 1 (IREAD,APT) ZZ1 is always 1 
  //   VEXN
  //   ISIOCN
  //   Enable CPU Reqest
  //   ICRLTIN
  //   Command 22,3 - CNEXT,NWP
  //   Command 22,2 (MAP) and 3 (CNEXT.NWP) ZZ1 is always 1 
  //   IWCHIMN
  //   21,3 - LDEXM
  //   Command 35 - WRITE & DEPOSIT
  //   ILDPANC
  //   ISTARTN
  //   35,2 WRITE, HOLD
  //   34,2 READ, HOLD
endmodule

module F091 (
  output N01,
  output N02
);


  assign N01 = 1'b1;
  assign N02 = 1'b0;

  // Notes on the sheet:
  //   F091 - G,L LEVEL GENERATOR
  //   REN_A12213XJ5V1UM00_OTH_19980801.PDF
  //   High
  //   LOW
  //   Used in P17
endmodule

module F103 (
  input  F_IN,
  output F_OUT
);

  not not_1 (F_OUT, F_IN);

  // Notes on the sheet:
  //   F103 INVERTER
  //   REN_A12213XJ5V1UM00_OTH_19980801.PDF
  //   F103 used in Page 10 (DECODE_DGA_POW)
endmodule

module F571 (
  input  D0,
  input  D1,
  input  A,
  input  ENB_N,
  output Y
);

  wire not_1_out;

  not not_1 (not_1_out, ENB_N);
  Multiplexer #(.enable("true")) multiplexer_1 (.in0(D0), .in1(D1), .out(Y), .sel(A), .en(not_1_out));

  // Notes on the sheet:
  //   REN_A12213XJ5V1UM00_OTH_19980801.PDF
  //   F571 - 2 to 1 MULTIPLEXER POSITIVE OUTPUT WITH ENABLE
  //   Used in Page 17 and 10
endmodule

module F595 (
  input  H01_S,
  input  H02_R,
  input  H03_G,
  output N01_Q,
  output N02_QB
);

  wire and_1_out, and_2_out, nor_1_out, nor_2_out;

  and and_1 (and_1_out, H01_S, H03_G);
  and and_2 (and_2_out, H03_G, H02_R);
  nor nor_1 (nor_1_out, and_1_out, nor_2_out);
  nor nor_2 (nor_2_out, nor_1_out, and_2_out);
  not not_1 (N01_Q, nor_1_out);
  not not_2 (N02_QB, nor_2_out);

  // Notes on the sheet:
  //   F595 RS-LATCH
  //   S / H01
  //   R / H02
  //   G / H03
  //   REN_A12213XJ5V1UM00_OTH_19980801.PDF
  //   Used in Page 17
  //   Q / N01
  //   QB / N02
endmodule

module F617 (
  input  H04_SB,
  input  H01_D,
  input  H02_C,
  input  H03_RB,
  output N01_Q,
  output N02_QB
);

  wire not_1_out, not_2_out;

  not not_1 (not_1_out, H04_SB);
  D_Flip_Flop d_ff_1 (.D(H01_D), .clk(H02_C), .Q(N01_Q), .Qn(N02_QB), .preset(not_1_out), .reset(not_2_out));
  not not_2 (not_2_out, H03_RB);

  // Notes on the sheet:
  //   F617 - D Flip-Flop with RB an SB
  //   REN_A12213XJ5V1UM00_OTH_19980801.PDF
  //   (Probably better than to get an unstable flip-flop oscilating ?)
  //   According to truth table page 260 in the REN_A12213XJ5V1UM00_OTH_19980801.PDF :
  //   SB=0 and RB=0 should give both Q and QN to be 0. Logisim doesnt do that, it gives Q=0 and QN=1
  //   Used in Page 10
  //   Marked in the PDF with "Prohibition"
endmodule

module F924 (
  input  D0_H01,
  input  D1_H02,
  input  D2_H03,
  input  D3_H04,
  input  C_H05,
  output N01_Q0,
  output N02_Q1,
  output N03_Q2,
  output N04_Q3,
  output N05_Q0B,
  output N06_Q1B,
  output N07_Q2B,
  output N08_Q3B
);

  D_Flip_Flop d_ff_1 (.D(D0_H01), .clk(C_H05), .Q(N01_Q0), .Qn(N05_Q0B));  // open: preset, reset
  D_Flip_Flop d_ff_2 (.D(D1_H02), .clk(C_H05), .Q(N02_Q1), .Qn(N06_Q1B));  // open: preset, reset
  D_Flip_Flop d_ff_3 (.D(D2_H03), .clk(C_H05), .Q(N03_Q2), .Qn(N07_Q2B));  // open: preset, reset
  D_Flip_Flop d_ff_4 (.D(D3_H04), .clk(C_H05), .Q(N04_Q3), .Qn(N08_Q3B));  // open: preset, reset

  // Notes on the sheet:
  //   F924 4-BIT D Flip-Flop
  //   REN_A12213XJ5V1UM00_OTH_19980801.PDF
endmodule

module F714 (
  input  H03_S,
  input  H01_T,
  input  H02_R,
  output N01_Q,
  output N02_QB
);

  wire not_1_out;

  T_Flip_Flop t_ff_1 (.T(not_1_out), .clk(H01_T), .Q(N01_Q), .Qn(N02_QB), .reset(H02_R), .preset(H03_S));
  not not_1 (not_1_out, H01_T);

  // Notes on the sheet:
  //   F714 - T Flip-Flop with R an S
  //   REN_A12213XJ5V1UM00_OTH_19980801.PDF
  //   (Probably better than to get an unstable flip-flop oscilating ?)
  //   According to truth table page 273 in the REN_A12213XJ5V1UM00_OTH_19980801.PDF :
  //   S=1 and R=1 should give both Q and QN to be 1. Logisim doesnt do that, it gives Q=0 and QN=1
  //   Used in Page 10
  //   Marked in the PDF with "Prohibition"
endmodule

module F774 (
  input  S_H05,
  input  J_H01,
  input  K_H02,
  input  C_H03,
  input  R_H04,
  output N01_Q,
  output N02_QB
);

  J_K_Flip_Flop j_k_ff_1 (.J(J_H01), .K(K_H02), .clk(C_H03), .Q(N01_Q), .Qn(N02_QB), .preset(S_H05), .reset(R_H04));

  // Notes on the sheet:
  //   F774  JK-F/F WITH R,S
  //   REN_A12213XJ5V1UM00_OTH_19980801.PDF
  //   According to truth table page 282 in the REN_A12213XJ5V1UM00_OTH_19980801.PDF :
  //   (Probably better than to get an unstable flip-flop oscilating ?)
  //   S=1 and R=1 should give both Q and QN to be 1. Logisim doesnt do that, it gives Q=0 and QN=1
  //   Marked in the PDF with "Prohibition"
endmodule

module test_DGA (
);

  DECODE_DGA decode_dga_1 ();  // open: XCLK, XLCN, XLSH, XUCK, XEON, XBDN, XDAN, XPDI, XID_4_0, XCO_4_0, XST_4_3, XMI_1_0, XHIN, XBRN, XTON, XLON, XEFN, XCON, XPWC, XPOW, XRTO, XS5N, XCLO, XTES, XRMN, XI_3_0_I, XIB_7_4, XFEC, XWRI, XMRN, XRWN, XECR, XPAN, XPEN, XION, XCSN, XTRN, XEPN, XRIN, XDON, XPSN, XVAL, XRUN, XEUN, XDVN, XPIN, XOCN, XFMI, XWHN, XESN, XSWN, XSHN, XSSN, XCRN, XRTN, XDTN, XRQN, XSCN, XLHN, XFON, XC10, XI_3_0_O, XI_3_0_C, XRFN, XTOT, XPSC, XPFN, XTE0, XPNN, XMCL, XCLN, XSTP, XA_7_0, XA_7_0_C, XEMN, XFUN
endmodule
