// Logisim project CGA_DCD_.circ as structural Verilog: 2 circuits, main circuit CGA_DCD
module CGA_DCD (
  input  [4:0] CSCOMM_4_0,
  input  [1:0] CSMIS_1_0,
  input  MCLK,
  input  ILCSN,
  input  F15,
  input  ZF,
  input  CRY,
  input  SGR,
  input  WPN,
  input  PONI,
  input  VEX,
  input  BRKN,
  input  FIDBO5,
  input  MRN,
  input  LSHADOW,
  input  INTRQN,
  input  [4:0] CSIDBS_4_0,
  output INDN,
  output XFETCHN,
  output CBRKN,
  output LDLCN,
  output LDPILN,
  output LDIRV,
  output DSTOPN,
  output CSMREQ,
  output LDDBRN,
  output FETCHN,
  output WRITEN,
  output CLFFN,
  output EPIC,
  output LWCAN,
  output LDGPRN,
  output WRTRF,
  output CFETCH,
  output VACCN,
  output CLIRQN,
  output EPGSN,
  output EPCRN,
  output EPICVN,
  output EPICSN,
  output ERFN
);

  wire and_1_out, C22_z0, C22_z1, C22_z3, C22_z4, C22_z5, C22_z6, C22_z7, C24_z0, C24_z1, C24_z2, C24_z3,
       C24_z4, C24_z5, C24_z6, C24_z7, CFETCH_FF_q, COMM_MIS_REG_qa, COMM_MIS_REG_qan, COMM_MIS_REG_qb,
       COMM_MIS_REG_qbn, COMM_MIS_REG_qc, COMM_MIS_REG_qcn, COMM_MIS_REG_qe, COMM_MIS_REG_qen,
       COMM_MIS_REG_qf, COMM_MIS_REG_qfn, COMM_MIS_REG_qg, COMM_MIS_REG_qgn, d_ff_4_q, d_ff_6_q, d_ff_6_qn,
       d_ff_8_q, d_ff_10_qn, d_ff_11_q, d_ff_16_qn, d_ff_17_q, FD25_q, LCSN, MREQ, nand_1_out, nand_2_out,
       nand_4_out, nand_5_out, nand_6_out, nand_7_out, nand_8_out, nand_9_out, nand_10_out, nand_11_out,
       nand_12_out, nand_13_out, nand_14_out, nand_15_out, nand_16_out, nand_18_out, nand_19_out,
       nand_20_out, nand_22_out, nand_23_out, nand_24_out, nand_25_out, nand_26_out, nand_27_out,
       nand_28_out, nand_29_out, nand_30_out, nand_31_out, nand_32_out, nand_33_out, nand_34_out,
       nand_35_out, nand_36_out, nand_37_out, nand_38_out, nand_39_out, nand_40_out, nand_41_out,
       nand_42_out, nand_43_out, nand_44_out, nand_45_out, nand_46_out, nand_47_out, nand_48_out,
       nand_49_out, nand_50_out, nand_51_out, nand_52_out, nand_53_out, nand_54_out, nand_55_out,
       nand_56_out, nand_57_out, nand_58_out, nand_59_out, nand_60_out, nand_61_out, nand_62_out,
       nand_63_out, nand_64_out, nor_1_out, not_1_out, not_2_out, not_3_out, not_4_out, not_5_out, not_7_out,
       not_8_out, not_9_out, not_10_out, not_11_out, not_44_out, not_54_out, not_57_out, not_58_out,
       not_59_out, or_1_out, or_2_out, or_3_out, or_4_out, or_5_out, or_6_out, or_7_out, or_8_out, or_9_out,
       or_10_out, or_12_out, or_13_out, SIOCN, WRTRFN;
  wire [1:0] ICSMIS_1_0, ICSMIS_1_0_N, MIS_1_0, MIS_1_0_N;
  wire [4:0] COMM_4_0, COMM_4_0_N, ICSCOMM_4_0, ICSCOMM_4_0_N, ICSIDBS_4_0, ICSIDBS_4_0_N;

  not not_1 (not_1_out, F15);
  not not_2 (not_2_out, ZF);
  not not_3 (not_3_out, CRY);
  not not_4 (not_4_out, WPN);
  not not_5 (not_5_out, ILCSN);
  not not_6 (LCSN, not_5_out);
  not not_7 (not_7_out, not_1_out);
  not not_8 (not_8_out, not_2_out);
  not not_9 (not_9_out, not_3_out);
  not not_10 (not_10_out, SGR);
  not not_11 (not_11_out, not_4_out);
  not not_12 (ICSIDBS_4_0_N[0], CSIDBS_4_0[0]);
  not not_13 (ICSIDBS_4_0_N[1], CSIDBS_4_0[1]);
  not not_14 (ICSIDBS_4_0_N[2], CSIDBS_4_0[2]);
  not not_15 (ICSIDBS_4_0_N[3], CSIDBS_4_0[3]);
  not not_16 (ICSIDBS_4_0_N[4], CSIDBS_4_0[4]);
  nand nand_1 (nand_1_out, CSCOMM_4_0[4], LCSN);
  nand nand_2 (nand_2_out, COMM_4_0[4], COMM_4_0_N[3], COMM_4_0[2]);
  nand nand_3 (LDLCN, COMM_4_0_N[4], COMM_4_0[3], COMM_4_0[2], COMM_4_0[1], COMM_4_0[0], LCSN);
  nand nand_4 (nand_4_out, LCSN, ICSIDBS_4_0[4], ICSIDBS_4_0_N[3], ICSIDBS_4_0_N[2], ICSIDBS_4_0[1], ICSIDBS_4_0[0]);
  not not_17 (ICSIDBS_4_0[0], ICSIDBS_4_0_N[0]);
  not not_18 (ICSIDBS_4_0[1], ICSIDBS_4_0_N[1]);
  not not_19 (ICSIDBS_4_0[2], ICSIDBS_4_0_N[2]);
  not not_20 (ICSIDBS_4_0[3], ICSIDBS_4_0_N[3]);
  not not_21 (ICSIDBS_4_0[4], ICSIDBS_4_0_N[4]);
  D_Flip_Flop d_ff_1 (.D(nand_4_out), .clk(MCLK), .Q(EPGSN));  // open: Qn, preset, reset
  nand nand_5 (nand_5_out, COMM_4_0[4], COMM_4_0_N[3], COMM_4_0_N[2], COMM_4_0[1], COMM_4_0_N[0], MIS_1_0[1], MIS_1_0[0], not_11_out);
  nand nand_6 (nand_6_out, COMM_4_0[4], COMM_4_0_N[3], COMM_4_0_N[0], MIS_1_0[1], MIS_1_0[0], LCSN);
  nand nand_7 (nand_7_out, COMM_4_0[4], COMM_4_0_N[3], COMM_4_0_N[2], COMM_4_0[1], COMM_4_0[0], MIS_1_0_N[1], MIS_1_0_N[0], not_7_out);
  or or_1 (or_1_out, ~nand_2_out, ~nand_5_out, ~nand_7_out, ~nand_10_out, ~nand_13_out, ~nand_16_out);  // OR_Gate
  nand nand_8 (nand_8_out, COMM_4_0[4], COMM_4_0_N[3], COMM_4_0[1], MIS_1_0[1], LCSN);
  nor nor_1 (nor_1_out, ~nand_6_out, ~nand_8_out, ~nand_11_out, ~nand_14_out);  // NOR_Gate
  nand nand_9 (nand_9_out, LCSN, ICSIDBS_4_0[4], ICSIDBS_4_0_N[3], ICSIDBS_4_0[2], ICSIDBS_4_0_N[1], ICSIDBS_4_0[0]);
  R81P COMM_MIS_REG (
    .A(CSCOMM_4_0[0]), .B(CSCOMM_4_0[1]), .C(CSCOMM_4_0[2]), .D(CSCOMM_4_0[3]), .E(nand_1_out),
    .F(CSMIS_1_0[0]), .G(CSMIS_1_0[1]), .CP(MCLK), .QA(COMM_MIS_REG_qa), .QAN(COMM_MIS_REG_qan),
    .QB(COMM_MIS_REG_qb), .QBN(COMM_MIS_REG_qbn), .QC(COMM_MIS_REG_qc), .QCN(COMM_MIS_REG_qcn),
    .QD(COMM_4_0[3]), .QE(COMM_MIS_REG_qe), .QEN(COMM_MIS_REG_qen), .QF(COMM_MIS_REG_qf),
    .QFN(COMM_MIS_REG_qfn), .QG(COMM_MIS_REG_qg), .QGN(COMM_MIS_REG_qgn));  // open: H, QDN, QH, QHN
  nand nand_10 (nand_10_out, COMM_4_0[4], COMM_4_0_N[3], COMM_4_0_N[2], COMM_4_0[1], COMM_4_0[0], MIS_1_0_N[1], MIS_1_0[0], not_1_out);
  nand nand_11 (nand_11_out, COMM_4_0[4], COMM_4_0_N[3], COMM_4_0[1], COMM_4_0[0], LCSN);
  nand nand_12 (nand_12_out, ICSCOMM_4_0[4], ICSCOMM_4_0[3], ICSCOMM_4_0_N[2], ICSCOMM_4_0_N[1], LCSN);
  D_Flip_Flop d_ff_2 (.D(nand_9_out), .clk(MCLK), .Q(EPCRN));  // open: Qn, preset, reset
  nand nand_13 (nand_13_out, COMM_4_0[4], COMM_4_0_N[3], COMM_4_0_N[2], COMM_4_0[1], COMM_4_0[0], MIS_1_0[1], not_8_out, MIS_1_0_N[0]);
  not not_22 (XFETCHN, or_1_out);
  nand nand_14 (nand_14_out, COMM_4_0[4], COMM_4_0_N[3], COMM_4_0[2], LCSN);
  nor nor_2 (LDIRV, nor_1_out, MCLK);
  nand nand_15 (nand_15_out, ICSCOMM_4_0[4], ICSCOMM_4_0[3], ICSCOMM_4_0_N[1], ICSCOMM_4_0_N[0], LCSN);
  not not_23 (COMM_4_0_N[0], COMM_MIS_REG_qa);
  not not_24 (COMM_4_0[0], COMM_MIS_REG_qan);
  not not_25 (COMM_4_0_N[1], COMM_MIS_REG_qb);
  not not_26 (COMM_4_0[1], COMM_MIS_REG_qbn);
  not not_27 (COMM_4_0_N[2], COMM_MIS_REG_qc);
  not not_28 (COMM_4_0[2], COMM_MIS_REG_qcn);
  not not_29 (COMM_4_0_N[3], COMM_4_0[3]);
  not not_30 (COMM_4_0[4], COMM_MIS_REG_qe);
  not not_31 (COMM_4_0_N[4], COMM_MIS_REG_qen);
  not not_32 (MIS_1_0_N[0], COMM_MIS_REG_qf);
  not not_33 (MIS_1_0[0], COMM_MIS_REG_qfn);
  not not_34 (MIS_1_0_N[1], COMM_MIS_REG_qg);
  not not_35 (MIS_1_0[1], COMM_MIS_REG_qgn);
  nand nand_16 (nand_16_out, COMM_4_0[4], COMM_4_0_N[3], COMM_4_0_N[2], COMM_4_0[1], COMM_4_0[0], MIS_1_0[1], MIS_1_0[0], not_2_out);
  nand nand_17 (LDPILN, COMM_4_0_N[4], COMM_4_0_N[3], COMM_4_0_N[2], COMM_4_0_N[1], COMM_4_0[0], LCSN);
  nand nand_18 (nand_18_out, ICSCOMM_4_0[4], ICSCOMM_4_0[2], ICSCOMM_4_0[1], ICSCOMM_4_0[0], ICSMIS_1_0[1], LCSN);
  nand nand_19 (nand_19_out, LCSN, ICSIDBS_4_0[4], ICSIDBS_4_0[3], ICSIDBS_4_0_N[2], ICSIDBS_4_0_N[1], ICSIDBS_4_0[0]);
  nand nand_20 (nand_20_out, ICSCOMM_4_0[4], ICSCOMM_4_0_N[3], ICSCOMM_4_0[1], ICSCOMM_4_0[0], LCSN);
  or or_2 (or_2_out, ~nand_12_out, ~nand_15_out, ~nand_18_out, ~nand_20_out, ~nand_22_out, ~nand_24_out, ~nand_25_out);  // OR_Gate
  D_Flip_Flop d_ff_3 (.D(nand_19_out), .clk(MCLK), .Q(EPICVN));  // open: Qn, preset, reset
  nand nand_21 (SIOCN, COMM_4_0_N[4], COMM_4_0_N[3], COMM_4_0[2], COMM_4_0[1], COMM_4_0[0], LCSN);
  nand nand_22 (nand_22_out, ICSCOMM_4_0[4], ICSCOMM_4_0_N[3], ICSCOMM_4_0[2]);
  D_Flip_Flop d_ff_4 (.D(or_2_out), .clk(MCLK), .Q(d_ff_4_q));  // open: Qn, preset, reset
  nand nand_23 (nand_23_out, COMM_4_0[1], COMM_4_0_N[2], COMM_4_0_N[3], COMM_4_0[4]);
  nand nand_24 (nand_24_out, ICSCOMM_4_0[4], ICSCOMM_4_0_N[3], ICSCOMM_4_0[1], ICSMIS_1_0_N[1]);
  not not_36 (LDDBRN, d_ff_4_q);
  nand nand_25 (nand_25_out, ICSCOMM_4_0[4], ICSCOMM_4_0_N[3], ICSCOMM_4_0[1], ICSMIS_1_0[0]);
  nand nand_26 (nand_26_out, LCSN, ICSIDBS_4_0_N[4], ICSIDBS_4_0[3], ICSIDBS_4_0[2], ICSIDBS_4_0_N[1], ICSIDBS_4_0[0]);
  D_Flip_Flop d_ff_5 (.D(nand_26_out), .clk(MCLK), .Q(EPICSN));  // open: Qn, preset, reset
  ND38GHP C22 (
    .A(MIS_1_0[0]), .B(MIS_1_0[1]), .C(COMM_4_0[0]), .GN(nand_23_out), .Z0(C22_z0), .Z1(C22_z1), .Z3(C22_z3),
    .Z4(C22_z4), .Z5(C22_z5), .Z6(C22_z6), .Z7(C22_z7));  // open: Z2
  nor nor_3 (INDN, C22_z0, C22_z1);
  nand nand_27 (nand_27_out, LCSN, ICSCOMM_4_0[4], ICSCOMM_4_0_N[3], ICSCOMM_4_0[1], ICSMIS_1_0[1], ICSMIS_1_0[0]);
  and and_1 (and_1_out, not_4_out, C22_z3);
  nand nand_28 (nand_28_out, LCSN, ICSCOMM_4_0[4], ICSCOMM_4_0_N[3], ICSCOMM_4_0[1], ICSCOMM_4_0[0]);
  or or_3 (or_3_out, ~nand_27_out, ~nand_28_out, ~nand_29_out);  // OR_Gate
  nand nand_29 (nand_29_out, LCSN, ICSCOMM_4_0[4], ICSCOMM_4_0_N[3], ICSCOMM_4_0[2]);
  D_Flip_Flop d_ff_6 (.D(or_3_out), .clk(MCLK), .Q(d_ff_6_q), .Qn(d_ff_6_qn));  // open: preset, reset
  not not_37 (ICSCOMM_4_0_N[4], CSCOMM_4_0[4]);
  not not_38 (ICSCOMM_4_0_N[3], CSCOMM_4_0[3]);
  not not_39 (ICSCOMM_4_0_N[2], CSCOMM_4_0[2]);
  not not_40 (ICSCOMM_4_0_N[1], CSCOMM_4_0[1]);
  not not_41 (ICSCOMM_4_0_N[0], CSCOMM_4_0[0]);
  not not_42 (ICSMIS_1_0_N[1], CSMIS_1_0[1]);
  not not_43 (ICSMIS_1_0_N[0], CSMIS_1_0[0]);
  nand nand_30 (nand_30_out, not_1_out, C22_z4);
  not not_44 (not_44_out, BRKN);
  nand nand_31 (nand_31_out, LCSN, ICSIDBS_4_0_N[4], ICSIDBS_4_0_N[3], ICSIDBS_4_0[2], ICSIDBS_4_0_N[1], ICSIDBS_4_0[0]);
  not not_45 (ICSMIS_1_0[1], ICSMIS_1_0_N[1]);
  not not_46 (ICSMIS_1_0[0], ICSMIS_1_0_N[0]);
  nand nand_32 (nand_32_out, not_7_out, C22_z5);
  not not_47 (FETCHN, d_ff_6_q);
  or or_4 (or_4_out, ~nand_31_out, ~WRTRFN);  // OR_Gate
  not not_48 (ICSCOMM_4_0[4], ICSCOMM_4_0_N[4]);
  not not_49 (ICSCOMM_4_0[3], ICSCOMM_4_0_N[3]);
  not not_50 (ICSCOMM_4_0[2], ICSCOMM_4_0_N[2]);
  not not_51 (ICSCOMM_4_0[1], ICSCOMM_4_0_N[1]);
  not not_52 (ICSCOMM_4_0[0], ICSCOMM_4_0_N[0]);
  nand nand_33 (nand_33_out, not_2_out, C22_z6);
  D_Flip_Flop d_ff_7 (.D(or_4_out), .clk(MCLK), .Qn(ERFN));  // open: Q, preset, reset
  nand nand_34 (nand_34_out, not_8_out, C22_z7);
  or or_5 (or_5_out, ~nand_30_out, ~nand_32_out, ~nand_33_out, ~nand_34_out);  // OR_Gate
  SCAN_FF CFETCH_FF (.D(CFETCH_FF_q), .TE(not_44_out), .TI(d_ff_6_qn), .CLK(MCLK), .Q(CFETCH_FF_q), .QN(CFETCH));
  nand nand_35 (nand_35_out, COMM_4_0_N[1], COMM_4_0[2], COMM_4_0_N[3], COMM_4_0[4]);
  nand nand_36 (nand_36_out, ICSCOMM_4_0[4], ICSCOMM_4_0[3], ICSCOMM_4_0_N[2], ICSCOMM_4_0[1], LCSN);
  nand nand_37 (nand_37_out, ICSCOMM_4_0[4], ICSCOMM_4_0[3], ICSCOMM_4_0[2], ICSCOMM_4_0_N[1], ICSCOMM_4_0[0], LCSN);
  or or_6 (or_6_out, ~nand_36_out, ~nand_37_out);  // OR_Gate
  ND38GHP C24 (
    .A(MIS_1_0[0]), .B(MIS_1_0[1]), .C(COMM_4_0[0]), .GN(nand_35_out), .Z0(C24_z0), .Z1(C24_z1), .Z2(C24_z2),
    .Z3(C24_z3), .Z4(C24_z4), .Z5(C24_z5), .Z6(C24_z6), .Z7(C24_z7));
  D_Flip_Flop d_ff_8 (.D(or_6_out), .clk(MCLK), .Q(d_ff_8_q));  // open: Qn, preset, reset
  nand nand_38 (nand_38_out, not_10_out, C24_z0);
  not not_53 (WRITEN, d_ff_8_q);
  nand nand_39 (nand_39_out, SGR, C24_z1);
  nand nand_40 (nand_40_out, not_3_out, C24_z2);
  nand nand_41 (nand_41_out, LCSN, ICSCOMM_4_0_N[4], ICSCOMM_4_0[3], ICSCOMM_4_0[2], ICSCOMM_4_0[1], ICSCOMM_4_0_N[0]);
  D_Flip_Flop d_ff_9 (.D(nand_41_out), .clk(MCLK), .Q(CLFFN));  // open: Qn, preset, reset
  nand nand_42 (nand_42_out, not_9_out, C24_z3);
  or or_7 (or_7_out, ~nand_38_out, ~nand_39_out, ~nand_40_out, ~nand_42_out);  // OR_Gate
  nand nand_43 (nand_43_out, LCSN, ICSCOMM_4_0_N[4], ICSCOMM_4_0_N[3], ICSCOMM_4_0[2], ICSCOMM_4_0_N[1], ICSCOMM_4_0_N[0]);
  nand nand_44 (nand_44_out, not_1_out, C24_z4);
  D_Flip_Flop d_ff_10 (.D(nand_43_out), .clk(MCLK), .Qn(d_ff_10_qn));  // open: Q, preset, reset
  not not_54 (not_54_out, MRN);
  nand nand_45 (nand_45_out, not_7_out, C24_z5);
  nor nor_4 (CLIRQN, d_ff_10_qn, not_54_out);
  nand nand_46 (nand_46_out, not_2_out, C24_z6);
  nand nand_47 (nand_47_out, not_8_out, C24_z7);
  nand nand_48 (nand_48_out, LCSN, ICSCOMM_4_0_N[4], ICSCOMM_4_0[3], ICSCOMM_4_0_N[2], ICSCOMM_4_0_N[1], ICSCOMM_4_0[0]);
  D_Flip_Flop d_ff_11 (.D(nand_48_out), .clk(MCLK), .Q(d_ff_11_q));  // open: Qn, preset, reset
  or or_8 (or_8_out, ~nand_44_out, ~nand_45_out, ~nand_46_out, ~nand_47_out);  // OR_Gate
  not not_55 (EPIC, d_ff_11_q);
  or or_9 (or_9_out, or_7_out, or_8_out, and_1_out, or_5_out);
  not not_56 (CBRKN, or_9_out);
  nand nand_49 (nand_49_out, LCSN, ICSCOMM_4_0[4], ICSCOMM_4_0[3], ICSCOMM_4_0[2], ICSCOMM_4_0[1], ICSCOMM_4_0_N[0], ICSMIS_1_0_N[1], ICSMIS_1_0_N[0]);
  D_Flip_Flop d_ff_12 (.D(nand_49_out), .clk(MCLK), .Q(LWCAN));  // open: Qn, preset, reset
  nand nand_50 (nand_50_out, LCSN, ICSCOMM_4_0_N[4], ICSCOMM_4_0_N[3], ICSCOMM_4_0_N[2], ICSCOMM_4_0[1], ICSCOMM_4_0_N[0]);
  or or_10 (or_10_out, ~nand_50_out, ~nand_51_out);  // OR_Gate
  nand nand_51 (nand_51_out, LCSN, ICSCOMM_4_0[4], ICSCOMM_4_0_N[3], ICSCOMM_4_0_N[2], ICSCOMM_4_0[1], ICSCOMM_4_0_N[0], ICSMIS_1_0[1], ICSMIS_1_0_N[0]);
  D_Flip_Flop d_ff_13 (.D(or_10_out), .clk(MCLK), .Qn(LDGPRN));  // open: Q, preset, reset
  nand nand_52 (nand_52_out, LCSN, ICSCOMM_4_0_N[4], ICSCOMM_4_0_N[3], ICSCOMM_4_0_N[2], ICSCOMM_4_0[1], ICSCOMM_4_0[0]);
  D_Flip_Flop d_ff_14 (.D(nand_52_out), .clk(MCLK), .Q(WRTRFN), .Qn(WRTRF));  // open: preset, reset
  nand nand_53 (nand_53_out, LCSN, ICSCOMM_4_0[4], ICSCOMM_4_0_N[3], ICSCOMM_4_0_N[2], ICSCOMM_4_0[1], ICSCOMM_4_0_N[0], ICSMIS_1_0_N[1]);
  nand nand_54 (nand_54_out, LCSN, ICSCOMM_4_0[4], ICSCOMM_4_0_N[3], ICSCOMM_4_0_N[2], ICSCOMM_4_0[1], ICSCOMM_4_0_N[0], ICSMIS_1_0[0]);
  nand nand_55 (nand_55_out, LCSN, ICSCOMM_4_0[4], ICSCOMM_4_0_N[3], ICSCOMM_4_0[1], ICSCOMM_4_0[0]);
  or or_11 (CSMREQ, ~nand_53_out, ~nand_54_out, ~nand_55_out, ~nand_56_out, ~nand_57_out, ~nand_58_out);  // OR_Gate
  nand nand_56 (nand_56_out, LCSN, ICSCOMM_4_0[4], ICSCOMM_4_0_N[3], ICSCOMM_4_0[2]);
  D_Flip_Flop d_ff_15 (.D(CSMREQ), .clk(MCLK), .Q(MREQ));  // open: Qn, preset, reset
  nand nand_57 (nand_57_out, LCSN, ICSCOMM_4_0[4], ICSCOMM_4_0[3], ICSCOMM_4_0_N[2]);
  nand nand_58 (nand_58_out, LCSN, ICSCOMM_4_0[4], ICSCOMM_4_0[3], ICSCOMM_4_0_N[1]);
  not not_57 (not_57_out, PONI);
  not not_58 (not_58_out, VEX);
  nand nand_59 (nand_59_out, not_57_out, LCSN);
  nand nand_60 (nand_60_out, ICSCOMM_4_0[4], ICSCOMM_4_0[3], ICSCOMM_4_0[2], ICSCOMM_4_0_N[1], ICSMIS_1_0[1], ICSMIS_1_0[0], not_58_out, LCSN);
  or or_12 (or_12_out, ~nand_59_out, ~nand_60_out, ~nand_61_out);  // OR_Gate
  not not_59 (not_59_out, LSHADOW);
  nand nand_61 (nand_61_out, ICSCOMM_4_0[4], ICSCOMM_4_0[3], ICSCOMM_4_0[2], ICSCOMM_4_0[1], ICSCOMM_4_0[0], ICSMIS_1_0[1], LCSN);
  D_Flip_Flop d_ff_16 (.D(or_12_out), .clk(MCLK), .Qn(d_ff_16_qn));  // open: Q, preset, reset
  SCAN_WITH_RESET_N FD25 (.D(FIDBO5), .TE(SIOCN), .TI(FD25_q), .CLK(MCLK), .R(MRN), .Q(FD25_q));  // open: QN
  nand nand_62 (nand_62_out, d_ff_16_qn, not_59_out, MREQ, FD25_q, not_58_out, FETCHN);
  nand nand_63 (nand_63_out, d_ff_16_qn, not_59_out, MREQ, FD25_q, not_58_out, INTRQN);
  or or_13 (or_13_out, ~nand_62_out, ~nand_63_out);  // OR_Gate
  not not_60 (VACCN, or_13_out);
  nand nand_64 (nand_64_out, ICSCOMM_4_0_N[4], ICSCOMM_4_0[3], ICSCOMM_4_0[2], ICSCOMM_4_0_N[1], ICSCOMM_4_0_N[0], LCSN);
  D_Flip_Flop d_ff_17 (.D(nand_64_out), .clk(MCLK), .Q(d_ff_17_q));  // open: Qn, preset, reset
  D_Flip_Flop d_ff_18 (.D(d_ff_17_q), .clk(MCLK), .Q(DSTOPN));  // open: Qn, preset, reset

  // Notes on the sheet:
  //   Page 65 - CGA_DCD
  //   ICRY
  //   ICRYN
  //   SGR
  //   ISGRN
  //   IWP
  //   IWPN
  //   Page 72 - Sheet 8 of 10
  //   Page 68 - Sheet 4 of 10
  //   23
  //   Page 66 - Sheet 2 of 10
  //   25
  //   Page 69 - Sheet  5 of 10
  //   31
  //   Page 67 - Sheet 3 of 10
  //   COMM 23 and 24 -> CJMP
  //   MIS0
  //   MIS1
  //   MIS0N
  //   MIS1N
  //   15
  //   IWP
  //   IF15N
  //   IF15
  //   COMM, CONTINUE (27,3)
  //   5
  //   IZFN
  //   IZ
  //   Page 70 - Sheet  6 of 10
  //   32
  //   33
  //   35
  //   ISGRN
  //   SGR
  //   ICRYN
  //   ICRY
  //   16
  //   IF15N
  //   04
  //   IF15
  //   IZFN
  //   IZF
  //   11
  //   Page 71 - Sheet 7 of 10
  //   2
  //   3
  //   Page 73 - Sheet 9 of 10
  //   34.3
  //   35.3
  //   LSHADOWN
  //   37.2, 37.3
  //   DVACCN
  //   EMCLN
  //   Page 75 - Sheet 10 of 10
  //   14
endmodule

module test_DCD (
  input  in_1,
  input  in_2,
  input  in_3
);

  wire scan_with_reset_n_1_q;

  CGA_DCD cga_dcd_1 ();  // open: CSCOMM_4_0, CSMIS_1_0, MCLK, ILCSN, F15, ZF, CRY, SGR, WPN, PONI, VEX, BRKN, FIDBO5, MRN, LSHADOW, INTRQN, CSIDBS_4_0, INDN, XFETCHN, CBRKN, LDLCN, LDPILN, LDIRV, DSTOPN, CSMREQ, LDDBRN, FETCHN, WRITEN, CLFFN, EPIC, LWCAN, LDGPRN, WRTRF, CFETCH, VACCN, CLIRQN, EPGSN, EPCRN, EPICVN, EPICSN, ERFN
  SCAN_WITH_RESET_N scan_with_reset_n_1 (
    .D(in_1), .TE(in_2), .TI(scan_with_reset_n_1_q), .CLK(in_2), .R(in_3), .Q(scan_with_reset_n_1_q));  // open: QN
  // Probe on scan_with_reset_n_1_q
endmodule
