// Logisim project CGA_HELPER.circ as structural Verilog: 1 circuit, main circuit BusDriver16
module BusDriver16 (
  input  [15:0] A_15_0,
  input  [15:0] IN_15_0,
  input  EN,
  input  TN,
  output [15:0] ZI_15_0,
  output [15:0] OUT_15_0
);

  BD4TU BD0 (.EN(EN), .TN(TN), .A(A_15_0[0]), .BUF_IN(IN_15_0[0]), .ZI(ZI_15_0[0]), .BUF_OUT(OUT_15_0[0]));
  BD4TU BD1 (.EN(EN), .TN(TN), .A(A_15_0[1]), .BUF_IN(IN_15_0[1]), .ZI(ZI_15_0[1]), .BUF_OUT(OUT_15_0[1]));
  BD4TU BD2 (.EN(EN), .TN(TN), .A(A_15_0[2]), .BUF_IN(IN_15_0[2]), .ZI(ZI_15_0[2]), .BUF_OUT(OUT_15_0[2]));
  BD4TU BD3 (.EN(EN), .TN(TN), .A(A_15_0[3]), .BUF_IN(IN_15_0[3]), .ZI(ZI_15_0[3]), .BUF_OUT(OUT_15_0[3]));
  BD4TU BD4 (.EN(EN), .TN(TN), .A(A_15_0[4]), .BUF_IN(IN_15_0[4]), .ZI(ZI_15_0[4]), .BUF_OUT(OUT_15_0[4]));
  BD4TU BD5 (.EN(EN), .TN(TN), .A(A_15_0[5]), .BUF_IN(IN_15_0[5]), .ZI(ZI_15_0[5]), .BUF_OUT(OUT_15_0[5]));
  BD4TU BD6 (.EN(EN), .TN(TN), .A(A_15_0[6]), .BUF_IN(IN_15_0[6]), .ZI(ZI_15_0[6]), .BUF_OUT(OUT_15_0[6]));
  BD4TU BD7 (.EN(EN), .TN(TN), .A(A_15_0[7]), .BUF_IN(IN_15_0[7]), .ZI(ZI_15_0[7]), .BUF_OUT(OUT_15_0[7]));
  BD4TU BD8 (.EN(EN), .TN(TN), .A(A_15_0[8]), .BUF_IN(IN_15_0[8]), .ZI(ZI_15_0[8]), .BUF_OUT(OUT_15_0[8]));
  BD4TU BD9 (.EN(EN), .TN(TN), .A(A_15_0[9]), .BUF_IN(IN_15_0[9]), .ZI(ZI_15_0[9]), .BUF_OUT(OUT_15_0[9]));
  BD4TU BD10 (.EN(EN), .TN(TN), .A(A_15_0[10]), .BUF_IN(IN_15_0[10]), .ZI(ZI_15_0[10]), .BUF_OUT(OUT_15_0[10]));
  BD4TU BD11 (.EN(EN), .TN(TN), .A(A_15_0[11]), .BUF_IN(IN_15_0[11]), .ZI(ZI_15_0[11]), .BUF_OUT(OUT_15_0[11]));
  BD4TU BD12 (.EN(EN), .TN(TN), .A(A_15_0[12]), .BUF_IN(IN_15_0[12]), .ZI(ZI_15_0[12]), .BUF_OUT(OUT_15_0[12]));
  BD4TU BD13 (.EN(EN), .TN(TN), .A(A_15_0[13]), .BUF_IN(IN_15_0[13]), .ZI(ZI_15_0[13]), .BUF_OUT(OUT_15_0[13]));
  BD4TU BD14 (.EN(EN), .TN(TN), .A(A_15_0[14]), .BUF_IN(IN_15_0[14]), .ZI(ZI_15_0[14]), .BUF_OUT(OUT_15_0[14]));
  BD4TU BD15 (.EN(EN), .TN(TN), .A(A_15_0[15]), .BUF_IN(IN_15_0[15]), .ZI(ZI_15_0[15]), .BUF_OUT(OUT_15_0[15]));

  // Notes on the sheet:
  //   16 bit three-state bus driver
  //   Special made for CGA page 6 (Sheet 5 of 8)
endmodule
