// Logisim project CGA_IDBCTL_.circ as structural Verilog: 4 circuits, main circuit CGA_IDBCTL_PGSREG
module CGA_IDBCTL (
  input  MCLK,
  input  VACCN,
  input  [11:0] LA_21_10,
  input  FETCHN,
  input  PVIOL,
  input  EPGSN,
  input  EPCRN,
  input  EPICSN,
  input  EPICVN,
  input  EPICMASKN,
  input  PD,
  input  HIGSN,
  input  LOGSN,
  input  [15:0] PCR_15_0,
  input  [15:0] XFIDBI_15_0,
  input  [15:0] PICMASK_15_0,
  input  [2:0] PICV_2_0,
  input  [2:0] PICS_2_0,
  output [15:0] FIDBI_15_0
);

  wire nand_1_out;
  wire [1:0] PGSREG_pgs_15_14;
  wire [5:0] not_1_out;
  wire [11:0] PGSREG_pgs_11_0;

  nand nand_1 (nand_1_out, EPICMASKN, EPICVN, EPICSN, EPCRN, EPGSN);
  not not_1 (not_1_out[0], EPGSN);
  not not_2 (not_1_out[1], EPCRN);
  not not_3 (not_1_out[2], EPICSN);
  not not_4 (not_1_out[3], EPICVN);
  not not_5 (not_1_out[4], EPICMASKN);
  not not_6 (not_1_out[5], nand_1_out);
  CGA_IDBCTL_PGSREG PGSREG (
    .MCLK(MCLK), .VACCN(VACCN), .LA_21_10(LA_21_10), .FETCHN(FETCHN), .PVIOL(PVIOL),
    .PGS_15_14(PGSREG_pgs_15_14), .PGS_11_0(PGSREG_pgs_11_0));
  CGA_IDBCTL_SEL6 IDB15 (
    .D(XFIDBI_15_0[15]), .M(PICMASK_15_0[15]), .V(1'b0), .S(1'b0), .PCR(PCR_15_0[15]),
    .PGS(PGSREG_pgs_15_14[1]), .E_PINS(not_1_out), .D0(FIDBI_15_0[15]));
  CGA_IDBCTL_SEL6 IDB14 (
    .D(XFIDBI_15_0[14]), .M(PICMASK_15_0[14]), .V(1'b0), .S(1'b0), .PCR(PCR_15_0[14]),
    .PGS(PGSREG_pgs_15_14[0]), .E_PINS(not_1_out), .D0(FIDBI_15_0[14]));
  CGA_IDBCTL_SEL6 IDB13 (
    .D(XFIDBI_15_0[13]), .M(PICMASK_15_0[13]), .V(1'b0), .S(1'b0), .PCR(PCR_15_0[13]), .PGS(1'b0),
    .E_PINS(not_1_out), .D0(FIDBI_15_0[13]));
  CGA_IDBCTL_SEL6 IDB12 (
    .D(XFIDBI_15_0[12]), .M(PICMASK_15_0[12]), .V(1'b0), .S(1'b0), .PCR(PCR_15_0[12]), .PGS(1'b0),
    .E_PINS(not_1_out), .D0(FIDBI_15_0[12]));
  CGA_IDBCTL_SEL6 IDB11 (
    .D(XFIDBI_15_0[11]), .M(PICMASK_15_0[11]), .V(1'b0), .S(1'b0), .PCR(PCR_15_0[11]),
    .PGS(PGSREG_pgs_11_0[11]), .E_PINS(not_1_out), .D0(FIDBI_15_0[11]));
  CGA_IDBCTL_SEL6 IDB10 (
    .D(XFIDBI_15_0[10]), .M(PICMASK_15_0[10]), .PCR(PCR_15_0[10]), .PGS(PGSREG_pgs_11_0[10]),
    .E_PINS(not_1_out), .D0(FIDBI_15_0[10]));  // open: V, S
  CGA_IDBCTL_SEL6 IDB9 (
    .D(XFIDBI_15_0[9]), .M(PICMASK_15_0[9]), .V(1'b0), .S(1'b0), .PCR(PCR_15_0[9]), .PGS(PGSREG_pgs_11_0[9]),
    .E_PINS(not_1_out), .D0(FIDBI_15_0[9]));
  CGA_IDBCTL_SEL6 IDB8 (
    .D(XFIDBI_15_0[8]), .M(PICMASK_15_0[8]), .V(1'b0), .S(1'b0), .PCR(PCR_15_0[8]), .PGS(PGSREG_pgs_11_0[8]),
    .E_PINS(not_1_out), .D0(FIDBI_15_0[8]));
  CGA_IDBCTL_SEL6 IDB7 (
    .D(XFIDBI_15_0[7]), .M(PICMASK_15_0[7]), .V(1'b0), .S(1'b0), .PCR(PCR_15_0[7]), .PGS(PGSREG_pgs_11_0[7]),
    .E_PINS(not_1_out), .D0(FIDBI_15_0[7]));
  CGA_IDBCTL_SEL6 IDB6 (
    .D(XFIDBI_15_0[6]), .M(PICMASK_15_0[6]), .V(1'b0), .S(1'b0), .PCR(1'b0), .PGS(PGSREG_pgs_11_0[6]),
    .E_PINS(not_1_out), .D0(FIDBI_15_0[6]));
  CGA_IDBCTL_SEL6 IDB5 (
    .D(XFIDBI_15_0[5]), .M(PICMASK_15_0[5]), .V(1'b0), .S(1'b0), .PCR(1'b0), .PGS(PGSREG_pgs_11_0[5]),
    .E_PINS(not_1_out), .D0(FIDBI_15_0[5]));
  CGA_IDBCTL_SEL6 IDB4 (
    .D(XFIDBI_15_0[4]), .M(PICMASK_15_0[4]), .V(1'b0), .S(LOGSN), .PCR(1'b0), .PGS(PGSREG_pgs_11_0[4]),
    .E_PINS(not_1_out), .D0(FIDBI_15_0[4]));
  CGA_IDBCTL_SEL6 IDB3 (
    .D(XFIDBI_15_0[3]), .M(PICMASK_15_0[3]), .V(PD), .S(HIGSN), .PCR(1'b0), .PGS(PGSREG_pgs_11_0[3]),
    .E_PINS(not_1_out), .D0(FIDBI_15_0[3]));
  CGA_IDBCTL_SEL6 IDB2 (
    .D(XFIDBI_15_0[2]), .M(PICMASK_15_0[2]), .V(PICV_2_0[2]), .S(PICS_2_0[2]), .PCR(PCR_15_0[2]),
    .PGS(PGSREG_pgs_11_0[2]), .E_PINS(not_1_out), .D0(FIDBI_15_0[2]));
  CGA_IDBCTL_SEL6 IDB1 (
    .D(XFIDBI_15_0[1]), .M(PICMASK_15_0[1]), .V(PICV_2_0[1]), .S(PICS_2_0[1]), .PCR(PCR_15_0[1]),
    .PGS(PGSREG_pgs_11_0[1]), .E_PINS(not_1_out), .D0(FIDBI_15_0[1]));
  CGA_IDBCTL_SEL6 IDB0 (
    .D(XFIDBI_15_0[0]), .M(PICMASK_15_0[0]), .V(PICV_2_0[0]), .S(PICS_2_0[0]), .PCR(PCR_15_0[0]),
    .PGS(PGSREG_pgs_11_0[0]), .E_PINS(not_1_out), .D0(FIDBI_15_0[0]));

  // Notes on the sheet:
  //   Bit 5 = ED
  //   Page 97 - CGA_IDBCTL
  //   ED,EM,EV,ES,EPCR,EPGS
  //   BIT 0 = EPGS
  //   EPGS
  //   EPCR
  //   ES
  //   EV
  //   EM
  //   ED
  //   XFIDBI15
  //   XFIDBI0
  //   PICMASK15
  //   PICMASK0
  //   PCR15
  //   PCR0
  //   PGS15
  //   PGS14
  //   PGS11
  //   PGS0
  //   PICV2
  //   PICV1
  //   PICV0
  //   PICS2
  //   PICS1
  //   PICS0
endmodule

module CGA_IDBCTL_PGSREG (
  input  MCLK,
  input  VACCN,
  input  [11:0] LA_21_10,
  input  FETCHN,
  input  PVIOL,
  output [1:0] PGS_15_14,
  output [11:0] PGS_11_0
);

  wire not_1_out, PGS15_q;

  not not_1 (not_1_out, VACCN);
  SCAN_FF PGS15 (.D(PGS15_q), .TE(not_1_out), .TI(FETCHN), .CLK(MCLK), .Q(PGS15_q), .QN(PGS_15_14[1]));
  SCAN_FF PGS14 (.D(PGS_15_14[0]), .TE(not_1_out), .TI(PVIOL), .CLK(MCLK), .Q(PGS_15_14[0]));  // open: QN
  SCAN_FF PGS11 (.D(PGS_11_0[11]), .TE(not_1_out), .TI(LA_21_10[11]), .CLK(MCLK), .Q(PGS_11_0[11]));  // open: QN
  SCAN_FF PGS10 (.D(PGS_11_0[10]), .TE(not_1_out), .TI(LA_21_10[10]), .CLK(MCLK), .Q(PGS_11_0[10]));  // open: QN
  SCAN_FF PGS9 (.D(PGS_11_0[9]), .TE(not_1_out), .TI(LA_21_10[9]), .CLK(MCLK), .Q(PGS_11_0[9]));  // open: QN
  SCAN_FF PGS8 (.D(PGS_11_0[8]), .TE(not_1_out), .TI(LA_21_10[8]), .CLK(MCLK), .Q(PGS_11_0[8]));  // open: QN
  SCAN_FF PGS7 (.D(PGS_11_0[7]), .TE(not_1_out), .TI(LA_21_10[7]), .CLK(MCLK), .Q(PGS_11_0[7]));  // open: QN
  SCAN_FF PGS6 (.D(PGS_11_0[6]), .TE(not_1_out), .TI(LA_21_10[6]), .CLK(MCLK), .Q(PGS_11_0[6]));  // open: QN
  SCAN_FF PGS5 (.D(PGS_11_0[5]), .TE(not_1_out), .TI(LA_21_10[5]), .CLK(MCLK), .Q(PGS_11_0[5]));  // open: QN
  SCAN_FF PGS4 (.D(PGS_11_0[4]), .TE(not_1_out), .TI(LA_21_10[4]), .CLK(MCLK), .Q(PGS_11_0[4]));  // open: QN
  SCAN_FF PGS3 (.D(PGS_11_0[3]), .TE(not_1_out), .TI(LA_21_10[3]), .CLK(MCLK), .Q(PGS_11_0[3]));  // open: QN
  SCAN_FF PGS2 (.D(PGS_11_0[2]), .TE(not_1_out), .TI(LA_21_10[2]), .CLK(MCLK), .Q(PGS_11_0[2]));  // open: QN
  SCAN_FF PGS1 (.D(PGS_11_0[1]), .TE(not_1_out), .TI(LA_21_10[1]), .CLK(MCLK), .Q(PGS_11_0[1]));  // open: QN
  SCAN_FF PGS0 (.D(PGS_11_0[0]), .TE(not_1_out), .TI(LA_21_10[0]), .CLK(MCLK), .Q(PGS_11_0[0]));  // open: QN

  // Notes on the sheet:
  //   Page 98 - CGA_IDBCTL_PGSREG - Completed, not tested
endmodule

module CGA_IDBCTL_SEL6 (
  input  D,
  input  M,
  input  V,
  input  S,
  input  PCR,
  input  PGS,
  input  [5:0] E_PINS,
  output D0
);

  wire nand_1_out, nand_2_out, nand_3_out, nand_4_out, nand_5_out, nand_6_out;

  nand nand_1 (nand_1_out, D, E_PINS[5]);
  nand nand_2 (nand_2_out, M, E_PINS[4]);
  nand nand_3 (nand_3_out, V, E_PINS[3]);
  nand nand_4 (nand_4_out, S, E_PINS[2]);
  nand nand_5 (nand_5_out, PCR, E_PINS[1]);
  nand nand_6 (nand_6_out, PGS, E_PINS[0]);
  or or_1 (D0, ~nand_1_out, ~nand_2_out, ~nand_3_out, ~nand_4_out, ~nand_5_out, ~nand_6_out);  // OR_Gate

  // Notes on the sheet:
  //   Bit 5 = ED
  //   ED,EM,EV,ES,EPCR,EPGS
  //   Page 99 - CGA_IDBCTL_SEL6   - Tested manually
  //   BIT 0 = EPGS
endmodule

module test_IDBCTL (
);

  CGA_IDBCTL cga_idbctl_1 ();  // open: MCLK, VACCN, LA_21_10, FETCHN, PVIOL, EPGSN, EPCRN, EPICSN, EPICVN, EPICMASKN, PD, HIGSN, LOGSN, PCR_15_0, XFIDBI_15_0, PICMASK_15_0, PICV_2_0, PICS_2_0, FIDBI_15_0
endmodule
