// Logisim project CGA_INTR_.circ as structural Verilog: 28 circuits, main circuit CGA_INTR_CNTLR_IRQ_REG_RQBIT
module CGA_INTR (
  input  PANN,
  input  MCLK,
  input  CLIRQN,
  input  EMPIDN,
  input  BINT15N,
  input  POWFAILN,
  input  NORN,
  input  PARERRN,
  input  IOXERRN,
  input  Z,
  input  BINT13N,
  input  BINT12N,
  input  BINT11N,
  input  BINT10N,
  input  [15:0] FIDBO_15_0,
  input  [3:0] LAA_3_0,
  input  EPIC,
  output INTRQN,
  output [15:0] PICMASK_15_0,
  output HIGSN,
  output PD,
  output [2:0] PICV_2_0,
  output IRQ,
  output LOGSN,
  output [2:0] PICS_2_0,
  output EPICMASKN
);

  wire CNTLR_irqn, not_2_out, or_1_out;
  wire [15:0] IRSRC_ireq_15_0_n;

  CGA_INTR_IRSRC IRSRC (
    .EMPIDN(EMPIDN), .BINT15N(BINT15N), .POWFAILN(POWFAILN), .NORN(NORN), .PARERRN(PARERRN),
    .IOXERRN(IOXERRN), .Z(Z), .BINT13N(BINT13N), .BINT12N(BINT12N), .BINT11N(BINT11N), .BINT10N(BINT10N),
    .FIDBO_15_0(FIDBO_15_0), .IREQ_15_0_N(IRSRC_ireq_15_0_n));
  CGA_INTR_CNTLR CNTLR (
    .IREQ_15_0_N(IRSRC_ireq_15_0_n), .MCLK(MCLK), .FIDBO_15_0(FIDBO_15_0), .LAA_3_0(LAA_3_0), .EPIC(EPIC),
    .PICMASK_15_0(PICMASK_15_0), .HIGSN(HIGSN), .PD(PD), .PICV_2_0(PICV_2_0), .IRQN(CNTLR_irqn),
    .LOGSN(LOGSN), .PICS_2_0(PICS_2_0), .EPICMASKN(EPICMASKN));
  not not_1 (IRQ, CNTLR_irqn);
  or or_1 (or_1_out, ~PANN, ~CNTLR_irqn);  // OR_Gate
  not not_2 (not_2_out, CLIRQN);
  D_Flip_Flop d_ff_1 (.D(or_1_out), .clk(MCLK), .Qn(INTRQN), .reset(not_2_out));  // open: Q, preset

  // Notes on the sheet:
  //   Page 74 - CGA_INTR
endmodule

module CGA_INTR_IRSRC (
  input  EMPIDN,
  input  BINT15N,
  input  POWFAILN,
  input  NORN,
  input  PARERRN,
  input  IOXERRN,
  input  Z,
  input  BINT13N,
  input  BINT12N,
  input  BINT11N,
  input  BINT10N,
  input  [15:0] FIDBO_15_0,
  output [15:0] IREQ_15_0_N
);

  wire nand_1_out, nand_3_out, nand_4_out, nand_5_out, nand_6_out, nand_8_out, nand_13_out, nand_14_out,
       nand_15_out, nand_16_out, not_1_out, not_2_out;

  not not_1 (not_1_out, Z);
  not not_2 (not_2_out, EMPIDN);
  nand nand_1 (nand_1_out, FIDBO_15_0[15], not_2_out);
  nand nand_2 (IREQ_15_0_N[14], FIDBO_15_0[14], not_2_out);
  nand nand_3 (nand_3_out, FIDBO_15_0[13], not_2_out);
  nand nand_4 (nand_4_out, FIDBO_15_0[12], not_2_out);
  nand nand_5 (nand_5_out, FIDBO_15_0[11], not_2_out);
  nand nand_6 (nand_6_out, FIDBO_15_0[10], not_2_out);
  nand nand_7 (IREQ_15_0_N[9], FIDBO_15_0[9], not_2_out);
  nand nand_8 (nand_8_out, FIDBO_15_0[8], not_2_out);
  nand nand_9 (IREQ_15_0_N[7], FIDBO_15_0[7], not_2_out);
  nand nand_10 (IREQ_15_0_N[6], FIDBO_15_0[6], not_2_out);
  nand nand_11 (IREQ_15_0_N[5], FIDBO_15_0[5], not_2_out);
  nand nand_12 (IREQ_15_0_N[4], FIDBO_15_0[4], not_2_out);
  nand nand_13 (nand_13_out, FIDBO_15_0[3], not_2_out);
  nand nand_14 (nand_14_out, FIDBO_15_0[2], not_2_out);
  nand nand_15 (nand_15_out, FIDBO_15_0[1], not_2_out);
  nand nand_16 (nand_16_out, FIDBO_15_0[0], not_2_out);
  nor nor_1 (IREQ_15_0_N[15], ~nand_1_out, ~BINT15N);  // NOR_Gate
  nor nor_2 (IREQ_15_0_N[13], ~nand_3_out, ~POWFAILN);  // NOR_Gate
  nor nor_3 (IREQ_15_0_N[12], ~nand_4_out, ~NORN);  // NOR_Gate
  nor nor_4 (IREQ_15_0_N[11], ~nand_5_out, ~PARERRN);  // NOR_Gate
  nor nor_5 (IREQ_15_0_N[10], ~nand_6_out, ~IOXERRN);  // NOR_Gate
  nor nor_6 (IREQ_15_0_N[8], ~nand_8_out, ~not_1_out);  // NOR_Gate
  nor nor_7 (IREQ_15_0_N[3], ~nand_13_out, ~BINT13N);  // NOR_Gate
  nor nor_8 (IREQ_15_0_N[2], ~nand_14_out, ~BINT12N);  // NOR_Gate
  nor nor_9 (IREQ_15_0_N[1], ~nand_15_out, ~BINT11N);  // NOR_Gate
  nor nor_10 (IREQ_15_0_N[0], ~nand_16_out, ~BINT10N);  // NOR_Gate

  // Notes on the sheet:
  //   Page 76 - CGA_INTR_IRSRC
  //   EMPID
  //   IREQ15N
  //   IREQ14N
  //   IREQ13N
  //   IREQ12N
  //   IREQ11N
  //   IREQ10N
endmodule

module CGA_INTR_CNTLR (
  input  [15:0] IREQ_15_0_N,
  input  MCLK,
  input  [15:0] FIDBO_15_0,
  input  [3:0] LAA_3_0,
  input  EPIC,
  output [15:0] PICMASK_15_0,
  output HIGSN,
  output PD,
  output [2:0] PICV_2_0,
  output IRQN,
  output LOGSN,
  output [2:0] PICS_2_0,
  output EPICMASKN
);

  wire A, B, C, D, E, G, H, HIF, HIK, HIPASSALL, J, L, LOF, LOK, LOPASSALL, M, N, not_1_out, OEM, OESN, S,
       VECGEN_hidet, VECGEN_hivges, VECGEN_lodet, VECGEN_lovges;
  wire [2:0] VECGEN_hivec_2_0, VECGEN_hx_2_0, VECGEN_hx_2_0_n, VECGEN_lovec_2_0, VECGEN_lx_2_0,
       VECGEN_lx_2_0_n;
  wire [7:0] multiplexer_1_out, multiplexer_1_out_2;
  wire [15:0] CLR_CLEAR_CONTROL_clrq, IRQ_mireq_15_0_n;

  Multiplexer #(.width(16)) multiplexer_1 (
    .in0(FIDBO_15_0), .in1(PICMASK_15_0), .out({multiplexer_1_out_2, multiplexer_1_out}), .sel(OEM));
  not not_1 (not_1_out, MCLK);
  CGA_INTR_CNTLR_MDCD MDCD (
    .LAA_3_0(LAA_3_0), .EPIC(EPIC), .HIPASSALL(HIPASSALL), .LOPASSALL(LOPASSALL), .MCLK(MCLK), .OESN(OESN),
    .E(E), .J(J), .D(D), .N(N), .HIK(HIK), .A(A), .HIF(HIF), .G(G), .H(H), .L(L), .B(B), .S(S), .M(M),
    .LOF(LOF), .C(C), .LOK(LOK), .OEM(OEM), .EPICMASKN(EPICMASKN));
  CGA_INTR_CNTLR_IRQ IRQ (
    .CLRQ_15_0(CLR_CLEAR_CONTROL_clrq), .IREQ_15_0_N(IREQ_15_0_N), .CPN(not_1_out), .MCLK(MCLK),
    .DIN_15_0({multiplexer_1_out_2, multiplexer_1_out}), .A(A), .B(B), .C(C),
    .MIREQ_15_0_N(IRQ_mireq_15_0_n), .PICMASK_15_0(PICMASK_15_0));
  CGA_INTR_CNTLR_VECGEN VECGEN (
    .MIREQ_15_0_N(IRQ_mireq_15_0_n), .MCLK(MCLK), .N(N), .HIF(HIF), .FIDBO3(FIDBO_15_0[3]), .LOF(LOF), .G(G),
    .FIDBO4(FIDBO_15_0[4]), .HIGSN(HIGSN), .FIDBO_2_0(FIDBO_15_0[2:0]), .LOGSN(LOGSN), .OESN(OESN),
    .HIDET(VECGEN_hidet), .HIVEC_2_0(VECGEN_hivec_2_0), .LODET(VECGEN_lodet), .LOVEC_2_0(VECGEN_lovec_2_0),
    .HX_2_0(VECGEN_hx_2_0), .HX_2_0_N(VECGEN_hx_2_0_n), .LX_2_0(VECGEN_lx_2_0), .LX_2_0_N(VECGEN_lx_2_0_n),
    .PICS_2_0(PICS_2_0), .HIVGES(VECGEN_hivges), .LOVGES(VECGEN_lovges));
  CGA_INTR_CNTLR_CLR CLR_CLEAR_CONTROL (
    .J(J), .LOK(LOK), .HIK(HIK), .DIN_7_0(multiplexer_1_out), .DIN_15_8(multiplexer_1_out_2),
    .LX_2_0(VECGEN_lx_2_0), .HX_2_0(VECGEN_hx_2_0), .LX_2_0_N(VECGEN_lx_2_0_n), .HX_2_0_N(VECGEN_hx_2_0_n),
    .CLRQ(CLR_CLEAR_CONTROL_clrq));
  CGA_INTR_CNTLR_IRGEL IRGEL (
    .FIDB03(FIDBO_15_0[3]), .HIDET(VECGEN_hidet), .HIVGES(VECGEN_hivges), .E(E), .MCLK(MCLK), .D(D), .S(S),
    .H(H), .HIVEC_2_0(VECGEN_hivec_2_0), .LOVEC_2_0(VECGEN_lovec_2_0), .LODET(VECGEN_lodet),
    .LOVGES(VECGEN_lovges), .N(N), .L(L), .FIDB04(FIDBO_15_0[4]), .M(M), .HIGSN(HIGSN), .PD(PD),
    .HIPASSALL(HIPASSALL), .PICV_2_0(PICV_2_0), .IRQN(IRQN), .LOPASSALL(LOPASSALL), .LOGSN(LOGSN));

  // Other names for the same wires on the sheet: FIDB0_2_0[2:0] = FIDBO_15_0[2:0]; FIDB03 = FIDBO_15_0[3];
  //   FIDB04 = FIDBO_15_0[4]

  // Notes on the sheet:
  //   Page 77 - CGA_INTR_CNTLR
  //   Vector Generator & Status
endmodule

module CGA_INTR_CNTLR_IRQ_REG (
  input  [15:0] CLRQ_15_0,
  input  [15:0] IRQ_15_0_N,
  input  CPN,
  input  MCLK,
  output [15:0] LREQ_15_0
);

  CGA_INTR_CNTLR_IRQ_REG_RQBIT RQBIT_0 (
    .PN(IRQ_15_0_N[0]), .CPN(CPN), .CLR(CLRQ_15_0[0]), .CP(MCLK), .INR(LREQ_15_0[0]));
  CGA_INTR_CNTLR_IRQ_REG_RQBIT RQBIT_1 (
    .PN(IRQ_15_0_N[1]), .CPN(CPN), .CLR(CLRQ_15_0[1]), .CP(MCLK), .INR(LREQ_15_0[1]));
  CGA_INTR_CNTLR_IRQ_REG_RQBIT RQBIT_2 (
    .PN(IRQ_15_0_N[2]), .CPN(CPN), .CLR(CLRQ_15_0[2]), .CP(MCLK), .INR(LREQ_15_0[2]));
  CGA_INTR_CNTLR_IRQ_REG_RQBIT RQBIT_3 (
    .PN(IRQ_15_0_N[3]), .CPN(CPN), .CLR(CLRQ_15_0[3]), .CP(MCLK), .INR(LREQ_15_0[3]));
  CGA_INTR_CNTLR_IRQ_REG_RQBIT RQBIT_4 (
    .PN(IRQ_15_0_N[4]), .CPN(CPN), .CLR(CLRQ_15_0[4]), .CP(MCLK), .INR(LREQ_15_0[4]));
  CGA_INTR_CNTLR_IRQ_REG_RQBIT RQBIT_5 (
    .PN(IRQ_15_0_N[5]), .CPN(CPN), .CLR(CLRQ_15_0[5]), .CP(MCLK), .INR(LREQ_15_0[5]));
  CGA_INTR_CNTLR_IRQ_REG_RQBIT RQBIT_6 (
    .PN(IRQ_15_0_N[6]), .CPN(CPN), .CLR(CLRQ_15_0[6]), .CP(MCLK), .INR(LREQ_15_0[6]));
  CGA_INTR_CNTLR_IRQ_REG_RQBIT RQBIT_7 (
    .PN(IRQ_15_0_N[7]), .CPN(CPN), .CLR(CLRQ_15_0[7]), .CP(MCLK), .INR(LREQ_15_0[7]));
  CGA_INTR_CNTLR_IRQ_REG_RQBIT RQBIT_8 (
    .PN(CLRQ_15_0[8]), .CPN(CPN), .CLR(IRQ_15_0_N[8]), .CP(MCLK), .INR(LREQ_15_0[8]));
  CGA_INTR_CNTLR_IRQ_REG_RQBIT RQBIT_9 (
    .PN(CLRQ_15_0[9]), .CPN(CPN), .CLR(IRQ_15_0_N[9]), .CP(MCLK), .INR(LREQ_15_0[9]));
  CGA_INTR_CNTLR_IRQ_REG_RQBIT RQBIT_10 (
    .PN(CLRQ_15_0[10]), .CPN(CPN), .CLR(IRQ_15_0_N[10]), .CP(MCLK), .INR(LREQ_15_0[10]));
  CGA_INTR_CNTLR_IRQ_REG_RQBIT RQBIT_11 (
    .PN(CLRQ_15_0[11]), .CPN(CPN), .CLR(IRQ_15_0_N[11]), .CP(MCLK), .INR(LREQ_15_0[11]));
  CGA_INTR_CNTLR_IRQ_REG_RQBIT RQBIT_12 (
    .PN(CLRQ_15_0[12]), .CPN(CPN), .CLR(IRQ_15_0_N[12]), .CP(MCLK), .INR(LREQ_15_0[12]));
  CGA_INTR_CNTLR_IRQ_REG_RQBIT RQBIT_13 (
    .PN(CLRQ_15_0[13]), .CPN(CPN), .CLR(IRQ_15_0_N[13]), .CP(MCLK), .INR(LREQ_15_0[13]));
  CGA_INTR_CNTLR_IRQ_REG_RQBIT RQBIT_14 (
    .PN(CLRQ_15_0[14]), .CPN(CPN), .CLR(IRQ_15_0_N[14]), .CP(MCLK), .INR(LREQ_15_0[14]));
  CGA_INTR_CNTLR_IRQ_REG_RQBIT RQBIT_15 (
    .PN(CLRQ_15_0[15]), .CPN(CPN), .CLR(IRQ_15_0_N[15]), .CP(MCLK), .INR(LREQ_15_0[15]));

  // Notes on the sheet:
  //   Page 78 - CGA_INTR_CNTLR_IRQ_REG - Completed, not tested
endmodule

module CGA_INTR_CNTLR_IRQ_REG_RQBIT (
  input  PN,
  input  CPN,
  input  CLR,
  input  CP,
  output INR
);

  wire nand_1_out, nand_2_out, nand_3_out, not_1_out, not_2_out, not_3_out, or_1_out;

  nand nand_1 (nand_1_out, CPN, CLR);
  not not_1 (not_1_out, CLR);
  not not_2 (not_2_out, PN);
  not not_3 (not_3_out, nand_2_out);
  or or_1 (or_1_out, not_2_out, not_3_out);
  nand nand_2 (nand_2_out, or_1_out, nand_1_out);
  nand nand_3 (nand_3_out, or_1_out, not_1_out);
  D_Flip_Flop d_ff_1 (.D(nand_3_out), .clk(CP), .Qn(INR));  // open: Q, preset, reset

  // Notes on the sheet:
  //   Page 78 - CGA_INTR_CNTLR_IRQ_REG_RQBIT - Completed, not tested
endmodule

module CGA_INTR_CNTLR_IRQ (
  input  [15:0] CLRQ_15_0,
  input  [15:0] IREQ_15_0_N,
  input  CPN,
  input  MCLK,
  input  [15:0] DIN_15_0,
  input  A,
  input  B,
  input  C,
  output [15:0] MIREQ_15_0_N,
  output [15:0] PICMASK_15_0
);

  wire [15:0] IRQ_MASK_picmask_15_0_n, IRQ_REG_lreq_15_0;

  CGA_INTR_CNTLR_IRQ_REG IRQ_REG (
    .CLRQ_15_0(CLRQ_15_0), .IRQ_15_0_N(IREQ_15_0_N), .CPN(CPN), .MCLK(MCLK), .LREQ_15_0(IRQ_REG_lreq_15_0));
  CGA_INTR_CNTLR_IRQ_MASK IRQ_MASK (
    .DIN_15_0(DIN_15_0), .A(A), .B(B), .C(C), .MCLK(MCLK), .PICMASK_15_0_N(IRQ_MASK_picmask_15_0_n),
    .PICMASK_15_0(PICMASK_15_0));
  CGA_INTR_CNTLR_IRQ_MREQ IRQ_MREQ (
    .LREQ_15_0(IRQ_REG_lreq_15_0), .PICMASK_15_0_N(IRQ_MASK_picmask_15_0_n), .MIREQ_15_0(MIREQ_15_0_N));

  // Notes on the sheet:
  //   Page 79 - CGA_INTR_CNTLR_IRQ 
endmodule

module CGA_INTR_CNTLR_IRQ_MASK (
  input  [15:0] DIN_15_0,
  input  A,
  input  B,
  input  C,
  input  MCLK,
  output [15:0] PICMASK_15_0_N,
  output [15:0] PICMASK_15_0
);

  wire not_1_out;

  not not_1 (not_1_out, C);
  CGA_INTR_CNTLR_IRQ_MASK_MASKBIT MASKBIT15 (
    .DCDA(A), .DATAIN(DIN_15_0[15]), .DCDB(B), .DCDCN(not_1_out), .CLOCK(MCLK), .MSKN(PICMASK_15_0_N[15]),
    .MSK(PICMASK_15_0[15]));
  CGA_INTR_CNTLR_IRQ_MASK_MASKBIT MASKBIT14 (
    .DCDA(A), .DATAIN(DIN_15_0[14]), .DCDB(B), .DCDCN(not_1_out), .CLOCK(MCLK), .MSKN(PICMASK_15_0_N[14]),
    .MSK(PICMASK_15_0[14]));
  CGA_INTR_CNTLR_IRQ_MASK_MASKBIT MASKBIT13 (
    .DCDA(A), .DATAIN(DIN_15_0[13]), .DCDB(B), .DCDCN(not_1_out), .CLOCK(MCLK), .MSKN(PICMASK_15_0_N[13]),
    .MSK(PICMASK_15_0[13]));
  CGA_INTR_CNTLR_IRQ_MASK_MASKBIT MASKBIT12 (
    .DCDA(A), .DATAIN(DIN_15_0[12]), .DCDB(B), .DCDCN(not_1_out), .CLOCK(MCLK), .MSKN(PICMASK_15_0_N[12]),
    .MSK(PICMASK_15_0[12]));
  CGA_INTR_CNTLR_IRQ_MASK_MASKBIT MASKBIT11 (
    .DCDA(A), .DATAIN(DIN_15_0[11]), .DCDB(B), .DCDCN(not_1_out), .CLOCK(MCLK), .MSKN(PICMASK_15_0_N[11]),
    .MSK(PICMASK_15_0[11]));
  CGA_INTR_CNTLR_IRQ_MASK_MASKBIT MASKBIT10 (
    .DCDA(A), .DATAIN(DIN_15_0[10]), .DCDB(B), .DCDCN(not_1_out), .CLOCK(MCLK), .MSKN(PICMASK_15_0_N[10]),
    .MSK(PICMASK_15_0[10]));
  CGA_INTR_CNTLR_IRQ_MASK_MASKBIT MASKBIT9 (
    .DCDA(A), .DATAIN(DIN_15_0[9]), .DCDB(B), .DCDCN(not_1_out), .CLOCK(MCLK), .MSKN(PICMASK_15_0_N[9]),
    .MSK(PICMASK_15_0[9]));
  CGA_INTR_CNTLR_IRQ_MASK_MASKBIT MASKBIT8 (
    .DCDA(A), .DATAIN(DIN_15_0[8]), .DCDB(B), .DCDCN(not_1_out), .CLOCK(MCLK), .MSKN(PICMASK_15_0_N[8]),
    .MSK(PICMASK_15_0[8]));
  CGA_INTR_CNTLR_IRQ_MASK_MASKBIT MASKBIT7 (
    .DCDA(A), .DATAIN(DIN_15_0[7]), .DCDB(B), .DCDCN(not_1_out), .CLOCK(MCLK), .MSKN(PICMASK_15_0_N[7]),
    .MSK(PICMASK_15_0[7]));
  CGA_INTR_CNTLR_IRQ_MASK_MASKBIT MASKBIT6 (
    .DCDA(A), .DATAIN(DIN_15_0[6]), .DCDB(B), .DCDCN(not_1_out), .CLOCK(MCLK), .MSKN(PICMASK_15_0_N[6]),
    .MSK(PICMASK_15_0[6]));
  CGA_INTR_CNTLR_IRQ_MASK_MASKBIT MASKBIT5 (
    .DCDA(A), .DATAIN(DIN_15_0[5]), .DCDB(B), .DCDCN(not_1_out), .CLOCK(MCLK), .MSKN(PICMASK_15_0_N[5]),
    .MSK(PICMASK_15_0[5]));
  CGA_INTR_CNTLR_IRQ_MASK_MASKBIT MASKBIT4 (
    .DCDA(A), .DATAIN(DIN_15_0[4]), .DCDB(B), .DCDCN(not_1_out), .CLOCK(MCLK), .MSKN(PICMASK_15_0_N[4]),
    .MSK(PICMASK_15_0[4]));
  CGA_INTR_CNTLR_IRQ_MASK_MASKBIT MASKBIT3 (
    .DCDA(A), .DATAIN(DIN_15_0[3]), .DCDB(B), .DCDCN(not_1_out), .CLOCK(MCLK), .MSKN(PICMASK_15_0_N[3]),
    .MSK(PICMASK_15_0[3]));
  CGA_INTR_CNTLR_IRQ_MASK_MASKBIT MASKBIT2 (
    .DCDA(A), .DATAIN(DIN_15_0[2]), .DCDB(B), .DCDCN(not_1_out), .CLOCK(MCLK), .MSKN(PICMASK_15_0_N[2]),
    .MSK(PICMASK_15_0[2]));
  CGA_INTR_CNTLR_IRQ_MASK_MASKBIT MASKBIT1 (
    .DCDA(A), .DATAIN(DIN_15_0[1]), .DCDB(B), .DCDCN(not_1_out), .CLOCK(MCLK), .MSKN(PICMASK_15_0_N[1]),
    .MSK(PICMASK_15_0[1]));
  CGA_INTR_CNTLR_IRQ_MASK_MASKBIT MASKBIT0 (
    .DCDA(A), .DATAIN(DIN_15_0[0]), .DCDB(B), .DCDCN(not_1_out), .CLOCK(MCLK), .MSKN(PICMASK_15_0_N[0]),
    .MSK(PICMASK_15_0[0]));

  // Notes on the sheet:
  //   Page 80 - CGA_INTR_CNTLR_IRQ_MASK 
  //   CN
endmodule

module CGA_INTR_CNTLR_IRQ_MASK_MASKBIT (
  input  DCDA,
  input  DATAIN,
  input  DCDB,
  input  DCDCN,
  input  CLOCK,
  output MSKN,
  output MSK
);

  wire nand_1_out, nand_2_out, nand_3_out, or_1_out, xnor_1_out;

  nand nand_1 (nand_1_out, MSK, DCDA);
  nand nand_2 (nand_2_out, DATAIN, DCDB);
  nand nand_3 (nand_3_out, DCDB, MSKN, DCDCN);
  or or_1 (or_1_out, ~nand_1_out, ~nand_2_out, ~nand_3_out);  // OR_Gate
  xnor xnor_1 (xnor_1_out, or_1_out, DCDCN);
  D_Flip_Flop d_ff_1 (.D(xnor_1_out), .clk(CLOCK), .Q(MSKN), .Qn(MSK));  // open: preset, reset

  // Notes on the sheet:
  //   Page 80 - CGA_INTR_CNTLR_IRQ_MASK_MASKBIT
endmodule

module CGA_INTR_CNTLR_IRQ_MREQ (
  input  [15:0] LREQ_15_0,
  input  [15:0] PICMASK_15_0_N,
  output [15:0] MIREQ_15_0
);

  nand nand_1 (MIREQ_15_0[15], LREQ_15_0[15], PICMASK_15_0_N[15]);
  nand nand_2 (MIREQ_15_0[14], LREQ_15_0[14], PICMASK_15_0_N[14]);
  nand nand_3 (MIREQ_15_0[13], LREQ_15_0[13], PICMASK_15_0_N[13]);
  nand nand_4 (MIREQ_15_0[12], LREQ_15_0[12], PICMASK_15_0_N[12]);
  nand nand_5 (MIREQ_15_0[11], LREQ_15_0[11], PICMASK_15_0_N[11]);
  nand nand_6 (MIREQ_15_0[10], LREQ_15_0[10], PICMASK_15_0_N[10]);
  nand nand_7 (MIREQ_15_0[9], LREQ_15_0[9], PICMASK_15_0_N[9]);
  nand nand_8 (MIREQ_15_0[8], LREQ_15_0[8], PICMASK_15_0_N[8]);
  nand nand_9 (MIREQ_15_0[7], LREQ_15_0[7], PICMASK_15_0_N[7]);
  nand nand_10 (MIREQ_15_0[6], LREQ_15_0[6], PICMASK_15_0_N[6]);
  nand nand_11 (MIREQ_15_0[5], LREQ_15_0[5], PICMASK_15_0_N[5]);
  nand nand_12 (MIREQ_15_0[4], LREQ_15_0[4], PICMASK_15_0_N[4]);
  nand nand_13 (MIREQ_15_0[3], LREQ_15_0[3], PICMASK_15_0_N[3]);
  nand nand_14 (MIREQ_15_0[2], LREQ_15_0[2], PICMASK_15_0_N[2]);
  nand nand_15 (MIREQ_15_0[1], LREQ_15_0[1], PICMASK_15_0_N[1]);
  nand nand_16 (MIREQ_15_0[0], LREQ_15_0[0], PICMASK_15_0_N[0]);

  // Notes on the sheet:
  //   Page 81 - CGA_INTR_CNTLR_IRQ_MREQ
  //   PICMASK0N
  //   PICMASK15N
  //   MIREQ15N
  //   MIREQ0N
endmodule

module CGA_INTR_CNTLR_CLR (
  input  J,
  input  LOK,
  input  HIK,
  input  [7:0] DIN_7_0,
  input  [7:0] DIN_15_8,
  input  [2:0] LX_2_0,
  input  [2:0] HX_2_0,
  input  [2:0] LX_2_0_N,
  input  [2:0] HX_2_0_N,
  output [15:0] CLRQ
);

  CGA_INTR_CNTLR_CLR_CLRBIT CLRB7 (
    .DCDJ(J), .DCDK(LOK), .DATA(DIN_7_0[7]), .X0(LX_2_0[0]), .X1(LX_2_0[1]), .X2(LX_2_0[2]), .BIT(CLRQ[7]));
  CGA_INTR_CNTLR_CLR_CLRBIT CLRB6 (
    .DCDJ(J), .DCDK(LOK), .DATA(DIN_7_0[6]), .X0(LX_2_0_N[0]), .X1(LX_2_0[1]), .X2(LX_2_0[2]), .BIT(CLRQ[6]));
  CGA_INTR_CNTLR_CLR_CLRBIT CLRB5 (
    .DCDJ(J), .DCDK(LOK), .DATA(DIN_7_0[5]), .X0(LX_2_0[0]), .X1(LX_2_0_N[1]), .X2(LX_2_0[2]), .BIT(CLRQ[5]));
  CGA_INTR_CNTLR_CLR_CLRBIT CLRB4 (
    .DCDJ(J), .DCDK(LOK), .DATA(DIN_7_0[4]), .X0(LX_2_0_N[0]), .X1(LX_2_0_N[1]), .X2(LX_2_0[2]), .BIT(CLRQ[4]));
  CGA_INTR_CNTLR_CLR_CLRBIT CLRB3 (
    .DCDJ(J), .DCDK(LOK), .DATA(DIN_7_0[3]), .X0(LX_2_0[0]), .X1(LX_2_0[1]), .X2(LX_2_0_N[2]), .BIT(CLRQ[3]));
  CGA_INTR_CNTLR_CLR_CLRBIT CLRB2 (
    .DCDJ(J), .DCDK(LOK), .DATA(DIN_7_0[2]), .X0(LX_2_0_N[0]), .X1(LX_2_0[1]), .X2(LX_2_0_N[2]), .BIT(CLRQ[2]));
  CGA_INTR_CNTLR_CLR_CLRBIT CLRB1 (
    .DCDJ(J), .DCDK(LOK), .DATA(DIN_7_0[1]), .X0(LX_2_0[0]), .X1(LX_2_0_N[1]), .X2(LX_2_0_N[2]), .BIT(CLRQ[1]));
  CGA_INTR_CNTLR_CLR_CLRBIT CLRB0 (
    .DCDJ(J), .DCDK(LOK), .DATA(DIN_7_0[0]), .X0(LX_2_0_N[0]), .X1(LX_2_0_N[1]), .X2(LX_2_0_N[2]),
    .BIT(CLRQ[0]));
  CGA_INTR_CNTLR_CLR_CLRBIT CLRB15 (
    .DCDJ(J), .DCDK(HIK), .DATA(DIN_15_8[7]), .X0(HX_2_0[0]), .X1(HX_2_0[1]), .X2(HX_2_0[2]), .BIT(CLRQ[15]));
  CGA_INTR_CNTLR_CLR_CLRBIT CLRB14 (
    .DCDJ(J), .DCDK(HIK), .DATA(DIN_15_8[6]), .X0(HX_2_0_N[0]), .X1(HX_2_0[1]), .X2(HX_2_0[2]), .BIT(CLRQ[14]));
  CGA_INTR_CNTLR_CLR_CLRBIT CLRB13 (
    .DCDJ(J), .DCDK(HIK), .DATA(DIN_15_8[5]), .X0(HX_2_0[0]), .X1(HX_2_0_N[1]), .X2(HX_2_0[2]), .BIT(CLRQ[13]));
  CGA_INTR_CNTLR_CLR_CLRBIT CLRB12 (
    .DCDJ(J), .DCDK(HIK), .DATA(DIN_15_8[4]), .X0(HX_2_0_N[0]), .X1(HX_2_0_N[1]), .X2(HX_2_0[2]),
    .BIT(CLRQ[12]));
  CGA_INTR_CNTLR_CLR_CLRBIT CLRB11 (
    .DCDJ(J), .DCDK(HIK), .DATA(DIN_15_8[3]), .X0(HX_2_0[0]), .X1(HX_2_0[1]), .X2(HX_2_0_N[2]), .BIT(CLRQ[11]));
  CGA_INTR_CNTLR_CLR_CLRBIT CLRB10 (
    .DCDJ(J), .DCDK(HIK), .DATA(DIN_15_8[2]), .X0(HX_2_0_N[0]), .X1(HX_2_0[1]), .X2(HX_2_0_N[2]),
    .BIT(CLRQ[10]));
  CGA_INTR_CNTLR_CLR_CLRBIT CLRB9 (
    .DCDJ(J), .DCDK(HIK), .DATA(DIN_15_8[1]), .X0(HX_2_0[0]), .X1(HX_2_0_N[1]), .X2(HX_2_0_N[2]),
    .BIT(CLRQ[9]));
  CGA_INTR_CNTLR_CLR_CLRBIT CLRB8 (
    .DCDJ(J), .DCDK(HIK), .DATA(DIN_15_8[0]), .X0(HX_2_0_N[0]), .X1(HX_2_0_N[1]), .X2(HX_2_0_N[2]),
    .BIT(CLRQ[8]));

  // Notes on the sheet:
  //   Page 82 - CGA_INTR_CNTLR_CLR
  //   CLRQ7
  //   CLRQ15
endmodule

module CGA_INTR_CNTLR_CLR_CLRBIT (
  input  DCDJ,
  input  DCDK,
  input  DATA,
  input  X0,
  input  X1,
  input  X2,
  output BIT
);

  wire nand_1_out, nand_2_out, nand_3_out;

  nand nand_1 (nand_1_out, DCDJ, DCDK);
  nand nand_2 (nand_2_out, DCDJ, DATA);
  nand nand_3 (nand_3_out, DCDK, X0, X1, X2);
  or or_1 (BIT, ~nand_1_out, ~nand_2_out, ~nand_3_out);  // OR_Gate
endmodule

module CGA_INTR_CNTLR_VECGEN (
  input  [15:0] MIREQ_15_0_N,
  input  MCLK,
  input  N,
  input  HIF,
  input  FIDBO3,
  input  LOF,
  input  G,
  input  FIDBO4,
  input  HIGSN,
  input  [2:0] FIDBO_2_0,
  input  LOGSN,
  input  OESN,
  output HIDET,
  output [2:0] HIVEC_2_0,
  output LODET,
  output [2:0] LOVEC_2_0,
  output [2:0] HX_2_0,
  output [2:0] HX_2_0_N,
  output [2:0] LX_2_0,
  output [2:0] LX_2_0_N,
  output [2:0] PICS_2_0,
  output HIVGES,
  output LOVGES
);

  wire [2:0] ISMUX_hisin_2_0, ISMUX_losin_2_0, STAT_histat_2_0, STAT_lostat_2_0;

  CGA_INTR_CNTLR_VECGEN_PTY PTY (
    .MIREQ_15_0_N(MIREQ_15_0_N), .HIDET(HIDET), .HIVEC(HIVEC_2_0), .LODET(LODET), .LOVEC(LOVEC_2_0));
  CGA_INTR_CNTLR_VECGEN_VHR VHR (
    .HIVEC_2_0(HIVEC_2_0), .LOVEC_2_0(LOVEC_2_0), .MCLK(MCLK), .N(N), .HX_2_0(HX_2_0), .HX_2_0_N(HX_2_0_N),
    .LX_2_0(LX_2_0), .LX_2_0_N(LX_2_0_N));
  CGA_INTR_CNTLR_VECGEN_ISMUX ISMUX (
    .HIGSN(HIGSN), .HISTAT_2_0(STAT_histat_2_0), .FIDBO_2_0(FIDBO_2_0), .LOSTAT_2_0(STAT_lostat_2_0),
    .LOGSN(LOGSN), .OESN(OESN), .HISIN_2_0(ISMUX_hisin_2_0), .LOSIN_2_0(ISMUX_losin_2_0));
  CGA_INTR_CNTLR_VECGEN_CMP CMP (
    .HIVEC_2_0(HIVEC_2_0), .HISTAT_2_0(STAT_histat_2_0), .LOVEC_2_0(LOVEC_2_0), .LOSTAT_2_0(STAT_lostat_2_0),
    .HIVGES(HIVGES), .LOVGES(LOVGES));
  CGA_INTR_CNTLR_VECGEN_STAT STAT (
    .HIVEC_2_0(HIVEC_2_0), .HISIN_2_0(ISMUX_hisin_2_0), .HIF(HIF), .FIDBO3(FIDBO3), .LOVEC_2_0(LOVEC_2_0),
    .LOSIN_2_0(ISMUX_losin_2_0), .LOF(LOF), .G(G), .FIDBO4(FIDBO4), .MCLK(MCLK),
    .HISTAT_2_0(STAT_histat_2_0), .LOSTAT_2_0(STAT_lostat_2_0));
  CGA_INTR_CNTLR_VECGEN_OSMUX OSMUX (
    .HIGSN(HIGSN), .HISTAT_2_0(STAT_histat_2_0), .LOSTAT_2_0(STAT_lostat_2_0), .LOGSN(LOGSN), .OESN(OESN),
    .PICS_2_0(PICS_2_0));

  // Notes on the sheet:
  //   Page 83 - CGA_INTR_CNTLR_VECGEN 
  //   HIGSN
  //   LOGSN
  //   HISTAT
  //   LOSTAT
endmodule

module CGA_INTR_CNTLR_VECGEN_PTY (
  input  [15:0] MIREQ_15_0_N,
  output HIDET,
  output [2:0] HIVEC,
  output LODET,
  output [2:0] LOVEC
);

  CGA_INTR_CNTLR_VECGEN_PTY_PTYENC PTYENC_HI (.RN(MIREQ_15_0_N[15:8]), .DET(HIDET), .V_2_0(HIVEC));
  CGA_INTR_CNTLR_VECGEN_PTY_PTYENC PTYENC_LO (.RN(MIREQ_15_0_N[7:0]), .DET(LODET), .V_2_0(LOVEC));

  // Notes on the sheet:
  //   Page 84 - CGA_INTR_CNTLR_VECGEN_PTY  Completed. Tested manually
endmodule

module CGA_INTR_CNTLR_VECGEN_PTY_PTYENC (
  input  [7:0] RN,
  output DET,
  output [2:0] V_2_0
);

  wire ANDv1_out, nand_1_out, nand_2_out, nand_3_out, nor_1_out, nor_2_out, not_1_out, not_2_out, not_3_out,
       not_4_out, not_5_out, not_6_out, not_7_out, O1_out, O2_out, or_1_out;

  not not_1 (not_1_out, RN[7]);
  not not_2 (not_2_out, RN[6]);
  not not_3 (not_3_out, RN[5]);
  not not_4 (not_4_out, RN[4]);
  not not_5 (not_5_out, RN[3]);
  not not_6 (not_6_out, RN[2]);
  not not_7 (not_7_out, RN[1]);
  // NOT_Gate not_8 has open pins: in=RN[0], out=open
  or OR_DET (DET, ~RN[0], ~RN[1], ~RN[2], ~RN[3], ~RN[4], ~RN[5], ~RN[6], ~RN[7]);  // OR_Gate
  nor O2 (O2_out, not_4_out, not_3_out, not_2_out, not_1_out);
  not V2 (V_2_0[2], O2_out);
  or or_1 (or_1_out, not_1_out, not_2_out);
  nor O1 (O1_out, or_1_out, ANDv1_out);
  not V1 (V_2_0[1], O1_out);
  nor nor_1 (nor_1_out, not_5_out, not_6_out);
  and ANDv1 (ANDv1_out, ~not_3_out, ~not_4_out, ~nor_1_out);  // AND_Gate
  not V0 (V_2_0[0], nor_2_out);
  nand nand_1 (nand_1_out, RN[6], not_3_out);
  nor nor_2 (nor_2_out, ~RN[7], ~nand_1_out, ~nand_2_out, ~nand_3_out);  // NOR_Gate
  nand nand_2 (nand_2_out, RN[6], RN[4], not_5_out);
  nand nand_3 (nand_3_out, RN[6], RN[4], RN[2], not_7_out);

  // Notes on the sheet:
  //   R7-0
  //   R7-0N
  //   Page 84 - CGA_INTR_CNTLR_VECGEN_PTY_PTYENC  Completed, tested manually
endmodule

module CGA_INTR_CNTLR_VECGEN_ISMUX (
  input  HIGSN,
  input  [2:0] HISTAT_2_0,
  input  [2:0] FIDBO_2_0,
  input  [2:0] LOSTAT_2_0,
  input  LOGSN,
  input  OESN,
  output [2:0] HISIN_2_0,
  output [2:0] LOSIN_2_0
);

  wire and_1_out, and_2_out, nand_1_out, nand_2_out, nand_3_out, nand_4_out, nand_5_out, nand_6_out,
       nand_7_out, nand_8_out, nand_9_out, nand_10_out, nand_11_out, nand_12_out, not_1_out, not_2_out,
       not_3_out, not_4_out;

  not not_1 (not_1_out, HIGSN);
  not not_2 (not_2_out, OESN);
  and and_1 (and_1_out, not_1_out, not_2_out);
  and and_2 (and_2_out, ~LOGSN, ~OESN);  // AND_Gate
  not not_3 (not_3_out, and_1_out);
  not not_4 (not_4_out, and_2_out);
  nand nand_1 (nand_1_out, HISTAT_2_0[2], and_1_out);
  nand nand_2 (nand_2_out, FIDBO_2_0[2], not_3_out);
  nand nand_3 (nand_3_out, HISTAT_2_0[1], and_1_out);
  nand nand_4 (nand_4_out, FIDBO_2_0[1], not_3_out);
  nand nand_5 (nand_5_out, HISTAT_2_0[0], and_1_out);
  nand nand_6 (nand_6_out, FIDBO_2_0[0], not_3_out);
  nand nand_7 (nand_7_out, LOSTAT_2_0[2], and_2_out);
  nand nand_8 (nand_8_out, FIDBO_2_0[2], not_4_out);
  nand nand_9 (nand_9_out, LOSTAT_2_0[1], and_2_out);
  nand nand_10 (nand_10_out, FIDBO_2_0[1], not_4_out);
  nand nand_11 (nand_11_out, LOSTAT_2_0[0], and_2_out);
  nand nand_12 (nand_12_out, FIDBO_2_0[0], not_4_out);
  or or_1 (HISIN_2_0[2], ~nand_1_out, ~nand_2_out);  // OR_Gate
  or or_2 (HISIN_2_0[1], ~nand_3_out, ~nand_4_out);  // OR_Gate
  or or_3 (HISIN_2_0[0], ~nand_5_out, ~nand_6_out);  // OR_Gate
  or or_4 (LOSIN_2_0[2], ~nand_7_out, ~nand_8_out);  // OR_Gate
  or or_5 (LOSIN_2_0[1], ~nand_9_out, ~nand_10_out);  // OR_Gate
  or or_6 (LOSIN_2_0[0], ~nand_11_out, ~nand_12_out);  // OR_Gate

  // Notes on the sheet:
  //   Page 85 - CGA_INTR_CNTLR_VECGEN_ISMUX  
  //   HISTAT2
  //   FIDBO2
  //   HISTAT1
  //   FIDBO1
  //   HISTAT0
  //   FIDBO0
  //   LOSTAT2
  //   FIDBO2
  //   LOSTAT1
  //   FIDBO1
  //   LOSTAT0
  //   FIDBO0
  //   HISIN2
  //   HISIN1
  //   HISIN0
  //   LOSIN2
  //   LOSIN1
  //   LOSIN0
endmodule

module CGA_INTR_CNTLR_VECGEN_VHR (
  input  [2:0] HIVEC_2_0,
  input  [2:0] LOVEC_2_0,
  input  MCLK,
  input  N,
  output [2:0] HX_2_0,
  output [2:0] HX_2_0_N,
  output [2:0] LX_2_0,
  output [2:0] LX_2_0_N
);

  SCAN_FF HX2 (.D(HIVEC_2_0[2]), .TE(N), .TI(HX_2_0[2]), .CLK(MCLK), .Q(HX_2_0[2]), .QN(HX_2_0_N[2]));
  SCAN_FF HX1 (.D(HIVEC_2_0[1]), .TE(N), .TI(HX_2_0[1]), .CLK(MCLK), .Q(HX_2_0[1]), .QN(HX_2_0_N[1]));
  SCAN_FF HX0 (.D(HIVEC_2_0[0]), .TE(N), .TI(HX_2_0[0]), .CLK(MCLK), .Q(HX_2_0[0]), .QN(HX_2_0_N[0]));
  SCAN_FF LX2 (.D(LOVEC_2_0[2]), .TE(N), .TI(LX_2_0[2]), .CLK(MCLK), .Q(LX_2_0[2]), .QN(LX_2_0_N[2]));
  SCAN_FF LX1 (.D(LOVEC_2_0[1]), .TE(N), .TI(LX_2_0[1]), .CLK(MCLK), .Q(LX_2_0[1]), .QN(LX_2_0_N[1]));
  SCAN_FF LX0 (.D(LOVEC_2_0[0]), .TE(N), .TI(LX_2_0[0]), .CLK(MCLK), .Q(LX_2_0[0]), .QN(LX_2_0_N[0]));

  // Notes on the sheet:
  //   Page 86 - CGA_INTR_CNTLR_VECGEN_VHR  Completed. Tested manually
endmodule

module CGA_INTR_CNTLR_VECGEN_STAT (
  input  [2:0] HIVEC_2_0,
  input  [2:0] HISIN_2_0,
  input  HIF,
  input  FIDBO3,
  input  [2:0] LOVEC_2_0,
  input  [2:0] LOSIN_2_0,
  input  LOF,
  input  G,
  input  FIDBO4,
  input  MCLK,
  output [2:0] HISTAT_2_0,
  output [2:0] LOSTAT_2_0
);

  wire and_1_out, and_2_out, not_1_out, not_2_out, not_3_out, not_4_out, not_5_out, not_6_out, not_7_out,
       not_8_out, not_9_out, not_10_out, not_11_out, xnor_1_out, xnor_2_out, xnor_3_out, xnor_4_out;

  not not_1 (not_1_out, HIF);
  not not_2 (not_2_out, FIDBO3);
  not not_3 (not_3_out, LOF);
  not not_4 (not_4_out, G);
  not not_5 (not_5_out, FIDBO4);
  not not_6 (not_6_out, HIVEC_2_0[2]);
  not not_7 (not_7_out, HIVEC_2_0[1]);
  not not_8 (not_8_out, HIVEC_2_0[0]);
  not not_9 (not_9_out, LOVEC_2_0[2]);
  not not_10 (not_10_out, LOVEC_2_0[1]);
  not not_11 (not_11_out, LOVEC_2_0[0]);
  and and_1 (and_1_out, ~not_7_out, ~not_8_out);  // AND_Gate
  and and_2 (and_2_out, ~not_10_out, ~not_11_out);  // AND_Gate
  xnor xnor_1 (xnor_1_out, not_6_out, and_1_out);
  xnor xnor_2 (xnor_2_out, HIVEC_2_0[1], not_8_out);
  xnor xnor_3 (xnor_3_out, not_9_out, and_2_out);
  xnor xnor_4 (xnor_4_out, LOVEC_2_0[1], not_11_out);
  CGA_INTR_CNTLR_VECGEN_STAT_SBIT SBIT2_HI (
    .SIN(HISIN_2_0[2]), .DCDF(xnor_1_out), .GPE(HIF), .DCDG(not_1_out), .DCDFN(G), .VINN(not_4_out),
    .DCDGN(not_2_out), .CK(MCLK), .STS(HISTAT_2_0[2]));
  CGA_INTR_CNTLR_VECGEN_STAT_SBIT SBIT1_HI (
    .SIN(HISIN_2_0[1]), .DCDF(xnor_2_out), .GPE(HIF), .DCDG(not_1_out), .DCDFN(G), .VINN(not_4_out),
    .DCDGN(not_2_out), .CK(MCLK), .STS(HISTAT_2_0[1]));
  CGA_INTR_CNTLR_VECGEN_STAT_SBIT SBIT0_HI (
    .SIN(HISIN_2_0[0]), .DCDF(not_8_out), .GPE(HIF), .DCDG(not_1_out), .DCDFN(G), .VINN(not_4_out),
    .DCDGN(not_2_out), .CK(MCLK), .STS(HISTAT_2_0[0]));
  CGA_INTR_CNTLR_VECGEN_STAT_SBIT SBIT2_LO (
    .SIN(LOSIN_2_0[2]), .DCDF(xnor_3_out), .GPE(LOF), .DCDG(not_3_out), .DCDFN(G), .VINN(not_4_out),
    .DCDGN(not_5_out), .CK(MCLK), .STS(LOSTAT_2_0[2]));
  CGA_INTR_CNTLR_VECGEN_STAT_SBIT SBIT1_LO (
    .SIN(LOSIN_2_0[1]), .DCDF(xnor_4_out), .GPE(LOF), .DCDG(not_3_out), .DCDFN(G), .VINN(not_4_out),
    .DCDGN(not_5_out), .CK(MCLK), .STS(LOSTAT_2_0[1]));
  CGA_INTR_CNTLR_VECGEN_STAT_SBIT SBIT0_LO (
    .SIN(LOSIN_2_0[0]), .DCDF(not_11_out), .GPE(LOF), .DCDG(not_3_out), .DCDFN(G), .VINN(not_4_out),
    .DCDGN(not_5_out), .CK(MCLK), .STS(LOSTAT_2_0[0]));

  // Notes on the sheet:
  //   Page 87 - CGA_INTR_CNTLR_VECGEN_STAT
  //   HIVEC2
  //   HIVEC1
  //   HIVEC0
  //   HIF
  //   HIFN
  //   HIGE
  //   LOVEC2
  //   LOVEC1
  //   LOVEC0
  //   HIVEC2N
  //   HIVEC1N
  //   HIVEC0N
  //   LOVEC2N
  //   LOVEC1N
  //   LOVEC0N
  //   HIVEC2N
  //   HIVEC1
  //   HIVEC0N
  //   LOVEC1
  //   LOVEC0N
  //   HISIN2
  //   HISIN1
  //   HISIN0
  //   LOSIN2
  //   LOSIN1
  //   LOSIN0
  //   HISTAT2
  //   HISTAT1
  //   HISTAT0
  //   LOSTAT2
  //   LOSTAT1
  //   LOSTAT0
endmodule

module CGA_INTR_CNTLR_VECGEN_STAT_SBIT (
  input  SIN,
  input  DCDF,
  input  GPE,
  input  DCDG,
  input  DCDFN,
  input  VINN,
  input  DCDGN,
  input  CK,
  output STS
);

  wire nand_1_out, nand_2_out, nand_3_out, or_1_out;

  nand nand_1 (nand_1_out, SIN, DCDG, DCDF, GPE);
  nand nand_2 (nand_2_out, DCDG, DCDFN, STS);
  nand nand_3 (nand_3_out, VINN, GPE, DCDGN);
  or or_1 (or_1_out, ~nand_1_out, ~nand_2_out, ~nand_3_out);  // OR_Gate
  D_Flip_Flop d_ff_1 (.D(or_1_out), .clk(CK), .Q(STS));  // open: Qn, preset, reset

  // Notes on the sheet:
  //   Page 87 - CGA_INTR_CNTLR_VECGEN_STAT_SBIT
endmodule

module CGA_INTR_CNTLR_VECGEN_CMP (
  input  [2:0] HIVEC_2_0,
  input  [2:0] HISTAT_2_0,
  input  [2:0] LOVEC_2_0,
  input  [2:0] LOSTAT_2_0,
  output HIVGES,
  output LOVGES
);

  CGA_INTR_CNTLR_VECGEN_CMP_MAGCMP HICMP (.S_2_0(HISTAT_2_0), .V_2_0(HIVEC_2_0), .VGES(HIVGES));
  CGA_INTR_CNTLR_VECGEN_CMP_MAGCMP LOCMP (.S_2_0(LOSTAT_2_0), .V_2_0(LOVEC_2_0), .VGES(LOVGES));

  // Notes on the sheet:
  //   Page 88 - CGA_INTR_CNTLR_VECGEN_CMP
endmodule

module CGA_INTR_CNTLR_VECGEN_CMP_MAGCMP (
  input  [2:0] S_2_0,
  input  [2:0] V_2_0,
  output VGES
);

  wire nand_1_out, nand_2_out, nand_3_out, nand_4_out, nand_5_out, not_1_out, not_2_out, not_3_out,
       not_4_out, not_5_out;

  not not_1 (not_1_out, S_2_0[1]);
  nand nand_1 (nand_1_out, V_2_0[1], not_1_out);
  not not_2 (not_2_out, V_2_0[0]);
  not not_3 (not_3_out, S_2_0[2]);
  nand nand_2 (nand_2_out, V_2_0[2], not_3_out);
  not not_4 (not_4_out, V_2_0[1]);
  not not_5 (not_5_out, V_2_0[2]);
  nand nand_3 (nand_3_out, nand_1_out, S_2_0[0], not_2_out, nand_2_out);
  nand nand_4 (nand_4_out, nand_2_out, not_4_out, S_2_0[1]);
  nand nand_5 (nand_5_out, not_5_out, S_2_0[2]);
  nor nor_1 (VGES, ~nand_3_out, ~nand_4_out, ~nand_5_out);  // NOR_Gate

  // Notes on the sheet:
  //   Page 88 - CGA_INTR_CNTLR_VECGEN_CMP
  //   S1
  //   V1
  //   S0
  //   V0
  //   V2
  //   S2
  //   V1
  //   S1
  //   V2
  //   S2
endmodule

module CGA_INTR_CNTLR_VECGEN_OSMUX (
  input  HIGSN,
  input  [2:0] HISTAT_2_0,
  input  [2:0] LOSTAT_2_0,
  input  LOGSN,
  input  OESN,
  output [2:0] PICS_2_0
);

  wire and_1_out, and_2_out, nand_1_out, nand_2_out, nand_3_out, nand_4_out, nand_5_out, nand_6_out;

  and and_1 (and_1_out, ~HIGSN, ~OESN);  // AND_Gate
  and and_2 (and_2_out, ~OESN, ~LOGSN);  // AND_Gate
  nand nand_1 (nand_1_out, and_1_out, HISTAT_2_0[2]);
  nand nand_2 (nand_2_out, and_2_out, LOSTAT_2_0[2]);
  or or_1 (PICS_2_0[2], ~nand_1_out, ~nand_2_out);  // OR_Gate
  nand nand_3 (nand_3_out, and_1_out, HISTAT_2_0[1]);
  nand nand_4 (nand_4_out, and_2_out, LOSTAT_2_0[1]);
  or or_2 (PICS_2_0[1], ~nand_3_out, ~nand_4_out);  // OR_Gate
  nand nand_5 (nand_5_out, and_1_out, HISTAT_2_0[0]);
  nand nand_6 (nand_6_out, and_2_out, LOSTAT_2_0[0]);
  or or_3 (PICS_2_0[0], ~nand_5_out, ~nand_6_out);  // OR_Gate

  // Notes on the sheet:
  //   HI
  //   Page 89 - CGA_INTR_CNTLR_VECGEN_OSMUX
  //   LO
  //   PICS2
  //   PICS1
  //   PICS0
endmodule

module CGA_INTR_CNTLR_IRGEL (
  input  FIDB03,
  input  HIDET,
  input  HIVGES,
  input  E,
  input  MCLK,
  input  D,
  input  S,
  input  H,
  input  [2:0] HIVEC_2_0,
  input  [2:0] LOVEC_2_0,
  input  LODET,
  input  LOVGES,
  input  N,
  input  L,
  input  FIDB04,
  input  M,
  output HIGSN,
  output PD,
  output HIPASSALL,
  output [2:0] PICV_2_0,
  output IRQN,
  output LOPASSALL,
  output LOGSN
);

  wire HIRL_hienabn, HIRL_higas, HIRL_hirq, HIRL_hve, HIRL_rdn, LORL_lienabn, LORL_lirq, LORL_logas,
       LORL_logasn, LORL_lve;

  CGA_INTR_CNTLR_IRGEL_HIRL HIRL (
    .HIGSN(HIGSN), .HIDET(HIDET), .HIVGES(HIVGES), .E(E), .MCLK(MCLK), .D(D), .S(S), .HIVEC_2_0(HIVEC_2_0),
    .H(H), .RDN(HIRL_rdn), .PD(PD), .HIPASSALL(HIPASSALL), .HIRQ(HIRL_hirq), .HVE(HIRL_hve),
    .HIGAS(HIRL_higas), .HIENABN(HIRL_hienabn));
  CGA_INTR_CNTLR_IRGEL_LORL LORL (
    .RDN(HIRL_rdn), .LODET(LODET), .LOVGES(LOVGES), .E(E), .MCLK(MCLK), .D(D), .S(S), .LOVEC_2_0(LOVEC_2_0),
    .LIENABN(LORL_lienabn), .LOPASSALL(LOPASSALL), .LIRQ(LORL_lirq), .LVE(LORL_lve), .LOGAS(LORL_logas),
    .LOGASN(LORL_logasn));
  CGA_INTR_CNTLR_IRGEL_HIGEL HIGEL (
    .FIDB03(FIDB03), .LOGASN(LORL_logasn), .HIDET(HIDET), .HIGAS(HIRL_higas), .HIENABN(HIRL_hienabn),
    .MCLK(MCLK), .N(N), .L(L), .M(M), .HIGSN(HIGSN));
  CGA_INTR_CNTLR_IRGEL_VMUX VMUX (
    .HIVEC_2_0(HIVEC_2_0), .LOVEC_2_0(LOVEC_2_0), .LVE(LORL_lve), .HVE(HIRL_hve), .PICV_2_0(PICV_2_0));
  CGA_INTR_CNTLR_IRGEL_LOGEL LOGEL (
    .FIDB04(FIDB04), .LOGAS(LORL_logas), .LIENABN(LORL_lienabn), .MCLK(MCLK), .N(N), .L(L), .M(M),
    .LOGSN(LOGSN));
  nor nor_1 (IRQN, HIRL_hirq, LORL_lirq);

  // Notes on the sheet:
  //   Page 90 - CGA_INTR_CNTLR_IRGEL
endmodule

module CGA_INTR_CNTLR_IRGEL_HIRL (
  input  HIGSN,
  input  HIDET,
  input  HIVGES,
  input  E,
  input  MCLK,
  input  D,
  input  S,
  input  [2:0] HIVEC_2_0,
  input  H,
  output RDN,
  output PD,
  output HIPASSALL,
  output HIRQ,
  output HVE,
  output HIGAS,
  output HIENABN
);

  wire HIDISN, INT_REQ_ENABLE_FF_q, INT_REQ_ENABLE_FF_qn, nand_1_out, nand_2_out, nand_3_out;

  nand nand_1 (nand_1_out, HIDET, HIVGES);
  nand nand_2 (nand_2_out, HIVGES, HIDET, HIDISN);
  nor nor_1 (RDN, ~HIDISN, ~HIGSN, ~nand_1_out);  // NOR_Gate
  or or_1 (PD, ~HIGSN, ~nand_1_out);  // OR_Gate
  SCAN_FF INT_REQ_ENABLE_FF (
    .D(E), .TE(D), .TI(INT_REQ_ENABLE_FF_q), .CLK(MCLK), .Q(INT_REQ_ENABLE_FF_q), .QN(INT_REQ_ENABLE_FF_qn));
  not not_1 (HIPASSALL, nand_2_out);
  and and_1 (HIRQ, ~nand_2_out, ~INT_REQ_ENABLE_FF_qn);  // AND_Gate
  and and_2 (HVE, ~nand_2_out, ~S);  // AND_Gate
  nand nand_3 (nand_3_out, HVE, HIVEC_2_0[2], HIVEC_2_0[1], HIVEC_2_0[0]);
  not not_2 (HIGAS, nand_3_out);
  SCAN_FF STATUS_OVERFLOW_FF (.D(HIDISN), .TE(H), .TI(nand_3_out), .CLK(MCLK), .Q(HIDISN), .QN(HIENABN));

  // Notes on the sheet:
  //   Page 91 - CGA_INTR_CNTLR_IRGEL_HIGEL
endmodule

module CGA_INTR_CNTLR_IRGEL_LORL (
  input  RDN,
  input  LODET,
  input  LOVGES,
  input  E,
  input  MCLK,
  input  D,
  input  S,
  input  [2:0] LOVEC_2_0,
  output LIENABN,
  output LOPASSALL,
  output LIRQ,
  output LVE,
  output LOGAS,
  output LOGASN
);

  wire INT_REQ_ENABLE_FF_q, INT_REQ_ENABLE_FF_qn, nand_1_out;

  nand nand_1 (nand_1_out, RDN, LODET, LOVGES);
  SCAN_FF INT_REQ_ENABLE_FF (
    .D(E), .TE(D), .TI(INT_REQ_ENABLE_FF_q), .CLK(MCLK), .Q(INT_REQ_ENABLE_FF_q), .QN(INT_REQ_ENABLE_FF_qn));
  and and_1 (LIRQ, ~nand_1_out, ~INT_REQ_ENABLE_FF_qn);  // AND_Gate
  and and_2 (LVE, ~nand_1_out, ~S);  // AND_Gate
  not not_1 (LIENABN, RDN);
  not not_2 (LOPASSALL, nand_1_out);
  nand nand_2 (LOGASN, LVE, LOVEC_2_0[2], LOVEC_2_0[1], LOVEC_2_0[0]);
  not not_3 (LOGAS, LOGASN);

  // Notes on the sheet:
  //   Page 92 - CGA_INTR_CNTLR_IRGEL_LOGEL  
endmodule

module CGA_INTR_CNTLR_IRGEL_HIGEL (
  input  FIDB03,
  input  LOGASN,
  input  HIDET,
  input  HIGAS,
  input  HIENABN,
  input  MCLK,
  input  N,
  input  L,
  input  M,
  output HIGSN
);

  wire nand_1_out, nand_2_out, nand_3_out, nand_4_out, nand_5_out, nand_6_out, not_1_out, not_2_out,
       not_3_out, or_1_out;

  not not_1 (not_1_out, HIDET);
  not not_2 (not_2_out, L);
  not not_3 (not_3_out, M);
  nand nand_1 (nand_1_out, FIDB03, L, M);
  nand nand_2 (nand_2_out, LOGASN, L, not_3_out);
  nand nand_3 (nand_3_out, LOGASN, not_1_out, N);
  nand nand_4 (nand_4_out, HIGAS, N);
  nand nand_5 (nand_5_out, HIENABN, N);
  nand nand_6 (nand_6_out, not_2_out, M, HIGSN);
  or or_1 (or_1_out, ~nand_1_out, ~nand_2_out, ~nand_3_out, ~nand_4_out, ~nand_5_out, ~nand_6_out);  // OR_Gate
  D_Flip_Flop d_ff_1 (.D(or_1_out), .clk(MCLK), .Q(HIGSN));  // open: Qn, preset, reset

  // Notes on the sheet:
  //   Page 93 - CGA_INTR_CNTLR_IRGEL_LOGEL  
endmodule

module CGA_INTR_CNTLR_IRGEL_LOGEL (
  input  FIDB04,
  input  LOGAS,
  input  LIENABN,
  input  MCLK,
  input  N,
  input  L,
  input  M,
  output LOGSN
);

  wire nand_1_out, nand_2_out, nand_3_out, nand_4_out, not_1_out, or_1_out;

  not not_1 (not_1_out, L);
  nand nand_1 (nand_1_out, FIDB04, L, M);
  nand nand_2 (nand_2_out, LOGAS, N);
  nand nand_3 (nand_3_out, LIENABN, N);
  nand nand_4 (nand_4_out, not_1_out, M, LOGSN);
  or or_1 (or_1_out, ~nand_1_out, ~nand_2_out, ~nand_3_out, ~nand_4_out);  // OR_Gate
  D_Flip_Flop d_ff_1 (.D(or_1_out), .clk(MCLK), .Q(LOGSN));  // open: Qn, preset, reset

  // Notes on the sheet:
  //   Page 94 - CGA_INTR_CNTLR_IRGEL_LOGEL  
endmodule

module CGA_INTR_CNTLR_IRGEL_VMUX (
  input  [2:0] HIVEC_2_0,
  input  [2:0] LOVEC_2_0,
  input  LVE,
  input  HVE,
  output [2:0] PICV_2_0
);

  wire nand_1_out, nand_2_out, nand_3_out, nand_4_out, nand_5_out, nand_6_out;

  nand nand_1 (nand_1_out, HIVEC_2_0[2], HVE);
  nand nand_2 (nand_2_out, LOVEC_2_0[2], LVE);
  or or_1 (PICV_2_0[2], ~nand_1_out, ~nand_2_out);  // OR_Gate
  nand nand_3 (nand_3_out, HIVEC_2_0[1], HVE);
  nand nand_4 (nand_4_out, LOVEC_2_0[1], LVE);
  or or_2 (PICV_2_0[1], ~nand_3_out, ~nand_4_out);  // OR_Gate
  nand nand_5 (nand_5_out, HIVEC_2_0[0], HVE);
  nand nand_6 (nand_6_out, LOVEC_2_0[0], LVE);
  or or_3 (PICV_2_0[0], ~nand_5_out, ~nand_6_out);  // OR_Gate

  // Notes on the sheet:
  //   Page 95 - CGA_INTR_CNTLR_IRGEL_VMUX 
  //   PICV2
  //   PICV1
  //   PICV0
endmodule

module CGA_INTR_CNTLR_MDCD (
  input  [3:0] LAA_3_0,
  input  EPIC,
  input  HIPASSALL,
  input  LOPASSALL,
  input  MCLK,
  output OESN,
  output E,
  output J,
  output D,
  output N,
  output HIK,
  output A,
  output HIF,
  output G,
  output H,
  output L,
  output B,
  output S,
  output M,
  output LOF,
  output C,
  output LOK,
  output OEM,
  output EPICMASKN
);

  wire and_1_out, and_2_out, and_3_out, and_4_out, and_5_out, and_6_out, and_7_out, and_8_out, and_9_out,
       d_ff_1_q, d_ff_2_q, GLP_HI_z0, GLP_HI_z1, GLP_HI_z2, GLP_HI_z3, GLP_HI_z4, GLP_HI_z5, GLP_HI_z6,
       GLP_HI_z7, GLP_LO_z0, GLP_LO_z1, GLP_LO_z2, GLP_LO_z3, GLP_LO_z4, GLP_LO_z5, GLP_LO_z6, GLP_LO_z7,
       HIVCEN, LOVCEN, nand_1_out, nand_5_out, nand_6_out, nand_7_out, nand_8_out, nand_9_out, nand_11_out,
       nor_1_out, nor_2_out, nor_3_out, nor_4_out, not_1_out, not_2_out, not_3_out, not_4_out, not_15_out,
       or_1_out, or_2_out, or_3_out, or_4_out, or_5_out, or_6_out, or_7_out, or_8_out, or_9_out, or_10_out,
       or_11_out, or_12_out, or_13_out, R;

  not not_1 (not_1_out, EPIC);
  not not_2 (not_2_out, HIPASSALL);
  not not_3 (not_3_out, LOPASSALL);
  not not_4 (not_4_out, LAA_3_0[3]);
  ND38GLP GLP_LO (
    .A(LAA_3_0[0]), .B(LAA_3_0[1]), .C(LAA_3_0[2]), .G(not_4_out), .Z0(GLP_LO_z0), .Z1(GLP_LO_z1),
    .Z2(GLP_LO_z2), .Z3(GLP_LO_z3), .Z4(GLP_LO_z4), .Z5(GLP_LO_z5), .Z6(GLP_LO_z6), .Z7(GLP_LO_z7));
  ND38GLP GLP_HI (
    .A(LAA_3_0[0]), .B(LAA_3_0[1]), .C(LAA_3_0[2]), .G(LAA_3_0[3]), .Z0(GLP_HI_z0), .Z1(GLP_HI_z1),
    .Z2(GLP_HI_z2), .Z3(GLP_HI_z3), .Z4(GLP_HI_z4), .Z5(GLP_HI_z5), .Z6(GLP_HI_z6), .Z7(GLP_HI_z7));
  or or_1 (or_1_out, ~GLP_LO_z0, ~GLP_HI_z0, ~GLP_HI_z2, ~GLP_HI_z4, ~GLP_HI_z6);  // OR_Gate
  or or_2 (or_2_out, ~GLP_HI_z6, ~GLP_HI_z3, ~GLP_HI_z2);  // OR_Gate
  or or_3 (or_3_out, ~GLP_HI_z0, ~GLP_HI_z2);  // OR_Gate
  or or_4 (or_4_out, ~GLP_LO_z3, ~GLP_LO_z7);  // OR_Gate
  and and_1 (and_1_out, or_1_out, EPIC);
  nand nand_1 (nand_1_out, or_2_out, EPIC);
  nand nand_2 (C, or_3_out, EPIC);
  nand nand_3 (EPICMASKN, or_4_out, EPIC);
  not not_5 (A, and_1_out);
  not not_6 (B, nand_1_out);
  not not_7 (OEM, EPICMASKN);
  nand nand_4 (OESN, ~GLP_LO_z6, ~not_1_out);  // NAND_Gate
  and and_2 (and_2_out, ~GLP_LO_z5, ~not_2_out, ~not_1_out);  // AND_Gate
  and and_3 (and_3_out, ~GLP_HI_z1, ~not_1_out);  // AND_Gate
  and and_4 (and_4_out, ~GLP_LO_z5, ~not_3_out, ~not_1_out);  // AND_Gate
  nand nand_5 (nand_5_out, d_ff_1_q, R);
  nand nand_6 (nand_6_out, LOPASSALL, N);
  nor nor_1 (nor_1_out, and_2_out, and_3_out);
  not not_8 (HIF, nor_1_out);
  nor nor_2 (nor_2_out, and_3_out, and_4_out);
  not not_9 (LOF, nor_2_out);
  nand nand_7 (nand_7_out, d_ff_2_q, R);
  nand nand_8 (nand_8_out, HIPASSALL, N);
  or or_5 (or_5_out, ~nand_5_out, ~nand_6_out);  // OR_Gate
  or or_6 (or_6_out, ~nand_7_out, ~nand_8_out);  // OR_Gate
  D_Flip_Flop d_ff_1 (.D(or_5_out), .clk(MCLK), .Q(d_ff_1_q), .Qn(LOVCEN));  // open: preset, reset
  D_Flip_Flop d_ff_2 (.D(or_6_out), .clk(MCLK), .Q(d_ff_2_q), .Qn(HIVCEN));  // open: preset, reset
  or or_7 (or_7_out, ~GLP_LO_z0, ~GLP_LO_z5);  // OR_Gate
  or or_8 (or_8_out, ~GLP_LO_z0, ~GLP_HI_z1);  // OR_Gate
  or or_9 (or_9_out, ~GLP_LO_z0, ~GLP_LO_z5);  // OR_Gate
  and and_5 (and_5_out, or_7_out, EPIC);
  nand nand_9 (nand_9_out, or_8_out, EPIC);
  nand nand_10 (M, or_9_out, EPIC);
  not not_10 (G, and_5_out);
  not not_11 (L, nand_9_out);
  or or_10 (or_10_out, ~GLP_LO_z0, ~GLP_LO_z1, ~GLP_LO_z2, ~GLP_LO_z3);  // OR_Gate
  nand nand_11 (nand_11_out, or_10_out, EPIC);
  not not_12 (J, nand_11_out);
  and and_6 (and_6_out, ~GLP_LO_z4, ~not_1_out, ~HIVCEN);  // AND_Gate
  and and_7 (and_7_out, ~GLP_LO_z0, ~not_1_out);  // AND_Gate
  and and_8 (and_8_out, ~GLP_LO_z1, ~not_1_out);  // AND_Gate
  and and_9 (and_9_out, ~GLP_LO_z4, ~not_1_out, ~LOVCEN);  // AND_Gate
  nor nor_3 (nor_3_out, and_6_out, and_7_out, and_8_out);
  nor nor_4 (nor_4_out, and_8_out, and_7_out, and_9_out);
  not not_13 (HIK, nor_3_out);
  not not_14 (LOK, nor_4_out);
  or or_11 (or_11_out, ~GLP_LO_z0, ~GLP_HI_z5, ~GLP_HI_z7);  // OR_Gate
  nand nand_12 (D, or_11_out, EPIC);
  nand nand_13 (S, ~GLP_LO_z5, ~not_1_out);  // NAND_Gate
  not not_15 (not_15_out, GLP_HI_z5);
  not not_16 (N, S);
  not not_17 (E, not_15_out);
  or or_12 (or_12_out, ~GLP_LO_z0, ~GLP_LO_z1, ~GLP_LO_z4, ~GLP_LO_z5);  // OR_Gate
  or or_13 (or_13_out, ~GLP_LO_z0, ~GLP_LO_z5, ~GLP_HI_z1);  // OR_Gate
  nand nand_14 (R, or_12_out, EPIC);
  and and_10 (H, or_13_out, EPIC);

  // Notes on the sheet:
  //   EPICN
  //   HIPASSALLN
  //   LOPASSALLN
  //   Page 96 - CGA_INTR_CNTLR_MDCD
  //   D0N
  //   D1N
  //   D2N
  //   D3N
  //   D4N
  //   D5N
  //   D6N
  //   D7N
  //   D8N
  //   D9N
  //   D10N
  //   D11N
  //   D12N
  //   D13N
  //   D14N
  //   D15N
  //   D6N
  //   D5N
  //   EPICN
  //   VECTOR CLEAR ENABLE FLIP-FLOPS
  //   D9N
  //   D5N
  //   D0N
  //   D5N
  //   D0N
  //   D9N
  //   D0N
  //   D5N
  //   D0N-D3N
  //   D4N
  //   D0N
  //   D1N
  //   D4N
  //   D13N
  //   D15N
  //   D0N
  //   D5N
  //   D13N
  //   D1N
  //   D4N
  //   D5N
  //   D0N
  //   D9N
endmodule
