// Logisim project CGA_MAC_.circ as structural Verilog: 15 circuits, main circuit CGA_MAC_DECODE
module CGA_MAC (
  input  MCLK,
  input  PTM,
  input  [15:0] FIDBO_15_0,
  input  PONI,
  input  [1:0] CMIS_1_0,
  input  [4:0] CSCOMM_4_0,
  input  WR3,
  input  WR7,
  input  ILCSN,
  input  DOUBLE,
  input  CSMREQ,
  input  [15:0] CD_15_0,
  input  [15:0] RB_15_0,
  input  [15:0] XR_15_0,
  input  [15:0] BR_15_0,
  input  [15:0] PR_15_0,
  output VEX,
  output [15:0] PCR_15_7_2_0,
  output [13:0] LA_23_10,
  output LSHADOW,
  output ECCR,
  output [9:0] MCA_9_0,
  output [15:0] NLCA_15_0
);

  wire MAC_DECODE_addsel, MAC_DECODE_cds, MAC_DECODE_cdsel, MAC_DECODE_exmn, MAC_DECODE_hold,
       MAC_DECODE_lldexm, MAC_DECODE_lldpcr, MAC_DECODE_lldseg, MAC_DECODE_nlcasel, MAC_DECODE_pb,
       MAC_DECODE_plca, MAC_DECODE_prb, MAC_DECODE_psel, MAC_DECODE_px, MAC_DECODE_sapt, MAC_DECODE_sptn,
       MAC_LA1025_eccrhin, MAC_LASEL_a10, MAC_LASEL_a1617, MAC_LASEL_a1619, MAC_LASEL_a1819, MAC_LASEL_b1819,
       MAC_LASEL_b1821, MAC_LASEL_bb10, MAC_LASEL_c10, MAC_LASEL_d1617, MAC_LASEL_e1617, MAC_LASEL_f1617,
       MAC_PTSEL_selptn, MAC_SEGPT_pex, MAC_SEGPT_segzn, not_1_out, not_2_out;
  wire [1:0] MAC_SEGPT_xpt_1_0;
  wire [7:0] MAC_SEGPT_seg_7_0;
  wire [15:0] MAC_ADD_add_15_0, MAC_AP09_ica_15_0, MAC_AP09_lca_15_0, MAC_SEGPT_pcr_14_13_10_9_n;

  not not_1 (not_1_out, ILCSN);
  not not_2 (not_2_out, not_1_out);
  CGA_MAC_DECODE MAC_DECODE (
    .LCSN(not_2_out), .CSCOMM_4_0(CSCOMM_4_0), .CSMIS_1_0(CMIS_1_0), .WR3(WR3), .MCLK(MCLK), .WR7(WR7),
    .EXMN(MAC_DECODE_exmn), .PB(MAC_DECODE_pb), .PX(MAC_DECODE_px), .PRB(MAC_DECODE_prb),
    .PLCA(MAC_DECODE_plca), .CDSEL(MAC_DECODE_cdsel), .LLDEXM(MAC_DECODE_lldexm), .LLDSEG(MAC_DECODE_lldseg),
    .LLDPCR(MAC_DECODE_lldpcr), .NLCASEL(MAC_DECODE_nlcasel), .ADDSEL(MAC_DECODE_addsel),
    .CDS(MAC_DECODE_cds), .SPTN(MAC_DECODE_sptn), .SAPT(MAC_DECODE_sapt), .PSEL(MAC_DECODE_psel),
    .HOLD(MAC_DECODE_hold));
  CGA_MAC_ADD MAC_ADD (
    .CD_15_0(CD_15_0), .CDS(MAC_DECODE_cds), .PRB(MAC_DECODE_prb), .PB(MAC_DECODE_pb), .PX(MAC_DECODE_px),
    .PLCA(MAC_DECODE_plca), .RB_15_0(RB_15_0), .BR_15_0(BR_15_0), .XR_15_0(XR_15_0),
    .LCA_15_0(MAC_AP09_lca_15_0), .ADD_15_0(MAC_ADD_add_15_0));
  // Probe on MAC_ADD_add_15_0
  CGA_MAC_AP09 MAC_AP09 (
    .PSEL(MAC_DECODE_psel), .ADDSEL(MAC_DECODE_addsel), .CDSEL(MAC_DECODE_cdsel),
    .NLCASEL(MAC_DECODE_nlcasel), .HOLD(MAC_DECODE_hold), .PR_15_0(PR_15_0), .ADD_15_0(MAC_ADD_add_15_0),
    .CD_15_0(CD_15_0), .ECCRHIN(MAC_LA1025_eccrhin), .MCLK(MCLK), .ICA_15_0(MAC_AP09_ica_15_0), .ECCR(ECCR),
    .MCA_9_0(MCA_9_0), .LCA_15_0(MAC_AP09_lca_15_0), .NLCA_15_0(NLCA_15_0));
  // Probe on FIDBO_15_0
  CGA_MAC_SEGPT MAC_SEGPT (
    .FIDBO_15_0(FIDBO_15_0), .MCLK(MCLK), .LLDSEG(MAC_DECODE_lldseg), .LLDPCR(MAC_DECODE_lldpcr),
    .LLDEXM(MAC_DECODE_lldexm), .EXMN(MAC_DECODE_exmn), .SEG_7_0(MAC_SEGPT_seg_7_0), .SEGZN(MAC_SEGPT_segzn),
    .PCR_15_7_2_0(PCR_15_7_2_0), .PCR_14_13_10_9_N(MAC_SEGPT_pcr_14_13_10_9_n), .XPT_1_0(MAC_SEGPT_xpt_1_0),
    .VEX(VEX), .PEX(MAC_SEGPT_pex));
  CGA_MAC_PTSEL MAC_PTSEL (
    .SPTN(MAC_DECODE_sptn), .SAPT(MAC_DECODE_sapt), .PONI(PONI), .PTM(PTM), .MCLK(MCLK),
    .SELPTN(MAC_PTSEL_selptn));
  // Probe on MAC_SEGPT_seg_7_0
  // Probe on MAC_SEGPT_xpt_1_0
  // Probe on PCR_15_7_2_0
  CGA_MAC_LASEL MAC_LASEL (
    .DOUBLE(DOUBLE), .PCR_15_7_2_0(PCR_15_7_2_0), .ICA_15_8(MAC_AP09_ica_15_0), .CSMREQ(CSMREQ), .VEX(VEX),
    .PONI(PONI), .PEX(MAC_SEGPT_pex), .SEGZN(MAC_SEGPT_segzn), .EXMN(MAC_DECODE_exmn),
    .SELPTN(MAC_PTSEL_selptn), .MCLK(MCLK), .A10(MAC_LASEL_a10), .BB10(MAC_LASEL_bb10), .C10(MAC_LASEL_c10),
    .A1617(MAC_LASEL_a1617), .D1617(MAC_LASEL_d1617), .E1617(MAC_LASEL_e1617), .F1617(MAC_LASEL_f1617),
    .A1819(MAC_LASEL_a1819), .B1821(MAC_LASEL_b1821), .B1819(MAC_LASEL_b1819), .A1619(MAC_LASEL_a1619),
    .LSHADOW(LSHADOW));
  // Probe on MAC_SEGPT_pcr_14_13_10_9_n
  // Probe on MAC_AP09_ica_15_0
  CGA_MAC_LA1025 MAC_LA1025 (
    .ICA_15_0(MAC_AP09_ica_15_0), .A10(MAC_LASEL_a10), .BB10(MAC_LASEL_bb10), .C10(MAC_LASEL_c10),
    .A1617(MAC_LASEL_a1617), .D1617(MAC_LASEL_d1617), .E1617(MAC_LASEL_e1617), .F1617(MAC_LASEL_f1617),
    .A1819(MAC_LASEL_a1819), .B1821(MAC_LASEL_b1821), .B1819(MAC_LASEL_b1819), .A1619(MAC_LASEL_a1619),
    .SEG_7_0(MAC_SEGPT_seg_7_0), .PCR_15_0(PCR_15_7_2_0), .PCR_15_0_N(MAC_SEGPT_pcr_14_13_10_9_n),
    .XPT_1_0(MAC_SEGPT_xpt_1_0), .MCLK(MCLK), .ECCRHIN(MAC_LA1025_eccrhin), .LA_23_10(LA_23_10));

  // Notes on the sheet:
  //   Page 24 - CGA_MAC
endmodule

module CGA_MAC_DECODE (
  input  LCSN,
  input  [4:0] CSCOMM_4_0,
  input  [1:0] CSMIS_1_0,
  input  WR3,
  input  MCLK,
  input  WR7,
  output EXMN,
  output PB,
  output PX,
  output PRB,
  output PLCA,
  output CDSEL,
  output LLDEXM,
  output LLDSEG,
  output LLDPCR,
  output NLCASEL,
  output ADDSEL,
  output CDS,
  output SPTN,
  output SAPT,
  output PSEL,
  output HOLD
);

  wire LDEXMN, LDPCRN, LDSEGN, nand_1_out, nand_3_out, nand_4_out, nand_6_out, nand_7_out, nand_8_out,
       nand_9_out, nand_10_out, nand_11_out, nand_12_out, nand_13_out, nand_14_out, nand_15_out, nand_16_out,
       nand_18_out, nand_19_out, nand_20_out, nand_21_out, nand_22_out, nand_23_out, nand_24_out,
       nand_25_out, nand_26_out, nand_27_out, nand_28_out, nand_29_out, nand_30_out, nand_31_out,
       nand_32_out, nand_33_out, nand_34_out, nand_35_out, nand_36_out, nand_37_out, nand_38_out,
       nand_39_out, nand_40_out, nand_41_out, nand_42_out, nand_43_out, nand_45_out, nand_46_out,
       nand_47_out, nand_48_out, nand_49_out, nand_50_out, nand_51_out, nand_52_out, nand_53_out,
       nand_54_out, nor_1_out, nor_2_out, nor_3_out, not_3_out, not_4_out, not_5_out, not_6_out, not_7_out,
       not_8_out, not_9_out, not_10_out, not_11_out, not_12_out, not_13_out, not_14_out, not_15_out,
       not_16_out, WR3N, WR7N;

  not not_1 (WR3N, WR3);
  not not_2 (WR7N, WR7);
  not not_3 (not_3_out, CSCOMM_4_0[0]);
  not not_4 (not_4_out, CSCOMM_4_0[1]);
  not not_5 (not_5_out, CSCOMM_4_0[2]);
  not not_6 (not_6_out, CSCOMM_4_0[3]);
  not not_7 (not_7_out, CSCOMM_4_0[4]);
  not not_8 (not_8_out, CSMIS_1_0[0]);
  not not_9 (not_9_out, CSMIS_1_0[1]);
  not not_10 (not_10_out, not_3_out);
  not not_11 (not_11_out, not_4_out);
  not not_12 (not_12_out, not_5_out);
  not not_13 (not_13_out, not_6_out);
  not not_14 (not_14_out, not_7_out);
  not not_15 (not_15_out, not_8_out);
  not not_16 (not_16_out, not_9_out);
  nand nand_1 (nand_1_out, not_6_out, not_5_out, not_4_out);
  nand nand_2 (LDPCRN, LCSN, not_7_out, not_6_out, not_12_out, not_11_out, not_3_out, not_16_out, not_15_out);
  nand nand_3 (nand_3_out, not_13_out, not_12_out, not_11_out);
  nand nand_4 (nand_4_out, not_5_out, not_9_out, not_15_out);
  nand nand_5 (SPTN, nand_1_out, nand_3_out, not_14_out, nand_4_out, nand_7_out, nand_8_out, nand_9_out, nand_10_out);
  nand nand_6 (nand_6_out, WR3N, not_15_out, not_9_out, not_3_out);
  nand nand_7 (nand_7_out, not_5_out, not_10_out, not_16_out, not_8_out);
  not not_17 (PB, nand_6_out);
  nand nand_8 (nand_8_out, not_13_out, not_16_out);
  nand nand_9 (nand_9_out, not_13_out, not_5_out, not_10_out);
  nand nand_10 (nand_10_out, not_13_out, not_9_out, not_15_out);
  nand nand_11 (nand_11_out, not_6_out, not_5_out, not_10_out);
  nand nand_12 (nand_12_out, not_3_out, not_9_out);
  nand nand_13 (nand_13_out, WR7N, not_15_out, nand_11_out, nand_12_out);
  nand nand_14 (nand_14_out, not_15_out, not_14_out, not_9_out, not_3_out, not_11_out, not_5_out);
  not not_18 (PX, nand_13_out);
  nand nand_15 (nand_15_out, not_15_out, not_14_out, not_9_out, not_4_out, not_12_out, not_13_out);
  nand nand_16 (nand_16_out, not_9_out, not_10_out, not_5_out, not_13_out, not_14_out);
  nand nand_17 (SAPT, nand_14_out, nand_15_out, nand_16_out, nand_19_out, nand_21_out);
  nand nand_18 (nand_18_out, nand_11_out, nand_12_out, WR7, not_15_out);
  nor nor_1 (nor_1_out, ~nand_18_out, ~nand_20_out, ~nand_22_out, ~nand_23_out);  // NOR_Gate
  nand nand_19 (nand_19_out, not_16_out, not_3_out, not_5_out, not_13_out, not_14_out);
  nand nand_20 (nand_20_out, WR3, not_15_out, not_9_out, not_3_out);
  not not_19 (PRB, nor_1_out);
  nand nand_21 (nand_21_out, not_15_out, not_3_out, not_5_out, not_13_out, not_14_out);
  nand nand_22 (nand_22_out, not_10_out, not_12_out, not_8_out);
  nand nand_23 (nand_23_out, not_10_out, not_13_out, not_8_out);
  nand nand_24 (nand_24_out, not_6_out, not_4_out);
  nand nand_25 (nand_25_out, not_8_out, not_16_out, not_3_out, not_11_out, not_12_out, not_14_out);
  nand nand_26 (nand_26_out, not_13_out, not_12_out);
  nand nand_27 (nand_27_out, not_8_out, not_16_out, not_3_out, not_13_out, not_14_out);
  nand nand_28 (nand_28_out, not_6_out, not_5_out, not_16_out, not_3_out);
  nor nor_2 (nor_2_out, ~nand_25_out, ~nand_27_out, ~nand_29_out, ~nand_32_out);  // NOR_Gate
  nand nand_29 (nand_29_out, not_14_out, not_4_out, not_5_out, not_6_out);
  not not_20 (CDSEL, nor_2_out);
  nand nand_30 (nand_30_out, not_8_out, not_12_out, not_11_out, not_16_out);
  nand nand_31 (nand_31_out, nand_24_out, not_14_out, nand_26_out, nand_28_out, nand_30_out, nand_33_out, nand_34_out, nand_35_out);
  nand nand_32 (nand_32_out, not_14_out, not_12_out, not_13_out);
  nand nand_33 (nand_33_out, not_13_out, not_3_out, not_16_out, not_8_out);
  not not_21 (ADDSEL, nand_31_out);
  nand nand_34 (nand_34_out, not_13_out, not_10_out, not_16_out);
  nand nand_35 (nand_35_out, not_12_out, not_11_out, not_10_out, not_16_out);
  nand nand_36 (nand_36_out, not_13_out, not_10_out, not_5_out, not_16_out, not_14_out, nand_37_out);
  not not_22 (NLCASEL, nand_36_out);
  nand nand_37 (nand_37_out, not_16_out, not_8_out, not_11_out);
  nand nand_38 (nand_38_out, not_16_out, not_15_out);
  nand nand_39 (nand_39_out, not_5_out, not_11_out, not_16_out, nand_38_out, nand_40_out, nand_41_out);
  nor nor_3 (nor_3_out, ~not_14_out, ~nand_39_out);  // NOR_Gate
  not not_23 (HOLD, nor_3_out);
  nand nand_40 (nand_40_out, not_6_out, not_10_out, not_16_out);
  nand nand_41 (nand_41_out, not_13_out, not_3_out, not_16_out);
  nand nand_42 (nand_42_out, not_15_out, not_10_out, not_13_out);
  nand nand_43 (nand_43_out, not_15_out, not_10_out, not_12_out, not_6_out);
  nor nor_4 (CDS, ~nand_42_out, ~nand_43_out);  // NOR_Gate
  nand nand_44 (EXMN, not_15_out, not_16_out, not_4_out, not_12_out, not_13_out, not_14_out);
  nand nand_45 (nand_45_out, not_15_out, not_3_out);
  nand nand_46 (nand_46_out, not_13_out, not_10_out);
  nand nand_47 (nand_47_out, nand_45_out, nand_46_out, nand_49_out);
  nand nand_48 (nand_48_out, not_5_out, not_4_out);
  nand nand_49 (nand_49_out, not_12_out, not_10_out);
  not not_24 (PLCA, nand_47_out);
  nand nand_50 (nand_50_out, not_5_out, not_11_out, not_10_out);
  nand nand_51 (nand_51_out, not_9_out, not_11_out);
  nand nand_52 (nand_52_out, not_5_out, not_16_out, not_8_out);
  nand nand_53 (nand_53_out, nand_48_out, nand_50_out, nand_51_out, not_6_out, nand_52_out, nand_54_out, not_14_out);
  nand nand_54 (nand_54_out, not_12_out, not_11_out, not_3_out);
  not not_25 (PSEL, nand_53_out);
  nand nand_55 (LDEXMN, LCSN, not_15_out, not_16_out, not_10_out, not_4_out, not_5_out, not_6_out, not_14_out);
  nand nand_56 (LDSEGN, LCSN, not_8_out, not_9_out, not_3_out, not_4_out, not_5_out, not_6_out, not_14_out);
  R41P DECODE_R41 (
    .A(LDEXMN), .B(LDSEGN), .C(LDPCRN), .CP(MCLK), .QAN(LLDEXM), .QBN(LLDSEG), .QCN(LLDPCR));  // open: D, QA, QB, QC, QD, QDN

  // Notes on the sheet:
  //   Page 25-28 - CGA_MAC_DECODE
  //   CSCOMM0
  //   CSCOMM1
  //   CSOMM2
  //   CSCOMM3
  //   CSCOMM4
  //   CSMIS0
  //   CSMIS1
  //   Page 25 ->
  //   Page 26 ->
  //   Page 27 ->
  //   Page 28 ->
endmodule

module CGA_MAC_ADD (
  input  [15:0] CD_15_0,
  input  CDS,
  input  PRB,
  input  PB,
  input  PX,
  input  PLCA,
  input  [15:0] RB_15_0,
  input  [15:0] BR_15_0,
  input  [15:0] XR_15_0,
  input  [15:0] LCA_15_0,
  output [15:0] ADD_15_0
);

  wire A02_1_z, A02_2_z, A02_3_z, A02_4_z, A02_5_z, A02_6_z, A02_7_z, A02_8_z, A02_9_z, A02_10_z, A02_11_z,
       A02_12_z, A02_13_z, A02_14_z, A02_15_z, A02_16_z, A02_17_z, A02_18_z, A02_19_z, A02_20_z, A02_21_z,
       A02_22_z, A02_23_z, A02_24_z, A02_25_z, A02_26_z, A02_27_z, A02_28_z, A02_29_z, A02_30_z, A02_31_z,
       A02_32_z, nand_1_out, nand_2_out, nand_3_out, nand_4_out, nand_5_out, nand_6_out, nand_7_out,
       nand_8_out, nand_9_out, nand_10_out, not_1_out;
  wire [7:0] nand_11_out;
  wire [15:0] or_1_out;

  A02 A02_16 (.A(XR_15_0[7]), .B(PX), .C(LCA_15_0[7]), .D(PLCA), .Z(A02_16_z));
  A02 A02_18 (.A(XR_15_0[8]), .B(PX), .C(LCA_15_0[8]), .D(PLCA), .Z(A02_18_z));
  A02 A02_20 (.A(XR_15_0[9]), .B(PX), .C(LCA_15_0[9]), .D(PLCA), .Z(A02_20_z));
  A02 A02_22 (.A(XR_15_0[10]), .B(PX), .C(LCA_15_0[10]), .D(PLCA), .Z(A02_22_z));
  A02 A02_24 (.A(XR_15_0[11]), .B(PX), .C(LCA_15_0[11]), .D(PLCA), .Z(A02_24_z));
  A02 A02_26 (.A(XR_15_0[12]), .B(PX), .C(LCA_15_0[12]), .D(PLCA), .Z(A02_26_z));
  A02 A02_28 (.A(XR_15_0[13]), .B(PX), .C(LCA_15_0[13]), .D(PLCA), .Z(A02_28_z));
  A02 A02_30 (.A(XR_15_0[14]), .B(PX), .C(LCA_15_0[14]), .D(PLCA), .Z(A02_30_z));
  A02 A02_32 (.A(XR_15_0[15]), .B(PX), .C(LCA_15_0[15]), .D(PLCA), .Z(A02_32_z));
  A02 A02_2 (.A(XR_15_0[0]), .B(PX), .C(LCA_15_0[0]), .D(PLCA), .Z(A02_2_z));
  A02 A02_4 (.A(XR_15_0[1]), .B(PX), .C(LCA_15_0[1]), .D(PLCA), .Z(A02_4_z));
  A02 A02_6 (.A(XR_15_0[2]), .B(PX), .C(LCA_15_0[2]), .D(PLCA), .Z(A02_6_z));
  A02 A02_8 (.A(XR_15_0[3]), .B(PX), .C(LCA_15_0[3]), .D(PLCA), .Z(A02_8_z));
  A02 A02_10 (.A(XR_15_0[4]), .B(PX), .C(LCA_15_0[4]), .D(PLCA), .Z(A02_10_z));
  A02 A02_12 (.A(XR_15_0[5]), .B(PX), .C(LCA_15_0[5]), .D(PLCA), .Z(A02_12_z));
  A02 A02_14 (.A(XR_15_0[6]), .B(PX), .C(LCA_15_0[6]), .D(PLCA), .Z(A02_14_z));
  A02 A02_11 (.A(RB_15_0[5]), .B(PRB), .C(BR_15_0[5]), .D(PB), .Z(A02_11_z));
  A02 A02_13 (.A(RB_15_0[6]), .B(PRB), .C(BR_15_0[6]), .D(PB), .Z(A02_13_z));
  A02 A02_15 (.A(RB_15_0[7]), .B(PRB), .C(BR_15_0[7]), .D(PB), .Z(A02_15_z));
  A02 A02_17 (.A(RB_15_0[8]), .B(PRB), .C(BR_15_0[8]), .D(PB), .Z(A02_17_z));
  A02 A02_19 (.A(RB_15_0[9]), .B(PRB), .C(BR_15_0[9]), .D(PB), .Z(A02_19_z));
  A02 A02_21 (.A(RB_15_0[10]), .B(PRB), .C(BR_15_0[10]), .D(PB), .Z(A02_21_z));
  A02 A02_23 (.A(RB_15_0[11]), .B(PRB), .C(BR_15_0[11]), .D(PB), .Z(A02_23_z));
  A02 A02_25 (.A(RB_15_0[12]), .B(PRB), .C(BR_15_0[12]), .D(PB), .Z(A02_25_z));
  A02 A02_27 (.A(RB_15_0[13]), .B(PRB), .C(BR_15_0[13]), .D(PB), .Z(A02_27_z));
  A02 A02_29 (.A(RB_15_0[14]), .B(PRB), .C(BR_15_0[14]), .D(PB), .Z(A02_29_z));
  A02 A02_31 (.A(RB_15_0[15]), .B(PRB), .C(BR_15_0[15]), .D(PB), .Z(A02_31_z));
  A02 A02_1 (.A(RB_15_0[0]), .B(PRB), .C(BR_15_0[0]), .D(PB), .Z(A02_1_z));
  A02 A02_3 (.A(RB_15_0[1]), .B(PRB), .C(BR_15_0[1]), .D(PB), .Z(A02_3_z));
  A02 A02_5 (.A(RB_15_0[2]), .B(PRB), .C(BR_15_0[2]), .D(PB), .Z(A02_5_z));
  A02 A02_7 (.A(RB_15_0[3]), .B(PRB), .C(BR_15_0[3]), .D(PB), .Z(A02_7_z));
  A02 A02_9 (.A(RB_15_0[4]), .B(PRB), .C(BR_15_0[4]), .D(PB), .Z(A02_9_z));
  or or_1 (or_1_out[0], ~A02_1_z, ~A02_2_z);  // OR_Gate
  or or_2 (or_1_out[1], ~A02_3_z, ~A02_4_z);  // OR_Gate
  or or_3 (or_1_out[2], ~A02_5_z, ~A02_6_z);  // OR_Gate
  or or_4 (or_1_out[3], ~A02_7_z, ~A02_8_z);  // OR_Gate
  or or_5 (or_1_out[4], ~A02_9_z, ~A02_10_z);  // OR_Gate
  or or_6 (or_1_out[5], ~A02_11_z, ~A02_12_z);  // OR_Gate
  or or_7 (or_1_out[6], ~A02_13_z, ~A02_14_z);  // OR_Gate
  or or_8 (or_1_out[7], ~A02_15_z, ~A02_16_z);  // OR_Gate
  or or_9 (or_1_out[8], ~A02_17_z, ~A02_18_z);  // OR_Gate
  or or_10 (or_1_out[9], ~A02_19_z, ~A02_20_z);  // OR_Gate
  or or_11 (or_1_out[10], ~A02_21_z, ~A02_22_z);  // OR_Gate
  or or_12 (or_1_out[11], ~A02_23_z, ~A02_24_z);  // OR_Gate
  or or_13 (or_1_out[12], ~A02_25_z, ~A02_26_z);  // OR_Gate
  or or_14 (or_1_out[13], ~A02_27_z, ~A02_28_z);  // OR_Gate
  or or_15 (or_1_out[14], ~A02_29_z, ~A02_30_z);  // OR_Gate
  or or_16 (or_1_out[15], ~A02_31_z, ~A02_32_z);  // OR_Gate
  nand nand_1 (nand_1_out, not_1_out, CD_15_0[8]);
  nand nand_2 (nand_2_out, not_1_out, CD_15_0[9]);
  nand nand_3 (nand_3_out, not_1_out, CD_15_0[10]);
  nand nand_4 (nand_4_out, not_1_out, CD_15_0[11]);
  nand nand_5 (nand_5_out, not_1_out, CD_15_0[12]);
  nand nand_6 (nand_6_out, not_1_out, CD_15_0[13]);
  nand nand_7 (nand_7_out, not_1_out, CD_15_0[14]);
  nand nand_8 (nand_8_out, not_1_out, CD_15_0[15]);
  nand nand_9 (nand_9_out, CD_15_0[8], CDS);
  nand nand_10 (nand_10_out, CDS, CD_15_0[8]);
  nand nand_11 (nand_11_out[0], nand_1_out, nand_9_out);
  nand nand_12 (nand_11_out[1], nand_2_out, nand_9_out);
  nand nand_13 (nand_11_out[2], nand_3_out, nand_9_out);
  nand nand_14 (nand_11_out[3], nand_4_out, nand_9_out);
  nand nand_15 (nand_11_out[4], nand_5_out, nand_10_out);
  nand nand_16 (nand_11_out[5], nand_6_out, nand_10_out);
  nand nand_17 (nand_11_out[6], nand_7_out, nand_10_out);
  nand nand_18 (nand_11_out[7], nand_8_out, nand_10_out);
  not not_1 (not_1_out, CDS);
  // Probe on CD_15_0[7:0]
  // Probe on or_1_out
  // Probe on nand_11_out
  CGA_MAC_FASTADD FASTADD (.CD_7_0(CD_15_0[7:0]), .CDE_15_8(nand_11_out), .PRP_15_0(or_1_out), .ADD_15_0(ADD_15_0));
endmodule

module CGA_MAC_FASTADD (
  input  [7:0] CD_7_0,
  input  [7:0] CDE_15_8,
  input  [15:0] PRP_15_0,
  output [15:0] ADD_15_0
);

  wire adder_1_cout;

  Adder adder_1 (.a(CD_7_0), .b(PRP_15_0[7:0]), .out(ADD_15_0[7:0]), .cout(adder_1_cout));  // open: cin
  // Probe on adder_1_cout
  Adder adder_2 (.a(CDE_15_8), .b(PRP_15_0[15:8]), .out(ADD_15_0[15:8]), .cin(adder_1_cout));  // open: cout
endmodule

module CGA_MAC_AP09 (
  input  PSEL,
  input  ADDSEL,
  input  CDSEL,
  input  NLCASEL,
  input  HOLD,
  input  [15:0] PR_15_0,
  input  [15:0] ADD_15_0,
  input  [15:0] CD_15_0,
  input  ECCRHIN,
  input  MCLK,
  output [15:0] ICA_15_0,
  output ECCR,
  output [9:0] MCA_9_0,
  output [15:0] LCA_15_0,
  output [15:0] NLCA_15_0
);

  wire ICA0A_z, ICA0B_z, ICA1A_z, ICA1B_z, ICA2A_z, ICA2B_z, ICA3A_z, ICA3B_z, ICA4A_z, ICA4B_z, ICA5A_z,
       ICA5B_z, ICA6A_z, ICA6B_z, ICA7A_z, ICA7B_z, ICA8A_z, ICA8B_z, ICA9A_z, ICA9B_z, ICA10A_z, ICA10B_z,
       ICA11A_z, ICA11B_z, ICA12A_z, ICA12B_z, ICA13A_z, ICA13B_z, ICA14A_z, ICA14B_z, ICA15A_z, ICA15B_z,
       nand_1_out, nand_2_out, nand_3_out, nand_4_out, nand_5_out, nand_6_out, nand_7_out, nand_8_out,
       nand_9_out, nand_10_out, nand_11_out, nand_12_out, nand_13_out, nand_14_out, nand_15_out, nand_16_out;

  A02 ICA0A (.A(LCA_15_0[0]), .B(HOLD), .C(PR_15_0[0]), .D(PSEL), .Z(ICA0A_z));
  A02 ICA0B (.A(ADDSEL), .B(ADD_15_0[0]), .C(CDSEL), .D(CD_15_0[0]), .Z(ICA0B_z));
  nand nand_1 (nand_1_out, NLCASEL, NLCA_15_0[0]);
  A02 ICA1A (.A(LCA_15_0[1]), .B(HOLD), .C(PR_15_0[1]), .D(PSEL), .Z(ICA1A_z));
  A02 ICA1B (.A(ADDSEL), .B(ADD_15_0[1]), .C(CD_15_0[1]), .D(CDSEL), .Z(ICA1B_z));
  nand nand_2 (nand_2_out, NLCASEL, NLCA_15_0[1]);
  A02 ICA2A (.A(LCA_15_0[2]), .B(HOLD), .C(PR_15_0[2]), .D(PSEL), .Z(ICA2A_z));
  A02 ICA2B (.A(ADDSEL), .B(ADD_15_0[2]), .C(CD_15_0[2]), .D(CDSEL), .Z(ICA2B_z));
  nand nand_3 (nand_3_out, NLCASEL, NLCA_15_0[2]);
  A02 ICA3A (.A(LCA_15_0[3]), .B(HOLD), .C(PR_15_0[3]), .D(PSEL), .Z(ICA3A_z));
  A02 ICA3B (.A(ADDSEL), .B(ADD_15_0[3]), .C(CD_15_0[3]), .D(CDSEL), .Z(ICA3B_z));
  nand nand_4 (nand_4_out, NLCASEL, NLCA_15_0[3]);
  A02 ICA4A (.A(LCA_15_0[4]), .B(HOLD), .C(PR_15_0[4]), .D(PSEL), .Z(ICA4A_z));
  A02 ICA4B (.A(ADDSEL), .B(ADD_15_0[4]), .C(CD_15_0[4]), .D(CDSEL), .Z(ICA4B_z));
  nand nand_5 (nand_5_out, NLCASEL, NLCA_15_0[4]);
  A02 ICA5A (.A(LCA_15_0[5]), .B(HOLD), .C(PR_15_0[5]), .D(PSEL), .Z(ICA5A_z));
  A02 ICA5B (.A(ADDSEL), .B(ADD_15_0[5]), .C(CD_15_0[5]), .D(CDSEL), .Z(ICA5B_z));
  nand nand_6 (nand_6_out, NLCASEL, NLCA_15_0[5]);
  A02 ICA6A (.A(LCA_15_0[6]), .B(HOLD), .C(PR_15_0[6]), .D(PSEL), .Z(ICA6A_z));
  A02 ICA6B (.A(ADDSEL), .B(ADD_15_0[6]), .C(CD_15_0[6]), .D(CDSEL), .Z(ICA6B_z));
  nand nand_7 (nand_7_out, NLCASEL, NLCA_15_0[6]);
  A02 ICA7A (.A(LCA_15_0[7]), .B(HOLD), .C(PR_15_0[7]), .D(PSEL), .Z(ICA7A_z));
  A02 ICA7B (.A(ADDSEL), .B(ADD_15_0[7]), .C(CD_15_0[7]), .D(CDSEL), .Z(ICA7B_z));
  nand nand_8 (nand_8_out, NLCASEL, NLCA_15_0[7]);
  A02 ICA8A (.A(LCA_15_0[8]), .B(HOLD), .C(PR_15_0[8]), .D(PSEL), .Z(ICA8A_z));
  A02 ICA8B (.A(ADDSEL), .B(ADD_15_0[8]), .C(CD_15_0[8]), .D(CDSEL), .Z(ICA8B_z));
  nand nand_9 (nand_9_out, NLCASEL, NLCA_15_0[8]);
  A02 ICA9A (.A(LCA_15_0[9]), .B(HOLD), .C(PR_15_0[9]), .D(PSEL), .Z(ICA9A_z));
  A02 ICA9B (.A(ADDSEL), .B(ADD_15_0[9]), .C(CD_15_0[9]), .D(CDSEL), .Z(ICA9B_z));
  nand nand_10 (nand_10_out, NLCASEL, NLCA_15_0[9]);
  A02 ICA10A (.A(LCA_15_0[10]), .B(HOLD), .C(PR_15_0[10]), .D(PSEL), .Z(ICA10A_z));
  A02 ICA10B (.A(ADDSEL), .B(ADD_15_0[10]), .C(CD_15_0[10]), .D(CDSEL), .Z(ICA10B_z));
  nand nand_11 (nand_11_out, NLCASEL, NLCA_15_0[10]);
  A02 ICA11A (.A(LCA_15_0[11]), .B(HOLD), .C(PR_15_0[11]), .D(PSEL), .Z(ICA11A_z));
  A02 ICA11B (.A(ADDSEL), .B(ADD_15_0[11]), .C(CD_15_0[11]), .D(CDSEL), .Z(ICA11B_z));
  nand nand_12 (nand_12_out, NLCASEL, NLCA_15_0[11]);
  A02 ICA12A (.A(LCA_15_0[12]), .B(HOLD), .C(PR_15_0[12]), .D(PSEL), .Z(ICA12A_z));
  A02 ICA12B (.A(ADDSEL), .B(ADD_15_0[12]), .C(CD_15_0[12]), .D(CDSEL), .Z(ICA12B_z));
  nand nand_13 (nand_13_out, NLCASEL, NLCA_15_0[12]);
  A02 ICA13A (.A(LCA_15_0[13]), .B(HOLD), .C(PR_15_0[13]), .D(PSEL), .Z(ICA13A_z));
  A02 ICA13B (.A(ADDSEL), .B(ADD_15_0[13]), .C(CD_15_0[13]), .D(CDSEL), .Z(ICA13B_z));
  nand nand_14 (nand_14_out, NLCASEL, NLCA_15_0[13]);
  A02 ICA14A (.A(LCA_15_0[14]), .B(HOLD), .C(PR_15_0[14]), .D(PSEL), .Z(ICA14A_z));
  A02 ICA14B (.A(ADDSEL), .B(ADD_15_0[14]), .C(CD_15_0[14]), .D(CDSEL), .Z(ICA14B_z));
  nand nand_15 (nand_15_out, NLCASEL, NLCA_15_0[14]);
  A02 ICA15A (.A(LCA_15_0[15]), .B(HOLD), .C(PR_15_0[15]), .D(PSEL), .Z(ICA15A_z));
  A02 ICA15B (.A(ADDSEL), .B(ADD_15_0[15]), .C(CD_15_0[15]), .D(CDSEL), .Z(ICA15B_z));
  nand nand_16 (nand_16_out, NLCASEL, NLCA_15_0[15]);
  CGA_MAC_APOS_CALCA CALCA (
    .ECCRHIN(ECCRHIN), .ICA_15_0(ICA_15_0), .MCLK(MCLK), .MCA_9_0(MCA_9_0), .LCA_15_0(LCA_15_0), .ECCR(ECCR));
  CGA_MAC_APOS_INC AINC (.LCA_15_0(LCA_15_0), .NLCA_15_0(NLCA_15_0));
  or or_1 (ICA_15_0[0], ~ICA0A_z, ~ICA0B_z, ~nand_1_out);  // OR_Gate
  or or_2 (ICA_15_0[1], ~ICA1A_z, ~ICA1B_z, ~nand_2_out);  // OR_Gate
  or or_3 (ICA_15_0[2], ~ICA2A_z, ~ICA2B_z, ~nand_3_out);  // OR_Gate
  or or_4 (ICA_15_0[3], ~ICA3A_z, ~ICA3B_z, ~nand_4_out);  // OR_Gate
  or or_5 (ICA_15_0[4], ~ICA4A_z, ~ICA4B_z, ~nand_5_out);  // OR_Gate
  or or_6 (ICA_15_0[5], ~ICA5A_z, ~ICA5B_z, ~nand_6_out);  // OR_Gate
  or or_7 (ICA_15_0[6], ~ICA6A_z, ~ICA6B_z, ~nand_7_out);  // OR_Gate
  or or_8 (ICA_15_0[7], ~ICA7A_z, ~ICA7B_z, ~nand_8_out);  // OR_Gate
  or or_9 (ICA_15_0[8], ~ICA8A_z, ~ICA8B_z, ~nand_9_out);  // OR_Gate
  or or_10 (ICA_15_0[9], ~ICA9A_z, ~ICA9B_z, ~nand_10_out);  // OR_Gate
  or or_11 (ICA_15_0[10], ~ICA10A_z, ~ICA10B_z, ~nand_11_out);  // OR_Gate
  or or_12 (ICA_15_0[11], ~ICA11A_z, ~ICA11B_z, ~nand_12_out);  // OR_Gate
  or or_13 (ICA_15_0[12], ~ICA12A_z, ~ICA12B_z, ~nand_13_out);  // OR_Gate
  or or_14 (ICA_15_0[13], ~ICA13A_z, ~ICA13B_z, ~nand_14_out);  // OR_Gate
  or or_15 (ICA_15_0[14], ~ICA14A_z, ~ICA14B_z, ~nand_15_out);  // OR_Gate
  or or_16 (ICA_15_0[15], ~ICA15A_z, ~ICA15B_z, ~nand_16_out);  // OR_Gate

  // Notes on the sheet:
  //   Page 31 - CGA_MAC_APO9
  //   ICA0
  //   ICA1
  //   ICA2
  //   ICA3
  //   ICA4
  //   ICA5
  //   ICA6
  //   ICA7
  //   ICA8
  //   ICA9
  //   ICA10
  //   ICA11
  //   ICA12
  //   ICA13
  //   ICA14
  //   ICA15
endmodule

module CGA_MAC_APOS_CALCA (
  input  ECCRHIN,
  input  [15:0] ICA_15_0,
  input  MCLK,
  output [9:0] MCA_9_0,
  output [15:0] LCA_15_0,
  output ECCR
);

  wire L_HI_qc, L_HI_qd, L_HI_qe, L_HI_qf, L_HI_qg, L_HI_qh, nand_1_out, nand_2_out, not_1_out;
  wire [9:1] R_LO_qbn;

  not not_1 (not_1_out, MCLK);
  L8 L_LO (
    .A(ICA_15_0[0]), .B(ICA_15_0[1]), .C(ICA_15_0[2]), .D(ICA_15_0[3]), .E(ICA_15_0[4]), .F(ICA_15_0[5]),
    .G(ICA_15_0[6]), .H(ICA_15_0[7]), .L(not_1_out), .QA(MCA_9_0[0]), .QB(MCA_9_0[1]), .QC(MCA_9_0[2]),
    .QD(MCA_9_0[3]), .QE(MCA_9_0[4]), .QF(MCA_9_0[5]), .QG(MCA_9_0[6]), .QH(MCA_9_0[7]));  // open: QAN, QBN, QCN, QDN, QEN, QFN, QGN, QHN
  L8 L_HI (
    .A(ICA_15_0[8]), .B(ICA_15_0[9]), .C(ICA_15_0[10]), .D(ICA_15_0[11]), .E(ICA_15_0[12]), .F(ICA_15_0[13]),
    .G(ICA_15_0[14]), .H(ICA_15_0[15]), .L(not_1_out), .QA(MCA_9_0[8]), .QB(MCA_9_0[9]), .QC(L_HI_qc),
    .QD(L_HI_qd), .QE(L_HI_qe), .QF(L_HI_qf), .QG(L_HI_qg), .QH(L_HI_qh));  // open: QAN, QBN, QCN, QDN, QEN, QFN, QGN, QHN
  R81 R_LO (
    .A(MCA_9_0[0]), .B(MCA_9_0[1]), .C(MCA_9_0[2]), .D(MCA_9_0[3]), .E(MCA_9_0[4]), .F(MCA_9_0[5]),
    .G(MCA_9_0[6]), .H(MCA_9_0[7]), .CP(MCLK), .QA(LCA_15_0[0]), .QB(LCA_15_0[1]), .QBN(R_LO_qbn[1]),
    .QC(LCA_15_0[2]), .QD(LCA_15_0[3]), .QE(LCA_15_0[4]), .QEN(R_LO_qbn[4]), .QF(LCA_15_0[5]),
    .QFN(R_LO_qbn[5]), .QG(LCA_15_0[6]), .QH(LCA_15_0[7]), .QHN(R_LO_qbn[7]));  // open: QAN, QCN, QDN, QGN
  R81 R_HI (
    .A(MCA_9_0[8]), .B(MCA_9_0[9]), .C(L_HI_qc), .D(L_HI_qd), .E(L_HI_qe), .F(L_HI_qf), .G(L_HI_qg),
    .H(L_HI_qh), .CP(MCLK), .QA(LCA_15_0[8]), .QAN(R_LO_qbn[8]), .QB(LCA_15_0[9]), .QBN(R_LO_qbn[9]),
    .QC(LCA_15_0[10]), .QD(LCA_15_0[11]), .QE(LCA_15_0[12]), .QF(LCA_15_0[13]), .QG(LCA_15_0[14]),
    .QH(LCA_15_0[15]));  // open: QCN, QDN, QEN, QFN, QGN, QHN
  nand nand_1 (nand_1_out, LCA_15_0[0], R_LO_qbn[1], LCA_15_0[2], LCA_15_0[3], R_LO_qbn[4]);
  nand nand_2 (nand_2_out, R_LO_qbn[5], LCA_15_0[6], R_LO_qbn[7], R_LO_qbn[8], R_LO_qbn[9]);
  and and_1 (ECCR, ~ECCRHIN, ~nand_1_out, ~nand_2_out);  // AND_Gate

  // Notes on the sheet:
  //   Page 32 - CGA_MAC_APOS_CALCA
  //   LCA0
  //   LCA9N
  //   DECODE TRR ECCR = IOX 100115
endmodule

module CGA_MAC_APOS_INC (
  input  [15:0] LCA_15_0,
  output [15:0] NLCA_15_0
);

  wire adder_1_cout, adder_2_cout, adder_3_cout, adder_4_cout, adder_5_cout, adder_6_cout, adder_7_cout,
       adder_9_cout, adder_10_cout, adder_11_cout, adder_12_cout, adder_14_cout, adder_15_cout, nand_1_out,
       nand_2_out, not_1_out, not_2_out;

  Adder #(.width(1)) adder_1 (.a(LCA_15_0[0]), .b(1'b1), .out(NLCA_15_0[0]), .cout(adder_1_cout));  // open: cin
  Adder #(.width(1)) adder_2 (.a(LCA_15_0[1]), .b(adder_1_cout), .out(NLCA_15_0[1]), .cout(adder_2_cout));  // open: cin
  Adder #(.width(1)) adder_3 (.a(LCA_15_0[2]), .b(adder_2_cout), .out(NLCA_15_0[2]), .cout(adder_3_cout));  // open: cin
  Adder #(.width(1)) adder_4 (.a(LCA_15_0[3]), .b(adder_3_cout), .out(NLCA_15_0[3]), .cout(adder_4_cout));  // open: cin
  Adder #(.width(1)) adder_5 (.a(LCA_15_0[4]), .b(adder_4_cout), .out(NLCA_15_0[4]), .cout(adder_5_cout));  // open: cin
  Adder #(.width(1)) adder_6 (.a(LCA_15_0[5]), .b(adder_5_cout), .out(NLCA_15_0[5]), .cout(adder_6_cout));  // open: cin
  Adder #(.width(1)) adder_7 (.a(LCA_15_0[6]), .b(adder_6_cout), .out(NLCA_15_0[6]), .cout(adder_7_cout));  // open: cin
  Adder #(.width(1)) adder_8 (.a(LCA_15_0[7]), .b(adder_7_cout), .out(NLCA_15_0[7]));  // open: cin, cout
  nand nand_1 (nand_1_out, LCA_15_0[7], LCA_15_0[6], LCA_15_0[5], LCA_15_0[4], LCA_15_0[3], LCA_15_0[2], LCA_15_0[1], LCA_15_0[0]);
  not not_1 (not_1_out, nand_1_out);
  Adder #(.width(1)) adder_9 (.a(LCA_15_0[8]), .b(not_1_out), .out(NLCA_15_0[8]), .cout(adder_9_cout));  // open: cin
  Adder #(.width(1)) adder_10 (
    .a(LCA_15_0[9]), .b(adder_9_cout), .out(NLCA_15_0[9]), .cout(adder_10_cout));  // open: cin
  Adder #(.width(1)) adder_11 (
    .a(LCA_15_0[10]), .b(adder_10_cout), .out(NLCA_15_0[10]), .cout(adder_11_cout));  // open: cin
  Adder #(.width(1)) adder_12 (
    .a(LCA_15_0[11]), .b(adder_11_cout), .out(NLCA_15_0[11]), .cout(adder_12_cout));  // open: cin
  nand nand_2 (nand_2_out, LCA_15_0[12], LCA_15_0[11], LCA_15_0[10], LCA_15_0[9], LCA_15_0[8], not_1_out);
  Adder #(.width(1)) adder_13 (.a(LCA_15_0[12]), .b(adder_12_cout), .out(NLCA_15_0[12]));  // open: cin, cout
  not not_2 (not_2_out, nand_2_out);
  Adder #(.width(1)) adder_14 (
    .a(LCA_15_0[13]), .b(not_2_out), .out(NLCA_15_0[13]), .cout(adder_14_cout));  // open: cin
  Adder #(.width(1)) adder_15 (
    .a(LCA_15_0[14]), .b(adder_14_cout), .out(NLCA_15_0[14]), .cout(adder_15_cout));  // open: cin
  Adder #(.width(1)) adder_16 (.a(LCA_15_0[15]), .b(adder_15_cout), .out(NLCA_15_0[15]));  // open: cin, cout

  // Notes on the sheet:
  //   Page 33 - CGA_MAC_APOS_INC
endmodule

module CGA_MAC_PTSEL (
  input  SPTN,
  input  SAPT,
  input  PONI,
  input  PTM,
  input  MCLK,
  output SELPTN
);

  wire j_k_ff_1_qn, nor_1_out, not_1_out, not_2_out, or_1_out, or_2_out;

  nor nor_1 (nor_1_out, ~PTM, ~PONI);  // NOR_Gate
  not not_1 (not_1_out, SPTN);
  not not_2 (not_2_out, nor_1_out);
  J_K_Flip_Flop j_k_ff_1 (
    .J(not_1_out), .K(SAPT), .clk(MCLK), .Qn(j_k_ff_1_qn), .preset(not_2_out), .reset(1'b0));  // open: Q
  or or_1 (or_1_out, ~SPTN, ~j_k_ff_1_qn);  // OR_Gate
  or or_2 (or_2_out, ~SAPT, ~PONI, ~PTM);  // OR_Gate
  nand nand_1 (SELPTN, or_1_out, or_2_out);

  // Notes on the sheet:
  //   Page 34 - CGA_MAC_PTSEL
  //   In the original schematics for the FF the PR and CL is negated, this LogiSim J/K FF doesnt support that - so the signals has been changed to accomodate
endmodule

module CGA_MAC_SEGPT (
  input  [15:0] FIDBO_15_0,
  input  MCLK,
  input  LLDSEG,
  input  LLDPCR,
  input  LLDEXM,
  input  EXMN,
  output [7:0] SEG_7_0,
  output SEGZN,
  output [15:0] PCR_15_7_2_0,
  output [15:0] PCR_14_13_10_9_N,
  output [1:0] XPT_1_0,
  output VEX,
  output PEX
);

  wire not_1_out;
  wire [6:3] undriven;

  not not_1 (not_1_out, MCLK);
  CGA_MAC_SEGPT_SEG SEG (
    .FIDB_7_0(FIDBO_15_0[7:0]), .MCLKN(not_1_out), .LLDSEG(LLDSEG), .SEG_7_0(SEG_7_0), .SEGZN(SEGZN));
  CGA_MAC_SEGPT_PCR PCR (
    .FIDB_15_7_2_0({FIDBO_15_0[15:7], undriven, FIDBO_15_0[2:0]}), .MCLKN(not_1_out), .LLDPCR(LLDPCR),
    .PCR_15_7_2_0(PCR_15_7_2_0), .PCR_14_13_10_9_N(PCR_14_13_10_9_N));
  CGA_MAC_SEGPT_XPT XPT (
    .FIDBO_2_0(FIDBO_15_0[2:0]), .MCLKN(not_1_out), .LLDEXM(LLDEXM), .EXMN(EXMN), .XPT_1_0(XPT_1_0),
    .VEX(VEX), .PEX(PEX));

  // Notes on the sheet:
  //   MCLKN
  //   MCLKN
  //   MCLKN
endmodule

module CGA_MAC_SEGPT_SEG (
  input  [7:0] FIDB_7_0,
  input  MCLKN,
  input  LLDSEG,
  output [7:0] SEG_7_0,
  output SEGZN
);

  wire and_1_out;
  wire [7:0] SEG_L_qan;

  and and_1 (and_1_out, MCLKN, LLDSEG);
  L8 SEG_L (
    .A(FIDB_7_0[0]), .B(FIDB_7_0[1]), .C(FIDB_7_0[2]), .D(FIDB_7_0[3]), .E(FIDB_7_0[4]), .F(FIDB_7_0[5]),
    .G(FIDB_7_0[6]), .H(FIDB_7_0[7]), .L(and_1_out), .QA(SEG_7_0[0]), .QAN(SEG_L_qan[0]), .QB(SEG_7_0[1]),
    .QBN(SEG_L_qan[1]), .QC(SEG_7_0[2]), .QCN(SEG_L_qan[2]), .QD(SEG_7_0[3]), .QDN(SEG_L_qan[3]),
    .QE(SEG_7_0[4]), .QEN(SEG_L_qan[4]), .QF(SEG_7_0[5]), .QFN(SEG_L_qan[5]), .QG(SEG_7_0[6]),
    .QGN(SEG_L_qan[6]), .QH(SEG_7_0[7]), .QHN(SEG_L_qan[7]));
  nand nand_1 (SEGZN, SEG_L_qan[0], SEG_L_qan[1], SEG_L_qan[2], SEG_L_qan[3], SEG_L_qan[4], SEG_L_qan[5], SEG_L_qan[6], SEG_L_qan[7]);
endmodule

module CGA_MAC_SEGPT_PCR (
  input  [15:0] FIDB_15_7_2_0,
  input  MCLKN,
  input  LLDPCR,
  output [15:0] PCR_15_7_2_0,
  output [15:0] PCR_14_13_10_9_N
);

  wire and_1_out, PCR_HI_qdn;

  and and_1 (and_1_out, MCLKN, LLDPCR);
  L8 PCR_HI (
    .A(FIDB_15_7_2_0[15]), .B(FIDB_15_7_2_0[14]), .C(FIDB_15_7_2_0[13]), .D(FIDB_15_7_2_0[12]),
    .E(FIDB_15_7_2_0[11]), .F(FIDB_15_7_2_0[10]), .G(FIDB_15_7_2_0[9]), .H(FIDB_15_7_2_0[8]), .L(and_1_out),
    .QA(PCR_15_7_2_0[15]), .QB(PCR_15_7_2_0[14]), .QBN(PCR_14_13_10_9_N[14]), .QC(PCR_15_7_2_0[13]),
    .QCN(PCR_14_13_10_9_N[13]), .QD(PCR_15_7_2_0[12]), .QDN(PCR_HI_qdn), .QE(PCR_15_7_2_0[11]),
    .QF(PCR_15_7_2_0[10]), .QFN(PCR_14_13_10_9_N[10]), .QG(PCR_15_7_2_0[9]), .QGN(PCR_14_13_10_9_N[9]),
    .QH(PCR_15_7_2_0[8]));  // open: QAN, QEN, QHN
  L4 PCR_LO (
    .A(FIDB_15_7_2_0[7]), .B(FIDB_15_7_2_0[2]), .C(FIDB_15_7_2_0[1]), .D(FIDB_15_7_2_0[0]), .L(and_1_out),
    .QA(PCR_15_7_2_0[7]), .QB(PCR_15_7_2_0[2]), .QC(PCR_15_7_2_0[1]), .QD(PCR_15_7_2_0[0]));  // open: QAN, QBN, QCN, QDN

  // Notes on the sheet:
  //   Page 37 - CGA_MAC_SEGPTR_PCR
endmodule

module CGA_MAC_SEGPT_XPT (
  input  [2:0] FIDBO_2_0,
  input  MCLKN,
  input  LLDEXM,
  input  EXMN,
  output [1:0] XPT_1_0,
  output VEX,
  output PEX
);

  wire and_1_out, not_1_out, XPT_L_qc, XPT_L_qcn;

  and and_1 (and_1_out, MCLKN, LLDEXM);
  not not_1 (not_1_out, EXMN);
  L4 XPT_L (
    .A(FIDBO_2_0[0]), .B(FIDBO_2_0[1]), .C(FIDBO_2_0[2]), .L(and_1_out), .QA(XPT_1_0[0]), .QB(XPT_1_0[1]),
    .QC(XPT_L_qc), .QCN(XPT_L_qcn));  // open: D, QAN, QBN, QD, QDN
  and and_2 (VEX, not_1_out, XPT_L_qc);
  and and_3 (PEX, XPT_L_qcn, not_1_out);

  // Notes on the sheet:
  //   Page 38 - CGA_MAC_SEGPT_XPT
  //   FIDBO0
  //   FIDBO1
  //   FIDBO2
  //   XPT0
  //   XPT1
endmodule

module CGA_MAC_LASEL (
  input  DOUBLE,
  input  [15:0] PCR_15_7_2_0,
  input  [15:0] ICA_15_8,
  input  CSMREQ,
  input  VEX,
  input  PONI,
  input  PEX,
  input  SEGZN,
  input  EXMN,
  input  SELPTN,
  input  MCLK,
  output A10,
  output BB10,
  output C10,
  output A1617,
  output D1617,
  output E1617,
  output F1617,
  output A1819,
  output B1821,
  output B1819,
  output A1619,
  output LSHADOW
);

  wire and_1_out, nand_1_out, nand_2_out, nand_3_out, nand_4_out, nand_5_out, nand_6_out, nand_7_out,
       nor_1_out, not_1_out, not_2_out, not_3_out, not_4_out, not_5_out, not_6_out, not_7_out, not_8_out,
       not_9_out, not_10_out, or_1_out, or_2_out, or_3_out;

  not not_1 (not_1_out, DOUBLE);
  not not_2 (not_2_out, PCR_15_7_2_0[2]);
  nand nand_1 (nand_1_out, not_1_out, not_2_out);
  nand nand_2 (nand_2_out, PCR_15_7_2_0[2], DOUBLE);
  nand nand_3 (nand_3_out, ICA_15_8[10], ICA_15_8[9]);
  nor nor_1 (nor_1_out, nand_1_out, ICA_15_8[8]);
  nand nand_4 (nand_4_out, ICA_15_8[15], ICA_15_8[14], ICA_15_8[13], ICA_15_8[12], ICA_15_8[11]);
  not not_3 (not_3_out, PEX);
  nand nand_5 (nand_5_out, PCR_15_7_2_0[1], PCR_15_7_2_0[0]);
  or or_1 (or_1_out, ~nand_2_out, ~nand_3_out);  // OR_Gate
  and and_1 (and_1_out, ~nor_1_out, ~nand_4_out);  // AND_Gate
  or or_2 (or_2_out, ~nand_5_out, ~PONI, ~not_3_out);  // OR_Gate
  or or_3 (or_3_out, ~PEX, ~SEGZN);  // OR_Gate
  nand nand_6 (nand_6_out, or_1_out, and_1_out, CSMREQ, or_2_out, or_3_out);
  not not_4 (not_4_out, nand_6_out);
  nand nand_7 (nand_7_out, EXMN, CSMREQ, PONI);
  not not_5 (not_5_out, not_4_out);
  not not_6 (not_6_out, SELPTN);
  not not_7 (not_7_out, EXMN);
  not not_8 (not_8_out, nand_7_out);
  not not_9 (not_9_out, nand_1_out);
  not not_10 (not_10_out, nand_2_out);
  D_Flip_Flop d_ff_1 (.D(not_5_out), .clk(MCLK), .Qn(LSHADOW));  // open: Q, preset, reset
  and and_2 (A10, not_4_out, not_9_out);
  and and_3 (BB10, not_4_out, nand_1_out);
  and and_4 (C10, not_5_out, 1'b1);
  and and_5 (A1617, not_5_out, PEX);
  and and_6 (D1617, not_5_out, nand_2_out, not_6_out, not_8_out);
  and and_7 (E1617, not_5_out, not_8_out, SELPTN);
  and and_8 (F1617, not_5_out, VEX);
  and and_9 (A1819, not_4_out, not_10_out);
  and and_10 (B1821, not_5_out, not_7_out);
  and and_11 (B1819, not_5_out, SELPTN, not_8_out, not_10_out);
  and and_12 (A1619, not_5_out, not_8_out, not_6_out, not_10_out);

  // Notes on the sheet:
  //   Page 39 - CGA_MAC_LASEL
  //   REXN
  //   EXN
  //   SHADOW
  //   SHADOWN
  //   ISELPT
  //   SHADOWN
endmodule

module CGA_MAC_LA1025 (
  input  [15:0] ICA_15_0,
  input  A10,
  input  BB10,
  input  C10,
  input  A1617,
  input  D1617,
  input  E1617,
  input  F1617,
  input  A1819,
  input  B1821,
  input  B1819,
  input  A1619,
  input  [7:0] SEG_7_0,
  input  [15:0] PCR_15_0,
  input  [15:0] PCR_15_0_N,
  input  [1:0] XPT_1_0,
  input  MCLK,
  output ECCRHIN,
  output [13:0] LA_23_10
);

  wire ILA10A_z, ILA11A_z, ILA12A_z, ILA13A_z, ILA14A_z, ILA15A_z, ILA16A_z, ILA16B_z, ILA16C_z, ILA17A_z,
       ILA17B_z, ILA17C_z, ILA18A_z, ILA18B_z, ILA19A_z, ILA19B_z, nand_1_out, nand_2_out, nand_3_out,
       nand_4_out, nand_5_out, nand_6_out, nand_7_out, nand_8_out, nand_9_out, nand_10_out, nand_11_out,
       nand_12_out, not_1_out, not_2_out, or_1_out, or_2_out, or_3_out, or_4_out, or_5_out, or_6_out,
       or_7_out, or_8_out, or_9_out, or_10_out, R_LA_L_qdn, R_LA_L_qen, R_LA_L_qfn, R_LA_L_qgn, R_LA_L_qhn;

  not not_1 (not_1_out, ICA_15_0[9]);
  not not_2 (not_2_out, ICA_15_0[10]);
  A02 ILA15A (.A(ICA_15_0[5]), .B(A10), .C(ICA_15_0[6]), .D(BB10), .Z(ILA15A_z));
  nand nand_1 (nand_1_out, ICA_15_0[15], C10);
  A02 ILA14A (.A(ICA_15_0[4]), .B(A10), .C(ICA_15_0[5]), .D(BB10), .Z(ILA14A_z));
  nand nand_2 (nand_2_out, ICA_15_0[14], C10);
  A02 ILA13A (.A(ICA_15_0[3]), .B(A10), .C(ICA_15_0[4]), .D(BB10), .Z(ILA13A_z));
  nand nand_3 (nand_3_out, ICA_15_0[13], C10);
  A02 ILA12A (.A(ICA_15_0[2]), .B(A10), .C(ICA_15_0[3]), .D(BB10), .Z(ILA12A_z));
  nand nand_4 (nand_4_out, ICA_15_0[12], C10);
  A02 ILA11A (.A(ICA_15_0[1]), .B(A10), .C(ICA_15_0[2]), .D(BB10), .Z(ILA11A_z));
  nand nand_5 (nand_5_out, ICA_15_0[11], C10);
  A02 ILA10A (.A(ICA_15_0[0]), .B(A10), .C(ICA_15_0[1]), .D(BB10), .Z(ILA10A_z));
  nand nand_6 (nand_6_out, ICA_15_0[10], C10);
  nand nand_7 (nand_7_out, SEG_7_0[5], B1821);
  nand nand_8 (nand_8_out, SEG_7_0[4], B1821);
  A02 ILA19A (.A(A1619), .B(PCR_15_0_N[14]), .C(SEG_7_0[3]), .D(B1821), .Z(ILA19A_z));
  A02 ILA19B (.A(not_2_out), .B(A1819), .C(PCR_15_0_N[10]), .D(B1819), .Z(ILA19B_z));
  A02 ILA18A (.A(A1619), .B(PCR_15_0_N[13]), .C(PCR_15_0_N[9]), .D(B1819), .Z(ILA18A_z));
  A02 ILA18B (.A(SEG_7_0[2]), .B(B1821), .C(not_1_out), .D(A1819), .Z(ILA18B_z));
  nand nand_9 (nand_9_out, SEG_7_0[7], A1617);
  nand nand_10 (nand_10_out, SEG_7_0[6], A1617);
  A02 ILA17A (.A(ICA_15_0[7]), .B(A10), .C(ICA_15_0[8]), .D(BB10), .Z(ILA17A_z));
  A02 ILA17B (.A(PCR_15_0[12]), .B(A1619), .C(SEG_7_0[1]), .D(A1617), .Z(ILA17B_z));
  A02 ILA17C (.A(PCR_15_0[10]), .B(D1617), .C(PCR_15_0[8]), .D(E1617), .Z(ILA17C_z));
  nand nand_11 (nand_11_out, XPT_1_0[1], F1617);
  A02 ILA16A (.A(ICA_15_0[6]), .B(A10), .C(ICA_15_0[7]), .D(BB10), .Z(ILA16A_z));
  A02 ILA16B (.A(PCR_15_0[11]), .B(A1619), .C(SEG_7_0[0]), .D(A1617), .Z(ILA16B_z));
  A02 ILA16C (.A(PCR_15_0[9]), .B(D1617), .C(PCR_15_0[7]), .D(E1617), .Z(ILA16C_z));
  nand nand_12 (nand_12_out, XPT_1_0[0], F1617);
  or or_1 (or_1_out, ~ILA15A_z, ~nand_1_out);  // OR_Gate
  or or_2 (or_2_out, ~ILA14A_z, ~nand_2_out);  // OR_Gate
  or or_3 (or_3_out, ~ILA13A_z, ~nand_3_out);  // OR_Gate
  or or_4 (or_4_out, ~ILA12A_z, ~nand_4_out);  // OR_Gate
  or or_5 (or_5_out, ~ILA11A_z, ~nand_5_out);  // OR_Gate
  or or_6 (or_6_out, ~ILA10A_z, ~nand_6_out);  // OR_Gate
  or or_7 (or_7_out, ~ILA19A_z, ~ILA19B_z);  // OR_Gate
  or or_8 (or_8_out, ~ILA18A_z, ~ILA18B_z);  // OR_Gate
  or or_9 (or_9_out, ~ILA17A_z, ~ILA17B_z, ~ILA17C_z, ~nand_11_out);  // OR_Gate
  or or_10 (or_10_out, ~ILA16A_z, ~ILA16B_z, ~ILA16C_z, ~nand_12_out);  // OR_Gate
  R81 R_LA_H (
    .C(nand_9_out), .D(nand_10_out), .E(nand_7_out), .F(nand_8_out), .G(or_7_out), .H(or_8_out), .CP(MCLK),
    .QCN(LA_23_10[13]), .QDN(LA_23_10[12]), .QEN(LA_23_10[11]), .QFN(LA_23_10[10]), .QG(LA_23_10[9]),
    .QH(LA_23_10[8]));  // open: A, B, QA, QAN, QB, QBN, QC, QD, QE, QF, QGN, QHN
  R81 R_LA_L (
    .A(or_9_out), .B(or_10_out), .C(or_1_out), .D(or_2_out), .E(or_3_out), .F(or_4_out), .G(or_5_out),
    .H(or_6_out), .CP(MCLK), .QA(LA_23_10[7]), .QB(LA_23_10[6]), .QC(LA_23_10[5]), .QD(LA_23_10[4]),
    .QDN(R_LA_L_qdn), .QE(LA_23_10[3]), .QEN(R_LA_L_qen), .QF(LA_23_10[2]), .QFN(R_LA_L_qfn),
    .QG(LA_23_10[1]), .QGN(R_LA_L_qgn), .QH(LA_23_10[0]), .QHN(R_LA_L_qhn));  // open: QAN, QBN, QCN
  nand nand_13 (ECCRHIN, LA_23_10[5], R_LA_L_qhn, R_LA_L_qgn, R_LA_L_qfn, R_LA_L_qen, R_LA_L_qdn);

  // Notes on the sheet:
  //   Page 40 - CGA_MAC_LA1025
  //   ICA6
  //   BB10
  //   ICA5
  //   BB10
  //   ICA4
  //   BB10
  //   ICA3
  //   BB10
  //   ICA2
  //   BB10
  //   ICA1
  //   BB10
  //   ICA5
  //   A10
  //   ICA4
  //   A10
  //   ICA3
  //   A10
  //   ICA2
  //   A10
  //   ICA1
  //   A10
  //   ICA0
  //   A10
  //   ICA7
  //   A10
  //   ICA8
  //   BB10
  //   PCR12
  //   A1619
  //   SEG1
  //   A1617
  //   ICA6
  //   A10
  //   ICA7
  //   BB10
  //   PCR11
  //   A1619
  //   SEG0
  //   A1617
  //   PCR9
  //   D1617
  //   PCR7
  //   E1617
  //   ICA15
  //   C10
  //   ICA14
  //   C10
  //   ICA13
  //   C10
  //   ICA12
  //   C10
  //   ICA11
  //   C10
  //   ICA10
  //   C10
  //   PCR10
  //   D1617
  //   PCR8
  //   E1617
  //   XPT1
  //   F1617
  //   XPT0
  //   F1617
  //   ILA15
  //   ILA14
  //   ILA13
  //   ILA12
  //   ILA11
  //   ILA10
  //   ILA21N
  //   ILA20N
  //   ILA19
  //   ILA18
  //   ILA23N
  //   ILA22N
  //   ILA17
  //   ILA16
  //   LA10
  //   LA23
endmodule

module test_MAC (
  input  in_1,
  input  in_2,
  input  [15:0] in_3,
  input  in_4,
  input  [1:0] in_5,
  input  [4:0] in_6,
  input  in_7,
  input  in_8,
  input  in_9,
  input  in_10,
  input  in_11,
  input  [15:0] in_12,
  input  [15:0] in_13,
  input  [15:0] in_14,
  input  [15:0] in_15,
  input  [15:0] in_16
);

  wire cga_mac_1_eccr, cga_mac_1_lshadow, cga_mac_1_vex;
  wire [9:0] cga_mac_1_mca_9_0;
  wire [13:0] cga_mac_1_la_23_10;
  wire [15:0] cga_mac_1_nlca_15_0, cga_mac_1_pcr_15_7_2_0;

  CGA_MAC cga_mac_1 (
    .MCLK(in_1), .PTM(in_2), .FIDBO_15_0(in_3), .PONI(in_4), .CMIS_1_0(in_5), .CSCOMM_4_0(in_6), .WR3(in_7),
    .WR7(in_8), .ILCSN(in_9), .DOUBLE(in_10), .CSMREQ(in_11), .CD_15_0(in_12), .RB_15_0(in_13),
    .XR_15_0(in_14), .BR_15_0(in_15), .PR_15_0(in_16), .VEX(cga_mac_1_vex),
    .PCR_15_7_2_0(cga_mac_1_pcr_15_7_2_0), .LA_23_10(cga_mac_1_la_23_10), .LSHADOW(cga_mac_1_lshadow),
    .ECCR(cga_mac_1_eccr), .MCA_9_0(cga_mac_1_mca_9_0), .NLCA_15_0(cga_mac_1_nlca_15_0));
  // Probe on cga_mac_1_vex
  // Probe on cga_mac_1_lshadow
  // Probe on cga_mac_1_eccr
  // Probe on cga_mac_1_nlca_15_0
  // Probe on cga_mac_1_la_23_10
  // Probe on cga_mac_1_mca_9_0
  // Probe on cga_mac_1_pcr_15_7_2_0

  // Notes on the sheet:
  //   MAC UNDER TEST
endmodule
