// Logisim project CGA_MIC_.circ as structural Verilog: 13 circuits, main circuit CGA_MIC
module CGA_MIC (
  input  [15:0] CSBIT_15_0,
  input  CSBIT20,
  input  LCZ,
  input  MI,
  input  IRQ,
  input  RESTR,
  input  CFETCH,
  input  SPARE,
  input  OVF,
  input  CRY,
  input  F11,
  input  F15,
  input  ZF,
  input  STP,
  input  ALUCLK,
  input  MCLK,
  input  CSLOOP,
  input  CSECOND,
  input  CLFFN,
  input  CSALUI8,
  input  CSCOND,
  input  ILCSN,
  input  [3:0] CSTS_6_3,
  input  [3:0] TVEC_3_0,
  input  TRAPN,
  input  MAPN,
  input  EWCAN,
  input  CSMIS0,
  input  CSVECT,
  input  [15:0] CD_15_0,
  input  LDIRV,
  input  LWCAN,
  input  MRN,
  input  LDLCN,
  input  [3:0] PIL_3_0,
  input  CSXRF3,
  input  [3:0] CSRB_3_0,
  input  [1:0] CSRASEL_1_0,
  input  [1:0] CSRBSEL_1_0,
  output DZD,
  output COND,
  output OOD,
  output ACONDN,
  output [3:0] SC_6_3,
  output [12:0] MA_12_0,
  output WCSN,
  output DEEP,
  output UPN,
  output PN,
  output LCZN,
  output TN,
  output [3:0] LAA_3_0,
  output [3:0] LBA_3_0,
  output [1:0] RF_1_0
);

  wire and_1_out, and_2_out, and_3_out, and_4_out, and_5_out, and_6_out, and_7_out, and_8_out, and_9_out,
       and_10_out, and_11_out, CIN, CSEL_condn, d_ff_1_q, d_ff_2_q, d_ff_6_q, d_ff_7_qn, DZD_FF_q,
       LAA_REG_qan, LAA_REG_qbn, LAA_REG_qcn, LAA_REG_qdn, LBA_REG_qan, LBA_REG_qbn, LBA_REG_qcn,
       LBA_REG_qdn, LC_CMP_aeb, LC_HI_con, LC_HI_qa, LC_HI_qb, LC_HI_qc, LC_HI_qd, LCSN, LCZ_t, M_LAA_0_z,
       M_LAA_1_z, M_LAA_2_z, M_LAA_3_z, M_LBA_0_z, M_LBA_1_z, M_LBA_2_z, M_LBA_3_z, MIC_LOOP, nand_1_out,
       nand_2_out, nand_3_out, nand_5_out, nand_6_out, nand_9_out, nor_1_out, nor_2_out, nor_3_out,
       nor_4_out, nor_5_out, nor_6_out, nor_7_out, nor_8_out, nor_9_out, not_1_out, not_2_out, not_3_out,
       not_4_out, not_5_out, not_6_out, not_8_out, not_10_out, not_11_out, not_12_out, not_13_out,
       not_17_out, OOD_FF_q, or_1_out, or_2_out;
  wire [1:0] CSWAN_1_0;
  wire [3:0] CONDREG_fs_6_3, CONDREG_tsel_3_0, ILC_MUX_z0, LC_3_0, LCC_3_0;
  wire [6:0] IR_6_0;
  wire [12:0] MIC_IINC_next_12_0, MIC_MASEL_iw_12_0, MIC_MASEL_w_12_0, MIC_STACK_ret_12_0,
       MIC_WCAREG_wca_12_0;

  not not_1 (not_1_out, LCSN);
  not not_2 (not_2_out, CLFFN);
  nand nand_1 (nand_1_out, CSRASEL_1_0[0], CSXRF3);
  not not_3 (not_3_out, CSRASEL_1_0[1]);
  nand nand_2 (nand_2_out, CSXRF3, not_3_out);
  not not_4 (not_4_out, CSVECT);
  not not_5 (not_5_out, CSXRF3);
  and and_1 (and_1_out, not_5_out, IR_6_0[6]);
  D_Flip_Flop d_ff_1 (.D(nand_2_out), .clk(MCLK), .Q(d_ff_1_q));  // open: Qn, preset, reset
  D_Flip_Flop d_ff_2 (.D(nand_1_out), .clk(MCLK), .Q(d_ff_2_q));  // open: Qn, preset, reset
  not not_6 (not_6_out, ILCSN);
  not not_7 (LCSN, not_6_out);
  nand nand_3 (nand_3_out, LCSN, EWCAN);
  CGA_MIC_CSEL CSEL (
    .DZD(DZD), .LCZ(LCZ), .IRQ(IRQ), .RESTR(RESTR), .CFETCH(CFETCH), .OOD(OOD), .SPARE(SPARE), .COND(COND),
    .OVF(OVF), .CRY(CRY), .F11(F11), .F15(F15), .ZF(ZF), .STP(STP), .ALUCLK(ALUCLK),
    .TSEL_3_0(CONDREG_tsel_3_0), .CONDN(CSEL_condn));
  // Probe on CONDREG_tsel_3_0
  not not_8 (not_8_out, CSLOOP);
  // Probe on CSBIT_15_0[11:0]
  MUX41P M_LAA_3 (
    .D0(CSBIT_15_0[12]), .D1(PIL_3_0[0]), .D2(and_1_out), .D3(LC_3_0[3]), .A(CSRASEL_1_0[0]),
    .B(CSRASEL_1_0[1]), .Z(M_LAA_3_z));
  CGA_MIC_INCOUNT MIC_INCOUNT (
    .CD0(CD_15_0[0]), .LWCAN(LWCAN), .EC(not_1_out), .MRN(MRN), .CD1(CD_15_0[1]), .MCLK(MCLK),
    .CSWAN0(CSWAN_1_0[0]), .CSWAN1(CSWAN_1_0[1]));
  M169C LC_HI (
    .A(CD_15_0[4]), .B(CD_15_0[5]), .C(CD_15_0[5]), .D(CD_15_0[5]), .NL(LDLCN), .CP(MCLK), .PN(PN), .TN(TN),
    .UP(not_11_out), .QA(LC_HI_qa), .QB(LC_HI_qb), .QC(LC_HI_qc), .QD(LC_HI_qd), .CON(LC_HI_con));
  M169C LC_LO (
    .A(CD_15_0[0]), .B(CD_15_0[1]), .C(CD_15_0[2]), .D(CD_15_0[3]), .NL(LDLCN), .CP(MCLK), .PN(PN),
    .TN(1'b0), .UP(not_11_out), .QA(LC_3_0[0]), .QB(LC_3_0[1]), .QC(LC_3_0[2]), .QD(LC_3_0[3]), .CON(TN));
  D_Flip_Flop d_ff_3 (.D(CSEL_condn), .clk(MCLK), .Qn(COND));  // open: Q, preset, reset
  D_Flip_Flop d_ff_4 (.D(CSLOOP), .clk(MCLK), .Q(MIC_LOOP));  // open: Qn, preset, reset
  not not_9 (UPN, LC_HI_qd);
  MUX21L M_RF1 (.A(d_ff_1_q), .B(CSWAN_1_0[1]), .S(nand_3_out), .ZN(RF_1_0[1]));
  MUX21L M_RF0 (.A(d_ff_2_q), .B(CSWAN_1_0[0]), .S(nand_3_out), .ZN(RF_1_0[0]));
  not not_10 (not_10_out, CSECOND);
  MUX34P ILC_MUX (
    .D00(IR_6_0[0]), .D10(LAA_3_0[0]), .D20(CSBIT_15_0[0]), .D01(IR_6_0[1]), .D11(LAA_3_0[1]),
    .D21(CSBIT_15_0[1]), .D02(IR_6_0[2]), .D12(LAA_3_0[2]), .D22(CSBIT_15_0[2]), .D03(IR_6_0[3]),
    .D13(LAA_3_0[3]), .D23(CSBIT_15_0[3]), .A(CSMIS0), .B(not_4_out), .Z0(ILC_MUX_z0[0]), .Z1(ILC_MUX_z0[1]),
    .Z2(ILC_MUX_z0[2]), .Z3(ILC_MUX_z0[3]));
  L8 IRLATCH (
    .A(CD_15_0[0]), .B(CD_15_0[1]), .C(CD_15_0[2]), .D(CD_15_0[3]), .E(CD_15_0[4]), .F(CD_15_0[5]),
    .G(CD_15_0[6]), .L(LDIRV), .QA(IR_6_0[0]), .QB(IR_6_0[1]), .QC(IR_6_0[2]), .QD(IR_6_0[3]),
    .QE(IR_6_0[4]), .QF(IR_6_0[5]), .QG(IR_6_0[6]));  // open: H, QAN, QBN, QCN, QDN, QEN, QFN, QGN, QH, QHN
  or or_1 (or_1_out, CSWAN_1_0[1], CSWAN_1_0[0]);
  not not_11 (not_11_out, UPN);
  nand nand_4 (CIN, or_1_out, not_1_out, 1'b1);
  // Probe on LCC_3_0
  CGA_MIC_CONDREG CONDREG (
    .CSBIT_11_0(CSBIT_15_0[11:0]), .CSSCOND(CSCOND), .MCLK(MCLK), .LCSN(LCSN), .LCC_3_0(LCC_3_0),
    .FS_6_3(CONDREG_fs_6_3), .TSEL_3_0(CONDREG_tsel_3_0), .ACONDN(ACONDN));
  nor nor_1 (nor_1_out, LC_HI_qa, LC_HI_qb, not_2_out);
  MUX41P M_LAA_2 (
    .D0(CSBIT_15_0[13]), .D1(PIL_3_0[1]), .D2(IR_6_0[5]), .D3(LC_3_0[2]), .A(CSRASEL_1_0[0]),
    .B(CSRASEL_1_0[1]), .Z(M_LAA_2_z));
  or or_2 (or_2_out, LC_HI_con, not_11_out);
  nand nand_5 (nand_5_out, LCSN, not_8_out, not_10_out);
  and and_2 (and_2_out, CSEL_condn, not_8_out, LCSN, CSECOND);
  nand nand_6 (nand_6_out, CSEL_condn, nand_5_out);
  nand nand_7 (PN, or_2_out, MIC_LOOP, 1'b1);
  CMP4 LC_CMP (
    .A0(LCC_3_0[0]), .A1(LCC_3_0[1]), .A2(LCC_3_0[2]), .A3(LCC_3_0[3]), .B0(LC_3_0[0]), .B1(LC_3_0[1]),
    .B2(LC_3_0[2]), .B3(LC_3_0[3]), .AEB(LC_CMP_aeb));  // open: AGB, ALB
  and and_3 (and_3_out, nand_6_out, CSTS_6_3[3]);
  and and_4 (and_4_out, and_2_out, CONDREG_fs_6_3[3]);
  and and_5 (and_5_out, nand_6_out, CSTS_6_3[2]);
  and and_6 (and_6_out, and_2_out, CONDREG_fs_6_3[2]);
  and and_7 (and_7_out, nand_6_out, CSTS_6_3[1]);
  and and_8 (and_8_out, and_2_out, CONDREG_fs_6_3[1]);
  and and_9 (and_9_out, nand_6_out, CSTS_6_3[0]);
  and and_10 (and_10_out, and_2_out, CONDREG_fs_6_3[0]);
  not not_12 (not_12_out, MCLK);
  not not_13 (not_13_out, MCLK);
  CGA_MIC_IINC MIC_IINC (.IW_12_0(MIC_MASEL_iw_12_0), .CIN(CIN), .NEXT_12_0(MIC_IINC_next_12_0));
  nand nand_8 (LCZN, nor_1_out, LC_CMP_aeb);
  MUX41P M_LAA_1 (
    .D0(CSBIT_15_0[14]), .D1(PIL_3_0[2]), .D2(IR_6_0[4]), .D3(LC_3_0[1]), .A(CSRASEL_1_0[0]),
    .B(CSRASEL_1_0[1]), .Z(M_LAA_1_z));
  nand nand_9 (nand_9_out, LCSN, CSEL_condn, CSLOOP);
  nor nor_2 (nor_2_out, and_3_out, and_4_out);
  nor nor_3 (nor_3_out, and_5_out, and_6_out);
  nor nor_4 (nor_4_out, and_7_out, and_8_out);
  nor nor_5 (nor_5_out, and_9_out, and_10_out);
  not not_14 (LCZ_t, LCZN);
  D_Flip_Flop #(.trigger("falling")) d_ff_5 (.D(nor_4_out), .clk(MCLK), .Qn(SC_6_3[1]));  // open: Q, preset, reset
  D_Flip_Flop d_ff_6 (.D(ZF), .clk(MCLK), .Q(d_ff_6_q), .reset(not_17_out));  // open: Qn, preset
  D_Flip_Flop d_ff_7 (.D(CSALUI8), .clk(MCLK), .Qn(d_ff_7_qn));  // open: Q, preset, reset
  nor nor_6 (nor_6_out, ~LCSN, ~nor_2_out);  // NOR_Gate
  nor nor_7 (nor_7_out, ~nand_9_out, ~nor_3_out);  // NOR_Gate
  CGA_MIC_STACK MIC_STACK (
    .SC3(SC_6_3[0]), .SC4(SC_6_3[1]), .NEXT_12_0(MIC_IINC_next_12_0), .SCLKN(not_13_out), .MCLK(MCLK),
    .DEEP(DEEP), .RET_12_0(MIC_STACK_ret_12_0));
  not not_15 (SC_6_3[3], nor_6_out);
  not not_16 (SC_6_3[2], nor_7_out);
  D_Flip_Flop #(.trigger("falling")) d_ff_8 (.D(nor_5_out), .clk(MCLK), .Qn(SC_6_3[0]));  // open: Q, preset, reset
  MUX41P M_LAA_0 (
    .D0(CSBIT_15_0[15]), .D1(PIL_3_0[3]), .D2(IR_6_0[3]), .D3(LC_3_0[0]), .A(CSRASEL_1_0[0]),
    .B(CSRASEL_1_0[1]), .Z(M_LAA_0_z));
  and and_11 (and_11_out, d_ff_6_q, ZF);
  not not_17 (not_17_out, CLFFN);
  nor nor_8 (nor_8_out, OOD, MI);
  nor nor_9 (nor_9_out, and_11_out, DZD, 1'b0);
  R41P LAA_REG (
    .A(M_LAA_0_z), .B(M_LAA_1_z), .C(M_LAA_2_z), .D(M_LAA_3_z), .CP(MCLK), .QAN(LAA_REG_qan),
    .QBN(LAA_REG_qbn), .QCN(LAA_REG_qcn), .QDN(LAA_REG_qdn));  // open: QA, QB, QC, QD
  CGA_MIC_MASEL MIC_MASEL (
    .JMP_3_0(ILC_MUX_z0), .CSBIT_11_0(CSBIT_15_0[11:0]), .RET_12_0(MIC_STACK_ret_12_0),
    .NEXT_12_0(MIC_IINC_next_12_0), .SC5(SC_6_3[2]), .SC6(SC_6_3[3]), .CSBIT20(CSBIT20), .MCLK(MCLK),
    .MRN(MRN), .MCLKN(not_12_out), .IW_12_0(MIC_MASEL_iw_12_0), .W_12_0(MIC_MASEL_w_12_0));
  not not_18 (LAA_3_0[0], LAA_REG_qan);
  not not_19 (LAA_3_0[1], LAA_REG_qbn);
  not not_20 (LAA_3_0[2], LAA_REG_qcn);
  not not_21 (LAA_3_0[3], LAA_REG_qdn);
  SCAN_WITH_SET_N OOD_FF (.S(CLFFN), .D(nor_8_out), .TE(d_ff_7_qn), .TI(OOD_FF_q), .CLK(MCLK), .Q(OOD_FF_q), .QN(OOD));
  SCAN_WITH_SET_N DZD_FF (.S(CLFFN), .D(nor_9_out), .TE(d_ff_7_qn), .TI(DZD_FF_q), .CLK(MCLK), .Q(DZD_FF_q), .QN(DZD));
  MUX41P M_LBA_3 (
    .D0(CSRB_3_0[3]), .D1(1'b0), .D2(1'b0), .D3(LC_3_0[3]), .A(CSRBSEL_1_0[0]), .B(CSRBSEL_1_0[1]),
    .Z(M_LBA_3_z));
  CGA_MIC_WCAREG MIC_WCAREG (
    .LWCAN(LWCAN), .LCSN(LCSN), .MCLK(MCLK), .CD_15_0(CD_15_0), .WCSN(WCSN), .WCA_12_0(MIC_WCAREG_wca_12_0));
  MUX41P M_LBA_2 (
    .D0(CSRB_3_0[2]), .D1(IR_6_0[2]), .D2(IR_6_0[5]), .D3(LC_3_0[2]), .A(CSRBSEL_1_0[0]), .B(CSRBSEL_1_0[1]),
    .Z(M_LBA_2_z));
  MUX41P M_LBA_1 (
    .D0(CSRB_3_0[1]), .D1(IR_6_0[1]), .D2(IR_6_0[4]), .D3(LC_3_0[1]), .A(CSRBSEL_1_0[0]), .B(CSRBSEL_1_0[1]),
    .Z(M_LBA_1_z));
  CGA_MIC_IPOS MIC_IPOS (
    .W_12_0(MIC_MASEL_w_12_0), .WCA_12_0(MIC_WCAREG_wca_12_0), .CD_15_0(CD_15_0), .TVEC_3_0(TVEC_3_0),
    .TRAPN(TRAPN), .MAPN(MAPN), .EWCAN(EWCAN), .MA_12_0(MA_12_0));
  MUX41P M_LBA_0 (
    .D0(CSRB_3_0[0]), .D1(IR_6_0[0]), .D2(IR_6_0[3]), .D3(LC_3_0[0]), .A(CSRBSEL_1_0[0]), .B(CSRBSEL_1_0[1]),
    .Z(M_LBA_0_z));
  R41P LBA_REG (
    .A(M_LBA_0_z), .B(M_LBA_1_z), .C(M_LBA_2_z), .D(M_LBA_3_z), .CP(MCLK), .QAN(LBA_REG_qan),
    .QBN(LBA_REG_qbn), .QCN(LBA_REG_qcn), .QDN(LBA_REG_qdn));  // open: QA, QB, QC, QD
  not not_22 (LBA_3_0[0], LBA_REG_qan);
  not not_23 (LBA_3_0[1], LBA_REG_qbn);
  not not_24 (LBA_3_0[2], LBA_REG_qcn);
  not not_25 (LBA_3_0[3], LBA_REG_qdn);

  // Other names for the same wires on the sheet: CSBIT_3_0[3:0] = CSBIT_15_0[3:0];
  //   CSBIT_11_0[11:0] = CSBIT_15_0[11:0]; CSBIT_15_12[3:0] = CSBIT_15_0[15:12]; SC3 = SC_6_3[0]; SC4 = SC_6_3[1];
  //   SC5 = SC_6_3[2]; SC6 = SC_6_3[3]

  // Notes on the sheet:
  //   Notes:
  //   Page 10-14 CGA_MIC (Sheet 1-4)
  //   Sheet 1/4 ->
  //   Sheet 2/4 ->
  //   Sheet 3/4 ->
  //   CSBIT = Microinstruction Bits
  //   LC = Loop Counter
  //   RF(1:0) = Register File selector
  //   Sheet 4/4 ->
  //   IR = Instruction Register (Current MacroInstruction)
  //   CSRASEL0
  //   CD0
  //   LC3
  //   CD3
  //   PIL3
  //   IR6
  //   CSRASEL1
  //   CD0
  //   CD6
  //   CD5
  //   CD4
  //   CD5
  //   CD0
  //   CD1
  //   CD2
  //   CSBIT15
  //   LCSN
  //   IR0
  //   LAA0
  //   CSBIT0
  //   IR3
  //   LAA3
  //   CSBIT3
  //   PIL2
  //   IR5
  //   LC2
  //   A
  //   B
  //   C
  //   D
  //   IR0
  //   IR1
  //   IR2
  //   IR3
  //   IR4
  //   IR5
  //   IR6
  //   LC0
  //   LC1
  //   LC2
  //   LC3
  //   CSBIT14
  //   RF1
  //   RF0
  //   A
  //   B
  //   C
  //   D
  //   IR4
  //   LC1
  //   PIL1
  //   EFALSE
  //   CSTS6
  //   FS6
  //   CSTS5
  //   FS5
  //   CSTS4
  //   FS4
  //   CSTS3
  //   FS3
  //   CSBIT13
  //   ETRUE
  //   CSALUI8
  //   ZF
  //   MCLK
  //   MCLKN
  //   SCLKN
  //   G8C5
  //   PIL0
  //   IR3
  //   LC0
  //   CSBIT12
  //   SC4
  //   SC3
  //   LC3
  //   CSRB3
  //   LAA2
  //   LAA0
  //   LAA1
  //   LAA3
  //   DZD
  //   OOD
  //   DZD
  //   IR5
  //   LC2
  //   IR2
  //   CSRB2
  //   IR4
  //   LC1
  //   Write Control Store Address - 13-bit address for writing to control store
  //   IR1
  //   CSRB1
  //   Working Address
  //   LC0
  //   IR3
  //   IR0
  //   CSRB0
  //   Microcode Address
  //   LBA0
  //   LBA1
  //   LBA2
  //   LBA3
endmodule

module CGA_MIC_CSEL (
  input  DZD,
  input  LCZ,
  input  IRQ,
  input  RESTR,
  input  CFETCH,
  input  OOD,
  input  SPARE,
  input  COND,
  input  OVF,
  input  CRY,
  input  F11,
  input  F15,
  input  ZF,
  input  STP,
  input  ALUCLK,
  input  [3:0] TSEL_3_0,
  output CONDN
);

  wire multiplexer_1_out, multiplexer_2_out, multiplexer_3_out, not_1_out, not_2_out;

  Multiplexer #(.select(3)) multiplexer_1 (
    .in0(DZD), .in1(LCZ), .in2(IRQ), .in3(RESTR), .in4(CFETCH), .in5(OOD), .in6(SPARE), .in7(COND),
    .out(multiplexer_1_out), .sel(TSEL_3_0[2:0]));
  Multiplexer #(.select(3)) multiplexer_2 (
    .in0(1'b0), .in1(1'b0), .in2(OVF), .in3(CRY), .in4(F11), .in5(F15), .in6(ZF), .in7(STP),
    .out(multiplexer_2_out), .sel(TSEL_3_0[2:0]));
  Multiplexer multiplexer_3 (
    .in0(multiplexer_1_out), .in1(multiplexer_2_out), .out(multiplexer_3_out), .sel(TSEL_3_0[3]));
  not not_1 (not_1_out, multiplexer_3_out);
  not not_2 (not_2_out, ALUCLK);
  LATCH CSEL_LATCH (.D(not_1_out), .ENABLE(not_2_out), .Q(CONDN));  // open: QN
endmodule

module CGA_MIC_CONDREG (
  input  [11:0] CSBIT_11_0,
  input  CSSCOND,
  input  MCLK,
  input  LCSN,
  output [3:0] LCC_3_0,
  output [3:0] FS_6_3,
  output [3:0] TSEL_3_0,
  output ACONDN
);

  wire CSBIT4_q, CSBIT5_q, CSBIT6_q, CSBIT7_q, CSBIT7_qn, nand_2_out, nand_4_out, nand_5_out, not_1_out,
       xnor_1_out;

  not not_1 (not_1_out, CSSCOND);
  SCAN_FF CSBIT11 (.D(CSBIT_11_0[11]), .TE(not_1_out), .TI(LCC_3_0[3]), .CLK(MCLK), .Q(LCC_3_0[3]));  // open: QN
  SCAN_FF CSBIT10 (.D(CSBIT_11_0[10]), .TE(not_1_out), .TI(LCC_3_0[2]), .CLK(MCLK), .Q(LCC_3_0[2]));  // open: QN
  SCAN_FF CSBIT9 (.D(CSBIT_11_0[9]), .TE(not_1_out), .TI(LCC_3_0[1]), .CLK(MCLK), .Q(LCC_3_0[1]));  // open: QN
  SCAN_FF CSBIT8 (.D(CSBIT_11_0[8]), .TE(not_1_out), .TI(LCC_3_0[0]), .CLK(MCLK), .Q(LCC_3_0[0]));  // open: QN
  SCAN_FF CSBIT7 (.D(CSBIT_11_0[7]), .TE(not_1_out), .TI(CSBIT7_q), .CLK(MCLK), .Q(CSBIT7_q), .QN(CSBIT7_qn));
  nand nand_1 (TSEL_3_0[3], LCSN, CSBIT7_qn);
  SCAN_FF CSBIT6 (.D(CSBIT_11_0[6]), .TE(not_1_out), .TI(CSBIT6_q), .CLK(MCLK), .Q(CSBIT6_q));  // open: QN
  and and_1 (TSEL_3_0[2], LCSN, CSBIT6_q);
  xnor xnor_1 (xnor_1_out, TSEL_3_0[2], TSEL_3_0[1]);
  nand nand_2 (nand_2_out, xnor_1_out, nand_4_out);
  nand nand_3 (ACONDN, nand_2_out, TSEL_3_0[3]);
  SCAN_FF CSBIT5 (.D(CSBIT_11_0[5]), .TE(not_1_out), .TI(CSBIT5_q), .CLK(MCLK), .Q(CSBIT5_q));  // open: QN
  and and_2 (TSEL_3_0[1], LCSN, CSBIT5_q);
  nand nand_4 (nand_4_out, TSEL_3_0[1], nand_5_out);
  SCAN_FF CSBIT4 (.D(CSBIT_11_0[4]), .TE(not_1_out), .TI(CSBIT4_q), .CLK(MCLK), .Q(CSBIT4_q));  // open: QN
  nand nand_5 (nand_5_out, LCSN, CSBIT4_q);
  not not_2 (TSEL_3_0[0], nand_5_out);
  SCAN_FF CSBIT3 (.D(CSBIT_11_0[3]), .TE(not_1_out), .TI(FS_6_3[3]), .CLK(MCLK), .Q(FS_6_3[3]));  // open: QN
  SCAN_FF CSBIT2 (.D(CSBIT_11_0[2]), .TE(not_1_out), .TI(FS_6_3[2]), .CLK(MCLK), .Q(FS_6_3[2]));  // open: QN
  SCAN_FF CSBIT1 (.D(CSBIT_11_0[1]), .TE(not_1_out), .TI(FS_6_3[1]), .CLK(MCLK), .Q(FS_6_3[1]));  // open: QN
  SCAN_FF CSBIT0 (.D(CSBIT_11_0[0]), .TE(not_1_out), .TI(FS_6_3[0]), .CLK(MCLK), .Q(FS_6_3[0]));  // open: QN

  // Notes on the sheet:
  //   Page  15 - CGA_MIC_CONDREG
  //   Tested ?
  //   LCC3
  //   LCC2
  //   LCC1
  //   LCC0
  //   TSEL3
  //   TSEL2
  //   TSEL1
  //   TSEL0
  //   FS6
  //   FS5
  //   FS4
  //   FS3
endmodule

module CGA_MIC_IINC (
  input  [12:0] IW_12_0,
  input  CIN,
  output [12:0] NEXT_12_0
);

  wire adder_1_cout, adder_2_cout, adder_3_cout, adder_4_cout, adder_6_cout, adder_7_cout, adder_8_cout,
       adder_9_cout, adder_11_cout, adder_12_cout, nand_1_out, nand_2_out, not_1_out, not_2_out;

  Adder #(.width(1)) adder_1 (.a(IW_12_0[0]), .b(CIN), .out(NEXT_12_0[0]), .cout(adder_1_cout));  // open: cin
  Adder #(.width(1)) adder_2 (.a(IW_12_0[1]), .b(adder_1_cout), .out(NEXT_12_0[1]), .cout(adder_2_cout));  // open: cin
  Adder #(.width(1)) adder_3 (.a(IW_12_0[2]), .b(adder_2_cout), .out(NEXT_12_0[2]), .cout(adder_3_cout));  // open: cin
  Adder #(.width(1)) adder_4 (.a(IW_12_0[3]), .b(adder_3_cout), .out(NEXT_12_0[3]), .cout(adder_4_cout));  // open: cin
  Adder #(.width(1)) adder_5 (.a(IW_12_0[4]), .b(adder_4_cout), .out(NEXT_12_0[4]));  // open: cin, cout
  nand nand_1 (nand_1_out, IW_12_0[4], IW_12_0[3], IW_12_0[2], IW_12_0[1], IW_12_0[0], CIN);
  Adder #(.width(1)) adder_6 (.a(IW_12_0[5]), .b(not_1_out), .out(NEXT_12_0[5]), .cout(adder_6_cout));  // open: cin
  not not_1 (not_1_out, nand_1_out);
  Adder #(.width(1)) adder_7 (.a(IW_12_0[6]), .b(adder_6_cout), .out(NEXT_12_0[6]), .cout(adder_7_cout));  // open: cin
  Adder #(.width(1)) adder_8 (.a(IW_12_0[7]), .b(adder_7_cout), .out(NEXT_12_0[7]), .cout(adder_8_cout));  // open: cin
  Adder #(.width(1)) adder_9 (.a(IW_12_0[8]), .b(adder_8_cout), .out(NEXT_12_0[8]), .cout(adder_9_cout));  // open: cin
  Adder #(.width(1)) adder_10 (.a(IW_12_0[9]), .b(adder_9_cout), .out(NEXT_12_0[9]));  // open: cin, cout
  nand nand_2 (nand_2_out, IW_12_0[9], IW_12_0[8], IW_12_0[7], IW_12_0[6], IW_12_0[5], not_1_out);
  not not_2 (not_2_out, nand_2_out);
  Adder #(.width(1)) adder_11 (.a(IW_12_0[10]), .b(not_2_out), .out(NEXT_12_0[10]), .cout(adder_11_cout));  // open: cin
  Adder #(.width(1)) adder_12 (
    .a(IW_12_0[11]), .b(adder_11_cout), .out(NEXT_12_0[11]), .cout(adder_12_cout));  // open: cin
  Adder #(.width(1)) adder_13 (.a(IW_12_0[12]), .b(adder_12_cout), .out(NEXT_12_0[12]));  // open: cin, cout

  // Notes on the sheet:
  //   Page  16 - CGA_MIC_IINC
  //   Tested manually OK 19.05.23 RH
endmodule

module CGA_MIC_STACK (
  input  SC3,
  input  SC4,
  input  [12:0] NEXT_12_0,
  input  SCLKN,
  input  MCLK,
  output DEEP,
  output [12:0] RET_12_0
);

  wire nand_1_out, nand_2_out, nor_1_out, not_1_out, not_2_out, not_3_out, not_4_out, not_5_out, not_6_out,
       not_7_out, not_8_out;

  // Probe on RET_12_0
  not not_1 (not_1_out, MCLK);
  not not_2 (not_2_out, SC3);
  not not_3 (not_3_out, SC3);
  not not_4 (not_4_out, SC4);
  not not_5 (not_5_out, not_2_out);
  nand nand_1 (nand_1_out, not_3_out, SC4);
  nand nand_2 (nand_2_out, not_3_out, not_4_out);
  nor nor_1 (nor_1_out, not_3_out, not_4_out);
  not not_6 (not_6_out, nand_1_out);
  not not_7 (not_7_out, nand_2_out);
  not not_8 (not_8_out, nor_1_out);
  CGA_MIC_STACK_BIT12 Bit12 (
    .STIN(NEXT_12_0[12]), .MCLK(MCLK), .S3N(not_3_out), .S4S3N(not_6_out), .S4NS3N(not_7_out),
    .S3(not_5_out), .LOAD(not_8_out), .SCLKN(not_1_out), .STOUT(RET_12_0[12]), .DEEP(DEEP));
  CGA_MIC_STACK_BIT Bit11 (
    .STIN(NEXT_12_0[11]), .CLK(MCLK), .S3N(not_3_out), .S4S3N(not_6_out), .S4NS3N(not_7_out), .S3(not_5_out),
    .LOAD(not_8_out), .CLKN(not_1_out), .STOUT(RET_12_0[11]));
  CGA_MIC_STACK_BIT Bit10 (
    .STIN(NEXT_12_0[10]), .CLK(MCLK), .S3N(not_3_out), .S4S3N(not_6_out), .S4NS3N(not_7_out), .S3(not_5_out),
    .LOAD(not_8_out), .CLKN(not_1_out), .STOUT(RET_12_0[10]));
  CGA_MIC_STACK_BIT Bit9 (
    .STIN(NEXT_12_0[9]), .CLK(MCLK), .S3N(not_3_out), .S4S3N(not_6_out), .S4NS3N(not_7_out), .S3(not_5_out),
    .LOAD(not_8_out), .CLKN(not_1_out), .STOUT(RET_12_0[9]));
  CGA_MIC_STACK_BIT Bit8 (
    .STIN(NEXT_12_0[8]), .CLK(MCLK), .S3N(not_3_out), .S4S3N(not_6_out), .S4NS3N(not_7_out), .S3(not_5_out),
    .LOAD(not_8_out), .CLKN(not_1_out), .STOUT(RET_12_0[8]));
  CGA_MIC_STACK_BIT Bit7 (
    .STIN(NEXT_12_0[7]), .CLK(MCLK), .S3N(not_3_out), .S4S3N(not_6_out), .S4NS3N(not_7_out), .S3(not_5_out),
    .LOAD(not_8_out), .CLKN(not_1_out), .STOUT(RET_12_0[7]));
  CGA_MIC_STACK_BIT Bit6 (
    .STIN(NEXT_12_0[6]), .CLK(MCLK), .S3N(not_3_out), .S4S3N(not_6_out), .S4NS3N(not_7_out), .S3(not_5_out),
    .LOAD(not_8_out), .CLKN(not_1_out), .STOUT(RET_12_0[6]));
  CGA_MIC_STACK_BIT Bit5 (
    .STIN(NEXT_12_0[5]), .CLK(MCLK), .S3N(not_3_out), .S4S3N(not_6_out), .S4NS3N(not_7_out), .S3(not_5_out),
    .LOAD(not_8_out), .CLKN(not_1_out), .STOUT(RET_12_0[5]));
  CGA_MIC_STACK_BIT Bit4 (
    .STIN(NEXT_12_0[4]), .CLK(MCLK), .S3N(not_3_out), .S4S3N(not_6_out), .S4NS3N(not_7_out), .S3(not_5_out),
    .LOAD(not_8_out), .CLKN(not_1_out), .STOUT(RET_12_0[4]));
  CGA_MIC_STACK_BIT Bit3 (
    .STIN(NEXT_12_0[3]), .CLK(MCLK), .S3N(not_3_out), .S4S3N(not_6_out), .S4NS3N(not_7_out), .S3(not_5_out),
    .LOAD(not_8_out), .CLKN(not_1_out), .STOUT(RET_12_0[3]));
  CGA_MIC_STACK_BIT Bit2 (
    .STIN(NEXT_12_0[2]), .CLK(MCLK), .S3N(not_3_out), .S4S3N(not_6_out), .S4NS3N(not_7_out), .S3(not_5_out),
    .LOAD(not_8_out), .CLKN(not_1_out), .STOUT(RET_12_0[2]));
  CGA_MIC_STACK_BIT Bit1 (
    .STIN(NEXT_12_0[1]), .CLK(MCLK), .S3N(not_3_out), .S4S3N(not_6_out), .S4NS3N(not_7_out), .S3(not_5_out),
    .LOAD(not_8_out), .CLKN(not_1_out), .STOUT(RET_12_0[1]));
  CGA_MIC_STACK_BIT Bit0 (
    .STIN(NEXT_12_0[0]), .CLK(MCLK), .S3N(not_3_out), .S4S3N(not_6_out), .S4NS3N(not_7_out), .S3(not_5_out),
    .LOAD(not_8_out), .CLKN(not_1_out), .STOUT(RET_12_0[0]));

  // Notes on the sheet:
  //   Page 17 - CGA_MIC_STACK (tested manually OK 19.05.23 RH)
  //   NEXT0
  //   NEXT12
  //   POP
  //   HOLD
  //   PUSH
  //   LOAD
  //   LOAD
  //   PUSH
  //   POP
  //   HOLD
  //   Function  (Simulates the 74S482)
  //   S3
  //   S4
  //   L
  //   H
  //   H
  //   H
  //   H
  //   L
  //   L
  //   L
endmodule

module CGA_MIC_STACK_BIT (
  input  STIN,
  input  CLK,
  input  S3N,
  input  S4S3N,
  input  S4NS3N,
  input  S3,
  input  LOAD,
  input  CLKN,
  output STOUT
);

  wire d_ff_1_q, nand_1_out, nand_2_out, nand_3_out, nand_4_out, nand_5_out, or_1_out, or_2_out, or_3_out,
       or_4_out, or_5_out, SR44_1_qbn, SR44_1_qcn, SR44_1_qd, SR44_1_qdn;

  D_Flip_Flop d_ff_1 (.D(STIN), .clk(CLK), .Q(d_ff_1_q));  // open: Qn, preset, reset
  nand nand_1 (nand_1_out, d_ff_1_q, S4S3N);
  nand nand_2 (nand_2_out, STOUT, S4NS3N);
  or or_1 (or_1_out, SR44_1_qbn, S3N);
  or or_2 (or_2_out, S3, SR44_1_qbn);
  or or_3 (or_3_out, S3N, SR44_1_qcn);
  or or_4 (or_4_out, S3, SR44_1_qcn);
  or or_5 (or_5_out, S3N, SR44_1_qdn);
  nand nand_3 (nand_3_out, or_1_out, nand_1_out, nand_2_out);
  nand nand_4 (nand_4_out, or_2_out, or_3_out);
  nand nand_5 (nand_5_out, or_4_out, or_5_out);
  SR44 SR44_1 (
    .SI(d_ff_1_q), .A(nand_3_out), .B(nand_4_out), .C(nand_5_out), .D(SR44_1_qd), .L(LOAD), .CP(CLKN),
    .QA(STOUT), .QBN(SR44_1_qbn), .QCN(SR44_1_qcn), .QD(SR44_1_qd), .QDN(SR44_1_qdn));  // open: QAN, QB, QC

  // Notes on the sheet:
  //   S4SN3=1 AND LOAD=1 => HOLD
  //   A
  //   B
  //   C
  //   D
endmodule

module CGA_MIC_STACK_BIT12 (
  input  STIN,
  input  MCLK,
  input  S3N,
  input  S4S3N,
  input  S4NS3N,
  input  S3,
  input  LOAD,
  input  SCLKN,
  output STOUT,
  output DEEP
);

  wire d_ff_1_q, nand_1_out, nand_2_out, nand_3_out, nand_4_out, nand_5_out, or_1_out, or_2_out, or_3_out,
       or_4_out, or_5_out, SR44_2_qbn, SR44_2_qcn, SR44_2_qdn;

  D_Flip_Flop d_ff_1 (.D(STIN), .clk(MCLK), .Q(d_ff_1_q));  // open: Qn, preset, reset
  nand nand_1 (nand_1_out, d_ff_1_q, S4S3N);
  nand nand_2 (nand_2_out, STOUT, S4NS3N);
  or or_1 (or_1_out, SR44_2_qbn, S3N);
  or or_2 (or_2_out, S3, SR44_2_qbn);
  or or_3 (or_3_out, S3N, SR44_2_qcn);
  or or_4 (or_4_out, S3, SR44_2_qcn);
  or or_5 (or_5_out, S3N, SR44_2_qdn);
  nand nand_3 (nand_3_out, or_1_out, nand_1_out, nand_2_out);
  nand nand_4 (nand_4_out, or_2_out, or_3_out);
  nand nand_5 (nand_5_out, or_4_out, or_5_out);
  SR44 SR44_2 (
    .SI(d_ff_1_q), .A(nand_3_out), .B(nand_4_out), .C(nand_5_out), .D(DEEP), .L(LOAD), .CP(SCLKN),
    .QA(STOUT), .QBN(SR44_2_qbn), .QCN(SR44_2_qcn), .QD(DEEP), .QDN(SR44_2_qdn));  // open: QAN, QB, QC

  // Notes on the sheet:
  //   S4SN3=1 AND LOAD=1 => HOLD
  //   A
  //   B
  //   C
  //   D
endmodule

module CGA_MIC_MASEL (
  input  [3:0] JMP_3_0,
  input  [11:0] CSBIT_11_0,
  input  [12:0] RET_12_0,
  input  [12:0] NEXT_12_0,
  input  SC5,
  input  SC6,
  input  CSBIT20,
  input  MCLK,
  input  MRN,
  input  MCLKN,
  output [12:0] IW_12_0,
  output [12:0] W_12_0
);

  wire [12:0] multiplexer_13_out;

  Multiplexer #(.select(2)) multiplexer_1 (
    .in0(CSBIT20), .in1(RET_12_0[12]), .in2(NEXT_12_0[12]), .in3(IW_12_0[12]), .out(multiplexer_13_out[12]),
    .sel({SC6, SC5}));
  Multiplexer #(.select(2)) multiplexer_2 (
    .in0(CSBIT_11_0[11]), .in1(RET_12_0[11]), .in2(NEXT_12_0[11]), .in3(IW_12_0[11]),
    .out(multiplexer_13_out[11]), .sel({SC6, SC5}));
  Multiplexer #(.select(2)) multiplexer_3 (
    .in0(CSBIT_11_0[10]), .in1(RET_12_0[10]), .in2(NEXT_12_0[10]), .in3(IW_12_0[10]),
    .out(multiplexer_13_out[10]), .sel({SC6, SC5}));
  Multiplexer #(.select(2)) multiplexer_4 (
    .in0(CSBIT_11_0[9]), .in1(RET_12_0[9]), .in2(NEXT_12_0[9]), .in3(IW_12_0[9]),
    .out(multiplexer_13_out[9]), .sel({SC6, SC5}));
  Multiplexer #(.select(2)) multiplexer_5 (
    .in0(CSBIT_11_0[8]), .in1(RET_12_0[8]), .in2(NEXT_12_0[8]), .in3(IW_12_0[8]),
    .out(multiplexer_13_out[8]), .sel({SC6, SC5}));
  Multiplexer #(.select(2)) multiplexer_6 (
    .in0(CSBIT_11_0[7]), .in1(RET_12_0[7]), .in2(NEXT_12_0[7]), .in3(IW_12_0[7]),
    .out(multiplexer_13_out[7]), .sel({SC6, SC5}));
  Multiplexer #(.select(2)) multiplexer_7 (
    .in0(CSBIT_11_0[6]), .in1(RET_12_0[6]), .in2(NEXT_12_0[6]), .in3(IW_12_0[6]),
    .out(multiplexer_13_out[6]), .sel({SC6, SC5}));
  Multiplexer #(.select(2)) multiplexer_8 (
    .in0(CSBIT_11_0[5]), .in1(RET_12_0[5]), .in2(NEXT_12_0[5]), .in3(IW_12_0[5]),
    .out(multiplexer_13_out[5]), .sel({SC6, SC5}));
  Multiplexer #(.select(2)) multiplexer_9 (
    .in0(CSBIT_11_0[4]), .in1(RET_12_0[4]), .in2(NEXT_12_0[4]), .in3(IW_12_0[4]),
    .out(multiplexer_13_out[4]), .sel({SC6, SC5}));
  Multiplexer #(.select(2)) multiplexer_10 (
    .in0(JMP_3_0[3]), .in1(RET_12_0[3]), .in2(NEXT_12_0[3]), .in3(IW_12_0[3]), .out(multiplexer_13_out[3]),
    .sel({SC6, SC5}));
  Multiplexer #(.select(2)) multiplexer_11 (
    .in0(JMP_3_0[2]), .in1(RET_12_0[2]), .in2(NEXT_12_0[2]), .in3(IW_12_0[2]), .out(multiplexer_13_out[2]),
    .sel({SC6, SC5}));
  Multiplexer #(.select(2)) multiplexer_12 (
    .in0(JMP_3_0[1]), .in1(RET_12_0[1]), .in2(NEXT_12_0[1]), .in3(IW_12_0[1]), .out(multiplexer_13_out[1]),
    .sel({SC6, SC5}));
  Multiplexer #(.select(2)) multiplexer_13 (
    .in0(JMP_3_0[0]), .in1(RET_12_0[0]), .in2(NEXT_12_0[0]), .in3(IW_12_0[0]), .out(multiplexer_13_out[0]),
    .sel({SC6, SC5}));
  L8 WL_HI (
    .A(multiplexer_13_out[12]), .B(multiplexer_13_out[11]), .C(multiplexer_13_out[10]),
    .D(multiplexer_13_out[9]), .E(multiplexer_13_out[8]), .F(multiplexer_13_out[7]),
    .G(multiplexer_13_out[6]), .H(multiplexer_13_out[5]), .L(MCLKN), .QA(W_12_0[12]), .QB(W_12_0[11]),
    .QC(W_12_0[10]), .QD(W_12_0[9]), .QE(W_12_0[8]), .QF(W_12_0[7]), .QG(W_12_0[6]), .QH(W_12_0[5]));  // open: QAN, QBN, QCN, QDN, QEN, QFN, QGN, QHN
  L8 WL_LO (
    .A(multiplexer_13_out[4]), .B(multiplexer_13_out[3]), .C(multiplexer_13_out[2]),
    .D(multiplexer_13_out[1]), .E(multiplexer_13_out[0]), .L(MCLKN), .QA(W_12_0[4]), .QB(W_12_0[3]),
    .QC(W_12_0[2]), .QD(W_12_0[1]), .QE(W_12_0[0]));  // open: F, G, H, QAN, QBN, QCN, QDN, QEN, QF, QFN, QG, QGN, QH, QHN
  CGA_MIC_MASEL_REPEAT MASEL_REPEAT (.REP_12_0(multiplexer_13_out), .MCLK(MCLK), .MPN(MRN), .IW_12_0(IW_12_0));

  // Other names for the same wires on the sheet: CSBIT_11_4[7:0] = CSBIT_11_0[11:4]

  // Notes on the sheet:
  //   A
  //   B
  //   CSBIT11
  //   CSBIT4
  //   RET12
  //   RET0
  //   NEXT12
  //   NEXT0
  //   IW12
  //   IW0
  //   REP12
  //   REP11
  //   REP10
  //   REP9
  //   REP8
  //   REP7
  //   REP6
  //   REP5
  //   REP4
  //   REP3
  //   REP2
  //   REP1
  //   REP0
  //   Working Address
endmodule

module CGA_MIC_MASEL_REPEAT (
  input  [12:0] REP_12_0,
  input  MCLK,
  input  MPN,
  output [12:0] IW_12_0
);

  wire not_1_out;

  not not_1 (not_1_out, MPN);
  D_Flip_Flop IWFF12 (.D(REP_12_0[12]), .clk(MCLK), .Q(IW_12_0[12]), .reset(not_1_out));  // open: Qn, preset
  D_Flip_Flop IWFF11 (.D(REP_12_0[11]), .clk(MCLK), .Q(IW_12_0[11]), .reset(not_1_out));  // open: Qn, preset
  D_Flip_Flop IWFF10 (.D(REP_12_0[10]), .clk(MCLK), .Q(IW_12_0[10]), .reset(not_1_out));  // open: Qn, preset
  D_Flip_Flop IWFF9 (.D(REP_12_0[9]), .clk(MCLK), .Q(IW_12_0[9]), .reset(not_1_out));  // open: Qn, preset
  D_Flip_Flop IWFF8 (.D(REP_12_0[8]), .clk(MCLK), .Q(IW_12_0[8]), .reset(not_1_out));  // open: Qn, preset
  D_Flip_Flop IWFF7 (.D(REP_12_0[7]), .clk(MCLK), .Q(IW_12_0[7]), .reset(not_1_out));  // open: Qn, preset
  D_Flip_Flop IWFF6 (.D(REP_12_0[6]), .clk(MCLK), .Q(IW_12_0[6]), .reset(not_1_out));  // open: Qn, preset
  D_Flip_Flop IWFF5 (.D(REP_12_0[5]), .clk(MCLK), .Q(IW_12_0[5]), .reset(not_1_out));  // open: Qn, preset
  D_Flip_Flop IWFF4 (.D(REP_12_0[4]), .clk(MCLK), .Q(IW_12_0[4]), .reset(not_1_out));  // open: Qn, preset
  D_Flip_Flop IWFF3 (.D(REP_12_0[3]), .clk(MCLK), .Q(IW_12_0[3]), .reset(not_1_out));  // open: Qn, preset
  D_Flip_Flop IWFF2 (.D(REP_12_0[2]), .clk(MCLK), .Q(IW_12_0[2]), .reset(not_1_out));  // open: Qn, preset
  D_Flip_Flop IWFF1 (.D(REP_12_0[1]), .clk(MCLK), .Q(IW_12_0[1]), .reset(not_1_out));  // open: Qn, preset
  D_Flip_Flop IWFF0 (.D(REP_12_0[0]), .clk(MCLK), .Q(IW_12_0[0]), .reset(not_1_out));  // open: Qn, preset

  // Notes on the sheet:
  //   Page 20 - CGA_MIC_MASEL_REPEAT
  //   REP12
  //   REP0
  //   IW0
  //   IW12
endmodule

module CGA_MIC_WCAREG (
  input  LWCAN,
  input  LCSN,
  input  MCLK,
  input  [15:0] CD_15_0,
  output WCSN,
  output [12:0] WCA_12_0
);

  wire not_1_out, WCAFF0_q, WCAFF1_q, WCAFF2_q, WCAFF3_q, WCAFF4_q, WCAFF5_q, WCAFF6_q, WCAFF7_q, WCAFF8_q,
       WCAFF9_q, WCAFF10_q, WCAFF11_q, WCSNFF_q;

  not not_1 (not_1_out, LWCAN);
  SCAN_FF WCSNFF (.D(WCSNFF_q), .TE(not_1_out), .TI(CD_15_0[15]), .CLK(MCLK), .Q(WCSNFF_q));  // open: QN
  SCAN_FF WCAFF12 (.D(WCA_12_0[12]), .TE(not_1_out), .TI(CD_15_0[14]), .CLK(MCLK), .Q(WCA_12_0[12]));  // open: QN
  nor nor_1 (WCSN, ~WCSNFF_q, ~LCSN);  // NOR_Gate
  SCAN_FF WCAFF11 (.D(WCAFF11_q), .TE(not_1_out), .TI(CD_15_0[13]), .CLK(MCLK), .Q(WCAFF11_q), .QN(WCA_12_0[11]));
  SCAN_FF WCAFF10 (.D(WCAFF10_q), .TE(not_1_out), .TI(CD_15_0[12]), .CLK(MCLK), .Q(WCAFF10_q), .QN(WCA_12_0[10]));
  SCAN_FF WCAFF9 (.D(WCAFF9_q), .TE(not_1_out), .TI(CD_15_0[11]), .CLK(MCLK), .Q(WCAFF9_q), .QN(WCA_12_0[9]));
  SCAN_FF WCAFF8 (.D(WCAFF8_q), .TE(not_1_out), .TI(CD_15_0[10]), .CLK(MCLK), .Q(WCAFF8_q), .QN(WCA_12_0[8]));
  SCAN_FF WCAFF7 (.D(WCAFF7_q), .TE(not_1_out), .TI(CD_15_0[9]), .CLK(MCLK), .Q(WCAFF7_q), .QN(WCA_12_0[7]));
  SCAN_FF WCAFF6 (.D(WCAFF6_q), .TE(not_1_out), .TI(CD_15_0[8]), .CLK(MCLK), .Q(WCAFF6_q), .QN(WCA_12_0[6]));
  SCAN_FF WCAFF5 (.D(WCAFF5_q), .TE(not_1_out), .TI(CD_15_0[7]), .CLK(MCLK), .Q(WCAFF5_q), .QN(WCA_12_0[5]));
  SCAN_FF WCAFF4 (.D(WCAFF4_q), .TE(not_1_out), .TI(CD_15_0[6]), .CLK(MCLK), .Q(WCAFF4_q), .QN(WCA_12_0[4]));
  SCAN_FF WCAFF3 (.D(WCAFF3_q), .TE(not_1_out), .TI(CD_15_0[5]), .CLK(MCLK), .Q(WCAFF3_q), .QN(WCA_12_0[3]));
  SCAN_FF WCAFF2 (.D(WCAFF2_q), .TE(not_1_out), .TI(CD_15_0[4]), .CLK(MCLK), .Q(WCAFF2_q), .QN(WCA_12_0[2]));
  SCAN_FF WCAFF1 (.D(WCAFF1_q), .TE(not_1_out), .TI(CD_15_0[3]), .CLK(MCLK), .Q(WCAFF1_q), .QN(WCA_12_0[1]));
  SCAN_FF WCAFF0 (.D(WCAFF0_q), .TE(not_1_out), .TI(CD_15_0[2]), .CLK(MCLK), .Q(WCAFF0_q), .QN(WCA_12_0[0]));

  // Notes on the sheet:
  //   CD(15:2)
  //   Page 21 - CGA_MIC_WGAREG
  //   CD15
  //   CD2
endmodule

module CGA_MIC_IPOS (
  input  [12:0] W_12_0,
  input  [12:0] WCA_12_0,
  input  [15:0] CD_15_0,
  input  [3:0] TVEC_3_0,
  input  TRAPN,
  input  MAPN,
  input  EWCAN,
  output [12:0] MA_12_0
);

  wire and_1_out, and_2_out, nand_1_out, not_1_out;
  wire [1:0] nand_2_out, not_3_out;

  not not_1 (not_1_out, EWCAN);
  nand nand_1 (nand_1_out, MAPN, not_1_out);
  nand nand_2 (nand_2_out[0], TRAPN, EWCAN, MAPN);
  nand nand_3 (nand_2_out[1], MAPN, TRAPN);
  and and_1 (and_1_out, MAPN, TRAPN);
  not not_2 (not_3_out[1], and_1_out);
  and and_2 (and_2_out, TRAPN, nand_1_out);
  not not_3 (not_3_out[0], and_2_out);
  Multiplexer #(.select(2)) multiplexer_1 (
    .in0(W_12_0[12]), .in1(WCA_12_0[12]), .in2(1'b1), .in3(1'b0), .out(MA_12_0[12]), .sel(nand_2_out));
  Multiplexer #(.select(2)) multiplexer_2 (
    .in0(W_12_0[11]), .in1(WCA_12_0[11]), .in2(1'b1), .in3(1'b0), .out(MA_12_0[11]), .sel(not_3_out));
  Multiplexer #(.select(2)) multiplexer_3 (
    .in0(W_12_0[10]), .in1(WCA_12_0[10]), .in2(1'b1), .in3(1'b0), .out(MA_12_0[10]), .sel(not_3_out));
  Multiplexer #(.select(2)) multiplexer_4 (
    .in0(W_12_0[9]), .in1(WCA_12_0[9]), .in2(CD_15_0[15]), .in3(1'b0), .out(MA_12_0[9]), .sel(not_3_out));
  Multiplexer #(.select(2)) multiplexer_5 (
    .in0(W_12_0[8]), .in1(WCA_12_0[8]), .in2(CD_15_0[14]), .in3(1'b0), .out(MA_12_0[8]), .sel(not_3_out));
  Multiplexer #(.select(2)) multiplexer_6 (
    .in0(W_12_0[7]), .in1(WCA_12_0[7]), .in2(CD_15_0[13]), .in3(1'b0), .out(MA_12_0[7]), .sel(not_3_out));
  Multiplexer #(.select(2)) multiplexer_7 (
    .in0(W_12_0[6]), .in1(WCA_12_0[6]), .in2(CD_15_0[12]), .in3(1'b0), .out(MA_12_0[6]), .sel(not_3_out));
  Multiplexer #(.select(2)) multiplexer_8 (
    .in0(W_12_0[5]), .in1(WCA_12_0[5]), .in2(CD_15_0[11]), .in3(1'b0), .out(MA_12_0[5]), .sel(not_3_out));
  Multiplexer #(.select(2)) multiplexer_9 (
    .in0(W_12_0[4]), .in1(WCA_12_0[4]), .in2(CD_15_0[10]), .in3(1'b0), .out(MA_12_0[4]), .sel(not_3_out));
  Multiplexer #(.select(2)) multiplexer_10 (
    .in0(W_12_0[3]), .in1(WCA_12_0[3]), .in2(CD_15_0[9]), .in3(TVEC_3_0[3]), .out(MA_12_0[3]), .sel(not_3_out));
  Multiplexer #(.select(2)) multiplexer_11 (
    .in0(W_12_0[2]), .in1(WCA_12_0[2]), .in2(CD_15_0[8]), .in3(TVEC_3_0[2]), .out(MA_12_0[2]), .sel(not_3_out));
  Multiplexer #(.select(2)) multiplexer_12 (
    .in0(W_12_0[1]), .in1(WCA_12_0[1]), .in2(CD_15_0[7]), .in3(TVEC_3_0[1]), .out(MA_12_0[1]), .sel(not_3_out));
  // Probe on not_3_out
  Multiplexer #(.select(2)) multiplexer_13 (
    .in0(W_12_0[0]), .in1(WCA_12_0[0]), .in2(CD_15_0[6]), .in3(TVEC_3_0[0]), .out(MA_12_0[0]), .sel(not_3_out));

  // Notes on the sheet:
  //   MAP=(CD_15_0 >> 6) + oct 6000
  //   Enable WCA_12_0
  //   Page 22 - CGA_MIC_IPOS
  //   W12
  //   W0
  //   WCA12
  //   WCA0
  //   CD15
  //   CD6
  //   TVEC3
  //   TVEC0
  //   B-Select
  //   A-Select
  //   MA12
  //   MA11
  //   MA10
  //   MA9
  //   MA8
  //   MA7
  //   MA6
  //   MA5
  //   MA4
  //   MA3
  //   MA2
  //   MA1
  //   MA0
endmodule

module CGA_MIC_INCOUNT (
  input  CD0,
  input  LWCAN,
  input  EC,
  input  MRN,
  input  CD1,
  input  MCLK,
  output CSWAN0,
  output CSWAN1
);

  wire d_ff_1_qn, d_ff_2_qn, multiplexer_1_out, multiplexer_2_out, nand_1_out, not_1_out, not_2_out,
       not_3_out, not_4_out, xnor_1_out, xor_1_out;

  xor xor_1 (xor_1_out, EC, d_ff_1_qn);
  nand nand_1 (nand_1_out, d_ff_1_qn, EC);
  xnor xnor_1 (xnor_1_out, nand_1_out, d_ff_2_qn);
  Multiplexer multiplexer_1 (.in0(CD0), .in1(xor_1_out), .out(multiplexer_1_out), .sel(LWCAN));
  Multiplexer multiplexer_2 (.in0(CD1), .in1(xnor_1_out), .out(multiplexer_2_out), .sel(LWCAN));
  not not_1 (not_1_out, multiplexer_1_out);
  not not_2 (not_2_out, multiplexer_2_out);
  not not_3 (not_3_out, MRN);
  not not_4 (not_4_out, MRN);
  D_Flip_Flop d_ff_1 (.D(not_1_out), .clk(MCLK), .Q(CSWAN0), .Qn(d_ff_1_qn), .preset(not_3_out));  // open: reset
  D_Flip_Flop d_ff_2 (.D(not_2_out), .clk(MCLK), .Q(CSWAN1), .Qn(d_ff_2_qn), .preset(not_4_out));  // open: reset

  // Notes on the sheet:
  //   Page 23 - CGA_MIC_INCOUNT
endmodule

module test_MIC (
);

  CGA_MIC cga_mic_1 ();  // open: CSBIT_15_0, CSBIT20, LCZ, MI, IRQ, RESTR, CFETCH, SPARE, OVF, CRY, F11, F15, ZF, STP, ALUCLK, MCLK, CSLOOP, CSECOND, CLFFN, CSALUI8, CSCOND, ILCSN, CSTS_6_3, TVEC_3_0, TRAPN, MAPN, EWCAN, CSMIS0, CSVECT, CD_15_0, LDIRV, LWCAN, MRN, LDLCN, PIL_3_0, CSXRF3, CSRB_3_0, CSRASEL_1_0, CSRBSEL_1_0, DZD, COND, OOD, ACONDN, SC_6_3, MA_12_0, WCSN, DEEP, UPN, PN, LCZN, TN, LAA_3_0, LBA_3_0, RF_1_0
endmodule
