// Logisim project CGA_TRAP_.circ as structural Verilog: 5 circuits, main circuit CGA_TRAP_TVGEN_P2
module CGA_TRAP (
  input  CBRKN,
  input  ETRAPN,
  input  [6:0] PT_15_9,
  input  [1:0] PCR_1_0,
  input  FETCHN,
  input  WRITEN,
  input  INDN,
  input  INTRQN,
  input  PANN,
  input  VACCN,
  input  PONI,
  input  TCLK,
  input  VTRAPN,
  input  FTRAPN,
  input  DSTOPN,
  output BRKN,
  output TRAPN,
  output RESTR,
  output [3:0] TVEC_3_0,
  output PVIOL
);

  wire TBUF_ifetch, TBUF_ifetchn, TBUF_iind, TBUF_iindn, TBUF_intrq, TBUF_iwrite, TBUF_iwriten, TBUF_pan,
       TBUF_vacc;
  wire [1:0] TBUF_ipcr_1_0, TBUF_ipcr_1_0_n;
  wire [6:0] TBUF_ipt_15_9, TBUF_ipt_15_9_n;

  CGA_TRAP_TBUF TBUF (
    .PT_15_9(PT_15_9), .PCR_1_0(PCR_1_0), .FETCHN(FETCHN), .WRITEN(WRITEN), .INDN(INDN), .INTRQN(INTRQN),
    .PANN(PANN), .VACCN(VACCN), .IPT_15_9_N(TBUF_ipt_15_9_n), .IPT_15_9(TBUF_ipt_15_9),
    .IPCR_1_0_N(TBUF_ipcr_1_0_n), .IPCR_1_0(TBUF_ipcr_1_0), .IFETCH(TBUF_ifetch), .IFETCHN(TBUF_ifetchn),
    .IWRITE(TBUF_iwrite), .IWRITEN(TBUF_iwriten), .IIND(TBUF_iind), .IINDN(TBUF_iindn), .INTRQ(TBUF_intrq),
    .PAN(TBUF_pan), .VACC(TBUF_vacc));
  // Probe on TBUF_ipt_15_9_n
  // Probe on TBUF_ipt_15_9
  // Probe on TBUF_ipcr_1_0_n
  // Probe on TBUF_ipcr_1_0
  CGA_TRAP_BRKDET BRKDET (
    .IPT_15_9(TBUF_ipt_15_9), .IPT_15_9_N(TBUF_ipt_15_9_n), .IPCR_1_0(TBUF_ipcr_1_0),
    .IPCR_1_0_N(TBUF_ipcr_1_0_n), .IWRITE(TBUF_iwrite), .IWRITEN(TBUF_iwriten), .IFETCH(TBUF_ifetch),
    .IFETCHN(TBUF_ifetchn), .VACC(TBUF_vacc), .IINDN(TBUF_iindn), .INTRQ(TBUF_intrq), .FTRAPN(FTRAPN),
    .VTRAPN(VTRAPN), .CBRKN(CBRKN), .ETRAPN(ETRAPN), .BRKN(BRKN), .TRAPN(TRAPN));
  CGA_TRAP_TVGEN TVGEN (
    .IPT_15_9(TBUF_ipt_15_9_n), .IPT_15_9_N(TBUF_ipt_15_9), .IPCR_1_0(TBUF_ipcr_1_0_n),
    .IPCR_1_0_N(TBUF_ipcr_1_0), .IWRITE(TBUF_iwrite), .PONI(PONI), .IWRITEN(TBUF_iwriten),
    .IFETCH(TBUF_ifetch), .IFETCHN(TBUF_ifetchn), .VACC(TBUF_vacc), .IIND(TBUF_iind), .IINDN(TBUF_iindn),
    .TCLK(TCLK), .VTRAPN(VTRAPN), .FTRAPN(FTRAPN), .INTRQ(TBUF_intrq), .PAN(TBUF_pan), .DSTOPN(DSTOPN),
    .RESTR(RESTR), .TVEC_3_0(TVEC_3_0), .PVIOL(PVIOL));

  // Notes on the sheet:
  //   Page 100 - /CGA/TRAP - Implemented, not tested
endmodule

module CGA_TRAP_TBUF (
  input  [6:0] PT_15_9,
  input  [1:0] PCR_1_0,
  input  FETCHN,
  input  WRITEN,
  input  INDN,
  input  INTRQN,
  input  PANN,
  input  VACCN,
  output [6:0] IPT_15_9_N,
  output [6:0] IPT_15_9,
  output [1:0] IPCR_1_0_N,
  output [1:0] IPCR_1_0,
  output IFETCH,
  output IFETCHN,
  output IWRITE,
  output IWRITEN,
  output IIND,
  output IINDN,
  output INTRQ,
  output PAN,
  output VACC
);

  not not_1 (IPCR_1_0_N[1], PCR_1_0[1]);
  not not_2 (IFETCH, FETCHN);
  not not_3 (IWRITE, WRITEN);
  not not_4 (IIND, INDN);
  not not_5 (INTRQ, INTRQN);
  not not_6 (PAN, PANN);
  not not_7 (VACC, VACCN);
  not not_8 (IPT_15_9_N[6], PT_15_9[6]);
  not not_9 (IPT_15_9_N[3], PT_15_9[3]);
  not not_10 (IPT_15_9_N[0], PT_15_9[0]);
  not not_11 (IPCR_1_0[1], IPCR_1_0_N[1]);
  not not_12 (IPT_15_9[6], IPT_15_9_N[6]);
  not not_13 (IPT_15_9_N[5], PT_15_9[5]);
  not not_14 (IPT_15_9_N[2], PT_15_9[2]);
  not not_15 (IPT_15_9[0], IPT_15_9_N[0]);
  not not_16 (IPCR_1_0_N[0], PCR_1_0[0]);
  not not_17 (IFETCHN, IFETCH);
  not not_18 (IWRITEN, IWRITE);
  not not_19 (IINDN, IIND);
  not not_20 (IPT_15_9_N[4], PT_15_9[4]);
  not not_21 (IPT_15_9_N[1], PT_15_9[1]);
  not not_22 (IPCR_1_0[0], IPCR_1_0_N[0]);
  not not_23 (IPT_15_9[4], IPT_15_9_N[4]);
  not not_24 (IPT_15_9[1], IPT_15_9_N[1]);

  // Notes on the sheet:
  //   Page 101 - /CGA/TRAP/TBUF - Completed, not tested
  //   IPT15
  //   IPT13
  //   IPT10
  //   IPT9
  //   IPT15N
  //   IPT14N
  //   IPT13N
  //   IPT12N
  //   IPT11N
  //   IPT10N
  //   IPT9N
endmodule

module CGA_TRAP_TVGEN (
  input  [6:0] IPT_15_9,
  input  [6:0] IPT_15_9_N,
  input  [1:0] IPCR_1_0,
  input  [1:0] IPCR_1_0_N,
  input  IWRITE,
  input  PONI,
  input  IWRITEN,
  input  IFETCH,
  input  IFETCHN,
  input  VACC,
  input  IIND,
  input  IINDN,
  input  TCLK,
  input  VTRAPN,
  input  FTRAPN,
  input  INTRQ,
  input  PAN,
  input  DSTOPN,
  output RESTR,
  output [3:0] TVEC_3_0,
  output PVIOL
);

  wire FPVN_out, IPVN_out, LEV1, LEV2, PGF, PGFN_out, PGU, PGUN, RD, RD1N_out, RD2N_out, RD3N_out, RPVN_out,
       RV, RV1N_out, RV2N_out, RV3N_out, WIP, WIPN, WPVN_out;

  nand PGFN (PGFN_out, VACC, IPT_15_9_N[6], IPT_15_9_N[5], IPT_15_9_N[4]);
  nand WPVN (WPVN_out, VACC, IWRITE, IINDN, IFETCHN, IPT_15_9_N[6]);
  nand IPVN (IPVN_out, VACC, IWRITEN, IIND, IFETCHN, IPT_15_9_N[5], IPT_15_9_N[4]);
  nand FPVN (FPVN_out, VACC, IWRITEN, IINDN, IFETCH, IPT_15_9_N[4]);
  nand RPVN (RPVN_out, VACC, IWRITEN, IINDN, IFETCHN, IPT_15_9_N[5]);
  nand RV1N (RV1N_out, VACC, IPT_15_9[1], IPCR_1_0_N[1]);
  nand RV2N (RV2N_out, VACC, IPT_15_9[0], IPCR_1_0_N[1], IPCR_1_0_N[0]);
  nand RV3N (RV3N_out, VACC, IPT_15_9[1], IPT_15_9[0], IPCR_1_0_N[0]);
  not not_1 (PGF, PGFN_out);
  or or_1 (LEV1, ~PGFN_out, ~WPVN_out, ~IPVN_out, ~FPVN_out, ~RPVN_out, ~RV1N_out, ~RV2N_out, ~RV3N_out);  // OR_Gate
  or or_2 (PVIOL, ~PGFN_out, ~WPVN_out, ~IPVN_out, ~FPVN_out, ~RPVN_out);  // OR_Gate
  or or_3 (RV, ~RV3N_out, ~RV2N_out, ~RV1N_out);  // OR_Gate
  nand u_WIPN (WIPN, VACC, IWRITE, IPT_15_9[6], IPT_15_9_N[3]);
  nand u_PGUN (PGUN, VACC, IPT_15_9_N[2]);
  nand RD1N (RD1N_out, VACC, IFETCH, IPT_15_9[4], IPT_15_9_N[1], IPCR_1_0[1]);
  nand RD2N (RD2N_out, VACC, IFETCH, IPT_15_9[4], IPT_15_9_N[1], IPT_15_9_N[0], IPCR_1_0[0]);
  nand RD3N (RD3N_out, VACC, IFETCH, IPT_15_9[4], IPT_15_9_N[0], IPCR_1_0[1], IPCR_1_0[0]);
  not not_2 (PGU, PGUN);
  not not_3 (WIP, WIPN);
  or or_4 (LEV2, ~WIPN, ~PGUN, ~RD1N_out, ~RD2N_out, ~RD3N_out);  // OR_Gate
  or or_5 (RD, ~RD3N_out, ~RD2N_out, ~RD1N_out);  // OR_Gate
  and and_1 (RESTR, IPCR_1_0_N[1], PONI);
  CGA_TRAP_TVGEN_P2 TRAP_TVGEN (
    .LEV2(LEV2), .LEV1(LEV1), .TCLK(TCLK), .RD(RD), .WIPN(WIPN), .PGUN(PGUN), .VTRAPN(VTRAPN), .VACC(VACC),
    .FTRAPN(FTRAPN), .WIP(WIP), .IFETCH(IFETCH), .PGU(PGU), .PGF(PGF), .INTRQ(INTRQ), .PAN(PAN),
    .DSTOPN(DSTOPN), .PVIOL(PVIOL), .RV(RV), .TVEC_3_0(TVEC_3_0));

  // Notes on the sheet:
  //   Page 102 - /CGA/TRAP/TVGEN (1/2) - Completed, not tested
  //   IPT15
  //   IPT9
  //   IPT15N
  //   IPT9N
  //   PGFN
  //   WPVN
  //   IPVN
  //   FPVN
  //   RPVN
  //   RING_0
endmodule

module CGA_TRAP_TVGEN_P2 (
  input  LEV2,
  input  LEV1,
  input  TCLK,
  input  RD,
  input  WIPN,
  input  PGUN,
  input  VTRAPN,
  input  VACC,
  input  FTRAPN,
  input  WIP,
  input  IFETCH,
  input  PGU,
  input  PGF,
  input  INTRQ,
  input  PAN,
  input  DSTOPN,
  input  PVIOL,
  input  RV,
  output [3:0] TVEC_3_0
);

  wire and_1_out, and_2_out, and_3_out, d_ff_1_qn, d_ff_2_qn, d_ff_3_qn, d_ff_4_q, d_ff_5_qn, d_ff_6_qn,
       d_ff_7_q, multiplexer_1_out, multiplexer_2_out, multiplexer_3_out, nand_1_out, nand_2_out, nand_3_out,
       nand_4_out, nand_5_out, nor_1_out, nor_2_out, not_1_out, not_2_out, not_3_out, not_4_out, not_5_out,
       not_6_out;

  not not_1 (not_1_out, VTRAPN);
  not not_2 (not_2_out, FTRAPN);
  nand nand_1 (nand_1_out, not_1_out, VACC);
  nand nand_2 (nand_2_out, VACC, not_2_out, IFETCH);
  nor nor_1 (nor_1_out, PVIOL, RV);
  and and_1 (and_1_out, nand_1_out, nand_2_out);
  nand nand_3 (nand_3_out, nand_1_out, IFETCH, INTRQ, PAN, DSTOPN);
  not not_3 (not_3_out, PGF);
  not not_4 (not_4_out, nor_1_out);
  nand nand_4 (nand_4_out, RD, WIPN, PGUN);
  nor nor_2 (nor_2_out, WIP, PGU);
  and and_2 (and_2_out, nand_2_out, nand_3_out);
  and and_3 (and_3_out, not_3_out, not_4_out);
  nand nand_5 (nand_5_out, WIPN, PGU);
  D_Flip_Flop d_ff_1 (.D(nand_4_out), .clk(TCLK), .Qn(d_ff_1_qn));  // open: Q, preset, reset
  D_Flip_Flop d_ff_2 (.D(and_1_out), .clk(TCLK), .Qn(d_ff_2_qn));  // open: Q, preset, reset
  D_Flip_Flop d_ff_3 (.D(nor_2_out), .clk(TCLK), .Qn(d_ff_3_qn));  // open: Q, preset, reset
  D_Flip_Flop d_ff_4 (.D(PGF), .clk(TCLK), .Q(d_ff_4_q));  // open: Qn, preset, reset
  D_Flip_Flop d_ff_5 (.D(and_2_out), .clk(TCLK), .Qn(d_ff_5_qn));  // open: Q, preset, reset
  D_Flip_Flop d_ff_6 (.D(nand_5_out), .clk(TCLK), .Qn(d_ff_6_qn));  // open: Q, preset, reset
  D_Flip_Flop d_ff_7 (.D(and_3_out), .clk(TCLK), .Q(d_ff_7_q));  // open: Qn, preset, reset
  not not_5 (not_5_out, LEV2);
  not not_6 (not_6_out, LEV1);
  and and_4 (TVEC_3_0[3], not_5_out, not_6_out);
  Multiplexer #(.select(2)) multiplexer_1 (
    .in0(1'b0), .in1(d_ff_1_qn), .in2(1'b1), .in3(1'b1), .out(multiplexer_1_out), .sel({LEV1, LEV2}));
  Multiplexer #(.select(2)) multiplexer_2 (
    .in0(d_ff_2_qn), .in1(d_ff_3_qn), .in2(d_ff_4_q), .in3(d_ff_4_q), .out(multiplexer_2_out),
    .sel({LEV1, LEV2}));
  Multiplexer #(.select(2)) multiplexer_3 (
    .in0(d_ff_5_qn), .in1(d_ff_6_qn), .in2(d_ff_7_q), .in3(d_ff_7_q), .out(multiplexer_3_out),
    .sel({LEV1, LEV2}));
  not not_7 (TVEC_3_0[2], multiplexer_1_out);
  not not_8 (TVEC_3_0[1], multiplexer_2_out);
  not not_9 (TVEC_3_0[0], multiplexer_3_out);

  // Notes on the sheet:
  //   /CGA/TRAP/TVGEN_P2 - (2/2) Page 104 - Completed, not tested
  //   IVA
  //   IVA
  //   ND2
  //   ND3
  //   VTRPN
  //   NR2
  //   AN2
  //   ND5
  //   PGF
  //   WIPN
  //   PGU
  //   ND3
  //   NR2
  //   AN2
  //   ND2
  //   NR2
  //   L2V2N
  //   L3V1N
  //   L2V1N
  //   L3V0N
  //   L2V0N
  //   L1V0N
  //   L1V1N
  //   TVEC3
  //   TVEC2
  //   TVEC1
  //   TVEC0
endmodule

module CGA_TRAP_BRKDET (
  input  [6:0] IPT_15_9,
  input  [6:0] IPT_15_9_N,
  input  [1:0] IPCR_1_0,
  input  [1:0] IPCR_1_0_N,
  input  IWRITE,
  input  IWRITEN,
  input  IFETCH,
  input  IFETCHN,
  input  VACC,
  input  IINDN,
  input  INTRQ,
  input  FTRAPN,
  input  VTRAPN,
  input  CBRKN,
  input  ETRAPN,
  output BRKN,
  output TRAPN
);

  wire A02_1_z, A02_2_z, A02_3_z, A02_4_z, AN2_1_out, and_1_out, and_2_out, and_3_out, and_4_out, and_5_out,
       and_6_out, and_7_out, and_8_out, and_9_out, INTR_out, IPV_out, nand_1_out, nand_2_out, nor_1_out,
       not_1_out, not_2_out, or_1_out, or_2_out, or_3_out, PGF_out, RD2_out, RV3_out, WIP_out;

  and AN2_1 (AN2_1_out, VACC, IWRITE);
  and and_1 (and_1_out, VACC, IFETCH);
  A02 A02_1 (.A(IPT_15_9_N[4]), .B(and_1_out), .C(IPT_15_9_N[6]), .D(AN2_1_out), .Z(A02_1_z));
  and and_2 (and_2_out, VACC, IWRITEN, IINDN, IFETCHN);
  and and_3 (and_3_out, VACC, IFETCH, IPCR_1_0[1]);
  A02 A02_2 (.A(IPT_15_9_N[2]), .B(VACC), .C(IPT_15_9_N[5]), .D(and_2_out), .Z(A02_2_z));
  or or_1 (or_1_out, ~A02_1_z, ~A02_2_z, ~A02_3_z, ~A02_4_z);  // OR_Gate
  A02 A02_3 (.A(IPT_15_9_N[0]), .B(and_4_out), .C(IPT_15_9_N[1]), .D(and_3_out), .Z(A02_3_z));
  and and_4 (and_4_out, VACC, IFETCH, IPCR_1_0[1], IPCR_1_0[0]);
  and and_5 (and_5_out, VACC, IPCR_1_0_N[1]);
  and and_6 (and_6_out, VACC, IPCR_1_0_N[1], IPCR_1_0_N[0]);
  A02 A02_4 (.A(IPT_15_9[0]), .B(and_6_out), .C(IPT_15_9[1]), .D(and_5_out), .Z(A02_4_z));
  nand IPV (IPV_out, VACC, IPT_15_9_N[5], IPT_15_9_N[4]);
  and and_7 (and_7_out, VACC, IWRITE);
  nand WIP (WIP_out, and_7_out, IPT_15_9[6], IPT_15_9_N[3]);
  and and_8 (and_8_out, VACC, IFETCH, IPCR_1_0[0]);
  or or_2 (or_2_out, ~IPV_out, ~WIP_out, ~RD2_out, ~RV3_out);  // OR_Gate
  nand RD2 (RD2_out, and_8_out, IPT_15_9_N[1], IPT_15_9_N[0]);
  and and_9 (and_9_out, VACC, IPCR_1_0_N[0]);
  nand RV3 (RV3_out, and_9_out, IPT_15_9[1], IPT_15_9[0]);
  nand PGF (PGF_out, VACC, IPT_15_9_N[6], IPT_15_9_N[5], IPT_15_9_N[4]);
  or or_3 (or_3_out, ~PGF_out, ~INTR_out, ~nand_1_out, ~nand_2_out);  // OR_Gate
  nand INTR (INTR_out, IFETCH, INTRQ);
  nor nor_1 (nor_1_out, or_3_out, or_2_out, or_1_out);
  not not_1 (not_1_out, VTRAPN);
  nand nand_1 (nand_1_out, not_1_out, VACC);
  nor nor_2 (BRKN, ~nor_1_out, ~CBRKN);  // NOR_Gate
  not not_2 (not_2_out, CBRKN);
  nand nand_2 (nand_2_out, ~FTRAPN, ~IFETCHN);  // NAND_Gate
  nand nand_3 (TRAPN, ~BRKN, ~not_2_out, ~ETRAPN);  // NAND_Gate

  // Notes on the sheet:
  //   Page 103 - /CGA/TRAP/BRKDET - Partly
  //   SPARE VACC TRAP
  //   SPARE FETCH TRAP
endmodule
