// Logisim project CGA_WRF_.circ as structural Verilog: 7 circuits, main circuit CGA_WRF
module CGA_WRF (
  input  BDEST,
  input  [3:0] LBA_3_0,
  input  [3:0] LAA_3_0,
  input  ALUCLK,
  input  [15:0] RB_15_0,
  input  [15:0] NLCA_15_0,
  input  XFETCHN,
  output WPN,
  output WR3,
  output WR7,
  output [15:0] B_15_0,
  output [15:0] A_15_0,
  output [15:0] PR_15_0,
  output [15:0] BR_15_0,
  output [15:0] XR_15_0,
  output [15:0] EA_15_0
);

  wire LAA_HI_z0, LAA_HI_z1, LAA_HI_z2, LAA_HI_z3, LAA_HI_z4, LAA_HI_z5, LAA_HI_z6, LAA_HI_z7, LAA_LO_z0,
       LAA_LO_z1, LAA_LO_z2, LAA_LO_z3, LAA_LO_z4, LAA_LO_z5, LAA_LO_z6, LAA_LO_z7, LBA_HI_z0, LBA_HI_z1,
       LBA_HI_z2, LBA_HI_z3, LBA_HI_z4, LBA_HI_z5, LBA_HI_z6, LBA_HI_z7, LBA_LO_z0, LBA_LO_z1, LBA_LO_z2,
       LBA_LO_z3, LBA_LO_z4, LBA_LO_z5, LBA_LO_z6, LBA_LO_z7, nand_1_out, nand_2_out, nand_4_out, nand_5_out,
       nand_6_out, nand_7_out, nand_8_out, nand_9_out, nand_10_out, nand_11_out, nand_12_out, nand_13_out,
       nand_14_out, nand_15_out, nand_16_out, not_1_out, not_2_out, not_3_out;
  wire [15:0] EB_15_0, WR_15_0;

  not not_1 (not_1_out, LBA_3_0[3]);
  not not_2 (not_2_out, LAA_3_0[3]);
  not not_3 (not_3_out, ALUCLK);
  ND38GLP LBA_LO (
    .A(LBA_3_0[0]), .B(LBA_3_0[1]), .C(LBA_3_0[2]), .G(not_1_out), .Z0(LBA_LO_z0), .Z1(LBA_LO_z1),
    .Z2(LBA_LO_z2), .Z3(LBA_LO_z3), .Z4(LBA_LO_z4), .Z5(LBA_LO_z5), .Z6(LBA_LO_z6), .Z7(LBA_LO_z7));
  ND38GLP LBA_HI (
    .A(LBA_3_0[0]), .B(LBA_3_0[1]), .C(LBA_3_0[2]), .G(LBA_3_0[3]), .Z0(LBA_HI_z0), .Z1(LBA_HI_z1),
    .Z2(LBA_HI_z2), .Z3(LBA_HI_z3), .Z4(LBA_HI_z4), .Z5(LBA_HI_z5), .Z6(LBA_HI_z6), .Z7(LBA_HI_z7));
  ND38GLP LAA_LO (
    .A(LAA_3_0[0]), .B(LAA_3_0[1]), .C(LAA_3_0[2]), .G(not_2_out), .Z0(LAA_LO_z0), .Z1(LAA_LO_z1),
    .Z2(LAA_LO_z2), .Z3(LAA_LO_z3), .Z4(LAA_LO_z4), .Z5(LAA_LO_z5), .Z6(LAA_LO_z6), .Z7(LAA_LO_z7));
  ND38GLP LAA_HI (
    .A(LAA_3_0[0]), .B(LAA_3_0[1]), .C(LAA_3_0[2]), .G(LAA_3_0[3]), .Z0(LAA_HI_z0), .Z1(LAA_HI_z1),
    .Z2(LAA_HI_z2), .Z3(LAA_HI_z3), .Z4(LAA_HI_z4), .Z5(LAA_HI_z5), .Z6(LAA_HI_z6), .Z7(LAA_HI_z7));
  not not_4 (EB_15_0[0], LBA_LO_z0);
  not not_5 (EB_15_0[1], LBA_LO_z1);
  not not_6 (EB_15_0[2], LBA_LO_z2);
  not not_7 (EB_15_0[3], LBA_LO_z3);
  not not_8 (EB_15_0[4], LBA_LO_z4);
  not not_9 (EB_15_0[5], LBA_LO_z5);
  not not_10 (EB_15_0[6], LBA_LO_z6);
  not not_11 (EB_15_0[7], LBA_LO_z7);
  not not_12 (EB_15_0[8], LBA_HI_z0);
  not not_13 (EB_15_0[9], LBA_HI_z1);
  not not_14 (EB_15_0[10], LBA_HI_z2);
  not not_15 (EB_15_0[11], LBA_HI_z3);
  not not_16 (EB_15_0[12], LBA_HI_z4);
  not not_17 (EB_15_0[13], LBA_HI_z5);
  not not_18 (EB_15_0[14], LBA_HI_z6);
  not not_19 (EB_15_0[15], LBA_HI_z7);
  not not_20 (EA_15_0[0], LAA_LO_z0);
  not not_21 (EA_15_0[1], LAA_LO_z1);
  not not_22 (EA_15_0[2], LAA_LO_z2);
  not not_23 (EA_15_0[3], LAA_LO_z3);
  not not_24 (EA_15_0[4], LAA_LO_z4);
  not not_25 (EA_15_0[5], LAA_LO_z5);
  not not_26 (EA_15_0[6], LAA_LO_z6);
  not not_27 (EA_15_0[7], LAA_LO_z7);
  not not_28 (EA_15_0[8], LAA_HI_z0);
  not not_29 (EA_15_0[9], LAA_HI_z1);
  not not_30 (EA_15_0[10], LAA_HI_z2);
  not not_31 (EA_15_0[11], LAA_HI_z3);
  not not_32 (EA_15_0[12], LAA_HI_z4);
  not not_33 (EA_15_0[13], LAA_HI_z5);
  not not_34 (EA_15_0[14], LAA_HI_z6);
  not not_35 (EA_15_0[15], LAA_HI_z7);
  CGA_WRF_RBLOCK RBLOCK (
    .EA_15_0(EA_15_0), .EB_15_0(EB_15_0), .ALUCLK(ALUCLK), .RB_15_0(RB_15_0),
    .WR_15_0({WR_15_0[15:8], WR7, WR_15_0[6:4], WR3, WR_15_0[2:0]}), .NLCA_15_0(NLCA_15_0),
    .XFETCHN(XFETCHN), .ALUCLKN(not_3_out), .B_15_0(B_15_0), .A_15_0(A_15_0), .PR_15_0(PR_15_0),
    .BR_15_0(BR_15_0), .XR_15_0(XR_15_0));
  // Probe on EA_15_0
  nand nand_1 (nand_1_out, BDEST, EB_15_0[0]);
  not not_36 (WR_15_0[0], nand_1_out);
  nand nand_2 (nand_2_out, BDEST, EB_15_0[1]);
  not not_37 (WR_15_0[1], nand_2_out);
  nand nand_3 (WPN, BDEST, EB_15_0[2]);
  not not_38 (WR_15_0[2], WPN);
  nand nand_4 (nand_4_out, BDEST, EB_15_0[3]);
  not not_39 (WR3, nand_4_out);
  nand nand_5 (nand_5_out, BDEST, EB_15_0[4]);
  not not_40 (WR_15_0[4], nand_5_out);
  nand nand_6 (nand_6_out, BDEST, EB_15_0[5]);
  not not_41 (WR_15_0[5], nand_6_out);
  nand nand_7 (nand_7_out, BDEST, EB_15_0[6]);
  not not_42 (WR_15_0[6], nand_7_out);
  nand nand_8 (nand_8_out, BDEST, EB_15_0[7]);
  not not_43 (WR7, nand_8_out);
  nand nand_9 (nand_9_out, BDEST, EB_15_0[8]);
  nand nand_10 (nand_10_out, BDEST, EB_15_0[9]);
  nand nand_11 (nand_11_out, BDEST, EB_15_0[10]);
  nand nand_12 (nand_12_out, BDEST, EB_15_0[11]);
  nand nand_13 (nand_13_out, BDEST, EB_15_0[12]);
  nand nand_14 (nand_14_out, BDEST, EB_15_0[13]);
  nand nand_15 (nand_15_out, BDEST, EB_15_0[14]);
  nand nand_16 (nand_16_out, BDEST, EB_15_0[15]);
  not not_44 (WR_15_0[8], nand_9_out);
  not not_45 (WR_15_0[9], nand_10_out);
  not not_46 (WR_15_0[10], nand_11_out);
  not not_47 (WR_15_0[11], nand_12_out);
  not not_48 (WR_15_0[12], nand_13_out);
  not not_49 (WR_15_0[13], nand_14_out);
  not not_50 (WR_15_0[14], nand_15_out);
  not not_51 (WR_15_0[15], nand_16_out);
  // Probe on {WR_15_0[15:8], WR7, WR_15_0[6:4], WR3, WR_15_0[2:0]}
  // Probe on EB_15_0

  // Other names for the same wires on the sheet: WR_15_0 (some bits) = {WR7, WR3}

  // Notes on the sheet:
  //   Page 59 - CGA_ALU_WRF
  //   LBA0
  //   LBA1
  //   LBA2
  //   LBA3
  //   LBA0
  //   LBA1
  //   LBA2
  //   LBA3
  //   LAA0
  //   LAA1
  //   LAA2
  //   LAA3
  //   LAA0
  //   LAA1
  //   LAA2
  //   LAA3
  //   EB0
  //   EB15
  //   EA0
  //   EA15
endmodule

module CGA_WRF_RBLOCK (
  input  [15:0] EA_15_0,
  input  [15:0] EB_15_0,
  input  ALUCLK,
  input  [15:0] RB_15_0,
  input  [15:0] WR_15_0,
  input  [15:0] NLCA_15_0,
  input  XFETCHN,
  input  ALUCLKN,
  output [15:0] B_15_0,
  output [15:0] A_15_0,
  output [15:0] PR_15_0,
  output [15:0] BR_15_0,
  output [15:0] XR_15_0
);

  wire AR0, AR1, AR2, AR3, AR4, AR5, AR6, AR7, AR8, AR9, AR10, AR11, AR12, AR13, AR14, AR15, C0, C1, C2, C3,
       C4, C5, C6, C7, C8, C9, C10, C11, C12, C13, C14, C15, D0, D1, D2, D3, D4, D5, D6, D7, D8, D9, D10,
       D11, D12, D13, D14, D15, IB0, IB1, IB2, IB3, IB4, IB5, IB6, IB7, IB8, IB9, IB10, IB11, IB12, IB13,
       IB14, IB15, P0, P1, P2, P3, P4, P5, P6, P7, P8, P9, P10, P11, P12, P13, P14, P15, R10, R11, R12, R13,
       R14, R15, R16, R17, R18, R19, R20, R21, R22, R23, R24, R25, R26, R27, R28, R29, R30, R31, R32, R33,
       R34, R35, R36, R37, R38, R39, R40, R41, R42, R43, R44, R45, R46, R47, R48, R49, R50, R51, R52, R53,
       R54, R55, R56, R57, R58, R59, R60, R61, R62, R63, R64, R65, R66, R67, R68, R69, R70, R71, R72, R73,
       R74, R75, R76, R77, R78, R79, R110, R111, R112, R113, R114, R115, R210, R211, R212, R213, R214, R215,
       R310, R311, R312, R313, R314, R315, R410, R411, R412, R413, R414, R415, R510, R511, R512, R513, R514,
       R515, R610, R611, R612, R613, R614, R615, R710, R711, R712, R713, R714, R715, STS0, STS1, STS2, STS3,
       STS4, STS5, STS6, STS7, STS8, STS9, STS10, STS11, STS12, STS13, STS14, STS15, T0, T1, T2, T3, T4, T5,
       T6, T7, T8, T9, T10, T11, T12, T13, T14, T15, X0, X1, X2, X3, X4, X5, X6, X7, X8, X9, X10, X11, X12,
       X13, X14, X15, Z0, Z1, Z2, Z3, Z4, Z5, Z6, Z7, Z8, Z9, Z10, Z11, Z12, Z13, Z14, Z15;

  CGA_WRF_RBLOCK_DR16 Z_REG_0 (
    .ALUCLK(ALUCLK), .WR(WR_15_0[0]), .RB_15_0(RB_15_0),
    .REG_15_0({Z15, Z14, Z13, Z12, Z11, Z10, Z9, Z8, Z7, Z6, Z5, Z4, Z3, Z2, Z1, Z0}));
  CGA_WRF_RBLOCK_DR16 D_REG_1 (
    .ALUCLK(ALUCLK), .WR(WR_15_0[1]), .RB_15_0(RB_15_0),
    .REG_15_0({D15, D14, D13, D12, D11, D10, D9, D8, D7, D6, D5, D4, D3, D2, D1, D0}));
  // Probe on {P15, P14, P13, P12, P11, P10, P9, P8, P7, P6, P5, P4, P3, P2, P1, P0}
  CGA_WRF_RBLOCK_PREG P_REG_2 (
    .NLCA_15_0(NLCA_15_0), .RB_15_0(RB_15_0), .XFETCHN(XFETCHN), .WR2(WR_15_0[2]), .ALUCLKN(ALUCLKN),
    .ALUCLK(ALUCLK), .P_15_0({P15, P14, P13, P12, P11, P10, P9, P8, P7, P6, P5, P4, P3, P2, P1, P0}),
    .PR_15_0(PR_15_0));
  CGA_WRF_RBLOCK_LR16 B_REG_3 (
    .RB_15_0(RB_15_0), .ALUCLK(ALUCLK), .WR(WR_15_0[3]),
    .R_15_0({IB15, IB14, IB13, IB12, IB11, IB10, IB9, IB8, IB7, IB6, IB5, IB4, IB3, IB2, IB1, IB0}),
    .LR_15_0(BR_15_0));
  CGA_WRF_RBLOCK_DR16 L_REG_4 (
    .ALUCLK(ALUCLK), .WR(WR_15_0[4]), .RB_15_0(RB_15_0),
    .REG_15_0({C15, C14, C13, C12, C11, C10, C9, C8, C7, C6, C5, C4, C3, C2, C1, C0}));
  CGA_WRF_RBLOCK_DR16 A_REG_5 (
    .ALUCLK(ALUCLK), .WR(WR_15_0[5]), .RB_15_0(RB_15_0),
    .REG_15_0({AR15, AR14, AR13, AR12, AR11, AR10, AR9, AR8, AR7, AR6, AR5, AR4, AR3, AR2, AR1, AR0}));
  CGA_WRF_RBLOCK_DR16 T_REG_6 (
    .ALUCLK(ALUCLK), .WR(WR_15_0[6]), .RB_15_0(RB_15_0),
    .REG_15_0({T15, T14, T13, T12, T11, T10, T9, T8, T7, T6, T5, T4, T3, T2, T1, T0}));
  CGA_WRF_RBLOCK_LR16 X_REG_7 (
    .RB_15_0(RB_15_0), .ALUCLK(ALUCLK), .WR(WR_15_0[7]),
    .R_15_0({X15, X14, X13, X12, X11, X10, X9, X8, X7, X6, X5, X4, X3, X2, X1, X0}), .LR_15_0(XR_15_0));
  CGA_WRF_RBLOCK_DR16 STS_REG_8 (
    .ALUCLK(ALUCLK), .WR(WR_15_0[8]), .RB_15_0(RB_15_0),
    .REG_15_0({STS15, STS14, STS13, STS12, STS11, STS10, STS9, STS8, STS7, STS6, STS5, STS4, STS3, STS2, STS1, STS0}));
  CGA_WRF_RBLOCK_DR16 R1_REG_9 (
    .ALUCLK(ALUCLK), .WR(WR_15_0[9]), .RB_15_0(RB_15_0),
    .REG_15_0({R115, R114, R113, R112, R111, R110, R19, R18, R17, R16, R15, R14, R13, R12, R11, R10}));
  CGA_WRF_RBLOCK_DR16 R2_REG_10 (
    .ALUCLK(ALUCLK), .WR(WR_15_0[10]), .RB_15_0(RB_15_0),
    .REG_15_0({R215, R214, R213, R212, R211, R210, R29, R28, R27, R26, R25, R24, R23, R22, R21, R20}));
  CGA_WRF_RBLOCK_DR16 R3_REG_11 (
    .ALUCLK(ALUCLK), .WR(WR_15_0[11]), .RB_15_0(RB_15_0),
    .REG_15_0({R315, R314, R313, R312, R311, R310, R39, R38, R37, R36, R35, R34, R33, R32, R31, R30}));
  CGA_WRF_RBLOCK_DR16 R4_REG_12 (
    .ALUCLK(ALUCLK), .WR(WR_15_0[12]), .RB_15_0(RB_15_0),
    .REG_15_0({R415, R414, R413, R412, R411, R410, R49, R48, R47, R46, R45, R44, R43, R42, R41, R40}));
  CGA_WRF_RBLOCK_DR16 R5_REG_13 (
    .ALUCLK(ALUCLK), .WR(WR_15_0[13]), .RB_15_0(RB_15_0),
    .REG_15_0({R515, R514, R513, R512, R511, R510, R59, R58, R57, R56, R55, R54, R53, R52, R51, R50}));
  CGA_WRF_RBLOCK_DR16 R6_REG_14 (
    .ALUCLK(ALUCLK), .WR(WR_15_0[14]), .RB_15_0(RB_15_0),
    .REG_15_0({R615, R614, R613, R612, R611, R610, R69, R68, R67, R66, R65, R64, R63, R62, R61, R60}));
  CGA_WRF_RBLOCK_DR16 R7_REG_15 (
    .ALUCLK(ALUCLK), .WR(WR_15_0[15]), .RB_15_0(RB_15_0),
    .REG_15_0({R715, R714, R713, R712, R711, R710, R79, R78, R77, R76, R75, R74, R73, R72, R71, R70}));
  // Probe on {Z15, Z14, Z13, Z12, Z11, Z10, Z9, Z8, Z7, Z6, Z5, Z4, Z3, Z2, Z1, Z0}
  // Probe on PR_15_0
  // Probe on {IB15, IB14, IB13, IB12, IB11, IB10, IB9, IB8, IB7, IB6, IB5, IB4, IB3, IB2, IB1, IB0}
  CGA_WRF_RBLOCK_SEL16 SEL_0 (
    .SI_15_0({R70, R60, R50, R40, R30, R20, R10, STS0, X0, T0, AR0, C0, IB0, P0, D0, Z0}), .EA_15_0(EA_15_0),
    .EB_15_0(EB_15_0), .PA(A_15_0[0]), .PB(B_15_0[0]));
  CGA_WRF_RBLOCK_SEL16 SEL_1 (
    .SI_15_0({R71, R61, R51, R41, R31, R21, R11, STS1, X1, T1, AR1, C1, IB1, P1, D1, Z1}), .EA_15_0(EA_15_0),
    .EB_15_0(EB_15_0), .PA(A_15_0[1]), .PB(B_15_0[1]));
  CGA_WRF_RBLOCK_SEL16 SEL_4 (
    .SI_15_0({R74, R64, R54, R44, R34, R24, R14, STS4, X4, T4, AR4, C4, IB4, P4, D4, Z4}), .EA_15_0(EA_15_0),
    .EB_15_0(EB_15_0), .PA(A_15_0[4]), .PB(B_15_0[4]));
  CGA_WRF_RBLOCK_SEL16 SEL_5 (
    .SI_15_0({R75, R65, R55, R45, R35, R25, R15, STS5, X5, T5, AR5, C5, IB5, P5, D5, Z5}), .EA_15_0(EA_15_0),
    .EB_15_0(EB_15_0), .PA(A_15_0[5]), .PB(B_15_0[5]));
  CGA_WRF_RBLOCK_SEL16 SEL_2 (
    .SI_15_0({R72, R62, R52, R42, R32, R22, R12, STS2, X2, T2, AR2, C2, IB2, P2, D2, Z2}), .EA_15_0(EA_15_0),
    .EB_15_0(EB_15_0), .PA(A_15_0[2]), .PB(B_15_0[2]));
  CGA_WRF_RBLOCK_SEL16 SEL_3 (
    .SI_15_0({R73, R63, R53, R43, R33, R23, R13, STS3, X3, T3, AR3, C3, IB3, P3, D3, Z3}), .EA_15_0(EA_15_0),
    .EB_15_0(EB_15_0), .PA(A_15_0[3]), .PB(B_15_0[3]));
  CGA_WRF_RBLOCK_SEL16 SEL_6 (
    .SI_15_0({R76, R66, R56, R46, R36, R26, R16, STS6, X6, T6, AR6, C6, IB6, P6, D6, Z6}), .EA_15_0(EA_15_0),
    .EB_15_0(EB_15_0), .PA(A_15_0[6]), .PB(B_15_0[6]));
  CGA_WRF_RBLOCK_SEL16 SEL_7 (
    .SI_15_0({R77, R67, R57, R47, R37, R27, R17, STS7, X7, T7, AR7, C7, IB7, P7, D7, Z7}), .EA_15_0(EA_15_0),
    .EB_15_0(EB_15_0), .PA(A_15_0[7]), .PB(B_15_0[7]));
  CGA_WRF_RBLOCK_SEL16 SEL_8 (
    .SI_15_0({R78, R68, R58, R48, R38, R28, R18, STS8, X8, T8, AR8, C8, IB8, P8, D8, Z8}), .EA_15_0(EA_15_0),
    .EB_15_0(EB_15_0), .PA(A_15_0[8]), .PB(B_15_0[8]));
  CGA_WRF_RBLOCK_SEL16 SEL_9 (
    .SI_15_0({R79, R69, R59, R49, R39, R29, R19, STS9, X9, T9, AR9, C9, IB9, P9, D9, Z9}), .EA_15_0(EA_15_0),
    .EB_15_0(EB_15_0), .PA(A_15_0[9]), .PB(B_15_0[9]));
  CGA_WRF_RBLOCK_SEL16 SEL_10 (
    .SI_15_0({R710, R610, R510, R410, R310, R210, R110, STS10, X10, T10, AR10, C10, IB10, P10, D10, Z10}),
    .EA_15_0(EA_15_0), .EB_15_0(EB_15_0), .PA(A_15_0[10]), .PB(B_15_0[10]));
  CGA_WRF_RBLOCK_SEL16 SEL_11 (
    .SI_15_0({R711, R611, R511, R411, R311, R211, R111, STS11, X11, T11, AR11, C11, IB11, P11, D11, Z11}),
    .EA_15_0(EA_15_0), .EB_15_0(EB_15_0), .PA(A_15_0[11]), .PB(B_15_0[11]));
  CGA_WRF_RBLOCK_SEL16 SEL_12 (
    .SI_15_0({R712, R612, R512, R412, R312, R212, R112, STS12, X12, T12, AR12, C12, IB12, P12, D12, Z12}),
    .EA_15_0(EA_15_0), .EB_15_0(EB_15_0), .PA(A_15_0[12]), .PB(B_15_0[12]));
  CGA_WRF_RBLOCK_SEL16 SEL_13 (
    .SI_15_0({R713, R613, R513, R413, R313, R213, R113, STS13, X13, T13, AR13, C13, IB13, P13, D13, Z13}),
    .EA_15_0(EA_15_0), .EB_15_0(EB_15_0), .PA(A_15_0[13]), .PB(B_15_0[13]));
  CGA_WRF_RBLOCK_SEL16 SEL_14 (
    .SI_15_0({R714, R614, R514, R414, R314, R214, R114, STS14, X14, T14, AR14, C14, IB14, P14, D14, Z14}),
    .EA_15_0(EA_15_0), .EB_15_0(EB_15_0), .PA(A_15_0[14]), .PB(B_15_0[14]));
  CGA_WRF_RBLOCK_SEL16 SEL_15 (
    .SI_15_0({R715, R615, R515, R415, R315, R215, R115, STS15, X15, T15, AR15, C15, IB15, P15, D15, Z15}),
    .EA_15_0(EA_15_0), .EB_15_0(EB_15_0), .PA(A_15_0[15]), .PB(B_15_0[15]));
  // Probe on B_15_0[2]

  // Other names for the same wires on the sheet: A0 = A_15_0[0]; A1 = A_15_0[1]; A2 = A_15_0[2]; A3 = A_15_0[3];
  //   A4 = A_15_0[4]; A5 = A_15_0[5]; A6 = A_15_0[6]; A7 = A_15_0[7]; A8 = A_15_0[8]; A9 = A_15_0[9];
  //   A10 = A_15_0[10]; A11 = A_15_0[11]; A12 = A_15_0[12]; A13 = A_15_0[13]; A14 = A_15_0[14]; A15 = A_15_0[15];
  //   B0 = B_15_0[0]; B1 = B_15_0[1]; B2 = B_15_0[2]; B3 = B_15_0[3]; B4 = B_15_0[4]; B5 = B_15_0[5]; B6 = B_15_0[6];
  //   B7 = B_15_0[7]; B8 = B_15_0[8]; B9 = B_15_0[9]; B10 = B_15_0[10]; B11 = B_15_0[11]; B12 = B_15_0[12];
  //   B13 = B_15_0[13]; B14 = B_15_0[14]; B15 = B_15_0[15]

  // Notes on the sheet:
  //   Page 60 - CGA_ALU_WRF_RBLOCK
  //   WR0
  //   WR1
  //   WR2
  //   WR3
  //   WR4
  //   WR5
  //   WR6
  //   WR7
  //   WR8
  //   WR9
  //   WR11
  //   WR10
  //   WR12
  //   WR13
  //   WR14
  //   WR15
endmodule

module CGA_WRF_RBLOCK_SEL16 (
  input  [15:0] SI_15_0,
  input  [15:0] EA_15_0,
  input  [15:0] EB_15_0,
  output PA,
  output PB
);

  wire A1_0_z, A3_2_z, A5_4_z, A7_6_z, A9_8_z, A11_10_z, A13_12_z, A15_14_z, B1_0_z, B4_3_z, B5_4_z, B7_6_z,
       B9_8_z, B11_10_z, B13_12_z, B15_14_z;

  A02 A15_14 (.A(SI_15_0[15]), .B(EA_15_0[15]), .C(SI_15_0[14]), .D(EA_15_0[14]), .Z(A15_14_z));
  A02 A13_12 (.A(SI_15_0[13]), .B(EA_15_0[13]), .C(SI_15_0[12]), .D(EA_15_0[12]), .Z(A13_12_z));
  A02 A11_10 (.A(SI_15_0[11]), .B(EA_15_0[11]), .C(SI_15_0[10]), .D(EA_15_0[10]), .Z(A11_10_z));
  A02 A9_8 (.A(SI_15_0[9]), .B(EA_15_0[9]), .C(SI_15_0[8]), .D(EA_15_0[8]), .Z(A9_8_z));
  A02 A7_6 (.A(SI_15_0[7]), .B(EA_15_0[7]), .C(SI_15_0[6]), .D(EA_15_0[6]), .Z(A7_6_z));
  A02 A5_4 (.A(SI_15_0[5]), .B(EA_15_0[5]), .C(SI_15_0[4]), .D(EA_15_0[4]), .Z(A5_4_z));
  A02 A3_2 (.A(SI_15_0[3]), .B(EA_15_0[3]), .C(SI_15_0[2]), .D(EA_15_0[2]), .Z(A3_2_z));
  A02 A1_0 (.A(SI_15_0[1]), .B(EA_15_0[1]), .C(SI_15_0[0]), .D(EA_15_0[0]), .Z(A1_0_z));
  nand nand_1 (PA, A15_14_z, A13_12_z, A11_10_z, A9_8_z, A7_6_z, A5_4_z, A3_2_z, A1_0_z);
  A02 B15_14 (.A(SI_15_0[15]), .B(EB_15_0[15]), .C(SI_15_0[14]), .D(EB_15_0[14]), .Z(B15_14_z));
  A02 B13_12 (.A(SI_15_0[13]), .B(EB_15_0[13]), .C(SI_15_0[12]), .D(EB_15_0[12]), .Z(B13_12_z));
  A02 B11_10 (.A(SI_15_0[11]), .B(EB_15_0[11]), .C(SI_15_0[10]), .D(EB_15_0[10]), .Z(B11_10_z));
  A02 B9_8 (.A(SI_15_0[9]), .B(EB_15_0[9]), .C(SI_15_0[8]), .D(EB_15_0[8]), .Z(B9_8_z));
  A02 B7_6 (.A(SI_15_0[7]), .B(EB_15_0[7]), .C(SI_15_0[6]), .D(EB_15_0[6]), .Z(B7_6_z));
  A02 B5_4 (.A(SI_15_0[5]), .B(EB_15_0[5]), .C(SI_15_0[4]), .D(EB_15_0[4]), .Z(B5_4_z));
  A02 B4_3 (.A(SI_15_0[3]), .B(EB_15_0[3]), .C(SI_15_0[2]), .D(EB_15_0[2]), .Z(B4_3_z));
  A02 B1_0 (.A(SI_15_0[1]), .B(EB_15_0[1]), .C(SI_15_0[0]), .D(EB_15_0[0]), .Z(B1_0_z));
  nand nand_2 (PB, B15_14_z, B13_12_z, B11_10_z, B9_8_z, B7_6_z, B5_4_z, B4_3_z, B1_0_z);

  // Notes on the sheet:
  //   Page 61 - CGA_ALU_WRF_RBLOCK_SEL16 
  //   EA15
  //   EA0
  //   SI0
  //   SI15
  //   EB15
  //   EB0
  //   SI0
  //   SI15
endmodule

module CGA_WRF_RBLOCK_PREG (
  input  [15:0] NLCA_15_0,
  input  [15:0] RB_15_0,
  input  XFETCHN,
  input  WR2,
  input  ALUCLKN,
  input  ALUCLK,
  output [15:0] P_15_0,
  output [15:0] PR_15_0
);

  wire not_1_out, R0_zn, R1_zn, R2_zn, R3_zn, R4_zn, R5_zn, R6_zn, R7_zn, R8_zn, R9_zn, R10_zn, R11_zn,
       R12_zn, R13_zn, R14_zn, R15_zn;

  not not_1 (not_1_out, XFETCHN);
  MUX31LP R0 (.D0(P_15_0[0]), .D1(NLCA_15_0[0]), .D2(RB_15_0[0]), .A(not_1_out), .B(WR2), .ZN(R0_zn));
  MUX31LP R1 (.D0(P_15_0[1]), .D1(NLCA_15_0[1]), .D2(RB_15_0[1]), .A(not_1_out), .B(WR2), .ZN(R1_zn));
  MUX31LP R2 (.D0(P_15_0[2]), .D1(NLCA_15_0[2]), .D2(RB_15_0[2]), .A(not_1_out), .B(WR2), .ZN(R2_zn));
  MUX31LP R3 (.D0(P_15_0[3]), .D1(NLCA_15_0[3]), .D2(RB_15_0[3]), .A(not_1_out), .B(WR2), .ZN(R3_zn));
  MUX31LP R4 (.D0(P_15_0[4]), .D1(NLCA_15_0[4]), .D2(RB_15_0[4]), .A(not_1_out), .B(WR2), .ZN(R4_zn));
  MUX31LP R5 (.D0(P_15_0[5]), .D1(NLCA_15_0[5]), .D2(RB_15_0[5]), .A(not_1_out), .B(WR2), .ZN(R5_zn));
  MUX31LP R6 (.D0(P_15_0[6]), .D1(NLCA_15_0[6]), .D2(RB_15_0[6]), .A(not_1_out), .B(WR2), .ZN(R6_zn));
  MUX31LP R7 (.D0(P_15_0[7]), .D1(NLCA_15_0[7]), .D2(RB_15_0[7]), .A(not_1_out), .B(WR2), .ZN(R7_zn));
  R81P R_P_0_7 (
    .A(R0_zn), .B(R1_zn), .C(R2_zn), .D(R3_zn), .E(R4_zn), .F(R5_zn), .G(R6_zn), .H(R7_zn), .CP(ALUCLK),
    .QAN(P_15_0[0]), .QBN(P_15_0[1]), .QCN(P_15_0[2]), .QDN(P_15_0[3]), .QEN(P_15_0[4]), .QFN(P_15_0[5]),
    .QGN(P_15_0[6]), .QHN(P_15_0[7]));  // open: QA, QB, QC, QD, QE, QF, QG, QH
  L8 L_PR_7_0 (
    .A(R0_zn), .B(R1_zn), .C(R2_zn), .D(R3_zn), .E(R4_zn), .F(R5_zn), .G(R6_zn), .H(R7_zn), .L(ALUCLKN),
    .QAN(PR_15_0[0]), .QBN(PR_15_0[1]), .QCN(PR_15_0[2]), .QDN(PR_15_0[3]), .QEN(PR_15_0[4]),
    .QFN(PR_15_0[5]), .QGN(PR_15_0[6]), .QHN(PR_15_0[7]));  // open: QA, QB, QC, QD, QE, QF, QG, QH
  MUX31LP R8 (.D0(P_15_0[8]), .D1(NLCA_15_0[8]), .D2(RB_15_0[8]), .A(not_1_out), .B(WR2), .ZN(R8_zn));
  MUX31LP R9 (.D0(P_15_0[9]), .D1(NLCA_15_0[9]), .D2(RB_15_0[9]), .A(not_1_out), .B(WR2), .ZN(R9_zn));
  MUX31LP R10 (.D0(P_15_0[10]), .D1(NLCA_15_0[10]), .D2(RB_15_0[10]), .A(not_1_out), .B(WR2), .ZN(R10_zn));
  MUX31LP R11 (.D0(P_15_0[11]), .D1(NLCA_15_0[11]), .D2(RB_15_0[11]), .A(not_1_out), .B(WR2), .ZN(R11_zn));
  MUX31LP R12 (.D0(P_15_0[12]), .D1(NLCA_15_0[12]), .D2(RB_15_0[12]), .A(not_1_out), .B(WR2), .ZN(R12_zn));
  MUX31LP R13 (.D0(P_15_0[13]), .D1(NLCA_15_0[13]), .D2(RB_15_0[13]), .A(not_1_out), .B(WR2), .ZN(R13_zn));
  MUX31LP R14 (.D0(P_15_0[14]), .D1(NLCA_15_0[14]), .D2(RB_15_0[14]), .A(not_1_out), .B(WR2), .ZN(R14_zn));
  MUX31LP R15 (.D0(P_15_0[15]), .D1(NLCA_15_0[15]), .D2(RB_15_0[15]), .A(not_1_out), .B(WR2), .ZN(R15_zn));
  R81P R_P_8_15 (
    .A(R8_zn), .B(R9_zn), .C(R10_zn), .D(R11_zn), .E(R12_zn), .F(R13_zn), .G(R14_zn), .H(R15_zn),
    .CP(ALUCLK), .QAN(P_15_0[8]), .QBN(P_15_0[9]), .QCN(P_15_0[10]), .QDN(P_15_0[11]), .QEN(P_15_0[12]),
    .QFN(P_15_0[13]), .QGN(P_15_0[14]), .QHN(P_15_0[15]));  // open: QA, QB, QC, QD, QE, QF, QG, QH
  L8 L_PR_8_15 (
    .A(R8_zn), .B(R9_zn), .C(R10_zn), .D(R11_zn), .E(R12_zn), .F(R13_zn), .G(R14_zn), .H(R15_zn),
    .L(ALUCLKN), .QAN(PR_15_0[8]), .QBN(PR_15_0[9]), .QCN(PR_15_0[10]), .QDN(PR_15_0[11]), .QEN(PR_15_0[12]),
    .QFN(PR_15_0[13]), .QGN(PR_15_0[14]), .QHN(PR_15_0[15]));  // open: QA, QB, QC, QD, QE, QF, QG, QH

  // Notes on the sheet:
  //   Page 62 - CGA_WRF_RBLOCK_PREG 
  //   IP0N
  //   IP1N
  //   IP2N
  //   IP3N
  //   IP4N
  //   IP5N
  //   IP6N
  //   IP7N
  //   IP0N
  //   PR7
  //   PR0
  //   P7
  //   P0
  //   IP8N
  //   IP9N
  //   IP10N
  //   IP11N
  //   IP12N
  //   IP13N
  //   IP14N
  //   IP15N
  //   IP8N
  //   PR15
  //   P15
  //   PR8
  //   P8
endmodule

module CGA_WRF_RBLOCK_LR16 (
  input  [15:0] RB_15_0,
  input  ALUCLK,
  input  WR,
  output [15:0] R_15_0,
  output [15:0] LR_15_0
);

  wire MUX_3_0_z0, MUX_3_0_z1, MUX_3_0_z2, MUX_3_0_z3, MUX_7_4_z0, MUX_7_4_z1, MUX_7_4_z2, MUX_7_4_z3,
       MUX_11_8_z0, MUX_11_8_z1, MUX_11_8_z2, MUX_11_8_z3, MUX_15_12_z0, MUX_15_12_z1, MUX_15_12_z2,
       MUX_15_12_z3, nand_1_out, not_1_out, not_2_out;

  not not_1 (not_1_out, WR);
  nand nand_1 (nand_1_out, ~ALUCLK, ~not_1_out);  // NAND_Gate
  MUX24P MUX_15_12 (
    .D00(R_15_0[15]), .D10(RB_15_0[15]), .D01(R_15_0[14]), .D11(RB_15_0[14]), .D02(R_15_0[13]),
    .D12(RB_15_0[13]), .D03(R_15_0[12]), .D13(RB_15_0[12]), .A(WR), .Z0(MUX_15_12_z0), .Z1(MUX_15_12_z1),
    .Z2(MUX_15_12_z2), .Z3(MUX_15_12_z3));
  MUX24P MUX_11_8 (
    .D00(R_15_0[11]), .D10(RB_15_0[11]), .D01(R_15_0[10]), .D11(RB_15_0[10]), .D02(R_15_0[9]),
    .D12(RB_15_0[9]), .D03(R_15_0[8]), .D13(RB_15_0[8]), .A(WR), .Z0(MUX_11_8_z0), .Z1(MUX_11_8_z1),
    .Z2(MUX_11_8_z2), .Z3(MUX_11_8_z3));
  not not_2 (not_2_out, nand_1_out);
  R81P R_15_8 (
    .A(MUX_15_12_z0), .B(MUX_15_12_z1), .C(MUX_15_12_z2), .D(MUX_15_12_z3), .E(MUX_11_8_z0), .F(MUX_11_8_z1),
    .G(MUX_11_8_z2), .H(MUX_11_8_z3), .CP(ALUCLK), .QA(R_15_0[15]), .QB(R_15_0[14]), .QC(R_15_0[13]),
    .QD(R_15_0[12]), .QE(R_15_0[11]), .QF(R_15_0[10]), .QG(R_15_0[9]), .QH(R_15_0[8]));  // open: QAN, QBN, QCN, QDN, QEN, QFN, QGN, QHN
  L8 L_15_8 (
    .A(MUX_15_12_z0), .B(MUX_15_12_z1), .C(MUX_15_12_z2), .D(MUX_15_12_z3), .E(MUX_11_8_z0), .F(MUX_11_8_z1),
    .G(MUX_11_8_z2), .H(MUX_11_8_z3), .L(not_2_out), .QA(LR_15_0[15]), .QB(LR_15_0[14]), .QC(LR_15_0[13]),
    .QD(LR_15_0[12]), .QE(LR_15_0[11]), .QF(LR_15_0[10]), .QG(LR_15_0[9]), .QH(LR_15_0[8]));  // open: QAN, QBN, QCN, QDN, QEN, QFN, QGN, QHN
  MUX24P MUX_7_4 (
    .D00(R_15_0[7]), .D10(RB_15_0[7]), .D01(R_15_0[6]), .D11(RB_15_0[6]), .D02(R_15_0[5]), .D12(RB_15_0[5]),
    .D03(R_15_0[4]), .D13(RB_15_0[4]), .A(WR), .Z0(MUX_7_4_z0), .Z1(MUX_7_4_z1), .Z2(MUX_7_4_z2),
    .Z3(MUX_7_4_z3));
  MUX24P MUX_3_0 (
    .D00(R_15_0[3]), .D10(RB_15_0[3]), .D01(R_15_0[2]), .D11(RB_15_0[2]), .D02(R_15_0[1]), .D12(RB_15_0[1]),
    .D03(R_15_0[0]), .D13(RB_15_0[0]), .A(WR), .Z0(MUX_3_0_z0), .Z1(MUX_3_0_z1), .Z2(MUX_3_0_z2),
    .Z3(MUX_3_0_z3));
  R81P R_7_0 (
    .A(MUX_7_4_z0), .B(MUX_7_4_z1), .C(MUX_7_4_z2), .D(MUX_7_4_z3), .E(MUX_3_0_z0), .F(MUX_3_0_z1),
    .G(MUX_3_0_z2), .H(MUX_3_0_z3), .CP(ALUCLK), .QA(R_15_0[7]), .QB(R_15_0[6]), .QC(R_15_0[5]),
    .QD(R_15_0[4]), .QE(R_15_0[3]), .QF(R_15_0[2]), .QG(R_15_0[1]), .QH(R_15_0[0]));  // open: QAN, QBN, QCN, QDN, QEN, QFN, QGN, QHN
  L8 L_7_0 (
    .A(MUX_7_4_z0), .B(MUX_7_4_z1), .C(MUX_7_4_z2), .D(MUX_7_4_z3), .E(MUX_3_0_z0), .F(MUX_3_0_z1),
    .G(MUX_3_0_z2), .H(MUX_3_0_z3), .L(not_2_out), .QA(LR_15_0[7]), .QB(LR_15_0[6]), .QC(LR_15_0[5]),
    .QD(LR_15_0[4]), .QE(LR_15_0[3]), .QF(LR_15_0[2]), .QG(LR_15_0[1]), .QH(LR_15_0[0]));  // open: QAN, QBN, QCN, QDN, QEN, QFN, QGN, QHN

  // Notes on the sheet:
  //   Page 63 - CGA_WRF_RBLOCK_LR16 
  //   IR15
  //   IR8
  //   /ALUCLK * WR
  //   LR8
  //   LR15
  //   LR0
  //   LR7
endmodule

module CGA_WRF_RBLOCK_DR16 (
  input  ALUCLK,
  input  WR,
  input  [15:0] RB_15_0,
  output [15:0] REG_15_0
);

  SCAN_FF R15 (.D(REG_15_0[15]), .TE(WR), .TI(RB_15_0[15]), .CLK(ALUCLK), .Q(REG_15_0[15]));  // open: QN
  SCAN_FF R14 (.D(REG_15_0[14]), .TE(WR), .TI(RB_15_0[14]), .CLK(ALUCLK), .Q(REG_15_0[14]));  // open: QN
  SCAN_FF R13 (.D(REG_15_0[13]), .TE(WR), .TI(RB_15_0[13]), .CLK(ALUCLK), .Q(REG_15_0[13]));  // open: QN
  SCAN_FF R12 (.D(REG_15_0[12]), .TE(WR), .TI(RB_15_0[12]), .CLK(ALUCLK), .Q(REG_15_0[12]));  // open: QN
  SCAN_FF R11 (.D(REG_15_0[11]), .TE(WR), .TI(RB_15_0[11]), .CLK(ALUCLK), .Q(REG_15_0[11]));  // open: QN
  SCAN_FF R10 (.D(REG_15_0[10]), .TE(WR), .TI(RB_15_0[10]), .CLK(ALUCLK), .Q(REG_15_0[10]));  // open: QN
  SCAN_FF R9 (.D(REG_15_0[9]), .TE(WR), .TI(RB_15_0[9]), .CLK(ALUCLK), .Q(REG_15_0[9]));  // open: QN
  SCAN_FF R8 (.D(REG_15_0[8]), .TE(WR), .TI(RB_15_0[8]), .CLK(ALUCLK), .Q(REG_15_0[8]));  // open: QN
  SCAN_FF R7 (.D(REG_15_0[7]), .TE(WR), .TI(RB_15_0[7]), .CLK(ALUCLK), .Q(REG_15_0[7]));  // open: QN
  SCAN_FF R6 (.D(REG_15_0[6]), .TE(WR), .TI(RB_15_0[6]), .CLK(ALUCLK), .Q(REG_15_0[6]));  // open: QN
  SCAN_FF R5 (.D(REG_15_0[5]), .TE(WR), .TI(RB_15_0[5]), .CLK(ALUCLK), .Q(REG_15_0[5]));  // open: QN
  SCAN_FF R4 (.D(REG_15_0[4]), .TE(WR), .TI(RB_15_0[4]), .CLK(ALUCLK), .Q(REG_15_0[4]));  // open: QN
  SCAN_FF R3 (.D(REG_15_0[3]), .TE(WR), .TI(RB_15_0[3]), .CLK(ALUCLK), .Q(REG_15_0[3]));  // open: QN
  SCAN_FF R2 (.D(REG_15_0[2]), .TE(WR), .TI(RB_15_0[2]), .CLK(ALUCLK), .Q(REG_15_0[2]));  // open: QN
  SCAN_FF R1 (.D(REG_15_0[1]), .TE(WR), .TI(RB_15_0[1]), .CLK(ALUCLK), .Q(REG_15_0[1]));  // open: QN
  SCAN_FF R0 (.D(REG_15_0[0]), .TE(WR), .TI(RB_15_0[0]), .CLK(ALUCLK), .Q(REG_15_0[0]));  // open: QN

  // Notes on the sheet:
  //   Page 64 - CGA_WRF_RBLOCK_DR16
endmodule

module test_WRF (
  input  in_1,
  input  [3:0] in_2,
  input  [3:0] in_3,
  input  in_4,
  input  [15:0] in_5,
  input  [15:0] in_6,
  input  in_7,
  input  [15:0] in_8,
  input  [15:0] in_9,
  input  [15:0] in_10
);

  wire cga_wrf_rblock_sel16_1_pa, cga_wrf_rblock_sel16_1_pb;
  wire [15:0] cga_wrf_1_a_15_0, cga_wrf_1_b_15_0, cga_wrf_1_br_15_0, cga_wrf_1_pr_15_0, cga_wrf_1_xr_15_0;

  CGA_WRF cga_wrf_1 (
    .BDEST(in_1), .LBA_3_0(in_2), .LAA_3_0(in_3), .ALUCLK(in_4), .RB_15_0(in_5), .NLCA_15_0(in_6),
    .XFETCHN(in_7), .B_15_0(cga_wrf_1_b_15_0), .A_15_0(cga_wrf_1_a_15_0), .PR_15_0(cga_wrf_1_pr_15_0),
    .BR_15_0(cga_wrf_1_br_15_0), .XR_15_0(cga_wrf_1_xr_15_0));  // open: WPN, WR3, WR7, EA_15_0
  CGA_WRF_RBLOCK_SEL16 cga_wrf_rblock_sel16_1 (
    .SI_15_0(in_8), .EA_15_0(in_9), .EB_15_0(in_10), .PA(cga_wrf_rblock_sel16_1_pa),
    .PB(cga_wrf_rblock_sel16_1_pb));
  // Probe on cga_wrf_1_pr_15_0
  // Probe on cga_wrf_1_br_15_0
  // Probe on cga_wrf_1_xr_15_0
  // Probe on cga_wrf_rblock_sel16_1_pa
  // Probe on cga_wrf_rblock_sel16_1_pb
  // Probe on cga_wrf_1_b_15_0
  // Probe on cga_wrf_1_a_15_0

  // Notes on the sheet:
  //   B
  //   A
endmodule
