// Logisim project DELILAH.circ as structural Verilog: 1 circuit, main circuit CGA
module CGA (
  input  XPTSTN,
  input  XSCOMM0,
  input  XCSCOMM1,
  input  XCSCOMM2,
  input  XCSCOMM3,
  input  XCSCOMM4,
  input  XCSMIS0,
  input  XCMIS1,
  input  XCD0,
  input  XCD1,
  input  XCD2,
  input  XCD3,
  input  XCD4,
  input  XCD5,
  input  XCD6,
  input  XCD7,
  input  XCD8,
  input  XCD9,
  input  XCD10,
  input  XCD11,
  input  XCD12,
  input  XCD13,
  input  XCD14,
  input  XCD15,
  input  XEDON,
  input  XCSCINSEL0,
  input  XCSCINSEL1,
  input  XCSSST0,
  input  XCSSST1,
  input  XALUCLK,
  input  XCSBIT0,
  input  XCSBIT1,
  input  XCSBIT2,
  input  XCSBIT3,
  input  XCSBIT4,
  input  XCSBIT5,
  input  XCSBIT6,
  input  XCSBIT7,
  input  XCSBIT8,
  input  XCSBIT9,
  input  XCSBIT10,
  input  XCSBIT11,
  input  XCSBIT12,
  input  XCSBIT13,
  input  XCSBIT14,
  input  XCSBIT15,
  input  XCSALUM0,
  input  XCSALUM1,
  input  XCSALUI0,
  input  XCSALUI1,
  input  XCSALUI2,
  input  XCSALUI3,
  input  XCSALUI4,
  input  XCSALUI5,
  input  XCSALUI6,
  input  XCSALUI7,
  input  XCSALUI8,
  input  XCSIDBS0,
  input  XCSIDBS1,
  input  XCSIDBS2,
  input  XCSIDBS3,
  input  XCSIDBS4,
  input  XMRN,
  input  XCSLOOP,
  input  XCSECOND,
  input  XCSRASEL0,
  input  XCSRASEL1,
  input  XCSRB0,
  input  XCSRB1,
  input  XCSRB2,
  input  XCSRB3,
  input  XCSBIT20,
  input  XCSRBSEL0,
  input  XCSRBSEL1,
  input  XCSSCOND,
  input  XCSTS3,
  input  XCSTS4,
  input  XCSTS5,
  input  XCSTS6,
  input  XCSVECT,
  input  XCSXRF3,
  input  XEWCAN,
  input  XMAPN,
  input  XSPARE,
  input  XSTP,
  input  XETRAPN,
  input  XFTRAPN,
  input  XVTRAPN,
  input  XPT9,
  input  XPT10,
  input  XPT11,
  input  XPT12,
  input  XPT13,
  input  XPT14,
  input  XPT15,
  input  XTCLK,
  input  XPANN,
  input  XMCLK,
  input  XBINT10N,
  input  XBINT11N,
  input  XBINT12N,
  input  XBINT13N,
  input  XILCSN,
  input  XBINT15N,
  input  XEMPIDN,
  input  XIOXERRN,
  input  XMORN,
  input  XPARERRN,
  input  XPOWFAILN,
  input  XTSEL0,
  input  XTSEL1,
  input  XTSEL2,
  input  [15:0] XFIDB_15_0_IN,
  input  [15:0] FIDBI_15_0,
  input  BDEST,
  output XLSHADOW,
  output [3:0] XPIL_3_0,
  output XBRKN,
  output XIONI,
  output XINTRQN,
  output XDOUBLE,
  output XPONI,
  output XACONDN,
  output XWCSN,
  output XERFN,
  output XWRTRF,
  output XECCR,
  output XTRAPN,
  output [3:0] XLAA_3_0,
  output [3:0] XLBA_3_0,
  output [1:0] XRF_1_0,
  output [1:0] XPCR_1_0,
  output [4:0] XTEST_4_0,
  output [12:0] XMA_12_0,
  output [13:0] XLA_23_10,
  output [9:0] XMCA_9_0,
  output [15:0] XFIDB_15_0_OUT
);

  wire BDEST_t, CBRKN, CFETCH, CLFFN, COND, CRY, CSMREQ, DCD_p27, DCD_p30, DCD_p36, DCD_p37, DCD_p38,
       DCD_p39, DCD_p40, DEEP, DSTOPN, DZD, F11, F15, FIDBO5, INDN, INTR_epicmaskn, INTR_higsn, INTR_logsn,
       INTR_pd, IRQ, LCZN, LDDBRN, LDGPRN, LDIRV, LDLCN, LDPILN, LWCAN, MI, OOD, OVF, PN, PTM, RESTR, SGR,
       TN, TRAP_pviol, UPN, VACCN, VEX, WPN, WR3, WR7, WRITEN, XFETCHN, Z, ZF;
  wire [2:0] INTR_pics_2_0, INTR_picv_2_0;
  wire [3:0] PIL, SC_6_3, TVEC_3_0;
  wire [15:0] ALU_rb_15_0, EA_15_0, FIDBO_15_0, INTR_picmask_15_0, MAC_nlca_15_0, WRF_a_15_0, WRF_b_15_0,
       WRF_br_15_0, WRF_pr_15_0, WRF_xr_15_0, XFIDBI_15_0;
  wire [15:2] PCR_15_0;

  // Probe on {FIDBO_15_0[15:6], FIDBO5, FIDBO_15_0[4:0]}
  BusDriver16 BD_FIDBO (
    .A_15_0({FIDBO_15_0[15:6], FIDBO5, FIDBO_15_0[4:0]}), .IN_15_0(XFIDB_15_0_IN), .EN(XEDON), .TN(XPTSTN),
    .ZI_15_0(XFIDBI_15_0), .OUT_15_0(XFIDB_15_0_OUT));
  // CGA_DCD DCD: pin names not known; wires that end beside it: {XCSCOMM4, XCSCOMM3, XCSCOMM2, XCSCOMM1, XSCOMM0}, {XCMIS1, XCSMIS0}, XMCLK, XILCSN, F15, ZF, CRY, SGR, WPN, XPONI, VEX, XBRKN, FIDBO5, XMRN, XLSHADOW, XINTRQN, {XCSIDBS4, XCSIDBS3, XCSIDBS2, XCSIDBS1, XCSIDBS0}, INDN, XFETCHN, CBRKN, DSTOPN, LDLCN, LDPILN, LDIRV, CSMREQ, LDDBRN, DCD_p27, WRITEN, CLFFN, DCD_p30, LWCAN, LDGPRN, XWRTRF, CFETCH, VACCN, DCD_p36, DCD_p37, DCD_p38, DCD_p39, DCD_p40, XERFN
  // Probe on TVEC_3_0
  // Probe on {XTSEL2, XTSEL1, XTSEL0}
  CGA_INTR INTR (
    .PANN(XPANN), .MCLK(XMCLK), .CLIRQN(DCD_p36), .EMPIDN(XEMPIDN), .BINT15N(XBINT15N), .POWFAILN(XPOWFAILN),
    .NORN(XMORN), .PARERRN(XPARERRN), .IOXERRN(XIOXERRN), .Z(Z), .BINT13N(XBINT13N), .BINT12N(XBINT12N),
    .BINT11N(XBINT11N), .BINT10N(XBINT10N), .FIDBO_15_0({FIDBO_15_0[15:6], FIDBO5, FIDBO_15_0[4:0]}),
    .LAA_3_0(XLAA_3_0), .EPIC(DCD_p30), .INTRQN(XINTRQN), .PICMASK_15_0(INTR_picmask_15_0),
    .HIGSN(INTR_higsn), .PD(INTR_pd), .PICV_2_0(INTR_picv_2_0), .IRQ(IRQ), .LOGSN(INTR_logsn),
    .PICS_2_0(INTR_pics_2_0), .EPICMASKN(INTR_epicmaskn));
  CGA_MIC MIC (
    .CSBIT_15_0({XCSBIT15, XCSBIT14, XCSBIT13, XCSBIT12, XCSBIT11, XCSBIT10, XCSBIT9, XCSBIT8, XCSBIT7, XCSBIT6, XCSBIT5, XCSBIT4, XCSBIT3, XCSBIT2, XCSBIT1, XCSBIT0}),
    .CSBIT20(XCSBIT20), .MI(MI), .IRQ(IRQ), .RESTR(RESTR), .CFETCH(CFETCH), .SPARE(XSPARE), .OVF(OVF),
    .CRY(CRY), .F11(F11), .F15(F15), .ZF(ZF), .STP(XSTP), .ALUCLK(XALUCLK), .MCLK(XMCLK), .CSLOOP(XCSLOOP),
    .CSECOND(XCSECOND), .CLFFN(CLFFN), .CSALUI8(XCSALUI8), .CSCOND(XCSSCOND), .ILCSN(XILCSN),
    .CSTS_6_3({XCSTS6, XCSTS5, XCSTS4, XCSTS3}), .TVEC_3_0(TVEC_3_0), .TRAPN(XTRAPN), .MAPN(XMAPN),
    .EWCAN(XEWCAN), .CSMIS0(XCSMIS0), .CSVECT(XCSVECT),
    .CD_15_0({XCD15, XCD14, XCD13, XCD12, XCD11, XCD10, XCD9, XCD8, XCD7, XCD6, XCD5, XCD4, XCD3, XCD2, XCD1, XCD0}),
    .LDIRV(LDIRV), .LWCAN(LWCAN), .MRN(XMRN), .LDLCN(LDLCN), .PIL_3_0(XPIL_3_0), .CSXRF3(XCSXRF3),
    .CSRB_3_0({XCSRB3, XCSRB2, XCSRB1, XCSRB0}), .CSRASEL_1_0({XCSRASEL1, XCSRASEL0}),
    .CSRBSEL_1_0({XCSRBSEL1, XCSRBSEL0}), .DZD(DZD), .COND(COND), .OOD(OOD), .ACONDN(XACONDN),
    .SC_6_3(SC_6_3), .MA_12_0(XMA_12_0), .WCSN(XWCSN), .DEEP(DEEP), .UPN(UPN), .PN(PN), .LCZN(LCZN), .TN(TN),
    .LAA_3_0(XLAA_3_0), .LBA_3_0(XLBA_3_0), .RF_1_0(XRF_1_0));  // open: LCZ
  CGA_MAC MAC (
    .MCLK(XMCLK), .PTM(PTM), .FIDBO_15_0({FIDBO_15_0[15:6], FIDBO5, FIDBO_15_0[4:0]}), .PONI(XPONI),
    .CMIS_1_0({XCMIS1, XCSMIS0}), .CSCOMM_4_0({XCSCOMM4, XCSCOMM3, XCSCOMM2, XCSCOMM1, XSCOMM0}), .WR3(WR3),
    .WR7(WR7), .ILCSN(XILCSN), .DOUBLE(XDOUBLE), .CSMREQ(CSMREQ),
    .CD_15_0({XCD15, XCD14, XCD13, XCD12, XCD11, XCD10, XCD9, XCD8, XCD7, XCD6, XCD5, XCD4, XCD3, XCD2, XCD1, XCD0}),
    .RB_15_0(ALU_rb_15_0), .XR_15_0(WRF_xr_15_0), .BR_15_0(WRF_br_15_0), .PR_15_0(WRF_pr_15_0), .VEX(VEX),
    .PCR_15_7_2_0({PCR_15_0, XPCR_1_0}), .LA_23_10(XLA_23_10), .LSHADOW(XLSHADOW), .ECCR(XECCR),
    .MCA_9_0(XMCA_9_0), .NLCA_15_0(MAC_nlca_15_0));
  // Probe on SC_6_3
  // Probe on XTEST_4_0
  CGA_TESTMUX TESTMUX (
    .TVEC_3_0(TVEC_3_0), .SC_6_3(SC_6_3), .PTREEOUT(1'b1), .VACCN(VACCN), .MI(MI), .OVF(OVF), .UPN(UPN),
    .LCZN(LCZN), .CSMREQ(CSMREQ), .INDN(INDN), .PTM(PTM), .ZF(ZF), .COND(COND), .DZD(DZD), .LDIRV(LDIRV),
    .CBRKN(CBRKN), .WPN(WPN), .F15(F15), .PN(PN), .OOD(OOD), .VEX(VEX), .WRITEN(WRITEN), .XFETCHN(XFETCHN),
    .SGR(SGR), .TN(TN), .CFETCH(CFETCH), .DSTOPN(DSTOPN), .CRY(CRY), .RESTR(RESTR), .DEEP(DEEP),
    .TSEL_2_0({XTSEL2, XTSEL1, XTSEL0}), .PTSTN(XPTSTN), .TEST_4_0(XTEST_4_0));
  // Probe on {PCR_15_0, XPCR_1_0}
  CGA_ALU ALU (
    .A_15_0(WRF_a_15_0), .B_15_0(WRF_b_15_0),
    .CSBIT_15_0({XCSBIT15, XCSBIT14, XCSBIT13, XCSBIT12, XCSBIT11, XCSBIT10, XCSBIT9, XCSBIT8, XCSBIT7, XCSBIT6, XCSBIT5, XCSBIT4, XCSBIT3, XCSBIT2, XCSBIT1, XCSBIT0}),
    .EA_15_0(EA_15_0), .FIDBI_15_0(FIDBI_15_0),
    .CSIDBS_4_0({XCSIDBS4, XCSIDBS3, XCSIDBS2, XCSIDBS1, XCSIDBS0}), .LBA_3_0(XLBA_3_0), .LAA_3_0(XLAA_3_0),
    .LDPILN(LDPILN), .LDDBRN(LDDBRN), .XFETCHN(XFETCHN), .LDGPRN(LDGPRN), .CSMIS_1_0({XCMIS1, XCSMIS0}),
    .CSSST_1_0({XCSSST1, XCSSST0}), .CSCINSEL_1_0({XCSCINSEL1, XCSCINSEL0}), .LDIRV(LDIRV), .UPN(UPN),
    .LCZN(LCZN),
    .CSALUI_8_0({XCSALUI8, XCSALUI7, XCSALUI6, XCSALUI5, XCSALUI4, XCSALUI3, XCSALUI2, XCSALUI1, XCSALUI0}),
    .CSALUM_1_0({XCSALUM1, XCSALUM0}), .ALUCLK(XALUCLK),
    .CD_15_0({XCD15, XCD14, XCD13, XCD12, XCD11, XCD10, XCD9, XCD8, XCD7, XCD6, XCD5, XCD4, XCD3, XCD2, XCD1, XCD0}),
    .ZF(CRY), .CRY(ZF), .SGR(SGR), .OVF(OVF), .RB_15_0(ALU_rb_15_0), .F11(F11), .F15(F15), .BDEST(BDEST_t),
    .MI(MI), .PTM(PTM), .Z(Z), .PIL(PIL), .DOUBLE(XDOUBLE), .PONI(XPONI), .IONI(XIONI),
    .FIDBO_15_0({FIDBO_15_0[15:6], FIDBO5, FIDBO_15_0[4:0]}));
  CGA_TRAP TRAP (
    .CBRKN(CBRKN), .ETRAPN(XETRAPN), .PT_15_9({XPT15, XPT14, XPT13, XPT12, XPT11, XPT10, XPT9}),
    .PCR_1_0(XPCR_1_0), .FETCHN(DCD_p27), .WRITEN(WRITEN), .INDN(INDN), .INTRQN(XINTRQN), .PANN(XPANN),
    .VACCN(VACCN), .PONI(XPONI), .TCLK(XTCLK), .VTRAPN(XVTRAPN), .FTRAPN(XFTRAPN), .DSTOPN(DSTOPN),
    .BRKN(XBRKN), .TRAPN(XTRAPN), .RESTR(RESTR), .TVEC_3_0(TVEC_3_0), .PVIOL(TRAP_pviol));
  CGA_IDBCTL IDBCTL (
    .MCLK(XMCLK), .VACCN(VACCN), .LA_21_10(XLA_23_10[11:0]), .FETCHN(DCD_p27), .PVIOL(TRAP_pviol),
    .EPGSN(DCD_p37), .EPCRN(DCD_p38), .EPICSN(DCD_p40), .EPICVN(DCD_p39), .EPICMASKN(INTR_epicmaskn),
    .PD(INTR_pd), .HIGSN(INTR_higsn), .LOGSN(INTR_logsn), .PCR_15_0({PCR_15_0, XPCR_1_0}),
    .XFIDBI_15_0(XFIDBI_15_0), .PICMASK_15_0(INTR_picmask_15_0), .PICV_2_0(INTR_picv_2_0),
    .PICS_2_0(INTR_pics_2_0), .FIDBI_15_0(FIDBI_15_0));
  // Probe on FIDBI_15_0
  CGA_WRF WRF (
    .BDEST(BDEST), .LBA_3_0(XLBA_3_0), .LAA_3_0(XLAA_3_0), .ALUCLK(XALUCLK), .RB_15_0(ALU_rb_15_0),
    .NLCA_15_0(MAC_nlca_15_0), .XFETCHN(XFETCHN), .WPN(WPN), .WR3(WR3), .WR7(WR7), .B_15_0(WRF_b_15_0),
    .A_15_0(WRF_a_15_0), .PR_15_0(WRF_pr_15_0), .BR_15_0(WRF_br_15_0), .XR_15_0(WRF_xr_15_0),
    .EA_15_0(EA_15_0));

  // Other names for the same wires on the sheet: ACONDN = XACONDN; ALUCLK = XALUCLK; BINT10N = XBINT10N;
  //   BINT11N = XBINT11N; BINT12N = XBINT12N; BINT13N = XBINT13N; BINT15N = XBINT15N; BRKN = XBRKN; CD0 = XCD0;
  //   CD_15_0[15:0] = {XCD15, XCD14, XCD13, XCD12, XCD11, XCD10, XCD9, XCD8, XCD7, XCD6, XCD5, XCD4, XCD3, XCD2, XCD1, XCD0};
  //   CD1 = XCD1; CD2 = XCD2; CD3 = XCD3; CD4 = XCD4; CD5 = XCD5; CD6 = XCD6; CD7 = XCD7; CD8 = XCD8; CD9 = XCD9;
  //   CD10 = XCD10; CD11 = XCD11; CD12 = XCD12; CD13 = XCD13; CD14 = XCD14; CD15 = XCD15; CSALUI0 = XCSALUI0;
  //   CSALUI_8_0[8:0] = {XCSALUI8, XCSALUI7, XCSALUI6, XCSALUI5, XCSALUI4, XCSALUI3, XCSALUI2, XCSALUI1, XCSALUI0};
  //   CSALUI1 = XCSALUI1; CSALUI2 = XCSALUI2; CSALUI3 = XCSALUI3; CSALUI4 = XCSALUI4; CSALUI5 = XCSALUI5;
  //   CSALUI6 = XCSALUI6; CSALUI7 = XCSALUI7; CSALUI8 = XCSALUI8; CSALUM0 = XCSALUM0;
  //   CSALUM_1_0[1:0] = {XCSALUM1, XCSALUM0}; CSALUM1 = XCSALUM1; CSBIT20 = XCSBIT20; CSBIT0 = XCSBIT0;
  //   CSBIT_15_0[15:0] = {XCSBIT15, XCSBIT14, XCSBIT13, XCSBIT12, XCSBIT11, XCSBIT10, XCSBIT9, XCSBIT8, XCSBIT7, XCSBIT6, XCSBIT5, XCSBIT4, XCSBIT3, XCSBIT2, XCSBIT1, XCSBIT0};
  //   CSBIT1 = XCSBIT1; CSBIT2 = XCSBIT2; CSBIT3 = XCSBIT3; CSBIT4 = XCSBIT4; CSBIT5 = XCSBIT5; CSBIT6 = XCSBIT6;
  //   CSBIT7 = XCSBIT7; CSBIT8 = XCSBIT8; CSBIT9 = XCSBIT9; CSBIT10 = XCSBIT10; CSBIT11 = XCSBIT11;
  //   CSBIT12 = XCSBIT12; CSBIT13 = XCSBIT13; CSBIT14 = XCSBIT14; CSBIT15 = XCSBIT15; CSCINSEL0 = XCSCINSEL0;
  //   CSCINSEL_1_0[1:0] = {XCSCINSEL1, XCSCINSEL0}; CSCINSEL1 = XCSCINSEL1; CSCOMM0 = XSCOMM0;
  //   CSCOMM_4_0[4:0] = {XCSCOMM4, XCSCOMM3, XCSCOMM2, XCSCOMM1, XSCOMM0}; CSCOMM1 = XCSCOMM1; CSCOMM2 = XCSCOMM2;
  //   CSCOMM3 = XCSCOMM3; CSCOMM4 = XCSCOMM4; CSECOND = XCSECOND; CSIDBS0 = XCSIDBS0;
  //   CSIDBS_4_0[4:0] = {XCSIDBS4, XCSIDBS3, XCSIDBS2, XCSIDBS1, XCSIDBS0}; CSIDBS1 = XCSIDBS1; CSIDBS2 = XCSIDBS2;
  //   CSIDBS3 = XCSIDBS3; CSIDBS4 = XCSIDBS4; CSLOOP = XCSLOOP; CSMIS0 = XCSMIS0; CSMIS_1_0[1:0] = {XCMIS1, XCSMIS0};
  //   CSMIS1 = XCMIS1; CSRASEL0 = XCSRASEL0; CSRASEL_1_0[1:0] = {XCSRASEL1, XCSRASEL0}; CSRASEL1 = XCSRASEL1;
  //   CSRB0 = XCSRB0; CSRB_3_0[3:0] = {XCSRB3, XCSRB2, XCSRB1, XCSRB0}; CSRB1 = XCSRB1; CSRB2 = XCSRB2;
  //   CSRB3 = XCSRB3; CSRBSEL0 = XCSRBSEL0; CSRBSEL_1_0[1:0] = {XCSRBSEL1, XCSRBSEL0}; CSRBSEL1 = XCSRBSEL1;
  //   CSSCOND = XCSSCOND; CSSST0 = XCSSST0; CSSST_1_0[1:0] = {XCSSST1, XCSSST0}; CSSST1 = XCSSST1; CSTS3 = XCSTS3;
  //   CSTS_6_3[3:0] = {XCSTS6, XCSTS5, XCSTS4, XCSTS3}; CSTS4 = XCSTS4; CSTS5 = XCSTS5; CSTS6 = XCSTS6;
  //   CSVECT = XCSVECT; CSXRF3 = XCSXRF3; DOUBLE = XDOUBLE; ECCR = XECCR; EDON = XEDON; EMPIDN = XEMPIDN;
  //   ERFN = XERFN; ETRAPN = XETRAPN; EWCAN = XEWCAN; FIDBO_15_0[5] = FIDBO5; FTRAPN = XFTRAPN; ILCSN = XILCSN;
  //   INTRQN = XINTRQN; IONI = XIONI; IOXERRN = XIOXERRN; LA_21_10[11:0] = XLA_23_10[11:0];
  //   LA_23_10[13:0] = XLA_23_10; LAA_3_0[3:0] = XLAA_3_0; LBA_3_0[3:0] = XLBA_3_0; LSHADOW = XLSHADOW;
  //   MA_12_0[12:0] = XMA_12_0; MAPN = XMAPN; MCA_9_0[9:0] = XMCA_9_0; MCLK = XMCLK; MORN = XMORN; MRN = XMRN;
  //   PANN = XPANN; PARERRN = XPARERRN; PCR_1_0[1:0] = XPCR_1_0; PCR_15_0[1:0] = XPCR_1_0; PIL_3_0[3:0] = XPIL_3_0;
  //   PONI = XPONI; POWFAILN = XPOWFAILN; PT9 = XPT9; PT_15_9[6:0] = {XPT15, XPT14, XPT13, XPT12, XPT11, XPT10, XPT9};
  //   PT10 = XPT10; PT11 = XPT11; PT12 = XPT12; PT13 = XPT13; PT14 = XPT14; PT15 = XPT15; PTSTN = XPTSTN;
  //   RF_1_0[1:0] = XRF_1_0; SPARE = XSPARE; STP = XSTP; TCLK = XTCLK; TEST_4_0[4:0] = XTEST_4_0; TRAPN = XTRAPN;
  //   TSEL0 = XTSEL0; TSEL_2_0[2:0] = {XTSEL2, XTSEL1, XTSEL0}; TSEL1 = XTSEL1; TSEL2 = XTSEL2; VTRAPN = XVTRAPN;
  //   WCSN = XWCSN; WRTRF = XWRTRF

  // Notes on the sheet:
  //   Page 3 - CGA - Sheet 2/8  (down)
  //   Page 4 - CGA - Sheet 3/8  (down)
  //   Page 7 - CGA - Sheet 6/8 (down)
  //   Page 8 - CGA - Sheet 7/8 (down)
  //   Page 2 - CGA - Sheet 1/8
  //   Page 5 - CGA - Sheet 4/8  (down)
  //   Page 6 - CGA - Sheet 5/8 (down)
  //   Page 9 - CGA - Sheet 8/8 (down)
  //   Normally IN and OUT will be connected together - but Logisim doesnt allow IN and OUT on the same pin
  //   WILL SHOW RED AS THERE IS LATCHES THAT IS "UNDEFINED" UNTIL USED
endmodule
