// Logisim project ND_LIB.circ as structural Verilog: 26 circuits, main circuit SCAN_FF
module SCAN_FF (
  input  D,
  input  TE,
  input  TI,
  input  CLK,
  output Q,
  output QN
);

  wire and_1_out, and_2_out, not_1_out, or_1_out;

  not not_1 (not_1_out, TE);
  and and_1 (and_1_out, D, not_1_out);
  and and_2 (and_2_out, TE, TI);
  or or_1 (or_1_out, and_1_out, and_2_out);
  D_Flip_Flop d_ff_1 (.D(or_1_out), .clk(CLK), .Q(Q), .Qn(QN));  // open: preset, reset

  // Notes on the sheet:
  //   Scan Flip Flop
  //   Positive-edge-triggered D flip-flop with scan
  //   It is a D flip-flop with a 2-input multiplexer on the D input
  //   Used in some Diagrams, was not a standard component in LogiSim so it was added.
  //   Also known as FDIS (In the Delilah Schematics)
  //   When TE (test enable) input is negated, circuit behaves like an ordinary D flip-flop. When TE is asserted, it takes its data from TI (test input) instead of from D.
endmodule

module SCAN_WITH_RESET_N (
  input  D,
  input  TE,
  input  TI,
  input  CLK,
  input  R,
  output Q,
  output QN
);

  wire and_1_out, and_2_out, not_1_out, not_2_out, or_1_out;

  not not_1 (not_1_out, TE);
  not not_2 (not_2_out, R);
  and and_1 (and_1_out, D, not_1_out);
  and and_2 (and_2_out, TE, TI);
  or or_1 (or_1_out, and_1_out, and_2_out);
  D_Flip_Flop d_ff_1 (.D(or_1_out), .clk(CLK), .Q(Q), .Qn(QN), .reset(not_2_out));  // open: preset

  // Notes on the sheet:
  //   Reset is NEGATED
  //   Positive-edge-triggered D flip-flop with scan
  //   It is a D flip-flop with a 2-input multiplexer on the D input
  //   Used in some Diagrams, was not a standard component in LogiSim so it was added.
  //   When TE (test enable) input is negated, circuit behaves like an ordinary D flip-flop. When TE is asserted, it takes its data from TI (test input) instead of from D.
endmodule

module SCAN_WITH_SET_N (
  input  S,
  input  D,
  input  TE,
  input  TI,
  input  CLK,
  output Q,
  output QN
);

  wire and_1_out, and_2_out, not_1_out, not_2_out, or_1_out;

  not not_1 (not_1_out, S);
  not not_2 (not_2_out, TE);
  and and_1 (and_1_out, D, not_2_out);
  and and_2 (and_2_out, TE, TI);
  or or_1 (or_1_out, and_1_out, and_2_out);
  D_Flip_Flop d_ff_1 (.D(or_1_out), .clk(CLK), .Q(Q), .Qn(QN), .preset(not_1_out));  // open: reset

  // Notes on the sheet:
  //   Set is NEGATED
  //   Positive-edge-triggered D flip-flop with scan
  //   It is a D flip-flop with a 2-input multiplexer on the D input
  //   Used in some Diagrams, was not a standard component in LogiSim so it was added.
  //   When TE (test enable) input is negated, circuit behaves like an ordinary D flip-flop. When TE is asserted, it takes its data from TI (test input) instead of from D.
endmodule

module A02 (
  input  A,
  input  B,
  input  C,
  input  D,
  output Z
);

  wire and_1_out, and_2_out, or_1_out;

  and and_1 (and_1_out, A, B);
  and and_2 (and_2_out, C, D);
  or or_1 (or_1_out, and_1_out, and_2_out);
  not not_1 (Z, or_1_out);

  // Notes on the sheet:
  //   A02
  //   From Lasse Bockelie:
  //   As you can see, there wasn't even room for the title field on this page
  //   AO2 is an And Or Invert gate. So 2 And followed by an Or gate and then inverted. The function is a selector (multiplexer) of each of the 4 16-bit signal groups.
  //   AO2 was a component of LSI Logic's library on Daisy. The symbol for it was like in your drawing, but we didn't have room for that. We could also make our own components on Daisy, so I made the shrunken one.
endmodule

module ND38GLP (
  input  A,
  input  B,
  input  C,
  input  G,
  output Z0,
  output Z1,
  output Z2,
  output Z3,
  output Z4,
  output Z5,
  output Z6,
  output Z7
);

  wire decoder_1_out0, decoder_1_out1, decoder_1_out2, decoder_1_out3, decoder_1_out4, decoder_1_out5,
       decoder_1_out6, decoder_1_out7;

  // NOT_Gate not_1 is placed but not wired
  Decoder #(.select(3)) decoder_1 (
    .out0(decoder_1_out0), .out1(decoder_1_out1), .out2(decoder_1_out2), .out3(decoder_1_out3),
    .out4(decoder_1_out4), .out5(decoder_1_out5), .out6(decoder_1_out6), .out7(decoder_1_out7),
    .sel({C, B, A}), .en(G));
  not not_2 (Z0, decoder_1_out0);
  not not_3 (Z1, decoder_1_out1);
  not not_4 (Z2, decoder_1_out2);
  not not_5 (Z3, decoder_1_out3);
  not not_6 (Z4, decoder_1_out4);
  not not_7 (Z5, decoder_1_out5);
  not not_8 (Z6, decoder_1_out6);
  not not_9 (Z7, decoder_1_out7);

  // Notes on the sheet:
  //   3 to 8 decoder
  //   https://www.elprocus.com/designing-4-to-16-decoder-using-3-to-8-decoder/
endmodule

module ND38GHP (
  input  A,
  input  B,
  input  C,
  input  G,
  output Z0,
  output Z1,
  output Z2,
  output Z3,
  output Z4,
  output Z5,
  output Z6,
  output Z7
);

  wire decoder_1_out0, decoder_1_out1, decoder_1_out2, decoder_1_out3, decoder_1_out4, decoder_1_out5,
       decoder_1_out6, decoder_1_out7;

  Decoder #(.select(3)) decoder_1 (
    .out0(decoder_1_out0), .out1(decoder_1_out1), .out2(decoder_1_out2), .out3(decoder_1_out3),
    .out4(decoder_1_out4), .out5(decoder_1_out5), .out6(decoder_1_out6), .out7(decoder_1_out7),
    .sel({C, B, A}), .en(G));
  not not_1 (Z0, decoder_1_out0);
  not not_2 (Z1, decoder_1_out1);
  not not_3 (Z2, decoder_1_out2);
  not not_4 (Z3, decoder_1_out3);
  not not_5 (Z4, decoder_1_out4);
  not not_6 (Z5, decoder_1_out5);
  not not_7 (Z6, decoder_1_out6);
  not not_8 (Z7, decoder_1_out7);

  // Notes on the sheet:
  //   3 to 8 decoder
  //   TODO: Similar to the ND38GLP.. what is different ?
endmodule

module LATCH (
  input  D,
  input  ENABLE,
  output Q,
  output QN
);

  wire nand_1_out, nand_2_out, not_1_out;

  not not_1 (not_1_out, D);
  nand nand_1 (nand_1_out, D, ENABLE);
  nand nand_2 (nand_2_out, ENABLE, not_1_out);
  nand nand_3 (Q, nand_1_out, QN);
  nand nand_4 (QN, Q, nand_2_out);
endmodule

module L4 (
  input  A,
  input  B,
  input  C,
  input  D,
  input  L,
  output QA,
  output QAN,
  output QB,
  output QBN,
  output QC,
  output QCN,
  output QD,
  output QDN
);

  LATCH L0 (.D(A), .ENABLE(L), .Q(QA), .QN(QAN));
  LATCH L1 (.D(B), .ENABLE(L), .Q(QB), .QN(QBN));
  LATCH L2 (.D(C), .ENABLE(L), .Q(QC), .QN(QCN));
  LATCH L3 (.D(D), .ENABLE(L), .Q(QD), .QN(QDN));
endmodule

module L8 (
  input  A,
  input  B,
  input  C,
  input  D,
  input  E,
  input  F,
  input  G,
  input  H,
  input  L,
  output QA,
  output QAN,
  output QB,
  output QBN,
  output QC,
  output QCN,
  output QD,
  output QDN,
  output QE,
  output QEN,
  output QF,
  output QFN,
  output QG,
  output QGN,
  output QH,
  output QHN
);

  LATCH L0 (.D(A), .ENABLE(L), .Q(QA), .QN(QAN));
  LATCH L1 (.D(B), .ENABLE(L), .Q(QB), .QN(QBN));
  LATCH L2 (.D(C), .ENABLE(L), .Q(QC), .QN(QCN));
  LATCH L3 (.D(D), .ENABLE(L), .Q(QD), .QN(QDN));
  LATCH L4 (.D(E), .ENABLE(L), .Q(QE), .QN(QEN));
  LATCH L5 (.D(F), .ENABLE(L), .Q(QF), .QN(QFN));
  LATCH L6 (.D(G), .ENABLE(L), .Q(QG), .QN(QGN));
  LATCH L7 (.D(H), .ENABLE(L), .Q(QH), .QN(QHN));
endmodule

module SR44 (
  input  SI,
  input  A,
  input  B,
  input  C,
  input  D,
  input  L,
  input  CP,
  output QA,
  output QAN,
  output QB,
  output QBN,
  output QC,
  output QCN,
  output QD,
  output QDN
);

  wire multiplexer_1_out, multiplexer_2_out, multiplexer_3_out, multiplexer_4_out;

  Multiplexer multiplexer_1 (.in0(SI), .in1(A), .out(multiplexer_1_out), .sel(L));
  Multiplexer multiplexer_2 (.in0(QA), .in1(B), .out(multiplexer_2_out), .sel(L));
  Multiplexer multiplexer_3 (.in0(QB), .in1(C), .out(multiplexer_3_out), .sel(L));
  Multiplexer multiplexer_4 (.in0(QC), .in1(D), .out(multiplexer_4_out), .sel(L));
  D_Flip_Flop d_ff_1 (.D(multiplexer_1_out), .clk(CP), .Q(QA), .Qn(QAN));  // open: preset, reset
  D_Flip_Flop d_ff_2 (.D(multiplexer_2_out), .clk(CP), .Q(QB), .Qn(QBN));  // open: preset, reset
  D_Flip_Flop d_ff_3 (.D(multiplexer_3_out), .clk(CP), .Q(QC), .Qn(QCN));  // open: preset, reset
  D_Flip_Flop d_ff_4 (.D(multiplexer_4_out), .clk(CP), .Q(QD), .Qn(QDN));  // open: preset, reset

  // Notes on the sheet:
  //   Used by CGA_MIC_STACK_BIT12 (Page 17 and 18)
  //   4 bit shift register with Serial Input (SI) and Load (L) which triggers parallell load from A-D
endmodule

module MUX21L (
  input  A,
  input  B,
  input  S,
  output ZN
);

  wire multiplexer_1_out;

  Multiplexer multiplexer_1 (.in0(A), .in1(B), .out(multiplexer_1_out), .sel(S));
  not not_1 (ZN, multiplexer_1_out);

  // Notes on the sheet:
  //   Helper circuit for all MUX21L components
endmodule

module MUX21LP (
  input  A,
  input  B,
  input  S,
  output ZN
);

  wire multiplexer_1_out;

  Multiplexer multiplexer_1 (.in0(A), .in1(B), .out(multiplexer_1_out), .sel(S));
  not not_1 (ZN, multiplexer_1_out);

  // Notes on the sheet:
  //   Helper circuit for all MUX21LP components
  //   WAS: This is different from MUX21L in that its not NEGATED
  //   Chnaged 04.12.2023 - Its used in CGA_ALU mostly, and there it is definitively negated
endmodule

module MUX24P (
  input  D00,
  input  D10,
  input  D01,
  input  D11,
  input  D02,
  input  D12,
  input  D03,
  input  D13,
  input  A,
  output Z0,
  output Z1,
  output Z2,
  output Z3
);

  Multiplexer multiplexer_1 (.in0(D00), .in1(D10), .out(Z0), .sel(A));
  Multiplexer multiplexer_2 (.in0(D01), .in1(D11), .out(Z1), .sel(A));
  Multiplexer multiplexer_3 (.in0(D02), .in1(D12), .out(Z2), .sel(A));
  Multiplexer multiplexer_4 (.in0(D03), .in1(D13), .out(Z3), .sel(A));

  // Notes on the sheet:
  //   MUX24P
  //   Used in page 63, CGA_WRF_RBLOCK_LR16
  //   Undefined what happens with Z (out) when A = 1 and B = 1. Guessing 0
endmodule

module MUX31LP (
  input  D0,
  input  D1,
  input  D2,
  input  A,
  input  B,
  output ZN
);

  wire multiplexer_1_out;

  Multiplexer #(.select(2)) multiplexer_1 (
    .in0(D0), .in1(D1), .in2(D2), .in3(D2), .out(multiplexer_1_out), .sel({B, A}));
  not not_1 (ZN, multiplexer_1_out);

  // Notes on the sheet:
  //   Helper circuit for all MUX31LP components
  //   TODO: What about address 11 ? is 0 correct ?
  //   Was GND, now connected to D2..
endmodule

module MUX34P (
  input  D00,
  input  D10,
  input  D20,
  input  D01,
  input  D11,
  input  D21,
  input  D02,
  input  D12,
  input  D22,
  input  D03,
  input  D13,
  input  D23,
  input  A,
  input  B,
  output Z0,
  output Z1,
  output Z2,
  output Z3
);

  Multiplexer #(.select(2)) multiplexer_1 (.in0(D00), .in1(D10), .in2(D20), .in3(1'b0), .out(Z0), .sel({B, A}));
  Multiplexer #(.select(2)) multiplexer_2 (.in0(D01), .in1(D11), .in2(D21), .in3(1'b0), .out(Z1), .sel({B, A}));
  Multiplexer #(.select(2)) multiplexer_3 (.in0(D02), .in1(D12), .in2(D22), .in3(1'b0), .out(Z2), .sel({B, A}));
  Multiplexer #(.select(2)) multiplexer_4 (.in0(D03), .in1(D13), .in2(D23), .in3(1'b0), .out(Z3), .sel({B, A}));

  // Notes on the sheet:
  //   MUX34P
  //   Used in page 11, CGA_MIC
  //   TODO: Undefined what happens with Z (out) when A = 1 and B = 1. Guessing 0
endmodule

module MUX41P (
  input  D0,
  input  D1,
  input  D2,
  input  D3,
  input  A,
  input  B,
  output Z
);

  Multiplexer #(.select(2)) multiplexer_1 (.in0(D0), .in1(D1), .in2(D2), .in3(D3), .out(Z), .sel({B, A}));

  // Notes on the sheet:
  //   MUX41P - Used in many places
endmodule

module MUX81 (
  input  D0,
  input  D1,
  input  D2,
  input  D3,
  input  D4,
  input  D5,
  input  D6,
  input  D7,
  input  A,
  input  B,
  input  C,
  output Z
);

  Multiplexer #(.select(3)) multiplexer_1 (
    .in0(D0), .in1(D1), .in2(D2), .in3(D3), .in4(D4), .in5(D5), .in6(D6), .in7(D7), .out(Z), .sel({C, B, A}));

  // Notes on the sheet:
  //   MUX81 - Used in TESTMUX
endmodule

module R41P (
  input  A,
  input  B,
  input  C,
  input  D,
  input  CP,
  output QA,
  output QAN,
  output QB,
  output QBN,
  output QC,
  output QCN,
  output QD,
  output QDN
);

  D_Flip_Flop d_ff_1 (.D(A), .clk(CP), .Q(QA), .Qn(QAN));  // open: preset, reset
  D_Flip_Flop d_ff_2 (.D(B), .clk(CP), .Q(QB), .Qn(QBN));  // open: preset, reset
  D_Flip_Flop d_ff_3 (.D(C), .clk(CP), .Q(QC), .Qn(QCN));  // open: preset, reset
  D_Flip_Flop d_ff_4 (.D(D), .clk(CP), .Q(QD), .Qn(QDN));  // open: preset, reset

  // Notes on the sheet:
  //   4 bit register. Latched on positive clock pulse
endmodule

module R81 (
  input  A,
  input  B,
  input  C,
  input  D,
  input  E,
  input  F,
  input  G,
  input  H,
  input  CP,
  output QA,
  output QAN,
  output QB,
  output QBN,
  output QC,
  output QCN,
  output QD,
  output QDN,
  output QE,
  output QEN,
  output QF,
  output QFN,
  output QG,
  output QGN,
  output QH,
  output QHN
);

  D_Flip_Flop d_ff_1 (.D(A), .clk(CP), .Q(QA), .Qn(QAN));  // open: preset, reset
  D_Flip_Flop d_ff_2 (.D(B), .clk(CP), .Q(QB), .Qn(QBN));  // open: preset, reset
  D_Flip_Flop d_ff_3 (.D(C), .clk(CP), .Q(QC), .Qn(QCN));  // open: preset, reset
  D_Flip_Flop d_ff_4 (.D(D), .clk(CP), .Q(QD), .Qn(QDN));  // open: preset, reset
  D_Flip_Flop d_ff_5 (.D(E), .clk(CP), .Q(QE), .Qn(QEN));  // open: preset, reset
  D_Flip_Flop d_ff_6 (.D(F), .clk(CP), .Q(QF), .Qn(QFN));  // open: preset, reset
  D_Flip_Flop d_ff_7 (.D(G), .clk(CP), .Q(QG), .Qn(QGN));  // open: preset, reset
  D_Flip_Flop d_ff_8 (.D(H), .clk(CP), .Q(QH), .Qn(QHN));  // open: preset, reset

  // Notes on the sheet:
  //   8-bt register. Latched on RISING EDGE (Clock going LOW->HIGH)
endmodule

module R81P (
  input  A,
  input  B,
  input  C,
  input  D,
  input  E,
  input  F,
  input  G,
  input  H,
  input  CP,
  output QA,
  output QAN,
  output QB,
  output QBN,
  output QC,
  output QCN,
  output QD,
  output QDN,
  output QE,
  output QEN,
  output QF,
  output QFN,
  output QG,
  output QGN,
  output QH,
  output QHN
);

  D_Flip_Flop d_ff_1 (.D(A), .clk(CP), .Q(QA), .Qn(QAN));  // open: preset, reset
  D_Flip_Flop d_ff_2 (.D(B), .clk(CP), .Q(QB), .Qn(QBN));  // open: preset, reset
  D_Flip_Flop d_ff_3 (.D(C), .clk(CP), .Q(QC), .Qn(QCN));  // open: preset, reset
  D_Flip_Flop d_ff_4 (.D(D), .clk(CP), .Q(QD), .Qn(QDN));  // open: preset, reset
  D_Flip_Flop d_ff_5 (.D(E), .clk(CP), .Q(QE), .Qn(QEN));  // open: preset, reset
  D_Flip_Flop d_ff_6 (.D(F), .clk(CP), .Q(QF), .Qn(QFN));  // open: preset, reset
  D_Flip_Flop d_ff_7 (.D(G), .clk(CP), .Q(QG), .Qn(QGN));  // open: preset, reset
  D_Flip_Flop d_ff_8 (.D(H), .clk(CP), .Q(QH), .Qn(QHN));  // open: preset, reset

  // Notes on the sheet:
  //   8 bit flip flop with Q and QN outputs
  //   Used by CGA_DCD page 65
  //   Latched on RISING EDGE (Clock going LOW->HIGH)
endmodule

module M169C (
  input  A,
  input  B,
  input  C,
  input  D,
  input  NL,
  input  CP,
  input  PN,
  input  TN,
  input  UP,
  output QA,
  output QB,
  output QC,
  output QD,
  output CON
);

  wire and_1_out, and_2_out, and_3_out, and_4_out, and_5_out, and_6_out, and_7_out, and_8_out, and_9_out,
       and_10_out, and_11_out, and_12_out, and_13_out, and_14_out, and_15_out, and_16_out, and_17_out,
       and_18_out, and_19_out, and_20_out, and_21_out, and_22_out, d_ff_1_q, d_ff_1_qn, d_ff_2_q, d_ff_2_qn,
       d_ff_3_q, d_ff_3_qn, d_ff_4_q, d_ff_4_qn, nor_1_out, nor_2_out, nor_3_out, nor_4_out, nor_5_out,
       nor_6_out, nor_7_out, nor_8_out, not_1_out, not_2_out, not_3_out, not_4_out, not_5_out, not_6_out,
       not_7_out, not_8_out, not_9_out, not_10_out, not_11_out, not_12_out, xor_1_out, xor_2_out, xor_3_out,
       xor_4_out;

  not not_1 (not_1_out, UP);
  not not_2 (not_2_out, TN);
  and and_1 (and_1_out, ~PN, ~TN, ~not_3_out);  // AND_Gate
  not not_3 (not_3_out, NL);
  not not_4 (not_4_out, CP);
  and and_2 (and_2_out, d_ff_1_q, NL);
  and and_3 (and_3_out, d_ff_2_q, NL);
  and and_4 (and_4_out, and_1_out, nor_1_out);
  and and_5 (and_5_out, d_ff_3_q, NL);
  and and_6 (and_6_out, and_1_out, nor_1_out, nor_2_out);
  and and_7 (and_7_out, d_ff_4_q, NL);
  and and_8 (and_8_out, and_1_out, nor_1_out, nor_2_out, nor_3_out);
  xor xor_1 (xor_1_out, and_2_out, and_1_out);
  and and_9 (and_9_out, not_3_out, A);
  nor nor_1 (nor_1_out, and_13_out, and_14_out);
  xor xor_2 (xor_2_out, and_3_out, and_4_out);
  and and_10 (and_10_out, not_3_out, B);
  nor nor_2 (nor_2_out, and_15_out, and_16_out);
  xor xor_3 (xor_3_out, and_5_out, and_6_out);
  and and_11 (and_11_out, not_3_out, C);
  nor nor_3 (nor_3_out, and_17_out, and_18_out);
  xor xor_4 (xor_4_out, and_7_out, and_8_out);
  and and_12 (and_12_out, not_3_out, D);
  nor nor_4 (nor_4_out, and_19_out, and_20_out);
  and and_13 (and_13_out, UP, d_ff_1_qn);
  and and_14 (and_14_out, not_1_out, d_ff_1_q);
  and and_15 (and_15_out, UP, d_ff_2_qn);
  and and_16 (and_16_out, not_1_out, d_ff_2_q);
  and and_17 (and_17_out, UP, d_ff_3_qn);
  and and_18 (and_18_out, not_1_out, d_ff_3_q);
  and and_19 (and_19_out, UP, d_ff_4_qn);
  and and_20 (and_20_out, not_1_out, d_ff_4_q);
  nor nor_5 (nor_5_out, xor_1_out, and_9_out);
  nor nor_6 (nor_6_out, xor_2_out, and_10_out);
  nor nor_7 (nor_7_out, xor_3_out, and_11_out);
  nor nor_8 (nor_8_out, xor_4_out, and_12_out);
  and and_21 (and_21_out, nor_4_out, nor_3_out, nor_2_out, not_2_out, UP);
  and and_22 (and_22_out, not_1_out, not_2_out, nor_1_out, nor_2_out, nor_3_out, nor_4_out);
  D_Flip_Flop d_ff_1 (.D(not_5_out), .clk(not_6_out), .Q(d_ff_1_q), .Qn(d_ff_1_qn));  // open: preset, reset
  not not_5 (not_5_out, nor_5_out);
  not not_6 (not_6_out, not_4_out);
  D_Flip_Flop d_ff_2 (.D(not_7_out), .clk(not_8_out), .Q(d_ff_2_q), .Qn(d_ff_2_qn));  // open: preset, reset
  not not_7 (not_7_out, nor_6_out);
  not not_8 (not_8_out, not_4_out);
  D_Flip_Flop d_ff_3 (.D(not_9_out), .clk(not_10_out), .Q(d_ff_3_q), .Qn(d_ff_3_qn));  // open: preset, reset
  not not_9 (not_9_out, nor_7_out);
  not not_10 (not_10_out, not_4_out);
  D_Flip_Flop d_ff_4 (.D(not_11_out), .clk(not_12_out), .Q(d_ff_4_q), .Qn(d_ff_4_qn));  // open: preset, reset
  not not_11 (not_11_out, nor_8_out);
  not not_12 (not_12_out, not_4_out);
  nor nor_9 (CON, and_21_out, and_22_out);
  not not_13 (QA, d_ff_1_qn);
  not not_14 (QB, d_ff_2_qn);
  not not_15 (QC, d_ff_3_qn);
  not not_16 (QD, d_ff_4_qn);

  // Other names for the same wires on the sheet: CLK = CP; ENP_N = PN; ENT_N = TN; LOAD_N = NL; RCO_N = CON;
  //   U_DN = UP

  // Notes on the sheet:
  //   Circuit used in CGA_MIC page 12
  //   https://www.ti.com/lit/ds/symlink/sn74als169b.pdf
  //   M169C - 74LS169 - Synchronous 4-biy up/down binary counters
  //   CP Rising
  //   Count Enable P
  //   Count Enable N
  //   Count: UP  /DOWN
  //   Ripple Carry Out
endmodule

module CMP4 (
  input  A0,
  input  A1,
  input  A2,
  input  A3,
  input  B0,
  input  B1,
  input  B2,
  input  B3,
  output AGB,
  output AEB,
  output ALB
);

  Comparator #(.width(4)) comparator_1 (.a({A3, A2, A1, A0}), .b({B3, B2, B1, B0}), .gt(AGB), .eq(AEB), .lt(ALB));

  // Notes on the sheet:
  //   Wrapping the Logisim Comparator in a 4 bit ND Comparator
endmodule

module test_169 (
  input  [3:0] in_1,
  input  NL,
  input  CP,
  input  PN,
  input  TN,
  input  UP,
  output [3:0] CNT,
  output CON
);

  M169C ls169 (
    .A(in_1[0]), .B(in_1[1]), .C(in_1[2]), .D(in_1[3]), .NL(NL), .CP(CP), .PN(PN), .TN(TN), .UP(UP),
    .QA(CNT[0]), .QB(CNT[1]), .QC(CNT[2]), .QD(CNT[3]), .CON(CON));
endmodule

module BD4TU (
  input  EN,
  input  TN,
  input  A,
  input  BUF_IN,
  output BUF_OUT,
  output ZI
);

  wire controlled_buffer_1_out, not_1_out;

  not not_1 (not_1_out, EN);
  assign controlled_buffer_1_out = not_1_out ? A : 1'bz;  // Controlled_Buffer controlled_buffer_1
  assign BUF_OUT = not_1_out ? controlled_buffer_1_out : 1'bz;  // Controlled_Buffer controlled_buffer_2
  assign ZI = EN ? BUF_IN : 1'bz;  // Controlled_Buffer controlled_buffer_3

  // Notes on the sheet:
  //   Databuffer with 3-state
  //   Used in CGA (Sheet 5/10) page 6 
  //   Don't know what TN is, guessing its for testing. Seems like its not in use in the 3202 CPU board
endmodule

module test_BD (
  input  in_1,
  input  in_2,
  input  in_3,
  input  [15:0] in_4,
  input  [15:0] in_5,
  input  in_6,
  output [15:0] out_7
);

  wire bd4tu_1_zi, undriven;

  // Probe on bd4tu_1_zi
  BD4TU bd4tu_1 (.EN(in_1), .TN(undriven), .A(in_2), .BUF_IN(in_3), .ZI(bd4tu_1_zi), .BUF_OUT(in_3));
  // Probe on in_3
  BusDriver16xx busdriver16xx_1 (
    .A_15_0(in_4), .IN_15_0(in_5), .EN(in_6), .ZI_15_0(out_7), .OUT_15_0(in_5));  // open: TN
  // Probe on in_5
endmodule

module BusDriver16xx (
  input  [15:0] A_15_0,
  input  [15:0] IN_15_0,
  input  EN,
  input  TN,
  output [15:0] ZI_15_0,
  output [15:0] OUT_15_0
);

  BD4TU BD_0 (.EN(EN), .TN(TN), .A(A_15_0[0]), .BUF_IN(IN_15_0[0]), .ZI(ZI_15_0[0]), .BUF_OUT(OUT_15_0[0]));
  BD4TU BD_1 (.EN(EN), .TN(TN), .A(A_15_0[1]), .BUF_IN(IN_15_0[1]), .ZI(ZI_15_0[1]), .BUF_OUT(OUT_15_0[1]));
  BD4TU BD_2 (.EN(EN), .TN(TN), .A(A_15_0[2]), .BUF_IN(IN_15_0[2]), .ZI(ZI_15_0[2]), .BUF_OUT(OUT_15_0[2]));
  BD4TU BD_3 (.EN(EN), .TN(TN), .A(A_15_0[3]), .BUF_IN(IN_15_0[3]), .ZI(ZI_15_0[3]), .BUF_OUT(OUT_15_0[3]));
  BD4TU BD_4 (.EN(EN), .TN(TN), .A(A_15_0[4]), .BUF_IN(IN_15_0[4]), .ZI(ZI_15_0[4]), .BUF_OUT(OUT_15_0[4]));
  BD4TU BD_5 (.EN(EN), .TN(TN), .A(A_15_0[5]), .BUF_IN(IN_15_0[5]), .ZI(ZI_15_0[5]), .BUF_OUT(OUT_15_0[5]));
  BD4TU BD_6 (.EN(EN), .TN(TN), .A(A_15_0[6]), .BUF_IN(IN_15_0[6]), .ZI(ZI_15_0[6]), .BUF_OUT(OUT_15_0[6]));
  BD4TU BD_7 (.EN(EN), .TN(TN), .A(A_15_0[7]), .BUF_IN(IN_15_0[7]), .ZI(ZI_15_0[7]), .BUF_OUT(OUT_15_0[7]));
  BD4TU BD_8 (.EN(EN), .TN(TN), .A(A_15_0[8]), .BUF_IN(IN_15_0[8]), .ZI(ZI_15_0[8]), .BUF_OUT(OUT_15_0[8]));
  BD4TU BD_9 (.EN(EN), .TN(TN), .A(A_15_0[9]), .BUF_IN(IN_15_0[9]), .ZI(ZI_15_0[9]), .BUF_OUT(OUT_15_0[9]));
  BD4TU BD_10 (.EN(EN), .TN(TN), .A(A_15_0[10]), .BUF_IN(IN_15_0[10]), .ZI(ZI_15_0[10]), .BUF_OUT(OUT_15_0[10]));
  BD4TU BD_11 (.EN(EN), .TN(TN), .A(A_15_0[11]), .BUF_IN(IN_15_0[11]), .ZI(ZI_15_0[11]), .BUF_OUT(OUT_15_0[11]));
  BD4TU BD_12 (.EN(EN), .TN(TN), .A(A_15_0[12]), .BUF_IN(IN_15_0[12]), .ZI(ZI_15_0[12]), .BUF_OUT(OUT_15_0[12]));
  BD4TU BD_13 (.EN(EN), .TN(TN), .A(A_15_0[13]), .BUF_IN(IN_15_0[13]), .ZI(ZI_15_0[13]), .BUF_OUT(OUT_15_0[13]));
  BD4TU BD_14 (.EN(EN), .TN(TN), .A(A_15_0[14]), .BUF_IN(IN_15_0[14]), .ZI(ZI_15_0[14]), .BUF_OUT(OUT_15_0[14]));
  BD4TU BD_15 (.EN(EN), .TN(TN), .A(A_15_0[15]), .BUF_IN(IN_15_0[15]), .ZI(ZI_15_0[15]), .BUF_OUT(OUT_15_0[15]));

  // Notes on the sheet:
  //   16 bit three-state bus driver
  //   Special made for CGA page 6 (Sheet 5 of 8)
endmodule
