// Logisim project TESTMUX_.circ as structural Verilog: 1 circuit, main circuit CGA_TESTMUX
module CGA_TESTMUX (
  input  [3:0] TVEC_3_0,
  input  [3:0] SC_6_3,
  input  PTREEOUT,
  input  VACCN,
  input  MI,
  input  OVF,
  input  UPN,
  input  LCZN,
  input  CSMREQ,
  input  INDN,
  input  PTM,
  input  ZF,
  input  COND,
  input  DZD,
  input  LDIRV,
  input  CBRKN,
  input  WPN,
  input  F15,
  input  PN,
  input  OOD,
  input  VEX,
  input  WRITEN,
  input  XFETCHN,
  input  SGR,
  input  TN,
  input  CFETCH,
  input  DSTOPN,
  input  CRY,
  input  RESTR,
  input  DEEP,
  input  [2:0] TSEL_2_0,
  input  PTSTN,
  output [4:0] TEST_4_0
);

  wire and_1_out, and_2_out, and_3_out, nand_1_out;

  and and_1 (and_1_out, TSEL_2_0[0], PTSTN);
  and and_2 (and_2_out, TSEL_2_0[1], PTSTN);
  and and_3 (and_3_out, TSEL_2_0[2], PTSTN);
  nand nand_1 (nand_1_out, ~PTSTN, ~PTREEOUT);  // NAND_Gate
  MUX81 TM0 (
    .D0(nand_1_out), .D1(VACCN), .D2(MI), .D3(OVF), .D4(UPN), .D5(LCZN), .D6(SC_6_3[0]), .D7(TVEC_3_0[0]),
    .A(and_1_out), .B(and_2_out), .C(and_3_out), .Z(TEST_4_0[0]));
  MUX81 TM1 (
    .D0(CSMREQ), .D1(INDN), .D2(PTM), .D3(ZF), .D4(COND), .D5(DZD), .D6(SC_6_3[1]), .D7(TVEC_3_0[1]),
    .A(and_1_out), .B(and_2_out), .C(and_3_out), .Z(TEST_4_0[1]));
  MUX81 TM2 (
    .D0(LDIRV), .D1(CBRKN), .D2(WPN), .D3(F15), .D4(PN), .D5(OOD), .D6(SC_6_3[2]), .D7(TVEC_3_0[2]),
    .A(and_1_out), .B(and_2_out), .C(and_3_out), .Z(TEST_4_0[2]));
  MUX81 TM3 (
    .D0(VEX), .D1(WRITEN), .D2(XFETCHN), .D3(SGR), .D4(TN), .D5(CFETCH), .D6(SC_6_3[3]), .D7(TVEC_3_0[3]),
    .A(and_1_out), .B(and_2_out), .C(and_3_out), .Z(TEST_4_0[3]));
  MUX81 TM4 (
    .D0(1'b1), .D1(DSTOPN), .D2(1'b1), .D3(CRY), .D4(1'b1), .D5(RESTR), .D6(DEEP), .D7(1'b0), .A(and_1_out),
    .B(and_2_out), .C(and_3_out), .Z(TEST_4_0[4]));

  // Notes on the sheet:
  //   TSEL0
  //   TSEL1
  //   TSEL2
  //   SC3
  //   TVEC0
  //   SC4
  //   TVEC1
  //   SC5
  //   TVEC2
  //   SC6
  //   TVEC3
  //   TEST0
  //   TEST1
  //   TEST2
  //   TEST3
  //   TEST4
endmodule
