// Logisim project SMD3044-MA-WC.circ as structural Verilog: 3 circuits, main circuit SMD3044_MA_WC
module SMD3044_MA_WC (
  input  LMAR0,
  input  WCS0,
  input  LCW0,
  input  RMAR0,
  input  RWC0,
  input  RSTAT0,
  input  CF0,
  input  RFT1,
  input  PIODRY1,
  input  DWC0,
  input  ADREN1,
  input  INGRANT0,
  input  BUSDRV0,
  input  [15:0] A_REG,
  output SELH0,
  output SELH1,
  output I0_1,
  output I1_1,
  output I2_1,
  output CPH1,
  output CPL1,
  output OEL0,
  output OEH0,
  output DIR11B,
  output E11B,
  output CLK4E,
  output RREG1,
  output DWCZ1,
  output WCZ0,
  output DB0,
  output DB1,
  output DB2,
  output DB3,
  output DB4,
  output DB5,
  output DB6,
  output DB7,
  output DB8,
  output DB9,
  output DB10,
  output DB11,
  output DB12,
  output DB13,
  output DB14,
  output DB15,
  output DB16,
  output DB17,
  output DB18,
  output DB19,
  output DB20,
  output DB21,
  output DB22,
  output DB23
);

  wire ACO_12A, ACO_12C, ACO_14C, D12C_0, D12C_1, D12C_2, D14C_0, D14C_1, D14C_2, H9, LCW1, LMAR1, N2C6,
       N2D6, N4B8, PRE4E, RMAR1, RREG0, RWC1, WCO_12C, WCO_14C, WCS1, WCZ1;

  Am2942 am2942_1 (
    .WCI(1'b0), .ACI(1'b0), .IE(1'b0), .OED(OEL0), .CP(CPL1), .I0(I0_1), .I1(I1_1), .I2(I2_1), .I3(1'b0),
    .WCO(WCO_14C), .ACO(ACO_14C), .D0(D14C_0), .D1(D14C_1), .D2(D14C_2), .D3(DB3), .D4(DB4), .D5(DB5),
    .D6(DB6), .D7(DB7), .Y0_out(D14C_0), .Y1_out(D14C_1), .Y2_out(D14C_2), .Y3_out(DB3), .Y4_out(DB4),
    .Y5_out(DB5), .Y6_out(DB6), .Y7_out(DB7));  // open: DONE
  _7411 u_7411_1 (
    .pin1(RREG0), .pin2(WCS0), .pin3(RFT1), .pin4(RSTAT0), .pin5(CF0), .pin6(PRE4E), .pin13(LMAR0),
    .pin12(E11B));  // open: pin11, pin10, pin9, pin8
  _7451 u_7451_1 (
    .pin1(ADREN1), .pin13(ADREN1), .pin10(SELH0), .pin9(RREG1), .pin8(OEL0));  // open: pin2, pin3, pin4, pin5, pin6, pin12, pin11
  _7411 u_7411_2 (
    .pin11(INGRANT0), .pin10(WCZ1), .pin9(WCZ1), .pin8(DWCZ1));  // open: pin1, pin2, pin3, pin4, pin5, pin6, pin13, pin12
  Pull_Resistor #(.pull(0)) pull_resistor_1 (.node(D14C_0));
  Pull_Resistor #(.pull(0)) pull_resistor_2 (.node(D14C_1));
  Am2942 am2942_2 (
    .WCI(WCO_14C), .ACI(ACO_14C), .IE(1'b0), .OED(OEL0), .CP(CPL1), .I0(I0_1), .I1(I1_1), .I2(I2_1),
    .I3(1'b0), .WCO(WCO_12C), .ACO(ACO_12C), .D0(D12C_0), .D1(D12C_1), .D2(D12C_2), .D3(DB11), .D4(DB12),
    .D5(DB13), .D6(DB14), .D7(DB15), .Y0_out(D12C_0), .Y1_out(D12C_1), .Y2_out(D12C_2), .Y3_out(DB11),
    .Y4_out(DB12), .Y5_out(DB13), .Y6_out(DB14), .Y7_out(DB15));  // open: DONE
  _7427 u_7427_1 (
    .pin1(RMAR1), .pin2(LMAR1), .pin3(WCS1), .pin4(LCW1), .pin5(RWC1), .pin6(I0_1), .pin13(N4B8),
    .pin12(CLK4E), .pin11(RWC1), .pin10(LCW1), .pin9(RMAR1), .pin8(I2_1));
  _7408 u_7408_1 (
    .pin1(SELH1), .pin2(RREG1), .pin3(DIR11B));  // open: pin4, pin5, pin6, pin13, pin12, pin11, pin10, pin9, pin8
  _7404 u_7404_1 (
    .pin1(LMAR0), .pin2(LMAR1), .pin3(WCS0), .pin4(WCS1), .pin5(LCW0), .pin6(LCW1), .pin11(RWC0),
    .pin10(RWC1), .pin9(RMAR0), .pin8(RMAR1));  // open: pin13, pin12
  Pull_Resistor #(.pull(0)) pull_resistor_3 (.node(D14C_2));
  Pull_Resistor #(.pull(0)) pull_resistor_4 (.node(D12C_0));
  Pull_Resistor #(.pull(0)) pull_resistor_5 (.node(D12C_1));
  Pull_Resistor #(.pull(0)) pull_resistor_6 (.node(D12C_2));
  Am2942 am2942_3 (
    .WCI(WCO_12C), .ACI(ACO_12C), .IE(1'b0), .OED(OEH0), .CP(CPH1), .I0(I0_1), .I1(I1_1), .I2(I2_1),
    .I3(1'b0), .WCO(WCZ0), .ACO(ACO_12A), .D0(DB16), .D1(DB17), .D2(DB18), .D3(DB19), .D4(DB20), .D5(DB21),
    .D6(DB22), .D7(DB23), .Y0_out(DB16), .Y1_out(DB17), .Y2_out(DB18), .Y3_out(DB19), .Y4_out(DB20),
    .Y5_out(DB21), .Y6_out(DB22), .Y7_out(DB23));  // open: DONE
  _7402 u_7402_1 (
    .pin4(RREG0), .pin5(RMAR1), .pin6(RWC1), .pin13(I1_1), .pin12(LMAR1), .pin11(LCW1));  // open: pin1, pin2, pin3, pin10, pin9, pin8
  _7404 u_7404_2 (
    .pin11(N2D6), .pin10(CPL1), .pin9(N2C6), .pin8(CPH1));  // open: pin1, pin2, pin3, pin4, pin5, pin6, pin13, pin12
  _74244 u_74244_1 (
    .pin1(BUSDRV0), .pin2(A_REG[0]), .pin3(DB7), .pin4(A_REG[1]), .pin5(DB6), .pin6(A_REG[2]), .pin7(DB5),
    .pin8(A_REG[3]), .pin9(DB4), .pin19(BUSDRV0), .pin18(DB0), .pin17(A_REG[7]), .pin16(DB1),
    .pin15(A_REG[6]), .pin14(DB2), .pin13(A_REG[5]), .pin12(DB3), .pin11(A_REG[4]));
  Pull_Resistor #(.pull(0)) pull_resistor_7 (.node(DB16));
  Pull_Resistor #(.pull(0)) pull_resistor_8 (.node(DB17));
  Pull_Resistor #(.pull(0)) pull_resistor_9 (.node(DB18));
  Pull_Resistor #(.pull(1)) pull_resistor_10 (.node(H9));
  _74245 u_74245_1 (
    .pin1(OEL0), .pin2(DB0), .pin3(DB1), .pin4(DB2), .pin7(DB8), .pin8(DB9), .pin9(DB10), .pin19(LCW1),
    .pin18(D14C_0), .pin17(D14C_1), .pin16(D14C_2), .pin13(D12C_0), .pin12(D12C_1), .pin11(D12C_2));  // open: pin5, pin6, pin15, pin14
  _7400 u_7400_1 (
    .pin10(WCS0), .pin9(RWC0), .pin8(N4B8));  // open: pin1, pin2, pin3, pin4, pin5, pin6, pin13, pin12, pin11
  _74LS54 u_74ls54_1 (
    .A1(DWC0), .B1(DWC0), .A2(LMAR1), .B2(SELH0), .C2(PIODRY1), .A3(PIODRY1), .B3(SELH0), .C3(WCS1),
    .A4(LCW1), .B4(PIODRY1), .Y(N2C6));
  _74244 u_74244_2 (
    .pin1(BUSDRV0), .pin2(A_REG[8]), .pin3(DB15), .pin4(A_REG[9]), .pin5(DB14), .pin6(A_REG[10]),
    .pin7(DB13), .pin8(A_REG[11]), .pin9(DB12), .pin19(BUSDRV0), .pin18(DB8), .pin17(A_REG[15]), .pin16(DB9),
    .pin15(A_REG[14]), .pin14(DB10), .pin13(A_REG[13]), .pin12(DB11), .pin11(A_REG[12]));
  _74245 u_74245_2 (
    .pin1(DIR11B), .pin2(DB16), .pin3(DB17), .pin4(DB23), .pin5(DB22), .pin6(DB18), .pin7(DB19), .pin8(DB21),
    .pin9(DB20), .pin19(E11B), .pin18(DB0), .pin17(DB1), .pin16(DB7), .pin15(DB6), .pin14(DB2), .pin13(DB3),
    .pin12(DB5), .pin11(DB4));
  _7404 u_7404_3 (.pin11(RREG0), .pin10(RREG1));  // open: pin1, pin2, pin3, pin4, pin5, pin6, pin13, pin12, pin9, pin8
  _74LS54 u_74ls54_2 (
    .A1(DWC0), .B1(DWC0), .A2(LMAR1), .B2(PIODRY1), .C2(PIODRY1), .A3(PIODRY1), .B3(PIODRY1), .C3(WCS1),
    .A4(LCW1), .B4(PIODRY1), .Y(N2D6));
  _7474 u_7474_1 (
    .pin13(H9), .pin12(SELH1), .pin11(CLK4E), .pin10(PRE4E), .pin9(SELH0), .pin8(SELH1));  // open: pin1, pin2, pin3, pin4, pin5, pin6
  _7402 u_7402_2 (
    .pin10(OEH0), .pin9(RREG1), .pin8(ADREN1));  // open: pin1, pin2, pin3, pin4, pin5, pin6, pin13, pin12, pin11
  _7404 u_7404_4 (.pin3(WCZ0), .pin4(WCZ1));  // open: pin1, pin2, pin5, pin6, pin13, pin12, pin11, pin10, pin9, pin8

  // Other names for the same wires on the sheet: A0 = A_REG[0]; AREG[15:0] = A_REG; A1 = A_REG[1]; A2 = A_REG[2];
  //   A3 = A_REG[3]; A4 = A_REG[4]; A5 = A_REG[5]; A6 = A_REG[6]; A7 = A_REG[7]; A8 = A_REG[8]; A9 = A_REG[9];
  //   A10 = A_REG[10]; A11 = A_REG[11]; A12 = A_REG[12]; A13 = A_REG[13]; A14 = A_REG[14]; A15 = A_REG[15]

  // Notes on the sheet:
  //   3E
  //   AND - chosen by function
  //   3C  74S51
  //   1G
  //   AND - same symbol as 3E
  //   14C  bits 0-7
  //   12C  bits 8-15
  //   3D  LS27
  //   4C
  //   AND - same symbol as 3E
  //   7404#4
  //   Strobes are the active-low LS138 outputs of sheet 1. One IOX write: set A_REG, BUSDRV0=0, PIODRY1=1, strobe low, strobe high.
  //   RN9 13C on 14C/12C D0-D2; RN9 pin 8, R40, R39 on DB16-18; H9 (R15) pull-up on 4E /R
  //   12A  bits 16-23
  //   4D  LS02
  //   1C  LS04
  //   inverter - same symbol as 3A
  //   STAND-IN
  //   A register bits 0-7 onto DB (sheet 1 transceivers)
  //   4B  74S00
  //   NAND - chosen by function
  //   2C  LS54
  //   high slice clock
  //   11C  LS245
  //   off during a control-word load (LCW1 on /E)
  //   STAND-IN
  //   A register bits 8-15 onto DB (sheet 1 transceivers)
  //   3A  LS04
  //   2D  LS54
  //   low slice clock
  //   11B  LS245
  //   byte swapper: A = DB16-23, B = DB0-7
  //   4E  LS74
  //   D <- /Q: toggles on each CLK4E rising edge
  //   2B  74S02
  //   14F  74S04
  //   inverter - from the WCZ0/WCZ1 names
  //   ND-632 15 MHz SMD controller, card 3044, logic diagram sheet 3, block 'MEMORY ADDRESS & WORD COUNT'
  //   (ND-11.020.01, scan page 118). Chip position codes, DIP pin numbers and signal names are the drawing's.
  //   Gate types the manual does not state (it has no parts list), chosen by what the circuit must do - check them:
  //     3E, 1G, 4C = AND; 4B = NAND; 1C, 14F = inverter. 3E and 1C/3A are drawn with the SAME symbol, yet 3E must
  //     be an AND (a NAND would hold 4E preset) and 3A must invert (RREG1 must be the opposite of RREG0).
  //     R40, R39 and RN9 pin 8 on DB16-18: the far end is not drawn; shown as pull-downs like the rest of RN9.
  //     C13 (220 pF on the 4E preset) is not drawn. 14C /ACI and /WCI (pins 3, 1) use the same rail symbol as
  //     /IE (pin 8), which must be ground for any instruction to run - so they are ground.
  //   Am2942: subcircuit built from the AMD data sheet (03574B) function table; D0-D7 inputs on the DIP pins,
  //   the three-state outputs Y0-Y7 beside the body are tied to the same nets (Logisim cannot make a two-way port).
  //   Not on this sheet, drawn as stand-ins: the NOT gates making X1 from the LS138 X0 strobes (sheet 1, 3A),
  //   and two 74244s putting the ND-100 A register on DB0-15 (the sheet 1 bus transceivers).
  //   SCOPE: the controller's own microcode ROM (which runs disc transfers) is not available, so the controller
  //   as a whole cannot be simulated. This block's register loads come straight from the CPU's IOX strobes and
  //   do not pass through that ROM; transfer-time signals from it (DWC0, ADREN1, INGRANT0, RFT1) are inputs here.
  //   OPEN: DWC0 must rest LOW between transfers for any IOX load to clock the 2942s - 2C/2D pins 1 and 2 are both
  //   DWC0, so DWC0 HIGH holds the LS54 output LOW. The 0 subscript would say active-low; DWC0 is made off this
  //   sheet and has not been traced.
endmodule

module Am2942 (
  input  WCI,
  input  ACI,
  input  IE,
  input  OED,
  input  CP,
  input  I0,
  input  I1,
  input  I2,
  input  I3,
  input  D0,
  input  D1,
  input  D2,
  input  D3,
  input  D4,
  input  D5,
  input  D6,
  input  D7,
  output WCO,
  output ACO,
  output DONE,
  output Y0_out,
  output Y1_out,
  output Y2_out,
  output Y3_out,
  output Y4_out,
  output Y5_out,
  output Y6_out,
  output Y7_out
);

  wire AC0, AC1, AC2, AC3, AC4, AC5, AC6, AC7, AC_____1_c4, AC_AR, AC_CNTE, AC_CNTI, AC_COUT, AC_TERM, ACM0,
       ACM1, ACM2, ACM3, ACM4, ACM5, ACM6, ACM7, ACN0, ACN1, ACN2, ACN3, ACN4, ACN5, ACN6, ACN7, ACX0, ACX1,
       ACX2, ACX3, ACX4, ACX5, ACX6, ACX7, address_counter_ld, address_counter_n0, address_counter_n1,
       address_counter_n2, address_counter_n3, address_counter_n4, address_counter_n5, address_counter_n6,
       address_counter_n7, address_register_ld, address_register_n0, address_register_n1,
       address_register_n2, address_register_n3, address_register_n4, address_register_n5,
       address_register_n6, address_register_n7, AR0, AR1, AR2, AR3, AR4, AR5, AR6, AR7, AR_LD, CMPB0, CMPB1,
       CMPB2, CMPB3, CMPB4, CMPB5, CMPB6, CMPB7, control_register__D0_D2__ld, control_register__D0_D2__n0,
       control_register__D0_D2__n1, control_register__D0_D2__n2, control_register__D0_D2__n3,
       control_register__D0_D2__n4, control_register__D0_D2__n5, control_register__D0_D2__n6,
       control_register__D0_D2__n7, control_register__D0_D2__q3, control_register__D0_D2__q4,
       control_register__D0_D2__q5, control_register__D0_D2__q6, control_register__D0_D2__q7, CR0, CR1, CR2,
       CR_LD, DONE__WC___k_c4, DONE_T, EQ, EQ_L, GND, GT_L, KANY, KNEG, KPOS, LT_L, M0, M1, M2_SEL, nACI,
       nC0, nC1, nC2, nC3, nC4, nC5, nC6, nC7, nC8, nC9, nCA, nCB, nCC, nCD, nCE, nCF, nDIS_DMA, nDIS_TC,
       nEN_AC, nEN_AR, nEN_CR, nEN_WC, nEN_WR, nI3, nM0, nM1, nM2, nM3, nWCI, VCC, WC0, WC1, WC2, WC3, WC4,
       WC5, WC6, WC7, WC_____1_c4, WC_CNTE, WC_CNTI, WC_COUT, WC_EN_X, WC_FROM_WR, WC_LD_D, WC_REIN, WC_TERM,
       WC_TERM0, WC_Z_ANY, WC_ZERO, WCK0, WCK1, WCK2, WCK3, WCK4, WCK5, WCK6, WCK7, WCM0, WCM1, WCM2, WCM3,
       WCM4, WCM5, WCM6, WCM7, WCN0, WCN1, WCN2, WCN3, WCN4, WCN5, WCN6, WCN7, WCX0, WCX1, WCX2, WCX3, WCX4,
       WCX5, WCX6, WCX7, word_count_register_ld, word_count_register_n0, word_count_register_n1,
       word_count_register_n2, word_count_register_n3, word_count_register_n4, word_count_register_n5,
       word_count_register_n6, word_count_register_n7, word_counter_ld, word_counter_n0, word_counter_n1,
       word_counter_n2, word_counter_n3, word_counter_n4, word_counter_n5, word_counter_n6, word_counter_n7,
       WR0, WR1, WR2, WR3, WR4, WR5, WR6, WR7, WR_LD, Y0, Y1, Y2, Y3, Y4, Y5, Y6, Y7, Y_CR, Y_HIGH, Y_WC,
       YA0, YA1, YA2, YA3, YA4, YA5, YA6, YA7, YB0, YB1, YB2, YB3, YB4, YB5, YB6, YB7;

  _74138 u_74138_1 (
    .pin1(I0), .pin2(I1), .pin3(I2), .pin4(IE), .pin5(I3), .pin6(VCC), .pin7(nC7), .pin15(nC0), .pin14(nC1),
    .pin13(nC2), .pin12(nC3), .pin11(nC4), .pin10(nC5), .pin9(nC6));
  _7430 u_7430_1 (
    .pin1(nC7), .pin2(nC8), .pin3(nC9), .pin4(nCA), .pin5(nCB), .pin6(nCD), .pin12(nDIS_TC),
    .pin11(nDIS_DMA), .pin8(WC_CNTI));  // open: pin13, pin10, pin9
  _74157 u_74157_1 (
    .pin1(address_register_ld), .pin2(AR4), .pin3(D4), .pin4(address_register_n4), .pin5(AR5), .pin6(D5),
    .pin7(address_register_n5), .pin15(GND), .pin14(AR7), .pin13(D7), .pin12(address_register_n7),
    .pin11(AR6), .pin10(D6), .pin9(address_register_n6));
  _74157 u_74157_2 (
    .pin1(control_register__D0_D2__ld), .pin2(control_register__D0_D2__q4), .pin3(GND),
    .pin4(control_register__D0_D2__n4), .pin5(control_register__D0_D2__q5), .pin6(GND),
    .pin7(control_register__D0_D2__n5), .pin15(GND), .pin14(control_register__D0_D2__q7), .pin13(GND),
    .pin12(control_register__D0_D2__n7), .pin11(control_register__D0_D2__q6), .pin10(GND),
    .pin9(control_register__D0_D2__n6));
  _74157 u_74157_3 (
    .pin1(AR_LD), .pin2(ACM4), .pin3(D4), .pin4(ACX4), .pin5(ACM5), .pin6(D5), .pin7(ACX5), .pin15(GND),
    .pin14(ACM7), .pin13(D7), .pin12(ACX7), .pin11(ACM6), .pin10(D6), .pin9(ACX6));
  _74157 u_74157_4 (
    .pin1(WC_FROM_WR), .pin2(WCN0), .pin3(WR0), .pin4(WCM0), .pin5(WCN1), .pin6(WR1), .pin7(WCM1),
    .pin15(GND), .pin14(WCN3), .pin13(WR3), .pin12(WCM3), .pin11(WCN2), .pin10(WR2), .pin9(WCM2));
  _74175 u_74175_1 (
    .pin1(VCC), .pin2(WC4), .pin4(word_counter_n4), .pin5(word_counter_n5), .pin7(WC5), .pin15(WC7),
    .pin13(word_counter_n7), .pin12(word_counter_n6), .pin10(WC6), .pin9(CP));  // open: pin3, pin6, pin14, pin11
  _74244 u_74244_1 (
    .pin1(OED), .pin2(Y0), .pin3(Y7_out), .pin4(Y1), .pin5(Y6_out), .pin6(Y2), .pin7(Y5_out), .pin8(Y3),
    .pin9(Y4_out), .pin19(OED), .pin18(Y0_out), .pin17(Y7), .pin16(Y1_out), .pin15(Y6), .pin14(Y2_out),
    .pin13(Y5), .pin12(Y3_out), .pin11(Y4));
  _74138 u_74138_2 (
    .pin1(I0), .pin2(I1), .pin3(I2), .pin4(IE), .pin5(GND), .pin6(I3), .pin7(nCF), .pin15(nC8), .pin14(nC9),
    .pin13(nCA), .pin12(nCB), .pin11(nCC), .pin10(nCD), .pin9(nCE));
  _7430 u_7430_2 (
    .pin1(nC2), .pin2(nC5), .pin3(nCA), .pin4(nCD), .pin5(nCF), .pin6(nDIS_TC), .pin12(VCC), .pin11(VCC),
    .pin8(Y_WC));  // open: pin13, pin10, pin9
  _74175 u_74175_2 (
    .pin1(VCC), .pin2(AR0), .pin4(address_register_n0), .pin5(address_register_n1), .pin7(AR1), .pin15(AR3),
    .pin13(address_register_n3), .pin12(address_register_n2), .pin10(AR2), .pin9(CP));  // open: pin3, pin6, pin14, pin11
  _74175 u_74175_3 (
    .pin1(VCC), .pin2(CR0), .pin4(control_register__D0_D2__n0), .pin5(control_register__D0_D2__n1),
    .pin7(CR1), .pin15(control_register__D0_D2__q3), .pin13(control_register__D0_D2__n3),
    .pin12(control_register__D0_D2__n2), .pin10(CR2), .pin9(CP));  // open: pin3, pin6, pin14, pin11
  _74157 u_74157_5 (
    .pin1(address_counter_ld), .pin2(AC0), .pin3(ACX0), .pin4(address_counter_n0), .pin5(AC1), .pin6(ACX1),
    .pin7(address_counter_n1), .pin15(GND), .pin14(AC3), .pin13(ACX3), .pin12(address_counter_n3),
    .pin11(AC2), .pin10(ACX2), .pin9(address_counter_n2));
  _74157 u_74157_6 (
    .pin1(WC_FROM_WR), .pin2(WCN4), .pin3(WR4), .pin4(WCM4), .pin5(WCN5), .pin6(WR5), .pin7(WCM5),
    .pin15(GND), .pin14(WCN7), .pin13(WR7), .pin12(WCM7), .pin11(WCN6), .pin10(WR6), .pin9(WCM6));
  _7408 u_7408_1 (
    .pin1(WC_TERM0), .pin2(nM2), .pin3(WC_TERM), .pin4(M0), .pin5(nWCI), .pin6(KNEG), .pin13(nM3),
    .pin12(EQ), .pin11(DONE_T), .pin10(nWCI), .pin9(M1), .pin8(KPOS));
  _74283 u_74283_1 (
    .pin1(WCK1), .pin2(KNEG), .pin3(WC1), .pin4(WCK0), .pin5(WC0), .pin6(KANY), .pin7(GND), .pin15(KNEG),
    .pin14(WC2), .pin13(WCK2), .pin12(WC3), .pin11(KNEG), .pin10(WCK3), .pin9(DONE__WC___k_c4));
  _74138 u_74138_3 (
    .pin1(CR0), .pin2(CR1), .pin3(GND), .pin4(GND), .pin5(GND), .pin6(VCC), .pin15(nM0), .pin14(nM1),
    .pin13(nM2), .pin12(nM3));  // open: pin7, pin11, pin10, pin9
  _7408 u_7408_2 (
    .pin1(WR_LD), .pin2(nM1), .pin3(WC_LD_D), .pin4(WC_Z_ANY), .pin5(M1), .pin6(WC_ZERO), .pin13(nACI),
    .pin12(AC_CNTI), .pin11(AC_CNTE), .pin10(nM1), .pin9(WC_REIN), .pin8(WC_FROM_WR));
  _74175 u_74175_4 (
    .pin1(VCC), .pin2(AR4), .pin4(address_register_n4), .pin5(address_register_n5), .pin7(AR5), .pin15(AR7),
    .pin13(address_register_n7), .pin12(address_register_n6), .pin10(AR6), .pin9(CP));  // open: pin3, pin6, pin14, pin11
  _74175 u_74175_5 (
    .pin1(VCC), .pin2(control_register__D0_D2__q4), .pin4(control_register__D0_D2__n4),
    .pin5(control_register__D0_D2__n5), .pin7(control_register__D0_D2__q5),
    .pin15(control_register__D0_D2__q7), .pin13(control_register__D0_D2__n7),
    .pin12(control_register__D0_D2__n6), .pin10(control_register__D0_D2__q6), .pin9(CP));  // open: pin3, pin6, pin14, pin11
  _74157 u_74157_7 (
    .pin1(address_counter_ld), .pin2(AC4), .pin3(ACX4), .pin4(address_counter_n4), .pin5(AC5), .pin6(ACX5),
    .pin7(address_counter_n5), .pin15(GND), .pin14(AC7), .pin13(ACX7), .pin12(address_counter_n7),
    .pin11(AC6), .pin10(ACX6), .pin9(address_counter_n6));
  _74157 u_74157_8 (
    .pin1(WC_LD_D), .pin2(WCM0), .pin3(D0), .pin4(WCX0), .pin5(WCM1), .pin6(D1), .pin7(WCX1),
    .pin15(WC_ZERO), .pin14(WCM3), .pin13(D3), .pin12(WCX3), .pin11(WCM2), .pin10(D2), .pin9(WCX2));
  _74157 u_74157_9 (
    .pin1(Y_WC), .pin2(AC0), .pin3(WC0), .pin4(YA0), .pin5(AC1), .pin6(WC1), .pin7(YA1), .pin15(GND),
    .pin14(AC3), .pin13(WC3), .pin12(YA3), .pin11(AC2), .pin10(WC2), .pin9(YA2));
  _74283 u_74283_2 (
    .pin1(WCK5), .pin2(KNEG), .pin3(WC5), .pin4(WCK4), .pin5(WC4), .pin6(KNEG), .pin7(DONE__WC___k_c4),
    .pin15(KNEG), .pin14(WC6), .pin13(WCK6), .pin12(WC7), .pin11(KNEG), .pin10(WCK7));  // open: pin9
  _7404 u_7404_1 (
    .pin1(I3), .pin2(nI3), .pin3(nM0), .pin4(M0), .pin5(nM1), .pin6(M1), .pin13(AR_LD), .pin12(nEN_AR),
    .pin11(WCI), .pin10(nWCI), .pin9(ACI), .pin8(nACI));
  _7432 u_7432_1 (
    .pin1(WR_LD), .pin2(WC_REIN), .pin3(WC_Z_ANY), .pin4(WC_FROM_WR), .pin5(WC_CNTE), .pin6(WC_EN_X),
    .pin13(Y_HIGH), .pin12(YB1), .pin11(Y1), .pin10(Y_HIGH), .pin9(YB0), .pin8(Y0));
  _74157 u_74157_10 (
    .pin1(word_count_register_ld), .pin2(WR0), .pin3(D0), .pin4(word_count_register_n0), .pin5(WR1),
    .pin6(D1), .pin7(word_count_register_n1), .pin15(GND), .pin14(WR3), .pin13(D3),
    .pin12(word_count_register_n3), .pin11(WR2), .pin10(D2), .pin9(word_count_register_n2));
  _74283 u_74283_3 (
    .pin1(ACN1), .pin2(CR2), .pin3(AC1), .pin4(ACN0), .pin5(AC0), .pin6(VCC), .pin7(GND), .pin15(CR2),
    .pin14(AC2), .pin13(ACN2), .pin12(AC3), .pin11(CR2), .pin10(ACN3), .pin9(AC_____1_c4));
  _74175 u_74175_6 (
    .pin1(VCC), .pin2(AC0), .pin4(address_counter_n0), .pin5(address_counter_n1), .pin7(AC1), .pin15(AC3),
    .pin13(address_counter_n3), .pin12(address_counter_n2), .pin10(AC2), .pin9(CP));  // open: pin3, pin6, pin14, pin11
  _74157 u_74157_11 (
    .pin1(WC_LD_D), .pin2(WCM4), .pin3(D4), .pin4(WCX4), .pin5(WCM5), .pin6(D5), .pin7(WCX5),
    .pin15(WC_ZERO), .pin14(WCM7), .pin13(D7), .pin12(WCX7), .pin11(WCM6), .pin10(D6), .pin9(WCX6));
  _74157 u_74157_12 (
    .pin1(Y_WC), .pin2(AC4), .pin3(WC4), .pin4(YA4), .pin5(AC5), .pin6(WC5), .pin7(YA5), .pin15(GND),
    .pin14(AC7), .pin13(WC7), .pin12(YA7), .pin11(AC6), .pin10(WC6), .pin9(YA6));
  _74157 u_74157_13 (
    .pin1(M2_SEL), .pin2(WR0), .pin3(AC0), .pin4(CMPB0), .pin5(WR1), .pin6(AC1), .pin7(CMPB1), .pin15(M0),
    .pin14(WR3), .pin13(AC3), .pin12(CMPB3), .pin11(WR2), .pin10(AC2), .pin9(CMPB2));
  _7400 u_7400_1 (
    .pin1(IE), .pin2(nI3), .pin3(nDIS_DMA), .pin4(IE), .pin5(I3), .pin6(nDIS_TC), .pin13(nCD), .pin12(nC5),
    .pin11(AR_LD), .pin10(nC8), .pin9(nC0), .pin8(CR_LD));
  _7411 u_7411_1 (
    .pin1(WC_CNTI), .pin2(nM2), .pin13(nWCI), .pin12(WC_CNTE));  // open: pin3, pin4, pin5, pin6, pin11, pin10, pin9, pin8
  _74157 u_74157_14 (
    .pin1(word_count_register_ld), .pin2(WR4), .pin3(D4), .pin4(word_count_register_n4), .pin5(WR5),
    .pin6(D5), .pin7(word_count_register_n5), .pin15(GND), .pin14(WR7), .pin13(D7),
    .pin12(word_count_register_n7), .pin11(WR6), .pin10(D6), .pin9(word_count_register_n6));
  _74283 u_74283_4 (
    .pin1(ACN5), .pin2(CR2), .pin3(AC5), .pin4(ACN4), .pin5(AC4), .pin6(CR2), .pin7(AC_____1_c4),
    .pin15(CR2), .pin14(AC6), .pin13(ACN6), .pin12(AC7), .pin11(CR2), .pin10(ACN7), .pin9(AC_COUT));
  _74175 u_74175_7 (
    .pin1(VCC), .pin2(AC4), .pin4(address_counter_n4), .pin5(address_counter_n5), .pin7(AC5), .pin15(AC7),
    .pin13(address_counter_n7), .pin12(address_counter_n6), .pin10(AC6), .pin9(CP));  // open: pin3, pin6, pin14, pin11
  _7404 u_7404_2 (
    .pin1(nEN_WC), .pin2(word_counter_ld), .pin3(nM2), .pin4(M2_SEL));  // open: pin5, pin6, pin13, pin12, pin11, pin10, pin9, pin8
  _74157 u_74157_15 (
    .pin1(Y_CR), .pin2(YA0), .pin3(CR0), .pin4(YB0), .pin5(YA1), .pin6(CR1), .pin7(YB1), .pin15(GND),
    .pin14(YA3), .pin13(VCC), .pin12(YB3), .pin11(YA2), .pin10(CR2), .pin9(YB2));
  _74157 u_74157_16 (
    .pin1(M2_SEL), .pin2(WR4), .pin3(AC4), .pin4(CMPB4), .pin5(WR5), .pin6(AC5), .pin7(CMPB5), .pin15(M0),
    .pin14(WR7), .pin13(AC7), .pin12(CMPB7), .pin11(WR6), .pin10(AC6), .pin9(CMPB6));
  _7400 u_7400_2 (
    .pin1(nC6), .pin2(nCE), .pin3(WR_LD), .pin4(nC1), .pin5(nC8), .pin6(Y_CR), .pin13(WC_TERM), .pin12(nWCI),
    .pin11(WCO), .pin10(AC_TERM), .pin9(nACI), .pin8(ACO));
  _7427 u_7427_1 (
    .pin1(AR_LD), .pin2(AC_AR), .pin3(WC_LD_D), .pin4(WC_ZERO), .pin5(WC_EN_X), .pin6(nEN_WC),
    .pin13(AC_CNTE), .pin12(nEN_AC));  // open: pin11, pin10, pin9, pin8
  _74175 u_74175_8 (
    .pin1(VCC), .pin2(WR0), .pin4(word_count_register_n0), .pin5(word_count_register_n1), .pin7(WR1),
    .pin15(WR3), .pin13(word_count_register_n3), .pin12(word_count_register_n2), .pin10(WR2), .pin9(CP));  // open: pin3, pin6, pin14, pin11
  _74157 u_74157_17 (
    .pin1(AC_AR), .pin2(ACN0), .pin3(AR0), .pin4(ACM0), .pin5(ACN1), .pin6(AR1), .pin7(ACM1), .pin15(GND),
    .pin14(ACN3), .pin13(AR3), .pin12(ACM3), .pin11(ACN2), .pin10(AR2), .pin9(ACM2));
  _7486 u_7486_1 (
    .pin1(AC_COUT), .pin2(CR2), .pin3(AC_TERM), .pin4(WC_COUT), .pin5(M0), .pin6(WC_TERM0));  // open: pin13, pin12, pin11, pin10, pin9, pin8
  _74157 u_74157_18 (
    .pin1(word_counter_ld), .pin2(WC0), .pin3(WCX0), .pin4(word_counter_n0), .pin5(WC1), .pin6(WCX1),
    .pin7(word_counter_n1), .pin15(GND), .pin14(WC3), .pin13(WCX3), .pin12(word_counter_n3), .pin11(WC2),
    .pin10(WCX2), .pin9(word_counter_n2));
  _74157 u_74157_19 (
    .pin1(Y_CR), .pin2(YA4), .pin3(VCC), .pin4(YB4), .pin5(YA5), .pin6(VCC), .pin7(YB5), .pin15(GND),
    .pin14(YA7), .pin13(VCC), .pin12(YB7), .pin11(YA6), .pin10(VCC), .pin9(YB6));
  _7485 u_7485_1 (
    .pin1(CMPB3), .pin2(GND), .pin3(VCC), .pin4(GND), .pin5(GT_L), .pin6(EQ_L), .pin7(LT_L), .pin15(WCK3),
    .pin14(CMPB2), .pin13(WCK2), .pin12(WCK1), .pin11(CMPB1), .pin10(WCK0), .pin9(CMPB0));
  _7410 u_7410_1 (
    .pin1(nC4), .pin2(nC9), .pin3(nC4), .pin4(nCC), .pin5(nCF), .pin6(WC_REIN), .pin13(nCC), .pin12(AC_AR),
    .pin11(nCE), .pin10(nC6), .pin9(nC0), .pin8(Y_HIGH));
  _7404 u_7404_3 (
    .pin1(WR_LD), .pin2(nEN_WR), .pin3(CR_LD), .pin4(nEN_CR), .pin5(nEN_AR), .pin6(address_register_ld),
    .pin13(nEN_AC), .pin12(address_counter_ld), .pin11(nEN_CR), .pin10(control_register__D0_D2__ld),
    .pin9(nEN_WR), .pin8(word_count_register_ld));
  _74175 u_74175_9 (
    .pin1(VCC), .pin2(WR4), .pin4(word_count_register_n4), .pin5(word_count_register_n5), .pin7(WR5),
    .pin15(WR7), .pin13(word_count_register_n7), .pin12(word_count_register_n6), .pin10(WR6), .pin9(CP));  // open: pin3, pin6, pin14, pin11
  _74157 u_74157_20 (
    .pin1(AC_AR), .pin2(ACN4), .pin3(AR4), .pin4(ACM4), .pin5(ACN5), .pin6(AR5), .pin7(ACM5), .pin15(GND),
    .pin14(ACN7), .pin13(AR7), .pin12(ACM7), .pin11(ACN6), .pin10(AR6), .pin9(ACM6));
  _74283 u_74283_5 (
    .pin1(WCN1), .pin2(M0), .pin3(WC1), .pin4(WCN0), .pin5(WC0), .pin6(VCC), .pin7(GND), .pin15(M0),
    .pin14(WC2), .pin13(WCN2), .pin12(WC3), .pin11(M0), .pin10(WCN3), .pin9(WC_____1_c4));
  _74157 u_74157_21 (
    .pin1(word_counter_ld), .pin2(WC4), .pin3(WCX4), .pin4(word_counter_n4), .pin5(WC5), .pin6(WCX5),
    .pin7(word_counter_n5), .pin15(GND), .pin14(WC7), .pin13(WCX7), .pin12(word_counter_n7), .pin11(WC6),
    .pin10(WCX6), .pin9(word_counter_n6));
  _7432 u_7432_2 (
    .pin1(YB2), .pin2(Y_HIGH), .pin3(Y2), .pin4(YB3), .pin5(Y_HIGH), .pin6(Y3), .pin13(Y_HIGH), .pin12(YB5),
    .pin11(Y5), .pin10(Y_HIGH), .pin9(YB4), .pin8(Y4));
  _7485 u_7485_2 (
    .pin1(CMPB7), .pin2(LT_L), .pin3(EQ_L), .pin4(GT_L), .pin6(EQ), .pin15(WCK7), .pin14(CMPB6),
    .pin13(WCK6), .pin12(WCK5), .pin11(CMPB5), .pin10(WCK4), .pin9(CMPB4));  // open: pin5, pin7
  _7430 u_7430_3 (
    .pin1(nC7), .pin2(nC8), .pin3(nCA), .pin4(nCB), .pin5(nCE), .pin6(nCF), .pin12(nDIS_TC),
    .pin11(nDIS_DMA), .pin8(AC_CNTI));  // open: pin13, pin10, pin9
  _74157 u_74157_22 (
    .pin1(address_register_ld), .pin2(AR0), .pin3(D0), .pin4(address_register_n0), .pin5(AR1), .pin6(D1),
    .pin7(address_register_n1), .pin15(GND), .pin14(AR3), .pin13(D3), .pin12(address_register_n3),
    .pin11(AR2), .pin10(D2), .pin9(address_register_n2));
  _74157 u_74157_23 (
    .pin1(control_register__D0_D2__ld), .pin2(CR0), .pin3(D0), .pin4(control_register__D0_D2__n0),
    .pin5(CR1), .pin6(D1), .pin7(control_register__D0_D2__n1), .pin15(GND),
    .pin14(control_register__D0_D2__q3), .pin13(GND), .pin12(control_register__D0_D2__n3), .pin11(CR2),
    .pin10(D2), .pin9(control_register__D0_D2__n2));
  _74157 u_74157_24 (
    .pin1(AR_LD), .pin2(ACM0), .pin3(D0), .pin4(ACX0), .pin5(ACM1), .pin6(D1), .pin7(ACX1), .pin15(GND),
    .pin14(ACM3), .pin13(D3), .pin12(ACX3), .pin11(ACM2), .pin10(D2), .pin9(ACX2));
  _74283 u_74283_6 (
    .pin1(WCN5), .pin2(M0), .pin3(WC5), .pin4(WCN4), .pin5(WC4), .pin6(M0), .pin7(WC_____1_c4), .pin15(M0),
    .pin14(WC6), .pin13(WCN6), .pin12(WC7), .pin11(M0), .pin10(WCN7), .pin9(WC_COUT));
  _74175 u_74175_10 (
    .pin1(VCC), .pin2(WC0), .pin4(word_counter_n0), .pin5(word_counter_n1), .pin7(WC1), .pin15(WC3),
    .pin13(word_counter_n3), .pin12(word_counter_n2), .pin10(WC2), .pin9(CP));  // open: pin3, pin6, pin14, pin11
  _7432 u_7432_3 (
    .pin1(YB6), .pin2(Y_HIGH), .pin3(Y6), .pin4(YB7), .pin5(Y_HIGH), .pin6(Y7), .pin10(KPOS), .pin9(KNEG),
    .pin8(KANY));  // open: pin13, pin12, pin11
  _74125 u_74125_1 (
    .pin1(DONE_T), .pin2(GND), .pin3(DONE));  // open: pin4, pin5, pin6, pin13, pin12, pin11, pin10, pin9, pin8
  // also tied to GND on the sheet: GND
  // also tied to VCC on the sheet: VCC

  // Notes on the sheet:
  //   DMA codes 0-7
  //   active low, only while /IE low and I3 low
  //   7430#2
  //   address register hold / load bits 4-7
  //   control register (D0-D2) hold / load bits 4-7
  //   AC source: D bits 4-7
  //   WC source: count / WR bits 0-3
  //   word counter bits 4-7
  //   D0-D7 output buffers
  //   /OE_D low = drive
  //   T/C codes 8-F
  //   active low, only while /IE low and I3 high
  //   7430#3
  //   address register bits 0-3
  //   control register (D0-D2) bits 0-3
  //   address counter hold / load bits 0-3
  //   WC source: count / WR bits 4-7
  //   7408#2
  //   DONE: WC + k bits 0-3
  //   control mode 0-3
  //   Figure 1: CR1 CR0
  //   7408#1
  //   address register bits 4-7
  //   control register (D0-D2) bits 4-7
  //   address counter hold / load bits 4-7
  //   WC source: D, or zero bits 0-3
  //   Y: AC / WC bits 0-3
  //   DONE: WC + k bits 4-7
  //   7404#1
  //   7432#1
  //   word count register hold / load bits 0-3
  //   AC +/- 1 bits 0-3
  //   address counter bits 0-3
  //   WC source: D, or zero bits 4-7
  //   Y: AC / WC bits 4-7
  //   DONE: compare with WR / AC, or 0 bits 0-3
  //   Am2942 - registers and AMD's Figure 4 function table, built from TTL parts. Initial register contents after power-up are not defined by AMD; Logisim starts them at 0.
  //   7400#1
  //   7411#1
  //   word count register hold / load bits 4-7
  //   AC +/- 1 bits 4-7
  //   address counter bits 4-7
  //   7404#3
  //   Y: CR bits 0-3
  //   DONE: compare with WR / AC, or 0 bits 4-7
  //   7400#2
  //   7427#1
  //   word count register bits 0-3
  //   AC source: count / AR bits 0-3
  //   7486#1
  //   word counter hold / load bits 0-3
  //   Y: CR bits 4-7
  //   DONE compare bits 0-3
  //   7410#1
  //   7404#2
  //   word count register bits 4-7
  //   AC source: count / AR bits 4-7
  //   WC +/- 1 bits 0-3
  //   word counter hold / load bits 4-7
  //   7432#2
  //   DONE compare bits 4-7
  //   7430#1
  //   7432#3
  //   DONE open collector
  //   drives LOW when not done, floats when done
  //   address register hold / load bits 0-3
  //   control register (D0-D2) hold / load bits 0-3
  //   AC source: D bits 0-3
  //   WC +/- 1 bits 4-7
  //   word counter bits 0-3
endmodule

module _74LS54 (
  input  A1,
  input  B1,
  input  A2,
  input  B2,
  input  C2,
  input  A3,
  input  B3,
  input  C3,
  input  A4,
  input  B4,
  output Y
);

  wire n1, n2, n3, n4, orx;

  _7400 u_7400_1 (
    .pin1(A1), .pin2(B1), .pin3(n1), .pin4(A4), .pin5(B4), .pin6(n4));  // open: pin13, pin12, pin11, pin10, pin9, pin8
  _7404 u_7404_1 (.pin1(orx), .pin2(Y));  // open: pin3, pin4, pin5, pin6, pin13, pin12, pin11, pin10, pin9, pin8
  _7410 u_7410_1 (
    .pin1(A2), .pin2(B2), .pin3(A3), .pin4(B3), .pin5(C3), .pin6(n3), .pin13(C2), .pin12(n2));  // open: pin11, pin10, pin9, pin8
  _7420 u_7420_1 (
    .pin1(n1), .pin2(n2), .pin4(n3), .pin5(n4), .pin6(orx));  // open: pin3, pin13, pin12, pin11, pin10, pin9, pin8

  // Other names for the same wires on the sheet: p1 = A1; p2 = B1; p3 = A2; p4 = B2; p5 = C2; p6 = Y; p9 = A3;
  //   p10 = B3; p11 = C3; p12 = A4; p13 = B4

  // Notes on the sheet:
  //   7400#1
  //   7404#1
  //   74LS54: Y(6) = NOT(1.2 + 3.4.5 + 9.10.11 + 12.13), TI pinout
  //   7410#1
  //   7420#1
endmodule
